// Logisim project audio-demo.circ as structural Verilog: 58 circuits, main circuit demo-wave-generators
module notes (
);


  // Notes on the sheet:
  //   Some notes on these audio circuits....
  //   We use 16kHz signed 16-bit PCM audio output, but try to avoid sounds that are very loud. 
  //   That means the audio system expects to receive:
  //    * 16000 samples (values) per second.
  //    * Each sample  (value) should be a signed 16-bit number. 
  //    * The "neutral" middle sample value is 0.
  //    * We aim to keep samples in the range [-10000, +10000] so they aren't too loud.
  //    * The max range for samples is [-32768, +32767]. But that's very loud.
  //   When doing math or arithemetic, we sometimes use 16-bit signed numbers, but we
  //   must keep in mind that any intermediate results need to stay within the [-32768, +32767]
  //   range, otherwise we get distortion or unexpected results. The end result should ideally
  //   be within [-10000, +10000], so it isn't too loud.
  //   More often, when doing math and arithmetic we "widen" everything to 32-bit signed
  //   numbers, so that intermediate results can have a wider range (plus or minus 2 billion).
  //   After the calculations, we "narrow" the numbers back to 16-bit signed numbers. But
  //   even here, the end result should ideally be within [-10000, +10000], so it isn't too loud.
endmodule

module demo_wave_generators (
  input  in_1,
  input  in_2,
  input  in_3,
  input  in_4,
  input  in_5
);

  wire lineselect_1_p4, saturatingdivider_1_p1, saturatingdivider_2_p1, scaledmath_1_p2, scaledmath_2_p2,
       scope_1_p2;
  wire [11:0] Freq_2_out, Freq_out;
  wire [15:0] Duty_out, sawtooth_1_audiosignal, sawtooth_80hz_1_audiosignal, scaledmath_1_p1,
       squarewave_1_audiosignal, triangle_160hz_1_audiosample;

  Slider #(.width(16)) Duty (.out(Duty_out));
  // Callout #(.background("#feffa189"), .dx(34), .dy(-28), .foreground("#cc45bf"), .halign("right"), .text("Click to enable\na wave generator")) callout_1: pin names not known
  Slider #(.width(12)) Freq (.out(Freq_out));
  Slider #(.width(12)) Freq_2 (.out(Freq_2_out));
  sawtooth_80hz sawtooth_80hz_1 (.Enable(in_1), .AudioSignal(sawtooth_80hz_1_audiosignal));  // open: Reset
  triangle_160hz triangle_160hz_1 (.Enable(in_2), .AudioSample(triangle_160hz_1_audiosample));  // open: Reset
  squarewave squarewave_1 (
    .AudioSignal(squarewave_1_audiosignal), .DutyCycle(Duty_out), .Enable(in_3), .Freq(Freq_out));  // open: Reset
  sawtooth sawtooth_1 (.Enable(in_4), .AudioSignal(sawtooth_1_audiosignal), .Freq(Freq_2_out));  // open: Reset
  // ScaledMath #(.mode("twosComplement"), .width(16)) scaledmath_1: pin names not known; wires that end beside it: scaledmath_1_p1, scaledmath_1_p2, scaledmath_1_p2, 16'h3
  // ScaledMath #(.\function ("abs"), .mode("twosComplement"), .width(16)) scaledmath_2: pin names not known; wires that end beside it: scaledmath_1_p1, scaledmath_2_p2, scaledmath_2_p2, 16'h3
  sweep___32768__to___32767 sweep_32768_to_32767_1 (
    .Enable(in_5), .Sweep(scaledmath_1_p1), .Freq(Freq_2_out));  // open: Reset, click
  // LineSelect #(.mode("twosComplement"), .spacing(7), .width(16)) lineselect_1: pin names not known; wires that end beside it: triangle_160hz_1_audiosample, squarewave_1_audiosignal, sawtooth_1_audiosignal, lineselect_1_p4
  // SaturatingDivider #(.mode("twosComplement"), .width(16)) saturatingdivider_1: pin names not known; wires that end beside it: saturatingdivider_1_p1, saturatingdivider_1_p1
  // SaturatingDivider #(.mode("twosComplement"), .width(16)) saturatingdivider_2: pin names not known; wires that end beside it: saturatingdivider_2_p1, saturatingdivider_2_p1
  // Scope #(.mode("twosComplement"), .samples(320), .scopeheight(100), .scopewidth(240), .width(16)) scope_1: pin names not known; wires that end beside it: lineselect_1_p4, scope_1_p2
  // PCMSink #(.mode("twosComplement"), .rate("16 kHz"), .width(16)) pcmsink_1: pin names not known; wires that end beside it: lineselect_1_p4, scope_1_p2
  Clock clock_1 (.out(scope_1_p2));
  // Callout #(.dx(-64), .dy(-41), .foreground("#cc45bf"), .text("Divide by 3 to make\nthe values smaller\n(and the sound quieter)")) callout_2: pin names not known
  // Callout #(.background("#feffa189"), .dx(-129), .dy(43), .foreground("#cc45bf"), .text("Select some of these buttons, and\nalso turn on the corresponding\nwave generator(s) at the left.")) callout_3: pin names not known; wires that end beside it: sawtooth_80hz_1_audiosignal
  // Callout #(.background("#feffa189"), .dx(-46), .dy(-37), .foreground("#cc45bf"), .text("Turn \"auto ticks\" on, and crank up\nthe auto tick speed to the max.")) callout_4: pin names not known

  // Notes on the sheet:
  //   A demonstration of a few different wave generators.
endmodule

module demo_wacky_technosynth (
);

  wire A_out, B_out, pcmsink_1_p2, scope_1_p2;
  wire [11:0] slider_1_out, slider_2_out;
  wire [15:0] or_1_out, sawtooth_1_audiosignal, trianglewave_1_audiosignal;

  // Callout #(.background("#fbfc025e"), .dx(27), .dy(38), .foreground("#d15c5a"), .text("Click A or B, or both!\nYou can also just type the letter.")) callout_1: pin names not known
  Slider #(.width(12)) slider_1 (.out(slider_1_out));
  Slider #(.width(12)) slider_2 (.out(slider_2_out));
  Button #(.behavior("latching")) A (.out(A_out));
  Button #(.behavior("latching")) B (.out(B_out));
  // Callout #(.background("#fbfc025e"), .dx(-58), .dy(-48), .foreground("#d15c5a"), .text("Play with the frequency sliders.\nTry keeping one of them close\nto zero, this produces \n\"low frequency oscillator\" effect!")) callout_2: pin names not known
  trianglewave trianglewave_1 (
    .Enable(A_out), .AudioSignal(trianglewave_1_audiosignal), .Freq(slider_1_out));  // open: Reset
  sawtooth sawtooth_1 (.Enable(B_out), .AudioSignal(sawtooth_1_audiosignal), .Freq(slider_2_out));  // open: Reset
  assign or_1_out = trianglewave_1_audiosignal | sawtooth_1_audiosignal;  // OR_Gate or_1, 16 bits wide
  // Scope #(.mode("twosComplement"), .samples(1600), .scopeheight(80), .scopewidth(240), .width(16)) scope_1: pin names not known; wires that end beside it: or_1_out, scope_1_p2
  Clock clock_1 (.out(scope_1_p2));
  // PCMSink #(.mode("twosComplement"), .rate("16 kHz"), .trigger("falling"), .width(16)) pcmsink_1: pin names not known; wires that end beside it: or_1_out, pcmsink_1_p2
  Clock clock_2 (.out(pcmsink_1_p2));
  // Callout #(.dx(-190), .dy(-94), .foreground("#cc45bf"), .text("The two waves are mixed together by\n\"bitwise OR\" which is a *terrible* way\nto mix audio. But whatever!")) callout_3: pin names not known

  // Notes on the sheet:
  //   Buttons allow you to selectively enable or pause either of two
  //   generators: a triangle generator, or a sawtooth generator.
  //   The results are mixed by bitwise-ORing the signals together. If one is
  //   paused, it garbles the other. Bitwise-OR is *terrible* for mixing.
  //   If both are playing, they mix with a strange techno beat, espcially
  //   if one of the frequencies is close to zero.
endmodule

module demo_chaos_synth (
);

  wire A_out, B_out, C_out, pcmsink_1_p2, random_1_p1, random_1_p2, random_1_p3, random_2_p2, random_2_p3,
       saturatingadder_1_p3, scope_1_p2, scope_2_p2, scope_3_p2;
  wire [11:0] random_1_p5, random_2_p5;
  wire [15:0] sawtooth_1_audiosignal, trianglewave_1_audiosignal;

  Button A (.out(A_out));
  // Random #(.width(12)) random_1: pin names not known; wires that end beside it: random_1_p1, random_1_p2, random_1_p3, random_1_p3, random_1_p5
  not not_1 (random_1_p1, A_out);
  Clock #(.highDuration(2048), .lowDuration(2048)) clock_1 (.out(random_1_p2));
  // Callout #(.background("#fbfc025e"), .dx(100), .dy(-27), .foreground("#d15c5a"), .text("Press (or type) and hold \"B\"\nfor a sawtooth tone.")) callout_1: pin names not known
  Button C (.out(C_out));
  // Callout #(.background("#fbfc025e"), .dx(26), .dy(-60), .foreground("#d15c5a"), .text("Press (or type) and hold \"C\"\nto pick random frequencies.")) callout_2: pin names not known
  // Callout #(.background("#fbfc025e"), .dx(-92), .dy(56), .foreground("#d15c5a"), .text("Press (or type) \"A\" to enable or disable \na random-frequency but steady droning tone.")) callout_3: pin names not known
  // ScaledMath #(.\function ("exp"), .width(12)) scaledmath_1: pin names not known
  Button B (.out(B_out));
  // Random #(.width(12)) random_2: pin names not known; wires that end beside it: C_out, random_2_p2, random_2_p3, random_2_p3, random_2_p5
  Clock #(.highDuration(2048), .lowDuration(2048)) clock_2 (.out(random_2_p2));
  // ScaledMath #(.\function ("exp"), .width(12)) scaledmath_2: pin names not known
  trianglewave trianglewave_1 (
    .Enable(A_out), .AudioSignal(trianglewave_1_audiosignal), .Freq(random_1_p5));  // open: Reset
  sawtooth sawtooth_1 (.Enable(B_out), .AudioSignal(sawtooth_1_audiosignal), .Freq(random_2_p5));  // open: Reset
  // SaturatingAdder #(.mode("twosComplement"), .normalization("fit"), .width(16)) saturatingadder_1: pin names not known; wires that end beside it: trianglewave_1_audiosignal, sawtooth_1_audiosignal, saturatingadder_1_p3
  // Callout #(.dx(-61), .dy(-57), .foreground("#cc45bf"), .text("Converts to signed,\nthen averages the\ntwo signals, a simple mix.")) callout_4: pin names not known
  // Scope #(.mode("twosComplement"), .samples(1600), .scopeheight(80), .scopewidth(240), .width(16)) scope_1: pin names not known; wires that end beside it: trianglewave_1_audiosignal, scope_1_p2
  // Scope #(.mode("twosComplement"), .samples(1600), .scopeheight(80), .scopewidth(240), .width(16)) scope_2: pin names not known; wires that end beside it: saturatingadder_1_p3, scope_2_p2
  // PCMSink #(.mode("twosComplement"), .rate("16 kHz"), .trigger("falling"), .width(16)) pcmsink_1: pin names not known; wires that end beside it: saturatingadder_1_p3, pcmsink_1_p2
  Clock clock_3 (.out(pcmsink_1_p2));
  // Scope #(.mode("twosComplement"), .samples(1600), .scopeheight(80), .scopewidth(240), .width(16)) scope_3: pin names not known; wires that end beside it: sawtooth_1_audiosignal, scope_3_p2
  Clock clock_4 (.out(scope_1_p2));
  Clock clock_5 (.out(scope_2_p2));
  Clock clock_6 (.out(scope_3_p2));

  // Notes on the sheet:
  //   Try typing A, or B, or both, then also press C at the same time!
  //   This clock runs at slower rate
endmodule

module demo_mixing (
);

  wire lineselect_2_p2, lineselect_2_p3, pcmsink_1_p2, saturatingadder_1_p3, saturatingmultiplier_1_p7,
       saturatingmultiplier_1_p8, saturatingmultiplier_1_p9, scaledmath_1_p2, scope_1_p5;
  wire [11:0] lineselect_1_p2, slider_1_out;
  wire [15:0] nand_1_out, or_1_out, sawtooth_1_audiosignal, triangle_62_5hz_1_audiosample, xor_1_out;

  // Callout #(.background("#feffa189"), .dx(41), .dy(64), .foreground("#cc45bf"), .text("Pick a frequency \nfor the sawtooth")) callout_1: pin names not known; wires that end beside it: 12'h1
  triangle_62_5hz triangle_62_5hz_1 (.AudioSample(triangle_62_5hz_1_audiosample));  // open: Enable, Reset
  sawtooth sawtooth_1 (.AudioSignal(sawtooth_1_audiosignal), .Freq(lineselect_1_p2));  // open: Enable, Reset
  // LineSelect #(.behavior("one"), .spacing(4), .width(12)) lineselect_1: pin names not known; wires that end beside it: 12'h3e, lineselect_1_p2, 12'h78, 12'haf
  Slider #(.width(12)) slider_1 (.out(slider_1_out));
  // ScaledMath #(.\function ("exp"), .width(12)) scaledmath_1: pin names not known; wires that end beside it: slider_1_out, scaledmath_1_p2, scaledmath_1_p2
  assign or_1_out = triangle_62_5hz_1_audiosample | sawtooth_1_audiosignal;  // OR_Gate or_1, 16 bits wide
  assign xor_1_out = triangle_62_5hz_1_audiosample ^ sawtooth_1_audiosignal;  // XOR_Gate xor_1, 16 bits wide
  assign nand_1_out = ~(triangle_62_5hz_1_audiosample & sawtooth_1_audiosignal);  // NAND_Gate nand_1, 16 bits wide
  // SaturatingAdder #(.width(16)) saturatingadder_1: pin names not known; wires that end beside it: triangle_62_5hz_1_audiosample, sawtooth_1_audiosignal, saturatingadder_1_p3
  // LineSelect #(.mode("twosComplement"), .spacing(4), .width(16)) lineselect_2: pin names not known; wires that end beside it: saturatingadder_1_p3, lineselect_2_p2, lineselect_2_p3
  // SaturatingAdder #(.mode("twosComplement"), .width(16)) saturatingadder_2: pin names not known; wires that end beside it: triangle_62_5hz_1_audiosample, sawtooth_1_audiosignal, lineselect_2_p2
  // SaturatingMultiplier #(.mode("twosComplement"), .normalization("fit"), .width(16)) saturatingmultiplier_1: pin names not known; wires that end beside it: triangle_62_5hz_1_audiosample, sawtooth_1_audiosignal, triangle_62_5hz_1_audiosample, sawtooth_1_audiosignal, sawtooth_1_audiosignal, triangle_62_5hz_1_audiosample, saturatingmultiplier_1_p7, saturatingmultiplier_1_p8, saturatingmultiplier_1_p9, saturatingmultiplier_1_p7, saturatingmultiplier_1_p8
  // Scope #(.mode("twosComplement"), .samples(1600), .scopeheight(80), .scopewidth(240), .width(16)) scope_1: pin names not known; wires that end beside it: or_1_out, xor_1_out, nand_1_out, lineselect_2_p3, scope_1_p5
  Clock clock_1 (.out(scope_1_p5));
  // PCMSink #(.mode("twosComplement"), .rate("16 kHz"), .trigger("falling"), .width(16)) pcmsink_1: pin names not known; wires that end beside it: lineselect_2_p3, pcmsink_1_p2
  Clock clock_2 (.out(pcmsink_1_p2));
  // Callout #(.background("#feffa189"), .dx(-85), .dy(-28), .foreground("#cc45bf"), .text("Pick a mixing\nfunction")) callout_2: pin names not known
  // Callout #(.background("#77ff7989"), .dx(-85), .dy(-28), .foreground("#cc45bf"), .text("Add your\nown mixing\noptions...")) callout_3: pin names not known; wires that end beside it: saturatingmultiplier_1_p9
  // Callout #(.background("#77ff7900"), .dx(-15), .dy(-54), .foreground("#cc45bf"), .text("Poke with \"hand tool\"\nto zoom in/out.")) callout_4: pin names not known

  // Notes on the sheet:
  //   Demo of some different mixing options.
  //   ???
endmodule

module demo_lowpass_filter (
);

  wire pcmsink_1_p2, scope_1_p2, scope_2_p2;
  wire [11:0] scaledmath_1_p2, slider_1_out;
  wire [15:0] lowpass_filter_onepole_1_y, scope_1_p1, slider_2_out;

  Slider #(.width(12)) slider_1 (.out(slider_1_out));
  // Callout #(.background("#feffa189"), .dx(79), .dy(-6), .foreground("#cc45bf"), .text("Source signal\ndisplay")) callout_1: pin names not known
  // ScaledMath #(.\function ("exp"), .width(12)) scaledmath_1: pin names not known; wires that end beside it: slider_1_out, scaledmath_1_p2
  // Callout #(.background("#feffa189"), .dx(-67), .dy(-27), .foreground("#cc45bf"), .text("Vary the\nsource frequency")) callout_2: pin names not known
  // Scope #(.mode("twosComplement"), .samples(1024), .scopeheight(80), .scopewidth(240), .width(16)) scope_1: pin names not known; wires that end beside it: scope_1_p1, scope_1_p2
  sawtooth sawtooth_1 (.AudioSignal(scope_1_p1), .Freq(scaledmath_1_p2));  // open: Enable, Reset
  Clock clock_1 (.out(scope_1_p2));
  Slider #(.width(16)) slider_2 (.out(slider_2_out));
  lowpass_filter_onepole lowpass_filter_onepole_1 (.beta(slider_2_out), .x(scope_1_p1), .y(lowpass_filter_onepole_1_y));
  // Callout #(.background("#feffa189"), .dx(-85), .dy(-28), .foreground("#cc45bf"), .text("Adjust the filter\nparameter.")) callout_3: pin names not known
  // Scope #(.mode("twosComplement"), .samples(1024), .scopeheight(80), .scopewidth(240), .width(16)) scope_2: pin names not known; wires that end beside it: lowpass_filter_onepole_1_y, scope_2_p2
  // PCMSink #(.bufsize(1024), .mode("twosComplement"), .rate("16 kHz"), .width(16)) pcmsink_1: pin names not known; wires that end beside it: lowpass_filter_onepole_1_y, pcmsink_1_p2
  Clock clock_2 (.out(pcmsink_1_p2));
  Clock clock_3 (.out(scope_2_p2));
  // Callout #(.background("#feffa189"), .dx(-21), .dy(50), .foreground("#cc45bf"), .text("Result after going\nthrough the \"low-pass filter\"")) callout_4: pin names not known

  // Notes on the sheet:
  //   Try setting "beta" to be about 33% (part way down towards the bottom).
  //   Then vary the source frequency.  What do you notice?
  //   Which source frquencies seem to get smaller (or "attenuated") as they go through the filter?
  //   Which source frequencies seem to just "pass right through" without getting smaller?
  //   Try a different setting for beta. Does this change which frequencies get to "pass through" unharmed?
endmodule

module demo_highpass_filter (
);

  wire pcmsink_1_p2, scope_1_p2, scope_2_p2;
  wire [11:0] slider_1_out;
  wire [15:0] highpass_filter_onepole_1_y, highpass_filter_onepole_2_y, slider_2_out,
       trianglewave_1_audiosignal;

  // Callout #(.background("#feffa189"), .dx(79), .dy(-6), .foreground("#cc45bf"), .text("Source signal\ndisplay")) callout_1: pin names not known
  trianglewave trianglewave_1 (.AudioSignal(trianglewave_1_audiosignal), .Freq(slider_1_out));  // open: Enable, Reset
  Slider #(.width(12)) slider_1 (.out(slider_1_out));
  // Scope #(.mode("twosComplement"), .samples(256), .scopeheight(80), .scopewidth(240), .width(16)) scope_1: pin names not known; wires that end beside it: trianglewave_1_audiosignal, scope_1_p2
  Clock clock_1 (.out(scope_1_p2));
  // Callout #(.background("#feffa189"), .dx(-67), .dy(-27), .foreground("#cc45bf"), .text("Vary the\nsource frequency")) callout_2: pin names not known
  Slider #(.width(16)) slider_2 (.out(slider_2_out));
  highpass_filter_onepole highpass_filter_onepole_1 (
    .alpha(slider_2_out), .x(trianglewave_1_audiosignal), .y(highpass_filter_onepole_1_y));
  // Callout #(.background("#feffa189"), .dx(-85), .dy(-28), .foreground("#cc45bf"), .text("Adjust the filter\nparameter.")) callout_3: pin names not known
  highpass_filter_onepole highpass_filter_onepole_2 (
    .alpha(slider_2_out), .x(highpass_filter_onepole_1_y), .y(highpass_filter_onepole_2_y));
  // Scope #(.mode("twosComplement"), .samples(256), .scopeheight(80), .scopewidth(240), .width(16)) scope_2: pin names not known; wires that end beside it: highpass_filter_onepole_2_y, scope_2_p2
  // PCMSink #(.bufsize(1024), .mode("twosComplement"), .rate("16 kHz"), .width(16)) pcmsink_1: pin names not known; wires that end beside it: highpass_filter_onepole_2_y, pcmsink_1_p2
  Clock clock_2 (.out(pcmsink_1_p2));
  Clock clock_3 (.out(scope_2_p2));
  // Callout #(.background("#feffa189"), .dx(-21), .dy(50), .foreground("#cc45bf"), .text("Result after going\nthrough the \"high-pass filters\"")) callout_4: pin names not known

  // Notes on the sheet:
  //   Try setting "alpha" to be about 50% (near the middle).
  //   Then vary the source frequency.  What do you notice?
  //   Which source frquencies seem to get smaller (or "attenuated") as they go through the filter?
  //   Which source frequencies seem to just "pass right through" without getting smaller?
  //   Try other settings for alpha. Does this change which frequencies get to "pass through" unharmed?
  //   This circuit also has two back-to-back filters. What do you think that does?
endmodule

module demo_seascape_bandpass_filtered_noise (
);

  wire clock_1_out, pcmsink_1_p2, saturatingdivider_1_p2, scope_1_p2;
  wire [15:0] highpass_filter_onepole_1_y, lowpass_filter_onepole_1_y, saturatingdivider_1_p5, slider_1_out,
       slider_2_out;

  Random #(.width(16)) RANDOM ();  // open: clk, next, out, clr
  Clock clock_1 (.out(clock_1_out));
  // SaturatingDivider #(.mode("twosComplement"), .width(16)) saturatingdivider_1: pin names not known; wires that end beside it: clock_1_out, saturatingdivider_1_p2, saturatingdivider_1_p2, 16'h3, saturatingdivider_1_p5
  highpass_filter_onepole highpass_filter_onepole_1 (
    .alpha(slider_1_out), .x(saturatingdivider_1_p5), .y(highpass_filter_onepole_1_y));
  Slider #(.width(16)) slider_1 (.out(slider_1_out));
  lowpass_filter_onepole lowpass_filter_onepole_1 (
    .beta(slider_2_out), .x(highpass_filter_onepole_1_y), .y(lowpass_filter_onepole_1_y));
  Slider #(.width(16)) slider_2 (.out(slider_2_out));
  // Callout #(.background("#feffa189"), .dx(-52), .dy(-69), .foreground("#cc45bf"), .text("Tune both parameters to\ncontrol the bandpass filtering.")) callout_1: pin names not known
  // Scope #(.mode("twosComplement"), .scopeheight(80), .scopewidth(240), .width(16)) scope_1: pin names not known; wires that end beside it: lowpass_filter_onepole_1_y, scope_1_p2
  // PCMSink #(.bufsize(1024), .mode("twosComplement"), .rate("16 kHz"), .width(16)) pcmsink_1: pin names not known; wires that end beside it: lowpass_filter_onepole_1_y, pcmsink_1_p2
  Clock clock_2 (.out(pcmsink_1_p2));
  Clock clock_3 (.out(scope_1_p2));
endmodule

module demo_recorded_audio (
);

  wire button_1_out, clock_1_out, comparator_1_gt, fitrange_1_p1, or_1_out, pcmsink_1_p2;
  wire [15:0] fitrange_1_p3, highpass_filter_onepole_1_y, lowpass_filter_onepole_1_y, slider_1_out,
       slider_2_out;
  wire [17:0] counter_1_q;

  Clock clock_1 (.out(clock_1_out));
  Button button_1 (.out(button_1_out));
  ROM #(.addrWidth(18), .proportions("tall")) rom_1 (.addr(counter_1_q));  // open: data
  Counter #(.max('h3ffff), .width(18)) counter_1 (
    .Q(counter_1_q), .clk(clock_1_out), .clr(or_1_out));  // open: load, D, count, carry
  or or_1 (or_1_out, button_1_out, comparator_1_gt);
  Comparator #(.width(18)) comparator_1 (.a(counter_1_q), .b(18'h1a544), .gt(comparator_1_gt));  // open: eq, lt
  // FitRange #(.widthOut(16)) fitrange_1: pin names not known; wires that end beside it: fitrange_1_p1, fitrange_1_p1, fitrange_1_p3
  Slider #(.width(16)) slider_1 (.out(slider_1_out));
  lowpass_filter_onepole lowpass_filter_onepole_1 (
    .beta(slider_1_out), .x(fitrange_1_p3), .y(lowpass_filter_onepole_1_y));
  Slider #(.width(16)) slider_2 (.out(slider_2_out));
  // Callout #(.background("#feffa189"), .dx(-52), .dy(-69), .foreground("#cc45bf"), .text("Tune both parameters to\ncontrol the bandpass filtering.")) callout_1: pin names not known
  highpass_filter_onepole highpass_filter_onepole_1 (
    .alpha(slider_2_out), .x(lowpass_filter_onepole_1_y), .y(highpass_filter_onepole_1_y));
  // PCMSink #(.mode("twosComplement"), .rate("16 kHz"), .width(16)) pcmsink_1: pin names not known; wires that end beside it: highpass_filter_onepole_1_y, pcmsink_1_p2
  // Scope #(.mode("twosComplement"), .scopeheight(80), .scopewidth(240), .width(16)) scope_1: pin names not known; wires that end beside it: highpass_filter_onepole_1_y, pcmsink_1_p2
  Clock clock_2 (.out(pcmsink_1_p2));

  // Notes on the sheet:
  //   contents of rom_1 (hex, n*v repeats v):
  //   compressed eJyEXUm24zgO3PMUXv+VJorScTTe/wgtAgggKDurX7t/OW1ZA4gZQSAPn2n9THN9jcdny5/+06Vc
  //   PlP/yc+n+TPPn/n8lOkzdKnvPvq/Xv+flu4zXvKJv0v1u+X5/zx95r7+cO5Tv9ip63H6Knea/urb
  //   vr76/k8++0z230VOjvcfPXDWH6SCH/pfeVN/m3CO59/xU/lVnJqOrx/IxdP7TH4BupH4+PlXtsvR
  //   I+GO+mTfN9ejW/ST/LrBvvvjJ5PD0/p1bT/i103w531zC/751y0+SwIit989f+t37/M3n/v54+7S
  //   /Le8H9IeFfePRy68ZKldAfp6sYXye+NF1oXqXzduJ0r2a77oL157LZpczUmP2wEfLs06EUMmuzF8
  //   grsJWvnS8PX1GnwLfaxVcAUvO0kPk/N2Ci/+UUMnEpOg8p1aIjiF36tM9/eLk3F8/2nuIv5Nwvai
  //   G3/C959aRiUBqOfqx/Yp+w//qAdZZmaqxKfDKttBzXffyqB/aQJfQ18Reg77xcxLxEvYqiU9m996
  //   c21/ENxE74c3uqWVRxeAX88DFp/fFHIK9t+roRqOWYTY+msJwVqtRL/4+C3LYR/0S15gPNDEFHUx
  //   YT566SomEEgawvavNTdOAZO9nrYf/r5+8dbLveqvb01FDxgm7fu71zdYg5lvJyTqRcSvhXjf2/pm
  //   B9wNsYObZ1pH1UdB9841PvFTI68plphWTamTyv1eroX0H50yaEmr3L+fuSFOPDUtOknHa/2/6cEK
  //   sdHOL1mKN4kJxweAEP7B1JyQSUrKAawLNunzr1UjGSAr/EXTD3sBbxq9BHuUk12fcqRy4JMBwvr8
  //   c0r1k+mzLJ9lhsicIjWHvLnkSPyknPK5e0DP+0UO24kDBnlleZ/r+Z8D7LYnO1WQaqi3ZI9+yeeP
  //   T/tnl+3s47I9f5PeTj38sB/VE+ekj4gbr8/xHL+MyU6ZcfFBfqhX1jNscpJL/yZ7c+Bseq3Nnqz+
  //   c4JCUB0/2kWfz+tfexRagYHW5woLE+dXWzvh/KP8nfWYSol62k6uO4YqjgUfcBVd+REU6Ox5hd5w
  //   NIaPP4jTzT48cZJZOGIRdtjk7/qxf66pvt/pqyLHP+KQ5UJTJbU9+CT0Fy7Q5zKm6IVTnucdamhR
  //   Xxnv16RkqY+2fkoB18xCt+ew529vryeqyY+PdNcQ5QlU8vHJTxj0yMzwvEl5/8zjZ35imEWOX0mX
  //   Pjd2fNbus67yyp/1ed5b3sz180Xp/zzdATooZbI8+3NLV7Jnvz7r8FmX5wyfdXzOltYnAps+2/DZ
  //   us/Wy5vy2Za0LfK5voq8nuOvtD5neG5G/xZ5Pfp8TPVsY31fL9HJVZ5LDPU+6z0c8hQq1qvQ7XnY
  //   hxSrBHtjfep5eF7pIc5Dinx98vLJ42daarA47umJFMfyGa7PuH3GtR5ThfhK8y70XOr5n5t5rvXc
  //   xrPu9QaKEKcKuhx8VL6q95BreFljxU3izLo69TzPLZUZdDN9kCrlM8g+yKM9F9pSpWGx562vW/6u
  //   0HyTUHsHP4+VD4VQ8qsRryWtu3yyYjWLvHno2dk56xV7XOio91NfytKTUdX0hiq/Is+7iqI4RP8s
  //   9cP5kkeeKummPU3jQ9XPmD9TqRSeN/n5mOpC5Hp8JcJR+ep56od/6v3sYPWCaz1y8Szf8ZlL/VVd
  //   zV3++azLLddVKS5Gjfpcs7DfLA/VffCY8lybHNbLmWeRr40sgOqHWQ67k5FlBtF6+fxM9cNcX/WE
  //   GVqopEWfaMYZzmrf9nqmStdTdIbK+hocqoJeHyXL0yzyeRYOuuRxpyrEjwRPWTj0eT0n3upXlUhV
  //   yqvEF1GWi+oGFco5mRpTXXLJ8c/5u1RXaRGZmIRPlUNzEn6HlVrr2UTOkqwP1Nsub6r+S6r4Ky/M
  //   euewVe4Pj/Xgys6LcPQO7pvklfVVJbsuUfmE0X10T5dM8SiHjs6/ssL6E+fTSnvhxFO4ssjLOVTv
  //   cBSSHvXZH4rlkmqS6GHPUfJCU2Ux4e5UeW2px9v5V0iq2MzKmINQddQlSHWZiiiJXpbMDqic+1w6
  //   eOpQORbN0ctiKcuMykdJbU79lchHvflTLMmIYxbR0yblydm8nvmEUhySLZbKhKyj0bP/6KVNMvQ8
  //   YzLR32HTZr0rs7Qh60reU+hZ5PFVxR71wfOSplO06VTp+fx9lOu8ik+2iQ5e68H1uosI5ZHcqasn
  //   3MBCY5XsSs9JFLZm6iqphZ7lY/K6y6nEUpmUH2BOe4pk3pDzp7po4nuFN7aDtR5NuYInlURqYbLw
  //   v8rvJH8PoadangvE78HVE8m7ugaqFfqkLoY97CZv1KdU66GLrqZjFIv90LD7TIew6FT1aFWcSz3+
  //   eZNlFZ6nWLf61OYZCXHMg1M9s6R6wkMoiVUQzSP07IU4lSxQllcy72YzNWYPUkKuG597AH8Oxudm
  //   GOdkBk3F/+HbXazQQ+cJPsVufofyZ6WnvIyYqnplfettbBAiZdEhGQFPeOTqEa/JJCh/9AGr3eiE
  //   nlkU6Sn0fJRAL97TQ/9BFMImD3XX+3wEp8ypLsdMTqXokKo/i6mRMO9Vh6eqXkT/1NsTeay3Ogp9
  //   FtjwE56sRuAjlN5kLpWuo3lSPREki/48hYzKaUWoulU6MzEh48nej+ooyZv6VbI1XeDTOX8qcx7w
  //   /dWwT0kd0spF68e8p8e1nEXec33lHoSaqh7IIsvP2m1iV9WWPecxQ53Nk1VLXj2jS+xXJ/pZaFg/
  //   GcQyZ3BgB/ld4LkUxBm9PMUpFn6FJdeIaxV+vuVNlp+cwo0PDR89vKkrJGx21rtdb+NPNTrmzKrB
  //   eui2tRpYFe8My19g/NVMPHpyhSVahHlmNT2pOp4FTvpDwMddejiwq3xYn3EWz7Ra6nrOVe34JGym
  //   vpgwmEYMlVAZ2mMQhrzFrxjk1ZmbL1GIxKg7gr8dNOksIlG1pieXoC2Z2VLnGtqs8tX8cWe8EqeQ
  //   fd/kpW67/nOBHlCNOsDJ7eCRibiZER9Fri+KpS+hifpL+oCdSPQgSnITT7P+FY9IPKga9DyHif1a
  //   RUM+Xz3+ftHg76j8XxdFzlYy0gF7qidfhKSLfiLXncMvClO1U3ZqgtOiceGezOwy9eqTmr1Q1wXG
  //   Wuz4CHFehGKmKpNFY+4yjWFfTDOcGhOo1RM9M0OfZFDvSpqPMPnNYlgfHjtTVYZHNTFZtNbz4Oq5
  //   P9LtsXIV9ltMxi56I9flqN7RIKxVHTzRt0rM0YL4KvWT8OGETMClzqd8fkSiyOLsSejj8juRwnyu
  //   u5slcjoIBZI55iuYcAPdjPHkQ3c13Y5cHzc0wnvJZLaAeiNlq9Uf64R06ubl9JDr8W3q6zBl9XDX
  //   dFe6IcoR0b7rq9prpZs67RLcyEqJ/RqsEGk6XzMrE44R1qprdwsfbhZt1EscZv0r3XZRCEp5C5dF
  //   Hy5GRguJRrVKIo/KZhlG9vnnKXRzF33Bt9n8K9OH6rgeEokqnyvdCvI6g6XXzXx0ouSfv5vYza7K
  //   bJYQsMpaDcRrZfYhoPg2QuRB/qn6UDwlY91dBRP8fH1UYUr4JX7mDnWXYWQL6DYgPXAgUp+T3Xxv
  //   Oaf6z1v0Q7Hw2mLxEZHxDWcmQ/uNkFP/cEK8OKfGfA+WKjB+PvU9rPBMEaTrmdX84erDbHCJZ3nz
  //   vOYk+Qx5rfDuhkq3Slsl2i5vNuGfSeJKTTKNSFAiR2xx34h4xHOpvSfSILMaB82f+Kt674CcHjAl
  //   9uzJ3OkR3qC+5mSOt8eDZlPgB8KlMbO7JbNBHqGo4p2SOU6UxqtsM4v+0cSYkkJFeEn2fgHdFqVe
  //   sjfq1+3wRu5kCbbRjLiFlkeUeDyTanZzeH2ir2RquZCxWCG/B1STBWuf/LfWTDycNliLXt3lZNr/
  //   pBhVY/IFF5hpkeYULmYfCViL5Q6w2gz+eGSss8RE+GQ1ikizqrzjY29Oo1HlsA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
endmodule

module demo_recorded_audio_svf (
);

  wire lineselect_1_p5, pcmsink_1_p2;
  wire [15:0] recording_canning_ramps_1_audiosignal, slider_1_out, slider_2_out, svf_filter_1_bp,
       svf_filter_1_hp, svf_filter_1_lp;

  // Callout #(.background("#feffa189"), .dx(69), .dy(-80), .foreground("#cc45bf"), .text("You can swap out\nthis recording for\nother ones, like\nrecording-thank-you\nor some other audio source.")) callout_1: pin names not known
  recording_canning_ramps recording_canning_ramps_1 (.AudioSignal(recording_canning_ramps_1_audiosignal));  // open: Reset, Enable
  Slider #(.width(16)) slider_1 (.out(slider_1_out));
  Slider #(.width(16)) slider_2 (.out(slider_2_out));
  SVF_filter svf_filter_1 (
    .f(slider_1_out), .x(recording_canning_ramps_1_audiosignal), .hp(svf_filter_1_hp), .Q(slider_2_out),
    .bp(svf_filter_1_bp), .lp(svf_filter_1_lp));
  // LineSelect #(.mode("twosComplement"), .spacing(2), .width(16)) lineselect_1: pin names not known; wires that end beside it: recording_canning_ramps_1_audiosignal, svf_filter_1_hp, svf_filter_1_bp, svf_filter_1_lp, lineselect_1_p5
  // Callout #(.background("#feffa189"), .dx(-75), .dy(-84), .foreground("#cc45bf"), .text("This thing is simultaneously\na high-pass filter, a low-pass filter,\nand a bandpass filter,\nand it has \"resonance\"")) callout_2: pin names not known
  // PCMSink #(.mode("twosComplement"), .rate("16 kHz"), .width(16)) pcmsink_1: pin names not known; wires that end beside it: lineselect_1_p5, pcmsink_1_p2
  // Scope #(.mode("twosComplement"), .scopeheight(80), .scopewidth(240), .width(16)) scope_1: pin names not known; wires that end beside it: lineselect_1_p5, pcmsink_1_p2
  Clock clock_1 (.out(pcmsink_1_p2));
endmodule

module demo_reverb_tone (
);

  wire clock_2_out, pcmsink_1_p2, saturatingadder_1_p1, saturatingadder_1_p4, scope_1_p2, scope_2_p2,
       shift_register_1_p1;
  wire [11:0] slider_1_out;
  wire [15:0] saturatingmultiplier_1_p2, trianglewave_1_audiosignal;

  // Callout #(.background("#feffa189"), .dx(79), .dy(-6), .foreground("#cc45bf"), .text("Source signal\ndisplay")) callout_1: pin names not known
  trianglewave trianglewave_1 (.AudioSignal(trianglewave_1_audiosignal), .Freq(slider_1_out));  // open: Enable, Reset
  Slider #(.width(12)) slider_1 (.out(slider_1_out));
  // Scope #(.mode("twosComplement"), .samples(256), .scopeheight(80), .scopewidth(240), .width(16)) scope_1: pin names not known; wires that end beside it: trianglewave_1_audiosignal, scope_1_p2
  Clock clock_1 (.out(scope_1_p2));
  Clock clock_2 (.out(clock_2_out));
  // Callout #(.background("#feffa189"), .dx(-67), .dy(-27), .foreground("#cc45bf"), .text("Vary the\nsource frequency")) callout_2: pin names not known
  // Shift_Register #(.length(32), .width(16)) shift_register_1: pin names not known; wires that end beside it: shift_register_1_p1, clock_2_out
  // SaturatingAdder #(.mode("twosComplement"), .width(16)) saturatingadder_1: pin names not known; wires that end beside it: saturatingadder_1_p1, trianglewave_1_audiosignal, saturatingadder_1_p1, saturatingadder_1_p4
  // SaturatingMultiplier #(.mode("twosComplement"), .normalization("fit"), .width(16)) saturatingmultiplier_1: pin names not known; wires that end beside it: saturatingadder_1_p4, saturatingmultiplier_1_p2, shift_register_1_p1
  Slider #(.mode("twosComplement"), .width(16)) slider_2 (.out(saturatingmultiplier_1_p2));
  // Scope #(.mode("twosComplement"), .samples(256), .scopeheight(80), .scopewidth(240), .width(16)) scope_2: pin names not known; wires that end beside it: saturatingadder_1_p4, scope_2_p2
  // PCMSink #(.bufsize(1024), .mode("twosComplement"), .rate("16 kHz"), .width(16)) pcmsink_1: pin names not known; wires that end beside it: saturatingadder_1_p4, pcmsink_1_p2
  Clock clock_3 (.out(pcmsink_1_p2));
  Clock clock_4 (.out(scope_2_p2));
  // Callout #(.background("#feffa189"), .dx(-85), .dy(-28), .foreground("#cc45bf"), .text("Adjust the filter\nparameter.")) callout_3: pin names not known
  // Callout #(.background("#feffa189"), .dx(-21), .dy(50), .foreground("#cc45bf"), .text("Result after going\nthrough the \"reverb\" circuit")) callout_4: pin names not known
endmodule

module demo_reverb_voice (
);

  wire button_1_out, clock_1_out, clock_3_out, comparator_1_gt, fitrange_1_p1, or_1_out, pcmsink_1_p2,
       saturatingadder_1_p1, saturatingadder_1_p4, scope_1_p1, scope_1_p2, scope_2_p2, shift_register_1_p1;
  wire [15:0] saturatingmultiplier_1_p2;
  wire [17:0] counter_1_q;

  Clock clock_1 (.out(clock_1_out));
  Button button_1 (.out(button_1_out));
  // Callout #(.background("#feffa189"), .dx(79), .dy(-6), .foreground("#cc45bf"), .text("Source signal\ndisplay")) callout_1: pin names not known
  ROM #(.addrWidth(18), .proportions("tall")) rom_1 (.addr(counter_1_q));  // open: data
  Counter #(.max('h3ffff), .width(18)) counter_1 (
    .Q(counter_1_q), .clk(clock_1_out), .clr(or_1_out));  // open: load, D, count, carry
  or or_1 (or_1_out, button_1_out, comparator_1_gt);
  Comparator #(.width(18)) comparator_1 (.a(counter_1_q), .b(18'h1a544), .gt(comparator_1_gt));  // open: eq, lt
  // Scope #(.mode("twosComplement"), .samples(256), .scopeheight(80), .scopewidth(240), .width(16)) scope_1: pin names not known; wires that end beside it: scope_1_p1, scope_1_p2
  Clock clock_2 (.out(scope_1_p2));
  Clock clock_3 (.out(clock_3_out));
  // Shift_Register #(.length(32), .width(16)) shift_register_1: pin names not known; wires that end beside it: shift_register_1_p1, clock_3_out
  // FitRange #(.widthOut(16)) fitrange_1: pin names not known; wires that end beside it: fitrange_1_p1, fitrange_1_p1, scope_1_p1
  // SaturatingAdder #(.mode("twosComplement"), .width(16)) saturatingadder_1: pin names not known; wires that end beside it: saturatingadder_1_p1, scope_1_p1, saturatingadder_1_p1, saturatingadder_1_p4
  // SaturatingMultiplier #(.mode("twosComplement"), .normalization("fit"), .width(16)) saturatingmultiplier_1: pin names not known; wires that end beside it: saturatingadder_1_p4, saturatingmultiplier_1_p2, shift_register_1_p1
  Slider #(.mode("twosComplement"), .width(16)) slider_1 (.out(saturatingmultiplier_1_p2));
  // Scope #(.mode("twosComplement"), .samples(256), .scopeheight(80), .scopewidth(240), .width(16)) scope_2: pin names not known; wires that end beside it: saturatingadder_1_p4, scope_2_p2
  // PCMSink #(.bufsize(1024), .mode("twosComplement"), .rate("16 kHz"), .width(16)) pcmsink_1: pin names not known; wires that end beside it: saturatingadder_1_p4, pcmsink_1_p2
  Clock clock_4 (.out(pcmsink_1_p2));
  Clock clock_5 (.out(scope_2_p2));
  // Callout #(.background("#feffa189"), .dx(-85), .dy(-28), .foreground("#cc45bf"), .text("Adjust the filter\nparameter.")) callout_2: pin names not known
  // Callout #(.background("#feffa189"), .dx(-21), .dy(50), .foreground("#cc45bf"), .text("Result after going\nthrough the \"reverb\" circuit")) callout_3: pin names not known

  // Notes on the sheet:
  //   contents of rom_1 (hex, n*v repeats v):
  //   compressed eJyEXUm24zgO3PMUXv+VJorScTTe/wgtAgggKDurX7t/OW1ZA4gZQSAPn2n9THN9jcdny5/+06Vc
  //   PlP/yc+n+TPPn/n8lOkzdKnvPvq/Xv+flu4zXvKJv0v1u+X5/zx95r7+cO5Tv9ip63H6Knea/urb
  //   vr76/k8++0z230VOjvcfPXDWH6SCH/pfeVN/m3CO59/xU/lVnJqOrx/IxdP7TH4BupH4+PlXtsvR
  //   I+GO+mTfN9ejW/ST/LrBvvvjJ5PD0/p1bT/i103w531zC/751y0+SwIit989f+t37/M3n/v54+7S
  //   /Le8H9IeFfePRy68ZKldAfp6sYXye+NF1oXqXzduJ0r2a77oL157LZpczUmP2wEfLs06EUMmuzF8
  //   grsJWvnS8PX1GnwLfaxVcAUvO0kPk/N2Ci/+UUMnEpOg8p1aIjiF36tM9/eLk3F8/2nuIv5Nwvai
  //   G3/C959aRiUBqOfqx/Yp+w//qAdZZmaqxKfDKttBzXffyqB/aQJfQ18Reg77xcxLxEvYqiU9m996
  //   c21/ENxE74c3uqWVRxeAX88DFp/fFHIK9t+roRqOWYTY+msJwVqtRL/4+C3LYR/0S15gPNDEFHUx
  //   YT566SomEEgawvavNTdOAZO9nrYf/r5+8dbLveqvb01FDxgm7fu71zdYg5lvJyTqRcSvhXjf2/pm
  //   B9wNsYObZ1pH1UdB9841PvFTI68plphWTamTyv1eroX0H50yaEmr3L+fuSFOPDUtOknHa/2/6cEK
  //   sdHOL1mKN4kJxweAEP7B1JyQSUrKAawLNunzr1UjGSAr/EXTD3sBbxq9BHuUk12fcqRy4JMBwvr8
  //   c0r1k+mzLJ9lhsicIjWHvLnkSPyknPK5e0DP+0UO24kDBnlleZ/r+Z8D7LYnO1WQaqi3ZI9+yeeP
  //   T/tnl+3s47I9f5PeTj38sB/VE+ekj4gbr8/xHL+MyU6ZcfFBfqhX1jNscpJL/yZ7c+Bseq3Nnqz+
  //   c4JCUB0/2kWfz+tfexRagYHW5woLE+dXWzvh/KP8nfWYSol62k6uO4YqjgUfcBVd+REU6Ox5hd5w
  //   NIaPP4jTzT48cZJZOGIRdtjk7/qxf66pvt/pqyLHP+KQ5UJTJbU9+CT0Fy7Q5zKm6IVTnucdamhR
  //   Xxnv16RkqY+2fkoB18xCt+ew529vryeqyY+PdNcQ5QlU8vHJTxj0yMzwvEl5/8zjZ35imEWOX0mX
  //   Pjd2fNbus67yyp/1ed5b3sz180Xp/zzdATooZbI8+3NLV7Jnvz7r8FmX5wyfdXzOltYnAps+2/DZ
  //   us/Wy5vy2Za0LfK5voq8nuOvtD5neG5G/xZ5Pfp8TPVsY31fL9HJVZ5LDPU+6z0c8hQq1qvQ7XnY
  //   hxSrBHtjfep5eF7pIc5Dinx98vLJ42daarA47umJFMfyGa7PuH3GtR5ThfhK8y70XOr5n5t5rvXc
  //   xrPu9QaKEKcKuhx8VL6q95BreFljxU3izLo69TzPLZUZdDN9kCrlM8g+yKM9F9pSpWGx562vW/6u
  //   0HyTUHsHP4+VD4VQ8qsRryWtu3yyYjWLvHno2dk56xV7XOio91NfytKTUdX0hiq/Is+7iqI4RP8s
  //   9cP5kkeeKummPU3jQ9XPmD9TqRSeN/n5mOpC5Hp8JcJR+ep56od/6v3sYPWCaz1y8Szf8ZlL/VVd
  //   zV3++azLLddVKS5Gjfpcs7DfLA/VffCY8lybHNbLmWeRr40sgOqHWQ67k5FlBtF6+fxM9cNcX/WE
  //   GVqopEWfaMYZzmrf9nqmStdTdIbK+hocqoJeHyXL0yzyeRYOuuRxpyrEjwRPWTj0eT0n3upXlUhV
  //   yqvEF1GWi+oGFco5mRpTXXLJ8c/5u1RXaRGZmIRPlUNzEn6HlVrr2UTOkqwP1Nsub6r+S6r4Ky/M
  //   euewVe4Pj/Xgys6LcPQO7pvklfVVJbsuUfmE0X10T5dM8SiHjs6/ssL6E+fTSnvhxFO4ssjLOVTv
  //   cBSSHvXZH4rlkmqS6GHPUfJCU2Ux4e5UeW2px9v5V0iq2MzKmINQddQlSHWZiiiJXpbMDqic+1w6
  //   eOpQORbN0ctiKcuMykdJbU79lchHvflTLMmIYxbR0yblydm8nvmEUhySLZbKhKyj0bP/6KVNMvQ8
  //   YzLR32HTZr0rs7Qh60reU+hZ5PFVxR71wfOSplO06VTp+fx9lOu8ik+2iQ5e68H1uosI5ZHcqasn
  //   3MBCY5XsSs9JFLZm6iqphZ7lY/K6y6nEUpmUH2BOe4pk3pDzp7po4nuFN7aDtR5NuYInlURqYbLw
  //   v8rvJH8PoadangvE78HVE8m7ugaqFfqkLoY97CZv1KdU66GLrqZjFIv90LD7TIew6FT1aFWcSz3+
  //   eZNlFZ6nWLf61OYZCXHMg1M9s6R6wkMoiVUQzSP07IU4lSxQllcy72YzNWYPUkKuG597AH8Oxudm
  //   GOdkBk3F/+HbXazQQ+cJPsVufofyZ6WnvIyYqnplfettbBAiZdEhGQFPeOTqEa/JJCh/9AGr3eiE
  //   nlkU6Sn0fJRAL97TQ/9BFMImD3XX+3wEp8ypLsdMTqXokKo/i6mRMO9Vh6eqXkT/1NsTeay3Ogp9
  //   FtjwE56sRuAjlN5kLpWuo3lSPREki/48hYzKaUWoulU6MzEh48nej+ooyZv6VbI1XeDTOX8qcx7w
  //   /dWwT0kd0spF68e8p8e1nEXec33lHoSaqh7IIsvP2m1iV9WWPecxQ53Nk1VLXj2jS+xXJ/pZaFg/
  //   GcQyZ3BgB/ld4LkUxBm9PMUpFn6FJdeIaxV+vuVNlp+cwo0PDR89vKkrJGx21rtdb+NPNTrmzKrB
  //   eui2tRpYFe8My19g/NVMPHpyhSVahHlmNT2pOp4FTvpDwMddejiwq3xYn3EWz7Ra6nrOVe34JGym
  //   vpgwmEYMlVAZ2mMQhrzFrxjk1ZmbL1GIxKg7gr8dNOksIlG1pieXoC2Z2VLnGtqs8tX8cWe8EqeQ
  //   fd/kpW67/nOBHlCNOsDJ7eCRibiZER9Fri+KpS+hifpL+oCdSPQgSnITT7P+FY9IPKga9DyHif1a
  //   RUM+Xz3+ftHg76j8XxdFzlYy0gF7qidfhKSLfiLXncMvClO1U3ZqgtOiceGezOwy9eqTmr1Q1wXG
  //   Wuz4CHFehGKmKpNFY+4yjWFfTDOcGhOo1RM9M0OfZFDvSpqPMPnNYlgfHjtTVYZHNTFZtNbz4Oq5
  //   P9LtsXIV9ltMxi56I9flqN7RIKxVHTzRt0rM0YL4KvWT8OGETMClzqd8fkSiyOLsSejj8juRwnyu
  //   u5slcjoIBZI55iuYcAPdjPHkQ3c13Y5cHzc0wnvJZLaAeiNlq9Uf64R06ubl9JDr8W3q6zBl9XDX
  //   dFe6IcoR0b7rq9prpZs67RLcyEqJ/RqsEGk6XzMrE44R1qprdwsfbhZt1EscZv0r3XZRCEp5C5dF
  //   Hy5GRguJRrVKIo/KZhlG9vnnKXRzF33Bt9n8K9OH6rgeEokqnyvdCvI6g6XXzXx0ouSfv5vYza7K
  //   bJYQsMpaDcRrZfYhoPg2QuRB/qn6UDwlY91dBRP8fH1UYUr4JX7mDnWXYWQL6DYgPXAgUp+T3Xxv
  //   Oaf6z1v0Q7Hw2mLxEZHxDWcmQ/uNkFP/cEK8OKfGfA+WKjB+PvU9rPBMEaTrmdX84erDbHCJZ3nz
  //   vOYk+Qx5rfDuhkq3Slsl2i5vNuGfSeJKTTKNSFAiR2xx34h4xHOpvSfSILMaB82f+Kt674CcHjAl
  //   9uzJ3OkR3qC+5mSOt8eDZlPgB8KlMbO7JbNBHqGo4p2SOU6UxqtsM4v+0cSYkkJFeEn2fgHdFqVe
  //   sjfq1+3wRu5kCbbRjLiFlkeUeDyTanZzeH2ir2RquZCxWCG/B1STBWuf/LfWTDycNliLXt3lZNr/
  //   pBhVY/IFF5hpkeYULmYfCViL5Q6w2gz+eGSss8RE+GQ1ikizqrzjY29Oo1HlsA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
endmodule

module demo_usb_arduino (
);

  wire fitrange_1_p2, pcmsink_1_p2, scope_1_p2, serialin_1_p1, serialin_1_p2, serialin_1_p3, serialin_1_p4,
       serialin_1_p5, serialin_1_p6, serialin_1_p7, serialin_1_p8;
  wire [11:0] scaledmath_1_p1;
  wire [15:0] pcmsink_1_p1;

  // Callout #(.background("#feffa189"), .dx(57), .dy(113), .foreground("#cc45bf"), .halign("left"), .text("Connect arduino\nto usb, then poke\nto connect.")) callout_1: pin names not known
  // SerialIn #(.format("[\\n\\r]\n%8u %8u %8u %8u %8u %8u %8u %8u"), .port("/dev/ttyACM0")) serialin_1: pin names not known; wires that end beside it: serialin_1_p1, serialin_1_p2, serialin_1_p3, serialin_1_p4, serialin_1_p5, serialin_1_p6, serialin_1_p7, serialin_1_p8
  // FitRange #(.typeOut("unsigned"), .widthOut(12)) fitrange_1: pin names not known; wires that end beside it: serialin_1_p8, fitrange_1_p2, fitrange_1_p2
  // Probe on serialin_1_p8
  // ScaledMath #(.\function ("exp"), .width(12)) scaledmath_1: pin names not known; wires that end beside it: scaledmath_1_p1
  // Callout #(.background("#feffa189"), .dx(-33), .dy(-10), .foreground("#cc45bf"), .halign("left"), .text("Arduino's x-axis accelerometer is\nused to control sawtooth frequency.")) callout_2: pin names not known
  // Probe on serialin_1_p7
  // PCMSink #(.mode("twosComplement"), .rate("16 kHz"), .width(16)) pcmsink_1: pin names not known; wires that end beside it: pcmsink_1_p1, pcmsink_1_p2
  sawtooth sawtooth_1 (.AudioSignal(pcmsink_1_p1), .Freq(scaledmath_1_p1));  // open: Enable, Reset
  Clock clock_1 (.out(pcmsink_1_p2));
  // Probe on serialin_1_p6
  // Probe on serialin_1_p5
  // Scope #(.mode("twosComplement"), .scopeheight(80), .scopewidth(240), .width(16)) scope_1: pin names not known; wires that end beside it: pcmsink_1_p1, scope_1_p2
  Clock clock_2 (.out(scope_1_p2));
  // Probe on serialin_1_p4
  // Probe on serialin_1_p3
  // Probe on serialin_1_p2
  // Probe on serialin_1_p1
endmodule

module demo_arduino_trigger_boops (
);

  wire bang, clock_1_out, fitrange_1_p2, linearmap_1_p1, linearmap_1_p3, pcmsink_1_p2,
       saturatingmultiplier_1_p3, serialin_1_p1, serialin_1_p3, serialin_1_p4, serialin_1_p5, serialin_1_p7,
       serialin_1_p8;
  wire [7:0] serialin_1_p2, serialin_1_p6;
  wire [11:0] bit_extender_1_out, counter_1_q, divider_1_out, freqZ;
  wire [15:0] trianglewave_1_audiosignal;

  // Callout #(.background("#feffa189"), .dx(35), .dy(75), .foreground("#cc45bf"), .halign("left"), .text("Each click resets this counter.\nIt then goes from 0 to some\nbig number, taking a while,\nand we scale that down to [0, 7]")) callout_1: pin names not known
  Clock clock_1 (.out(clock_1_out));
  // Callout #(.background("#feffa189"), .dx(57), .dy(113), .foreground("#cc45bf"), .halign("left"), .text("Connect arduino\nto usb, then poke\nto connect.")) callout_2: pin names not known
  Counter #(.max('hfff), .ongoal("stay"), .width(12)) counter_1 (
    .Q(counter_1_q), .clk(clock_1_out), .clr(bang));  // open: load, D, count, carry
  // FitRange #(.typeOut("unsigned"), .widthIn(12), .widthOut(3)) fitrange_1: pin names not known; wires that end beside it: counter_1_q, fitrange_1_p2, fitrange_1_p2
  // SerialIn #(.format("[\\n\\r]\n%8u %8u %8u %8u %8u %8u %8u %8u"), .port("/dev/ttyACM0")) serialin_1: pin names not known; wires that end beside it: serialin_1_p1, serialin_1_p2, serialin_1_p3, serialin_1_p4, serialin_1_p5, serialin_1_p6, serialin_1_p7, serialin_1_p8
  ROM #(.addrWidth(3), .proportions("wide")) rom_1 (.sel(clock_1_out));  // open: addr, data
  assign bit_extender_1_out = {{4{1'b0}}, serialin_1_p2};  // Bit_Extender bit_extender_1
  // Probe on serialin_1_p8
  Divider #(.mode("unsigned"), .width(12)) divider_1 (
    .a(bit_extender_1_out), .b(12'ha), .out(divider_1_out));  // open: upper, rem
  // Probe on serialin_1_p7
  // Probe on serialin_1_p6
  trianglewave trianglewave_1 (.AudioSignal(trianglewave_1_audiosignal), .Freq(freqZ));  // open: Enable, Reset
  click_track click_track_1 (.click(bang), .Period(divider_1_out));  // open: Enable, count
  assign freqZ = {{4{1'b0}}, serialin_1_p6};  // Bit_Extender bit_extender_2
  // Probe on serialin_1_p5
  // LinearMap #(.domain("[0, 255]"), .range("[0, 32767]"), .widthOut(16)) linearmap_1: pin names not known; wires that end beside it: linearmap_1_p1, linearmap_1_p1, linearmap_1_p3
  // Callout #(.background("#feffa189"), .dx(-56), .dy(45), .foreground("#cc45bf"), .halign("left"), .text("x-accel controls click tempo.\nz-accel controls tone frequency.")) callout_3: pin names not known; wires that end beside it: {8{1'b0}}
  // Probe on serialin_1_p4
  // Probe on serialin_1_p3
  // SaturatingMultiplier #(.mode("twosComplement"), .normalization("fit"), .width(16)) saturatingmultiplier_1: pin names not known; wires that end beside it: trianglewave_1_audiosignal, linearmap_1_p3, saturatingmultiplier_1_p3
  // PCMSink #(.mode("twosComplement"), .rate("16 kHz"), .width(16)) pcmsink_1: pin names not known; wires that end beside it: saturatingmultiplier_1_p3, pcmsink_1_p2
  // Probe on serialin_1_p2
  // Scope #(.mode("twosComplement"), .scopeheight(80), .scopewidth(240), .width(16)) scope_1: pin names not known; wires that end beside it: saturatingmultiplier_1_p3, pcmsink_1_p2
  Clock clock_2 (.out(pcmsink_1_p2));
  // Probe on serialin_1_p1

  // Notes on the sheet:
  //   contents of rom_1 (hex, n*v repeats v):
  //   ff 4*aa 77 44
  //   These values control the "envelope" shape,
  //   attack-sustain-delay style... each value
  //   here is in range [0, 255], which we scale
  //   up to [0, 32767] before multiplying.
endmodule

module demo_arduino_multitrigger (
);

  wire bang, bang2, clock_1_out, clock_2_out, fitrange_1_p2, fitrange_3_p1, fitrange_4_p1, pcmsink_1_p2,
       saturatingadder_1_p3, saturatingmultiplier_1_p2, serialin_1_p1, serialin_1_p3, serialin_1_p4,
       serialin_1_p5, serialin_1_p7, trianglewave_2_p2, trianglewave_2_p3;
  wire [2:0] fitrange_2_p2;
  wire [7:0] serialin_1_p2, serialin_1_p6, serialin_1_p8;
  wire [11:0] bit_extender_1_out, counter_1_q, counter_2_q, divider_1_out, divider_2_out, freqX, freqZ;
  wire [15:0] trianglewave_1_audiosignal, Xnote, Znote;

  Clock clock_1 (.out(clock_1_out));
  Counter #(.max('hfff), .ongoal("stay"), .width(12)) counter_1 (
    .Q(counter_1_q), .clk(clock_2_out), .clr(bang2));  // open: load, D, count, carry
  Clock clock_2 (.out(clock_2_out));
  ROM #(.addrWidth(3), .proportions("wide")) rom_1 (.sel(clock_1_out));  // open: addr, data
  Counter #(.max('hfff), .ongoal("stay"), .width(12)) counter_2 (
    .Q(counter_2_q), .clk(clock_1_out), .clr(bang));  // open: load, D, count, carry
  // FitRange #(.typeOut("unsigned"), .widthIn(12), .widthOut(3)) fitrange_1: pin names not known; wires that end beside it: counter_2_q, fitrange_1_p2, fitrange_1_p2
  ROM #(.addrWidth(3), .proportions("wide")) rom_2 (.addr(fitrange_2_p2));  // open: data
  // FitRange #(.typeOut("unsigned"), .widthIn(12), .widthOut(3)) fitrange_2: pin names not known; wires that end beside it: counter_1_q, fitrange_2_p2
  assign bit_extender_1_out = {{4{1'b0}}, serialin_1_p2};  // Bit_Extender bit_extender_1
  // SerialIn #(.format("[\\n\\r]\n%8u %8u %8u %8u %8u %8u %8u %8u"), .port("/dev/ttyACM0")) serialin_1: pin names not known; wires that end beside it: serialin_1_p1, serialin_1_p2, serialin_1_p3, serialin_1_p4, serialin_1_p5, serialin_1_p6, serialin_1_p7, serialin_1_p8
  // Probe on serialin_1_p8
  Divider #(.mode("unsigned"), .width(12)) divider_1 (
    .a(bit_extender_1_out), .b(12'ha), .out(divider_1_out));  // open: upper, rem
  // Probe on serialin_1_p7
  // Probe on serialin_1_p6
  assign freqX = {{4{1'b0}}, serialin_1_p8};  // Bit_Extender bit_extender_2
  trianglewave trianglewave_1 (.AudioSignal(trianglewave_1_audiosignal), .Freq(freqZ));  // open: Enable, Reset
  // trianglewave trianglewave_2: pin names not known; wires that end beside it: freqX, trianglewave_2_p2, trianglewave_2_p3, trianglewave_2_p3
  click_track click_track_1 (.click(bang), .Period(divider_1_out));  // open: Enable, count
  // Probe on serialin_1_p5
  // SaturatingMultiplier #(.mode("twosComplement"), .normalization("fit"), .width(16)) saturatingmultiplier_1: pin names not known; wires that end beside it: trianglewave_1_audiosignal, saturatingmultiplier_1_p2, Znote
  // FitRange #(.typeIn("twosComplement"), .widthOut(16)) fitrange_3: pin names not known; wires that end beside it: fitrange_3_p1, fitrange_3_p1, saturatingmultiplier_1_p2
  // SaturatingMultiplier #(.mode("twosComplement"), .normalization("fit"), .width(16)) saturatingmultiplier_2: pin names not known; wires that end beside it: trianglewave_2_p2, Xnote
  // FitRange #(.typeIn("twosComplement"), .widthOut(16)) fitrange_4: pin names not known; wires that end beside it: fitrange_4_p1, fitrange_4_p1
  Divider #(.mode("unsigned"), .width(12)) divider_2 (
    .a(bit_extender_1_out), .b(12'h5), .out(divider_2_out));  // open: upper, rem
  // Probe on serialin_1_p4
  assign freqZ = {{4{1'b0}}, serialin_1_p6};  // Bit_Extender bit_extender_3
  click_track click_track_2 (.click(bang2), .Period(divider_2_out));  // open: Enable, count
  // Probe on serialin_1_p3
  // SaturatingAdder #(.mode("twosComplement"), .width(16)) saturatingadder_1: pin names not known; wires that end beside it: Znote, Xnote, saturatingadder_1_p3
  // Probe on serialin_1_p2
  // PCMSink #(.mode("twosComplement"), .rate("16 kHz"), .width(16)) pcmsink_1: pin names not known; wires that end beside it: saturatingadder_1_p3, pcmsink_1_p2
  // Scope #(.mode("twosComplement"), .scopeheight(80), .scopewidth(240), .width(16)) scope_1: pin names not known; wires that end beside it: saturatingadder_1_p3, pcmsink_1_p2
  Clock clock_3 (.out(pcmsink_1_p2));
  // Probe on serialin_1_p1

  // Notes on the sheet:
  //   contents of rom_1 (hex, n*v repeats v):
  //   76 66 55 55 44 22 11
  //   contents of rom_2 (hex, n*v repeats v):
  //   22 66 7f 7f 7f 55 55 33
endmodule

module demo_arduino_noisy_drumkit (
);

  wire bang, clock_1_out, clock_2_out, clock_3_out, comparator_1_eq, linearmap_1_p1, linearmap_1_p3,
       saturatingdivider_1_p2, saturatingmultiplier_1_p3, scope_1_p2, serialin_1_p1, serialin_1_p3,
       serialin_1_p4, serialin_1_p5, serialin_1_p7, serialin_1_p8;
  wire [2:0] counter_2_q;
  wire [7:0] attack, serialin_1_p2;
  wire [11:0] bit_extender_1_out, bit_extender_2_out, counter_1_q, divider_1_rem, divider_2_out;
  wire [15:0] highpass_filter_onepole_1_y, lowpass_filter_onepole_1_y, saturatingdivider_1_p5, slider_1_out,
       slider_2_out;

  Random #(.width(16)) RANDOM ();  // open: clk, next, out, clr
  Clock clock_1 (.out(clock_1_out));
  Counter #(.max('hfff), .ongoal("stay"), .width(12)) counter_1 (
    .Q(counter_1_q), .clk(clock_2_out), .clr(bang));  // open: load, D, count, carry
  Clock clock_2 (.out(clock_2_out));
  assign bit_extender_1_out = {{4{1'b0}}, attack};  // Bit_Extender bit_extender_1
  // SaturatingDivider #(.mode("twosComplement"), .width(16)) saturatingdivider_1: pin names not known; wires that end beside it: clock_1_out, saturatingdivider_1_p2, saturatingdivider_1_p2, 16'h3, saturatingdivider_1_p5
  Divider #(.mode("unsigned"), .width(12)) divider_1 (
    .a(counter_1_q), .b(bit_extender_1_out), .rem(divider_1_rem));  // open: out, upper
  highpass_filter_onepole highpass_filter_onepole_1 (
    .alpha(slider_1_out), .x(saturatingdivider_1_p5), .y(highpass_filter_onepole_1_y));
  Slider #(.width(16)) slider_1 (.out(slider_1_out));
  Counter #(.max('h7), .ongoal("stay"), .width(3)) counter_2 (
    .count(comparator_1_eq), .Q(counter_2_q), .clk(clock_3_out), .clr(bang));  // open: load, D, carry
  Comparator #(.width(12)) comparator_1 (.a(divider_1_rem), .b({12{1'b0}}), .eq(comparator_1_eq));  // open: gt, lt
  Clock clock_3 (.out(clock_3_out));
  // Callout #(.background("#feffa189"), .dx(-57), .dy(-102), .foreground("#cc45bf"), .text("Check if counter is perfectly\ndivisible by attack, if so,\nadvance the envelope counter.")) callout_1: pin names not known; wires that end beside it: counter_2_q
  lowpass_filter_onepole lowpass_filter_onepole_1 (
    .beta(slider_2_out), .x(highpass_filter_onepole_1_y), .y(lowpass_filter_onepole_1_y));
  Slider #(.width(16)) slider_2 (.out(slider_2_out));
  ROM #(.addrWidth(3), .proportions("wide")) rom_1 (.sel(clock_3_out));  // open: addr, data
  assign bit_extender_2_out = {{4{1'b0}}, serialin_1_p2};  // Bit_Extender bit_extender_2
  // SerialIn #(.format("[\\n\\r]\n%8u %8u %8u %8u %8u %8u %8u %8u"), .port("/dev/ttyACM0")) serialin_1: pin names not known; wires that end beside it: serialin_1_p1, serialin_1_p2, serialin_1_p3, serialin_1_p4, serialin_1_p5, attack, serialin_1_p7, serialin_1_p8
  // Probe on serialin_1_p8
  click_track click_track_1 (.click(bang), .Period(divider_2_out));  // open: Enable, count
  Divider #(.mode("unsigned"), .width(12)) divider_2 (
    .a(bit_extender_2_out), .b(12'h3), .out(divider_2_out));  // open: upper, rem
  // Probe on serialin_1_p7
  // Probe on attack
  // LinearMap #(.domain("[0, 255]"), .range("[0, 32767]"), .widthOut(16)) linearmap_1: pin names not known; wires that end beside it: linearmap_1_p1, linearmap_1_p1, linearmap_1_p3
  // Probe on serialin_1_p5
  // SaturatingMultiplier #(.mode("twosComplement"), .normalization("fit"), .width(16)) saturatingmultiplier_1: pin names not known; wires that end beside it: lowpass_filter_onepole_1_y, linearmap_1_p3, saturatingmultiplier_1_p3
  // Probe on serialin_1_p4
  // Scope #(.mode("twosComplement"), .scopeheight(80), .scopewidth(240), .width(16)) scope_1: pin names not known; wires that end beside it: saturatingmultiplier_1_p3, scope_1_p2
  // PCMSink #(.mode("twosComplement"), .rate("16 kHz"), .width(16)) pcmsink_1: pin names not known; wires that end beside it: saturatingmultiplier_1_p3, scope_1_p2
  Clock clock_4 (.out(scope_1_p2));
  // Probe on serialin_1_p3
  // Probe on serialin_1_p2
  // Probe on serialin_1_p1

  // Notes on the sheet:
  //   contents of rom_1 (hex, n*v repeats v):
  //   ff a0 80 80 30 20 10
endmodule

module demo_finch_multitrigger (
  input  in_1
);

  wire bang, bang2, btnA, btnB, clock_1_out, clock_2_out, fitrange_1_p2, fitrange_3_p1, fitrange_4_p1,
       pcmsink_1_p2, saturatingadder_1_p3, saturatingmultiplier_1_p2, trianglewave_2_p2, trianglewave_2_p3;
  wire [2:0] fitrange_2_p2;
  wire [7:0] finch_robot_bluetooth_1_distance;
  wire [11:0] counter_1_q, counter_2_q, freqX, freqZ, linearmap_2_p2, saturatingmultiplier_3_p3;
  wire [15:0] finch_robot_bluetooth_1_ax, finch_robot_bluetooth_1_ay, trianglewave_1_audiosignal, Xnote,
       Znote;

  Clock clock_1 (.out(clock_1_out));
  Counter #(.max('hfff), .ongoal("stay"), .width(12)) counter_1 (
    .Q(counter_1_q), .clk(clock_2_out), .clr(bang2));  // open: load, D, count, carry
  Clock clock_2 (.out(clock_2_out));
  ROM #(.addrWidth(3), .proportions("wide")) rom_1 (.sel(clock_1_out));  // open: addr, data
  Counter #(.max('hfff), .ongoal("stay"), .width(12)) counter_2 (
    .Q(counter_2_q), .clk(clock_1_out), .clr(bang));  // open: load, D, count, carry
  // FitRange #(.typeOut("unsigned"), .widthIn(12), .widthOut(3)) fitrange_1: pin names not known; wires that end beside it: counter_2_q, fitrange_1_p2, fitrange_1_p2
  ROM #(.addrWidth(3), .proportions("wide")) rom_2 (.addr(fitrange_2_p2));  // open: data
  // FitRange #(.typeOut("unsigned"), .widthIn(12), .widthOut(3)) fitrange_2: pin names not known; wires that end beside it: counter_1_q, fitrange_2_p2
  finch_robot_bluetooth finch_robot_bluetooth_1 (
    .Enable(in_1), .aX(finch_robot_bluetooth_1_ax), .aY(finch_robot_bluetooth_1_ay), .btnA(btnA),
    .btnB(btnB), .distance(finch_robot_bluetooth_1_distance));  // open: aZ, btnLogo
  trianglewave trianglewave_1 (.AudioSignal(trianglewave_1_audiosignal), .Freq(freqZ));  // open: Enable, Reset
  // trianglewave trianglewave_2: pin names not known; wires that end beside it: freqX, trianglewave_2_p2, trianglewave_2_p3, trianglewave_2_p3
  // Probe on freqX
  // LinearMap #(.domain("[-90, 90]"), .range("[30, 2000]"), .widthIn(16), .widthOut(12)) linearmap_1: pin names not known; wires that end beside it: finch_robot_bluetooth_1_ax, freqX
  // LinearMap #(.domain("[0, 255]"), .range("[1, 25]"), .widthOut(12)) linearmap_2: pin names not known; wires that end beside it: finch_robot_bluetooth_1_distance, linearmap_2_p2
  // SaturatingMultiplier #(.mode("twosComplement"), .normalization("fit"), .width(16)) saturatingmultiplier_1: pin names not known; wires that end beside it: trianglewave_1_audiosignal, saturatingmultiplier_1_p2, Znote
  // FitRange #(.typeIn("twosComplement"), .widthOut(16)) fitrange_3: pin names not known; wires that end beside it: fitrange_3_p1, fitrange_3_p1, saturatingmultiplier_1_p2
  // SaturatingMultiplier #(.mode("twosComplement"), .normalization("fit"), .width(16)) saturatingmultiplier_2: pin names not known; wires that end beside it: trianglewave_2_p2, Xnote
  // FitRange #(.typeIn("twosComplement"), .widthOut(16)) fitrange_4: pin names not known; wires that end beside it: fitrange_4_p1, fitrange_4_p1
  // Probe on freqZ
  // LinearMap #(.domain("[-90, 90]"), .range("[30, 4095]"), .widthIn(16), .widthOut(12)) linearmap_3: pin names not known; wires that end beside it: finch_robot_bluetooth_1_ay, freqZ
  // Probe on linearmap_2_p2
  // SaturatingAdder #(.mode("twosComplement"), .width(16)) saturatingadder_1: pin names not known; wires that end beside it: Znote, Xnote, saturatingadder_1_p3
  // PCMSink #(.mode("twosComplement"), .rate("16 kHz"), .width(16)) pcmsink_1: pin names not known; wires that end beside it: saturatingadder_1_p3, pcmsink_1_p2
  // Scope #(.mode("twosComplement"), .scopeheight(80), .scopewidth(240), .width(16)) scope_1: pin names not known; wires that end beside it: saturatingadder_1_p3, pcmsink_1_p2
  Clock clock_3 (.out(pcmsink_1_p2));
  click_track click_track_1 (.click(bang), .Period(linearmap_2_p2), .Enable(btnA));  // open: count
  // SaturatingMultiplier #(.mode("twosComplement"), .width(12)) saturatingmultiplier_3: pin names not known; wires that end beside it: linearmap_2_p2, 12'h2, saturatingmultiplier_3_p3
  click_track click_track_2 (.click(bang2), .Period(saturatingmultiplier_3_p3), .Enable(btnB));  // open: count

  // Notes on the sheet:
  //   contents of rom_1 (hex, n*v repeats v):
  //   76 66 55 55 44 22 11
  //   contents of rom_2 (hex, n*v repeats v):
  //   22 66 7f 7f 7f 55 55
endmodule

module demo_scaled_math (
);

  wire bang_out, clock_1_out, counter_carry, fitrange_1_p2, go, s_r_ff_1_q, scaledmath_1_p2, scaledmath_2_p2,
       scaledmath_3_p2, scaledmath_4_p2, scaledmath_5_p2, scope_1_p1, scope_1_p3;
  wire [11:0] counter_q;

  Button bang (.out(bang_out));
  // Callout #(.dx(45), .dy(53), .foreground("#8f726e"), .text("Changes from unsigned [0, 4096]\nto signed [-2048, 2047] scale.")) callout_1: pin names not known
  // Callout #(.background("#fbfc0280"), .dx(-36), .dy(-31), .foreground("#d15c5a"), .text("click to plot")) callout_2: pin names not known
  Counter #(.max('hfff), .width(12)) counter (
    .count(go), .Q(counter_q), .carry(counter_carry), .clk(clock_1_out), .clr(bang_out));  // open: load, D
  Clock clock_1 (.out(clock_1_out));
  // FitRange #(.widthIn(12), .widthOut(12)) fitrange_1: pin names not known; wires that end beside it: counter_q, fitrange_1_p2
  S_R_Flip_Flop s_r_ff_1 (
    .S(counter_carry), .clk(clock_1_out), .R(bang_out), .Q(s_r_ff_1_q));  // open: Qn, preset, reset
  nor nor_1 (go, counter_carry, s_r_ff_1_q);
  // Callout #(.dx(-52), .dy(-55), .foreground("#8f726e"), .text("This SR Latch s \"set\" to 1 when the\ncounter overflows, and \"reset\" to 0\nwhen bang is pressed.")) callout_3: pin names not known
  // ScaledMath #(.mode("twosComplement"), .width(12)) scaledmath_1: pin names not known; wires that end beside it: fitrange_1_p2, scaledmath_1_p2, scaledmath_1_p2
  // ScaledMath #(.\function ("exp"), .mode("twosComplement"), .width(12)) scaledmath_2: pin names not known; wires that end beside it: fitrange_1_p2, scaledmath_2_p2, scaledmath_2_p2
  // Scope #(.mode("twosComplement"), .samples(4096), .scopeheight(80), .scopewidth(240), .width(12)) scope_1: pin names not known; wires that end beside it: scope_1_p1, go, scope_1_p3
  // ScaledMath #(.\function ("log"), .mode("twosComplement"), .width(12)) scaledmath_3: pin names not known; wires that end beside it: fitrange_1_p2, scaledmath_3_p2, scaledmath_3_p2
  // LineSelect #(.\default ("undefined"), .mode("twosComplement"), .spacing(4), .width(12)) lineselect_1: pin names not known; wires that end beside it: scope_1_p1
  // ScaledMath #(.\function ("abs"), .mode("twosComplement"), .width(12)) scaledmath_4: pin names not known; wires that end beside it: fitrange_1_p2, scaledmath_4_p2, scaledmath_4_p2
  // ScaledMath #(.\function ("sinc"), .mode("twosComplement"), .width(12)) scaledmath_5: pin names not known; wires that end beside it: fitrange_1_p2, scaledmath_5_p2, scaledmath_5_p2
  // Callout #(.background("#fbfc0280"), .dx(-52), .dy(-55), .foreground("#d15c5a"), .text("select one to display")) callout_4: pin names not known
  Clock clock_2 (.out(scope_1_p3));
  // Callout #(.dx(-52), .dy(-55), .foreground("#8f726e"), .text("Function output displays here")) callout_5: pin names not known

  // Notes on the sheet:
  //   Demonstration of the audio "Scaled Math" feature. Click one of the buttons in the mux to choose
  //   which function you want to plot, then click bang.
  //   The counter sweeps from 0 to 4096, and that gets shifted to signed range [-2048, 2047], before
  //   being fed into five different functions, and one of them is sent to the screen for display.
  //   The other circuitry is used to stop the counter and plotting when it overflows. 
endmodule

module demo_realtime_clock (
);

  wire clock_1_out, realtimeclock_1_p2, realtimeclock_2_p1, realtimeclock_2_p2, realtimeclock_3_p1,
       realtimeclock_3_p2, realtimeclock_4_p1, realtimeclock_4_p2, realtimeclock_5_p1, realtimeclock_5_p2;

  Clock clock_1 (.out(clock_1_out));
  // Probe on realtimeclock_1_p2
  // RealTimeClock realtimeclock_1: pin names not known; wires that end beside it: clock_1_out, realtimeclock_1_p2
  // Callout #(.dx(24), .dy(-93), .foreground("#d15c5a"), .text("Actual date & time")) callout_1: pin names not known
  // Probe on realtimeclock_2_p2
  // RealTimeClock #(.clock("uptime-s")) realtimeclock_2: pin names not known; wires that end beside it: realtimeclock_2_p1, realtimeclock_2_p2
  Clock clock_2 (.out(realtimeclock_2_p1));
  // Probe on realtimeclock_3_p2
  // RealTimeClock #(.clock("uptime-ms")) realtimeclock_3: pin names not known; wires that end beside it: realtimeclock_3_p1, realtimeclock_3_p2
  Clock clock_3 (.out(realtimeclock_3_p1));
  // Probe on realtimeclock_4_p2
  // RealTimeClock #(.clock("uptime-us")) realtimeclock_4: pin names not known; wires that end beside it: realtimeclock_4_p1, realtimeclock_4_p2
  Clock clock_4 (.out(realtimeclock_4_p1));
  // Probe on realtimeclock_5_p2
  // RealTimeClock #(.clock("uptime-ns")) realtimeclock_5: pin names not known; wires that end beside it: realtimeclock_5_p1, realtimeclock_5_p2
  Clock clock_5 (.out(realtimeclock_5_p1));
  // Callout #(.dx(-52), .dy(-55), .foreground("#d15c5a"), .text("Nanoseconds!!\ngo quick, 1 billion per second.\nAt 32 bits, this will overflow \nin 4 seconds.")) callout_2: pin names not known
  // Callout #(.dx(-66), .dy(-8), .foreground("#d15c5a"), .text("Time since the\nsimulation was\nlast reset.")) callout_3: pin names not known

  // Notes on the sheet:
  //   Demonstration of the external "real time clock". These give you access to the current date
  //   and time (i.e. the number of seconds since the computer epoch began, midnight jan 1, 1970).
  //   Or you can access the "uptime", the amout of time since the simulation began or was reset.
  //   Using 32 bits means these won't overflow for a while yet. If you choose a narrower bit-width,
  //   it will overflow (and wrap around) quicker.
endmodule

module demo_adjustable_filter_ord1 (
  input  in_1,
  input  in_2,
  input  in_3
);

  wire pcmsink_1_p2, scope_1_p2, scope_2_p2;
  wire [7:0] Volume_Control_p1;
  wire [11:0] freq_out, scaledmath_1_p2;
  wire [15:0] a_1_out, a_2_out, filter_buildingblock_1_y, filter_buildingblock_1_z_1,
       filter_buildingblock_2_y, recording_thank_you_1_audiosignal, saturatingadder_1_p3, scope_1_p1,
       sinwave_1_audiosignal, volume_limiter_1_adjustedsample, white_noise_1_audiosignal;

  Slider #(.width(12)) freq (.out(freq_out));
  // ScaledMath #(.\function ("exp"), .width(12)) scaledmath_1: pin names not known; wires that end beside it: freq_out, scaledmath_1_p2
  // Callout #(.dx(51), .dy(-70), .foreground("#0e994c"), .text("Pick your source\nsignal(s), and also\nbe sure to enable them.")) callout_1: pin names not known
  white_noise white_noise_1 (.Enable(in_1), .AudioSignal(white_noise_1_audiosignal));
  sinwave sinwave_1 (.Enable(in_2), .AudioSignal(sinwave_1_audiosignal), .Freq(scaledmath_1_p2));  // open: Reset
  recording_thank_you recording_thank_you_1 (
    .AudioSignal(recording_thank_you_1_audiosignal), .Enable(in_3));  // open: Reset
  // Scope #(.mode("twosComplement"), .samples(800), .scopewidth(120), .width(16)) scope_1: pin names not known; wires that end beside it: scope_1_p1, scope_1_p2
  Clock clock_1 (.out(scope_1_p2));
  // LineSelect #(.behavior("one"), .spacing(4), .width(16)) lineselect_1: pin names not known; wires that end beside it: white_noise_1_audiosignal, sinwave_1_audiosignal, recording_thank_you_1_audiosignal, scope_1_p1
  Slider #(.mode("twosComplement"), .width(16)) a_1 (.out(a_1_out));
  filter_buildingblock filter_buildingblock_1 (
    .X(scope_1_p1), .\β (a_1_out), .Z_1(filter_buildingblock_1_z_1), .Y(filter_buildingblock_1_y));
  // Callout #(.dx(21), .dy(-43), .foreground("#0e994c"), .text("A two-part filter, with two coefficients.\nIn effect, this takes the two previous\nsamples, and mixes them together\nin some combination.")) callout_2: pin names not known
  Slider #(.mode("twosComplement"), .width(16)) a_2 (.out(a_2_out));
  filter_buildingblock filter_buildingblock_2 (
    .X(filter_buildingblock_1_z_1), .\β (a_2_out), .Y(filter_buildingblock_2_y));  // open: Z_1
  // SaturatingAdder #(.mode("twosComplement"), .width(16)) saturatingadder_1: pin names not known; wires that end beside it: filter_buildingblock_2_y, filter_buildingblock_1_y, saturatingadder_1_p3
  volume_limiter volume_limiter_1 (
    .AudioSample(saturatingadder_1_p3), .Volume(Volume_Control_p1),
    .AdjustedSample(volume_limiter_1_adjustedsample));
  // Dial #(.mode("twosComplement")) Volume_Control: pin names not known; wires that end beside it: Volume_Control_p1
  // Scope #(.mode("twosComplement"), .samples(800), .width(16)) scope_2: pin names not known; wires that end beside it: volume_limiter_1_adjustedsample, scope_2_p2
  Clock clock_2 (.out(scope_2_p2));
  // PCMSink #(.bufsize(500), .mode("twosComplement"), .rate("16 kHz"), .width(16)) pcmsink_1: pin names not known; wires that end beside it: volume_limiter_1_adjustedsample, pcmsink_1_p2
  Clock clock_3 (.out(pcmsink_1_p2));

  // Notes on the sheet:
  //   Original Signal
  //   Final Signal
endmodule

module demo_FIR_filter_ord1 (
  input  in_1,
  input  in_2,
  input  in_3
);

  wire pcmsink_1_p2, scope_1_p2, scope_2_p2;
  wire [7:0] Volume_Control_p1;
  wire [11:0] freq_out, scaledmath_1_p2;
  wire [15:0] b_1_out, b_2_out, b_3_out, filter_buildingblock_1_y, filter_buildingblock_1_z_1,
       filter_buildingblock_2_y, filter_buildingblock_2_z_1, filter_buildingblock_3_y,
       recording_thank_you_1_audiosignal, saturatingadder_1_p4, scope_1_p1, scope_2_p1,
       sinwave_1_audiosignal, white_noise_1_audiosignal;

  Slider #(.width(12)) freq (.out(freq_out));
  // ScaledMath #(.\function ("exp"), .width(12)) scaledmath_1: pin names not known; wires that end beside it: freq_out, scaledmath_1_p2
  // Callout #(.dx(51), .dy(-70), .foreground("#0e994c"), .text("Pick your source\nsignal(s), and also\nbe sure to enable them.")) callout_1: pin names not known
  white_noise white_noise_1 (.Enable(in_1), .AudioSignal(white_noise_1_audiosignal));
  sinwave sinwave_1 (.Enable(in_2), .AudioSignal(sinwave_1_audiosignal), .Freq(scaledmath_1_p2));  // open: Reset
  recording_thank_you recording_thank_you_1 (
    .AudioSignal(recording_thank_you_1_audiosignal), .Enable(in_3));  // open: Reset
  // Scope #(.mode("twosComplement"), .samples(800), .scopewidth(120), .width(16)) scope_1: pin names not known; wires that end beside it: scope_1_p1, scope_1_p2
  Clock clock_1 (.out(scope_1_p2));
  // LineSelect #(.behavior("one"), .spacing(4), .width(16)) lineselect_1: pin names not known; wires that end beside it: white_noise_1_audiosignal, sinwave_1_audiosignal, recording_thank_you_1_audiosignal, scope_1_p1
  Slider #(.mode("twosComplement"), .width(16)) b_1 (.out(b_1_out));
  filter_buildingblock filter_buildingblock_1 (
    .X(scope_1_p1), .\β (b_1_out), .Z_1(filter_buildingblock_1_z_1), .Y(filter_buildingblock_1_y));
  // Callout #(.dx(21), .dy(-43), .foreground("#0e994c"), .text("A three-part filter, with three coefficients.\nIn effect, this takes the three previous\nsamples, and mixes them together\nin some combination.")) callout_2: pin names not known
  Slider #(.mode("twosComplement"), .width(16)) b_2 (.out(b_2_out));
  filter_buildingblock filter_buildingblock_2 (
    .X(filter_buildingblock_1_z_1), .\β (b_2_out), .Z_1(filter_buildingblock_2_z_1),
    .Y(filter_buildingblock_2_y));
  filter_buildingblock filter_buildingblock_3 (
    .X(filter_buildingblock_2_z_1), .\β (b_3_out), .Y(filter_buildingblock_3_y));  // open: Z_1
  Slider #(.mode("twosComplement"), .width(16)) b_3 (.out(b_3_out));
  // SaturatingAdder #(.mode("twosComplement"), .width(16)) saturatingadder_1: pin names not known; wires that end beside it: filter_buildingblock_3_y, filter_buildingblock_2_y, filter_buildingblock_1_y, saturatingadder_1_p4
  // Dial #(.mode("twosComplement")) Volume_Control: pin names not known; wires that end beside it: Volume_Control_p1
  // Scope #(.mode("twosComplement"), .samples(800), .width(16)) scope_2: pin names not known; wires that end beside it: scope_2_p1, scope_2_p2
  Clock clock_2 (.out(scope_2_p2));
  // PCMSink #(.bufsize(500), .mode("twosComplement"), .rate("16 kHz"), .width(16)) pcmsink_1: pin names not known; wires that end beside it: scope_2_p1, pcmsink_1_p2
  volume_limiter volume_limiter_1 (
    .AudioSample(saturatingadder_1_p4), .Volume(Volume_Control_p1), .AdjustedSample(scope_2_p1));
  Clock clock_3 (.out(pcmsink_1_p2));

  // Notes on the sheet:
  //   Original Signal
  //   Final Signal
endmodule

module demo_digital_resonator (
  input  in_1,
  input  in_2,
  input  in_3
);

  wire pcmsink_1_p2, scope_1_p2, scope_2_p2, scope_3_p2;
  wire [7:0] Volume_Control_p1;
  wire [11:0] freq_out, scaledmath_1_p2;
  wire [15:0] a_1_out, a_2_out, b_0_out, filter_buildingblock_1_y, filter_buildingblock_2_z_1,
       recording_thank_you_1_audiosignal, saturatingadder_1_p2, saturatingadder_1_p3, saturatingadder_1_p4,
       scope_1_p1, scope_3_p1, sinwave_1_audiosignal, white_noise_1_audiosignal;

  Slider #(.width(12)) freq (.out(freq_out));
  // ScaledMath #(.\function ("exp"), .width(12)) scaledmath_1: pin names not known; wires that end beside it: freq_out, scaledmath_1_p2
  // Callout #(.dx(51), .dy(-70), .foreground("#0e994c"), .text("Pick your source\nsignal(s), and also\nbe sure to enable them.")) callout_1: pin names not known
  white_noise white_noise_1 (.Enable(in_1), .AudioSignal(white_noise_1_audiosignal));
  sinwave sinwave_1 (.Enable(in_2), .AudioSignal(sinwave_1_audiosignal), .Freq(scaledmath_1_p2));  // open: Reset
  recording_thank_you recording_thank_you_1 (
    .AudioSignal(recording_thank_you_1_audiosignal), .Enable(in_3));  // open: Reset
  // Scope #(.mode("twosComplement"), .samples(800), .scopewidth(120), .width(16)) scope_1: pin names not known; wires that end beside it: scope_1_p1, scope_1_p2
  Clock clock_1 (.out(scope_1_p2));
  // LineSelect #(.behavior("one"), .spacing(4), .width(16)) lineselect_1: pin names not known; wires that end beside it: white_noise_1_audiosignal, sinwave_1_audiosignal, recording_thank_you_1_audiosignal, scope_1_p1
  Slider #(.mode("twosComplement"), .width(16)) b_0 (.out(b_0_out));
  // Callout #(.dx(21), .dy(-43), .foreground("#0e994c"), .text("This first stage\nattenuates the\nsignal, making\nit smaller.")) callout_2: pin names not known
  filter_buildingblock filter_buildingblock_1 (
    .X(scope_1_p1), .\β (b_0_out), .Y(filter_buildingblock_1_y));  // open: Z_1
  // Scope #(.mode("twosComplement"), .samples(800), .scopewidth(120), .width(16)) scope_2: pin names not known; wires that end beside it: filter_buildingblock_1_y, scope_2_p2
  Clock clock_2 (.out(scope_2_p2));
  // SaturatingAdder #(.mode("twosComplement"), .width(16)) saturatingadder_1: pin names not known; wires that end beside it: filter_buildingblock_1_y, saturatingadder_1_p2, saturatingadder_1_p3, saturatingadder_1_p4
  Slider #(.mode("twosComplement"), .width(16)) a_1 (.out(a_1_out));
  filter_buildingblock filter_buildingblock_2 (
    .X(saturatingadder_1_p4), .\β (a_1_out), .Z_1(filter_buildingblock_2_z_1), .Y(saturatingadder_1_p2));
  // Callout #(.dx(21), .dy(-43), .foreground("#0e994c"), .text("The second stage involves a 2-part filter, both looping\nback in a feedback loop. Adjust all the \ncoefficients (b_0, a_1, a_2) to achieve diferent effects.")) callout_3: pin names not known
  Slider #(.mode("twosComplement"), .width(16)) a_2 (.out(a_2_out));
  filter_buildingblock filter_buildingblock_3 (
    .X(filter_buildingblock_2_z_1), .\β (a_2_out), .Y(saturatingadder_1_p3));  // open: Z_1
  // Scope #(.mode("twosComplement"), .samples(800), .width(16)) scope_3: pin names not known; wires that end beside it: scope_3_p1, scope_3_p2
  volume_limiter volume_limiter_1 (
    .AudioSample(saturatingadder_1_p4), .Volume(Volume_Control_p1), .AdjustedSample(scope_3_p1));
  // Dial #(.mode("twosComplement")) Volume_Control: pin names not known; wires that end beside it: Volume_Control_p1
  Clock clock_3 (.out(scope_3_p2));
  // PCMSink #(.bufsize(500), .mode("twosComplement"), .rate("16 kHz"), .width(16)) pcmsink_1: pin names not known; wires that end beside it: scope_3_p1, pcmsink_1_p2
  Clock clock_4 (.out(pcmsink_1_p2));

  // Notes on the sheet:
  //   Original Signal
  //   Attenuated Signal
  //   Final Signal
endmodule

module sawtooth_80hz (
  input  Enable,
  input  Reset,
  output [15:0] AudioSignal
);

  wire clock_1_out;
  wire [15:0] counter_1_q;

  // Callout #(.background("#feffa189"), .dx(37), .dy(98), .foreground("#cc45bf"), .halign("right"), .text("The heart of the circuit,\nan 16 bit counter configured\nto start counting at 100, \ncount up to 200,\nthen reset back to 0\nand start over again.")) callout_1: pin names not known
  Clock clock_1 (.out(clock_1_out));
  // RGBLED rgbled_1: pin names not known; wires that end beside it: Enable, Reset
  Counter #(.\initial ('h64), .max('hc8), .ongoal("load"), .width(16)) counter_1 (
    .count(Enable), .Q(counter_1_q), .clk(clock_1_out), .clr(Reset));  // open: load, D, carry
  // Callout #(.background("#feffa189"), .dx(-32), .dy(69), .foreground("#cc45bf"), .text("This handy \"linear map\" is configured\nto take values between [0, 200] and adjust \nthem so they fall within [-10000, +1000]")) callout_2: pin names not known
  // LinearMap #(.domain("[0, 200]"), .range("[-10000, 10000]"), .widthIn(16), .widthOut(16)) linearmap_1: pin names not known; wires that end beside it: counter_1_q, AudioSignal
  // Callout #(.background("#feffa189"), .dx(26), .dy(-56), .foreground("#cc45bf"), .text("16 bit signed audio samples in range [-10000, +10000]\nmeant to be played using 16 kHz audio PCM output.")) callout_3: pin names not known

  // Notes on the sheet:
  //   a 80 Hz sawtooth wave generator - When enabled, counts from -10000 to +10000, then
  //   resets to 0 and counts up again, forever. It counts by 100 per step, so at 16 kHz simulation speed,
  //   this produces an approx 80 Hz tone (because it has 201 steps, and 16000/201 = 79.6).
  //   Q: Can we instead make the counter start at 0 and count to 100, then go to -100?
  //   A: Sadly, Logisim "counter" components can't do that directly. They always reset to 0. 
  //   This is what the "subtract 100" is for. (Except, see sawtooth-80hz-alternate for a slightly
  //   different approach, which loads -100 into the counter whenever it reaches +100.)
  //   Q: Ok, but why not at least configure the counter to count by 100 at a time?
  //   A: Because Logisim "counter" commponents always count by 1.
  //   This is what the "multiply by 100" is for. The trick is that "count-by-one-then-multiply-by-100"
  //   achieves the same result as "count-by-100".
  //   Q: Why do we count by 100? Why not count by 75? Or 150? Or anything else?
  //   A: Good question! Try it and see what happens! 
endmodule

module sawtooth_80hz_alternate (
  input  Enable,
  input  Reset,
  output [15:0] AudioSignal
);

  wire clock_1_out, hitTop;
  wire [15:0] counter_1_q;

  // Callout #(.background("#feffa189"), .dx(31), .dy(125), .foreground("#cc45bf"), .halign("right"), .text("The heart of the circuit,\nan 16 bit counter configured\nto start at 0, counting up, \nthen when it reaches +100,\nit loads \"D\" = -100\nand resumes counting up.")) callout_1: pin names not known
  Clock clock_1 (.out(clock_1_out));
  // RGBLED rgbled_1: pin names not known; wires that end beside it: Enable, Reset
  Counter #(.max('hffff), .width(16)) counter_1 (
    .load(hitTop), .D(16'hff9c), .count(Enable), .Q(counter_1_q), .clk(clock_1_out), .clr(Reset));  // open: carry
  Comparator #(.width(16)) comparator_1 (.a(16'h64), .b(counter_1_q), .eq(hitTop));  // open: gt, lt
  // SaturatingMultiplier #(.mode("twosComplement"), .width(16)) saturatingmultiplier_1: pin names not known; wires that end beside it: counter_1_q, 16'h64, AudioSignal
  // Callout #(.background("#feffa189"), .dx(26), .dy(-56), .foreground("#cc45bf"), .text("16 bit signed audio samples in range [-10000, +10000]\nmeant to be played using 16 kHz audio PCM output.\nThis is the counter value, which is within [-100, +100], \nbut multiplied by 100 to get a louder sound.")) callout_2: pin names not known
  // Callout #(.dx(-144), .dy(57), .foreground("#cc45bf"), .text("This does a comparison to see if\nthe signal has reached +100. if so,\nthe \"hitTop\" signal triggers the\ncounter to load \"D\" = -100.")) callout_3: pin names not known

  // Notes on the sheet:
  //   another 80 Hz sawtooth wave generator - This one produces the same results as the
  //   sawtooth-80hz circuit, but it is implemented in a different way.
  //   Q: Why not configure the counter to just count by 100 at a time?
  //   A: Because Logisim "counter" commponents always count by 1.
  //   This is what the "multiply by 100" is for. The trick is that "count-by-one-then-multiply-by-100"
  //   achieves the same result as "count-by-100".
  //   Q: Why do we count by 100? Why not count by 75? Or 150? Or anything else?
  //   A: Good question! Try it and see what happens! 
endmodule

module triangle_160hz (
  input  Enable,
  input  Reset,
  output [15:0] AudioSample
);

  wire clock_1_out, clock_2_out, d_ff_1_q, d_ff_1_qn, Direction, hitBottom, hitTop, or_1_out;
  wire [15:0] counter_1_q;

  // Callout #(.background("#feffa189"), .dx(33), .dy(41), .foreground("#cc45bf"), .halign("right"), .text("The heart of this circuit, a\n16-bit counter, configured to\nstart at 0.")) callout_1: pin names not known
  Clock clock_1 (.out(clock_1_out));
  // RGBLED rgbled_1: pin names not known; wires that end beside it: Enable, Reset
  // Callout #(.dx(57), .dy(34), .foreground("#cc45bf"), .halign("right"), .text("This part keeps track of \nwhich direction we want \nto count (0=up, 1=down).")) callout_2: pin names not known
  Counter #(.max('hffff), .width(16)) counter_1 (
    .count(Enable), .Q(counter_1_q), .up(Direction), .clk(clock_1_out), .clr(Reset));  // open: load, D, carry
  Clock clock_2 (.out(clock_2_out));
  Comparator #(.width(16)) comparator_1 (.a(16'h19), .b(counter_1_q), .eq(hitTop));  // open: gt, lt
  Comparator #(.width(16)) comparator_2 (.a(16'hffe7), .b(counter_1_q), .eq(hitBottom));  // open: gt, lt
  // SaturatingMultiplier #(.mode("twosComplement"), .width(16)) saturatingmultiplier_1: pin names not known; wires that end beside it: counter_1_q, 16'h190, AudioSample
  D_Flip_Flop d_ff_1 (.clk(clock_2_out), .D(Direction), .Q(d_ff_1_q), .Qn(d_ff_1_qn));  // open: preset, reset
  Multiplexer multiplexer_1 (.in0(d_ff_1_q), .in1(d_ff_1_qn), .out(Direction), .sel(or_1_out), .en(Enable));
  or or_1 (or_1_out, hitBottom, hitTop);
  // Callout #(.dx(-144), .dy(57), .foreground("#cc45bf"), .text("These two comparisons are checking \nto see if the counter equals +25 (hit bottom)\nor if it equals -25 (hit top)")) callout_3: pin names not known
  // Callout #(.background("#feffa189"), .dx(-74), .dy(-56), .foreground("#cc45bf"), .text("16 bit signed audio samples in range [-10000, +10000]\nmeant to be played using 16 kHz audio PCM output.\nThis is the result of taking the counter, which is\nin the range [-25, +25], and multiplying it by 400.")) callout_4: pin names not known
  // Callout #(.dx(-106), .dy(-33), .foreground("#cc45bf"), .text("This part makes it change \ndirection when we \n\"hit top\" OR \"hit bottom\".\nBut if en=0, it goes\nback to \"up\" direction.")) callout_5: pin names not known

  // Other names for the same wires on the sheet: en = Enable

  // Notes on the sheet:
  //   a clumsy 120 hz triangle wave generator - When enabled, it counts up to 10000, then counts
  //   down to -10000, then back up again to 10000, etc., forever.  It counts by 400 at a time, so
  //   at 16kHz simulation speed, this produces a 120 Hz triangle wave (since it goes through 50 steps
  //   on the way up, and 50 steps on the way down, for 100 steps per wave, and 16000/100 = 160).
endmodule

module triangle_62_5hz (
  input  Enable,
  input  Reset,
  output [15:0] AudioSample
);

  wire clock_1_out, comparator_1_gt;
  wire [15:0] counter_1_q, multiplexer_1_out, saturatingsubtractor_1_p3, saturatingsubtractor_2_p3;

  // RGBLED rgbled_1: pin names not known; wires that end beside it: Enable, Reset
  // Callout #(.background("#feffa189"), .dx(24), .dy(43), .foreground("#cc45bf"), .halign("right"), .text("A counter, the\nheart of the circuit.\nIt counts from 0 to 255,\nthen resets to 0 again.")) callout_1: pin names not known
  Counter #(.width(16)) counter_1 (
    .count(Enable), .Q(counter_1_q), .clk(clock_1_out), .clr(Reset));  // open: load, D, carry
  Clock clock_1 (.out(clock_1_out));
  // Callout #(.dx(67), .dy(-76), .foreground("#cc45bf"), .halign("right"), .text("(2) But then as we count from x=128 to x=255, we do\nsomething different. We take (192-x), before the\nmultiplication. This gives the downward sequence:\n192-128=64   ---> times 150 ---> 9600\n192-129=63    --> times 150 ---> 9450\n192-130=62   ---> times 150 ---> 9300\netc etc etc\n192-253=-61   ---> times 2 ---> -9150\n192-254=-62   ---> times 2 ---> -9300\n192-255=-63   ---> times 2 ---> -9450")) callout_2: pin names not known
  // SaturatingSubtractor #(.mode("twosComplement"), .width(16)) saturatingsubtractor_1: pin names not known; wires that end beside it: counter_1_q, 16'h40, saturatingsubtractor_1_p3
  // SaturatingSubtractor #(.mode("twosComplement"), .width(16)) saturatingsubtractor_2: pin names not known; wires that end beside it: 16'hc0, counter_1_q, saturatingsubtractor_2_p3
  Comparator #(.mode("unsigned"), .width(16)) comparator_1 (
    .a(counter_1_q), .b(16'h7f), .gt(comparator_1_gt));  // open: eq, lt
  // Callout #(.dx(-55), .dy(82), .foreground("#cc45bf"), .halign("left"), .text("(1) The trick here is cute...\nFirst we count from x=0 to x=127. For those values, \nwe subtract 64, to get a result between -64 and 63.\nAfter the mux, this is multiplied by 150 to get a value\nin the range [-9600, +9450].")) callout_3: pin names not known
  Multiplexer #(.enable("false"), .width(16)) multiplexer_1 (
    .in0(saturatingsubtractor_1_p3), .in1(saturatingsubtractor_2_p3), .out(multiplexer_1_out),
    .sel(comparator_1_gt));
  // Callout #(.dx(-72), .dy(18), .foreground("#cc45bf"), .halign("left"), .text("(3) Last piece... this comparison, and the MUX, \nis deciding whether to use  \"x-64\" or \"192-x\"\nbefore the multiply-by-150. The decision is\nbased on a comparison:\n if x > 127  then use \"x-64\"\n otherwise use \"192-x\"")) callout_4: pin names not known
  // SaturatingMultiplier #(.mode("twosComplement"), .width(16)) saturatingmultiplier_1: pin names not known; wires that end beside it: multiplexer_1_out, 16'h50, AudioSample

  // Notes on the sheet:
  //   a somewhat clumsy 62.5 hz triangle wave generator - When enabled, it counts up to around 10000, then counts back
  //   down to around -10000, then back up again, forever. This counts through exactly 256 steps, counting by 80 each step.
  //   At 16kHz simulation speed, this produces a 62.5 Hz triangle wave (since it goes through 256 steps, and 16000/512 = 62.5).
endmodule

module sawtooth (
  input  Enable,
  input  Reset,
  input  [11:0] Freq,
  output [15:0] AudioSignal
);

  wire clock_1_out;
  wire [31:0] adder_1_out, bit_extender_1_out, register_1_q, step;

  // Callout #(.background("#feffa189"), .dx(39), .dy(65), .foreground("#cc45bf"), .text("The heart of this circuit is a\n 32-bit value, with a feedback loop\nadding \"step\" during each clock tick.")) callout_1: pin names not known
  // RGBLED rgbled_1: pin names not known; wires that end beside it: Enable, Reset
  // Probe on Freq
  assign bit_extender_1_out = {{20{1'b0}}, Freq};  // Bit_Extender bit_extender_1
  Adder #(.width(32)) adder_1 (.a(register_1_q), .b(step), .out(adder_1_out));  // open: cin, cout
  Clock clock_1 (.out(clock_1_out));
  Multiplier #(.width(32)) multiplier_1 (.a(bit_extender_1_out), .b(32'h41893), .out(step));  // open: cin, cout
  Register #(.width(32)) register_1 (.D(adder_1_out), .en(Enable), .Q(register_1_q), .clk(clock_1_out), .clr(Reset));
  // LinearMap #(.domain("[-2147483648, 2147483647]"), .range("[-10000, 10000]"), .widthIn(32), .widthOut(16)) linearmap_1: pin names not known; wires that end beside it: register_1_q, AudioSignal
  // Callout #(.dx(-68), .dy(80), .foreground("#cc45bf"), .text("This \"linear map\" takes values\nin the range [-2billion, +2billion]\nand adjusts them to fall within [-10000, +10000]")) callout_2: pin names not known

  // Notes on the sheet:
  //   a flexible sawtooth generator - When enabled, counts up to about 10000 then
  //   resets to -10000 and counts up again, forever. But it counts upwards at a speed
  //   determined by one of the inputs, you can choose any frequency from 1Hz to 4095Hz.
  //   Q: Why is this using a 32-bit counter instead of 16 bits?
  //   A: Because it lets us adjust the step size more finely,
  //   more precisly controlling exactly how long it takes to
  //   reach the maximum and wrap around back to zero.
  //   With a 32-bit counter (0 to 4billion), we have a lot
  //   of possible step sizes to choose from to control how
  //   often the counter wraps around.
  //   The counter up above is 32-bits, going from about -2billion to 2 billion,
  //   before wrapping around to -2billion again. Each simulated clock tick we
  //   add some "step" to the counter, so if the simulation is running
  //   at 16kHz for audio output, we'd wrap around this often:
  //        F=(16000*stepsize)/4billion  wraparounds per second.
  //   In other words, that's the frequency of the sawtooth we
  //   generated.  Inversely, if we want a given frequency F,
  //   we can calculate the needed stepsize to get it:
  //     stepsize = F*4billion/16000
  //                    = F*268435.46
  //   Q: Why is the frequency limited a 4095hz? Can we go higher?
  //   A: The "Freq" input is a 12 bit number, which maxes out at 4095.
  //   It would be simple to allow higher numbers, by using more bits
  //   for "Freq". But with 16kHz PCM audio, we are limited to 8000hz
  //   maximum anyway, and sounds above 4000hz sound pretty high
  //   anyway.
endmodule

module squarewave (
  input  Enable,
  input  Reset,
  input  [11:0] Freq,
  input  [15:0] DutyCycle,
  output [15:0] AudioSignal
);

  wire comparator_1_gt;
  wire [15:0] sweep_0_to_65535_1_sweep;

  sweep_0_to_65535 sweep_0_to_65535_1 (
    .Enable(Enable), .Sweep(sweep_0_to_65535_1_sweep), .Freq(Freq), .Reset(Reset));  // open: click
  Multiplexer #(.enable("false"), .width(16)) multiplexer_1 (
    .in0(16'h2710), .in1(16'hd8f0), .out(AudioSignal), .sel(comparator_1_gt));
  Comparator #(.mode("unsigned"), .width(16)) comparator_1 (
    .a(sweep_0_to_65535_1_sweep), .b(DutyCycle), .gt(comparator_1_gt));  // open: eq, lt
  // Callout #(.background("#feffa189"), .dx(-55), .dy(3), .foreground("#cc45bf"), .halign("left"), .text("The trick I'm using here is to use a sawtooth to\nsweep through numbers 0 to 65535 at the desired\nfrequency. I then take that result and\ncompare it to a threshold.\nWhenever the sweep value is above the \nthreshold, the multiplexer picks -10000 to\nsend to the audio output. And when\nthe sweep value is below (or equal) to\nthe threshold, it picks +10000 to send to the output.\n\nUsing DutyCycle=0 results in a signal that's always\n(or very nearly always) -10000. Using DutyCycle=65535\nresults in a signal that's always (or very nearly) +10000.")) callout_1: pin names not known

  // Notes on the sheet:
  //   flexible square wave generator - When enabled, alternates between -10000 and +10000 (with
  //   no values between them), forever.
  //   You can choose any frequency from 1Hz to 4096Hz. And another input determines
  //   the "duty cycle" (from 0 to 65535), controlling how long the "up" part of the square wave lasts.
endmodule

module trianglewave (
  input  Enable,
  input  Reset,
  input  [11:0] Freq,
  output [15:0] AudioSignal
);

  wire scaledmath_1_p2;
  wire [15:0] scaledmath_1_p1;

  // ScaledMath #(.\function ("abs"), .mode("twosComplement"), .width(16)) scaledmath_1: pin names not known; wires that end beside it: scaledmath_1_p1, scaledmath_1_p2, scaledmath_1_p2
  sweep___32768__to___32767 sweep_32768_to_32767_1 (
    .Enable(Enable), .Sweep(scaledmath_1_p1), .Freq(Freq), .Reset(Reset));  // open: click
  // Callout #(.background("#feffa189"), .dx(-42), .dy(-49), .foreground("#cc45bf"), .halign("left"), .text("The trick I'm using here is to sweep through\nthe numbers -32768 to +32767 at the desired\nfrequency. I then take that result and run it \nthrough a function that produces a \"V\" shape\nfor each sweep. The division by 3 makes\nthe result values smaller, so the samples\nare closer to 10000 maximum, instead of\n32767 maximum.")) callout_1: pin names not known
  // SaturatingDivider #(.mode("twosComplement"), .width(16)) saturatingdivider_1: pin names not known; wires that end beside it: 16'h3, AudioSignal

  // Notes on the sheet:
  //   flexible triangle-wave generator - When enabled, produces a triangle shaped
  //   audio signal, varying from around -11000 up to about +11000.
  //   The frequency is determined by one of the inputs.
endmodule

module sinwave (
  input  Enable,
  input  Reset,
  input  [11:0] Freq,
  output [15:0] AudioSignal
);

  wire scaledmath_1_p2;
  wire [15:0] scaledmath_1_p1;

  // ScaledMath #(.mode("twosComplement"), .width(16)) scaledmath_1: pin names not known; wires that end beside it: scaledmath_1_p1, scaledmath_1_p2
  sweep___32768__to___32767 sweep_32768_to_32767_1 (
    .Enable(Enable), .Sweep(scaledmath_1_p1), .Freq(Freq), .Reset(Reset));  // open: click
  // Callout #(.background("#feffa189"), .dx(-42), .dy(-49), .foreground("#cc45bf"), .halign("left"), .text("The trick I'm using here is to sweep through\nthe numbers -32768 to +32767 at the desired\nfrequency. I then take that result and run it \nthrough a function that produces a sine-shape\nfor each sweep. The division by 3 makes\nthe result values smaller, so the samples\nare closer to 10000 maximum, instead of\n32767 maximum.")) callout_1: pin names not known
  // SaturatingDivider #(.mode("twosComplement"), .width(16)) saturatingdivider_1: pin names not known; wires that end beside it: scaledmath_1_p2, 16'h3, AudioSignal

  // Notes on the sheet:
  //   flexible sine-wave generator - When enabled, produces a sine-wave shaped
  //   audio signal, varying from around -11000 up to about +11000.
  //   The frequency is determined by one of the inputs.
endmodule

module white_noise (
  input  Enable,
  output [15:0] AudioSignal
);

  wire random_1_p2, random_1_p3;

  // RGBLED rgbled_1: pin names not known; wires that end beside it: Enable
  // Random #(.width(16)) random_1: pin names not known; wires that end beside it: Enable, random_1_p2, random_1_p3, random_1_p3, 16'h3
  Clock clock_1 (.out(random_1_p2));
  // SaturatingDivider #(.mode("twosComplement"), .width(16)) saturatingdivider_1: pin names not known; wires that end beside it: AudioSignal

  // Notes on the sheet:
  //   white noise generator - outputs random values in the range approx [-11000, +11000]
  //   whenever it is enabled.
endmodule

module sweep_0_to_65535 (
  input  Enable,
  input  Reset,
  input  [11:0] Freq,
  output click,
  output [15:0] Sweep
);

  wire clock_1_out;
  wire [31:0] adder_1_out, bit_extender_1_out, register_1_q, step;

  // Callout #(.background("#feffa189"), .dx(39), .dy(65), .foreground("#cc45bf"), .text("The heart of this circuit is a\n 32-bit value, with a feedback loop\nadding \"step\" during each clock tick.")) callout_1: pin names not known
  // RGBLED rgbled_1: pin names not known; wires that end beside it: Enable, Reset
  // Probe on Freq
  assign bit_extender_1_out = {{20{1'b0}}, Freq};  // Bit_Extender bit_extender_1
  Adder #(.width(32)) adder_1 (.a(register_1_q), .b(step), .out(adder_1_out), .cout(click));  // open: cin
  Clock clock_1 (.out(clock_1_out));
  Multiplier #(.width(32)) multiplier_1 (.a(bit_extender_1_out), .b(32'h41893), .out(step));  // open: cin, cout
  Register #(.width(32)) register_1 (.D(adder_1_out), .en(Enable), .Q(register_1_q), .clk(clock_1_out), .clr(Reset));
  // FitRange #(.typeOut("unsigned"), .widthIn(32), .widthOut(16)) fitrange_1: pin names not known; wires that end beside it: register_1_q, Sweep
  // Callout #(.background("#feffa189"), .dx(-27), .dy(-37), .foreground("#cc45bf"), .text("This \"requantizer\" divides by 2^16, so\nthe large counter values are scaled down\nbut exactly fill the output range [0, 65535]")) callout_2: pin names not known

  // Notes on the sheet:
  //   a flexible but LOUD and UNSIGNED sawtooth-like generator - When enabled, counts from 0
  //   up to 65535, then resets to 0, and counts up again, forever. It counts upwards at a speed
  //   determined by one of the inputs, you can choose any frequency from 1Hz to 4095Hz.
  //   This also outputs click=1 each time it wraps around.
  //   Q: Why is this using a 32-bit counter instead of 16 bits?
  //   A: Because it lets us adjust the step size more finely,
  //   more precisly controlling exactly how long it takes to
  //   reach the maximum and wrap around back to zero.
  //   With a 32-bit counter (0 to 4billion), we have a lot
  //   of possible step sizes to choose from to control how
  //   often the counter wraps around.
  //   The counter up above is 32-bits, going from about -2billion to 2 billion,
  //   before wrapping around to -2billion again. Each simulated clock tick we
  //   add some "step" to the counter, so if the simulation is running
  //   at 16kHz for audio output, we'd wrap around this often:
  //        F=(16000*stepsize)/4billion  wraparounds per second.
  //   In other words, that's the frequency of the sawtooth we
  //   generated.  Inversely, if we want a given frequency F,
  //   we can calculate the needed stepsize to get it:
  //     stepsize = F*4billion/16000
  //                    = F*268435.46
  //   Q: Why is the frequency limited a 4095hz? Can we go higher?
  //   A: The "Freq" input is a 12 bit number, which maxes out at 4095.
  //   It would be simple to allow higher numbers, by using more bits
  //   for "Freq". But with 16kHz PCM audio, we are limited to 8000hz
  //   maximum anyway, and sounds above 4000hz sound pretty high
  //   anyway.
endmodule

module sweep___32768__to___32767 (
  input  Enable,
  input  Reset,
  input  [11:0] Freq,
  output [15:0] Sweep,
  output click
);

  wire [15:0] fitrange_1_p1;

  // FitRange #(.widthIn(16), .widthOut(16)) fitrange_1: pin names not known; wires that end beside it: fitrange_1_p1, Sweep
  sweep_0_to_65535 sweep_0_to_65535_1 (
    .Enable(Enable), .Sweep(fitrange_1_p1), .Freq(Freq), .Reset(Reset), .click(click));
  // Callout #(.background("#feffa189"), .dx(-27), .dy(-37), .foreground("#cc45bf"), .text("This \"requantizer\" adjusts the range\nso it is signed (-32768 to +32768)\ninstead of unsigned (0 to 65535).")) callout_1: pin names not known

  // Notes on the sheet:
  //   a flexible but LOUD and SIGNED sawtooth generator - When enabled, counts from -32768
  //   up to +32767, then resets to -32768, and counts up again, forever. It counts upwards at a speed
  //   determined by one of the inputs, you can choose any frequency from 1Hz to 4095Hz.
endmodule

module sweep_0_to_65535_slowly (
  input  Enable,
  input  Reset,
  input  [11:0] Period,
  output click,
  output [15:0] Sweep
);

  wire clock_1_out;
  wire [31:0] adder_1_out, bit_extender_1_out, register_1_q, step;

  // Callout #(.background("#feffa189"), .dx(39), .dy(65), .foreground("#cc45bf"), .text("The heart of this circuit is a\n 32-bit value, with a feedback loop\nadding \"step\" during each clock tick.")) callout_1: pin names not known
  // RGBLED rgbled_1: pin names not known; wires that end beside it: Enable, Reset
  // Probe on Period
  assign bit_extender_1_out = {{20{1'b0}}, Period};  // Bit_Extender bit_extender_1
  Adder #(.width(32)) adder_1 (.a(register_1_q), .b(step), .out(adder_1_out), .cout(click));  // open: cin
  Clock clock_1 (.out(clock_1_out));
  Divider #(.mode("unsigned"), .width(32)) divider_1 (
    .a(32'h199999a), .b(bit_extender_1_out), .out(step));  // open: upper, rem
  Register #(.width(32)) register_1 (.D(adder_1_out), .en(Enable), .Q(register_1_q), .clk(clock_1_out), .clr(Reset));
  // FitRange #(.typeOut("unsigned"), .widthIn(32), .widthOut(16)) fitrange_1: pin names not known; wires that end beside it: register_1_q, Sweep
  // Callout #(.background("#feffa189"), .dx(-27), .dy(-37), .foreground("#cc45bf"), .text("This \"requantizer\" divides by 2^16, so\nthe large counter values are scaled down\nbut exactly fill the output range [0, 65535]")) callout_2: pin names not known

  // Notes on the sheet:
  //   a flexible but LOUD and UNSIGNED sawtooth generator - When enabled, counts from 0
  //   up to 65535, then resets to 0, and counts up again, forever. It counts upwards at a speed
  //   determined by one of the inputs, you can choose any period from 0.01 seconds to about 41 seconds.
  //   The period is specified in hundredths-of-a-second as a 12-bit number between 0 and 4095.
  //   This also outputs click=1 each time it wraps around. 
  //   Q: Why is this using a 32-bit counter instead of 16 bits?
  //   A: Because it lets us adjust the step size more finely,
  //   more precisly controlling exactly how long it takes to
  //   reach the maximum and wrap around back to zero.
  //   With a 32-bit counter (0 to 4billion), we have a lot
  //   of possible step sizes to choose from to control how
  //   often the counter wraps around.
  //   The counter up above is 32-bits, going from about -2billion to 2 billion,
  //   before wrapping around to -2billion again. Each simulated clock tick we
  //   add some "step" to the counter, so if the simulation is running
  //   at 16kHz for audio output, we'd wrap around in about:
  //        P=4billion/(16000*stepsize) seconds.
  //   or:
  //    P=4billion/(160*stepsize) hundredths of a second.
  //   In other words, that's the period of the sawtooth we
  //   generated.  Inversely, if we want a given period P,
  //   we can calculate the needed stepsize to get it:
  //     stepsize = 4billion/(160*P)
  //                    = 26843545.6/P
endmodule
module sweep___32768__to___32767__slowly (
  input  Enable,
  input  Reset,
  input  [11:0] Period,
  output [15:0] Sweep,
  output click
);

  wire [15:0] fitrange_1_p1;

  // FitRange #(.widthIn(16), .widthOut(16)) fitrange_1: pin names not known; wires that end beside it: fitrange_1_p1, Sweep
  sweep_0_to_65535_slowly sweep_0_to_65535_slowly_1 (
    .Enable(Enable), .Sweep(fitrange_1_p1), .Period(Period), .Reset(Reset), .click(click));
  // Callout #(.background("#feffa189"), .dx(-27), .dy(-37), .foreground("#cc45bf"), .text("This \"requantizer\" adjusts the range\nso it is signed (-32768 to +32768)\ninstead of unsigned (0 to 65535).")) callout_1: pin names not known

  // Notes on the sheet:
  //   a flexible but LOUD and SIGNED sawtooth generator - When enabled, counts from -32768
  //   up to +32767, then resets to -32768, and counts up again, forever. It counts upwards at a speed
  //   determined by one of the inputs, you can choose any frequency from 1Hz to 4095Hz.
endmodule

module lowpass_filter_onepole (
  input  [15:0] beta,
  input  [15:0] x,
  output [15:0] y
);

  wire clock_1_out, fitrange_1_p2, linearmap_1_p2, saturatingmultiplier_1_p3, saturatingsubtractor_1_p3;
  wire [31:0] saturatingadder_1_p3, y_n_1_q;

  // FitRange #(.normalization("center"), .typeIn("twosComplement"), .widthIn(16), .widthOut(32)) fitrange_1: pin names not known; wires that end beside it: x, fitrange_1_p2
  // Callout #(.dx(41), .dy(82), .foreground("#cc45bf"), .text("The alpha parameter is a 16-bit unsigned number,\nfrom 0 to 65535. We scale it up to\nbe within the range [0, 2billion].")) callout_1: pin names not known
  Register #(.width(32)) y_n_1 (.D(saturatingadder_1_p3), .Q(y_n_1_q), .clk(clock_1_out));  // open: en, clr
  Clock clock_1 (.out(clock_1_out));
  // LinearMap #(.domain("[0, 65535]"), .range("[0, 2147483647]"), .widthIn(16), .widthOut(32)) linearmap_1: pin names not known; wires that end beside it: beta, linearmap_1_p2
  // SaturatingSubtractor #(.mode("twosComplement"), .width(32)) saturatingsubtractor_1: pin names not known; wires that end beside it: fitrange_1_p2, y_n_1_q, saturatingsubtractor_1_p3
  // Callout #(.dx(-22), .dy(70), .foreground("#cc45bf"), .halign("left"), .text("This multiplication is configured as\n\"scale to range\" meaning you can\nthink of one of the inputs as being\na percentage. That is, alpha is 0-100%.")) callout_2: pin names not known
  // SaturatingMultiplier #(.mode("twosComplement"), .normalization("fit"), .width(32)) saturatingmultiplier_1: pin names not known; wires that end beside it: linearmap_1_p2, saturatingsubtractor_1_p3, saturatingmultiplier_1_p3
  // SaturatingAdder #(.mode("twosComplement"), .width(32)) saturatingadder_1: pin names not known; wires that end beside it: saturatingmultiplier_1_p3, y_n_1_q, saturatingadder_1_p3
  // FitRange #(.normalization("cap"), .typeIn("twosComplement"), .widthIn(32), .widthOut(16)) fitrange_2: pin names not known; wires that end beside it: saturatingadder_1_p3, y

  // Notes on the sheet:
  //   This is a low-pass filter, with a parameter beta to control where the dropoff is.
  //   The parameter beta is a 16-bit unsigned number, from 0 to 65535, but we
  //   treat it mathematically as if it were a percentage from 0% (0) to 100% (65535). 
  //   The filter equation works like this:
  //   x[1], x[2], ..., x[n-1], x[n] are the input samples, with x[n] being the most recent.
  //   y[1], y[2], ..., y[n-1], y[n] are the output samples, with y[n] being the most recent.
  //   To compute the output y[n] for the current step:
  //          y[n] = (y[n-1]) + beta * (x[n] - y[n-1])
  //                  = most_recent_output + beta * (how_badly_wrong_is_that_output)
  //   In other words, the output doesn't change when the input changes, exactly. Instead,
  //   the output now equals the previous output, plus a "little bit" depending on how far off
  //   the previous output was from the current input. And beta controls whether we mix in a tiny
  //   bit, a moderate amount, or a lot of the diference, to either quickly adatpt to changes, or slowly.
  //   This circuit uses some tricks:
  //    * the full range for the input signal is [-32768, +32767], same for the output.
  //    * but internally, we use 32-bit numbers to hold these values and do arithmetic. Those
  //       have a much larger range, [-2billion, +2billion].
  //    * for beta, we scale it up too, so it falls in the range [0, +2billion]. And, when multiplying
  //      by beta, we use a special multiplier that is configured to "scale to range", meaning
  //      it treats one of the two inputs as a fraction from 0.0 to 1.0, rather than an as integer.
  //   The reason for using 32-bit numbers is to avoid "overflow" cases. If we multiply 
  //   two large numbers during some intermediate calculation, the intermediate result
  //   might not fit in 16 bits, even if later we will divide or scale the result back down
  //   to a more reasonable number. By using 32-bit values for arithmetic, we have plenty
  //   of "headroom".  At the end of the calculations, we narrow back to 16 bits (any
  //   values outside the 16-bit range get "clipped" to the max or min at that point, but
  //   that probably won't happen unless the arithmetic goes haywire.)
  //   x[n]
  //   y[n]
endmodule

module highpass_filter_onepole (
  input  [15:0] x,
  input  [15:0] alpha,
  output [15:0] y
);

  wire clock_1_out, clock_2_out, linearmap_1_p2, saturatingadder_1_p3, saturatingadder_2_p3,
       saturatingdivider_1_p2, saturatingsubtractor_1_p3;
  wire [31:0] fitrange_1_p2, saturatingmultiplier_1_p2, saturatingsubtractor_1_p2, y_n_1_q;

  // FitRange #(.normalization("center"), .typeIn("twosComplement"), .widthIn(16), .widthOut(32)) fitrange_1: pin names not known; wires that end beside it: x, fitrange_1_p2
  // LinearMap #(.domain("[0, 65535]"), .range("[0, 2147483647]"), .widthIn(16), .widthOut(32)) linearmap_1: pin names not known; wires that end beside it: alpha, linearmap_1_p2
  Clock clock_1 (.out(clock_1_out));
  Clock clock_2 (.out(clock_2_out));
  // SaturatingSubtractor #(.mode("twosComplement"), .width(32)) saturatingsubtractor_1: pin names not known; wires that end beside it: fitrange_1_p2, saturatingsubtractor_1_p2, saturatingsubtractor_1_p3
  Register #(.width(32)) x_n_1 (.D(fitrange_1_p2), .Q(saturatingsubtractor_1_p2), .clk(clock_1_out));  // open: en, clr
  Register #(.width(32)) y_n_1 (.D(saturatingmultiplier_1_p2), .Q(y_n_1_q), .clk(clock_2_out));  // open: en, clr
  // SaturatingAdder #(.width(32)) saturatingadder_1: pin names not known; wires that end beside it: linearmap_1_p2, 32'h7fffffff, saturatingadder_1_p3, saturatingadder_1_p3
  // SaturatingDivider #(.width(32)) saturatingdivider_1: pin names not known; wires that end beside it: 32'h2, saturatingdivider_1_p2
  // Callout #(.dx(-38), .dy(-23), .foreground("#cc45bf"), .halign("left"), .text("This part is calculating (100%+alpha)/2\nwhere 100% is represented as 2billion.")) callout_1: pin names not known
  // SaturatingAdder #(.mode("twosComplement"), .width(32)) saturatingadder_2: pin names not known; wires that end beside it: saturatingsubtractor_1_p3, y_n_1_q, saturatingadder_2_p3, saturatingadder_2_p3
  // SaturatingMultiplier #(.mode("twosComplement"), .normalization("fit"), .width(32)) saturatingmultiplier_1: pin names not known; wires that end beside it: saturatingdivider_1_p2, saturatingmultiplier_1_p2
  // FitRange #(.normalization("cap"), .typeIn("twosComplement"), .widthIn(32), .widthOut(16)) fitrange_2: pin names not known; wires that end beside it: saturatingmultiplier_1_p2, y

  // Notes on the sheet:
  //   This is a high-pass filter, with a parameter beta to control where the dropoff is.
  //   The parameter beta is a 16-bit unsigned number, from 0 to 65535, but we
  //   treat it mathematically as if it were a percentage from 0% (0) to 100% (65535). 
  //   The filter equation looks similar to the low-pass one, but rearranged...
  //   To compute the output y[n] for the current step:
  //          y[n] = ( alpha * (y[n-1]) + alpha * (x[n] - x[n-1]) ) * lambda
  //   where lambda = (1+a)/(2a). To simplify the circuit, we rearrange this to:
  //          y[n] = (  y[n-1] + x[n] - x[n-1] ) * ( (1 + alpha) / 2 )
  //   x[n]
  //   y[n]
endmodule

module highpass_filter_onepole_alternate (
  input  [15:0] x,
  input  [15:0] alpha,
  output [15:0] y
);

  wire [15:0] lowpass_filter_onepole_1_y, saturatingsubtractor_1_p3;

  lowpass_filter_onepole lowpass_filter_onepole_1 (
    .beta(saturatingsubtractor_1_p3), .x(x), .y(lowpass_filter_onepole_1_y));
  // SaturatingSubtractor #(.width(16)) saturatingsubtractor_1: pin names not known; wires that end beside it: {16{1'b1}}, alpha, saturatingsubtractor_1_p3
  // SaturatingSubtractor #(.mode("twosComplement"), .width(16)) saturatingsubtractor_2: pin names not known; wires that end beside it: x, lowpass_filter_onepole_1_y, y

  // Notes on the sheet:
  //   This is a high-pass filter, with a parameter beta to control where the dropoff is.
  //   The parameter beta is a 16-bit unsigned number, from 0 to 65535, but we
  //   treat it mathematically as if it were a percentage from 0% (0) to 100% (65535). 
  //   The filter equation looks similar to the low-pass one, but rearranged. In fact,
  //   there is a trick allowing us to make a high-pass filter using our existing low-pass filter.
endmodule

module SVF_filter (
  input  [15:0] x,
  input  [15:0] f,
  input  [15:0] Q,
  output [15:0] hp,
  output [15:0] bp,
  output [15:0] lp
);

  wire clock_1_out, clock_2_out;
  wire [15:0] bp_q, fitrange_2_p2, fitrange_3_p2, lp_q;
  wire [31:0] adder_1_out, adder_2_out, bit_extender_1_out, bit_extender_2_out, divider_1_out, divider_2_out,
       divider_3_out, divider_4_out, fitrange_1_p2, fitrange_4_p2, fitrange_5_p2, multiplier_1_out,
       multiplier_2_out, multiplier_3_out, subtractor_1_out, subtractor_2_out;

  Multiplier #(.width(32)) multiplier_1 (
    .a(divider_3_out), .b(subtractor_2_out), .out(multiplier_1_out));  // open: cin, cout
  Multiplier #(.width(32)) multiplier_2 (
    .a(fitrange_4_p2), .b(divider_3_out), .out(multiplier_2_out));  // open: cin, cout
  Divider #(.width(32)) divider_1 (.a(multiplier_1_out), .b(32'hccd), .out(divider_1_out));  // open: upper, rem
  Divider #(.width(32)) divider_2 (.a(multiplier_2_out), .b(32'hccd), .out(divider_2_out));  // open: upper, rem
  assign bit_extender_1_out = {{16{1'b0}}, Q};  // Bit_Extender bit_extender_1
  // FitRange #(.normalization("center"), .typeIn("twosComplement"), .widthIn(16), .widthOut(32)) fitrange_1: pin names not known; wires that end beside it: x, fitrange_1_p2
  Adder #(.width(32)) adder_1 (.a(divider_1_out), .b(fitrange_4_p2), .out(adder_1_out));  // open: cin, cout
  // FitRange #(.normalization("cap"), .typeIn("twosComplement"), .widthIn(32), .widthOut(16)) fitrange_2: pin names not known; wires that end beside it: adder_1_out, fitrange_2_p2
  Adder #(.width(32)) adder_2 (.a(divider_2_out), .b(fitrange_5_p2), .out(adder_2_out));  // open: cin, cout
  // FitRange #(.normalization("cap"), .typeIn("twosComplement"), .widthIn(32), .widthOut(16)) fitrange_3: pin names not known; wires that end beside it: adder_2_out, fitrange_3_p2
  assign bit_extender_2_out = {{16{1'b0}}, f};  // Bit_Extender bit_extender_2
  Divider #(.width(32)) divider_3 (.a(bit_extender_2_out), .b(32'ha), .out(divider_3_out));  // open: upper, rem
  Subtractor #(.width(32)) subtractor_1 (
    .a(fitrange_1_p2), .b(fitrange_5_p2), .out(subtractor_1_out));  // open: bin, bout
  Register #(.width(16)) u_bp (.D(fitrange_2_p2), .Q(bp_q), .clk(clock_1_out));  // open: en, clr
  // FitRange #(.normalization("center"), .typeIn("twosComplement"), .widthIn(16), .widthOut(32)) fitrange_4: pin names not known; wires that end beside it: bp_q, fitrange_4_p2
  Clock clock_1 (.out(clock_1_out));
  Register #(.width(16)) u_lp (.D(fitrange_3_p2), .Q(lp_q), .clk(clock_2_out));  // open: en, clr
  // FitRange #(.normalization("center"), .typeIn("twosComplement"), .widthIn(16), .widthOut(32)) fitrange_5: pin names not known; wires that end beside it: lp_q, fitrange_5_p2
  Clock clock_2 (.out(clock_2_out));
  Subtractor #(.width(32)) subtractor_2 (
    .a(subtractor_1_out), .b(divider_4_out), .out(subtractor_2_out));  // open: bin, bout
  Multiplier #(.width(32)) multiplier_3 (.a(fitrange_4_p2), .b(32'h199a), .out(multiplier_3_out));  // open: cin, cout
  Divider #(.width(32)) divider_4 (
    .a(multiplier_3_out), .b(bit_extender_1_out), .out(divider_4_out));  // open: upper, rem
  // FitRange #(.normalization("center"), .typeIn("twosComplement"), .widthIn(32), .widthOut(16)) fitrange_6: pin names not known; wires that end beside it: subtractor_2_out, hp
  // FitRange #(.normalization("center"), .typeIn("twosComplement"), .widthIn(32), .widthOut(16)) fitrange_7: pin names not known; wires that end beside it: fitrange_4_p2, bp
  // FitRange #(.normalization("center"), .typeIn("twosComplement"), .widthIn(32), .widthOut(16)) fitrange_8: pin names not known; wires that end beside it: fitrange_5_p2, lp

  // Notes on the sheet:
  //   Resonant State-Variable Filter (SVF), with outputs for LP, BP, and HP.
  //   Params:
  //     f = 2 * sin(something) = between 0 and +2. We will use 16 bit unsigned, and map that full range to [0, +2]
  //     Q = 0.5... 10   so we will use 16 bit unsigned, and map that rull range to [0.5, 10]
  //   Formulas:
  //     hp = x - lp - (1/Q)*bp
  //     bp += f * hp
  //     lp += f * bp
endmodule

module click_track (
  input  Enable,
  input  [11:0] Period,
  output [15:0] count,
  output click
);

  wire clock_1_out;

  LED led_1 (.in(Enable));
  sweep___32768__to___32767__slowly sweep_32768_to_32767_slowly_1 (
    .Enable(Enable), .Period(Period), .click(click));  // open: Sweep, Reset
  Counter #(.max('hffff), .width(16)) count_number_of_clicks (
    .count(click), .Q(count), .clk(clock_1_out));  // open: load, D, carry, clr
  Clock clock_1 (.out(clock_1_out));

  // Notes on the sheet:
  //   click-track generator - This outputs a "0" normally, with regularly spaced short "1" pulses.
  //   The period (the amount of time between clicks, in hundredths of a second) is controlled by an input.
endmodule

module pulse_generator (
  input  Enable,
  input  [11:0] Period,
  input  [15:0] Duty,
  output [15:0] count,
  output [15:0] sweep,
  output pulse
);

  wire clock_1_out, clock_2_out, sweep_32768_to_32767_slowly_1_click;
  wire [15:0] duration_of_pulse_q;

  LED led_1 (.in(Enable));
  sweep___32768__to___32767__slowly sweep_32768_to_32767_slowly_1 (
    .Enable(Enable), .Period(Period), .click(sweep_32768_to_32767_slowly_1_click));  // open: Sweep, Reset
  Counter #(.max('hffff), .width(16)) count_number_of_pulses (
    .count(sweep_32768_to_32767_slowly_1_click), .Q(count), .clk(clock_1_out));  // open: load, D, carry, clr
  Clock clock_1 (.out(clock_1_out));
  Clock clock_2 (.out(clock_2_out));
  Counter #(.max('hffff), .ongoal("stay"), .width(16)) duration_of_pulse (
    .load(sweep_32768_to_32767_slowly_1_click), .Q(duration_of_pulse_q), .clk(clock_2_out));  // open: D, count, carry, clr
  // Callout #(.dx(-50), .dy(-93), .foreground("#cc45bf"), .halign("left"), .text("This counter keeps track of how\nlong the pulse has lasted so far.\nWe compare to how long the user\nwants the pulse to last, to see if\nthe pulse is still active, or has expired.")) callout_1: pin names not known
  Comparator #(.mode("unsigned"), .width(16)) comparator_1 (
    .a(duration_of_pulse_q), .b(Duty), .lt(pulse));  // open: gt, eq
  // Probe on sweep
  Multiplexer #(.enable("false"), .width(16)) multiplexer_1 (
    .in0(Duty), .in1(duration_of_pulse_q), .out(sweep), .sel(pulse));

  // Notes on the sheet:
  //   pulse generator - This outputs a "0" normally, with regularly spaced bursts of "1" ouputs.
  //   The period (the amount of time between clicks, in hundredths of a second) is controlled by an
  //   input, and the duration of the pulse is controlled by a second input. The duration
  //   is specified as a number from 0 to 65535, corresponding to a maximum of 4 seconds pulse.
  //   This also outputs the "sweep" number, counting from 0 up to Duty, during each pulse.
endmodule

module serial_test (
);

  wire fitrange_1_p2, saturatingmultiplier_1_p1, saturatingmultiplier_1_p5, serialin_1_p1, serialin_1_p2;
  wire [6:0] serialin_1_p4;
  wire [7:0] slider_1_out, slider_2_out, slider_3_out;

  // SerialIn #(.\clocking ("synchronous"), .format("")) serialin_1: pin names not known; wires that end beside it: serialin_1_p1, serialin_1_p2, serialin_1_p1, serialin_1_p4
  // Probe on serialin_1_p4
  Clock clock_1 (.out(serialin_1_p2));
  // Probe on slider_1_out
  Slider #(.mode("twosComplement")) slider_1 (.out(slider_1_out));
  TTY #(.asciiwidth(8)) tty_1 (.data(serialin_1_p4), .clk(serialin_1_p2), .we(serialin_1_p1));  // open: clr
  Slider slider_2 (.out(slider_2_out));
  Slider slider_3 (.out(slider_3_out));
  // Probe on saturatingmultiplier_1_p5
  // SaturatingMultiplier #(.normalization("center")) saturatingmultiplier_1: pin names not known; wires that end beside it: saturatingmultiplier_1_p1, slider_2_out, slider_3_out, saturatingmultiplier_1_p1, saturatingmultiplier_1_p5
  // Probe on fitrange_1_p2
  // FitRange #(.typeIn("twosComplement"), .typeOut("unsigned"), .widthOut(9)) fitrange_1: pin names not known; wires that end beside it: slider_1_out, fitrange_1_p2
endmodule

module squarewave_alternate (
  input  Enable,
  input  Reset,
  input  [11:0] Freq,
  input  [6:0] DutyCycle,
  output [15:0] AudioSignal
);

  wire comparator_1_gt, fitrange_1_p2, saturatingsubtractor_1_p3;
  wire [15:0] saturatingmultiplier_1_p1, sawtooth_1_audiosignal;

  // Callout #(.dx(131), .dy(-66), .foreground("#cc45bf"), .halign("left"), .text("This part of the circuit converts a number in\nthe range [0, 127] first to a 16 bit number, then\nsubtracts 64, then multiplies by 158, to get\na value in the range approx [-10000, +10000]")) callout_1: pin names not known
  sawtooth sawtooth_1 (.Enable(Enable), .AudioSignal(sawtooth_1_audiosignal), .Freq(Freq), .Reset(Reset));
  // FitRange #(.normalization("cap"), .widthIn(7), .widthOut(16)) fitrange_1: pin names not known; wires that end beside it: DutyCycle, fitrange_1_p2
  // SaturatingSubtractor #(.mode("twosComplement"), .width(16)) saturatingsubtractor_1: pin names not known; wires that end beside it: fitrange_1_p2, 16'h40, saturatingsubtractor_1_p3, saturatingsubtractor_1_p3, 16'h9e
  // SaturatingMultiplier #(.mode("twosComplement"), .width(16)) saturatingmultiplier_1: pin names not known; wires that end beside it: saturatingmultiplier_1_p1
  Multiplexer #(.enable("false"), .width(16)) multiplexer_1 (
    .in0(16'h2710), .in1(16'hd8f0), .out(AudioSignal), .sel(comparator_1_gt));
  Comparator #(.mode("unsigned"), .width(16)) comparator_1 (
    .a(sawtooth_1_audiosignal), .b(saturatingmultiplier_1_p1), .gt(comparator_1_gt));  // open: eq, lt
  // Callout #(.background("#feffa189"), .dx(-55), .dy(3), .foreground("#cc45bf"), .halign("left"), .text("The trick I'm using here is to use a sawtooth to\nsweep through numbers -10000 to +10000 at the desired\nfrequency. I then take that result and\ncompare it to a threshold.\nWhenever the sawtooth is above the \nthreshold, the multiplexer picks -10000 to\nsend to the audio output. And when\nthe sawtooth is below (or equal) to\nthe threshold, it picks +10000 to send to the output.\n\nUsing duty=0 gives a threshold of -10000\nusing a duty of 128 gives a threshold of +10000")) callout_2: pin names not known

  // Notes on the sheet:
  //   flexible square wave generator - When enabled, alternates between -10000 and +10000 (with
  //   no values between them), forever.
  //   You can choose any frequency from 1Hz to 4096Hz. And another input determines
  //   the "duty cycle" (from 0 to 127), controlling how long the "up" part of the square wave lasts.
endmodule

module finch_robot_bluetooth (
  input  Enable,
  output [15:0] aX,
  output [15:0] aY,
  output [15:0] aZ,
  output btnLogo,
  output btnA,
  output btnB,
  output [7:0] distance
);

  wire comparator_1_eq, comparator_2_eq, comparator_3_eq, connected;
  wire [7:0] Accel_X_p2, Accel_X_p3, Accel_Y_p2, Accel_Y_p3, Accel_Z_p2, Accel_Z_p3, Bluetooth_Connected_p2,
       Bluetooth_Connected_p3, Bluetooth_Connected_p4, Button_A_p2, Button_B_p2, Button_Logo_p2;

  // HttpIn #(.delay(5000), .format("%c%c%c"), .url("http://localhost:30061/hummingbird/in/orientation/Shake/A")) Bluetooth_Connected: pin names not known; wires that end beside it: Enable, Bluetooth_Connected_p2, Bluetooth_Connected_p3, Bluetooth_Connected_p4
  // HttpIn #(.delay(250), .format("%8d.%c"), .url("http://localhost:30061/hummingbird/in/Accelerometer/X/A/")) Accel_X: pin names not known; wires that end beside it: connected, Accel_X_p2, Accel_X_p3
  // HttpIn #(.delay(250), .format("%8d.%c"), .url("http://localhost:30061/hummingbird/in/Accelerometer/Y/A/")) Accel_Y: pin names not known; wires that end beside it: connected, Accel_Y_p2, Accel_Y_p3
  // HttpIn #(.delay(250), .format("%8d.%c"), .url("http://localhost:30061/hummingbird/in/Accelerometer/Z/A/")) Accel_Z: pin names not known; wires that end beside it: connected, Accel_Z_p2, Accel_Z_p3
  // HttpIn #(.delay(250), .format("%c"), .url("http://localhost:30061/hummingbird/in/button/LOGO/A/")) Button_Logo: pin names not known; wires that end beside it: connected, Button_Logo_p2
  // HttpIn #(.delay(250), .format("%c"), .url("http://localhost:30061/hummingbird/in/button/A/A/")) Button_A: pin names not known; wires that end beside it: connected, Button_A_p2
  // HttpIn #(.delay(250), .format("%c"), .url("http://localhost:30061/hummingbird/in/button/B/A/")) Button_B: pin names not known; wires that end beside it: connected, Button_B_p2
  // HttpIn #(.delay(250), .format("%8d"), .url("http://localhost:30061/hummingbird/in/Distance/static/A/")) Distance: pin names not known; wires that end beside it: connected, distance
  Comparator #(.width(24)) comparator_1 (
    .a({Bluetooth_Connected_p2, Bluetooth_Connected_p3, Bluetooth_Connected_p4}), .b(24'h746f4e),
    .eq(comparator_1_eq));  // open: gt, lt
  finch_parse_number finch_parse_number_1 (.FractionPart(Accel_X_p2), .IntegerPart(Accel_X_p3), .out_3(aX));
  finch_parse_number finch_parse_number_2 (.FractionPart(Accel_Y_p2), .IntegerPart(Accel_Y_p3), .out_3(aY));
  finch_parse_number finch_parse_number_3 (.FractionPart(Accel_Z_p2), .IntegerPart(Accel_Z_p3), .out_3(aZ));
  finch_parse_boolean finch_parse_boolean_1 (.Ascii(Button_Logo_p2), .out_2(btnLogo));
  finch_parse_boolean finch_parse_boolean_2 (.Ascii(Button_A_p2), .out_2(btnA));
  finch_parse_boolean finch_parse_boolean_3 (.Ascii(Button_B_p2), .out_2(btnB));
  Comparator comparator_2 (.a(8'h66), .b(Bluetooth_Connected_p4), .eq(comparator_2_eq));  // open: gt, lt
  Comparator comparator_3 (.a(8'h74), .b(Bluetooth_Connected_p4), .eq(comparator_3_eq));  // open: gt, lt
  or or_1 (connected, comparator_2_eq, comparator_3_eq);
  LED Finch__A__connected (.in(connected));
  LED Finch__A__not_connected (.in(comparator_1_eq));

  // Notes on the sheet:
  //   ("Not" in ascii)
endmodule

module finch_parse_number (
  input  [7:0] FractionPart,
  input  [7:0] IntegerPart,
  output [15:0] out_3
);

  wire comparator_1_gt, saturatingmultiplier_1_p3;
  wire [15:0] bit_extender_1_out, linearmap_1_p2, multiplexer_1_out, saturatingnegator_1_p2;

  // LinearMap #(.domain("[48, 57]"), .range("[0, 9]"), .widthOut(16)) linearmap_1: pin names not known; wires that end beside it: FractionPart, linearmap_1_p2
  assign bit_extender_1_out = {{8{IntegerPart[7]}}, IntegerPart};  // Bit_Extender bit_extender_1
  Multiplexer #(.enable("false"), .width(16)) multiplexer_1 (
    .in0(linearmap_1_p2), .in1(saturatingnegator_1_p2), .out(multiplexer_1_out), .sel(comparator_1_gt));
  // SaturatingNegator #(.mode("twosComplement"), .width(16)) saturatingnegator_1: pin names not known; wires that end beside it: linearmap_1_p2, saturatingnegator_1_p2
  Comparator #(.width(16)) comparator_1 (.a({16{1'b0}}), .b(bit_extender_1_out), .gt(comparator_1_gt));  // open: eq, lt
  // SaturatingMultiplier #(.mode("twosComplement"), .width(16)) saturatingmultiplier_1: pin names not known; wires that end beside it: bit_extender_1_out, 16'ha, saturatingmultiplier_1_p3
  // SaturatingAdder #(.mode("twosComplement"), .width(16)) saturatingadder_1: pin names not known; wires that end beside it: multiplexer_1_out, saturatingmultiplier_1_p3, out_3

  // Notes on the sheet:
  //   The "BlueBird Connector" program used to communicate with the Finch robots
  //   has an unfortunate output format for the HTTP API. For accerlations, it
  //   outputs a signed floating point number, with 1 or more decimal places.
  //   For a number like "9.81", we take the "9" as an integer, and multiply by 10.
  //   We take the "8" as an ascii character, and convert to an integer in range [0, 9],
  //   then add that to the previous result. We ignore anything after that first decimal place.
  //   We output the result as a signed 16 bit number, so 81 in this example.
  //   Note: if the integer part is negative, we need to negate the decimal part too!
endmodule

module finch_parse_boolean (
  input  [7:0] Ascii,
  output out_2
);

  Comparator comparator_1 (.a(8'h74), .b(Ascii), .eq(out_2));  // open: gt, lt

  // Notes on the sheet:
  //   The "BlueBird Connector" program used to communicate with the Finch robots
  //   has an unfortunate output format for the HTTP API. For booleans, it
  //   outputs "true" or "false". We just check for the presence of "t" as the
  //   first ascii byte.
endmodule

module volume_limiter (
  input  [15:0] AudioSample,
  input  [7:0] Volume,
  output [15:0] AdjustedSample
);

  wire fitrange_1_p2, fitrange_2_p1, linearmap_1_p2, saturatingmultiplier_1_p2, saturatingmultiplier_2_p2,
       scaledmath_1_p2;

  // FitRange #(.normalization("cap"), .typeIn("twosComplement"), .widthIn(16), .widthOut(32)) fitrange_1: pin names not known; wires that end beside it: AudioSample, fitrange_1_p2
  // LinearMap #(.domain("[-128, 127]"), .range("[95599345, 2147483647]"), .widthOut(31)) linearmap_1: pin names not known; wires that end beside it: Volume, linearmap_1_p2, linearmap_1_p2
  // ScaledMath #(.\function ("exp"), .width(31)) scaledmath_1: pin names not known; wires that end beside it: 32'h5, scaledmath_1_p2, scaledmath_1_p2
  // SaturatingMultiplier #(.mode("twosComplement"), .width(32)) saturatingmultiplier_1: pin names not known; wires that end beside it: fitrange_1_p2, saturatingmultiplier_1_p2, saturatingmultiplier_1_p2
  // FitRange #(.normalization("cap"), .widthIn(31), .widthOut(32)) fitrange_2: pin names not known; wires that end beside it: fitrange_2_p1
  // SaturatingMultiplier #(.mode("twosComplement"), .normalization("fit"), .width(32)) saturatingmultiplier_2: pin names not known; wires that end beside it: fitrange_2_p1, saturatingmultiplier_2_p2, saturatingmultiplier_2_p2
  // FitRange #(.normalization("cap"), .typeIn("twosComplement"), .widthIn(32), .widthOut(16)) fitrange_3: pin names not known; wires that end beside it: AdjustedSample
  // Callout #(.dx(-63), .dy(-55), .foreground("#ed2d23"), .text("All of the constants here\nwere chosen by trial-and-error\nto get a good range of boosting and damping.")) callout_1: pin names not known

  // Notes on the sheet:
  //   This circuit takes a 16-bit signed audio signal, and either 
  //   boosts the volume (up to about 5x louder) or limits the volume (up to 30x quieter).
  //   The amount is controlled by a signed 8-bit input in the range [-128, 127].
endmodule

module balancing_fader (
  input  [15:0] AudioSampleLeft,
  input  [15:0] AudioSampleRight,
  input  [7:0] Balance,
  output [15:0] CombinedSample
);

  wire linearmap_1_p2, saturatingmultiplier_1_p2, saturatingmultiplier_2_p2, saturatingsubtractor_1_p3;

  // LinearMap #(.domain("[-128, 127]"), .range("[0, 32767]"), .widthOut(16)) linearmap_1: pin names not known; wires that end beside it: Balance, linearmap_1_p2
  // SaturatingSubtractor #(.mode("twosComplement"), .width(16)) saturatingsubtractor_1: pin names not known; wires that end beside it: 16'h7fff, linearmap_1_p2, saturatingsubtractor_1_p3, AudioSampleRight, saturatingsubtractor_1_p3
  // SaturatingMultiplier #(.mode("twosComplement"), .normalization("fit"), .width(16)) saturatingmultiplier_1: pin names not known; wires that end beside it: AudioSampleLeft, saturatingmultiplier_1_p2
  // SaturatingMultiplier #(.mode("twosComplement"), .normalization("fit"), .width(16)) saturatingmultiplier_2: pin names not known; wires that end beside it: linearmap_1_p2, saturatingmultiplier_2_p2
  // SaturatingAdder #(.mode("twosComplement"), .width(16)) saturatingadder_1: pin names not known; wires that end beside it: saturatingmultiplier_1_p2, saturatingmultiplier_2_p2, CombinedSample

  // Notes on the sheet:
  //   This circuit takes two 16-bit signed audio signals, and mixes them into one
  //   by taking some of one, and some of the other. The "balance" is controlled
  //   by a user input, a signed 8-bit input in the range [-128, 127]. 
  //   -128 means "use only the left sample, ignore the right"
  //   0 means "use half of each sample"
  //   +127 means "use only the right sample, ignore the left"
endmodule

module filter_buildingblock (
  input  [15:0] X,
  input  [15:0] \β ,
  output [15:0] Z_1,
  output [15:0] Y
);

  wire clock_1_out;

  Clock clock_1 (.out(clock_1_out));
  Register #(.width(16)) register_1 (.D(X), .Q(Z_1), .clk(clock_1_out));  // open: en, clr
  // SaturatingMultiplier #(.mode("twosComplement"), .normalization("fit"), .width(16)) saturatingmultiplier_1: pin names not known; wires that end beside it: Z_1, \β , Y

  // Notes on the sheet:
  //   This circuit is useful for creating a variety of filters.
  //   It takes as inputs:
  //    * X, an audio sample, a signed 16-bit value typically in the range [-10000, +10000] or so.
  //    * β, a coefficient, a signed 16-bit value, within [-32768, 32767], but treated as a percentage [-100%, +100%]
  //   It outputs:
  //    * Z-1, which is the same as the audio sample X but delayed by one clock tick,
  //    * Y, computed from β times the delayed audio sample X.
endmodule

module recording_thank_you (
  input  Enable,
  input  Reset,
  output [15:0] AudioSignal
);

  wire clock_1_out, comparator_1_gt, fitrange_1_p1, or_1_out;
  wire [17:0] counter_1_q;

  // RGBLED rgbled_1: pin names not known; wires that end beside it: Enable, Reset
  Clock clock_1 (.out(clock_1_out));
  or or_1 (or_1_out, Reset, comparator_1_gt);
  Counter #(.max('h3ffff), .width(18)) counter_1 (
    .count(Enable), .Q(counter_1_q), .clk(clock_1_out), .clr(or_1_out));  // open: load, D, carry
  ROM #(.addrWidth(18), .proportions("tall")) rom_1 (.addr(counter_1_q));  // open: data
  Comparator #(.mode("unsigned"), .width(18)) comparator_1 (
    .a(counter_1_q), .b(18'h1a544), .gt(comparator_1_gt));  // open: eq, lt
  // FitRange #(.widthOut(16)) fitrange_1: pin names not known; wires that end beside it: fitrange_1_p1, fitrange_1_p1, AudioSignal
  // Callout #(.dx(-153), .dy(-30), .foreground("#bd48d1"), .text("The recording is 107844 bytes long,\nso we reset the counter whenever it\ngoes above that (OR, when the\nuser chooses Reset=1)")) callout_1: pin names not known

  // Notes on the sheet:
  //   A pre-recorded message, stored in a ROM (read-only-memory).
  //   The counter starts at 0, counting upwards, reading out 
  //   the values from the rom one byte at a time. Each byte
  //   is converted from 8-bit unsigned PCM (what the recording was)
  //   to 16-bit signed PCM (which we will use in our circuits).
  //   contents of rom_1 (hex, n*v repeats v):
  //   compressed eJyEXUm24zgO3PMUXv+VJorScTTe/wgtAgggKDurX7t/OW1ZA4gZQSAPn2n9THN9jcdny5/+06Vc
  //   PlP/yc+n+TPPn/n8lOkzdKnvPvq/Xv+flu4zXvKJv0v1u+X5/zx95r7+cO5Tv9ip63H6Knea/urb
  //   vr76/k8++0z230VOjvcfPXDWH6SCH/pfeVN/m3CO59/xU/lVnJqOrx/IxdP7TH4BupH4+PlXtsvR
  //   I+GO+mTfN9ejW/ST/LrBvvvjJ5PD0/p1bT/i103w531zC/751y0+SwIit989f+t37/M3n/v54+7S
  //   /Le8H9IeFfePRy68ZKldAfp6sYXye+NF1oXqXzduJ0r2a77oL157LZpczUmP2wEfLs06EUMmuzF8
  //   grsJWvnS8PX1GnwLfaxVcAUvO0kPk/N2Ci/+UUMnEpOg8p1aIjiF36tM9/eLk3F8/2nuIv5Nwvai
  //   G3/C959aRiUBqOfqx/Yp+w//qAdZZmaqxKfDKttBzXffyqB/aQJfQ18Reg77xcxLxEvYqiU9m996
  //   c21/ENxE74c3uqWVRxeAX88DFp/fFHIK9t+roRqOWYTY+msJwVqtRL/4+C3LYR/0S15gPNDEFHUx
  //   YT566SomEEgawvavNTdOAZO9nrYf/r5+8dbLveqvb01FDxgm7fu71zdYg5lvJyTqRcSvhXjf2/pm
  //   B9wNsYObZ1pH1UdB9841PvFTI68plphWTamTyv1eroX0H50yaEmr3L+fuSFOPDUtOknHa/2/6cEK
  //   sdHOL1mKN4kJxweAEP7B1JyQSUrKAawLNunzr1UjGSAr/EXTD3sBbxq9BHuUk12fcqRy4JMBwvr8
  //   c0r1k+mzLJ9lhsicIjWHvLnkSPyknPK5e0DP+0UO24kDBnlleZ/r+Z8D7LYnO1WQaqi3ZI9+yeeP
  //   T/tnl+3s47I9f5PeTj38sB/VE+ekj4gbr8/xHL+MyU6ZcfFBfqhX1jNscpJL/yZ7c+Bseq3Nnqz+
  //   c4JCUB0/2kWfz+tfexRagYHW5woLE+dXWzvh/KP8nfWYSol62k6uO4YqjgUfcBVd+REU6Ox5hd5w
  //   NIaPP4jTzT48cZJZOGIRdtjk7/qxf66pvt/pqyLHP+KQ5UJTJbU9+CT0Fy7Q5zKm6IVTnucdamhR
  //   Xxnv16RkqY+2fkoB18xCt+ew529vryeqyY+PdNcQ5QlU8vHJTxj0yMzwvEl5/8zjZ35imEWOX0mX
  //   Pjd2fNbus67yyp/1ed5b3sz180Xp/zzdATooZbI8+3NLV7Jnvz7r8FmX5wyfdXzOltYnAps+2/DZ
  //   us/Wy5vy2Za0LfK5voq8nuOvtD5neG5G/xZ5Pfp8TPVsY31fL9HJVZ5LDPU+6z0c8hQq1qvQ7XnY
  //   hxSrBHtjfep5eF7pIc5Dinx98vLJ42daarA47umJFMfyGa7PuH3GtR5ThfhK8y70XOr5n5t5rvXc
  //   xrPu9QaKEKcKuhx8VL6q95BreFljxU3izLo69TzPLZUZdDN9kCrlM8g+yKM9F9pSpWGx562vW/6u
  //   0HyTUHsHP4+VD4VQ8qsRryWtu3yyYjWLvHno2dk56xV7XOio91NfytKTUdX0hiq/Is+7iqI4RP8s
  //   9cP5kkeeKummPU3jQ9XPmD9TqRSeN/n5mOpC5Hp8JcJR+ep56od/6v3sYPWCaz1y8Szf8ZlL/VVd
  //   zV3++azLLddVKS5Gjfpcs7DfLA/VffCY8lybHNbLmWeRr40sgOqHWQ67k5FlBtF6+fxM9cNcX/WE
  //   GVqopEWfaMYZzmrf9nqmStdTdIbK+hocqoJeHyXL0yzyeRYOuuRxpyrEjwRPWTj0eT0n3upXlUhV
  //   yqvEF1GWi+oGFco5mRpTXXLJ8c/5u1RXaRGZmIRPlUNzEn6HlVrr2UTOkqwP1Nsub6r+S6r4Ky/M
  //   euewVe4Pj/Xgys6LcPQO7pvklfVVJbsuUfmE0X10T5dM8SiHjs6/ssL6E+fTSnvhxFO4ssjLOVTv
  //   cBSSHvXZH4rlkmqS6GHPUfJCU2Ux4e5UeW2px9v5V0iq2MzKmINQddQlSHWZiiiJXpbMDqic+1w6
  //   eOpQORbN0ctiKcuMykdJbU79lchHvflTLMmIYxbR0yblydm8nvmEUhySLZbKhKyj0bP/6KVNMvQ8
  //   YzLR32HTZr0rs7Qh60reU+hZ5PFVxR71wfOSplO06VTp+fx9lOu8ik+2iQ5e68H1uosI5ZHcqasn
  //   3MBCY5XsSs9JFLZm6iqphZ7lY/K6y6nEUpmUH2BOe4pk3pDzp7po4nuFN7aDtR5NuYInlURqYbLw
  //   v8rvJH8PoadangvE78HVE8m7ugaqFfqkLoY97CZv1KdU66GLrqZjFIv90LD7TIew6FT1aFWcSz3+
  //   eZNlFZ6nWLf61OYZCXHMg1M9s6R6wkMoiVUQzSP07IU4lSxQllcy72YzNWYPUkKuG597AH8Oxudm
  //   GOdkBk3F/+HbXazQQ+cJPsVufofyZ6WnvIyYqnplfettbBAiZdEhGQFPeOTqEa/JJCh/9AGr3eiE
  //   nlkU6Sn0fJRAL97TQ/9BFMImD3XX+3wEp8ypLsdMTqXokKo/i6mRMO9Vh6eqXkT/1NsTeay3Ogp9
  //   FtjwE56sRuAjlN5kLpWuo3lSPREki/48hYzKaUWoulU6MzEh48nej+ooyZv6VbI1XeDTOX8qcx7w
  //   /dWwT0kd0spF68e8p8e1nEXec33lHoSaqh7IIsvP2m1iV9WWPecxQ53Nk1VLXj2jS+xXJ/pZaFg/
  //   GcQyZ3BgB/ld4LkUxBm9PMUpFn6FJdeIaxV+vuVNlp+cwo0PDR89vKkrJGx21rtdb+NPNTrmzKrB
  //   eui2tRpYFe8My19g/NVMPHpyhSVahHlmNT2pOp4FTvpDwMddejiwq3xYn3EWz7Ra6nrOVe34JGym
  //   vpgwmEYMlVAZ2mMQhrzFrxjk1ZmbL1GIxKg7gr8dNOksIlG1pieXoC2Z2VLnGtqs8tX8cWe8EqeQ
  //   fd/kpW67/nOBHlCNOsDJ7eCRibiZER9Fri+KpS+hifpL+oCdSPQgSnITT7P+FY9IPKga9DyHif1a
  //   RUM+Xz3+ftHg76j8XxdFzlYy0gF7qidfhKSLfiLXncMvClO1U3ZqgtOiceGezOwy9eqTmr1Q1wXG
  //   Wuz4CHFehGKmKpNFY+4yjWFfTDOcGhOo1RM9M0OfZFDvSpqPMPnNYlgfHjtTVYZHNTFZtNbz4Oq5
  //   P9LtsXIV9ltMxi56I9flqN7RIKxVHTzRt0rM0YL4KvWT8OGETMClzqd8fkSiyOLsSejj8juRwnyu
  //   u5slcjoIBZI55iuYcAPdjPHkQ3c13Y5cHzc0wnvJZLaAeiNlq9Uf64R06ubl9JDr8W3q6zBl9XDX
  //   dFe6IcoR0b7rq9prpZs67RLcyEqJ/RqsEGk6XzMrE44R1qprdwsfbhZt1EscZv0r3XZRCEp5C5dF
  //   Hy5GRguJRrVKIo/KZhlG9vnnKXRzF33Bt9n8K9OH6rgeEokqnyvdCvI6g6XXzXx0ouSfv5vYza7K
  //   bJYQsMpaDcRrZfYhoPg2QuRB/qn6UDwlY91dBRP8fH1UYUr4JX7mDnWXYWQL6DYgPXAgUp+T3Xxv
  //   Oaf6z1v0Q7Hw2mLxEZHxDWcmQ/uNkFP/cEK8OKfGfA+WKjB+PvU9rPBMEaTrmdX84erDbHCJZ3nz
  //   vOYk+Qx5rfDuhkq3Slsl2i5vNuGfSeJKTTKNSFAiR2xx34h4xHOpvSfSILMaB82f+Kt674CcHjAl
  //   9uzJ3OkR3qC+5mSOt8eDZlPgB8KlMbO7JbNBHqGo4p2SOU6UxqtsM4v+0cSYkkJFeEn2fgHdFqVe
  //   sjfq1+3wRu5kCbbRjLiFlkeUeDyTanZzeH2ir2RquZCxWCG/B1STBWuf/LfWTDycNliLXt3lZNr/
  //   pBhVY/IFF5hpkeYULmYfCViL5Q6w2gz+eGSss8RE+GQ1ikizqrzjY29Oo1HlsA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
endmodule

module recording_canning_ramps (
  input  Enable,
  input  Reset,
  output [15:0] AudioSignal
);

  wire clock_1_out, comparator_1_gt, or_1_out;
  wire [19:0] counter_1_q;

  // RGBLED rgbled_1: pin names not known; wires that end beside it: Enable, Reset
  Clock clock_1 (.out(clock_1_out));
  or or_1 (or_1_out, Reset, comparator_1_gt);
  Counter #(.max('hfffff), .width(20)) counter_1 (
    .count(Enable), .Q(counter_1_q), .clk(clock_1_out), .clr(or_1_out));  // open: load, D, carry
  ROM #(.addrWidth(20), .dataWidth(16), .proportions("tall")) rom_1 (.addr(counter_1_q));  // open: data
  Comparator #(.mode("unsigned"), .width(20)) comparator_1 (
    .a(counter_1_q), .b(20'h8982d), .gt(comparator_1_gt));  // open: eq, lt
  // Callout #(.dx(-153), .dy(-30), .foreground("#bd48d1"), .text("The recording is 563245 samples long,\nso we reset the counter whenever it\ngoes above that (OR, when the\nuser chooses Reset=1)")) callout_1: pin names not known; wires that end beside it: AudioSignal

  // Notes on the sheet:
  //   A pre-recorded message, stored in a ROM (read-only-memory).
  //   The counter starts at 0, counting upwards, reading out 
  //   the values from the rom 16-bits at a time. The recording
  //   is already in 16-bit signed PCM format at 16kHz audio rate.
  //   contents of rom_1 (hex, n*v repeats v):
  //   compressed eJxEnemZ5SizhP/LimOCQCCQOWLz34SJN1D1PPd+Nd1dZxGQ5BoZmZ4cf+lO9+869acQfink8ks5
  //   37973PcvniUd4fydv6D/u2blj2Wc+s+h15+/O9xJP0rSJ8TJJ8RXb7vTcd3zd9WlT9z/i+vRB9ff
  //   lfSaGY7rKb8r6H3Xq38rv6iniFFfU8pvnUeYSd8e9Ef9y/MLtf9COn9j6SmOtfQEd/ul9Vtzpd9a
  //   M+uHXrPWpffdx6O3vM8v5lPrK79x86umj6t1/GLNx2rl1ifP35P8fv2+6HvWM9tv9UevfMp5XGn8
  //   qt4U7996tbA1g55unEO/zuv33FHP0vQU73X+Ytf7S9KPoS8J49XGXPrsdR1rNN7X9FlF+xLm9ctF
  //   K+MtWr8+8T3irTVcz/jlc+qdUR+a9Rgr6k1pnHpnqPqgR38djxY59Dht6btTazoKfUrOfHcbx2x6
  //   d9HWXdfFs+m7e9F5ZW0Zi5zhOmrX10X2iEN69LrnvX6TlZZZf6Xce4/W+0tdH97vR8+sl3X9Nk7t
  //   76mDeHSqPejXt97MS9a92u/Wl63V9Wy9hcObX/Qk92Crn5NT0rPpO0vWTraej9b0NFUiULSGK3HY
  //   xVtUJTprhHK84/rprTHre4reVZdk5cqsr5ZfS+OIb/ndV/w9esD8ex++TKdRJMe5tSMN/So0Pk2f
  //   xFZ1yVeOugFvZlnvcUs2vWi+4PX/t/fU17I7tRzpqtoMDkAvzJKNFAZfIiluukNBYjX6/L3I0JBY
  //   tNT0r9r4Sy+/9CjPPC7dkf72X5HIxvjoafvvlhQiymMehaObof4CO9KHhGWx1xzE+fzaWMcqj04s
  //   /YIkaZU6f1l3dt1Rn6frsWrQyT26wToBbXzVUUlO9NDz1Y3UX5JkLE19Tn51klFrq3rW0BMX2h8Y
  //   5703fXXJThx6ksmVmJeWO5DT2R5EU2fRpB8u9mn+0uBcUtUp8LiStjBP3vAea94cu9YeKht7Lm7h
  //   /pdVH21HQ5oSnz941t64sPqSqq+7Op/CiY3CFci/OVko16MhkpIAfWb7xaBX9qC1+QwkAS/CubQ2
  //   qZv16PmRmNV0b+cMW2dE/tC0mSlF7m7+3TxHe8px61glJtpiXbuIzDxSQr3os4t2pcR8BN2j0LS4
  //   mVF0l24ZR/lIrCSBTzokgoE73KUpr4W8lPCT7Eeu5QonykGrmdJnPOvQESW+tkmpxsIdutZ+2ivd
  //   Wylw4/mWrr1e2g92Zxyc8Xolccknrm/jCrRbXyXFU+vJp+QfOn/Nqo+7w0+CGHXl5ysZfY9L8hg6
  //   e/nqOafWfUmctW26rVKVa5TOIV2/S0dXzvKb7FNAHvQJN8JXhlT3Qs1JpHSNAnKzJP/xYXE1ITs6
  //   alRsQnMilVHfGSe/kgRWvujtx9X8zv5riOWr1146nxS1922WX0/hQEYlyoiKHjjya2tcXYWKXMw8
  //   jyxRSzVuUasnAqhLrD9futn3Ow59f2GlgX3X13P3R0KBvL+3HkGa+5YCjCifqFVKPrBGSXc0d5kI
  //   6bo76u8yfw/KdenheNKq7Q1hHreMZpFSjJZ5fYkPWEKmp0yzH5FdunRs2vxLa9HbrhV1Zr/6yLro
  //   KWJEUrAuuv6/zE16E4suGQ2vbWDHJ/ZXWnM1nW28y3f/h+TqjrqBz6WNLsjIKfWq6xAeTAG7NyMi
  //   cY4D5SM7KMONnOpW6RSvk4/SAkKuR4xIem3aMo5LN0J3Pkqz4gLcSeIx9WRJNi3c6DvpJl4nrRwG
  //   V3P0I5WOquPa6lIFbMKQGeBY9a3jxKjo7bIBXq5OE83zoFJlqcLUI7asRS8U8auD0ssQGV47eO2b
  //   rDb0/veWKuxcvjb4ReC7TsSU9z7SCu/CbOp+9cXjbXlmW5DWl+s1bt6kvz5bueuicpl12cKLally
  //   W7BXuev01nFrl4PMROFEFyarSLdhT9OvvOuI+f0VaalHu5zC1t35xgrLuYmH/ZhhE8DSkcX+4lbc
  //   EY9kYi219jJRuTlj/NHoPFLhkSPeTDmxw7wuoA8zO5NRlmHpKOupF+fJj+Jd0KEV3YXV2ruFR6pK
  //   4orSnTKpWZfieueRonwh6aOnXroXMlraw6m9eiQj/byOV6f53O+Pw+w4VhKCInksEiO5NEeSidM9
  //   R1U31MvAwL0ZRY6xKk0bfCMtF4os8NAXoh44hZObxY/ZezrmlK6fM+l5T3mCC9dzdq1mSmj1QxZ/
  //   XVmS5I+6uAY3DtLDL6q+3LpmoV/mfdzaFZzEEiUPUsFNEjIQwaDrLsdKOt7GUfKvY9a9DAk/NVV+
  //   6PoE1H84V9fr9Nsm5TzPKLeo/F78BJ10lNELVarR6gk13jD4L/5VfvUc8qN5UP02TWnHEzfz0gdJ
  //   +KWdp1S8NCzeMA5d1KdOndmxIrcHB25FxDRhSJA8XSFcVLmg1oGLbQmSxCzlekvfd84JO9558ls2
  //   PGkfQ365eFKW4dUhh6qnCFWWLPC0Qa7ZEW7p1fBKNYec2AlterjkisoJOHUGUpnyzx/JYyYOGM3u
  //   bcemdG7fg4eVtRPyQvTUp/zzFbvWfupp5socsLTdfCQXc0iEdcr6t0c3anY9xETi5vvqo8Jz8w5k
  //   RdKnzcOTwEFJeKkV73PgIeHlJVn9cD5Hkr17dRM7NwRf8ObxdY9C1OOH2nSGWSY0FDl2oUWcLPy3
  //   B5V5o2BvvTtc6TpClJ4Ppy7CRFVr5x7JDX6CXfas0xkR/0u6fN3cNLvnQTu+16RQQWtq7zG7rOJ8
  //   WWKWNp2vVMm8dULzTdoFjMus18PrtEcFCWcvZ9O+aY8IDwq+fPetl4P0PHyvFE2QbxkJ6HRdUKrS
  //   h78RkGf5WCE8LEqmLxRtW7gR+VfXTh4a65aVDk1SFepE7veudEzaIkxi738o4rZwu1+HaSk7ekJr
  //   FUIorJS2hIvNRZRaWcQ+uskdqdZWDL14Tpm+WV+pv0cO42zSAlLAWmyTkMxXX6TtYcsqlz1wQbBD
  //   UaK5Lv702LtDhePcS+blOsV1PDJUCHGXlRja34D5ktuMlMuJDIpxD+2C/o33Sqwlxx2zXTs/CJmq
  //   9JVsG3KBqGOupBLeH2fxaBeKdiNhsmX5cKV7xElE2dwcdySGIHBdgcOb6Tzk8GjzHo6R0GQWfauO
  //   W0ojL4578G+3JL/qlunf9LZHAedsC8nBeTtPPsqqbcgJKjjS3W6TxKJjV+RxyMvpcsOnwsFwclUj
  //   +qqcnHRiYSz25Wibjio8vK52ZP3Bh71RB9k6QceNEpKb1+SWlUXwcX9uAca0Edsi/DI8KLCi8z5P
  //   NJY+Xd+PmyjHYjapmHlzwLf8x5nlhM/Cn4q0q7aBH7Kes6LIZeb0J1TBmDIMgdAi6qR0lZCpF5tu
  //   d1mLv2T/b7liVXq4yzvFjOuUdXAEItr4gAbTWnqW7ONSSv7lz4eAPyElGewSDXINnasgr+IILzqj
  //   4iddD8agYBW6YjdFa7LLqd9HTAgbO98RxffF2pImuIhPThwP6Y9Dy9dlbvLgJdX6UaVcZtEnT4Ll
  //   yVfOmpskQ3LD2XPfudts7GldR9B0NZSbzT8udyPIkoX+ZVmzW95VlbQ3PJSlo0yKD7R8Micvoo07
  //   /shnC4Ow7JWhCK1K+t8TdzazYcVHrhdfjjoyvgFhtAykHGt5JqHbEyM+QKHfqJmb5Z6lHHMpnplN
  //   akLHph9E5TOj2aKM4cQ5H7PWYyypGAnTpb9K8KaeVOayawtORVSTYEzXV5tWdbOkD/hQLXBOlnsS
  //   T6ZOmMkWyN3TtdPTXvKlb0y4btDAiJ0KfUIkcRQlPiHL5wm8T6oOX81LlYSFyz9Qa7HoACI36cKG yc2RYOnrQiM2OrnZ+jLObxX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
endmodule

module attempted_reverb (
);

  wire clock_3_out, scope_1_p2, shift_register_1_p2;
  wire [7:0] Reverb_Control_p1, Volume_Control_p1;
  wire [15:0] balancing_fader_1_combinedsample, recording_thank_you_1_audiosignal, saturatingadder_1_p3,
       shift_register_1_p3, volume_limiter_1_adjustedsample;

  recording_thank_you recording_thank_you_1 (.AudioSignal(recording_thank_you_1_audiosignal));  // open: Reset, Enable
  // Dial #(.mode("twosComplement")) Reverb_Control: pin names not known; wires that end beside it: Reverb_Control_p1
  balancing_fader balancing_fader_1 (
    .AudioSampleLeft(recording_thank_you_1_audiosignal), .Balance(Reverb_Control_p1),
    .CombinedSample(balancing_fader_1_combinedsample), .AudioSampleRight(shift_register_1_p3));
  // Shift_Register #(.width(16)) shift_register_1: pin names not known; wires that end beside it: balancing_fader_1_combinedsample, shift_register_1_p2, shift_register_1_p3
  Clock clock_1 (.out(shift_register_1_p2));
  // SaturatingAdder #(.mode("twosComplement"), .width(16)) saturatingadder_1: pin names not known; wires that end beside it: recording_thank_you_1_audiosignal, shift_register_1_p3, saturatingadder_1_p3
  // Scope #(.mode("twosComplement"), .samples(320), .scopeheight(100), .scopewidth(240), .width(16)) scope_1: pin names not known; wires that end beside it: saturatingadder_1_p3, scope_1_p2
  Clock clock_2 (.out(scope_1_p2));
  volume_limiter volume_limiter_1 (
    .AudioSample(saturatingadder_1_p3), .Volume(Volume_Control_p1),
    .AdjustedSample(volume_limiter_1_adjustedsample));
  // Dial #(.mode("twosComplement")) Volume_Control: pin names not known; wires that end beside it: Volume_Control_p1
  Clock clock_3 (.out(clock_3_out));
  // PCMSink #(.mode("twosComplement"), .rate("16 kHz"), .width(16)) pcmsink_1: pin names not known; wires that end beside it: volume_limiter_1_adjustedsample, clock_3_out
endmodule

module diy_wave_generator (
  input  [31:0] in_1,
  input  [31:0] in_2,
  input  [31:0] in_3
);

  wire clock_1_out, clock_2_out, clock_3_out, fitrange_1_p1, fitrange_1_p2, linearmap_1_p3, pcmsink_1_p2,
       scope_1_p2, This_one_is_a_SLOW_clock__one_tick_per_second_out;
  wire [7:0] random_q, Slider__0_255_out, Volume_Control_p1;
  wire [15:0] fitrange_1_p4, volume_limiter_1_adjustedsample;

  Clock #(.lowDuration(15999)) This_one_is_a_SLOW_clock__one_tick_per_second (.out(This_one_is_a_SLOW_clock__one_tick_per_second_out));
  Clock #(.lowDuration(7999)) This_one_is_a_slow_clock__one_tick_per_half_second ();  // open: out
  Register random (.Q(random_q));  // open: D, en, clk, clr
  Clock clock_1 (.out(clock_1_out));
  Register #(.width(32)) B ();  // open: D, en, Q, clk, clr
  // SaturatingAdder #(.mode("twosComplement"), .width(32)) saturatingadder_1: pin names not known; wires that end beside it: This_one_is_a_SLOW_clock__one_tick_per_second_out
  // LinearMap #(.domain("[0, 255]"), .range("[-20, 20]"), .widthOut(32)) linearmap_1: pin names not known; wires that end beside it: random_q, clock_1_out, linearmap_1_p3, linearmap_1_p3
  Clock clock_2 (.out(clock_2_out));
  // SaturatingAdder #(.mode("twosComplement"), .width(32)) saturatingadder_2: pin names not known; wires that end beside it: clock_2_out
  Slider Slider__0_255 (.out(Slider__0_255_out));
  // FitRange #(.normalization("cap"), .typeIn("twosComplement"), .widthIn(32), .widthOut(16)) fitrange_1: pin names not known; wires that end beside it: fitrange_1_p1, fitrange_1_p2, fitrange_1_p2, fitrange_1_p4
  Register #(.\initial ('h2710), .width(32)) A ();  // open: D, en, Q, clk, clr
  Clock clock_3 (.out(clock_3_out));
  // SaturatingMultiplier #(.mode("twosComplement"), .width(32)) saturatingmultiplier_1: pin names not known
  // LinearMap #(.domain("[0, 255]"), .range("[-5000, 5000]"), .widthOut(32)) linearmap_2: pin names not known; wires that end beside it: Slider__0_255_out
  // Callout #(.dx(-66), .dy(-133), .foreground("#f56224"), .text("This converts an 8-bit number\nwithin [0, 255] so it\nfalls between -5000 and 5000\nas a 32-bit number.")) callout_1: pin names not known
  // Scope #(.mode("twosComplement"), .samples(320), .scopeheight(100), .scopewidth(240), .width(16)) scope_1: pin names not known; wires that end beside it: fitrange_1_p4, scope_1_p2
  Clock clock_4 (.out(scope_1_p2));
  volume_limiter volume_limiter_1 (
    .AudioSample(fitrange_1_p4), .Volume(Volume_Control_p1), .AdjustedSample(volume_limiter_1_adjustedsample));
  // Dial #(.mode("twosComplement")) Volume_Control: pin names not known; wires that end beside it: Volume_Control_p1
  // Callout #(.dx(-20), .dy(22), .foreground("#f56224"), .text("Constants.")) callout_2: pin names not known; wires that end beside it: clock_3_out, 32'hfffffffc, 32'h205
  // SaturatingDivider #(.mode("twosComplement"), .width(32)) saturatingdivider_1: pin names not known
  // SaturatingMultiplier #(.mode("twosComplement"), .width(32)) saturatingmultiplier_2: pin names not known
  // Dial Dial__0_255: pin names not known
  // PCMSink #(.mode("twosComplement"), .rate("16 kHz"), .width(16)) pcmsink_1: pin names not known; wires that end beside it: volume_limiter_1_adjustedsample, pcmsink_1_p2
  Clock clock_5 (.out(pcmsink_1_p2));
  // SaturatingDivider #(.mode("twosComplement"), .width(32)) saturatingdivider_2: pin names not known
  // Dial Dial__0_255_2: pin names not known
  Slider Slider__0_255_2 ();  // open: out
  Slider #(.mode("twosComplement"), .width(32)) Slider___2billion__to__2billion ();  // open: out
  // Callout #(.dx(-20), .dy(22), .foreground("#f56224"), .text("Input, 32-bit binary")) callout_3: pin names not known; wires that end beside it: in_1
  // Dial #(.mode("twosComplement"), .width(32)) Dial___2billion__to__2billion: pin names not known
  // Callout #(.dx(-20), .dy(22), .foreground("#f56224"), .text("Input, Signed Decimal (32 bit)")) callout_4: pin names not known; wires that end beside it: in_2, in_3

  // Notes on the sheet:
  //   Your circuit goes here...
  //   Do some arithmetic and feedback loops with 32 bit numbers.
  //   These have a big range (-2 billion to +2 billion).
  //   But aim to have numbers varying between about -10000 and +10000,
  //   and try to make them oscillate rapidly (anywhere from a few times 
  //   per second, to a few hundred times per second).
  //   The clock will tick 16000 times per second.
  //   (2) Generate new
  //   values, by feeding
  //   the old values into
  //   some equation. You can
  //   encorporate random
  //   numbers too, or 
  //   also include user-input
  //   as part of the equation.
  //   (optional) Use some user
  //   input (dial, slider, input)
  //   to affect the calculation
  //   in some way.
  //   (1) Put a register
  //   in the middle, to
  //   keep track of 
  //   the current number.
  //   Or use a few
  //   registers, each
  //   serving as a variable. 
  //   (3) Send one
  //   of the values
  //   to the audio output.
  //   Or use a combination
  //   of several values.
endmodule

module diy_waves (
  input  [11:0] Binary_Freq_Input,
  input  [11:0] Decimal_Freq_Input
);

  wire callout_1_p1, callout_1_p3, callout_3_p1, callout_4_p1, callout_4_p2, callout_4_p3, callout_4_p4,
       callout_6_p1, callout_6_p2, clock_1_out, linearmap_1_p2, pcmsink_1_p2, scope_1_p2;
  wire [7:0] Volume_Control_p1;
  wire [11:0] random_q;
  wire [15:0] pcmsink_1_p1, scope_1_p1;

  Clock #(.lowDuration(15999)) clock_1 (.out(clock_1_out));
  // Callout #(.dx(-7), .dy(46), .foreground("#e02f89"), .text("These ones\nhave a fixed\nfrequency")) callout_1: pin names not known; wires that end beside it: callout_1_p1, callout_1_p1, callout_1_p3, callout_1_p3
  sawtooth_80hz sawtooth_80hz_1 ();  // open: Enable, AudioSignal, Reset
  triangle_160hz triangle_160hz_1 ();  // open: Enable, AudioSample, Reset
  // Callout #(.dx(-10), .dy(47), .foreground("#e02f89"), .text("Pick a random number\nbetween 60 and 440,\nonce each second.")) callout_2: pin names not known
  Register #(.width(12)) random (.Q(random_q), .clk(clock_1_out));  // open: D, en, clr
  // LinearMap #(.domain("[0, 4095]"), .range("[60, 440]"), .widthIn(12), .widthOut(12)) linearmap_1: pin names not known; wires that end beside it: random_q, linearmap_1_p2, linearmap_1_p2
  sinwave sinwave_1 (.Freq(12'h1b8));  // open: Enable, AudioSignal, Reset
  sawtooth sawtooth_1 ();  // open: Enable, AudioSignal, Freq, Reset
  // Callout #(.dx(-13), .dy(17), .foreground("#e02f89"), .text("For these, you can pick any frequency between [0, 4095].")) callout_3: pin names not known; wires that end beside it: callout_3_p1, callout_3_p1
  white_noise white_noise_1 ();  // open: Enable, AudioSignal
  squarewave squarewave_1 (.DutyCycle(16'h7fff));  // open: AudioSignal, Enable, Freq, Reset
  click_track click_track_1 (.Period(12'h96));  // open: click, Enable, count
  // Callout #(.dx(-23), .dy(37), .foreground("#e02f89"), .text("Click generators: these output a single \"1\" every so often\n(you choose how often)")) callout_4: pin names not known; wires that end beside it: callout_4_p1, callout_4_p2, callout_4_p3, callout_4_p4
  Clock #(.lowDuration(15999)) _1_click_per_second (.out(callout_4_p1));
  Clock #(.lowDuration(7999)) _1_click_per_half_second (.out(callout_4_p2));
  trianglewave trianglewave_1 ();  // open: Enable, AudioSignal, Freq, Reset
  Clock #(.lowDuration(3999)) _1_click_per_quarter_second (.out(callout_4_p3));
  Clock #(.lowDuration(31999)) _1_click_per_2_seconds (.out(callout_4_p4));
  // Scope #(.mode("twosComplement"), .samples(320), .scopeheight(100), .scopewidth(240), .width(16)) scope_1: pin names not known; wires that end beside it: scope_1_p1, scope_1_p2
  Slider #(.width(12)) Freq_Slider ();  // open: out
  Clock clock_2 (.out(scope_1_p2));
  // PCMSink #(.mode("twosComplement"), .rate("16 kHz"), .width(16)) pcmsink_1: pin names not known; wires that end beside it: pcmsink_1_p1, pcmsink_1_p2
  volume_limiter volume_limiter_1 (.AudioSample(scope_1_p1), .Volume(Volume_Control_p1), .AdjustedSample(pcmsink_1_p1));
  // Dial #(.mode("twosComplement")) Volume_Control: pin names not known; wires that end beside it: Volume_Control_p1
  Clock clock_3 (.out(pcmsink_1_p2));
  // Callout #(.dx(-11), .dy(31), .foreground("#e02f89"), .text("For choice of frequency, you can use a constant of your choice,\nor a slider, dial, or number input.")) callout_5: pin names not known
  // Dial #(.width(12)) Freq_Dial: pin names not known; wires that end beside it: 12'h1b8, 12'hdc, 12'h6e, 12'h14f, 12'h11d, 12'h3c, Binary_Freq_Input
  pulse_generator pulse_generator_1 (.Period(12'h96), .Duty(16'h1f40));  // open: pulse, Enable, count, sweep
  // Callout #(.dx(-23), .dy(37), .foreground("#e02f89"), .text("Pulse generators: these turn ON for a while, every so often\n(you choose how often, and how long they stay ON)")) callout_6: pin names not known; wires that end beside it: callout_6_p1, callout_6_p2, Decimal_Freq_Input
  Clock #(.highDuration(1000), .lowDuration(7000)) sixteenth_second_pulse_each_half_second (.out(callout_6_p1));
  Clock #(.highDuration(8000), .lowDuration(16000)) half_second_pulse__then_wait_1_second (.out(callout_6_p2));

  // Notes on the sheet:
  //   Vary and modify a waveform generators
  //   (1) Pick a number
  //   for the frequency
  //   (can be constant,
  //   or adjustable, 
  //   random, or
  //   even varying over
  //   time)
  //   (2) Generate
  //   a waveform at
  //   that frequency.
  //   (optional) Selectively
  //   enable/disable the
  //   waveform using
  //   a button, or a
  //   periodic pulse,
  //   or some other
  //   varying true/false value.
  //   Period=150
  //   here means one click
  //   every 1.50 seconds
  //   (3) Modify the
  //   resulting sound
  //   in some way
  //   Period=150
  //   here means one pulse
  //   every 1.50 seconds,
  //   and Duty=8000 means
  //   half-second pulse.
endmodule

module diy_create_a_wave (
  input  Enable,
  input  Reset,
  input  [11:0] Freq
);

  wire linearmap_1_p3, linearmap_2_p1, pcmsink_1_p2, scope_1_p2;
  wire [7:0] Volume_Control_p1;
  wire [11:0] Freq_Slider_out;
  wire [15:0] linearmap_1_p2, linearmap_2_p3, pcmsink_1_p1;

  // Callout #(.background("#f5f50074"), .dx(50), .dy(-50), .foreground("#bd48d1"), .text("Pick a frequency.")) callout_1: pin names not known
  Slider #(.width(12)) Freq_Slider (.out(Freq_Slider_out));
  // LinearMap #(.domain("[0, 65535]"), .range("[0, 23]"), .widthIn(16)) linearmap_1: pin names not known; wires that end beside it: Freq, linearmap_1_p2, linearmap_1_p3, linearmap_1_p3
  sweep_0_to_65535 sweep_0_to_65535_1 (
    .Enable(Enable), .Sweep(linearmap_1_p2), .Freq(Freq_Slider_out), .Reset(Reset));  // open: click
  // Callout #(.background("#f5f50074"), .dx(49), .dy(142), .foreground("#bd48d1"), .text("Each value in this ROM is a 4 bit unsigned audio\nsample, in the range of 0 to F, in hex...\n0 1 2 3 4 5 6 7 8 9 A B C D E F\nlow              middle            high\nClick to edit them. They will play back in\na loop, at whatever frequency you pick.\n(NOTE: Only the first 24 values are used.)")) callout_2: pin names not known
  // Callout #(.background("#d6f5982f"), .dx(-38), .dy(-190), .foreground("#bd48d1"), .text("This restricts the \"sweep\" through ROM\nto the range 0 to 23. So only the\nfirst 24 values in the ROM are used.\nIf you want to use more than 24, or less,\nadjust the range in here.")) callout_3: pin names not known
  ROM #(.dataWidth(4), .proportions("tall")) rom_1 ();  // open: addr, data
  // LinearMap #(.domain("[0, 15]"), .range("[-10000, +10000]"), .widthIn(4), .widthOut(16)) linearmap_2: pin names not known; wires that end beside it: linearmap_2_p1, linearmap_2_p1, linearmap_2_p3
  // Scope #(.mode("twosComplement"), .samples(320), .scopeheight(100), .scopewidth(240), .width(16)) scope_1: pin names not known; wires that end beside it: linearmap_2_p3, scope_1_p2
  Clock clock_1 (.out(scope_1_p2));
  // Dial #(.mode("twosComplement")) Volume_Control: pin names not known; wires that end beside it: Volume_Control_p1
  // Callout #(.dx(-96), .dy(-128), .text("This adjusts the range \nfrom [0, 15] to [-10000, +10000]")) callout_4: pin names not known
  // PCMSink #(.mode("twosComplement"), .rate("16 kHz"), .width(16)) pcmsink_1: pin names not known; wires that end beside it: pcmsink_1_p1, pcmsink_1_p2
  volume_limiter volume_limiter_1 (
    .AudioSample(linearmap_2_p3), .Volume(Volume_Control_p1), .AdjustedSample(pcmsink_1_p1));
  Clock clock_2 (.out(pcmsink_1_p2));

  // Notes on the sheet:
  //   contents of rom_1 (hex, n*v repeats v):
  //   48*7 31*0 2 f 0 9 9 d a 3 3 7 8 e 3 0 9 a a 5 d e 2 1 8 0 8 8 4 6 f b a 9 d 2 0 3 7 2 b 9 3 5 9 f 3
  //   3 6 8 6 6 a a 9 3 8 9 e 9 a 3 9 b 2 f 1 c 3 4 0 0 3 d 5 5 6 9 c 7 0 f 7 3 0 3 d 1 3 7 d 7 2 8 5 4 9
  //   6 b 2 b 3 9 1 2 5 a 1 6 d a a 0 3 7 8 8 1 d d 4 6 5 e b f b 2 1 9 e 1 c 5 9 c 6 f e 2 8 5 e 9 6 9 f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
endmodule

module diy_sine_wave (
);

  wire clock_1_out, clock_2_out, pcmsink_1_p2, saturatingadder_1_p1, saturatingmultiplier_1_p1,
       saturatingnegator_1_p2, scope_1_p2;
  wire [7:0] Volume_Control_p1;
  wire [15:0] fitrange_1_p2, scope_1_p1;
  wire [31:0] saturatingadder_1_p2, saturatingadder_1_p3, saturatingadder_2_p2, saturatingadder_2_p3;

  // SaturatingAdder #(.mode("twosComplement"), .width(32)) saturatingadder_1: pin names not known; wires that end beside it: saturatingadder_1_p1, saturatingadder_1_p2, saturatingadder_1_p3
  Clock clock_1 (.out(clock_1_out));
  // SaturatingAdder #(.mode("twosComplement"), .width(32)) saturatingadder_2: pin names not known; wires that end beside it: saturatingadder_1_p3, saturatingadder_2_p2, saturatingadder_2_p3
  Clock clock_2 (.out(clock_2_out));
  // Callout #(.dx(94), .dy(-8), .foreground("#0400fa"), .text("Using k=2 and m=5000\nworks well")) callout_1: pin names not known
  Register #(.width(32)) Xd (.D(saturatingadder_1_p3), .Q(saturatingadder_1_p2), .clk(clock_1_out));  // open: en, clr
  Register #(.\initial ('h2710), .width(32)) X (
    .D(saturatingadder_2_p3), .Q(saturatingadder_2_p2), .clk(clock_2_out));  // open: en, clr
  // Callout #(.dx(21), .dy(59), .foreground("#0400fa"), .text("X times (negative k)\ndivided by m")) callout_2: pin names not known
  // SaturatingNegator #(.mode("twosComplement"), .width(32)) saturatingnegator_1: pin names not known; wires that end beside it: 32'h2, saturatingnegator_1_p2, saturatingadder_2_p2, saturatingnegator_1_p2
  // SaturatingMultiplier #(.mode("twosComplement"), .width(32)) saturatingmultiplier_1: pin names not known; wires that end beside it: saturatingmultiplier_1_p1, saturatingmultiplier_1_p1, 32'h1388
  // SaturatingDivider #(.mode("twosComplement"), .width(32)) saturatingdivider_1: pin names not known; wires that end beside it: saturatingadder_1_p1
  // FitRange #(.normalization("cap"), .typeIn("twosComplement"), .widthIn(32), .widthOut(16)) fitrange_1: pin names not known; wires that end beside it: saturatingadder_2_p2, fitrange_1_p2
  // Dial #(.mode("twosComplement")) Volume_Control: pin names not known; wires that end beside it: Volume_Control_p1
  // Scope #(.mode("twosComplement"), .samples(1600), .scopeheight(80), .scopewidth(240), .width(16)) scope_1: pin names not known; wires that end beside it: scope_1_p1, scope_1_p2
  volume_limiter volume_limiter_1 (
    .AudioSample(fitrange_1_p2), .Volume(Volume_Control_p1), .AdjustedSample(scope_1_p1));
  Clock clock_3 (.out(scope_1_p2));
  // PCMSink #(.mode("twosComplement"), .rate("16 kHz"), .trigger("falling"), .width(16)) pcmsink_1: pin names not known; wires that end beside it: scope_1_p1, pcmsink_1_p2
  Clock clock_4 (.out(pcmsink_1_p2));

  // Notes on the sheet:
  //   Goal: generate an audio wave by simulating a "mass and spring" system. Just picture a
  //   baseball, suspended from the ceiling by a spring. When perfectly balanced, the ball will
  //   be at rest, not bouncing at all. Call that position X=0. If we give it a push to displace it
  //   upwards (making X positive) or downwards (making X negative), it will react by vibrating,
  //   oscillating up and down. The varying position, X, over time will be our audio signal: we
  //   will essentially be listening the the vibrations of the mass on a spring.
  //   Physics notes: Position is X, velocity is Xd (in units of distance per clock tick), and the
  //   spring is pulling back towards the origin with force X*k/m, where k is the spring
  //   constant and m is the mass. After 1 clock tick, Xd changes by by -X*k/m, so the new
  //   velocity Xd' after 1 clock tick will be:
  //       Xd' = Xd + X*(-k)/m
  //   And X changes depending on the velocity, so the new position after 1 clock tick will be:
  //      X' = X + Xd'
  //   The overall frequency of oscillation will be sqrt(k/m), in units of oscillations per clock tick.
  //   If we are running at 16kHz clock rate, then freq = 16000*sqrt(k/m) Hz.
  //   k
  //   m
endmodule

module diy_envelope (
  input  Enable,
  input  Reset,
  input  [11:0] Period
);

  wire linearmap_1_p3, linearmap_2_p1, linearmap_2_p3, pcmsink_1_p2, scope_1_p2;
  wire [7:0] Volume_Control_p1;
  wire [11:0] Freq_Slider_out, Period_Slider_out;
  wire [15:0] linearmap_1_p2, saturatingmultiplier_1_p3, sinwave_1_audiosignal,
       volume_limiter_1_adjustedsample;

  Slider #(.width(12)) Freq_Slider (.out(Freq_Slider_out));
  // Callout #(.background("#f5f50074"), .dx(50), .dy(-50), .foreground("#bd48d1"), .text("Pick a period")) callout_1: pin names not known
  Slider #(.width(12)) Period_Slider (.out(Period_Slider_out));
  sinwave sinwave_1 (.AudioSignal(sinwave_1_audiosignal), .Freq(12'h140));  // open: Enable, Reset
  // LinearMap #(.domain("[0, 65535]"), .range("[0, 256]"), .widthIn(16)) linearmap_1: pin names not known; wires that end beside it: Period, linearmap_1_p2, linearmap_1_p3, linearmap_1_p3
  sweep_0_to_65535_slowly sweep_0_to_65535_slowly_1 (
    .Enable(Enable), .Sweep(linearmap_1_p2), .Period(Period_Slider_out), .Reset(Reset));  // open: click
  // Callout #(.background("#d6f5982f"), .dx(-38), .dy(-190), .foreground("#bd48d1"), .text("This restricts the \"sweep\" through ROM\nto the range 0 to 255. So ALL values in the \nROM are used.\nIf you want to use fewer,\nadjust the range in here.")) callout_2: pin names not known
  // Callout #(.background("#f5f50074"), .dx(49), .dy(142), .foreground("#bd48d1"), .text("Each value in this ROM is a 4 bit unsigned \"volume\"\nnumer, in the range of 0 to F, in hex...\n0 1 2 3 4 5 6 7 8 9 A B C D E F\nlow              middle            high\nClick to edit them. These will be used\nto control the volume of the sound\n(0=OFF, 7=medium, F=loud)")) callout_3: pin names not known
  ROM #(.dataWidth(4), .proportions("tall")) rom_1 ();  // open: addr, data
  // LinearMap #(.domain("[0, 15]"), .range("[0, 32767]"), .widthIn(4), .widthOut(16)) linearmap_2: pin names not known; wires that end beside it: linearmap_2_p1, linearmap_2_p1, linearmap_2_p3
  // Callout #(.dx(-96), .dy(-128), .text("This adjusts the range \nfrom [0, 15] to [0, 32767]")) callout_4: pin names not known
  // SaturatingMultiplier #(.mode("twosComplement"), .normalization("fit"), .width(16)) saturatingmultiplier_1: pin names not known; wires that end beside it: sinwave_1_audiosignal, linearmap_2_p3, saturatingmultiplier_1_p3
  // Scope #(.mode("twosComplement"), .samples(320), .scopeheight(100), .scopewidth(240), .width(16)) scope_1: pin names not known; wires that end beside it: saturatingmultiplier_1_p3, scope_1_p2
  Clock clock_1 (.out(scope_1_p2));
  volume_limiter volume_limiter_1 (
    .AudioSample(saturatingmultiplier_1_p3), .Volume(Volume_Control_p1),
    .AdjustedSample(volume_limiter_1_adjustedsample));
  // Dial #(.mode("twosComplement")) Volume_Control: pin names not known; wires that end beside it: Volume_Control_p1
  // PCMSink #(.mode("twosComplement"), .rate("16 kHz"), .width(16)) pcmsink_1: pin names not known; wires that end beside it: volume_limiter_1_adjustedsample, pcmsink_1_p2
  Clock clock_2 (.out(pcmsink_1_p2));

  // Notes on the sheet:
  //   contents of rom_1 (hex, n*v repeats v):
  //   1 3 6 8 9 f f f e d 14*c b b a a a 9 9 9 8 8 8 7 7 7 5*6 6*5 6*4 6*3 7*2 7*1
endmodule

module diy_delayline_reverb (
);

  wire clock_2_out, clock_4_out, counter_1_p1, Play_out, scope_1_p2;
  wire [7:0] Mix_Control_p3, Reverb_Boost_2_p2, Reverb_Boost_p2, Volume_Control_p2;
  wire [13:0] counter_1_p2;
  wire [15:0] callout_1_p1, Mix_Control_p2, ram_1_dout, recording_thank_you_1_audiosignal, Reverb_Boost_2_p1,
       Reverb_Boost_p1, saturatingadder_1_p1, saturatingadder_2_p1, scope_1_p1,
       volume_limiter_1_adjustedsample, volume_limiter_2_adjustedsample, volume_limiter_3_adjustedsample;

  Button Play (.out(Play_out));
  recording_thank_you recording_thank_you_1 (
    .AudioSignal(recording_thank_you_1_audiosignal), .Enable(Play_out));  // open: Reset
  // SaturatingAdder #(.mode("twosComplement"), .width(16)) saturatingadder_1: pin names not known; wires that end beside it: saturatingadder_1_p1
  // Callout #(.background("#f5f50074"), .dx(22), .dy(-37), .foreground("#bd48d1"), .text("Feed audio data in here....")) callout_1: pin names not known; wires that end beside it: callout_1_p1
  // SaturatingAdder #(.mode("twosComplement"), .width(16)) saturatingadder_2: pin names not known; wires that end beside it: saturatingadder_2_p1
  balancing_fader balancing_fader_1 (
    .AudioSampleLeft(saturatingadder_1_p1), .Balance(Mix_Control_p3), .CombinedSample(saturatingadder_2_p1),
    .AudioSampleRight(Mix_Control_p2));
  // Dial #(.mode("twosComplement")) Mix_Control: pin names not known; wires that end beside it: recording_thank_you_1_audiosignal, Mix_Control_p2, Mix_Control_p3
  // Counter #(.max('h3fff), .width(14)) counter_1: pin names not known; wires that end beside it: counter_1_p1, counter_1_p2, callout_1_p1, callout_1_p1
  Clock clock_1 (.out(counter_1_p1));
  RAM #(.addrWidth(14), .dataWidth(16)) ram_1 (
    .addr(counter_1_p2), .we(1'b1), .clk(clock_2_out), .din(callout_1_p1), .dout(ram_1_dout));
  Clock clock_2 (.out(clock_2_out));
  volume_limiter volume_limiter_1 (
    .AudioSample(Reverb_Boost_p1), .Volume(Reverb_Boost_p2), .AdjustedSample(volume_limiter_1_adjustedsample));
  // Dial #(.mode("twosComplement")) Reverb_Boost: pin names not known; wires that end beside it: Reverb_Boost_p1, Reverb_Boost_p2, volume_limiter_1_adjustedsample
  volume_limiter volume_limiter_2 (
    .AudioSample(Reverb_Boost_2_p1), .Volume(Reverb_Boost_2_p2),
    .AdjustedSample(volume_limiter_2_adjustedsample));
  // Dial #(.mode("twosComplement")) Reverb_Boost_2: pin names not known; wires that end beside it: Reverb_Boost_2_p1, Reverb_Boost_2_p2, volume_limiter_2_adjustedsample
  // Callout #(.background("#f5f50074"), .dx(-31), .dy(89), .foreground("#bd48d1"), .text("This RAM can hold about 1 second of audio data\n(16000 samples x 16-bits each).\nThe total amount can be adjusted\nif you change the address bit-width,\nand the counter-bit width.")) callout_2: pin names not known
  // Callout #(.background("#f5f50074"), .dx(-44), .dy(-33), .foreground("#bd48d1"), .text("... and it will come out \nhere 1 second later.")) callout_3: pin names not known; wires that end beside it: ram_1_dout
  // Scope #(.mode("twosComplement"), .samples(320), .scopeheight(100), .scopewidth(240), .width(16)) scope_1: pin names not known; wires that end beside it: scope_1_p1, scope_1_p2
  Clock clock_3 (.out(scope_1_p2));
  volume_limiter volume_limiter_3 (
    .AudioSample(scope_1_p1), .Volume(Volume_Control_p2), .AdjustedSample(volume_limiter_3_adjustedsample));
  // Dial #(.mode("twosComplement")) Volume_Control: pin names not known; wires that end beside it: scope_1_p1, Volume_Control_p2
  Clock clock_4 (.out(clock_4_out));
  // PCMSink #(.mode("twosComplement"), .rate("16 kHz"), .width(16)) pcmsink_1: pin names not known; wires that end beside it: volume_limiter_3_adjustedsample, clock_4_out

  // Notes on the sheet:
  //   (1) Send something into the RAM. 
  //   - Maybe just the original audio?
  //   - Or, mix the original audio together with feedback from the RAM output!
  //   (2) Send something to the speakers (PCM audio output).
  //   - Maybe just the RAM output?
  //   - Or mix that together with the original audio?
  //   (3) Add volume/boost somewhere...
  //   - Maybe boost the feedback loop?
  //   - Or boost the output of the RAM?
  //   - Or both?
endmodule
