// Logisim project probes.circ as structural Verilog: 1 circuit, main circuit main
module main (
);

  wire buffer_1_out, controlled_buffer_1_out;

  assign controlled_buffer_1_out = 1'b0 ? 1'b0 : 1'bz;  // Controlled_Buffer controlled_buffer_1
  // Probe on 8'h4a
  // Probe on 8'h4a
  // Probe on 1'b1
  // Probe on 1'b0
  buf buffer_1 (buffer_1_out, 1'b0);
  buf buffer_2 (buffer_1_out, 1'b1);
  // Probe on controlled_buffer_1_out
  // Probe on buffer_1_out
endmodule
