// Logisim project simple-majority-demo.circ as structural Verilog: 1 circuit, main circuit main
module main (
  input  A,
  input  B,
  input  C,
  output Majority
);

  wire and_1_out, and_2_out, and_3_out;

  and and_1 (and_1_out, B, A);
  and and_2 (and_2_out, C, A);
  and and_3 (and_3_out, C, B);
  or or_1 (Majority, and_1_out, and_2_out, and_3_out);
endmodule
