// Logisim project simple-or3-demo.circ as structural Verilog: 1 circuit, main circuit main
module main (
  input  X,
  input  Y,
  input  Z
);

  wire or_1_out;

  or or_1 (or_1_out, X, Y, Z);
  LED Result (.in(or_1_out));
endmodule
