// Logisim project alchitry-cu-demo.circ as structural Verilog: 12 circuits, main circuit snake-on-digits
module simple_io_demo (
);

  wire C_out, center, clock_1_out, clock_2_out, D_out, DIPB_sw6, DIPB_sw7, DIPB_sw8, DIPC_sw7, DIPC_sw8,
       down, hexdigitmultiplexer4_1_digit_enable_1, hexdigitmultiplexer4_1_digit_enable_2,
       hexdigitmultiplexer4_1_digit_enable_3, hexdigitmultiplexer4_1_digit_enable_4, L_out, LEDB_p1, LEDB_p2,
       LEDB_p3, LEDB_p4, LEDB_p5, LEDC_p4, LEDC_p5, LEDC_p6, LEDC_p7, LEDC_p8, LEDC_p9, LEDD_p3, LEDD_p4,
       LEDD_p5, LEDD_p6, LEDD_p7, LEDD_p8, LEDD_p9, LEDD_p10, left, or_1_out, or_2_out, R_out, right, rst,
       timedpulse_1_p5, timedpulse_1_p6, U_out, up;
  wire [2:0] counter_1_q;
  wire [3:0] hexdigitmultiplexer4_1_multiplexednibble;
  wire [7:0] shifter_1_out;
  wire [15:0] counter_2_q;

  or or_1 (or_1_out, up, down);
  // LEDBar LEDB: pin names not known; wires that end beside it: LEDB_p1, LEDB_p2, LEDB_p3, LEDB_p4, LEDB_p5
  DipSwitch DIPB (
    .sw1(LEDB_p1), .sw2(LEDB_p2), .sw3(LEDB_p3), .sw4(LEDB_p4), .sw5(LEDB_p5), .sw6(DIPB_sw6),
    .sw7(DIPB_sw7), .sw8(DIPB_sw8));
  Clock clock_1 (.out(clock_1_out));
  // LEDBar LEDC: pin names not known; wires that end beside it: DIPB_sw6, DIPB_sw7, DIPB_sw8, LEDC_p4, LEDC_p5, LEDC_p6, LEDC_p7, LEDC_p8, LEDC_p9
  DipSwitch DIPC (
    .sw1(LEDC_p4), .sw2(LEDC_p5), .sw3(LEDC_p6), .sw4(LEDC_p7), .sw5(LEDC_p8), .sw6(LEDC_p9), .sw7(DIPC_sw7),
    .sw8(DIPC_sw8));
  or or_2 (or_2_out, left, right);
  Counter #(.max('h7), .width(3)) counter_1 (
    .load(center), .D(3'b100), .count(or_1_out), .Q(counter_1_q), .up(down), .clk(clock_1_out));  // open: carry, clr
  Counter #(.max('hffff), .width(16)) counter_2 (
    .count(or_2_out), .Q(counter_2_q), .up(right), .clk(clock_2_out), .clr(rst));  // open: load, D, carry
  Clock clock_2 (.out(clock_2_out));
  Shifter #(.shift("rl")) shifter_1 (.in(8'h1), .\dist (counter_1_q), .out(shifter_1_out));
  // LEDBar #(.inputtype("bus")) LEDA: pin names not known; wires that end beside it: shifter_1_out
  // LEDBar LEDD: pin names not known; wires that end beside it: DIPC_sw7, DIPC_sw8, LEDD_p3, LEDD_p4, LEDD_p5, LEDD_p6, LEDD_p7, LEDD_p8, LEDD_p9, LEDD_p10
  DipSwitch DIPD (
    .sw1(LEDD_p3), .sw2(LEDD_p4), .sw3(LEDD_p5), .sw4(LEDD_p6), .sw5(LEDD_p7), .sw6(LEDD_p8), .sw7(LEDD_p9),
    .sw8(LEDD_p10));
  Hex_Digit_Display #(.digits(4), .persist(40)) Hex (.value(hexdigitmultiplexer4_1_multiplexednibble));  // open: dp
  HexDigitMultiplexer4 hexdigitmultiplexer4_1 (
    .Input(counter_2_q), .MultiplexedNibble(hexdigitmultiplexer4_1_multiplexednibble),
    .Digit_Enable_1(hexdigitmultiplexer4_1_digit_enable_1),
    .Digit_Enable_2(hexdigitmultiplexer4_1_digit_enable_2),
    .Digit_Enable_3(hexdigitmultiplexer4_1_digit_enable_3),
    .Digit_Enable_4(hexdigitmultiplexer4_1_digit_enable_4), .refresh_1ms(timedpulse_1_p6));
  Button L (.out(L_out));
  Button U (.out(U_out));
  Button C (.out(C_out));
  Button R (.out(R_out));
  Button D (.out(D_out));
  // TimedPulse #(.interval(1.0), .unit("ms")) timedpulse_1: pin names not known; wires that end beside it: hexdigitmultiplexer4_1_digit_enable_1, hexdigitmultiplexer4_1_digit_enable_2, hexdigitmultiplexer4_1_digit_enable_3, hexdigitmultiplexer4_1_digit_enable_4, timedpulse_1_p5, timedpulse_1_p6
  Clock clock_3 (.out(timedpulse_1_p5));
  debounce debounce_1 (.Button(U_out), .RisingEdge(up), .enable_1ms(timedpulse_1_p6));  // open: Current
  debounce debounce_2 (.Button(L_out), .RisingEdge(left), .enable_1ms(timedpulse_1_p6));  // open: Current
  debounce debounce_3 (.Button(C_out), .RisingEdge(center), .enable_1ms(timedpulse_1_p6));  // open: Current
  debounce debounce_4 (.Button(R_out), .RisingEdge(right), .enable_1ms(timedpulse_1_p6));  // open: Current
  debounce debounce_5 (.Button(D_out), .RisingEdge(down), .enable_1ms(timedpulse_1_p6));  // open: Current
  // Callout #(.dx(-121), .dy(11), .format("wrapped"), .halign("center"), .style("margin: 4px;"), .text("This generates a pulse every 1ms to drive the hex digit display refresh and button debounce circuits."), .valign("base")) callout_1: pin names not known
  Button Reset (.out(rst));

  // Notes on the sheet:
  //   This circuit is meant to test all of the I/O features on the Alchitry Cu V2 fpga board with Io V2 hat, which has: a 4-digit seven segment display, six buttons (5 on the hat in a d-pad arrangement, and 1 more on the main fpga board), and 4x8 LEDs (3 bars of 8 on the hat, 1 bar of 8 on the main fpga board). The tiny DIP switches are used to control most of the LEDs.
  //   For this demo, set the fpga clock speed to a few kHz or higher, anything fast should be fine.
  //   Use the left/center/right D-Pad buttons to control
  //   which LED is illuminated along the vertical bar,
  //   and use the DIP switches to control the other LEDs.
  //   Use the up/down/reset
  //   buttons to countrol the
  //   value on the digit display.
  //   Map these to the Banks of LEDs
  //   (3x8 on Io hat, 1x8 more on fpga board)
  //   Map this to the 4-gang 7segment display.
  //   Map these to the
  //   D-Pad Buttons
  //   Map this to
  //   the reset button
endmodule

module simple_counter (
  output E12
);

  wire C_out, clock_1_out, Count_out, D_out, L_out, U_out;
  wire [3:0] counter_1_q;

  Button Count (.out(Count_out));
  Clock clock_1 (.out(clock_1_out));
  Counter #(.max('hf), .width(4)) counter_1 (
    .count(Count_out), .Q(counter_1_q), .clk(clock_1_out));  // open: load, D, carry, clr
  Hex_Digit_Display #(.digits(4)) hex_digit_display_1 (.value(counter_1_q));  // open: dp
  Button U (.out(U_out));
  Button L (.out(L_out));
  Button C (.out(C_out));
  Button D (.out(D_out));
  Button R (.out(E12));

  // Notes on the sheet:
  //   Another demo circuit for the Alchitry Cu V2 with Io V2 hat.
  //   A 4-bit counter can be displayed as a hex digit on any of the
  //   four seven-segment displays. The left/right/up/center buttons
  //   control which seven-segment digit(s) are enabled. All show the
  //   same 4-bit hex digit. The down button enables the decimal point
  //   of whichever digit(s) are enabled.
  //   The extra button is used to increment the count.
  //   For this demo, set the fpga clock to very slow speed, e.g. ~1hz,
  //   otherwise the count button will go very very fast.
endmodule

module snake_on_digits (
);

  wire A_out, and_1_out, and_2_out, and_3_out, and_4_out, and_5_out, clock_3_out, clock_4_out, clock_5_out,
       clock_6_out, clock_7_out, clock_8_out, clock_9_out, clock_10_out, collision, comparator_1_eq, D_out,
       debounce_1_risingedge, debounce_2_risingedge, debounce_3_risingedge, debounce_4_risingedge,
       decoder_2_out0, decoder_2_out1, decoder_2_out2, decoder_2_out3, died, Digit0__left_collision,
       Digit1_collision, Digit2_collision, Digit_3__right_collision, ending, go_play, go_prep, grow,
       or_1_out, or_2_out, or_3_out, play, prep, priority_encoder_1_gs, priority_encoder_2_gs, R_out, reset,
       S_out, sevensegmentmultiplexer4_1_digit_enable_1, sevensegmentmultiplexer4_1_digit_enable_2,
       sevensegmentmultiplexer4_1_digit_enable_3, sevensegmentmultiplexer4_1_digit_enable_4, tick, tick_1ms,
       W_out;
  wire [1:0] dir_q, head_digit, last_input_q, next_digit, next_dir_1_next_dir, priority_encoder_1_out,
       priority_encoder_2_out, state_q;
  wire [2:0] head_segment, next_segment;
  wire [3:0] LURD;
  wire [4:0] multiplexer_3_out, SnakeLen_q;
  wire [4:3] next_out;
  wire [5:5] dir_to_vec_1_rightordown;
  wire [7:0] sevensegmentmultiplexer4_1_multiplexedvalue;
  wire [31:0] digits, multiplexer_1_out, multiplexer_2_out, shifter_1_out, splash, timer_q;

  snake_clock snake_clock_1 (.tick_1ms(tick_1ms), .tick_1s(tick));
  _7_Segment_Display #(.digits(4), .persist(50)) u_7_segment_display_1 (
    .g(sevensegmentmultiplexer4_1_multiplexedvalue[6]), .f(sevensegmentmultiplexer4_1_multiplexedvalue[5]),
    .a(sevensegmentmultiplexer4_1_multiplexedvalue[0]), .b(sevensegmentmultiplexer4_1_multiplexedvalue[1]),
    .e(sevensegmentmultiplexer4_1_multiplexedvalue[4]), .d(sevensegmentmultiplexer4_1_multiplexedvalue[3]),
    .c(sevensegmentmultiplexer4_1_multiplexedvalue[2]), .dp(sevensegmentmultiplexer4_1_multiplexedvalue[7]));
  SevenSegmentMultiplexer4 sevensegmentmultiplexer4_1 (
    .Input4(multiplexer_1_out[7:0]), .MultiplexedValue(sevensegmentmultiplexer4_1_multiplexedvalue),
    .Digit_Enable_1(sevensegmentmultiplexer4_1_digit_enable_1),
    .Digit_Enable_2(sevensegmentmultiplexer4_1_digit_enable_2),
    .Digit_Enable_3(sevensegmentmultiplexer4_1_digit_enable_3),
    .Digit_Enable_4(sevensegmentmultiplexer4_1_digit_enable_4), .Input1(multiplexer_1_out[31:24]),
    .Input2(multiplexer_1_out[23:16]), .Input3(multiplexer_1_out[15:8]), .refresh_1ms(tick_1ms));
  Multiplexer #(.width(32)) multiplexer_1 (
    .in0(splash), .in1(digits), .out(multiplexer_1_out), .sel(play));  // open: en
  Priority_Encoder #(.select(2)) priority_encoder_1 (
    .in0(go_prep), .in1(go_play), .in2(died), .out(priority_encoder_1_out), .gs(priority_encoder_1_gs));  // open: in3, en_out, en_in
  and and_1 (and_1_out, priority_encoder_1_gs, tick);
  or or_1 (or_1_out, prep, grow);
  Multiplexer #(.width(32)) multiplexer_2 (
    .in0(shifter_1_out), .in1({32{1'b1}}), .out(multiplexer_2_out), .sel(or_1_out));  // open: en
  Clock clock_1 ();  // open: out
  Clock clock_2 ();  // open: out
  Decoder #(.enable("false"), .select(2)) decoder_1 (
    .out0(prep), .out1(play), .out2(ending), .sel(state_q));  // open: out3
  Register #(.width(2)) state (
    .D(priority_encoder_1_out), .en(and_1_out), .Q(state_q), .clk(clock_3_out));  // open: clr
  Clock clock_3 (.out(clock_3_out));
  and and_2 (and_2_out, grow, tick);
  Register #(.\initial ('hffffffff), .width(32)) timer (
    .D(multiplexer_2_out), .en(tick), .Q(timer_q), .clk(clock_4_out));  // open: clr
  Clock clock_4 (.out(clock_4_out));
  Multiplexer #(.width(5)) multiplexer_3 (
    .in0({next_digit, next_segment}), .in1(5'b00110), .out(multiplexer_3_out), .sel(prep));  // open: en
  Clock clock_5 (.out(clock_5_out));
  or or_2 (or_2_out, prep, tick);
  Counter #(.\initial ('h1), .max('h1f), .width(5)) SnakeLen (
    .load(prep), .D(5'b00001), .count(and_2_out), .Q(SnakeLen_q), .clk(clock_6_out));  // open: carry, clr
  Clock clock_6 (.out(clock_6_out));
  Comparator #(.mode("unsigned"), .width(32)) comparator_1 (
    .a(32'h1), .b(timer_q), .eq(comparator_1_eq));  // open: gt, lt
  Shifter #(.shift("lr"), .width(32)) shifter_1 (.in(timer_q), .\dist (5'b00001), .out(shifter_1_out));
  Button A (.out(A_out));
  Register #(.\initial ('h2), .width(2)) dir (
    .D(next_dir_1_next_dir), .en(and_3_out), .Q(dir_q), .clk(clock_7_out));  // open: clr
  and and_3 (and_3_out, tick_1ms, tick);
  Clock clock_7 (.out(clock_7_out));
  Register #(.\initial ('h6), .width(5)) head (
    .D(multiplexer_3_out), .en(or_2_out), .Q({head_digit, head_segment}), .clk(clock_5_out));  // open: clr
  Register #(.\initial ('h1), .width(1)) u_grow (
    .D(comparator_1_eq), .en(tick), .Q(grow), .clk(clock_8_out));  // open: clr
  Clock clock_8 (.out(clock_8_out));
  Button W (.out(W_out));
  Button D (.out(D_out));
  Button S (.out(S_out));
  next_dir next_dir_1 (.cur_dir(dir_q), .LURD(LURD), .next_dir(next_dir_1_next_dir));
  dir_to_vec dir_to_vec_1 (.dir(dir_q), .RightOrDown(dir_to_vec_1_rightordown[5]));
  Decoder #(.enable("false"), .select(2)) decoder_2 (
    .out0(decoder_2_out0), .out1(decoder_2_out1), .out2(decoder_2_out2), .out3(decoder_2_out3),
    .sel(next_digit));
  // LEDBar #(.inputtype("bus")) left: pin names not known; wires that end beside it: timer_q[23:16]
  Button R (.out(R_out));
  debounce debounce_1 (.Button(A_out), .RisingEdge(debounce_1_risingedge), .enable_1ms(tick_1ms));  // open: Current
  debounce debounce_2 (.Button(W_out), .RisingEdge(debounce_2_risingedge), .enable_1ms(tick_1ms));  // open: Current
  debounce debounce_3 (.Button(D_out), .RisingEdge(debounce_3_risingedge), .enable_1ms(tick_1ms));  // open: Current
  debounce debounce_4 (.Button(S_out), .RisingEdge(debounce_4_risingedge), .enable_1ms(tick_1ms));  // open: Current
  debounce debounce_5 (.Button(R_out), .Current(reset), .enable_1ms(tick_1ms));  // open: RisingEdge
  PLA #(.in_width(6), .out_width(5), .\table ("000000 11000 # <A\n000001 00000 # @A\n000010 00110 # @G\n000011 11011 # <D\n000100 11110 # <G\n000101 11000 # <A\n000110 11110 # <G\n000111 10111 # err\n001000 00100 # @E\n001001 00010 # @C\n001010 00001 # @B\n001011 00100 # @E\n001100 00101 # @F\n001101 00100 # @E\n001110 00101 # @F\n001111 10111 # err\n010000 10111 # err\n010001 01000 # >A\n010010 01110 # >G\n010011 10111 # err\n010100 00110 # @G\n010101 00000 # @A\n010110 10111 # err\n010111 10111 # err\n011000 00101 # @F\n011001 10111 # err\n011010 10111 # err\n011011 00101 # @F\n011100 10111 # err\n011101 10111 # err\n011110 00100 # @E\n011111 10111 # err\n100000 10111 # err\n100001 00110 # @G\n100010 00011 # @D\n100011 10111 # err\n100100 11011 # <D\n100101 11110 # <G\n100110 10111 # err\n100111 10111 # err\n101000 00010 # @C\n101001 10111 # err\n101010 10111 # err\n101011 00010 # @C\n101100 10111 # err\n101101 10111 # err\n101110 00001 # @B\n101111 10111 # err\n110000 01000 # >A\n110001 01110 # >G\n110010 01011 # >D\n110011 01011 # >D\n110100 00011 # @D\n110101 00110 # @G\n110110 01110 # >G\n110111 10111 # err\n111000 00001 # @B\n111001 00010 # @C\n111010 00001 # @B\n111011 00001 # @B\n111100 00101 # @F\n111101 00100 # @E\n111110 00010 # @C\n111111 10111 # err")) next (
    .in({dir_to_vec_1_rightordown[5], next_dir_1_next_dir, head_segment}), .out({next_out, next_segment}));
  // LEDBar #(.inputtype("bus")) middle: pin names not known; wires that end beside it: timer_q[15:8]
  Priority_Encoder #(.select(2)) priority_encoder_2 (
    .in0(debounce_1_risingedge), .in1(debounce_2_risingedge), .in2(debounce_3_risingedge),
    .in3(debounce_4_risingedge), .out(priority_encoder_2_out), .gs(priority_encoder_2_gs));  // open: en_out, en_in
  // LEDBar #(.inputtype("bus")) right: pin names not known; wires that end beside it: timer_q[7:0]
  and and_4 (and_4_out, priority_encoder_2_gs, tick_1ms);
  Adder #(.width(2)) adder_1 (.a(next_out), .b(head_digit), .out(next_digit));  // open: cin, cout
  digit_state Digit0__left (
    .SnakeLen(SnakeLen_q), .ArriveSegment(next_segment), .ArriveEnable(decoder_2_out0), .tick(tick),
    .SegState(digits[31:24]), .Collision(Digit0__left_collision), .grow(grow), .clear(prep));
  digit_state Digit1 (
    .SnakeLen(SnakeLen_q), .ArriveSegment(next_segment), .ArriveEnable(decoder_2_out1), .tick(tick),
    .SegState(digits[23:16]), .Collision(Digit1_collision), .grow(grow), .clear(prep));
  digit_state Digit2 (
    .SnakeLen(SnakeLen_q), .ArriveSegment(next_segment), .ArriveEnable(decoder_2_out2), .tick(tick),
    .SegState(digits[15:8]), .Collision(Digit2_collision), .grow(grow), .clear(prep));
  digit_state Digit_3__right (
    .SnakeLen(SnakeLen_q), .ArriveSegment(next_segment), .ArriveEnable(decoder_2_out3), .tick(tick),
    .SegState(digits[7:0]), .Collision(Digit_3__right_collision), .grow(grow), .clear(prep));
  Decoder #(.enable("false"), .select(2)) decoder_3 (
    .out0(LURD[3]), .out1(LURD[2]), .out2(LURD[1]), .out3(LURD[0]), .sel(last_input_q));
  Register #(.\initial ('h2), .width(2)) last_input (
    .D(priority_encoder_2_out), .en(and_4_out), .Q(last_input_q), .clk(clock_9_out));  // open: clr
  Clock clock_9 (.out(clock_9_out));
  or or_3 (or_3_out, go_play, and_4_out);
  or or_4 (collision, Digit0__left_collision, Digit1_collision, Digit2_collision, Digit_3__right_collision);
  and and_5 (and_5_out, or_3_out, prep);
  Register #(.width(1)) register_1 (.D(and_5_out), .en(tick_1ms), .Q(go_play), .clk(clock_10_out));  // open: clr
  Clock clock_10 (.out(clock_10_out));
  and and_6 (died, play, collision, tick);
  press_any_button press_any_button_1 (.reset(go_prep), .tick(tick), .splash(splash));
  or or_5 (go_prep, reset, ending);

  // Notes on the sheet:
  //   This circuit implements a "snake" like game on the Alchitry Cu V2 fpga board with Io V2 hat. It uses the 4-digit seven segment display as a kind of simple screen, and the buttons as a D-Pad to control the direction. The snake grows each time the timer reaches zero. You can wrap around the edge of the screen (otherwise the game becomes extremely difficult.
  //   This circuit is a bit rediculous.
  //   For this demo, set the fpga clock speed to a few MHz, but no more than 150MHz to avoid timing constraint failures. Most anything over a few kHz should be fine though.
  //   Map the 4-digit display to the display, of course.
  //   Map the W/A/S/D buttons to
  //   Up/Left/Down/Right buttons.
  //   Map R to the side button.
endmodule

module debounce (
  input  Button,
  input  enable_1ms,
  output Current,
  output RisingEdge
);

  wire and_1_out, clock_1_out, clock_2_out, clock_3_out, counter_carry, old_q, sample0_q, sample1_q, sync0_q,
       sync1_q, xor_1_out;

  Register #(.width(1)) sync0 (.D(Button), .Q(sync0_q), .clk(clock_1_out));  // open: en, clr
  Clock clock_1 (.out(clock_1_out));
  // Callout #(.dx(29), .dy(-39), .format("wrapped"), .halign("center"), .style("margin: 4px;"), .text("2-stage input chain to avoid meta-stability (sampling every clock cycle)"), .textwidth(118), .valign("top")) callout_1: pin names not known
  Register #(.width(1)) sync1 (.D(sync0_q), .Q(sync1_q), .clk(clock_1_out));  // open: en, clr
  Register #(.width(1)) sample0 (.D(sync1_q), .en(enable_1ms), .Q(sample0_q), .clk(clock_1_out));  // open: clr
  Register #(.width(1)) sample1 (.D(sample0_q), .en(enable_1ms), .Q(sample1_q), .clk(clock_1_out));  // open: clr
  xor xor_1 (xor_1_out, sample0_q, sample1_q);
  Counter #(.max('h1f), .width(5)) counter (
    .load(xor_1_out), .D({5{1'b0}}), .count(enable_1ms), .carry(counter_carry), .clk(clock_1_out));  // open: Q, clr
  and and_1 (and_1_out, counter_carry, enable_1ms);
  Register #(.width(1)) state (.D(sample1_q), .en(and_1_out), .Q(Current), .clk(clock_2_out));  // open: clr
  Clock clock_2 (.out(clock_2_out));
  Register #(.width(1)) old (.D(Current), .en(enable_1ms), .Q(old_q), .clk(clock_3_out));  // open: clr
  Clock clock_3 (.out(clock_3_out));
  // Callout #(.dx(38), .dy(-17), .format("wrapped"), .halign("right"), .style("margin: 4px;"), .text("Note: including the 1ms pulse in the AND ensures that RisingEdge is high for only one clock cycle, coinciding with the 1ms pulse (in case other downstream components sample this signal on the same 1ms pulse)."), .textwidth(357), .valign("base")) callout_2: pin names not known
  and and_2 (RisingEdge, Current, ~old_q, enable_1ms);  // AND_Gate

  // Other names for the same wires on the sheet: _1ms = enable_1ms

  // Notes on the sheet:
  //   A button-debouncing circuit, using four registers:
  //   * sync0,1: input chain to resolve meta-stability issues.
  //   * sample0,1: the button input value sampled once per ms, higher 
  //     resolution isn't needed for user input.  
  //   * counter: resets to 0 when button input changes, counts upwards (once per 
  //     ms), while the input is stable (6 bit counter, so max is 31).
  //   * state: captures the button state when the counter overflows, i.e.
  //     when the the last 31ms of samples have been constant.
  //   * edge: the captured state from one clock tick ago, used to generate
  //     a short 1-cycle pulse whenever the captured state rises from 0 to 1,
  //     i.e. detecting the moment the button was pressed.
  //   changed
  //   stable for a while
  //   Current only changes at the end of
  //   clock cycles where enable_1ms was high.
  //   RisingEdge is high after
  //   Current goes high, during
  //   the next enable_1ms pulse.
endmodule

module HexDigitMultiplexer4 (
  input  [15:0] Input,
  input  refresh_1ms,
  output [3:0] MultiplexedNibble,
  output Digit_Enable_1,
  output Digit_Enable_2,
  output Digit_Enable_3,
  output Digit_Enable_4
);

  wire clock_1_out;
  wire [1:0] Counter_q;

  Counter #(.max('h3), .width(2)) Counter (
    .count(refresh_1ms), .Q(Counter_q), .clk(clock_1_out));  // open: load, D, carry, clr
  Clock clock_1 (.out(clock_1_out));
  Multiplexer #(.select(2), .width(4)) multiplexer_1 (
    .in0(Input[3:0]), .in1(Input[7:4]), .in2(Input[11:8]), .in3(Input[15:12]), .out(MultiplexedNibble),
    .sel(Counter_q));  // open: en
  Decoder #(.enable("false"), .select(2)) decoder_1 (
    .out0(Digit_Enable_4), .out1(Digit_Enable_3), .out2(Digit_Enable_2), .out3(Digit_Enable_1),
    .sel(Counter_q));
  // Callout #(.dx(-31), .dy(-17), .text("Counter cycles 0, 1, 2, 3, repeating forever.")) callout_1: pin names not known

  // Notes on the sheet:
  //   HexDigitMultiplexer4 takes a 16-bit hex value and drives a 4-digit HexDisplay by multiplexing the nibbles. It relies on an external refresh pulse to drive the display at a reasonable rate. Using a Timed Pulse generator set to approx 1ms is ideal. Somewhat faster or slower rates should be fine as well, but very slow rates may lead to visible flicker.
endmodule

module dir_to_vec (
  input  [1:0] dir,
  output RightOrDown
);


  assign RightOrDown = dir[1];

  // Notes on the sheet:
  //   00=Left
  //   01=Up
  //   10=Right
  //   11=Down
endmodule

module next_dir (
  input  [1:0] cur_dir,
  input  [3:0] LURD,
  output [1:0] next_dir
);

  PLA #(.in_width(6), .\table ("000100 01 # L+U=U\n000001 11 # L+D=D\n011000 00 # U+L=L\n010010 10 # U+R=R\n100100 01 # R+U=U\n100001 11 # R+D=D\n111000 00 # D+L=L\n110010 10 # D+R=R\n00xxxx 00 # L+?=L\n01xxxx 01 # U+?=U\n10xxxx 10 # R+?=R\n11xxxx 11 # D+?=D")) pla_1 (
    .in({cur_dir, LURD}), .out(next_dir));

  // Notes on the sheet:
  //   00=Left
  //   01=Up
  //   10=Right
  //   11=Down
endmodule

module segment_state (
  input  [4:0] SnakeLen,
  input  Arrive,
  input  tick,
  input  grow,
  input  clear,
  output Here,
  output Collision
);

  wire and_1_out, and_2_out, and_3_out, and_4_out, clock_1_out, comparator_1_eq, comparator_2_lt, or_1_out;
  wire [4:0] counter_1_q, multiplexer_1_out;

  Multiplexer #(.width(5)) multiplexer_1 (
    .in0(SnakeLen), .in1({5{1'b0}}), .out(multiplexer_1_out), .sel(clear));  // open: en
  or or_1 (or_1_out, clear, Arrive);
  and and_1 (and_1_out, or_1_out, tick);
  Counter #(.max('h1f), .width(5)) counter_1 (
    .load(and_1_out), .D(multiplexer_1_out), .count(and_2_out), .Q(counter_1_q), .up(1'b0), .clk(clock_1_out));  // open: carry, clr
  and and_2 (and_2_out, tick, ~grow, Here);  // AND_Gate
  Clock clock_1 (.out(clock_1_out));
  Comparator #(.mode("unsigned"), .width(5)) comparator_1 (
    .a({5{1'b0}}), .b(counter_1_q), .eq(comparator_1_eq));  // open: gt, lt
  Comparator #(.mode("unsigned"), .width(5)) comparator_2 (
    .a(5'b00001), .b(counter_1_q), .lt(comparator_2_lt));  // open: gt, eq
  not not_1 (Here, comparator_1_eq);
  and and_3 (and_3_out, Here, grow, Arrive);
  and and_4 (and_4_out, comparator_2_lt, Arrive);
  or or_2 (Collision, and_3_out, and_4_out);
endmodule

module digit_state (
  input  [4:0] SnakeLen,
  input  [2:0] ArriveSegment,
  input  ArriveEnable,
  input  tick,
  input  grow,
  input  clear,
  output [7:0] SegState,
  output Collision
);

  wire A_collision, B_collision, C_collision, D_collision, decoder_1_out0, decoder_1_out1, decoder_1_out2,
       decoder_1_out3, decoder_1_out4, decoder_1_out5, decoder_1_out6, decoder_1_out7, E_collision,
       F_collision, G_collision;

  Decoder #(.select(3)) decoder_1 (
    .out0(decoder_1_out0), .out1(decoder_1_out1), .out2(decoder_1_out2), .out3(decoder_1_out3),
    .out4(decoder_1_out4), .out5(decoder_1_out5), .out6(decoder_1_out6), .out7(decoder_1_out7),
    .sel(ArriveSegment), .en(ArriveEnable));
  segment_state A (
    .SnakeLen(SnakeLen), .Arrive(decoder_1_out0), .tick(tick), .grow(grow), .clear(clear),
    .Here(SegState[0]), .Collision(A_collision));
  segment_state B (
    .SnakeLen(SnakeLen), .Arrive(decoder_1_out1), .tick(tick), .grow(grow), .clear(clear),
    .Here(SegState[1]), .Collision(B_collision));
  segment_state C (
    .SnakeLen(SnakeLen), .Arrive(decoder_1_out2), .tick(tick), .grow(grow), .clear(clear),
    .Here(SegState[2]), .Collision(C_collision));
  segment_state D (
    .SnakeLen(SnakeLen), .Arrive(decoder_1_out3), .tick(tick), .grow(grow), .clear(clear),
    .Here(SegState[3]), .Collision(D_collision));
  segment_state E (
    .SnakeLen(SnakeLen), .Arrive(decoder_1_out4), .tick(tick), .grow(grow), .clear(clear),
    .Here(SegState[4]), .Collision(E_collision));
  segment_state F (
    .SnakeLen(SnakeLen), .Arrive(decoder_1_out5), .tick(tick), .grow(grow), .clear(clear),
    .Here(SegState[5]), .Collision(F_collision));
  segment_state G (
    .SnakeLen(SnakeLen), .Arrive(decoder_1_out6), .tick(tick), .grow(grow), .clear(clear),
    .Here(SegState[6]), .Collision(G_collision));
  or or_1 (Collision, A_collision, B_collision, C_collision, D_collision, E_collision, F_collision, G_collision);

  assign SegState[7] = 1'b0;

  // Notes on the sheet:
  //   DP
endmodule

module SevenSegmentMultiplexer4 (
  input  [7:0] Input4,
  input  [7:0] Input3,
  input  [7:0] Input2,
  input  [7:0] Input1,
  input  refresh_1ms,
  output [7:0] MultiplexedValue,
  output Digit_Enable_1,
  output Digit_Enable_2,
  output Digit_Enable_3,
  output Digit_Enable_4
);

  wire clock_1_out;
  wire [1:0] Counter_q;

  Clock clock_1 (.out(clock_1_out));
  Multiplexer #(.select(2), .width(8)) multiplexer_1 (
    .in0(Input4), .in1(Input3), .in2(Input2), .in3(Input1), .out(MultiplexedValue), .sel(Counter_q));  // open: en
  Counter #(.max('h3), .width(2)) Counter (
    .count(refresh_1ms), .Q(Counter_q), .clk(clock_1_out));  // open: load, D, carry, clr
  // Callout #(.dx(-31), .dy(-17), .text("Counter cycles 0, 1, 2, 3, repeating forever.")) callout_1: pin names not known
  Decoder #(.enable("false"), .select(2)) decoder_1 (
    .out0(Digit_Enable_4), .out1(Digit_Enable_3), .out2(Digit_Enable_2), .out3(Digit_Enable_1),
    .sel(Counter_q));

  // Notes on the sheet:
  //   SevenSegmentMultiplexer4 takes four 8-bit inputs and multiplexes these onto a 4-digit SevenSegement display. It relies on an external refresh pulse to drive the display at a reasonable rate. Using a Timed Pulse generator set to approx 1ms is ideal. Somewhat faster or slower rates should be fine as well, but very slow rates may lead to visible flicker.
endmodule

module press_any_button (
  input  reset,
  input  tick,
  output [31:0] splash
);

  wire and_1_out, clock_1_out, shift_register_1_p3;
  wire [5:0] counter_1_q;
  wire [7:0] rom_1_data;

  Counter #(.max('h3f), .width(6)) counter_1 (
    .load(reset), .D({6{1'b0}}), .count(tick), .Q(counter_1_q), .clk(clock_1_out));  // open: carry, clr
  Clock clock_1 (.out(clock_1_out));
  ROM #(.addrWidth(6)) rom_1 (.addr(counter_1_q), .data(rom_1_data));
  and and_1 (and_1_out, tick, ~reset);  // AND_Gate
  // Shift_Register #(.length(4), .width(8)) shift_register_1: pin names not known; wires that end beside it: and_1_out, rom_1_data, shift_register_1_p3, reset, {8{1'b0}}, splash[7:0], {8{1'b0}}, splash[15:8], {8{1'b0}}, splash[23:16], {8{1'b0}}, splash[31:24]
  Clock clock_2 (.out(shift_register_1_p3));

  // Notes on the sheet:
  //   contents of rom_1 (hex, n*v repeats v):
  //   8 8 c 42 1 1 7 8 8 c 40 40 44 8 c 40 42 1 3 40 42 1 5b 8 8 52 1 1 5b 8 8 8 73 50 79 6d 6d 0 77 54 6e
  //   0 7c 1c 78 78 5c 54 0 78 5c 0 6d 78 77 50 78 7*8
endmodule

module snake_clock (
  output tick_1ms,
  output tick_1s
);

  wire _1_ms_timer_p1, clock_2_out, clock_3_out, clock_4_out, clock_5_out, comparator_1_eq, register_1_q,
       tick, tick_1ms_t;
  wire [7:0] counter_1_q;
  wire [9:0] clkdiv_q;

  // TimedPulse #(.interval(1.0), .unit("ms")) _1_ms_timer: pin names not known; wires that end beside it: _1_ms_timer_p1, tick_1ms_t
  Clock clock_1 (.out(_1_ms_timer_p1));
  Clock clock_2 (.out(clock_2_out));
  Counter #(.max('h3ff), .width(10)) clkdiv (
    .load(tick), .D({10{1'b0}}), .count(tick_1ms_t), .Q(clkdiv_q), .clk(clock_2_out));  // open: carry, clr
  Comparator #(.mode("unsigned"), .width(10)) comparator_1 (
    .a(10'h190), .b(clkdiv_q), .eq(comparator_1_eq));  // open: gt, lt
  Register #(.width(1)) register_1 (.D(comparator_1_eq), .Q(register_1_q), .clk(clock_2_out));  // open: en, clr
  Counter counter_1 (.count(tick), .Q(counter_1_q), .clk(clock_3_out));  // open: load, D, carry, clr
  Clock clock_3 (.out(clock_3_out));
  and and_1 (tick, tick_1ms_t, register_1_q);
  // Probe on counter_1_q
  Clock clock_4 (.out(clock_4_out));
  Clock clock_5 (.out(clock_5_out));
  Register #(.width(1)) register_2 (.D(tick_1ms_t), .Q(tick_1ms), .clk(clock_4_out));  // open: en, clr
  Register #(.width(1)) register_3 (.D(tick), .Q(tick_1s), .clk(clock_5_out));  // open: en, clr

  // Notes on the sheet:
  //   (actually, 400ms)
endmodule
