// Logisim project audio-midi.circ as structural Verilog: 9 circuits, main circuit midi-in
module main (
);

  wire clock_1_out, clock_2_out, clock_3_out, midisink_1_p7, midisink_2_p7, playL, playR;
  wire [11:0] counter_1_q, counter_2_q;
  wire [15:0] Time_q;
  wire [31:0] rom_1_data, rom_2_data;

  Counter #(.max('hffff), .width(16)) Time (.Q(Time_q), .clk(clock_1_out));  // open: load, D, count, carry, clr
  Clock clock_1 (.out(clock_1_out));
  Comparator #(.mode("unsigned"), .width(16)) comparator_1 (
    .a(rom_1_data[31:16]), .b(Time_q), .lt(playL));  // open: gt, eq
  Comparator #(.mode("unsigned"), .width(16)) comparator_2 (
    .a(rom_2_data[31:16]), .b(Time_q), .lt(playR));  // open: gt, eq
  // Probe on rom_1_data[31:16]
  ROM #(.addrWidth(12), .dataWidth(32)) rom_1 (.addr(counter_1_q), .data(rom_1_data));
  Counter #(.max('hfff), .width(12)) counter_1 (
    .count(playL), .Q(counter_1_q), .clk(clock_2_out));  // open: load, D, carry, clr
  Clock clock_2 (.out(clock_2_out));
  // Probe on rom_2_data[31:16]
  ROM #(.addrWidth(12), .dataWidth(32)) rom_2 (.addr(counter_2_q), .data(rom_2_data));
  Counter #(.max('hfff), .width(12)) counter_2 (
    .count(playR), .Q(counter_2_q), .clk(clock_3_out));  // open: load, D, carry, clr
  Clock clock_3 (.out(clock_3_out));
  // Probe on rom_1_data[15]
  // Probe on rom_2_data[15]
  // Probe on rom_1_data[7:0]
  // Probe on rom_1_data[14:8]
  // Probe on rom_2_data[7:0]
  // Probe on rom_2_data[14:8]
  // MidiSink midisink_1: pin names not known; wires that end beside it: 4'b0001, rom_1_data[15], rom_1_data[7:0], rom_1_data[14:8], 8'h3, playL, midisink_1_p7
  Clock clock_4 (.out(midisink_1_p7));
  // MidiSink midisink_2: pin names not known; wires that end beside it: 4'b0010, rom_2_data[15], rom_2_data[7:0], rom_2_data[14:8], 8'h1, playR, midisink_2_p7
  Clock clock_5 (.out(midisink_2_p7));

  // Notes on the sheet:
  //   Demo of kahdeg's MIDI sound emitter.
  //   Set the clock frequency to 1kHz (or higher), reset the simulation, then enable the clock.  The left-hand and right-hand ROMs 
  //   contain MIDI data for each of the two tracks that make up the song, with each word containing: 
  //      16 bit timestamp, 1 bit on/off damper, 7 bit velocity, 8 bit note. 
  //   The original data was meant for 16kHz playback, but I divided the timestamps by 16 so that most of the song would
  //   would with fit before the 16 bit timestamps overflows and so the Logisim simulation clock could run slower.
  //   For each ROM, at the appointed time the note is put into a register that feeds one of the two MIDI sound emitters.
  //   contents of rom_1 (hex, n*v repeats v):
  //   compressed eJxFnNuh4yoMAP+pIiXEhIcoR4Dov4TFoDn7ZcVJHBu0c8Sge/tM8TNqGp/0fL87Pof3VZfzasT9
  //   Su575zDC+J73xneU/d5a571zGJ/Hv7iP+135PP7Ve5Swj/d9ec63n/G975/j+MTvt8/082N9j6On
  //   9Ynnvn7hHqu/Xp/ffj/vz//u+590vvd9j/t78knn/NePEtJ787/9fOfu9+ff+35fn/v/ffJ7f7/6
  //   Hvf7309+7+t9fe7vG8r7fPvz5Txf/pT3ud7X5/n263N9e4/7/fop5/p2j6mGer4/P/V8v3zq+f68
  //   x/v6XL/KvX49vz/uMeUg7/Pt13Ke7/eROM775/i+zmWP7zme8RW54yI+d6Jjv18/+7jfXx+Z+Yzn
  //   Pa5PO+Mn73H0/HzaHbd7zE9oZ/7yp537m59278uP5/W5fjvPv693n9uPK2i639d051993O5xvz7f
  //   /77Hkz96vvf1o4R+7u/59PP8+unn/h4/ntdn/Pu5fv30M752j3v8h+fH8PwYnh/Dn3N4fgzPj+H5
  //   MW5+hOn5MT0/pufHvPnxMc8P8/wwzw+7zxnM88M8P8zzw3yclufH8vxYnh/r5kdYnh/L82N5fiyf
  //   h/2pmyBvcDLk+XqK3GA/w/P1JHmD+6/w62niwXvGE+UNzkw+X08VD1Z4Hk+WNzjZ8jw+jDc4Zzxh
  //   nscz5nm41RvM8Ab3tx7Pmufx4fBgn4meOG9w7zl66ngwwhM9ed7g0id6+niwz/w8gd7gZNDz8xTy
  //   QMMbnEl6gzNLz8/T6AbvmXSea5zg3nNyhHmwx+fAJvVzZn9mf/1iphPsM/ncj55g388en+yp7MEe
  //   n3yevZ4z+zr765nbuMF75vyWnOCOT+aRb7DH58DrHY1Lr7QDuenvwT2zP/Oc4GTYU87jPAQ5PAdy
  //   b7YUxrk4Pj3YZ6r/Q3iq/0t4qv9TuMF7nQO799cv7d5v+T8jD+6Zez/1/NYelnp+4iHY8yXMhTAX
  //   wlzc4J65cyHMhTAXN7DwNOaiMReNubjBPXPnojEXjbm4Qd/XYS4ac9EYlsbfyQvCSbBOMEreU3BZ
  //   uOf9BsvPnLfOlSfBOsGI561z5UmwPMgpPBea+60brBPsf7D7W53n6v4H9QbvW4NRHXdUwzMY1cGo
  //   DkZ1MKqDUR1k+GRU5x3V8ExGdfLrk1GdjOpkVCcZPhnVeUd1X4dRnYyqkeFGhhsZbmS4keF2Mzw8
  //   RoYbaDIy3MhwI8ONH11k+GX1vs4iwxdoWmT4IsMXGb7I8EWGr5vh+zpk+A10V0HnOukEZ3zi93w9
  //   Eewzt/R6TnCuE2/R9Z6RO+Ax+p+/GP3vX4z+B9CDfQayRSfbrrkozpxsJzjzHiFbhGwRskXIFp1s
  //   IUI2D+YJzrxHyBYhW4RsEbJFJ9u+jk+BB/vGIFuEbBGyRcgWIVt0soUI2TzIJzjzHiFbhGwRskXI
  //   Fp1sIUK26GQ7wb0fyBYhW4RsEbJFJ9u+js+7B3ugIFuEbBGyRcgWIVt0soUI2TzYcwHZImSLkC1C
  //   tgjZopMtRMjmwb4gZIuQLUK2CNkiZPNg5w9ki042guXBecvJFiFbhGzRyRYiZItOtk+EbBGyRcgW
  //   IVuEbNHJFiJki4NRhWwRskXIFiFbhGwe7HGGbHEyqpAtQrYI2SJki5DNgz3OkC1ORhWyRcgWIVuE
  //   bBGyebCfC7JFJ9sOyHDIFiFbhGwRsnkgIUK26GTbARkO2SJki5AtQjYP3uuQ4U62HZDhkO0H2X6Q
  //   7QfZPOjhB9l+TrYdONl+kO0H2X6Q7QfZPJDwu4vDfeV3dVjfz9xlYSK4Z+79pLP2fc8InxGuc57r
  //   PfOm6PnMeZxEsM9krpN9JfzLXCdznbPY3EX+764291PcZWYh2GeKL4jfYD/X2IEvdT0Y4Qf9foXf
  //   gn4evGe8Nv5dsuUdeG3sQQ6/6muHNzhrh19Nd95v8J4RxlAYZ2EMhXEWnl0YQ+HZhfsRxlAYQ2EM
  //   xfPw17hO47ka12lcpzGGjTFsjOENNPya5/wPav2a5/wPav0GzzXIjcFzDZ5rcD+D5xrcz+B+Bs81
  //   eK7Bcw2ea3KdyXNNrjO5zuS5Js81ea7Jcxm5YeSGMU3mHucHN37Gb8END/b9GLlh5IaRGzfYZxa5
  //   sciNRW4sdzPprD1fa/T1+0lfrNIXr/TFLH3dLaWv8Blfx6WvG6Y3OPOVvm6ZPHj91J+h8udKqKaE
  //   a0rIpoRtSuimhG9KCKeEcUoop4RzSkinhHVKaKf0553+xNN/8/SnnnBPf/Lpzz796Sf8U0JAJQxU
  //   QkElHFRCQiUsVEJDJTxUQkQlTFRCRSVcVEJGJWxUQkclfFRCSCWMVEJJJZxUQkolrFRCSyW8VEJM
  //   JcxUQk0l3FRCTiXsVEJPJfxUQlAlDFVCUSUcVUJSJSxVQlMlPFVCVCVMVUJVJVxVQlYlbFVCVyV8
  //   VUJYJYxVQlklnFVCWiWsVUJbJbxVQlwlzFVCXSXcVUJeJexVQl8l/FVCYCUMVkJhJRxWQmIlLFZC
  //   YyU8VkJkJUxWQmUlXFZCZiVsVkJnJXxWQmgljFZCaSWcVkJqJaxWQmslvFbGa2W8VsZrZbxWxmtl
  //   vFbGa2W8VsZrZbxWxmtlvFZ+PMfe4ORYxmtlvFbGa2W8VsZrZbxWxmtlvFbGa2W8VsZrZbxWxmtl
  //   vFbGa2W8VsZrZbxWxmtlvFbGa2W8VsZrZbxWxmtlvFZOPHtyhmdKIw/2/STuOTl7c+KevUbaAfcM
  //   63Linp11IWevIfNlXdqBp58H+0zhuW79s3+i8Fw3yCHf+kfOmTsXlD0evGe8xs6Xh+8Zhq74+iJX
  //   fqvyW5XfusE+I/73Il/WvTsFjjgPasiXdfsnDuvebBFu4wTnzMnDeYK9zHnPnPSbHmyO5earmwzr
  //   cjs/MT04Z85vjRPcHGuk+g12PrfzWzsl2sn59+vnt5Rgn1HmXZl3Zd6VeYeHWZl3eOjBe8Zr/qxe
  //   S2T1mt+DPV/dOZY7/5a7c8yD39lvufczuB8Q58G+n8H9DO5ncD/UY3mQh/AwD/IQHuZJHk7yEAx6
  //   sM8YuWHkhpEbRh4aeWjkoXEbRgIYeWjkIULJg52Hi99a/Nbit5bnYfl6Hpav52H5+tB5UEO5tZae
  //   M+e3yteXSx68Z8796Al2Pfae8aWZBzOUx9e55fF1bnlOHirBe+bkoZzgcKx4GUYw9nWcvW9watry
  //   OHs92GeoxwrruBJ5LtZxbzDe2SnRS9nygvEGPrnlVGjvxtzPy9QC2YqTLRTI5sE4wcmoAtkKZCuQ
  //   rUC24mTb1+FHqeIKZCuQrUC2AtkKZCtOtlAgmwf5BHdUIVuBbAWyFchWnGz7Op5RHuzPQLYC2Qpk
  //   K5CtQLbiZAsFsnmwpwmyFchWIFuBbAWyFSfbvo5DpjjZPgWyFchWIFuBbAWyFSdbKJDNg7UDJ1uB
  //   bAWyFchWIFtR5h2yeTBOcOcdshXIViBbgWzFybav42TzYH8YshXIViBbgWwFspXB/UA2D8YJ7v1A
  //   tgLZCmQrkK0M8hCyebB/C7IVyFYgW4FsBbIVIw8hmwf5BDfHIFuBbAWyFchWjDyEbB7sz0C2AtkK
  //   ZCuQrUK26mQLFbJ5UE9w5r1CtgrZKmSrkK062fZ1nGwe7M9AtgrZKmSrkK1CtupkCxWyeTB24GSr
  //   kK1CtgrZKmSrTrZQIVvFvVfIViFbhWwVslXIVp1soeK1Kl6r4rUqiKt4rYrXqnititeqeK2K16p4
  //   rYrXqnititeqeK2K16p4rYrXqnititeqeK2K16p4rYrXqnititeqeK0KBiteq+K1Kl6r4rUqXqvi
  //   tSpeq+K1Kl6r4rUqXqvitSpeq+K1Kl6r4rUqXqvitSpeq+K1Kl6r4rUqXqvitSpeq+K1Kl6r4rUq
  //   XqvitSpeq+K1Kl6r4rUqXqvitSpeq+K1Kl6rQpuK16p4rYrXqnititeqeK2K16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
  //   contents of rom_2 (hex, n*v repeats v):
  //   compressed eJxFmduB7CAMQ/+pIiUEwsOUw8P0X8JlwGfvV9iZDARLkYR3pC880b/vuYzfRe5f4z1/rXX+8val
  //   v9+6fb1/j/d8/73vSF95vjNXeaL9Hfn7TBefeOaLLp3fv086v3+ffOZPTz7z7+u5vzz53F+ecr7P
  //   TznfZ1fk3l/O79MjZ734SBi/+R9Je4ZvPHLu39c2xhvfR2Z699XV3/3RP/X3fL/rmU+feuY713N/
  //   /a2/r+2sP55253PtPF992nm++vSzfn/62e+5nufvcvc/rB7j1sMNq8e49Xim1WNaPdTqoVYPtXro
  //   rYdbVo916/G7nvuX1WN/egviX6uIf60k/rU9+NeK4t9blcd7K4v3VhfvrTDeW2V+g/srf2vjfLDi
  //   +GDV9sHK44PVx39WIP9ZhX6DsyX/3Ro5f0mzZ76s+Q1s2z4aD/wlzl7iMmcP8vnV3nI+v0rOX/L8
  //   vjq/2oNy7vkNoj0hBPIwyAury119c9xA8mIo+UuT/RiXJ3dw16qs1bmn33ucH8w82NdgX4N9TfY1
  //   2ZeyL2VfylrKWot9LfYFETxMCK+tHl7bV3jPPbI/OffswX292x4cLPYg2Mwh2Mwh2DOHYBwMvPSB
  //   tz58RuPwGY8DmAYwDWAaIvOAaQDTAKbBMN0D23sA0wCmwTB1AUwDmAYwDcLqYBrANIBpMExdANMA
  //   pgFMg2H6BDANYBrANAz2BaYBTAOYBmVfYBrANIBpWOwLTAOYfmD6GaZ7YJh+YPqB6WeYug9MPzD9
  //   wPQzTJ/vT8jB9APTzzB138E07J8fTM/gzPPtwZlnDxLPk3iezMzZNPC7mO6ZL6Z7cBAMfQ9+v/oN
  //   hLWEtYS1LoKf+yprVdZqrNXYRWOtxlqdtfpdy32DtQZrDdYa7Guy1mQtZS1lX8paylqLtZbtK14E
  //   t+m+uO9rFhtf89j4mgfH11w4YsPRfPgMBuZ9PwHBaAi6+N+MceM/OzY/fiKGHHHkiCVH82QXMeWI
  //   K0dsOZovn8H9Fe9gxJqjebOLmHPEnSP2HM2fn4hBRxw6YtHRPNpFTDri0hGbjo2ZMeqIU0esOppX
  //   u4hZR9w6Ytdx/OUXKoZjRyw7mme7iGlHXDti21GpGMYdce7I2x3t7XYJ7054d8K7k3n3HljFEt6d
  //   8O5k3u0S3p3w7oR3J/PuJ+HdCe9OeHcy73YJ7054d8K7k3n3k9D5hM6ny7G8B2ee7FKyqqZkVU0o
  //   f0L5E8qfUP6UrT6/Etz6oPwJN0+FXRR2AQ8TPExib1y6XhB2Bj1P+PvqPOEeVJ6w8oSXdXvLl3V7
  //   gLYk0xaXmrlDauYOqfOEnSfsPGHnCfGURE5IeErCU9Kghpd1ezBZffKEuEwyl3EJl0m4TFKqoVQD
  //   l0kkh7R4wmX5MMHMhO/k11bPr62eX4L6awzPnnv8YW9x2R/21v3Jmfk3+LF3FzP7H3t/A7wp4005
  //   WH1ysPrkz+qTP6tPhnU5/n1iFcvGuifDumyscxnWZViXYV2GdRnW5czeYV0mb2RYl2FdhnUZ1mVY
  //   l411e2Csy8Y6l2FdhnUZ1mVYl2FdxtEyrMuN+sC6DOsyrMuwLsO6TJLJsC4b61yGdRnWZViXYV2G
  //   dZlsk2FdJq9mWJdhXYZ1GdZlWJcXTwjrMnpYYF2BdQXWFVhXYF0x1u2Bsa4Y61yBdQXWFVhXYF2B
  //   dcVY9xRYV4x1rpB/CvmnkH8K+aeQfwr5p5B/CvmnkH8K+aeQfwr5p5B/CvmnkH8K+aeQfwr5p8CW
  //   AlsK+aeQfwr5p5B/CvmnkH8K+aeQfwr5p5B/CvmnkH8K+aeQfwr5p5B/hPwj5B8h/wj5R8g/Qv4R
  //   /9ejsPwj5B8h/wj5R8g/gkoIKiGohKASgkoI3iSohJhKOEElBJUQVEJQCUElBG8SVEJMJZygEvLX
  //   vUAlBJUQVELwJkElpLIvVEJQCQF3AXdBJQRvElRCTCWcoBKCSggqIaiEoBKCNwkqIaYSTlAJQSUE
  //   lRBUQlAJwZsElRBTCSeohKASgkoIKiGohOBNFZWophKuohIVlaioREUlKipR8aaKSlRTCVdRiYpK
  //   VFSiohIVlah4UyV118jzkLorqbuSuiupu5K6K52wSuqulrpdJXVXUneFURVGVVJ3pSNWSd3VUrer
  //   pO5K6q5/bbG/vthfY+yvM/bXGrPU7Sqpu5K6K6m7krorqbvSIauk7mqp21VSdyV1V1J3JXVXUnel
  //   U1ZJ3dVSt6uk7krqrqTuSuqu8KfCn0bqbpa6XSN1N1J3I3U3UncjdTc6Zo3U3Sx1u0bqbqTuRupu
  //   pO5G6m50zBqpu1nqdo3U3UjdDWVrKFuju9LomDV0rKFjDR1r6Fiju9LorjR0rKFjDY4145hrdFca
  //   3ZVGd6XRXWl0Vxods0Z3pVl3xTXUpqE2DbVpqE2ju9LomDW0pZF7G9rS0JZGd6XRXWloS0NbGkxo
  //   5I1Od6XTXel0VzrdlU53pdMx66hEN5Vwne5Kp7vS8aZOd6XTXel0zDqYdsPUdTDtYNrBtJNgO5h2
  //   MO1g2g1T18G0g2kH045udDDtYNrBtBumroNpB9MOpp2OWQfTDqYdTDs5s4NpB9MOph2/6GDawbSD
  //   aVf2BaYdTDuYdt7uAaYDTAeYDsPUDTAdYDrAdKD8A0wHmA4wHeSNAaYDTAeJcZAYB4lxkBgHiXEk
  //   nofEOCwx7oElq0FiHCTGQWIcJMZhidENEuMQ1iIxDhLjIDkMksMgMQ5LjG6QGEdnLRLjIDEOEuMg
  //   MQ4S45jsi8Q4lLVIjIPEOEiMg8Q4SYzTEqObJMZpiXEPLDFOEuMkMU4S4yQxTkuMboLg5K2cePeM
  //   f5/YWzDx7ol3T/NuN/HuiXdPvHvSMZt498S7J+/gRFcn3j3x7ol3TzpmE++eePfEu6d5t5t498S7
  //   J9496ZhNvHvi3RPvnubdbuLdE++eePekYzbx7ol3T7x7mne7+fdPLrx74t2TjtnEuyfePfHuad7t
  //   Jm/35O1WvFvpmCnerXi34t1q3u0U71a8W/FupWOmeLfi3Yp3q3m3U7xb8W7Fu5WOmeLdincrOq/o
  //   vHIqUU4lyqlEOZUoyq8ov6L8yv+/lFOJcipRlF9RfuVUovQuFB4qPFROJcqpRDmVKKcS5VSi9C6U
  //   U4naqcQp2qJoi3IqUU4lyqlE6V0opxLt1BlPUTxF8RQlJyinEqV3oZxK1E4lTnEZxWUUl1FcRjmV
  //   KL0LxWWU/8sopxLlVKIwU2Hm4lSy6F0sTiXr5X+5nEoWp5LFqWRxKlmcSha9i4U3LfLG4lSyOJUs
  //   TiWLU8mCdSv+fWIVW/RpF6xbsG7BugXrFqxb5I0F6xZ92gXrFqxbsG7BugXrFglkwbpFn3bBugXr
  //   FqxbsG7BusVZeMG6RZ92wboF6xasW7BuwbrFWXjBukWfdsG6BesWrFuwbsG6xVl4wbpFXl2wbsG6 BesWrFvrd9f7un/KV8uw
endmodule

module midi_out (
  input  in_1,
  input  [6:0] in_2,
  input  in_3
);

  wire and_1_out, button_1_out, clock_1_out, clock_2_out, d_ff_1_qn, midisink_1_p7, or_1_out;
  wire [4:0] undriven;
  wire [7:0] adder_1_out, bit_extender_1_out;

  Random #(.width(5)) random_1 ();  // open: clk, next, out, clr
  Clock clock_1 (.out(clock_1_out));
  assign bit_extender_1_out = {{3{1'b0}}, undriven};  // Bit_Extender bit_extender_1
  Button button_1 (.out(button_1_out));
  Adder adder_1 (.a(bit_extender_1_out), .b(8'h40), .out(adder_1_out));  // open: cin, cout
  Clock clock_2 (.out(clock_2_out));
  D_Flip_Flop d_ff_1 (.clk(clock_2_out), .D(button_1_out), .Qn(d_ff_1_qn));  // open: Q, preset, reset
  // Probe on in_1
  and and_1 (and_1_out, d_ff_1_qn, button_1_out);
  // Probe on adder_1_out
  // Probe on in_2
  or or_1 (or_1_out, and_1_out, in_3);
  // MidiSink #(.hold(50)) midisink_1: pin names not known; wires that end beside it: 4'b0001, in_1, adder_1_out, in_2, 8'h1, or_1_out, midisink_1_p7
  Clock clock_3 (.out(midisink_1_p7));
endmodule

module midi_parallell (
  input  in_1
);

  wire clock_1_out, midisink_1_p3;
  wire [6:0] counter_1_q;
  wire [7:0] bit_extender_1_out, midisink_1_p1;

  Counter #(.max('h7f), .width(7)) counter_1 (.Q(counter_1_q), .clk(clock_1_out));  // open: load, D, count, carry, clr
  Clock clock_1 (.out(clock_1_out));
  assign bit_extender_1_out = {{1{1'b0}}, counter_1_q};  // Bit_Extender bit_extender_1
  // MidiSink #(.\interface ("parallel4")) midisink_1: pin names not known; wires that end beside it: {midisink_1_p1, 8'h40, bit_extender_1_out, 8'h91}, in_1, midisink_1_p3
  Clock clock_2 (.out(midisink_1_p3));
endmodule

module midi_serial (
  input  in_1
);

  wire clock_1_out, clock_2_out, midisink_1_p3;
  wire [1:0] counter_2_q;
  wire [6:0] counter_1_q;
  wire [7:0] bit_extender_1_out, multiplexer_1_out;

  Counter #(.max('h7f), .width(7)) counter_1 (.Q(counter_1_q), .clk(clock_1_out));  // open: load, D, count, carry, clr
  Clock clock_1 (.out(clock_1_out));
  assign bit_extender_1_out = {{1{1'b0}}, counter_1_q};  // Bit_Extender bit_extender_1
  Clock clock_2 (.out(clock_2_out));
  Multiplexer #(.enable("false"), .select(2), .width(8)) multiplexer_1 (
    .in0(8'h91), .in1(bit_extender_1_out), .in2(8'h40), .in3({8{1'b0}}), .out(multiplexer_1_out),
    .sel(counter_2_q));
  Counter #(.max('h3), .width(2)) counter_2 (.Q(counter_2_q), .clk(clock_2_out));  // open: load, D, count, carry, clr
  // MidiSink #(.\interface ("serial")) midisink_1: pin names not known; wires that end beside it: multiplexer_1_out, in_1, midisink_1_p3
  Clock clock_3 (.out(midisink_1_p3));
endmodule

module midi_in (
);

  wire clock_1_out, midiin_1_p1, midiin_1_p4;

  Clock clock_1 (.out(clock_1_out));
  // Probe on midiin_1_p1
  // MidiIn midiin_1: pin names not known; wires that end beside it: midiin_1_p1, midiin_1_p1, clock_1_out, midiin_1_p4
  // Probe on midiin_1_p4
  // MidiSink #(.\interface ("serial")) midisink_1: pin names not known; wires that end beside it: midiin_1_p4, midiin_1_p1, clock_1_out
endmodule

module midi_in_parallel4 (
);

  wire clock_1_out, midiin_1_p1, midiin_1_p4;

  Clock clock_1 (.out(clock_1_out));
  // Probe on midiin_1_p1
  // MidiIn #(.\interface ("parallel3")) midiin_1: pin names not known; wires that end beside it: midiin_1_p1, midiin_1_p1, clock_1_out, midiin_1_p4
  // Probe on midiin_1_p4
  // MidiSink #(.\interface ("parallel3")) midisink_1: pin names not known; wires that end beside it: midiin_1_p4, midiin_1_p1, clock_1_out
endmodule

module midi_in_parallel3 (
);

  wire clock_1_out, midiin_1_p1, midiin_1_p4;

  Clock clock_1 (.out(clock_1_out));
  // Probe on midiin_1_p1
  // MidiIn #(.\interface ("parallel3")) midiin_1: pin names not known; wires that end beside it: midiin_1_p1, midiin_1_p1, clock_1_out, midiin_1_p4
  // Probe on midiin_1_p4
  // MidiSink #(.\interface ("parallel3")) midisink_1: pin names not known; wires that end beside it: midiin_1_p4, midiin_1_p1, clock_1_out
endmodule

module midi_in_logisim5 (
);

  wire clock_1_out, midiin_1_p1, midiin_1_p4, midiin_1_p5, midiin_1_p6, midiin_1_p7, midiin_1_p8;

  Clock clock_1 (.out(clock_1_out));
  // Probe on midiin_1_p1
  // MidiIn #(.\interface ("logisim5")) midiin_1: pin names not known; wires that end beside it: midiin_1_p1, midiin_1_p1, clock_1_out, midiin_1_p4, midiin_1_p5, midiin_1_p6, midiin_1_p7, midiin_1_p8
  // Probe on midiin_1_p4
  // Probe on midiin_1_p5
  // Probe on midiin_1_p6
  // Probe on midiin_1_p7
  // Probe on midiin_1_p8
  // MidiSink midisink_1: pin names not known; wires that end beside it: midiin_1_p4, midiin_1_p5, midiin_1_p6, midiin_1_p7, midiin_1_p8, midiin_1_p1, clock_1_out
endmodule

module midi_in_logisim1 (
);

  wire clock_1_out, midiin_1_p1, midiin_1_p4;

  Clock clock_1 (.out(clock_1_out));
  // Probe on midiin_1_p1
  // MidiIn #(.\interface ("logisim1")) midiin_1: pin names not known; wires that end beside it: midiin_1_p1, midiin_1_p1, clock_1_out, midiin_1_p4
  // Probe on midiin_1_p4
  // MidiSink #(.\interface ("logisim1")) midisink_1: pin names not known; wires that end beside it: midiin_1_p4, midiin_1_p1, clock_1_out
endmodule
