// Logisim project bounce.circ as structural Verilog: 1 circuit, main circuit main
module main (
);

  wire bounce, clk, comparator_1_eq, comparator_2_eq, decoder_1_out0, decoder_1_out1, decoder_1_out2,
       decoder_1_out3, decoder_1_out4, decoder_1_out5, decoder_1_out6, decoder_1_out7, decoder_1_out8,
       decoder_1_out9, decoder_1_out10, decoder_1_out11, decoder_1_out12, decoder_1_out13, decoder_1_out14,
       decoder_1_out15, hitBottom, hitTop, or_1_out, register_1_q, saturatingadder_1_p3;
  wire [3:0] position_q_2, subtractor_1_out;
  wire [11:0] position_q;
  wire [12:0] adder_1_out, divider_1_out, divider_2_out, gravity, multiplexer_1_out, multiplexer_2_out,
       multiplexer_3_out, saturatingnegator_1_p2, saturatingsubtractor_1_p3, velocity;
  wire [15:0] fitrange_1_p1;
  wire [16:0] bit_extender_1_out, saturatingadder_1_p2;

  Clock clock_1 (.out(clk));
  Register #(.width(16)) position (.D(fitrange_1_p1), .Q({position_q_2, position_q}), .clk(clk));  // open: en, clr
  Subtractor #(.width(4)) subtractor_1 (.a(4'b1111), .b(position_q_2), .out(subtractor_1_out));  // open: bin, bout
  Comparator #(.width(16)) comparator_1 (
    .a({position_q_2, position_q}), .b({16{1'b1}}), .eq(comparator_1_eq));  // open: gt, lt
  Comparator #(.width(16)) comparator_2 (
    .a({position_q_2, position_q}), .b({16{1'b0}}), .eq(comparator_2_eq));  // open: gt, lt
  Register #(.width(13)) u_velocity (.D(multiplexer_3_out), .Q(velocity), .clk(clk));  // open: en, clr
  assign bit_extender_1_out = {{4{velocity[12]}}, velocity};  // Bit_Extender bit_extender_1
  // SaturatingAdder #(.mode("twosComplement"), .width(17)) saturatingadder_1: pin names not known; wires that end beside it: bit_extender_1_out, saturatingadder_1_p2, saturatingadder_1_p3, saturatingadder_1_p3
  assign saturatingadder_1_p2 = {{1{1'b0}}, {position_q_2, position_q}};  // Bit_Extender bit_extender_2
  Divider #(.width(13)) divider_1 (.a(gravity), .b(13'ha), .out(divider_1_out));  // open: upper, rem
  // FitRange #(.normalization("cap"), .typeIn("twosComplement"), .typeOut("unsigned"), .widthIn(17), .widthOut(16)) fitrange_1: pin names not known; wires that end beside it: fitrange_1_p1
  Decoder #(.enable("false"), .select(4)) decoder_1 (
    .out0(decoder_1_out0), .out1(decoder_1_out1), .out2(decoder_1_out2), .out3(decoder_1_out3),
    .out4(decoder_1_out4), .out5(decoder_1_out5), .out6(decoder_1_out6), .out7(decoder_1_out7),
    .out8(decoder_1_out8), .out9(decoder_1_out9), .out10(decoder_1_out10), .out11(decoder_1_out11),
    .out12(decoder_1_out12), .out13(decoder_1_out13), .out14(decoder_1_out14), .out15(decoder_1_out15),
    .sel(subtractor_1_out));
  or or_1 (or_1_out, comparator_1_eq, comparator_2_eq);
  // SaturatingSubtractor #(.mode("twosComplement"), .width(13)) saturatingsubtractor_1: pin names not known; wires that end beside it: velocity, divider_1_out, saturatingsubtractor_1_p3
  DotMatrix #(.dotshape("circle"), .inputtype("row"), .matrixcols(1), .matrixrows(16)) dotmatrix_1 (
    .row0(decoder_1_out0), .row1(decoder_1_out1), .row2(decoder_1_out2), .row3(decoder_1_out3),
    .row4(decoder_1_out4), .row5(decoder_1_out5), .row6(decoder_1_out6), .row7(decoder_1_out7),
    .row8(decoder_1_out8), .row9(decoder_1_out9), .row10(decoder_1_out10), .row11(decoder_1_out11),
    .row12(decoder_1_out12), .row13(decoder_1_out13), .row14(decoder_1_out14), .row15(decoder_1_out15));
  and and_1 (hitTop, comparator_1_eq, ~register_1_q);  // AND_Gate
  Register #(.width(1)) register_1 (.D(or_1_out), .Q(register_1_q), .clk(clk));  // open: en, clr
  and and_2 (hitBottom, ~register_1_q, comparator_2_eq);  // AND_Gate
  Divider #(.width(13)) divider_2 (.a(saturatingsubtractor_1_p3), .b(13'h4), .out(divider_2_out));  // open: upper, rem
  // SaturatingNegator #(.mode("twosComplement"), .width(13)) saturatingnegator_1: pin names not known; wires that end beside it: saturatingsubtractor_1_p3, saturatingnegator_1_p2
  Adder #(.width(13)) adder_1 (.a(divider_2_out), .b(saturatingnegator_1_p2), .out(adder_1_out));  // open: cin, cout
  Button w (.out(bounce));
  // Dial #(.mode("twosComplement"), .width(13)) dial_1: pin names not known; wires that end beside it: gravity
  Multiplexer #(.width(13)) multiplexer_1 (
    .in0(saturatingsubtractor_1_p3), .in1(adder_1_out), .out(multiplexer_1_out), .sel(hitBottom));  // open: en
  Multiplexer #(.width(13)) multiplexer_2 (
    .in0(multiplexer_1_out), .in1(gravity), .out(multiplexer_2_out), .sel(bounce));  // open: en
  Multiplexer #(.width(13)) multiplexer_3 (
    .in0(multiplexer_2_out), .in1({13{1'b0}}), .out(multiplexer_3_out), .sel(hitTop));  // open: en

  // Notes on the sheet:
  //   User inputs:
  //    w - accelerate ball upwards
  //    gravity - how fast the ball accelerates
  //   How to play:
  //   * Set clock to around 32Hz, enable auto-ticks
  //   * Set gravity to slightly positive
  //   * Press 'w' button, or type 'w' to make
  //     the ball bounce
  //   position is in range [0, 65535]
  //   but displayed in range [0, 15]
  //   velocity is in range [-2048, 2047]
endmodule
