// Logisim project digital-clock.circ as structural Verilog: 1 circuit, main circuit main
module main (
);

  wire a, b, c, clock_1_out, d, e, f, g, h, i, j, k, l;
  wire [3:0] binary_to_bcd_converter_1_p2, binary_to_bcd_converter_1_p3, binary_to_bcd_converter_2_p2,
       binary_to_bcd_converter_2_p3, binary_to_bcd_converter_2_p4, binary_to_bcd_converter_3_p2,
       binary_to_bcd_converter_3_p3, binary_to_bcd_converter_4_p2, binary_to_bcd_converter_4_p3,
       binary_to_bcd_converter_4_p4, binary_to_bcd_converter_5_p2, binary_to_bcd_converter_5_p3,
       bit_extender_2_out;
  wire [5:0] divider_1_out, hh, mm, ss;
  wire [7:0] yy;
  wire [8:0] dd;
  wire [31:0] divider_2_out, divider_2_rem, divider_3_out, divider_3_rem, divider_4_out, divider_4_rem,
       divider_5_out, divider_5_rem, realtimeclock_1_p2;

  LED led_1 (.in(j));
  Clock clock_1 (.out(clock_1_out));
  LED led_2 (.in(l));
  LED led_3 (.in(k));
  LED led_4 (.in(i));
  LED led_5 (.in(h));
  // RealTimeClock realtimeclock_1: pin names not known; wires that end beside it: clock_1_out, realtimeclock_1_p2
  Divider #(.mode("unsigned"), .width(6)) divider_1 (.a(ss), .b(6'b000101), .out(divider_1_out));  // open: upper, rem
  LED led_6 (.in(a));
  LED led_7 (.in(b));
  LED led_8 (.in(f));
  LED led_9 (.in(g));
  Divider #(.mode("unsigned"), .width(32)) divider_2 (
    .a(realtimeclock_1_p2), .b(32'h3c), .out(divider_2_out), .rem(divider_2_rem));  // open: upper
  Bit_Extender #(.in_width(32), .out_width(6), .\type ("zero")) bit_extender_1 (.in(divider_2_rem), .out(ss));
  Decoder #(.enable("false"), .select(4)) decoder_1 (
    .out0(a), .out1(b), .out2(c), .out3(d), .out4(e), .out5(f), .out6(g), .out7(h), .out8(i), .out9(j),
    .out10(k), .out11(l), .sel(bit_extender_2_out));  // open: out12, out13, out14, out15
  Bit_Extender #(.in_width(6), .out_width(4)) bit_extender_2 (.in(divider_1_out), .out(bit_extender_2_out));
  LED led_10 (.in(c));
  LED led_11 (.in(d));
  LED led_12 (.in(e));
  Divider #(.mode("unsigned"), .width(32)) divider_3 (
    .a(divider_2_out), .b(32'h3c), .out(divider_3_out), .rem(divider_3_rem));  // open: upper
  Bit_Extender #(.in_width(32), .out_width(6), .\type ("zero")) bit_extender_3 (.in(divider_3_rem), .out(mm));
  Divider #(.mode("unsigned"), .width(32)) divider_4 (
    .a(divider_3_out), .b(32'h18), .out(divider_4_out), .rem(divider_4_rem));  // open: upper
  Hex_Digit_Display hex_digit_display_1 (.value(binary_to_bcd_converter_1_p2));  // open: dp
  Hex_Digit_Display hex_digit_display_2 (.value(binary_to_bcd_converter_1_p3));  // open: dp
  // Binary_to_BCD_converter #(.width(6)) binary_to_bcd_converter_1: pin names not known; wires that end beside it: hh, binary_to_bcd_converter_1_p2, binary_to_bcd_converter_1_p3
  Hex_Digit_Display hex_digit_display_3 (.value(binary_to_bcd_converter_2_p2));  // open: dp
  Hex_Digit_Display hex_digit_display_4 (.value(binary_to_bcd_converter_2_p3));  // open: dp
  // Binary_to_BCD_converter #(.width(8)) binary_to_bcd_converter_2: pin names not known; wires that end beside it: yy, binary_to_bcd_converter_2_p2, binary_to_bcd_converter_2_p3, binary_to_bcd_converter_2_p4
  Bit_Extender #(.in_width(32), .out_width(6), .\type ("zero")) bit_extender_4 (.in(divider_4_rem), .out(hh));
  Hex_Digit_Display hex_digit_display_5 (.value(binary_to_bcd_converter_2_p4));  // open: dp
  Bit_Extender #(.in_width(32), .out_width(8), .\type ("zero")) bit_extender_5 (.in(divider_5_out), .out(yy));
  Divider #(.mode("unsigned"), .width(32)) divider_5 (
    .a(divider_4_out), .b(32'h16d), .out(divider_5_out), .rem(divider_5_rem));  // open: upper
  Bit_Extender #(.in_width(32), .out_width(9), .\type ("zero")) bit_extender_6 (.in(divider_5_rem), .out(dd));
  Hex_Digit_Display hex_digit_display_6 (.value(binary_to_bcd_converter_3_p2));  // open: dp
  Hex_Digit_Display hex_digit_display_7 (.value(binary_to_bcd_converter_3_p3));  // open: dp
  // Binary_to_BCD_converter #(.width(6)) binary_to_bcd_converter_3: pin names not known; wires that end beside it: mm, binary_to_bcd_converter_3_p2, binary_to_bcd_converter_3_p3
  Hex_Digit_Display hex_digit_display_8 (.value(binary_to_bcd_converter_4_p2));  // open: dp
  // Binary_to_BCD_converter binary_to_bcd_converter_4: pin names not known; wires that end beside it: dd, binary_to_bcd_converter_4_p2, binary_to_bcd_converter_4_p3, binary_to_bcd_converter_4_p4
  Hex_Digit_Display hex_digit_display_9 (.value(binary_to_bcd_converter_5_p2));  // open: dp
  // Binary_to_BCD_converter #(.width(6)) binary_to_bcd_converter_5: pin names not known; wires that end beside it: ss, binary_to_bcd_converter_5_p2, binary_to_bcd_converter_5_p3
  Hex_Digit_Display hex_digit_display_10 (.value(binary_to_bcd_converter_4_p3));  // open: dp
  Hex_Digit_Display hex_digit_display_11 (.value(binary_to_bcd_converter_5_p3));  // open: dp
  Hex_Digit_Display hex_digit_display_12 (.value(binary_to_bcd_converter_4_p4));  // open: dp

  // Notes on the sheet:
  //   Tick the clock (or turn on auto-ticks) to see this demo.
  //   seconds
  //   hours
  //   years
  //   minutes
  //   seconds
  //   days
endmodule
