// Logisim project gates.circ as structural Verilog: 6 circuits, main circuit Common Gates - Basics
module NOT_Gate_Demo (
  input  in_1,
  input  [3:0] in_2,
  input  in_3,
  output out_4,
  output [3:0] out_5,
  output out_6
);

  wire not_1_out, not_4_out, not_5_out, not_6_out;

  // Callout #(.dx(40), .dy(40), .halign("center"), .style("margin: 4px;"), .text("input"), .valign("base")) callout_1: pin names not known
  not not_1 (not_1_out, in_3);
  not not_2 (out_4, in_1);
  assign out_5 = ~in_2;  // NOT_Gate not_3, 4 bits wide
  not not_4 (not_4_out, not_1_out);
  not not_5 (not_5_out, not_4_out);
  // Callout #(.dx(-31), .dy(41), .halign("center"), .style("margin: 4px;"), .text("ouput"), .valign("base")) callout_2: pin names not known
  // Callout #(.dx(-62), .dy(41), .halign("center"), .style("margin: 4px;"), .text("4-bit NOT gate"), .valign("base")) callout_3: pin names not known
  not not_6 (not_6_out, not_5_out);
  xor xor_1 (out_6, in_3, not_6_out);

  // Notes on the sheet:
  //   NOT Gate
  //   A NOT gate by default emits the complement of whatever input it receives. So it outputs a 1 when the input
  //   is 0, and it outputs a 0 when the input is 1.
  //   If the input is not connected, or has an error (E) or floating (X) value, then the output will be an error. This default
  //   behavior can be summarized with the truth table above.
  //   Multi-bit NOT Gate
  //   A multi-bit NOT gate performs the same transformation as a bitwise operation, with each output bit
  //   determined by the corresponding input bit.
  //   High-impedance Output Modes
  //   Instead of the default behavior described above, a NOT gate can be configured in special high-impedance output modes:
  //   * If the output behavior is set to "0/floating", it behaves in "open-collector" (a.k.a. "open-drain") inverter mode, 
  //   where output is either 0 (when the input is 1) or floating (when the input is 0). 
  //   * If the output behavior is set to "floating/1", the output is either floating (when the input is 1) or 0 (when the input is 1).
  //   When combined with pull-up or pull-down resistors, these modes can be used to create a circuit similar to a "wired-AND"
  //   or "wired-OR". See example circuits below.
  //   NOT Gate Attributes
  //   Facing - Used to rotate the gate. You can also rotate the gate using arrow keys (up/down/left/right).
  //   Data Bits - The width, in bits, of the gate's input and output.
  //   Gate Size - Used to select a wide or narrow symbol.
  //   Output Value - Configures the output behavior. Mode "0/1" is the traditional behavior, with the NOT gate outputing
  //   either 0 or 1, depending on the input. Mode "0/floating" is open-collector (aka open-drain) behavior, so the NOT gate
  //   either outputs 0 or leaves the output floating. Mode "floating/1" makes the NOT gate leave the output floating or output a 1.
  //   Label - A label to appear above the gate.
  //   Label Font - Font for the label.
  //   Example Circuits
  //   input
  //   0
  //   1
  //   other
  //   output
  //   floating
  //   0
  //   error
  //   "
  //   Output behavior as 0/floating
  //   input
  //   0
  //   1
  //   other
  //   output
  //   1
  //   0
  //   error
  //   input
  //   0
  //   1
  //   other
  //   Output behavior as floating/1
  //   output
  //   1
  //   floating
  //   error
  //   Transient Pulse Generator
endmodule

module Common_Gates___Basics (
  input  A,
  input  X,
  input  in_3,
  input  B,
  input  Y,
  input  in_6,
  input  P,
  input  in_8,
  input  in_9,
  input  Q,
  input  in_11,
  input  in_12,
  input  A_2,
  input  [7:0] P_2,
  input  B_2,
  input  [7:0] Q_2,
  input  C,
  input  [7:0] R,
  input  D,
  input  E,
  input  [4:0] in_21,
  input  [4:0] in_22,
  input  in_23,
  input  in_24,
  input  in_25,
  input  in_26,
  output C_2,
  output V,
  output out_29,
  output R_2,
  output out_31,
  output out_32,
  output out,
  output [7:0] out_2,
  output out_35,
  output out_36,
  output out_37,
  output out_38
);

  wire callout_5_p1, medium_out, not_1_out, not_2_out, wide_out;

  and and_1 (C_2, A, B);
  // Callout #(.background("#b7e1eb71"), .dx(-15), .dy(-20), .foreground("#185fba"), .halign("center"), .style("margin: 4px;"), .text("2-input\nAND gate"), .valign("top")) callout_1: pin names not known
  nand nand_1 (R_2, P, Q);
  // Callout #(.background("#b7e1eb71"), .dx(-15), .dy(-20), .foreground("#236494"), .halign("center"), .style("margin: 4px;"), .text("2-input\nNAND gate"), .valign("top")) callout_2: pin names not known
  or or_1 (out, A_2, B_2, C, D, E);
  // Callout #(.background("#b7e1eb71"), .dx(-15), .dy(-20), .foreground("#236494"), .halign("center"), .style("margin: 4px;"), .text("5-input\nOR gate"), .valign("top")) callout_3: pin names not known
  or or_2 (out_36, in_23, in_26);
  // Callout #(.background("#b7e1eb71"), .dx(20), .dy(-20), .foreground("#236494"), .halign("center"), .style("margin: 4px;"), .text("Unconnected\ninputs are ignored"), .valign("top")) callout_4: pin names not known
  not not_1 (not_1_out, in_22[0]);
  not not_2 (not_2_out, in_22[2]);
  // Probe on callout_5_p1
  // Callout #(.background("#b7e1eb71"), .dx(20), .dy(-20), .foreground("#236494"), .halign("center"), .style("margin: 4px;"), .text("Floating input causes\nerror, unless a result\ncan be determined\nfrom remaining inputs"), .valign("top")) callout_5: pin names not known; wires that end beside it: callout_5_p1
  // XOR_Gate xor_1 has open pins: out=out_38
  or or_3 (V, X, Y);
  // Callout #(.background("#b7e1eb71"), .dx(-15), .dy(-20), .foreground("#236494"), .halign("center"), .style("margin: 4px;"), .text("2-input\nOR gate"), .valign("top")) callout_6: pin names not known
  nor nor_1 (out_31, in_8, in_11);
  // Callout #(.background("#b7e1eb71"), .dx(-15), .dy(-20), .foreground("#236494"), .halign("center"), .style("margin: 4px;"), .text("2-input\nNOR gate"), .valign("top")) callout_7: pin names not known
  // Callout #(.background("#b7e1eb71"), .dx(-20), .dy(-19), .foreground("#236494"), .format("wrapped"), .halign("center"), .style("p-margin: 0px;"), .text("Each output bit is the result of ANDing the corresponding input bits."), .textwidth(228), .valign("base")) callout_8: pin names not known
  and wide (wide_out, not_1_out, in_22[1], not_2_out, in_22[3], in_22[4]);
  LED led_1 (.in(wide_out));
  // Callout #(.background("#b7e1eb71"), .dx(-15), .dy(-20), .foreground("#236494"), .halign("center"), .style("margin: 4px;"), .text("Both circuits work the same: the LED\nturns on only when  the input is 11010."), .valign("top")) callout_9: pin names not known
  or or_4 (out_37, in_24, callout_5_p1);
  // Callout #(.background("#b7e1eb71"), .dx(-13), .dy(-16), .foreground("#236494"), .halign("center"), .style("margin: 4px;"), .text("If no inputs, then error output"), .valign("top")) callout_10: pin names not known
  // Callout #(.background("#b7e1eb71"), .dx(20), .dy(-20), .foreground("#236494"), .halign("center"), .style("margin: 4px;"), .text("Same for \nerror inputs"), .valign("top")) callout_11: pin names not known
  xor xor_2 (out_29, in_3, in_6);
  // Callout #(.background("#b7e1eb71"), .dx(-15), .dy(-20), .foreground("#236494"), .halign("center"), .style("margin: 4px;"), .text("2-input\nXOR gate"), .valign("top")) callout_12: pin names not known
  xnor xnor_1 (out_32, in_9, in_12);
  // Callout #(.background("#b7e1eb71"), .dx(-15), .dy(-20), .foreground("#236494"), .halign("center"), .style("margin: 4px;"), .text("2-input\nXNOR gate"), .valign("top")) callout_13: pin names not known
  // Callout #(.background("#b7e1eb71"), .dx(-15), .dy(24), .foreground("#236494"), .format("wrapped"), .style("p-margin: 0px;"), .text("8-bit 3-input AND gate"), .textwidth(88), .valign("base")) callout_14: pin names not known
  assign out_2 = P_2 & Q_2 & R;  // AND_Gate and_2, 8 bits wide
  and \medium  (medium_out, in_21[4], in_21[3], ~in_21[2], in_21[1], ~in_21[0]);  // AND_Gate
  LED led_2 (.in(medium_out));
  and and_3 (out_35, out_37, in_25);

  // Notes on the sheet:
  //   # Common Gates - Basics
  //   The common logic gates are: AND, OR, NAND, NOR, XOR, XNOR.
  //   Each one takes several inputs, combines these using the rules of Boolean logic, and outputs the result.
  //   See also: [Advanced Features](#Common Gates - Advanced) and [Online Documentation & Reference](/libs/gates/common.html)
  //   ### Gate Behavior with 2 Inputs
  //    A | B || AND | NAND | OR | NOR | XOR | XNOR
  //   ---|---||-----|------|----|-----|-----|------
  //    0 | 0 ||  0  |  1   |  0 |  1  |  0  |   1
  //    0 | 1 ||  0  |  1   |  1 |  0  |  1  |   0
  //    1 | 0 ||  0  |  1   |  1 |  0  |  1  |   0
  //    1 | 1 ||  1  |  0   |  1 |  0  |  0  |   1
  //   ## Multiple Inputs and Multi-Bit Gates
  //   Use the ***number of inputs*** attribute to allow more than two inputs. All inputs are combined using the usual rules of Boolean logic to produce a single output result. Use the *data bits* attribute to allow a gate to operate on multiple bits simultaneously.
  //   **Keyboard shortcut** 👉To change the *number of inputs* for a gate, select it and type a number. Or select several gates to change them all.
  //   **Keyboard shortcut** 👉To change the *data bits*, select some gates, hold the option key (⌥) or Alt key, and type a number.
  //   ## Visuals
  //   The ***gate size*** attribute allows a choice of *narrow*, *medium*, or *wide*. Gates can be rotated to face any direction using the ***facing*** attribute. A gate can be given a ***label***, which will follow the gate if it is moved or copied.
  //   **Keyboard shortcut** 👉Select some gates, then use arrow keys (↑→↓←) to rotate them so they face a different direction.
  //   ## Negated Inputs
  //   Any of the inputs can be configured to be active-low. This behaves exactly as if there were a NOT gate attached to that input, but used judiciously, negated inputs can make circuits more compact and easier to undertand.
  //   ## XOR & XNOR Multiple-Input Behavior
  //   Multi-input XOR and XNOR gates can be confusing. Normally, XOR outputs a 1 when an *odd number of inputs* are 1, and XNOR does the opposite. This "parity" behavior is most typical. For XOR and XNOR gates with more than two inputs, the ***multiple-input behavior*** attribute allows for a different, less common behavior, where XOR outputs a 1 when *exactly one input* is a 1, and XNOR does the opposite. 
  //   **Suggestion** 👉 Don't use multi-input XOR and XNOR gates. For parity calculations, use the ***Even Parity*** or ***Odd Parity*** gates instead. For *exactly-one* calculations, which are less common, consider building a circuit from a ***Bit Adder*** and a ***Comparator*** (found under ***Arithmetic***).
  //   ## Errors, Unconnected, and Floating Inputs
  //   * As a convenience, any input left unconnected is ignored: if there is no wire or other connection to the input, the simulator acts as if the input did not exist at all. So a 5-input gate with only two inputs connected behaves just like a 2-input gate. This doesn't match physical circuits or more realistic simulators, where such inputs would be considered *floating*, but it makes editing a circuit a little more forgiving. 
  //   * If all inputs are unconnected, the output is an error. 
  //   * If only one input is connected, the behavior depends on the gate type.
  //   * If some inputs are errors, a gate's output is calculated from the remaining inputs, but only the output would be unchanged even if the errors were replaced by any combination of 0 and 1 values. For example, for an AND gate, if any input is 0, then the output is 0, even if some inputs are errors. Similarly, for an OR gate, if any input is 1, then the output is 1, regardless of other inputs.
  //   To enable a more strict simulation behavior, treating unconnected inputs as floating values, go to ***Project > Options > Simulation***.
  //   Note: See below for behavior when some inputs are floating (z), errors (e), or unconnected.
endmodule

module Common_Gates___Advanced (
  input  [1:0] in_1,
  input  in_2,
  input  in_3,
  input  in_4,
  input  in_5,
  input  in_6,
  input  in_7,
  input  in_8,
  input  in_9,
  output out_10,
  output out_11,
  output out_12
);

  wire or_1_out;

  and and_1 (out_10, in_1[0], in_1[1]);
  or or_1 (or_1_out, in_2, in_4);
  and and_2 (or_1_out, in_3, in_5);
  xor xor_1 (or_1_out, in_6, in_8);
  and and_3 (or_1_out, in_7, in_9);
  Pull_Resistor pull_resistor_1 (.node(or_1_out));
  // Image #(.image("PNG:\niVBORw0KGgoAAAANSUhEUgAAAdUAAADOCAYAAABo35gbAAAfOElEQVR4Xu2dwaolx5GGT6O1NjbM\nwmhphFEPCNvyakBCIPAYZuEH0NIPICG88KKlplcSWozxGBk/gMEIP4RsELRhYGaMvTPGe7+D7yhO\nK6TsuJlVUZl/ZmTW+T8IuvvcvJEVf0dFVmZV5bncEUIIIQTCxX5ACCGEkDo4qBJCCCEgOKgSQggh\nIDioEkKW5tNPP737+Se/sR/f48mTJ1+Z/A55BvXDsjmoXi6XIfa917579/7jR1/Z06ef20OZAjmu\nreNWe/e9d+yv3gT2/7WXWd1nzRcvzKs2VLe9Qm/zKGcPH75+HTRkkNnzdxaoH5YpBtWSSXGZrZDI\nMdnj3LOPPv7wJoqijXu0zZgvXphX9UgRFz3efvtn9kfPIQVftZO2Vs8tk9/1zOZWhPphcQ2qvZEr\n9fSKPFdg5LM//+VP9leHo7OKt95843o8djYhJsXOHr+N5QwzLAvzpR7mVRuqwd7saK+dfK4zrXQQ\nsXa2mdieLspeu1vVL2WzAqoAUcgVuC2YUjSi0WPxFm2Jo1T8xaRYnqEQMl/aYF7VowV8b7alszJp\nfwS9l2g1Vl+rDxDUD0e2Av7P/93d/fIXd3cv/cv/3r3w4Fv2xyFI8Uj/IyKKZarL5cHDazGTz44i\nha4064iIqxXmSxvMq3qkGL/yyj+/MolVivcWqkltIdfZmF0C1fuJK0H98GQHVTnBX3jp7u7Vbz/7\ncxbkCj69Kn/5Oy/bJl1Jdfm3f32WgP/1n/9tmx1ClzLtbGOlWQbzpQ3mVT1SmO2gsDeL8t5D9CJL\nmanGYtJH7aAzEuqHJzuo/vBHz07w2YqkIsVSxR957yzVRUz7RyHFzhZB+ffsRZD50gbzqh4pyHZQ\nENvD2+4IMgjY2Zf8e+bBgfrhyaoiS09SHPWqeVZk5qHijyiUqovY737rT8Aa7PLljIOBwnxpg3nV\nRvrQi94b3FtG9LarQY7Fzr569IOC+mHZPHN7ntwoIgulXv33fKXBFsGZ740xXzAwr+rRYuxdwtxr\n14r2ozb74ED92tmsgBrI7KSFciRS9KRP5FJdiTRGsRkHhIj/gxqi8sUL86oN7/+tt10rdllz9qdd\nvbp427WynH72g5RRoiHQ4jD6YZSRGtl7Y6Nj3WOkFq1E5YuXkVrOnldH8S5NetuhsIPDqH6P4tXF\n2w7FKvptnrUjT2wEEUVhxFKdJX3wRmyW2QXzBQfzqh7v0qS3HZp0SXPGWZdXF287NLPrt1kBVyuS\naVEY9WTjyKU6S7p0N8M9MeYLDuZVG95c9LZDY2dd0w0MTl287dDMrN+mGlGCtaAPYIwsRpE6pQ+c\nRM+4InWoJSJfvETqOVNeebBF1bs06W3XC+1fDPXeZw3UD0f2jJ1xh5wjqMjo2YfqIu8Vyp9i6SsQ\nNbvgIIhetmO+tMG8qkcGg/Q9S/u+5V6x16XEvXY9kRj0eEcvpVI/PNlBddYdcrz0mn2kuqT24uWn\n1/6il8rSZbuRBZD50gbzqh67I5CadwY1w6AgpMuZIwcG6ocnO6jOvkOOBy0CyNmH3flmtuInRBRA\n5ksbzKt6SjOtdLa1h7fdCEbfJ6R+eLJKrLJDzha6sbj8iSLd+UaX6cRkn1bpK2qmY0mX7UYUQOZL\nG8yrNkpfI+Yt9t52o0jvE+biQkP9sGwqMZtYR5AZx8jjH9mXh7QAjnrQZDYNjjA6X7zMdkwReVWL\nFte9wuptN5IZZlxeXbztRhKp3+bZOtsJfZSRxz+yLy+jC+CMGhxhxuOf8ZhG51Uter9PZmJbeNuN\nJnrG5dXF2240Ufptnq0zntBH0CW9ES/Q68v6EffktkgLYO97c8wXPMyrerwP0XjbRZDOuEbj1cXb\nLoIj+qGOf7Mn78HMij7VOeKkH9nXUUbdCztjvsgAm95vHT3g5o5pFjx5Famft9h720WhM67RT7V6\ndfG2i2JLP5nBag6n1hLLZgXUDlZF75ONeNBj5uIneApgK2fKF9Eo3Q/XWi8NLavmld1P2NoI/bzF\n3tsukojXRby6eNtFktPPfr1culxs2x5hswKq85UZFcPsxU/QYxTrUdRGad0TjeGtN9/46u8ywxK9\nUv1GxblqXqUD6gj9cvfMvMXe2y6SdEYlA0Qu3hZy/ry6eNtFktNP/22PW+MRy+myRzazV98hR/nH\n3/569+MHl7vff/Mb17+3ktv5Ru0//v2D63/CzMVPkAdLXv9CE9Hlj9//AVSX1fNFSIu+WA7Vj3n1\nNel7rL/69SfD9JOiZ9+vtO9a7s04tMDutYtGj1NjQ2zL59FPbOshpNX0E8vNXFNSXY7qnM16OZlX\n3iFH+fsHj+7+8IVwaq2kulib6UX9PX6SaILWZeV8EfSkEyu9s8q8ymOXe0foV9oRyA4Ke3jbRWPj\nbcX6s6a67M3YVtHPLvGWLhasLkfIqnCGHXIEuRJGnbxCaeeb1YofelA9S74I6QlXWiJnXuWxg+oI\n/bwzrT287SKZdaYqrKSf2N67tfCZ6hl2yBFkaUlP3NZlJqG0881Ky3T6YEkPXVbPF0FPuq3/S5mB\n9dDvDHklpvejS8eM1q+0I5D3Xp+3XSQSXzoQ7A1yR7gV/TQ/VT/5e2nATO+rHmXzN2qdzsSoGFZ4\noKT0pCaKUVr3RGPYikVnZCM2Plgxr/S7YKP18xZ7b7so0gFh5DF6dfG2iyLVTy9G7CBbal8TUz7r\nv2TrxFiFUTHMXvzSwtfrGEdp3RONQU0GAN14wb4m0uPCxLJqXs2gn7fYe9tFoXqVHqrphVcXb7so\nVD87K03vr8rP5PjtZzVsVkB1vip6xVx6YALJzMUvLXw9ZwdnypdUs5z1HhCUVfNqBv28xd7bLgIt\n8rUFvgWvLt52Eew95avHbq3U3sNmBdQOVkV3chlRkGbc4k4Ztdx2xnzRQU1NN4YYxep5Famft9h7\n241GB9SWAt+CVxdvu9Ec0U+OXc0uBx9lswLqibAqevwj9k2dUautmUQPZtTgCCPzxcuMmo7Oq1q8\nxd7bbiQ6w4qYoSpeXbztRrI3Q+3J5tk64wl9hJHHP7IvDxGFbzYNjjLj8c92TBF55SE3u/Bq5203\ngvQp35EDAvXDkVXiDDvk9LifWtr5Rr9MepbEGl34mC9tMK/qkSJq362071ju4W3Xm/Sp01EDwln1\ni5zhZ5WQE3r1HXL0fg9yKS/VJfeCfkRBtkQUPuZLG8yreuzON3ZQ2BuctBDvtetNOsMaOSCcUb/o\nY8kOqqvvkKPfNiKGpLTzzSy73qQPhYwsfMyXNphX9ZRmWnq8e/f5dBOAvXY90XuSEQMC9cOTrSKr\n75Cjsw50McrtfPO7336h0YOH1/4iZjmKFDtNLHTcezBf2mBetZHbEcj78Iy3XS90dhV5DNQPy2YF\n1INdCb2qlkI5ikid7PuAo15XyBGpQy0R+eIlUs+Z8qoGr3bedmjS+39idlCLxquLtx2amfXbVCNK\nsBb0mEdd3esDLhFFebZlOeYLDuZVPWnB3cLbDk26XDny/qkXry7edmhm129TjQjBWtClqpGFIOrl\n/BmX5ZgvOJhX9Xjv841eurSzq1H9HoX6tbFZAVcqkmkxGMnoPu0ONTMty43WooWofPEy+thmzquj\naAx7S4Ledq2If92MQEz+3rvPFry6eNu1spx+9oMUDWJ20vs/I4uBPjU6YonO3uOacXbFfMHAvKrH\nuyTpbddK+iCN2MyDgeDVxduuldX0EzYVGSFaK5EFcsQSnf1mD/n7bPf/FOYLBubVcbTYepckvUuc\ntaT3/Xr2g4L64chWwFV2yEmX8EYUyHTnm+srD1/23QNb9EbFWAPzpQ3mVT0yGOTer9yb0XjbHUF8\n2ZnV7EuV1A9P9sxdYYeciAJpd76RvtFLdPbeltjsD4wwX9pgXtVjdwTSQryFzoL22nkRf3YwkM9W\nGAyoH57soDrzDjm2OIwskKkuutGB7M/aiswedMkvtVWKHvOlDeZVPbmZ1t5SoerQUrRl+dMOBJ6+\nZ4P64ckOqjPukGOXrSIeqFBdroPHg29dj0M+q0Hul+UK3or3tpgvbTCv2pACrU+H7m1Tp7OsvXY5\ncjMqsRWXKFOoH5bNCqhBRyJFYrYHKvR4jlzxyzFLe3s/S00KYXRcrTBf2mBe1aPx7hVnTzv5mQwA\npdmUmHx+hlmV4tFF8LS7Rf1SNiugCjCS0pW22JFi0wspUFu6yPHLcW4VOjH5Wc+nOyPY0qUXs+eL\nF+ZVPd57fGmBl4Ivv6dWKv6pSbutwWRVqB+W/Bn8JVaUCJvtSnuroG2Z/J4UxJliQWNjjrDZ8sUL\n86oe1WKvYFvttkxnWns+zwD1wzLdoCpFcdYikc4mSqbHP2sMPbFajLCZ88UL86oNnSntoe3sLOtW\ni79C/bBsDqqEEEII8cNBlRBCCAHBQZUQQggBwUGVEEIIAcFBlRBCCAHBQZUQQggBwUGVEEIIAcFB\nlRBCCAHBQZUQQggBwUGVEEIIAcFBlRBCCAHBQZUQQggBwUGVEEIIAcFBlRBCCAHBQZUQQggBwUGV\nEEIIAcFBlRBCCAHBQZUQQggBwUGVEEIIAcFBlRBCCAFRHFTffe+du/cfPzqFSSwoqEse6tIG9avn\nyZMnN2korN9bsV4UB9XL5XIqQ2H9rm4orN/VbTS2/9VtJLbvWzEU1u+tWC+KnrXjjz7+8N6V6Com\nx44WkLrkoS5tUL96tE87EzmroTWmfliKnnt3PAp0HGh/UaDjQPuLIiqOqH7RRMQR0Wck6HjR/man\nd7xFz9eOHzy0Hy8HWkDqkoe6tEH96onoMxJ0vGh/s9M73qznX/7i7u7Vbz+zH/7I/nQtkAJSlzzU\npQ3qV8+nn35698or/7za22//zP74lCA1pn54sp7lxNaT/IWX7E8xyBOCI54SRAo4QpccT59+fjUk\nq+myYr54GaFfjtnzyoMMBDooiI1CBqOff/Ib+/EQkBpTPzxZz72vnF/+zsvPWU+QAvbQZa+oyUDy\nvde+e30QBMnsuqSsmi9eeuh3hrzyIIV59ExrxMMuWyD7pn54ip5fvPz0aj1IA+oZnIAWEK2LDBJy\nfKXitkrxQ+uSsnK+eEHrd5a88hDRpxDRp4COF+3PS0SfQu94i557dpzOOv78lz91WYZS0HGg/SlS\n3MSvaGK10FcWkKDjQPtLWTlfvPTqd/W88hDRpxDRp4COF+3PS0SfQu94i557dixXyfJOmy7l9bxf\nho4D7S9FNJHZg/W/QvFD+0tZOV+89Ox35bzyENGnENGngI4X7c9LRJ9C73iLnnt1LFfLWhBl1iF9\n/OrXnyxTJNH+RA+dTcifdjYhrFD80P6U1fPFC7rfs+SVh4g+hYg+BXS8aH9eIvoUesdb9NyrY511\nKP/421+v/cifPUDH0cPf3gCxQvFD+1NWzxcv6H7PklceIvoUIvoU0PGi/XmJ6FPoHW/Rc6+O5YpZ\n/Op2bLKkJzMP+UxmImjQcaD9aWGTApj+XZG/y9Kd2F6RPAI6DrQ/ZfV88YLu9yx55SGiTyGiTwEd\nL9qfl4g+hd7xFj1fO+64w4ucyGK6LJUu8yFBC4jWJS16peKX+7yV2XWxrJovXtD6nSWvPIzuU9+x\nlD7l9RD590jQ8aL97XE2/SxZzz3em4sCKSB1yUNd2qB+9UTsCCR96ubsMjisPChQPzxZz1E7vPQA\nKSB1yUNd2qB+9UTtCBQJUmPqhyfrmVfOeahLHurSBvWrJ2JHoGiQGlM/PEXP6B1eokALSF3yUJc2\nqF89EX1Ggo4X7W92esdb9Ny741Gg40D7iwIdB9pfFFFxRPWLJiKOiD4jQceL9jc7veMteu7d8SjQ\ncaD9RYGOA+0viqg4ovpFExFHRJ+RoONF+5ud3vEWPffueBToOND+okDHgfYXRSkO5GsnOUr9rkYp\njp76lfo8K+h40f5mpxSvPI2M4L7nLyl1vBroOND+okDHgfYXRRqHbotoTd7tREP96jmLdl7Q8aL9\nzU4ar7zOY/NTrGWALSp5FqHRcaD9RYGOA+0vCo1Dd21Se+vNN577N/p7XalfPWfRzgs6XrS/2dF4\ndQMKtYcPX7/37xqKSl4dA3d4iQKdMNQlz9l0UbOzKvm3/gy5/zD1qwedy7ODjhftb3ZsjtpZaeuX\nqGd/6yzvzf39g0d3f/hCGLHff/Mb9seHoS55zqKLkJ5ssi9uDupXZrR+ETsCRYKOF+1vBdIcLc1G\nW97fzQ6qZ9nhRU5YPXnFWqEuec6ii5CecHaWpVC/MqP1u7UdgdDxov2tQJqjMnjmaNElm9FnuXJG\nXhEL1CXPWXQR0hOu9C041K/MaP1aZhQrgo4X7W8F0hwt7Tvcokt2UBXOssPLjx9croaCuuQ5iy7p\nCVdavpSvofvJFz9/nfrdI0I/7e9WQMeL9jc7aY6WBsyW+6rF36h1OBvoOND+okDHgfYXRXrCidnZ\nVvqaSGl5swbqV89ZtPOCjhftb3ZsjtrZavqajX2IyUNRybMIjY4D7S8KdBxof1FoHOkrIDLjktmV\n/KmfIV8JEahfPWfRzgs6XrS/2dF401doZMYqA6j9rIaikmcRGh0H2l8U6DjQ/qJI40hf/0gNOSAo\n1K+es2jnBR0v2t/spPGmy7yplZ4K9lBU8ixCo+NA+4sCHQfaXxS5OGSLPRkgxJ4+/fy5n6HI9bsi\nuTh665fr88yg40X7m51cvPql6WJ2OfgoRSVzHa8IOg60vyjQcaD9RREVR1S/aCLiiOgzEnS8aH+z\n0zveoudrxyfa4QUFdclDXdqgfvVE9BkJOl60v9npHW/W8xnfm0NAXfJQlzaoXz23vCMQAuqHJ+v5\njDu8IKAueahLG9Svnpadb1YFqTH1w5P1zCvnPNQlD3Vpg/rV07LzzaogNaZ+eIqez7bDCwrqkoe6\ntEH96onoMxJ0vGh/s9M73qLn3h2PAh0H2l8U6DjQ/qKIiiOqXzQRcUT0GQk6XrS/2ekdb9Fz745H\ngY4D7S8KdBxof1FExRHVL5qIOCL6jAQdL9rf7PSOt+i5d8ejQMeB9hcFOg60vyii4ojqF01EHBF9\nRoKOF+1vdnrHW/Tcu+NRoONA+4sCHQfaXxRRcUT1iyYijog+I0HHi/Y3O73jLXru3fEo0HGg/UWB\njgPtL4qoOKL6RRMRR0SfkaDjRfubnd7xFj1fO+YOL/egLnmoSxvUr56IPiNBx4v2Nzu948165ntz\neahLHurSBvWrhzsCtUH98GQ9c4eXPNQlD3Vpg/rVwx2B2qB+eLKeeeWch7rkoS5tUL96uCNQG9QP\nT9Ezd3jJQ13yUJc2qF89EX1Ggo4X7W92esdb9Ny741Gg40D7iwIdB9pfFFFxRPWLJiKOiD4jQceL\n9jc7veMtetaOP/r4w7v3Hz9a0uTY0QJSlzzUpQ3qV4/2+eTJk5swtMbUD0vRs3Z8FkNh/a5uKKzf\n1W00tv/VbSS271sxFNbvrVgvip7ffe+de1eiq5rEgoK65KEubVC/euxM5FYMhfV7K9aL4qBKCCGE\nkGNwUCWEEEJAcFAlhBBCQHBQJYQQQkBwUCWEEEJAcFAlhBBCQHBQJYQQQkBwUCWEEEJAcFAlhBBC\nQHBQJYQQQkBwUCWEEEJAcFAlhBBCQHBQJYQQQkBwUCWEEEJAcFAlhBBCQHBQJYQQQkBwUCWEEEJA\ncFAlhBBCQBQH1Xffe+fu/ceP7p4+/dz+6KahLnmoSxvUj5BzUBxUL5dL1r732ndv+uS3elCXZ1g9\nqMsxrG7Uz49qRcgMFDNRE/WtN9+4d6Kn9tHHH97UCU9d8lCXNqhfPVaj1Mg+1ApLUcmS0HJCy4lt\nk/fl77xsm54S6pKHurRB/eqx2uwZeR6rD7Vqo6jaVdQHD+3Hz5E74WWp6sx4dPnzX/5EXTLcYr54\n8eh3i3nlQbXIkWqVGvkaq82ekW2yCv3yF3d3r377mf3wR/aneeTKORVeCsDZsLpIQduyX/36k3sJ\necYiaHXxcAv54sXqZ/PI2q3klZcjxd7qRrb1s3pttSXPyKojJ7ae5C+8ZH9aRmYi8mCFCn+2Qpnq\nImYTzWtn1oX5chzmVRuPHz++2hFS3W6dIzrYnCP3yapir5yPIlfNKvqZ7v1YXewMYs/Spbsz63KU\ns+aLF6ufzZs9O2teedABtXVgveUBolU78jxFRV68/PRqtchV8xlPdOqSh7q0Qf3qqRkUUm55gOBF\nCZ6iEgihzniiU5c81KUN6lcPQjv10epnRWoG1JRb1i5HUQWUSOmJfoZ7PtQlD3Vpg/rVg9JO/SB8\nrQQi5lvVLkdRAaRAZzrRqUse6tIG9asHqR3S1yqgYlY/CF8rU4weLU76CsXKoGOgLnnOoosXdKy3\npB86TrS/2UHGi/S1KsXoe4ijr0/IE4urQl3yUJc2qF89aO3UH9LnzKBjRftbjWLkV2F2dng5iryX\nuLrgPXRJl+tWpYcuZ8gXLz30O0NeeegRYw+fs4KOVf0hfa5ENmr73hySla+erS72fcFaW/09Q6sL\nkpXzxYvVz+ZHra2eV156FfBefmejR5w9fK5CNuraHXI8rDz7QO18s2erwXxpg3nVRq/4bkE7oVeM\nvfzOTjZie+WMRmcf8sXMK2F1sTODVtOv/VpdFzSr5osXq5/Ni1ZbNa+89CzePX3PQq8Y1W8P3zNT\njLZ1h5ct5OQWoaVYrgZ1yUNd2qB+9fQs3D19z0LPGHv6npVitL3F6O2/F72Pu7f/XvQ+7t7+o+kd\nX2//kdTEdqR9jf+V6BlfT9+zUoy2txi6pCf3zFaCuuShLm1Qv3pqtDvSvsb/SvSOr7f/2ShG2lsI\nudcj/uXPlaAueahLG9SvnhrtjrSv8b8SvePr7X82ipH2FkLv88hj/ytBXfL01kUHhdV08UL96ilp\np5/XmvVzVnrH19v/bBQjHSHEiD7QjDjmEX2g6XnMsomBPsEqJkuZZ3uSlfrVU6PdkfY1/leiFJ9+\nXmvWz61QjPQqBHiHF8sosf/xt7/aj6qhLnl66mJPVrXo+4PUrw2UfjXnS037o7+zCr1j6+1/NrKR\n2vfmeqFi//2DR13sj9//wd0fvvAv9vtvfsN2fxiri30fEGHpLjg2HpT11gWJLofnTGZcNrYR1ls/\nmxMtpg8o5ews+mk8R6hpf/R3VmFEbCP6mIVslD13yElRofUE622tjNr5Rs0efy9rpWe+pN+2kjMb\nS4S1MjqvUrOxRFgrGssRatqLfTaRobhcjut3lBF9zEI2Snvl3AsV2l7Jogx9RWx1sbMChHGm+jyi\nieph7SwzLaufzYkWu+WZqo33qOV8fTaZIbhc7seLRvuwx7+CHaX4Gz13eFEul/7/mXoio6AueXrq\nonpYi7wnSP3aQOpXc77UtD/6O7347FJX7EuUYrP5ctRyvj5b1I5QbH253BcGzYg+0Iw45hF9oOl5\nzDLjUv9q8tmZoH711GhX0/7o76zCiNhG9IHms8vxAVUo/kZvEfTbR1bbj5S65OmtizwpuqIuXqhf\nPTXa1bQ/+jurMCK2EX3MQjHK3iLo1fNqV8zUJQ91aYP61VOj3ZH2Nf5XYkR8I/qYhWKUvUXQByhW\newmduuShLm1Qv3pK2unntWb9nJXe8fX2PxvFSHsL0dt/L3ofd2//veh93L39R9M7vt7+I6mJ7Uj7\nGv8rUYpPP6816+dWKEZ6FaLTDi+r3jcUqEse6tIG9aunpmgfaV/jfyV6x9fb/2xkI7XvzaHRdzFX\nW4qyuth3AltN92ddXRc0q+aLF6ufzYtWWzWvvNQU7SPta/yvRO/4evufjWykPXfIEVYVedTON6vB\nfGmDedVGz/h6+p6F3jH29j8b2UjtlTMSuXIWgVdcirK62BlBi+ls4gy6IBFtVtXFi9XP5kaLrZxX\nXnoW7Z6+Z6FnjD19z0ox2h47vMhXUKnI8vcVoS55qEsb1K+eXoW7l9/Z6BlnT9+zUoy2hxj6WL9c\nQa8KdclDXdqgfvX00E59ov3OSK84e/mdnWLEaEHSq+aVQcdAXfKcRRcv6FhvSb8ecfbwOSs9YlWf\naL8rUIwYKciZlqGoSx7q0gb1qwepnYD2Nzs94u3hcxWKUSNFUV/y3ZirQ13yUJc2qF89PbRD+VsB\ndLxof6tRjBwljH7J9FlOcOqSh7q0Qf3qQWknIH2tAjJm9YXytyLFyK/CNOzwIstO+qDEmU5w6pKH\nurRB/epBFXGUn9VAxo30tSrZ6O17c0dJ7+mc6QS3uth3AvdMdwY6uy5HOWu+eLH62bzZs7PmlZfW\nQq6/3+pnVVBxo/ysTlaBlh1y5CQ/6wmO2vnmzLowX47DvGrj8ePHV6sh1e9WaY3f5uGtk1XAXjl7\nSGcbYlIsz4bVxc4YrMkMQne0uSVdPNxCvnix+tk8snYreeVBB9SjAysHgq85ql0KNbxPUQnvDi/y\nDRh6L0dM/n7mx/i9uqT3uKjL19xavnjx6ndreeXh6KDAgeBreFGCp6jGlljybRfpfRy1Wzi5qUse\n6tIG9atnS7sUqx95RsuASu5TVEVFk5NZl5xsUorJlfJZv1IqB3XJQ13aoH71qDa5z3JGnserC3X0\nUVTGCpjaLZ/YVgvq8gyrBXU5htWM+vmxepWM5MnpY7Wjjn6KCslJnD4cwZP6GdQlD3Vpg/rVY4s+\nC/8xrHYlIz6oFCGE3DB28OQA2gbVI4QQQkBwUCWEEEJAcFAlhBBCQHBQJYQQQkD8P7DZZVW9I2vY\nAAAAAElFTkSuQmCC"), .xscale(0.8), .yscale(0.8)) image_1: pin names not known
  // Callout #(.background("#b7e1eb71"), .dx(10), .dy(-10), .foreground("#236494"), .halign("right"), .style("margin: 4px;"), .text("ANSI/IEEE\n91a-1991"), .valign("bottom-overall")) callout_1: pin names not known
  // Callout #(.background("#b7e1eb71"), .dx(10), .dy(-10), .foreground("#236494"), .halign("right"), .style("margin: 4px;"), .text("IEC 60617-12"), .valign("bottom-overall")) callout_2: pin names not known
  // Callout #(.background("#b7e1eb71"), .dx(10), .dy(-10), .foreground("#236494"), .halign("right"), .style("margin: 4px;"), .text("DIN 40700"), .valign("bottom-overall")) callout_3: pin names not known
  // Callout #(.background("#b7e1eb71"), .dx(-20), .dy(-20), .foreground("#236494"), .format("wrapped"), .halign("right"), .style("p-margin: 0px;"), .text("push-pull output is always driving"), .textwidth(111), .valign("top")) callout_4: pin names not known
  // Callout #(.background("#b7e1eb71"), .dx(-15), .dy(-20), .foreground("#236494"), .format("wrapped"), .style("p-margin: 0px;"), .text("single bus wire with multiple device outputs"), .textwidth(267), .valign("base")) callout_5: pin names not known
  // Callout #(.background("#b7e1eb71"), .dx(-15), .dy(13), .foreground("#236494"), .format("wrapped"), .style("p-margin: 0px;"), .text("any of the four devices can drive the bus wire to 1, or even more than one of them at the same time"), .textwidth(216), .valign("base")) callout_6: pin names not known
  // Callout #(.background("#b7e1eb71"), .dx(-21), .dy(-16), .foreground("#236494"), .format("wrapped"), .style("p-margin: 0px;"), .text("pull-down resistor ensures the bus is pulled down to 0 if no output is driving to 1"), .textwidth(267), .valign("base")) callout_7: pin names not known
  and and_4 (out_11, in_1[0], in_1[1]);
  // Probe on or_1_out
  // Callout #(.background("#b7e1eb71"), .dx(-20), .dy(-20), .foreground("#236494"), .format("wrapped"), .halign("right"), .style("p-margin: 0px;"), .text("pull-down-only output is floating when not driving output low"), .textwidth(146), .valign("top")) callout_8: pin names not known
  and and_5 (out_12, in_1[0], in_1[1]);
  // Callout #(.background("#b7e1eb71"), .dx(-20), .dy(-20), .foreground("#236494"), .format("wrapped"), .halign("right"), .style("p-margin: 0px;"), .text("pull-up-only output is floating when not driving output high"), .textwidth(134), .valign("top")) callout_9: pin names not known

  // Notes on the sheet:
  //   # Common Gates - Advanced Features
  //   ## Output Driver Option
  //   Normally, gates use **push-pull** outputs: they actively output either 1 or 0 at all times, as long as the inputs are well defined. The ***Output Driver*** attribute allows for two other behaviors. 
  //   * With a **pull-up-only** output driver (equivalent to open-emitter/open-source) a gate can actively output 1, but instead of outputting 0 it will produce a floating (z) output. 
  //   * With **pull-down-only** output driver (equivalent to open-collector/open-drain), a gate can actively output 0, but instead of outputting 1 it will produce a floating (z) output. 
  //   This allows creation of *wired-OR* and *wired-AND* busses. ***Pull Resistor*** (found in the ***Analog*** library) can be useful for these too.
  //   ## Gate Appearance and International Standards
  //   Different standards bodies have adopted different symbols for  common gates. In **Logisim > Settings > International** you can choose from **ANSI/IEEE Standard 91a-1991** (curved, distinctive shapes commonly used in computer science textbooks and educational materials), **IEC 60617-12** (rectangular, uniform shapes often used in professional settings and engineering), and **DIN 40700** (an older, less common standard).
  //   or_1 drives only 1 and floats otherwise
  //   and_2 drives only 1 and floats otherwise
  //   xor_1 drives only 1 and floats otherwise
  //   and_3 drives only 1 and floats otherwise
  //   AND
  //   OR
  //   and_4 drives only 0 and floats otherwise
  //   NAND
  //   NOR
  //   XOR
  //   and_5 drives only 1 and floats otherwise
  //   XNOR
endmodule

module Common_Gates___Reference (
);


  // Notes on the sheet:
  //   # Common Gates - Reference
  //   ## Properties
  //   Common multiple-input logic gates, AND, OR, NAND, NOR, XOR, XNOR, support these properties:
  //   | Property      | Values                       | Notes
  //   |:--------      |:---------                    |:----------
  //   | Facing        | East, North, West, South     | Orientation of the output port.
  //   | Data Bits     | 1-32                         | Width of each input and output port. If set 
  //   +               |                              | to *N*, the gate outputs *N* values, with 
  //   +               |                              | each output value computed from the 
  //   +               |                              | corresponding bit of the input ports.
  //   | Gate Size     | Narrow, Medium, Wide         | Size of the gate symbol.
  //   | Number of     | 2-32                         | Up to 32 inputs are allowed.
  //   +    Inputs     |                              | Unconnected inputs are ignored.
  //   | Output Driver | 0/1 (push-pull),<br>         | Determines the set of possible output values,
  //   +               | 0/floating (pull-down-only), | in other words, if the output port is capable
  //   +               | <br>floating/1 (pull-up-only)| of actively driving high values, low values,
  //   +               |                              | or both.
  //   | Label         | any text                     | Text to be shown on top of the gate.
  //   | Label Font    | any font                     | Font to be used for the label.
  //   | Negate *i*    | Yes, No                      | Whether to invert the value of input port 
  //   +               |                              | *i*. Negated inputs are drawn with a "bubble"
  //   +               |                              | symbol at the port.
  //   | Multiple-Input| When an odd number are on,   | For XOR and XNOR gates with more than two 
  //   + Behavior      | <br>When one input is on     | inputs, chooses between parity-style 
  //   +               |                              | behavior and one-hot behavior.
  //   ## Keyboard Shortcuts
  //   + 👉Arrow keys (↑→↓←) change the *Facing* property for the selected gate or gates.
  //   + 👉Typing a number (2-32) changes the *Number of Inputs* property for the 
  //     selected gate or gates.
  //   + 👉Typing a number (1-32) while holding the option key (⌥) or Alt key changes the *Data Bits*
  //      property for the selected gate or gates.
  //   ## Behavior
  //   * **AND** Gate
  //     - Unconnected inputs are ignored.
  //     - If there are no connected inputs, outputs error (e).
  //     - Outputs 1 when *all* connected inputs are 1 (and there are some connected inputs).
  //     - Outputs 0 when *any* input is 0.
  //     - In all other cases, outputs error (e). This includes cases where some inputs are floating
  //       (z) or errors (e), unless some input is 0, in which case the above rule applies and the
  //       output is 0.
  //   * **NAND** Gate
  //     - Outputs 1, 0, or e, whenever AND would have outputted 0, 1, or e, respectively.
  //   * **OR** Gate
  //     - Unconnected inputs are ignored.
  //     - If there are no connected inputs, outputs error (e).
  //     - Outputs 1 when *any* input is 1.
  //     - Outputs 0 when *all* connected inputs are 0 (and there are some connected inputs).
  //     - In all other cases, outputs error (e). This includes cases where some inputs are floating
  //       (z) or errors (e), unless some input is 1, in which case the above rule applies and the
  //       output is 1.
  //   * **NOR** Gate
  //     - Outputs 1, 0, or e, whenever OR would have outputted 0, 1, or e, respectively.
  //   * **XOR** Gate with Multiple-Input Behavior set to "When an odd number are on"
  //     - Unconnected inputs are ignored.
  //     - If there are no connected inputs, outputs error (e).
  //     - Outputs 1 when an odd number of inputs are 1, and all other connected inputs
  //       are 0.
  //     - Outputs 0 when an even number of inputs are 1, and all other connected inputs
  //       are 0 (and there are some connected inputs).
  //     - In all other cases, outputs error (e). This includes all cases where some inputs are 
  //       floating (z) or errors (e).
  //   * **XOR** Gate with Multiple-Input Behavior set to "When one input is on"
  //     - Unconnected inputs are ignored.
  //     - If there are no connected inputs, outputs error (e).
  //     - Outputs 1 when exactly one input is 1, and all other connected inputs
  //       are 0.
  //     - Outputs 0 when either zero or more than two connected inputs are 1, and all
  //       other connected inputs are 0 (and there are some connected inputs).
  //     - In all other cases, outputs error (e). This includes all cases where some inputs are 
  //       floating (z) or errors (e).
  //   * **XNOR** Gate
  //     - Outputs 1, 0, or e, whenever XOR would have outputted 0, 1, or e, respectively.
endmodule

module Floating_Buses (
  input  A,
  input  X,
  input  in_3,
  input  B,
  input  Y,
  input  in_6,
  input  P,
  input  in_8,
  input  in_9,
  input  Q,
  input  in_11,
  input  in_12,
  input  A_2,
  input  [7:0] P_2,
  input  B_2,
  input  [7:0] Q_2,
  input  C,
  input  [7:0] R,
  input  D,
  input  E,
  input  [4:0] in_21,
  input  [4:0] in_22,
  input  in_23,
  input  in_24,
  input  in_25,
  input  in_26,
  input  [1:0] in_27,
  input  in_28,
  input  in_29,
  input  in_30,
  input  in_31,
  input  in_32,
  input  in_33,
  input  in_34,
  input  in_35,
  output C_2,
  output V,
  output out_38,
  output R_2,
  output out_40,
  output out_41,
  output out,
  output [7:0] out_2,
  output out_44,
  output out_45,
  output out_46,
  output out_47,
  output out_48,
  output out_49,
  output out_50
);

  wire callout_9_p1, medium_out, not_1_out, not_2_out, or_3_out, wide_out;

  // Callout #(.background("#b7e1eb71"), .dx(20), .dy(-20), .foreground("#236494"), .halign("center"), .style("margin: 4px;"), .text("Unconnected\ninputs are ignored"), .valign("top")) callout_1: pin names not known
  and and_1 (C_2, A, B);
  // Callout #(.background("#b7e1eb71"), .dx(-15), .dy(-20), .foreground("#185fba"), .halign("center"), .style("margin: 4px;"), .text("2-input\nAND gate"), .valign("top")) callout_2: pin names not known
  nand nand_1 (R_2, P, Q);
  // Callout #(.background("#b7e1eb71"), .dx(-15), .dy(-20), .foreground("#236494"), .halign("center"), .style("margin: 4px;"), .text("2-input\nNAND gate"), .valign("top")) callout_3: pin names not known
  or or_1 (out, A_2, B_2, C, D, E);
  // Callout #(.background("#b7e1eb71"), .dx(-15), .dy(-20), .foreground("#236494"), .halign("center"), .style("margin: 4px;"), .text("5-input\nOR gate"), .valign("top")) callout_4: pin names not known
  or or_2 (out_45, in_23, in_26);
  // XOR_Gate xor_1 has open pins: out=out_47
  // Callout #(.background("#b7e1eb71"), .dx(-13), .dy(-16), .foreground("#236494"), .halign("center"), .style("margin: 4px;"), .text("If no inputs, then error output"), .valign("top")) callout_5: pin names not known
  and and_2 (out_48, in_27[0], in_27[1]);
  or or_3 (or_3_out, in_28, in_30);
  and and_3 (or_3_out, in_29, in_31);
  xor xor_2 (or_3_out, in_32, in_34);
  and and_4 (or_3_out, in_33, in_35);
  Pull_Resistor pull_resistor_1 (.node(or_3_out));
  // Callout #(.background("#b7e1eb71"), .dx(25), .dy(16), .foreground("#236494"), .halign("right"), .style("margin: 4px;"), .text("ANSI/IEEE\n91a-1991"), .valign("bottom-overall")) callout_6: pin names not known
  // Callout #(.background("#b7e1eb71"), .dx(25), .dy(16), .foreground("#236494"), .halign("right"), .style("margin: 4px;"), .text("IEC 60617-12"), .valign("bottom-overall")) callout_7: pin names not known
  // Callout #(.background("#b7e1eb71"), .dx(25), .dy(16), .foreground("#236494"), .halign("right"), .style("margin: 4px;"), .text("DIN 40700"), .valign("bottom-overall")) callout_8: pin names not known
  not not_1 (not_1_out, in_22[0]);
  not not_2 (not_2_out, in_22[2]);
  // Callout #(.background("#b7e1eb71"), .dx(20), .dy(-20), .foreground("#236494"), .halign("center"), .style("margin: 4px;"), .text("Floating input causes\nerror, unless a result\ncan be determined\nfrom remaining inputs"), .valign("top")) callout_9: pin names not known; wires that end beside it: callout_9_p1
  // Callout #(.background("#b7e1eb71"), .dx(-20), .dy(-20), .foreground("#236494"), .format("wrapped"), .halign("right"), .style("p-margin: 0px;"), .text("push-pull output is always driving"), .textwidth(111), .valign("top")) callout_10: pin names not known
  // Callout #(.background("#b7e1eb71"), .dx(-15), .dy(-20), .foreground("#236494"), .format("wrapped"), .halign("center"), .style("p-margin: 0px;"), .text("single bus wire with multiple device outputs"), .textwidth(267), .valign("base")) callout_11: pin names not known
  // Callout #(.background("#b7e1eb71"), .dx(-15), .dy(13), .foreground("#236494"), .format("wrapped"), .halign("center"), .style("p-margin: 0px;"), .text("any of the four devices can drive the bus wire to 1, or even more than one of them at the same time"), .textwidth(216), .valign("base")) callout_12: pin names not known
  // Callout #(.background("#b7e1eb71"), .dx(-21), .dy(-16), .foreground("#236494"), .format("wrapped"), .halign("center"), .style("p-margin: 0px;"), .text("pull-down resistor ensures the bus is pulled down to 0 if no output is driving to 1"), .textwidth(267), .valign("base")) callout_13: pin names not known
  // Image #(.image("PNG:\niVBORw0KGgoAAAANSUhEUgAAASYAAADOCAYAAACTpK+BAAATo0lEQVR4Xu2dwapcxxGG70Vrb2zI\nImhphEEBY9leBSwMBseQhR/CD+AQtFSUZUIWAcdI6A2yyEvYYJAhkMTYO2G89ztkopqrivrUqT7T\nZ7q6q6vn/6CRfK/Vfeq7/9Q5c6bvzNUBAAAG40p+AQAAvEFjAgAMBxoTAGA40JgAAMOx2Ziurq66\njHvvvXP4wx8f/n88e/aNPJQhoOPaOm4ev/v95/KfXgTy59pqSO+j5qUU5GrNEI0pN+gHNNoPg45J\nHuep8ee//OkigiXr7j1GzEspyNWSosbUGjpjpGcG7YdEX/v+h+/kP+0On90++vD+8XjkWY0GBUYe\nv6xlhjO9BHk5H+RqyWaKegUtB50JZOhIvDd8LKXBpzpyDyAaFLgpwoS8VIFcvUJN0b/+czh8+cXh\ncPsX/z7cuv6l/LYL9APwDlzq5er67jEQ9LW9UFhyZz+PumpBXupArtaojYkk3bp9OLz95s2fo0Bn\nkvTscOetO/J/aUrq5de/+u/xGP7213/K/20X/LREnvUine2QlzqQqzVqY/r4kxtJowWNocCx6J73\nElIvNHh9KygwMkj036MHCXmpA7laozYmuoykgHH3HhU6A7LoHmFjLzT+8fcbN638yKciIz6gGOSl\nDuRqzWb1LQVZ4Rk2Pgu1fLlWBmnkewXIiw3I1QSNiUjD1hMKDq1pedmdI61x1AeVx8/gHLzyUgpy\nNUljIlhw7xucPR3JewW9az1FTxe1eOWllJ4uR8zVZuU95VjgIbbHZbckvZlLY5izHPJixqXnajNF\n0YKWiu31ikPPy25Jehk+wj0C5MWOS8/VZoqiBY3gm3o9f6CentKbmN5nfk8P5+KRl1I8fXrnSq16\nxJ28e2Ch1mdB9kL7TuhPGunLu+fs1rXA+xIceakDuVqjNqZRd/KW0uosmHpJx2tXD47reV32Mukl\neM8QIS91IFdr1MY0+k7eElqcBeUO3dECRHiECHmpA7laozamKDt5t+BfZqQ/rUh36PIlNw36vSbP\nM64kvQTvESLkpQ7kas1mivggIkJnvp7H33OtEtIQ9bp5OZqDPfTOSymjHVOvXG1WPJqUvfQ8/p5r\nldIrRMyIDvYw4vGPeEw9crVZ8YhS9sCX5z02qfGGOI97FFukIWp9rwJ5sedSc7WZouhB41dbWoiT\n9FxrL73uDcyYF2pS6f2n3k1LO6ZRKMnVuf42UxQ9aHzfoMfNw5EDRJSEqJaZ8kKO0t8fk6OVQ0nU\nXMnfv5PjlL/NFPEkkelVw+gBIvgYS4JxDr1ct4RroA8F4L/TmZ58pf561Rk1V2lTOsef+t3oO3mZ\nn398fvj0+urw1RuvH/9ei7ZDl8dvf/No+AARdLPygxdOyMu3775v6iV6Xoj0gZN78LA/5OoV6T6n\nJ08fV/tT/yUJibyTl/np0cPD1y/k8Kgl9SLHSJvhTvFZ4sTaS+S8EGlTyu1pQq505FO3Gn/qV2fY\nyUtQRz4lYA+5HbrRAmTdmGbJC5E+sHJPd5ErHdmYavypX51hJy9Bl4lcfO6ScQ+5HbqRLrn5ZmUL\nL9HzQqQPrNzPkq4EWvibIVc0+P5c7phL/G2miBeKTK8aItykzL2CYkUv1y1JG1OuFr4yaLW5MCVi\nrvi9pGr86f/yJVuTR6FXDaMHKA1Pq2Ps5bolXAMPehDx5kb5EniL5i6Jmqtaf5spih407ty5m3CW\njBygNDxbZ6laZspL6kwbWw8qS6LmqtbfZop4kqjwjtMeP9QRf52BKbl0tmDGvHBj4MGbL3sRPVfn\n+ttMUfSg8fH3+D2jEV1tndFaMKKDPfTMSykjOu2Rq82KR5Syh57H33OtEnqERzKag72MePyjHVOv\nXKkVz7CTt8X9pdwOXX5Dr1EC1Cs8DPJSB3K1Rq2YpETfycvPfy0vy1Mv2iY4j1BLeoaHQV7qQK7W\nqI0p+k7eVu9GmNuhO8ru3PRGY4/wMMhLHcjVGvUnEX0nL5/9rH+g2g7d48fsXN91O9syFBgOj3Xd\np0Be6kCu1mymyPMsci7c3SlsvfD0JPeLlLwU2wpPD+fikZdSPH1652qzak8x58LH3Oss4/lRzh6X\n2FsgL3Zceq42UxQtaHzZ2VOm1wY4r0vsLZAXOy49V5spihS0VGhPeq8pd9L2vsTeoreLGrzyUkrv\nYxstV5uV95ZzLunz4Z5C0/eIbo18zj/iWR55sQG5mqAxeYasx+W2/I1s+vto90MY5MUG5CrTmKLs\n5E0vx3uELN2he3w5t+EDUQanV43ngLzUgVytUauPsJPXI2Ryhy6tbX25LZ/r0/C8CVkC8lIHcrVG\nbUwj7+SVgnuGLPXCmwnp95lqobMYX75HCU4K8lIHcrVGbUwj7uSVl6AeN+nYy/EB+OIpCx0Hfe0c\n0k8oTcdoz/VLQF7qQK7WbKaIi/KERI92k46PZ8+Zh46Z/n/5/J4Hhcm7rlqQlzqQq1dspsgjaLmO\nv/cH1gr6IW95oeOn49wKCw36XstXXTzY8tKK0fNSCnK1RLfwElm0xxit42+FYmvQv6NQjVSLNbJm\njzFaXkpBrpYM15goWKOKTs9qucHHP2oNLZEueoyR81IKcrVmszEBAIAHaEwAgOFAYwIADAcaEwBg\nONCYAADDgcYEABgONCYAwHCgMQEAhgONCQAwHGhMAIDhQGMCAAwHGhMAYDjQmAAAw4HGBAAYDjQm\nAMBwoDEBAIYDjQkAMBxoTACA4UBjAgAMBxoTAGA4so0p/biY6MPy42zgRQde6oC/JdnGJD+lIfqw\nQs4bfVgh540+eiPXjz5qyc7AC6QfGxNtpB+EaAW86MBLHfC3JDuD1QLeWNdhPZ8X1nVYz+eFVx1e\n61pjVUd2huMC13fll8NhJYqBFx14qQP+lqgzfPnF4fD2mzfj40/kd2NhJYqAFx14qQP+1qgzkBwW\ndeu2/K4NdOfe4u79KaxEET28aNBHQlt/LHQ0LxHzUkoPfxoj50qdoXUHv/PWncVoiZUoooWXU8Gg\nB+O999453ly0ZHQvKVHzUkoLf9FzlZ3htasHx9GC9MAtitjCShRj7YUeaHR8uYCMHiDG2ktK5LyU\nYu0veq6yM1gtoJGe/b7/4bsml5SMdR3W8zEUEJqXnEgX/HKsJdZ1WM+XEjkvpbRaN2qusjNYLaBB\n3Zr2PPBlecv7B9Z1WM+XQk7oLCbnHzlAjPV8KZHzUkrLdSPmKjuD1QIS6tocKjr70RpPnj4OEzTr\n+cgHn9XoT3lWI0YOEGM9HxM9L6VYrxs9V9kZrBaQ8NmP+fnH58d16M8WWNfRYr5TD7KRA8RYz8dE\nz0sp1utGz1V2BqsFJNS5aV7eek+X53QGpK/RGdEa6zqs5+NwUIjSvzP0d7oMp3EqaHuwrsN6PiZ6\nXkqxXjd6rrIzHBdouBOVZNDgS8z0kt0SK1GMtZc0OLkAaV+vZXQvkqh5KcXaX/RcqTO02FfhhZUo\nAl504KUO+FujzuC1E7UFVqIIeNGBlzrgb406Azq4DrzowEsd8LcmO4P1TlQvrEQx8KIDL3XA35Ls\nDFYLeGNdh/V8XljXYT2fF151eK1rjVUd2RmsFvDGug7r+bywrsN6Pi+86vBa1xqrOrIzWC3gjXUd\n1vN5YV2H9Xxe5OqwfEldI7duNHJ17PW3nuEluQWiYV2H9XxeWNdhPZ8XaR38KzBy0N4fa+BvSdbE\njKIssJ7PC+s6rOfzguvg3eU8Pvrw/uK/rd8XCv6WZE0cJzDcieqF9Q8cXnRm88JDnt3pv/l7lr+v\nB39L1GTOsq/ip0cPD1+/EEDjqzdel9/eDbzozOKFSB9U9HtkGvCXx8qf2phm2YlKRbMAGrXAi84s\nXoitsz0Df3ms/KlfnaWDl3TmPcCLzixeiPSBlXv3AvjLY+VPbUzELDtRP72+Og4r4EVnFi8lT0Xo\nLVg+e/H9D+BvhZW/7Hd48uhY12E9nxfWdVjP50X6wKIhz/rpS+C5pyrnAH9LsiZmE2WF9XxeWNdh\nPZ8XXEf68jad+dP3zaZx6uXuvcDfkqyJ2URZYT2fF9Z1WM/nRVpH+tJ2Ok49qM4B/pZkTcwoygLr\n+bywrsN6Pi+0OtJ3e9Te1N8Cbd2IaHWc4y9rQlsgItZ1WM/nhXUd1vN54VWH17rWWNWRneG4wEQ7\nUa2AFx14qQP+lqgzzLivwgJ40YGXOuBvjTrDjDtRLYAXHXipA/7WqDOgg+vAiw681AF/a7IzzLYT\n1Qp40YGXOuBvSXYGqwW8sa7Dej4vrOuwns8Lrzq81rXGqo7sDFYLeGNdh/V8XljXYT2fF151eK1r\njVUd2RmsFvDGug7r+bywrsN6Pi+86vBa1xqrOrIzWC3gjXUd1vN5YV2H9XxeeNXhta41VnVkZ7Ba\nwBvrOqzn88K6Duv5vPCqw2tda6zqyM5wXAA7UVfAiw681AF/S9QZsK9CB1504KUO+FujzoCdqDrw\nogMvdcDfGnUGdHAdeNGBlzrgb012BuxE1YEXHXipA/6WZGewWsAb6zqs5/PCug7r+bzwqsNrXWus\n6sjOwAvQe/Xyu89FG3TsVqIYeNGBlzrgb0l2Bl5glmGFnDf6sELOG330Rq4ffdSSnSF9n97og2qx\nAl504KUO+FuSbUwAAOAFGhMAYDjQmAAAw4HGBAAYDjQmAMBwoDEBAIYDjQkAMBxoTACA4UBjAgAM\nBxoTAGA40JgAAMOBxgQAGA40JgDAcKAxAQCGA40JADAcaEwAgOFAYwIADAcaEwBgOLKNid/q89mz\nb+S3Lhp40YGXOuBvSbYxyTcX53HvvXcuWqD0AS83SB/wsg/p7dL9nWxMH314fyUrHfSRLZckDV50\n4KUO+FtysjFJSEr6+VE87rx1R/6vUwIvOvBSB/wtWZt4yVHA9V355QWaNLrsnJkSL9//8B28KFxi\nXkop8XdJuVIb05dfHA5vv3kzPv5EfleHOngqjCTOhvQiP09LjidPHy+czBok6aWES8hLKdKfzJEc\nl5ArtTGRHBZ167b8bh46I9LNulnDlnqhIcNROmb2grzsB7laozYm2cH3Qt2bZc30XFh6kWeyUyO9\nDJ/Zy15mzUsp0p/MzakxY67UxkS8dvXgOM6Fuvdssgh40YGXOuBvSbYxcZE1zCaLgBcdeKkD/pZk\nTViIIlJZMzwHhhcdeKkD/pZkTViJImaRRcCLDrzUAX9LsiYsRRHpy8ORsa4BXnRm8VKKda3R/WWP\nukVR/NIwvZIQFXjRgZc64G9J1sRR1ImdqHuhfSstfgA9aeElvfSOSgsvM+SllBb+IudKPWK5r8KS\nyF1cepH7Sc4d0fehSC+WRM5LKdKfzMe5I3Ku1MZ07k7eEiKfBa126J4a0UBe6kCu1qhHKzu4NXwW\npDfHioT0Is9QtYPf8iK6F2ui5qUU6U/monZEzJXamIjanahbkCASRYGLBrzowEsd8Lck25haX/61\nnr8VrY+79fytaH3cref3pnV9ree3JnukrQvhy/No78YHLzrwUgf8LcmaaC2KnvvS/PRnJOBFB17q\ngL8lWROtRfHzXnpJMxLwotPaCz+wonkpBf6WZE20FkX0WMOaHsfcYw1rWh4zbRRM36SfnpZEeoWp\nBPhbkjVxLMJ4J6qk5Q8j5ecfn8svnQ286LT0wj7k8L5fAn91bPlT0y/3VbSCBf306GGT8e277x++\nfjE/ja/eeF0uvxvpRe4XsRjpbl1Zj9Vo7cUSfmqrDTrzy9p6jNb+ZCZqBt/01sbI/tTG1HInbwoL\n4oNsPWrptUOXhzz+VqOWlnlJf0teG7IWj1FL71ylQ9biMTTUr8oO3gqWIzuq1SjpzHuQXuTZyWLg\nimkJOZEPJh4jn/H3IP3JTNSMqa6YiJY7URkW1BKWYQW86LT0Ih9QPDzvkcBfHaf8ZdPf48HRYw1r\nehxzjzWsaXnMdOaXDyr62kzA35KsiZaiCP6t8Ui/v0PAi05rL/QKTkQvpcDfkqyJ1qK4i4/euSXw\nogMvdcDfkqyJ1qL4ptzoG70k8KIDL3XA35KsidaiWs/fitbH3Xr+VrQ+7tbze9O6vtbzW5M90mMh\njXaiRr2PQsCLDrzUAX9L1MYk91VYw3t1olxWMtKL3DNSOyK+0yAhvVgTNS+lSH8yF7UjYq7UxtRy\nJy8R7bKS6bVDNxrISx3I1Rr1aGUHt4Q6OEmKdFnJSC/yzFQz+Kw2gxdLyE1UL6VIfzIbNSNqrtTG\nRLTYiTrDRxfDiw681AF/S7KNqcXlH79kSZ08KvCiAy91wN+SrAlrUZE/FTTFugZ40ZnFSynWtUb3\nlz1qy6IiX1JK4EUHXuqAvyVZE5aieK5oH1OsAS868FIH/C3JmrASxW/0FVlSCrzowEsd8Lcka+Io\nqmInKl1C8s236JJS4EUHXuqAvyVqY5L7KvaSPsedQRIjvcg9I6dG+u6UM3vZy6x5KUX6k7k5NWbM\nldqYanbykqjZJDFWO3Rn9oK87Ae5WqM2JtnBS0jPejQocLMhvcgzlxx0Jks/z+tSvJRwCXkpRfqT\nOZLjEnKlNiaidCcq/eYyP7elQX+P+hJlCaVe0uf88PKKS8tLKaX+LiVX2cbEhWvQbymnz2t5zChI\nAi868FIH/C3RTRxeiSIhfPkoxdCgjh3p7RRqgRcdeKkD/pacbEzauBQ5GtIFvNwgXcDLPqSzS/eX\nbUwkIr3hdmlicsCLDrzUAX9Lso0JAAC8QGMCAAwHGhMAYDjQmAAAw4HGBAAYjv8BQJY77djkFokA\nAAAASUVORK5CYII=")) image_1: pin names not known
  or or_4 (V, X, Y);
  // Callout #(.background("#b7e1eb71"), .dx(-15), .dy(-20), .foreground("#236494"), .halign("center"), .style("margin: 4px;"), .text("2-input\nOR gate"), .valign("top")) callout_14: pin names not known
  nor nor_1 (out_40, in_8, in_11);
  // Callout #(.background("#b7e1eb71"), .dx(-15), .dy(-20), .foreground("#236494"), .halign("center"), .style("margin: 4px;"), .text("2-input\nNOR gate"), .valign("top")) callout_15: pin names not known
  // Callout #(.background("#b7e1eb71"), .dx(-20), .dy(-19), .foreground("#236494"), .format("wrapped"), .halign("center"), .style("p-margin: 0px;"), .text("Each output bit is the result of ANDing the corresponding input bits."), .textwidth(228), .valign("base")) callout_16: pin names not known
  and wide (wide_out, not_1_out, in_22[1], not_2_out, in_22[3], in_22[4]);
  LED led_1 (.in(wide_out));
  // Callout #(.background("#b7e1eb71"), .dx(-15), .dy(-20), .foreground("#236494"), .halign("center"), .style("margin: 4px;"), .text("Both circuits work the same: the LED\nturns on only when  the input is 11010."), .valign("top")) callout_17: pin names not known
  or or_5 (out_46, in_24, callout_9_p1);
  and and_5 (out_49, in_27[0], in_27[1]);
  // Probe on or_3_out
  // Callout #(.background("#b7e1eb71"), .dx(-18), .dy(14), .foreground("#236494"), .format("wrapped"), .halign("center"), .style("p-margin: 0px;"), .text("8-bit 3-input AND gate"), .textwidth(107), .valign("base")) callout_18: pin names not known
  assign out_2 = P_2 & Q_2 & R;  // AND_Gate and_6, 8 bits wide
  // Callout #(.background("#b7e1eb71"), .dx(20), .dy(-20), .foreground("#236494"), .halign("center"), .style("margin: 4px;"), .text("Same for \nerror inputs"), .valign("top")) callout_19: pin names not known
  // Callout #(.background("#b7e1eb71"), .dx(-20), .dy(-20), .foreground("#236494"), .format("wrapped"), .halign("right"), .style("p-margin: 0px;"), .text("pull-down-only output is floating when not driving output low"), .textwidth(146), .valign("top")) callout_20: pin names not known
  xor xor_3 (out_38, in_3, in_6);
  // Callout #(.background("#b7e1eb71"), .dx(-15), .dy(-20), .foreground("#236494"), .halign("center"), .style("margin: 4px;"), .text("2-input\nXOR gate"), .valign("top")) callout_21: pin names not known
  xnor xnor_1 (out_41, in_9, in_12);
  // Callout #(.background("#b7e1eb71"), .dx(-15), .dy(-20), .foreground("#236494"), .halign("center"), .style("margin: 4px;"), .text("2-input\nXNOR gate"), .valign("top")) callout_22: pin names not known
  and \medium  (medium_out, in_21[4], in_21[3], ~in_21[2], in_21[1], ~in_21[0]);  // AND_Gate
  LED led_2 (.in(medium_out));
  and and_7 (out_44, out_46, in_25);
  and and_8 (out_50, in_27[0], in_27[1]);
  // Callout #(.background("#b7e1eb71"), .dx(-20), .dy(-20), .foreground("#236494"), .format("wrapped"), .halign("right"), .style("p-margin: 0px;"), .text("pull-up-only output is floating when not driving output high"), .textwidth(134), .valign("top")) callout_23: pin names not known

  // Notes on the sheet:
  //   # Overview of Common Gates
  //   Common mutliple-input logic gates are AND, OR, NAND, NOR, XOR, XNOR.
  //   Each one takes several inputs, combines these using the rules of Boolean logic, and outputs the result.
  //   ## Multiple Inputs and Multi-Bit Gates
  //   Use the ***number of inputs*** attribute to allow more than two inputs. All inputs are combined using the usual rules of Boolean logic to produce a single output result. Use the *data bits* attribute to allow a gate to operate on multiple bits simultaneously.
  //   **Keyboard shortcut** 👉To change the *number of inputs* for a gate, select it and type a number. Or select several gates to change them all.
  //   **Keyboard shortcut** 👉To change the *data bits*, select some gates, hold the option key (⌥) or Alt key, and type a number.
  //   ## Visuals
  //   The ***gate size*** attribute allows a choice of *narrow*, *medium*, or *wide*. Gates can be rotated to face any direction using the ***facing*** attribute. A gate can be given a ***label***, which will follow the gate if it is moved or copied.
  //   **Keyboard shortcut** 👉Select some gates, then use arrow keys (↑→↓←) to rotate them so they face a different direction.
  //   ## Negated Inputs
  //   Any of the inputs can be configured to be active-low. This behaves exactly as if there were a NOT gate attached to that input, but used judiciously, negated inputs can make circuits more compact and easier to undertand.
  //   ## XOR & XNOR Multiple-Input Behavior
  //   Multi-input XOR and XNOR gates can be confusing. Normally, XOR outputs a 1 when an *odd number of inputs* are 1, and XNOR does the opposite. This "parity" behavior is most typical. For XOR and XNOR gates with more than two inputs, the ***multiple-input behavior*** attribute allows for a different, less common behavior, where XOR outputs a 1 when *exactly one input* is a 1, and XNOR does the opposite. 
  //   **Suggestion** 👉 Don't use multi-input XOR and XNOR gates. For parity calculations, use the ***Even Parity*** or ***Odd Parity*** gates instead. For *exactly-one* calculations, which are less common, consider building a circuit from a ***Bit Adder*** and a ***Comparator*** (found under ***Arithmetic***).
  //   ## Errors, Unconnected, and Floating Inputs
  //   As a convenience, any input left unconnected is ignored: if there is no wire or other connection to the input, the simulator acts as if the input did not exist at all. So a 5-input gate with only two inputs connected behaves just like a 2-input gate. This doesn't match physical circuits or more realistic simulators, where such inputs would be considered *floating*, but it makes editing a circuit a little more forgiving. If all inputs are unconnected, the output is an error. If only one input is connected, the behavior depends on the gate type. To enable a more strict simulation behavior, treating unconnected inputs as floating values, go to ***Project > Options > Simulation***.
  //   ## Output Driver Option
  //   Normally, gates use **push-pull** outputs: they actively output either 1 or 0 at all times, as long as the inputs are well defined. The ***Output Driver*** attribute allows for two other behaviors. 
  //   * With a **pull-up-only** output driver (equivalent to open-emitter/open-source) a gate can actively output 1, but instead of outputting 0 it will produce a floating (z) output. 
  //   * With **pull-down-only** output driver (equivalent to open-collector/open-drain), a gate can actively output 0, but instead of outputting 1 it will produce a floating (z) output. 
  //   This allows creation of *wired-OR* and *wired-AND* busses. ***Pull Resistor*** (found in the ***Analog*** library) can be useful for these too.
  //   ## Gate Shapes and International Standards
  //   Different standards bodies have adopted different shapes for  common gates. In **Logisim > Settings > International** you can choose from **ANSI/IEEE Standard 91a-1991** (curved, distinctive shapes commonly used in computer science textbooks and educational materials), **IEC 60617-12** (rectangular, uniform shapes often used in professional settings and engineering), and **DIN 40700** (an older, less common standard).
  //   or_3 drives only 1 and floats otherwise
  //   and_3 drives only 1 and floats otherwise
  //   xor_2 drives only 1 and floats otherwise
  //   and_4 drives only 1 and floats otherwise
  //   AND
  //   and_5 drives only 0 and floats otherwise
  //   OR
  //   NAND
  //   and_8 drives only 1 and floats otherwise
  //   NOR
endmodule

module Multi_bit_Gates (
  input  [7:0] EightBitInput,
  input  [7:0] in_2,
  input  [7:0] in_3,
  input  [7:0] in_4,
  input  [7:0] in_5,
  input  in_6,
  input  in_7,
  input  in_8,
  input  in_9,
  input  in_10,
  input  in_11,
  input  in_12,
  input  in_13,
  output [7:0] EightBitOutput,
  output [7:0] out_15,
  output [7:0] out_16,
  output out_17
);

  assign EightBitOutput = ~EightBitInput;  // NOT_Gate not_1, 8 bits wide
  assign out_15 = in_2 ^ in_3;  // XOR_Gate xor_1, 8 bits wide
  assign out_16 = ~(in_4 ^ in_5);  // XNOR_Gate xnor_1, 8 bits wide
  or or_1 (out_17, in_6, in_7, in_8, in_9, in_10, in_11, in_12, in_13);

  // Notes on the sheet:
  //   Multi-bit gates can help simplify your circuits.
  //   For example, here's an **8-bit NOT gate**. It looks exactly like a regular NOT gate, but the "data size"  property 
  //   is set to 8 in the properties panel at the lower left of the window. Try it! Use the poke tool to change the input.
  //   Similarly, here is a **8-bit two-input XOR gate**. It is really eight separate two-input XOR gates, each 
  //   working on one pair of input bits to produce one bit of output.
  //   Multi-bit gates can help simplify your circuits.
  //   For example, you can do an eight-way pair-wise 
  //   "equality" comparison using a single XNOR gate to compute 8 results!
  //   By contrast, here is a 1-bit eight-input OR gate. This is just a single OR operation
  //   computed across all the inputs to produce a single bit of output.
endmodule
