// Logisim project help.circ as structural Verilog: 5 circuits, main circuit Common Gates - Basics
module NOT_Gate_Demo (
  input  in_1,
  input  [3:0] in_2,
  input  in_3,
  output out_4,
  output [3:0] out_5,
  output out_6
);

  wire not_1_out, not_4_out, not_5_out, not_6_out;

  // Callout #(.dx(40), .dy(40), .halign("center"), .style("margin: 4px;"), .text("input"), .valign("base")) callout_1: pin names not known
  not not_1 (not_1_out, in_3);
  not not_2 (out_4, in_1);
  assign out_5 = ~in_2;  // NOT_Gate not_3, 4 bits wide
  not not_4 (not_4_out, not_1_out);
  not not_5 (not_5_out, not_4_out);
  // Callout #(.dx(-31), .dy(41), .halign("center"), .style("margin: 4px;"), .text("ouput"), .valign("base")) callout_2: pin names not known
  // Callout #(.dx(-62), .dy(41), .halign("center"), .style("margin: 4px;"), .text("4-bit NOT gate"), .valign("base")) callout_3: pin names not known
  not not_6 (not_6_out, not_5_out);
  xor xor_1 (out_6, in_3, not_6_out);
  // Image #(.image("PNG:\niVBORw0KGgoAAAANSUhEUgAAAVQAAAFUCAYAAAB7ksS1AAAMPmlDQ1BJQ0MgcHJvZmlsZQAASImV\nVwdYU8kWnluSkJDQAghICb0JIlICSAmhBZDebYQkQCgxBoKKHVlUcC2oWMCGrooodpodsbMo9r5Y\nUFDWxYJdeZMCuu4r3zvfN/f+958z/zlz7twyAKif4IrFOagGALmifElMsD8jKTmFQeoGCKABKjAH\nCJeXJ2ZFRYUDaIPnv9u7G9Ab2lUHmdY/+/+rafIFeTwAkCiI0/h5vFyIDwKAV/HEknwAiDLefGq+\nWIZhA9oSmCDEC2U4Q4GrZDhNgffKfeJi2BC3AqBC5XIlGQCoXYY8o4CXATXU+iB2EvGFIgDUGRD7\n5OZO5kOcCrEN9BFDLNNnpv2gk/E3zbQhTS43Ywgr5iI3lQBhnjiHO/3/LMf/ttwc6WAMK9iomZKQ\nGNmcYd1uZU8Ok2EqxL2itIhIiLUg/iDky/0hRimZ0pB4hT9qyMtjw5oBXYid+NyAMIgNIQ4S5USE\nK/m0dGEQB2K4QtBpwnxOHMR6EC8U5AXGKn02SSbHKGOh9ekSNkvJn+NK5HFlsR5Is+NZSv3XmQKO\nUh9TK8yMS4SYArFFgTAhAmI1iB3zsmPDlD5jCjPZEYM+EmmMLH8LiGMEomB/hT5WkC4JilH6l+bm\nDc4X25Qp5EQo8f78zLgQRX2wVh5Xnj+cC3ZZIGLFD+oI8pLCB+fCFwQEKuaOdQtE8bFKnQ/ifP8Y\nxVicIs6JUvrjZoKcYBlvBrFLXkGsciyekA8XpEIfTxfnR8Up8sQLs7ihUYp88GUgHLBBAGAAKWxp\nYDLIAsL23oZeeKXoCQJcIAEZQAAclMzgiER5jwgeY0Eh+BMiAcgbGucv7xWAAsh/HWIVRweQLu8t\nkI/IBk8hzgVhIAdeS+WjREPREsATyAj/EZ0LGw/mmwObrP/f84Psd4YFmXAlIx2MyFAf9CQGEgOI\nIcQgoi1ugPvgXng4PPrB5owzcY/BeXz3JzwldBAeEa4TOgm3JwmLJD9lORZ0Qv0gZS3SfqwFbgU1\nXXF/3BuqQ2VcFzcADrgLjMPCfWFkV8iylXnLqsL4SftvM/jhbij9yE5klDyM7Ee2+Xmkmp2a65CK\nrNY/1keRa9pQvdlDPT/HZ/9QfT48h/3siS3EDmBnsZPYeewI1gAY2HGsEWvDjsrw0Op6Il9dg9Fi\n5PlkQx3hP+IN3llZJfOcap16nL4o+vIF02TvaMCeLJ4uEWZk5jNY8IsgYHBEPMcRDGcnZxcAZN8X\nxevrTbT8u4Hotn3n5v8BgPfxgYGBw9+50OMA7HOHj3/Td86GCT8dqgCca+JJJQUKDpcdCPAtoQ6f\nNH1gDL9eNnA+zsANeAE/EAhCQSSIA8lgIsw+E65zCZgKZoJ5oASUgWVgFVgHNoItYAfYDfaDBnAE\nnARnwEVwGVwHd+Hq6QIvQB94Bz4jCEJCaAgd0UdMEEvEHnFGmIgPEoiEIzFIMpKKZCAiRIrMROYj\nZUg5sg7ZjNQg+5Am5CRyHulAbiMPkR7kNfIJxVAqqo0aoVboSJSJstAwNA6dgGagU9BCtBhdgq5B\nq9FdaD16Er2IXkc70RdoPwYwVUwXM8UcMCbGxiKxFCwdk2CzsVKsAqvG6rBmeJ+vYp1YL/YRJ+J0\nnIE7wBUcgsfjPHwKPhtfjK/Dd+D1eCt+FX+I9+HfCDSCIcGe4EngEJIIGYSphBJCBWEb4RDhNHyW\nugjviESiLtGa6A6fxWRiFnEGcTFxPXEP8QSxg/iY2E8ikfRJ9iRvUiSJS8onlZDWknaRjpOukLpI\nH1RUVUxUnFWCVFJURCpFKhUqO1WOqVxReabymaxBtiR7kiPJfPJ08lLyVnIz+RK5i/yZokmxpnhT\n4ihZlHmUNZQ6ymnKPcobVVVVM1UP1WhVoepc1TWqe1XPqT5U/UjVotpR2dTxVCl1CXU79QT1NvUN\njUazovnRUmj5tCW0Gtop2gPaBzW6mqMaR42vNketUq1e7YraS3WyuqU6S32ieqF6hfoB9UvqvRpk\nDSsNtgZXY7ZGpUaTxk2Nfk265ijNSM1czcWaOzXPa3ZrkbSstAK1+FrFWlu0Tmk9pmN0czqbzqPP\np2+ln6Z3aRO1rbU52lnaZdq7tdu1+3S0dFx0EnSm6VTqHNXp1MV0rXQ5ujm6S3X3697Q/TTMaBhr\nmGDYomF1w64Me683XM9PT6BXqrdH77reJ32GfqB+tv5y/Qb9+wa4gZ1BtMFUgw0Gpw16h2sP9xrO\nG146fP/wO4aooZ1hjOEMwy2GbYb9RsZGwUZio7VGp4x6jXWN/YyzjFcaHzPuMaGb+JgITVaaHDd5\nztBhsBg5jDWMVkafqaFpiKnUdLNpu+lnM2uzeLMisz1m980p5kzzdPOV5i3mfRYmFmMtZlrUWtyx\nJFsyLTMtV1uetXxvZW2VaLXAqsGq21rPmmNdaF1rfc+GZuNrM8Wm2uaaLdGWaZttu972sh1q52qX\naVdpd8ketXezF9qvt+8YQRjhMUI0onrETQeqA8uhwKHW4aGjrmO4Y5Fjg+PLkRYjU0YuH3l25Dcn\nV6ccp61Od0dpjQodVTSqedRrZztnnnOl87XRtNFBo+eMbhz9ysXeReCyweWWK911rOsC1xbXr27u\nbhK3Orcedwv3VPcq95tMbWYUczHznAfBw99jjscRj4+ebp75nvs9//Jy8Mr22unVPcZ6jGDM1jGP\nvc28ud6bvTt9GD6pPpt8On1Nfbm+1b6P/Mz9+H7b/J6xbFlZrF2sl/5O/hL/Q/7v2Z7sWewTAVhA\ncEBpQHugVmB84LrAB0FmQRlBtUF9wa7BM4JPhBBCwkKWh9zkGHF4nBpOX6h76KzQ1jBqWGzYurBH\n4XbhkvDmsejY0LErxt6LsIwQRTREgkhO5IrI+1HWUVOiDkcTo6OiK6OfxoyKmRlzNpYeOyl2Z+y7\nOP+4pXF3423ipfEtCeoJ4xNqEt4nBiSWJ3YmjUyalXQx2SBZmNyYQkpJSNmW0j8ucNyqcV3jXceX\njL8xwXrCtAnnJxpMzJl4dJL6JO6kA6mE1MTUnalfuJHcam5/GietKq2Px+at5r3g+/FX8nsE3oJy\nwbN07/Ty9O4M74wVGT2ZvpkVmb1CtnCd8FVWSNbGrPfZkdnbswdyEnP25KrkpuY2ibRE2aLWycaT\np03uENuLS8SdUzynrJrSJwmTbMtD8ibkNeZrwx/5NqmN9BfpwwKfgsqCD1MTph6YpjlNNK1tut30\nRdOfFQYV/jYDn8Gb0TLTdOa8mQ9nsWZtno3MTpvdMsd8TvGcrrnBc3fMo8zLnvd7kVNRedHb+Ynz\nm4uNiucWP/4l+JfaErUSScnNBV4LNi7EFwoXti8avWjtom+l/NILZU5lFWVfFvMWX/h11K9rfh1Y\nkr6kfanb0g3LiMtEy24s912+o1yzvLD88YqxK+pXMlaWrny7atKq8xUuFRtXU1ZLV3euCV/TuNZi\n7bK1X9Zlrrte6V+5p8qwalHV+/X89Vc2+G2o22i0sWzjp03CTbc2B2+ur7aqrthC3FKw5enWhK1n\nf2P+VrPNYFvZtq/bRds7d8TsaK1xr6nZabhzaS1aK63t2TV+1+XdAbsb6xzqNu/R3VO2F+yV7n2+\nL3Xfjf1h+1sOMA/UHbQ8WHWIfqi0HqmfXt/XkNnQ2Zjc2NEU2tTS7NV86LDj4e1HTI9UHtU5uvQY\n5VjxsYHjhcf7T4hP9J7MOPm4ZVLL3VNJp661Rre2nw47fe5M0JlTZ1lnj5/zPnfkvOf5pgvMCw0X\n3S7Wt7m2Hfrd9fdD7W7t9ZfcLzVe9rjc3DGm49gV3ysnrwZcPXONc+3i9YjrHTfib9y6Of5m5y3+\nre7bObdf3Sm48/nu3HuEe6X3Ne5XPDB8UP2H7R97Ot06jz4MeNj2KPbR3ce8xy+e5D350lX8lPa0\n4pnJs5pu5+4jPUE9l5+Pe971Qvzic2/Jn5p/Vr20eXnwL7+/2vqS+rpeSV4NvF78Rv/N9rcub1v6\no/ofvMt99/l96Qf9Dzs+Mj+e/ZT46dnnqV9IX9Z8tf3a/C3s272B3IEBMVfClf8KYLCh6ekAvN4O\nAC0ZADrcn1HGKfZ/ckMUe1Y5Av8JK/aIcnMDoA7+v0f3wr+bmwDs3Qq3X1BffTwAUTQA4jwAOnr0\nUBvcq8n3lTIjwn3AJs7XtNw08G9Msef8Ie+fz0Cm6gJ+Pv8LU3t8Q4nh6JIAAAAGYktHRAD/AP8A\n/6C9p5MAAAAJcEhZcwAALiMAAC4jAXilP3YAAAAHdElNRQfoAggFDAe9rVCEAAAAGXRFWHRDb21t\nZW50AENyZWF0ZWQgd2l0aCBHSU1QV4EOFwAAIABJREFUeNrsXVdzXMeV/jA5B0xAzoEEA0BREoMC\nFSxRtmTLsl2u2i3v+/4pv+zDVm3ybq2tVTAtWRIFUswJIDJAZGAwOWfsg+t09e25M3MHMwOAtG4V\nSxSBe2/f7tOnT/jOd1r29/f3IVwy//R3d7W0tDRtPvhnN+Mdcs8vdx23tRbH/rzIYi1z3ojrxz16\nPNdco3Tx6M+LOCn05yBCXSwWm/bsanPe0tIClUrVlHkpFotNW2+l45Z7/1HLYj1r2mwFW2leqo27\n2nrXe//fi35QKVmkozqFXxQrtFYFcFzm/EVb7+MsL0dlrfKy+eN613/VZKEWCoUXboOo1Wrs7++j\npaWF/fcgFqoo1PzJVosVSc+hOS938tNzax1zrd/WDMXBz/lxG5sSa0WlUh1IXpqpTJXIi1qtLhtu\n4u8v991qtbrqerxoVmq5OatZodLEFAoFpFIpxONxRCIR5PP5prmZh3kVi0UYDAY4HA6YTCbo9fqa\nFVQikUAoFEIqlUI+n2f37e/vQ6PRwGw2w2azwWq1sn+v9Gx+c6TTaUSjUcTjcaTTaTbn+/v7UKvV\nMBgMsNlssNvtZQW9HmUVDAYRCoWQz+cbpjho7DabDU6nEzqdriblur+/j2w2i1AohHA4zDZxs5Ua\nrYvRaGRrajAYFK3pYYyrUCggk8kgkUggHA4jm81K5EWlUkGv18Pj8cBkMrE5pyufzyMejyMejyOZ\nTCKfz0OtVrP51ev1MJvNaG1tZd/NX9lsFsFgEPF4HLlc7lgcNPXOKx2cFosFbrcbOp1OkeuvqWSR\ntrS0IJfLIRAI4NmzZ1heXkYymYRGo3mulen+/j7y+TzcbjdGRkbQ3d2N1tZWplAruT/8z4PBIKan\np7G7u4tUKsWEuFAowGKxoLOzE4ODg7BYLMyiqfZs+lkkEsHi4iI2NjYQCATYSVkoFKDT6eByuTA6\nOgqz2czeW4/FR/cWi0Xk83msrKzg6dOnSKfTKBaLDYkbFotF6HQ6DA8PY2xsTHIYlNuE/MYvFotI\npVJYWFjA7OwsCoVCw8ZWbdwtLS1wu93o7u7G8PDwkStUfo8WCgWEw2Gsr69jfn4ekUiE7VE63J1O\nJ1555RV0dXUxOaf7s9ksNjc3sbq6it3dXaTTaWg0GhQKBezv78Nms6GrqwsTExPQ6/Ul1msikcDC\nwgLW1tYQj8dRKBQaesgf1UGl0WjQ19eHc+fOobW1taqsVlWoAJDJZLC5uYkHDx7ghx9+QDAYfCEs\n1EKhgKGhIeTzeRgMBtjtdmg0mpo2yNbWFq5fv47FxUVEo1HJz9xuN8bGxqDVatHf36/YQqU/fr8f\nd+/exczMDFZXVyWb22w2o6urCy0tLejr64NOp6t7c9O9xWIRuVwO09PT+NOf/oRkMskUSiMui8WC\nK1euwOv1wmAwwGAwKB53oVBALBbDgwcP8Pnnn1dMCDZ6g2k0GgwMDODMmTNwuVxwu90NnZd6Yp+5\nXA67u7t48uQJJicnsbGxIdn8arUaXV1d6OzsRFtbm0TZtrS0IJlMYmFhAbdv32ayrFKp2Pe1trZi\nfHwc/f39cDqdJWOJRqO4e/cu7t27h3A4jFwu90LEY1UqFS5evIj+/n52+FcLaWiqbbBsNovd3V08\nffoUk5OT2NraemHiI36/Hx0dHRgYGEA+n4der5e43XJWEr/5fT4f7t69i4cPHyIcDrMYs1qtRmdn\nJzKZDIaGhiSuNG+pltsg5HJPT0/j1q1bmJubQz6fZ79rtVoxNDSEkZER5HI52RhutVhgpXUvFAqY\nn5/HV199hXg83tC4mMvlgsfjwYULF+D1eivG3cSEyf7+PhKJBJ4+fYo///nPhxqvMxgM2N3dhVar\nxauvvnooFpKS0IxarWZe5Pz8PG7evImFhYWS9R4ZGcFHH30kkSOa33Q6jWfPnuHevXt49OgR/H6/\nJIbo8Xiwv7+PDz/8UPbwi8fjmJqawrfffotAIIBMJvNC6IeWlhbo9Xr8/Oc/Vxxe0ih5qEajgUaj\nYXEFOr1q2ahHabrLjbFYLEKlUkGj0VQM1lecPI0GBoMBWq2WBe3JnVKr1dDr9SXhkXIKRMzsU5yU\nLA16TqFQkLy32ncfZE1IkIxGI1KpFAqFAnOra1VicplxPrFTaa7LrZ9Op4PRaEQmk2m6lchbalqt\nlsXaj5tMq9Vqtkf5ZGuxWIRer2ex03JrpNPpWJxQpVKxGCodJkajsew+UalUMBgM0Ov1VWFGz4OO\nIMWp0+lqXm+NUqHiH3occXhKF4//t3KZT5rQagpEVMgkjLyyJiGvNm/8zyiRoNFoJPFRipeVOwga\nuSYqlQparRYqlYop1HreIcaQSaFWmxPeKqD7NBoNtFotcrkc2/TNkkd+fPTuo4ay8fLJrxcvD+LP\neFkqp5Bpn/MIErJSRTnm7+Vlvd54/nHQETS/lYytuhRqpVjf82jG14InFCdTTvnyYYJqMKdyCoSU\nqPgsPn4ounu8gmq0ABcKBeTzeTaGZsYrK1kA/CEjehji3B+GFXNYcVslMila+fx4ybUnWeHXslz4\ngOaU4ugkk4VCgSWolOqE5xlCJX5DLd+hqVWg+JfwQl6rJj+sixeUSidSJUET8bekHCnLLDfpdB/9\nnP5ebQzlSi9pfgmeRcq3UCgw4ZfzKg6qbOUs7HJzKneRxSN3aJDCpjmptlnpyuVyyOVyDMpVS8yx\nEcr0qBWEnLzxySf6GVmr9O+i9VjusCcZE11+tVpddX+LcyPqB9HLPU76oVrFYy1XQ/BParWaxViO\ni7lPC5rL5ZBOp2veDKSsstks0ul0iVLQaDTIZrNllQGd8tlslo2Bsp9ygkXjVavV0Gq1LOGg0Wgk\n8a1MJgO9Xs/iVTzEhZ97rVbLYrAHWQ+DwQCLxcLGzVtD+XwemUymrNVDuEcaM68QKPGXTqeRTqeR\nSqUksdByMVdKkCYSCWSz2b+7WnbC4JLM0bzr9XrkcjkmhxS7J1hXoVBg+Nly4QqKmVNcntAX9FyT\nyQSj0XgghUjGFi/DR1mZJSY58/k826ONkKm6FCpN1uDgIIPC0KIdpcAT/CedTmN+fh6Tk5MIhUJV\nK71EuBhl2m/cuMHiohRfUavVmJ+fx/LyMuLxeEkWMBKJYHZ2Fp9++ilWVlaYC13J5ReFzG6346OP\nPsJHH30keTb9fXd3F7///e9LXONisYgzZ87g0qVLcLlcMBqNimOgtCEvXrwItVqNRCIhQS/s7+9j\ndXUVU1NTWF1dhd/vl7zbZDKhtbUVFy9exNjYmARqwn/DN998g2+//bbEuimnUEk5hMNhPHz4ENls\n9li434e1+VOpFG7evImZmRkEAoESrCcB8H/729+WyLNWq4XX68XAwIBEqdEhabFYcObMGWi1WkxM\nTCCVSkGr1TIl3draisHBQbhcLsVKkN6h0+nQ3d2N0dFRTExMwGg0Mg/jKCxWPsGYSqWwvLyMubk5\nzM3NMSx5PXJVt0LVarXo6+vDxx9/jNHR0SM9hfhgfaFQQDQaxddff43p6WlEo1FFCpV3LwOBAO7e\nvYt/+Zd/QS6XK8nYp1IpxGIxZmHxz0gkElheXsbu7i5u3rypmBeBXODTp0/jgw8+wMsvv8zgUQSM\nj0ajWFpawhdffIGvvvoKiUSCbS66/+OPP8bQ0BBMJpOkuqVa9pWSUefOncPw8DCzhorFIrOcb926\nhXw+j3A4DL/fL3HjjUYjvF4v3n77bVy9ehV6vZ7NjUqlQjwex1dffYVPP/0Ua2triEQiLPmlZH1z\nuRxisViJ2/+iX+l0Gnfv3sUXX3yB1dVVZLNZ6PV69t+xsTG89tpr+MlPfoKenh5kMhnJftBqtXA4\nHAwZwh/sZrMZJ0+eRF9fH/Pm+D1M6Aa73a7IWOJDUlqtFl1dXbh06RJ+/etfw+l0MljVYStUHrqo\n1+sRiUQwOTmJ/f19PHv2jFUk1iNXmoMqUt7ioU3U0dHBXNGjtlDJVXE6nQzWpFTB8+GCeDyOvb09\nZDKZEgGoFP8jdziTySAcDsvW+lc6QROJBLRaLaxWKzweD1NKFALY29tDsViE3+9HJBJhY6P7o9Go\nYitOzNq2tLTAarXCbDZLrEuVSoVMJgO73Q6TycQOGDELr9PpYLfb0dbWBqPRKDlcQ6EQNBoNIpEI\n/H4/QqGQorCEksTfi3wVi0VEo1H4fD74fD5kMhkW6jGbzQwvbLfb4fV6mVzyayMX1ybPw2w2w2Qy\nlcgLv9f5kJ4SpUryYDAYYLVa0draCq/XyxJmR+nyU1zZ6XSyasNGJHcbEkPloSxywe9mC385bJxW\nq5VAmg4SgyXrjK/VV/J+Pg5bK6kML7giMQUF93kFyoO16XfqRWJQIkIuwVAtyUDjpXiw+Fw+SUd/\nlM5po+SpWmnxQTdqtWcoOThE5IKYyOMz93Lv4uPdIvyvnEzwyaiDjr2axUr/Fa3kwzgc6T2i50yH\nTKOUu6ZRA+VjiHydMG9VNGuixIXhiSHqWSwRg8g/t9bNp2TBRHIWOauMn29+TuXuacRJLrpK1ZSG\niKeVG6N4wImbqhI+tRFwnGoHbD1KtRo/bjVlzt8vokJE5AZZqCKrGb9e/H6shGapRSnWI09y1W/N\nhGFWSnTyc9yoq2EsJ7XiOQ/LvD9Idr+cgCt12+sdr5xC4ZUtD+w/rLltdEeBSkq1Uolfo761Ucpa\nNB6UWFyV8gvl8g8iVpR/N1n8oqei9FuOottAtaKb50WWm6ZQxQw0f8pSrFGE9tQ7IbxryVdoNJKg\nWaPRSLLkhxG6IJgJ8LfkWCqVYsqTYB5KSzUbpXAOEjY5iEtHVhgdGHL4RsKiHtT1pPiZ3Lh4CJIS\nxcjLPY1NDPHwcTvexRTvJ6VIVqeY5SfqTIPBwORdo9FAr9dLXPVyljA9u9Z9RmtCuYhGKySat0bS\nMfJjp6TnYezhpvPwpdNp+Hw+7O3tseSMEtaWahdhGp1OJ7xeL9xudwlb1EHr2Mmdslgs6Ovrw6VL\nl5DNZpu6IPx8aDQadHR0IJVKYX5+XkLfRwmrzc1NbG1t1Z3tPsyDQsllNpvhdDrR2dkJm80msQCJ\nvm99fR1bW1s1KQfKdNOaer1eibWnUqmQy+WwsbGBnZ0dpsBqWb94PI61tTX4fD5JUoi8nI6ODrS1\ntcFut0sYwgCw5OXa2hpCoZBEARApjEajwalTp9Df38++vVgswmg0YmBgAD09PTAajSVeQKFQQCKR\nwNLSEuO4VbIuNG6CwvX19cFisTRUNgqFAiKRCJ49e8YIhhqlUClJ19fXB4fDwea8mfKvaZZyIGB6\nIpHAzMwMpqamsLS0hEKhAK1WW7dCzWazsNvtGB0dxblz52C1WqHRaNh76934Wq0Wra2tOHv2LPue\nZsI8RKs6kUggGAxiY2MDyWRSkjTIZDIIBAJYWFhANpvF83zxEBvaACMjI4w2jTwcqkzz+/345ptv\n4PP5aorNt7S0wGAwoK2tDa+//jomJiYkCA2isbt+/ToymQyzNJVaZIVCAaFQCHfu3MHDhw8lsCWy\nLF999VWcP38eer2eQdDo21OpFNbW1vD1119jaWlJgnwoFovQaDRoa2vDlStXoNPpJIkqtVoNr9eL\n3t5e2Gy2Eu+AxjY5OYm5uTkmM9WUCc2Px+PB2NgYI2NvlDKise3u7uK7777D4uIiK35p1LMHBgbw\n3nvvSRLmzSyL1TRbOSSTSTx79gyPHj3CzMwM0um0JHt8kA1Ik+XxeJDNZuH1enHixImGThJZqAMD\nA8xSOqyrWCxiYWEBGxsbWFxcxNraGtt8tEHT6TTroPC8X/zmsVqt6OnpwZkzZ3D69GlJKKdYLGJ3\ndxfLy8sMC1tLKEGv18PlcuHUqVN47bXXShIkRNK8sLCAQCBQk9IoFouIxWKYnp7G9evXJQcdMT7Z\n7XZ0d3eju7sbVqtVgiRJpVKM0/Thw4clyT273Y5f/vKXOHv2LOt2wIcdjEYjLBYLwxyLFWrRaBSP\nHj3CnTt3GOVjpW/jiXgItnfp0iVFsdBalV4wGMSDBw/w8OHDhiaJisUi4vE4xsfH0dXVBavV2nRU\nQdNd/kwmg729PayurmJhYQGJRKJhJn00GoXdbpe4MfVubN4FJNoyr9d7qAqG3KB0Oo2trS3Mzc2V\nkKModXnE3z+OyUP+vUajES6XC729vaxQhL8cDgc8Ho/iklo+/KPT6WCxWNDT04OxsbESr2Bvbw9e\nr1e2jFoJ3ImszJmZGQZeJ5myWCw4deqU5BAUC0kikQjW1tYwOztbkpDyeDysiKajo0O2FUk5eaax\nURcGpS4/hefC4TA6OjokoP9GGl9UBDM9Pd2wgiB6jt1uRyQSObRy5aYrVAoKU0CbAtwHNbt5V4dA\n5DxwvxnKTQ7606wwiQjV4r+bh0zVolz53zvuXWx5fGWxWGSWnlqtRj6fRzKZZBaWku8QLRJ+Hvi1\nVRLXr+aKUtmuXq9nhR0iyUgl+r9K6021/BRK4El7lDSEJL4No9GIRCJR8j45jCaNW6fTwWAwNEVe\nePC/Xq+XHET1Gka8cXRYst702i8Rv9aIvuaiAL0ILVnKzZvIh1rLwaOEc/S4XUoy60ro5ModWNWq\nrMTqNxEnWc0l5ZmZxLmXg4opVdaV5qiZ8CgeSSN+U6NkinIDzVZ8h7EXNIe9SfgT96DxEiWVH426\nxHK9ZlqovFUsUiKS9aq07JKgV+S6iom641q6KdLIiS4//T9fVluNp1PO+uUVhWiV8bAp3j0nWNNB\neEHL8bqW+7vohRBKgRJS1SrVRE+EyqCp6aL4DjnFexig+0pz9jxeR9a+9LhPGG2sTCaDVCrV9O6W\n4kaLxWIl7m0tNeypVArBYBA2m61E8ZCyJYq942SZEu42FouxOn++11YkEmF9jqpxzPLPVqlUcDgc\nMJvNDCUh8uSGw2EAf0uMOZ1O1v6CiGGoJfhhdP0VCUoo6RUIBBi9Ho/bpLCaXNsdAIwcxev1Stxq\nSj5lMhlks1nZA+PvjTfhuVSox93dJPo/n8+Hzc3NQ6GKoySARqPB2toa/H4/U+a1CnU4HMbCwgIy\nmQwcDoeEnNhsNrPkjtPpPPJwAP99qVQKfr8fa2trjKyD4uXFYhHhcBg6nQ6nTp1iccpqbhx9t9Vq\nhdfrRTgcxszMTAlsinhvu7u7odPpJAQkADAwMICOjg6G9TzMK5/PY3t7G/Pz80gkEtDpdAwMr9Fo\nGPmIx+ORdDUlq99kMmFwcBDRaBTJZFISFqLEcSAQYExeP14/KtSGKtVsNgu/34979+7h2rVrh4L3\n5NnW9/b2sLi4WGJJKX3O0tISPv30U9jtdtaqmZRPe3s7Tpw4gZdffplRstEGOyplSt8XDAYxNTWF\nZDLJeGh5DLBer0dfXx/+6Z/+SXH8kSe4SSaTmJubw+TkZEmyUa/Xo7OzE2+88QarPqKk0v7+Ptxu\nNzo7O9Ha2noo88WvOdH3+Xw+2Gw2qNVqdiAYjUYGNbtw4QKMRiNba5Int9uNq1evYnx8XIJDValU\nDLb06NEjLC8vIxaL1U1j96NC/fGSCBDxfT59+hSffvopUqnUoYyBJ1Ou1BGg2ndsbm5ib29PtpHf\n4OAgUqkUenp6JMqqHvKMWsIZlZ4fjUaRSCSwvr4uwSvT5u/o6MCpU6fws5/9TBGfAT07n88jGAxi\nfn4e169fx1dffVXyXW63G//wD/+Ac+fOyVYFkYIVOxEcxpXNZjEzM4OFhYWSKiqr1coIok+dOlUy\np2q1Gna7HRcvXpR16anqbHd3F5ubm4jH40dOwfmjQn3BFCtZdJlMBtFoFKlUqiSxcJwv6r9EF29N\nURuRWmkF63HllV6UwedLffkulJlMBi0tLYw4m8qNyxGK0L0UJ6RnRCIRiWVL4PtCoQCdTger1crA\n9+KBd1REP3wrHlKqZGWnUilJF1hxzCqVShKq4Kv/rFYra5fzIiJmflSox+SqBHlRar3VS3fW6O/g\n/18phZ2oGGulCDxIozu5zLfIA6skA12JRrJcpl0u4yxiNsVnH9ZBK5J509h4mJySbrDi3P09knY3\n4/rxODpExXYcrO6jur/WQ6dRbFrNIqpWWq3WyEOm0WujxGD48frRQm2KEjroBn9RFLJccUYt1hR/\nieTYSmO3hAXlOWMrWZrVLFG5dxy0EIW3GHlrT46/tB7Z4J8rWst8iKMSRpX++6NF+qNCPXR3X6fT\nsZ4z4s/z+byEx1H8OUGgRBjLYYy9Em+qEouJOEdFJUBtn8vFX0nppdNpVuLIX8lkEvl8nvHMWiwW\nxWOk0s5ybGJyiq/WQ49aZCeTSUWsZXzSi9ptU2NC/rkmk0nCEnWQS6fTsdJVXiHSsynOKs47XyTx\nY4z0R4V6qEqUB0q3trZifHwcv/nNb0r4UFUqFdbX1zEzMwO/31/SLdJsNqOtrQ2Dg4MYGhqSkPs2\nw7XikzIqlQpLS0us2yslcpRclBSanp7G7OwsUqmUBOuZy+WwsLCAxcVFRCKREmspnU7D7/fjhx9+\nQDqdZoUDNC/E+/nKK6/g3LlzEnxstblRqVRwOp04ceJEw/gbRGjSzMwMTCYTvF4vg5tVGhd/4KTT\nabS1teHjjz8uaQek0+lw/vx5xllaa0sRg8GA06dPo7+/H3a7HSqVCvl8nvXtMhqNyOVy+Oabb3D7\n9m12iBNO1el04vz582hvb5cc8D9aqT8q1KZbpWQNeDweXLp0CYODg5KeSqRwv//+e6TTaaRSKWYN\n0iay2Ww4ceIE3n//ffz0pz9FOp1mSrmZCpVwh19++SUCgQDL9itFKBAhyZ07d/CHP/wBwWCQ8XmS\nS0tVTLFYTKJQyYLd2dnBtWvXcOfOHcmcERnyq6++infeeQft7e2wWCwMoF9NoRJW1O12N4WFPZVK\n4c6dO1hcXGSMU9WIcegwoHbJP/nJT/CLX/wCRqORzReVEre2tsLpdMJisUgUaqV2L7ReBoMBly5d\nwrvvvove3l5oNBpks1lotVrkcjmsrKzg4cOH+NOf/oTd3V3o9Xo2PoPBgKGhITidTrS2th6YL/jH\n60eFWpdypY4AIlUabYLW1laYTCZZAaUW0C6XC16vl22sw7BQAbBxH6RMcn9/H4FAACsrK4hEIiUN\n33K5HDKZjGxFDcGTqOpGzILb7XYUi0W43W50dHSw/1diofLwn2bMIZV3ZrNZxfSAfDmvVquFyWRC\nX18fa1PCW4EGg0HCr1DLReD8np4eRt9HFWSJRAKBQICVz25vb0tKdqkjcTKZ/NEifVEV6kGD4nK9\njpo1PrVaDZPJJFtq2NLSAovFIrGUxF5Xer0eJpMJNputpKNpI2Kq5b69WCzCYrHItvRWoiD29/eR\nTCYRCAQQiURqqu0mQhFRmfJjLhaLMJvNsNvtcDqdDXPZK7nj1eaQkknpdFqC96w277xCbWtrg06n\ng9PpZBaq0ph1tfG2tLSwkmGHwyE55NVqNaPXSyaTjJNAVMaZTOZQSqiPgzHUiP11bBWquLHqKWsj\nS4l3EZvF01iO8o1A5nK9vvl/E/sKidnpg2D/xFhpOQVdDhJTrquqnEVEh0U+nz+QkMp1A+W5PMVM\nuFLlX0uiTe4Q4zPhtDZKvo/Hw/JrSOQplBjiLfdyh5GIb1XCvpbP5yWJQrJQ5d7FIw40Gs2xT0gd\nBEVSbZ2O4vBoukKV6yFfTzBcPNlFAuhmx1ZrYZ2Soy0UleBBOokquSjLzwPgeQtWXBM5AZdze2vx\nLMopezn4UCVm/HoOX37MPO/mQVtGi4qXPxRIFkWolNx8iH+nbqzVcLN8AlA8CMR38YfncVSmYseC\ng5RZH8T7eq5boMi1/a1XofLJHx7e06yTU0xMiK1SlCo5MQlBca56Qh9yCo82NV9eyo+3XLvjSu5y\nPZhJJfNSi2VSa7hIRG/wJZYHwRfzioyeT3Arfk7lvkf0zmhsSq3IgxK1H9fYKRlFtI8bidzgvdnD\n+v6mK1SdTgev14v+/n6GYWxUkz63243e3l60trY2hKNSJHmmmm+/3y9rsa6vryMajZbgNcUFFTc1\nPT8cDiMYDNaMF6WYGcXTSDHzwuh0OjE8PAyTyYRoNCqxZHp6etDV1QWbzXbkPaRES0rOquVduFwu\nh0AggFAoVNNhRA3b9vb24HA4GImIqBSDwSCDmokHqcFggMVigcPhYIxONE6VSoWBgQE4nU5ZQppi\nsYhoNIpYLMYo8viQQzAYxNramix2t5xV+yJUOlEuYmBgANFotGFtpGnN+RbShzE/mmZNEgm62Wxm\n7EZOp1PSRroey4zaSA8NDaGzs5NNWKNOokKhgFgshuXlZdaNkV8QtVqN6elp7O3tMQyqknfzlvX6\n+jqmpqYQjUYVEyUTiUdraytOnjwJi8VSkjVuaWlBR0cHLl68CJ/Ph0QiwZRuLpdDW1sbTp48Cbfb\nrbgJ3XGxZpLJJBYWFvD06dMSPtNKlgqFQdLpNLxeL65cuVKioNLpNJ4+fYrFxUUJ1yopTLvdjq6u\nLjZ3PIZWo9Ggo6MDnZ2dkvg6L087OztYXl7G5uYmKxwgizQcDmNxcRGhUAh/Lxclb10uF15++WU4\nnc6GWak05/39/Whra2Ooi+eyBQofszGbzThx4gTcbjfOnTtXU/Kh2mRRRtXtdjMAeT3P5uOc2WwW\noVAIU1NT+NOf/iQL7Pf7/dje3mZtJWppOZzNZjE/P4/PP/8cPp9P0f2ktM1mM7q6uqBWqzEwMFDC\nut/S0oKenh688847SCaTyGazkiSFyWRiZMTHXZGKSikWi+H+/fv47LPPJIk+JWEFwrBeuHABJ0+e\nLJkzYqAKBAKIx+Os8okUJrWgvnLlCoaHhyXxabVaDbPZjJ6eHsnhzldSraysYHJyErOzswiFQpJw\nUTqdRjgcZu2rj7Ob3kg9odFo2AE3Pj6uyLCoJTRos9nQ29srqXZsplLVNFrwxYEaDAZ0d3ejs7Oz\nKQLCs+yIk1VPnLZQKCAej2ONnwR9AAAgAElEQVR1dRW3bt1i9H1yyR25bHKlmCRlgjc3N3Hv3j2s\nra1J5q/auK1WK4aGhnDmzJmyHUDdbjeDJJWjoKs3QdZsBSoiKKgd8tLSEiYnJ8tm8eU8ArVaDafT\niZMnT+KXv/wl3njjjZLfDwQCmJmZwYMHDyRN6UjObDYburu7MTExgfHx8bLlxnKZd+IbnZmZwb17\n9+Dz+STjJjlqNqXicbuoNY3Vam1KcpmUNh96aWZsuekx1GZnGPlYkpINVuuzyZoka0V85kGFgKdd\noxbBInGwnGKgbDLfibKSO1UJ13icrdNyIRQ+I55OpytCh/g1JIVF/AparbakoIDKWeUORz65Qc8Q\n2ziLh5KYQKX1pmZ/fFLyMDLQx12xNgv+eJjGgqrRAz9qF6JepaGkcKDScyvBg0QBkmvPK3dQyGWK\nlZABK43pHlcFWm49K7UcrtS+WZy3WpWYaEGKMKZKcsK//zivw3HwTJ6H5zbNQhVB0iJ4XYm11KgT\nSCSkaIT7L7d5ag17kBKUgyLxLYtrsXarKQIlFG7HPb5WyVIUCwOqPUdujWqdH/4e/u+VrCvR6+AV\nsAhpe1GtU96DFOddhBAehn4QcyGN3A8NcfmpARqRcBx1gy9qedFosHC1mJlc5RRdxOJElUeURSb3\nUezeWUt8tpo1pTSGWmsYRyy5lTsoDiJLIqcoXTzRi0ajYdjmchVqzbbORQtYLDThy1LlLFbyTnhL\n+UVkzhf5Yfl1O4qx8HFV2pdHqlDlwPWxWAzRaBR6vb6kNPQw3Qba7IVCgbXM5TfYQZRTuYvwoNQs\njt5LLEDU7yiTySCdTiOXy7FulQSVMpvNsFqtjGKPlDMBxasB8MvNA/W3l6tSo0Zz9EcJMQmvRAiE\nTiB5/n6yHoldq5ZDiueY5clXaE5yuRwSiQTrg6TVaiV4zpaWFmQyGXZvsyvoeIuHlCmhKnjLWafT\nMRmkuTMajaz+nge3U1z4RXDh6Q+tZzabRTKZZA0vD7t6i0fxGAwGZDIZxhQnV1F46BYqTdbi4iL+\n9V//lfUEF4lCDjsGQ4otnU6zVszNENKBgQFcuHABPT09sNlskvpq+vvjx4/x4MEDWUWu0Wjwi1/8\nQuISUpxtfX0d9+/fx+rqKnZ3dxXHhOjnc3NzuHnzpgSHSora7XZjZGQEp0+fxuDgYIllXc51JYXQ\n39+PU6dOYWRkBF6vlxUm6HQ6xGIx7O7u4tatW5idna1Zqfr9fiwtLeHRo0fY2Nhglhx/QNvtdvzz\nP/+z5H4igpmensbU1BSePXuGcDh8aMz0hUIBPp8PN27cwMzMjIQfl7fqx8bGcPbsWaZw6dCNRCJY\nWVnBrVu3sLa29kIoU+BvePHV1VV8/fXX8Pv9jLdVtNgPU6FSAjKdTmNlZQULCwuMEOfIFSrh63Z2\ndiTwhOOyqNlsluFEG3319fXhpz/9KV599VW0tbUxq0iv12N7exs3btzA//3f/+Gzzz5jFh1l6K1W\nKz755BP84z/+I3p7e6HT6Zi1pdPpcPfuXeRyOcTjcfh8vpq/fWFhAf/zP/+D+fl5+P1+ZolmMhmM\njo7i7bffhs1mQ39/f9UQDS/4Wq0W3d3duHLlCt555x2cPHkSyWSS4Vt3dnYwNzcHv9+PxcVFRQqV\nx+D6/X48fvwYf/jDH/DgwQNJZpze/bvf/Q6//e1vWafOfD7PaPE+/fRTZLNZxpR1GLJIh+fe3h6+\n/vprfP7554jFYswayuVy0Gq1+PDDD/Hhhx/i8uXLcLlcSCaTDFmwubmJyclJrK6uPvcKlXfzs9ks\n1tbWsLOzg9u3b8uW3h6mThBj8cR5kcvlGhJyaUgMlVyd41R1w8dsGqlMeYtHo9HAbDazlsa8Nce7\n/DzsilxuGpvJZILVamW/yysuUhIHwYpms1nE43GkUimk02lkMhk2L+TqiBhWpfFCjUbDuD2p/pxI\nlk0mEywWi6TUr5bEIC/gYm28RqORuPzUDoVi0cViUTKmw7SAeJc/FoshHo+zg4LWmcJExLBPVjX9\nXOTWfRH6PvEtcag45rC9Vzm9ILKfNSoxqDmoUpFrvHZcr2Zypsq18JV7rxijoZgaufiUmBJjwUqr\np+T+jWc/EjPNYiKklkNIZJvns921QLrkhFgcn0hiTQqW5owUqZhFPorDneacp9kTN7F4MPFZbjHB\nWekgEiFfSppJloP0NaIDazW44XEvWmgUdl1T68v4TVQNN3hcrNRqC3/QcfNKi6cplGvKR5uFapXJ\n8uSz+TwxRCUYVTk6PlJqPF6T/zspJBGnyZdPigqt0neLSo+UWzVKRXEz8wqx3HqJm56vtadQiZwV\nIrKFNTsRIhaaVAqnUEigXB6Aj8WXmzcejldtzkXkiPi8eotgRDiSkv13HHUEH6+vFQmjSKGWW4jn\nwR2pxuguQmxq+Saq2OEtNLmNJbcZ+KwvKT7x/ko4STnQuKiARHRDuXnhhZ9iuJWqsHjuTvHdPDF1\nuYv/HTlrl7fcxE1KPxfvJ8Up8pHy9f6EwJAD4zdio5crKFDSJls8xOT2mFgIIh6e1SrnKAwlpyxq\nVRzi2OWs8uclXCEnB3RoU2y14S4/QYT4fj7H3UItN0b6t0YxVFG8jycgyWQykriinFtKwii2bKZy\nV/E7xPklmA01ZOMFnDLvFK8TFSbFWVOpVAn1IX9CV1LIdD9PAKIkCSXGcul+wplWcnF5a0t8F8+p\naTAYWNdSvlz0OBc1EIELxVv5fUbx1WKxyOaMNr1cW+9yc0i0lLwVT/fXMzc0x9T6pZrHcZwVqhzX\nsdJxa6qdtlqtlsFsgsEgY8l53gPlxWIRAwMDrC0vD75WOvmUkU4mk7BarZJ6+3g8jmAwCK/Xi7fe\nektiKZEraDQa8eTJEzx79qwkWD4/P4+NjQ3E4/ESryCXyyEcDmNhYQE3btyA2WwusRgCgQBGRkbQ\n0dEh6chKNHQWiwXr6+v47rvvJJYNjX9lZYVtPP5PoVBAIBDA3NwctFotdnZ2JDXu0WgUu7u72N3d\nlY2Z5XI5bG5u4s6dO1hdXYXZbGaHjUqlYjCWcDgsCWXQuJLJJObn5/Hdd9+VVCHl83ns7u6itbUV\nExMTGBwclLjGVqsVvb29cLvdxyLpw29Wo9EIr9eLiYkJdtDzsmgymZDL5fDkyRNJ80WVSoVUKoWV\nlRWsrq6yRnxijDwWi+Hx48fMK6I5U6lUCAaDWFhYgN/vr4mbl8ZOjHKJRALhcFjCe/G86gea2zNn\nzrAutUqUqqZaPESv16OzsxPnzp2D3W5HKpV6rtvQ8uBzl8uF4eFhuN1uiVJRehptb2/j+++/x/z8\nPGvkR8pFr9fDarWiq6sLZ8+eLaGaIzLjyclJCZkxKRafz4eFhQWEQqESKEcmk4Hf78ejR48Qj8eh\n1WpLhKG1tRUvvfRSSedT4v2MRqNYXl7GgwcPJK4qxT+npqZYYQBvtebzeezs7ODevXvY2dlhHJa0\nUZPJJCKRCFZXV1lsVRz74uIi1Go17HY79Ho9s440Gg38fj82Njbg9/tLvpsOqocPHzI5FEMqTqcT\nXq8Xw8PDDCpGYzcajXC73ejs7DwW1hI/7yaTCb29vXjzzTcxOjpaEv6hef/+++8lFibBxvb29hjh\nOb9eFDcPBoO4fv06lpaWJApVrVYzhby5ucnwmNWoEfl/t9lsePnll+H1ehm64XlXqBRG6e3tZaTh\nSmSmrEKlBdNqtXC5XDAYDOjo6JAA15/ni/qV22w2CVyllk0WDAYxNTXFIDD8Yrjdbpw4cQIjIyO4\nfPlyyZzlcjn8+c9/xsOHD0twpqT0wuGwxCWmK5/PIxqNYmFhAbu7u7KJtrfeegtXrlyBx+NhJyyN\nb2trC9PT05iensajR49KXHxikJezVuhnuVwOW1tb0Ol0koQYuaChUEjWQiXawkQiwWK1vEWQTqeR\nSCQkpNu8oKdSKSwuLmJvb6/EtVSr1bhw4QKGhoYwNjYGr9crUegE96q302ozFKvBYEBbWxsDnIs/\nD4fD+O///m88evQIoVBIAo6neSGYnJysx+NxTE1NYXl5uWTOqUttLBZjz60lBmoymTAyMoLOzk4W\nsnkRyF5UKhWrZFR6QFR0+ekEs1gssFqtaGtrq+q+HCQ5pNQ1atazxQyp0sB6IpGQbVmhVquRTqfR\n3d0Nq9WKEydOlJA0pNNpfPPNN9jY2MDq6mpJqW6l91IcLZVKYWdnR1YQXnnlFbS1taGvrw9Op1MS\ns21pacHS0hJCoRAWFxdZfbySeSS3O5lMSiq4lF6FQgGRSASRSORAlkM2m4XP52OHED9fOp0OY2Nj\njOi5r6+vBKGiBCp0WMaCCKGy2WywWq2yv+fz+VAoFLC5uYmtrS2k02nFUB+KV29ubjZ0v9F86nS6\nirrhMPZ4NS7iet5dy6VRKshKsImV2lDU2za60tgaBfc4COBYjtiaz5ySIiNXmvCmVJqo1+uh0WhY\n3EmEwSitYJJTXBRKIEVEyl5kaxJJOmpZLzm8YT0bScn7eRgYzTMfmpBjdKrU1K5ZFlWt6BG5luV8\ncoSKPeg7eK9ICfKm0hyI3LC1Krd6KoyU7PFKc1iPjqgW5hPRM1Wt2no+9LgEjxsdz+JhKUpM/XJK\nVQ42RYqSJ++oBwdbTfiq8XTWc0qX4yOt1yqpZ13l8JZKik4a1blAro10vVCiRjbkU3KfnMXezMKd\naphnJRZ4pfur3dtIHaNR8rHVWtbWY24fpbtfbiPRN/MYUaWLWe2kI2uKZ6ai5E25jVhtA5ez4ChG\nSbFw3uUXiZZ5oL5ShXdQV6per0W0PGneeNga/UzkLJULbTSKM5ensZTjai1ngfLjkDvA+bpzHuQv\nkl3XMm9KlaocLaHcGOvlM61XhzT6/oMesIoUajablZCMiMpVr9fDbDZLXEdeEKiOl9zOWnqJE45T\npIojASUMKLm3Bz29RaB7IpFAMBhEIpFomCUsgtTNZjPcbjejGOTHTvR7hK2s9Uqn0wgGg6xXD5+E\nCIfDiMVikvp+UYCMRiNMJpMsGTDJQjabLdmgVHpqMplK8LH0rnQ6LUstqOQirCPhofm23ASNMhqN\nsklGUkrUzlxk+QqFQkgmkxKAei1rq9Vq4XA40NbWhmQyyf69UCiwFtT82ERlTLheMaZNSSlCRojj\nb6blSD2f9Ho9a8Pd6PijTqdje1yubxvtb15/8IlGokOUayVPlIH8YcTjwXU6HfR6PfR6fclBcZBv\nq6pQKQkRDAZZdlfMEjocDnR1dcFkMsmCz8PhMEKhEGKxWM3xKovFgvb2dthstpIPpkZ6NDaxv9BB\nLAwiNkmlUlhbW0MgEGi4u0OWSGtrKwYGBqDRaFhPKdpssVgMfr8f0Wj0QAo1Go1idXUVLS0tiEaj\nLEZLTFhE61dOcRD8SOyzRM+jsckpVL1eD4/Hg9bW1pK1Jhyrz+cryWYrmTfqPurxeCQVZsQd6/F4\nYLPZJFAy/t3JZBI7OzsMT80D/2OxGEKh0IHZyfR6PTo6OjA0NIREIiHpoKtSqeB2u2G1WksUKmFo\n4/E4dnZ2EIvFJMpeo9EglUpBp9Oho6ODkWvLKZBGXiR3brcbZrMZgUCA8fk2SpnSIdjZ2QmbzVby\nzHw+j3A4jHA4jEgkIsFyEzrC6XSira1Ndj4ymQz29vYQjUYlhSDFYhFarRZ2ux0OhwMul6shUC9N\nJTe2paUFyWSS8VPev38foVCopD/92bNn8Zvf/AY9PT3QarXsfjr1b926hcePH+PZs2c1nawtLS0Y\nHh7G1atXMTo6CpfLJXl2LBbD4uIi7t27h4cPHyIej9dd7UEbNJ/PIxKJYG1t7UAKrdqpbzAYcO7c\nOZjNZsTjcYmFWiwWsbi4iFu3bmFmZkbSFVWpazc3N4f//M//LMF6Evh+Z2cH6+vrJWEGKgu9fPky\n3nvvPUn7XTog5+bmcOfOHczMzGBzc1OCIDCZTGhra8MHH3yA8+fPs2olWs9YLIYffvgB3377LXw+\nH+LxeE3WqdPpxNtvv4133nmHlf0STrNYLKK3txe9vb2w2+2SjUfQobW1Nfz5z39m+Ft+TbLZLJaW\nluDz+RhkTGmZNbVDvnr1Kk6fPi2BD5EC6u/vR09PjwQoTmOLRqOYm5vDtWvXMD8/XzI2vV6P4eFh\nfPzxx8xbazYenJKX1FL9s88+k8DZGqFQ1Wo1hoeH8atf/QonTpxg2GGau0gkgjt37uDJkydYWlpi\n6AbyXqmI44MPPpAwvtG1vb2Nzz77DAsLCxIDYH9/H1arFaOjozh37hwuXrwIi8Ui2yalIQqVP113\nd3fx+PFjXLt2Ddvb2yWClEwm8e6776Kzs5PR0JEAJhIJzM/P48aNG3j48CFzhZQoB8IVnj59Gj09\nPSVjS6VS2Nrawv3793Ht2jUEg8GGxVX5DqONZskhV2NwcBC9vb2STUvK4e7du9jb28PW1lZJvywl\nCnVzcxO7u7slWE2ekIVPjPEeh0ajwcmTJ/Gzn/0MDoeDeSQtLS1IpVJwOp0MgM/H1Ai14HK58PLL\nL+Ojjz5iZZR0BYNBpFIpPH78GOFwuGar3mKxYHx8HL/4xS9KwkA8N4L43RRq8Pl8uHXrFr744gvZ\n+STXsFLzvXKWlsPhwPnz5zExMSF7Lz82PrlEONKNjQ1MTk7i5s2bJa6py+XCyZMncfHiRXR0dDC2\n/0a63nL7Mp/PY3t7G5OTk/j3f/93zM7ONsxjI4/jwoULeP311zE8PCxJJKrVaiQSCVYReO/ePQZT\n3N/fh8FgQFdXF1QqFV5//fWSsbe0tCAYDOLu3bu4ffs29vb2JDhbt9uNUCgEp9OJl156SaJbGqpQ\n5ZRrPp9HOp1GOp2WwFSovUO1+ynuRieMEkgQAb3L9QgSx5ZKpRSxzx/1JVK28d9CsThqJVMtIVju\nqvcgIEuVSJx5BUN8o5XWjW/zwV9Go7GEPEVpUognAqGxiQe4iKwQ/5+PVdabjJJjYdNqtSXhhnJj\nk0sYEb+B2CeL+CCoOIH4GZqBxOEP90KhwFxpkXuhEYYL3x6mkv4g3grSPyTbuVyuqoKn9jKpVIox\nkxFHa7lWOQdNhCmm7yt3GlbT5uVaJNeaeZcbi1J2n0bCkhqZmConyOX+v5Hvq/ZcOfhPreOS4wNt\nxJzKsZ+VU16NXkO5d9UDy6mmoJXIR61YyVoUqty7G/EevrxT7nCW61wsQhrloI2ihSr3u7xBWA7a\nWInbuKKnctDJrvVFtRC4HhcL87AxuIeJ+z1IF9VG/e5BMbDNkIl6oFvHxQt6HsvAm1mso/RdzShE\n0uDv4DquAldOsci5iIf97YQ4KMeXKUJb+LizCIcSLYxK1q+S8JPIBarUrW7EevHWoBLLsBYruZz1\nK9LJVQL4N6JYopxVKM5rI70NETPMz50cexZPyi4na2IoReTKlUs4ysnVjwpVJkZDccBGW3/ZbLZh\nLYsbPTbC1okcoDzRMvVuktt4mUyGNbnj47zEIaDRaGC1WuF2uyUbzOFwlPSUklsTi8UCh8NRk/AS\ndpey4slksqRsVq/XQ6fTSYi/G7Hx+d5I0WiUJUBruQjzKMfLSpl8m80Gl8tVcq/D4QAAho/mW1BT\ncodi73KwrEKhwDCutcwHwbmKxSKsVitcLldDYYQajQZ6vR6ZTAbhcLika3IkEkGhUIDRaITT6WRc\nviTjFouF/Z7cmsTjcajVathsthJ5J3xtLpdDMBiUxWMTDl5pouqFVqg6nQ69vb04d+4cHA5HSQKj\nXktldXUV09PTNWMqK7kajTpIenp6cObMGTidThgMBglFXjgcxvr6OpaXl7G1tVVSzZPL5TA1NYU/\n/vGPEmGinyUSCTgcDrzxxhu4ePGi5ECxWCxwu93o7e2VPcR0Oh2Gh4fx3nvvIRAISJo7VvsmyuLH\n43H88Y9/LIG5FYtFDA4OYmhoCB0dHbBYLJJ+Wge1oIC/JTb8fj9mZ2dhNpsxNzdX0TISlVJLSwtG\nRkYwODiI9vZ2mEwmieVpMpnQ09ODt99+G729vSXfrtVqkc/nMTk5KenbRV10vV4vent7MTQ0BLvd\nLok/FgoFhMNh3L17F5ubmxKAfKVx8+1skskkLl++jHPnzjU0y08Jt9nZWayvr0vGzSfCx8bGMDg4\nyFAY/ByYTCZcv34dd+/elcRTCafe2dmJ1tZWCYcFfwD5/X58+umnks7ENOd9fX1Mfygxyl5YhdrS\n0gK9Xo+hoSF88skn6OnpgV6vb0gXVIIWTU5OIhqNIh6Py1ZxHOW3DwwM4MMPP0RfXx8cDgfb1Dqd\nDqurq7h9+zbS6TR2dnYkWE3Kgt+/fx+bm5sM2M/jKYeHh3H+/HmcPHkSnZ2dkoop8gja29vZvfxl\nMBgwNjYGl8vFsqxKXVDi9fzuu+9w7do1Zm2p1Wo2hnfeeQf7+/uwWCwlxNv1XMQ5mslksLW1xSxl\nJQo1m81CrVbj/fffZ9VOfBeFlpYWWCwWDA4Owmw2IxaLSe4nztKvvvoKt27dgt/vZ4o0m81Cr9fj\n9OnTuHz5MtxuN2w2m8SNzufz8Pv9+Mtf/oJ79+4x6GI1q4sH9p84cQLvvvsu2traGgIj5HmBV1ZW\ncO3aNSwvLzM5pU4CTqcTr7zyCsbHxzE0NAStVsuKi+iQm5qawl/+8hf4/X5m4ZLy7Ovrw1tvvYXh\n4WEJNlmn0yGZTGJubg6PHj3Cl19+iUwmI8Fs6/V6vPHGG+jp6WEFGdUSc3Ur1OMcn1Sr1XA4HBge\nHkZfX59s87yDfC8J6tLSEiwWS9MrVg5y2e121pGA3EWal2KxiLW1NdZlQLQY9vf3GV5UjJ3pdDq0\nt7fDaDSira0NAwMDEtgLWQ4Gg0E2e0sdA/jDTakFWSgUsL29jVwuh4WFBVYiSkpDrVZjd3cXkUhE\nAsxvhJxSuCOfz7NQg9LkLJWe+nw+VrUmyirR9+l0OlZ6Su+lAplsNovNzU1sb2+z6qtCoQCz2Qy7\n3c4Y98uNfXV1FXNzc5LfqWahEnSxq6sLHo8HQ0NDDcn2k6zlcjlWebewsCDJvlNLHQol9fT0SNoJ\n0WGytLSE3d1dPHv2TCJzFKaw2+3o7u6Gx+NhXqparUYoFMLW1hbj9o1GoxKIIFmoxAynpMqzIZpA\nLsirhEqs2QqVThmn04nW1lY2mfWMR7Qq+GZxR3W4yCWL9Ho97HY7K63jE0IWi4XVTpf79nQ6zWr9\n+ctoNCKbzUKj0cBsNsPhcMhusHLCR7FCuaqWaoqvUCggkUgwS1XEL2q1WiQSCVY6WqnFdqW5q/R+\nwooqNTBILiwWC5LJpIRSkVf25D3wsWd+Xsn1jsViiEQikoqhQqGAWCzGFL5cUosUFxGHKw1DqdVq\nmM1m5HI5mM1mOJ3OEsq7epAS+XweRqMRqVSKrSk/b0QGTvFlq9XK5iudTiMWi7ECAL6Kk8aUSqVY\n9wyHw8EqsVpaWpDL5RgONh6Ps/t5SFcsFquJ26FhCrUSNlAUDpEVSImCKLchlCwYEXkQ/kwOq6Yk\nOcK/m0/UHKUVXi7LSxuflI7Y6pkni6gUJ+aLEMgVkmtjTZZUvRAoseUK/025XI6to9FoZEUfGo2G\nfQvhDMtx3IokOOIBoMQQKPedcjItdpTl7+Wtc34ji7JG/0ZxPxoDxVXlup7KIQao6ECOVV9uH/Bx\ndz6RJmI4y3H3VsoV0H3EwUDFGvRsnjOAfzbJLfEK891WRXQCf5jw+6BQKEjY1/gx8XJO81VLjX9D\nFCpNBmVWK3FAKq2NbgTprwjmlVtkJVbV8xpDLte18SD9xsU1FImca7H4y1nzIvFFubUUN4J4QPJA\nbv59YtvvZoeteIVDm1Vsvy1HTF4tSSRXMFGp4IXfnyIjXC3G0kGSreV+R6wW5MuFxd/jDyI5zmK5\nfnCikhTvF3/Gv4vnvaiVMKUhClWj0cBoNLJySTlBkGNUV6KolTDXV1o8ck3LjY1X8tW6Dhw3ZVvu\nYOLjmCRs/IlMXKmVYr8idyYfzCfLQM4iaUShRzllT5ZpsViU1HSTfJC7zG8QUmAUY+XLZg+SXKmF\nU1T8NlJs9H0ifKpcKIK35iieRyEAHpvJu8v8s/V6PWvvXOmQFN9NLj+9V2zcJyqmg+wPvvV0uT1H\n2XfSNTzLmMFgkFDvyckSr5v4+3krtJJlX4vuqVuhFotFhEIhPH36VNIRlSZ+d3cX+/v7aG9vx8mT\nJ1n/eqXX0NBQCf6sFnc/EAhgamoKwWCQKWgSQJPJBKfTCYvFciCyiaNSsKQsnU6npF8UP+9WqxVr\na2tIJpOMVpGHe62trTE6NHGTtLS0wOPxwOVySSwqcpX6+/vh8XhYHLQeJnlxI1OzOeImFZNioVAI\ner0eExMTJcJPCa9YLIbl5WXWt4pnm6JOrePj4yXrTfISDoclnWhpYxKnqdPphMlkkvSyJ97Ovb09\nRCIRifXOt99eXl6GxWLB3t6eBJROnMJElSdnGHR3d+PUqVPweDws9LG/vw+j0Yj29nbs7+9jdXWV\ndUXlx7aysoJwOCxbN6/VamGz2WCz2WA2m1mugUISXq8X/f39soqPYpl+v1/Csat07xQKBczNzTEm\nKFGJZTIZ7OzsYGlpCSaTiUEAibjJ5/NhbW2NHTSibCUSCSwtLcFsNqO1tZXpALVajUgkgpWVFezt\n7TEDoV5vpS6FSoLi8/nwww8/YHV1tYS+j/CBfX19aGtrk9QeK1HW/f398Hq9rE2zUkVGsZOtrS1M\nTk7C4/GwsZGF5fF4cOLECfT29jLL4Ti3wOVjaTabDSMjIxLKM34DW61WzM7OSjqL0om8u7uL2dlZ\nBAKBkvvIuu3r68P4+DjL1pPCAf4Gm+rq6mKg6kYeLIlEAhsbG5ibm2MdXXnrI5fLwWg04sqVK7Kh\nJLPZjGAwiMePH5ckIQmY39bWhitXrpQo1HQ6jenpaYYg4CvAVCoVbDYbenp6cOLECXg8HknsjrrB\nPnjwAIlEoiTxk8/nsWn4klwAACAASURBVLW1hSdPniCdTsNqtUqIPSwWC7q6ujAxMSEL99LpdBgZ\nGUEqlYLf72cWN88LCgBPnz7F/Py8xMLL5XLY2dmRKA7+olbxAwMD6OjogNFolJDruFwunDhxgq23\neCWTSczPz2N1dRWxWKziHhI9wVwuh+XlZQQCAdkOBMlkEisrKzAajQykT99OB+Ds7Kxss0wACIfD\nePz4MeLxOEvOFotF6HQ6xoS3sbHBkBf1Qio1B1Wk/Mm7tbWFr7/+Wpbh3eVy4cyZMzhz5gw6Ojpk\nWdwrvcdms6Grq4sp1FqSHtlslvFf8mMjpTo0NIRCoQCTyQS73S4B/h83917skODxePDSSy/h3Xff\nLRH0QqGAx48fM5wsuWsUi6KMqN/vLwmnULJjfHwcv/rVr2A2m0sSJQ6HAx6PR5JxPahiFctJg8Eg\nZmdn8e233zLFxq+b1WrFlStX8P7778tS783MzDCQOG8pkoXp8Xjw2muv4dSpUyXzGw6H0dLSgkAg\ngHg8zki5yaJxu90YGxvD22+/jeHhYUlyhqBoVDQhUiPm83msrq4ikUhgZmZGwrJEljXtkc7OzpJ5\n0uv1OHv2LDo7O5FMJiXzTnjipaUl3LhxA3t7eyUIgWQyie3tbQnul+43mUw4ceIELl++jJGREYbc\noPEbjUY4HA5GAC3OO3GW3r59G+FwWAL7UmI0RSIR+Hy+Elnc399nytrv9+PRo0fM6OFpD4PBIOPV\nFccWDAZx69YtzM7OSnQPGXvhcBiBQIBZ9fXG1Bvm8sdisZIkAAAMDAxgbGwMXV1djFC5FnIVcnfE\nGImSBaMTjEoo5WJSIyMj7FQ9rKx9uYSMEpgZzYfVakV/fz/Onz8vgS7RmpBbv76+jnA4LJtUknP/\nKB7W3d2Nl156iYGh5X6nXIvmeuYjkUhgZ2cHc3NzePDggQQG1NLSgs7OTly9ehXnz5+XwNUIl0js\n7KRU+fE5nU6cPHkSXq8XFy5cKJFDv9+PJ0+ewGKxSOJ0dBhZLBZ0dnbi1KlTGB8fL+GYtdlsDOso\nxuSKxSICgQBCoVBJYkitVsPlcsFoNJaA+vk8RXd3Nzo7O0tkJRaL4cmTJ1hYWMD8/DwWFhZkW4mI\njSHFNtCjo6OYmJiQlBOLyR+5tU6lUnj27BkeP36Mvb09WVhWNR0ilm/zLj91mCjHSlWJqjIej2N5\nebkkLi/2ymrU/m8YbIr/KDrVqWacEiF6vZ6VdtHvKc2UiiTJtSwWf2LysRvarEdljdbaZlgulkoB\ne5FFnQLt+XyexbX4mJpSxi/KTJeLtZYbv9LmiuUy1tTsjm9gyNd582TSZMVSFp/cXKpQ4pUazRlV\nxPBKjZIb5SBFfMxRp9OxsWk0GmbhVMPRik0EaUzlYGdyGWneQ+SbMVKVWyaTKYH1yY2N31M8mF1u\nj1aLj9Pv8dC2WpAE1fhQK3mNleRZjkCl0r314sk1jVQOlYC+4sI2ilNRrhpG6eY+KHmz3PvLcXOK\nC1np25UCpctxgPLP4GudReb6au/hD0i5uW30AVQJ0iWn2MiF5ttliPjGStCrckiOcsxGcpl0fi74\n8JeSGJzc2ET4z0Fkv1aKRf7ech6L0vXjIW2V9n+jdEytz6xWfHIQr7GpFqrcoMtt9Fpibko2f7n3\n86dQOeqxejJ7olDzXVeVMn5XUv5KN5dYBllJ0Sv5XjnsXyM6QipVqvx38DE/XsHJ4RLl1oNPtomY\nynJdA+SY/uXWhneB+QOsFq+E/l88wCoZALwXWK4NutxBLqdQxKIDuW9Tsl/Fw6YWF1qJ51muBVAt\n91byCpXO46EoVD6mVm7g/CnPu9pKYqgiK3e5n5ELWE0o+Y1aT/8YcjEpxkvPUgoM5sMk4kautJii\nRSTGxkig5YL89TDI824qj4OsBMKX46eUq6rj3Vn+uYQ/5BmCRFnj38NbeqKS4P+fHz/dx68b/T5V\n5IgHiyhDVLFTCaMqFpnwhzCPj6wWMuBlg6fq4w8PpfwSctVv9G3iwVVpfHzRAh9v5WWxUmWkuKZH\nedF3ixjVQ1OoPFchrxCy2SxrJRyLxbC7uwutVss6n1ZSNnx9s8PhkO1nTv3fHQ4HvF4vTCaTxA0s\nJ9TFYhHpdBoulwtWq1UCDK5l8oxGIzweD9rb2yWlf9lsFl6vFy6Xq6RJHS+88XgckUiElQJSPE2r\n1SIQCLDWt+K3EOYxEolge3tb0omSNiyRafAKu1FeSDqdRjweRzKZZJlw+hnF9AjTKNcgMJFIsG+j\n8REvZjgcRj6fZ+3DeepArVaLjo4O2XbD9Hyj0YjW1lZ4vV5Wq01z5nQ6YbPZkEwmsbGxUWKtUkKo\ntbUV7e3trHUzlXfabDaGX9za2kIqlWJySHhJah8t53mYTCaYzWbWQ55Xyu3t7XC73SUcB3xvp0gk\ngkQiweBWlFDKZDKs9bTT6URnZyfbi9W4K2iPUj283+9HLpdjOFxSLJTp5yF6dOl0OjZn1L+JFFGx\nWEQqlUIikWA8DOI4iG+DsOBHzYtBOFeDwQC3212W27fhCpVO1v7+frz33ntob2+XMDrRqZ9KpfDD\nDz/g+vXrimNwpHR6e3vx5ptvYmBggOHIaLKJ8uwnP/kJ+vr6GGmHEgs1l8vB6/Xi1KlTaGtrq/kk\nAoC+vj787Gc/w8TEBBKJBNv8uVwONpsNvb29GBwclA1BpNNpPH78GDdv3kQgEGCJMzrdt7a2MD09\njb29vZLsJ23e7777Dj6fTyLkJJCzs7PY2dmRNFWrN1ZNFs36+jqePHnCsKIkcLlcDlarFe3t7bh8\n+TLOnDkjaVhHY5+ensadO3ewu7uLRCJRYoXq9Xq89dZbeO+99yRWHMGLzp49yyqeRKb3wcFBvPvu\nuxgaGkIkEpEgRGizP378GHfu3Clxf6mq5q233pIkwEQugS+++KLEyyKKvPn5eQkEh295PDo6ijNn\nzmB4eJjhUMlCJIxrR0eH7Bqk02ncunULU1NTDE/KW6HE7fnJJ58ogv/x3hApvSdPnuD+/fuStabu\noKOjo3jzzTfR1tZW8iyHw4E333wTXV1diEQikqo0YgZ7+vQpHj9+zBQ/T4zd1dWFd955BwMDAyUG\n0VFYrPzYhoeHS5AbDVeovGmu1WoxMDCAX//61xgbG4PBYJDg19bW1vBf//Vf+Pbbb3H37l3kcjno\n9XpFTeL29/fx6quvoqOjAx6PRwLhIRD34OAgenp68NZbbx3IZec5CJSGIOjq6elBW1ubLHsQKUb+\ndOMFOJPJ4MmTJ/iP//gPLC8vI5vNSpQDbX65uBop1EAggBs3bsiOmajPGkUGTGPI5XJYX1/Hd999\nh7/+9a+YmZlhlVipVArt7e0M+H7ixImSDqDpdBpPnz7FH/7wBywsLCAQCDAgeTKZxLlz5/D222/j\n6tWrjMyYLAZaM2JlklsTkgc+DEKeg8/nw5MnT/D73/8e165dkxBf5HI5OJ1O/O53v8MHH3yA0dFR\nmM1mZDIZ9g2PHj3CX//6V3z55ZeYmppilUO8G06ENHyYgSzJ0dFRXL16FVeuXIHX62UWLn+Q0nfJ\nQZNu376NP/7xj0xeiOneYDDg3LlzuHr1Kj755BMMDg4ilUpVBNjTIUW0gp9++ik+//xz3LlzB6FQ\nCEajkcnf4OAg3n77bZw+fRper7dE3pxOJ15//XVcunRJEpYgAptvv/0WarUai4uLDJxPa0NwsJ//\n/Oe4dOkSjEajhHv3qEMAhOgQveOmuvxUCkl1tbz7J1o4fHWIkuSIGOuSi72QYjzo2A960eYu9y2V\nwho8E1Ymk2EKtVzCS25DkMBXOpCacZGyJ5eZYFn070QcXS5zSi4ljZ+saDGzTvMrh4mstia89caH\nDEhOeOuQRzbwhywpXJVKJfEg6Hk8hZ6SJAb/TKph58ctxmjFi2+5w8+/KCtkaVezUHn5F72QVCrF\n5ofeWykGSnMmMrLJ1cvL7UHiG+BbuxyHq1z+pi6FWgmTxwfv+YRBpcyaUniGiLmrZC03oly0XDvi\nasm4g148/Ri/uZXCQhrRfeCg88QrbDlokRyqgE+2iQmWckQromJUIjNyByXFeuWy/aLVRr8nJmH4\nRFu5cVeSUzFhJkc3J3eY8gxbIpZVTmbFJF052eHnuRI6QgTOiwlQ/p0ivE4uOSg3L5TcLZf4qpbF\nPwiKpBlXzRaqHNCez1hTVpSA2OXirtX4UGuNtdZzolUDLFeDi1TbRNVQAqJ1IiaBjtslKgRSXmTF\n8egGMZMuZuLJcqMkpnhgy21eJRtEKTxMbr7loHCVDlOxJ1c1kLqcAhcB9nJxRFEhEw+sXFdSvjyz\n0vyUk0++dz0/BrEwQQ5SxSdYK+kQOf1B4xbfUSkcV80zaISx1dCklFiaxZ9gPOErH7it5LqUY1OX\nCwwfBvt/s+6vBhqmai25+TiurWV4C5PGLSoJuRJHOcucp3Tk3U2xDr7WNRLnUY60+aChDh68L3fo\nKcVdlhtLOaiaWGwh7kOat1rGIirtcq2jRbdXDr8r513xYyvnkZCHJscVW8v+rOZJHtalUSpIImid\np3Sj+JQIBhZdK7GGudok8C6aXNZSzt06KEFHuefwsWClroYIQq7Eqs83mhMt9GpWxlFdPB8qj/vl\nEzzl4rv0zTyGk5cPOqRFi6NRXKv1fjdZhLxV2UhOAzk5p/mmeaN9IZawiqG0SnNWyz4Rsc1yONpK\nz6T7RDJnfk7JIBMPqloPUiWE8c1UsJpqk6jVatHe3o6zZ88yZhcRTNzd3Y2HDx9iZWWlxLKkvtqj\no6NwuVwlfcGrwTpGR0fR1dXFMsm8wKXTaYTDYWxvb2N7e1uSDa5342g0GkaGMTg4KKFKo//u7e1h\ndXUVoVCIYWtJaRiNRrjdbnR0dDAoDH8Q6XQ6BvEhph0+ThcKhbC+vo5AIIBYLHZslCq1LB4fH4dG\no8HQ0FAJYa/JZGJdNkXy3nQ6jUQigfHxcQwPDzPaNLJk+vv7cebMGbhcrpKquoNshEaBxVUqFVpb\nWzEyMoLXXnsNHR0dku8uFAqIRqNYWVnBzs6Oom6uvALOZDKML5V6G/HKmXojXbhwgbV+IVk1Go3o\n6+vD6OgoLBaLIjdZiRtN704kElhfX8f333+P1dXVElwxwRe9Xi/DdPPhnLa2Npw+fRqhUAiRSKQE\n9N/e3o75+XlEo1GJEqTmhj09PfB6vZJW8DTnqVQKe3t7WF5eZtBF/vB2Op0YHh6Gw+FgVJSVyOSb\nolB5ISauxHw+D7vdjlQqJYmNEtvU7du3Ga0YvyhENTc2Ngar1Vo2NlNuQb1eL+t2KMZW0uk0Njc3\ncf/+fTx48ADpdLohHUgLhQL0ej3a2tpw4cIF9PX1yYYwdnZ2cPPmTaysrCAajUowicRs9PLLL6Oj\no6PE+iAYDTVe48koNBoNlpaWcPPmTdZA7KgVKl+N1t7ezr4rFApJ4sDZbBapVArb29uYnZ2VWDR0\nULndbrz88ssM4M5bKm63G52dnXC73YqhbM2OF1O81OVy4eTJk9BoNDh79qzERSXuXSKSroXVn/re\nExxtcXGxxDvTarXo6urC66+/LilEIevO7Xaju7sbVqu17oNEjCHH43Gsrq7ir3/9KxwOR0mIp62t\nDe+//z5r/MgrVDLIJiYmYDKZkMlkSvRHLBbDzMwMbt26JVF2mUwGLpcLFy9exNmzZxkLmDi2hYUF\nfP311/D5fBLUAkG+9Ho9g9o1m+tYU80d0Gq1cLvdMBqN6OzslATBaeLv3r2LL7/8Euvr6yUbv6Oj\nA1euXEFfXx9GRkZgMBhqYqEhZnq5LpnpdBo+nw9zc3O4c+cOotFoTSw35awFwtB1dXXB7XaXjef5\n/X48fPgQT58+ZRR59AzqX97T01OSaOAZ2K1Wq6QaisZvNpuxsbGB7e3tsiW9h6lU6N1kqel0OnR3\nd5fgZ6PRKCOwvn37NtLptORZNpsNb731FqPRI05V+mMwGGAymWCxWI6NQqV1sdvt0Gq1cDgcrPME\n77ouLy9jenoaT548kVhC1RJDBMHy+Xx4/Pgx7t+/X7Lx7XY7hoaGMD4+zuafDAzCk1IVVqMscxof\n8a1mMpmSSqn9/X0MDg7i1KlTGBwchM1mY0TuvGWv1+vh9XqZF8nvtadPn+L69euYnp4usVA7Ozvh\n8XjQ2dmJ3t5e1oKH0AeJRIIZVXJtpOPxOCYmJtDV1SXZh82SKU015UJ4OSrpE3+HWhj4fD48e/ZM\nYkHypBROpxO9vb0wmUw1fZAc+QVd+Xwe8Xgcfr8fGxsbkjaw9QoStaEIh8NlM4jJZBI7OztYW1tD\nKBSSxJPy+Ty6uroY8a2c68y3xRUJgXd3d2Gz2VgvnKNQqOWSJoQXFH+HyJnz+TxSqRTW1taQSCQk\nY29tbUU2m4XH40FPTw+cTqcsREjOJa3125W0kVZyD42HrBybzVZyuBIelw6Cas8WE1O5XA6xWAw7\nOztYXV0t+W632w21Wo329nbGql8pXtpIhZHP5xGLxSRrKXqh0WhUEs7jDyKSF15/8Pt5a2sL4XCY\n6Q++AAYAAoEAK1QQ5zCbzSISiWBjY0OiUHkPl8jCj01Sio8bioLPt2XlW7DybhwfH5SDRNQasOdP\nGZH3sR7FI7bJJbByJUAy3zpF3Ph8EJ63RuQgRXQi81lOPqFXDp7SzEy+SFBcLRlAa0GZW3HsPDkO\nD5Tn2xrzG6oWhVfpO+TgaLWgBKq9n8I8PDfBQQ8s2jN8Apf+jS9GKLePDqpIlSRvxG+nMVRas0rY\nagoRURktz/NB1VRklIlrKMdvIZcwqyZPh6pQyyknXqnxbRwqnZByUBYlWEK5IgI50LAcMLoR1pkS\nYL+IfuDd+krzIpeRlANxN9tNKRczFdvzllMuIipCCSyu3KZTmlBRCuYWE1vVGJ1ElqxyCI1y8lEN\n3idSIvKeXLWxyeEt5ZA39aALKuGfa31HNc+qHPOYeKDLUUnybairhYaOHWxKzuXme7vIKVq5heeF\nSo7erRrJq2gx8TRvcqd2vYkIJaS7omUqZ5XxFGmVNp9ouYrQMVIIYkVLsxQq33mhUoa4GmGy2CNd\npOqrZb1oXWqxNPkNWklp8Ru2WvtyUVGIfKhyWFNerkSOXhF7yUPm5LCivMfXCAtMlDk5/uBK1VlK\nk5r8AczPAXmy/O/xlqlIRymWKIuyJsrwkSrUg8Q3a3En5Ervyl25XA7JZFLiTtHGjEajrN0DxbXq\nKQXlhYtaTPNN6mo58alOnyj6xL7p1SxiQlOYzWY4HI6SkEkul0MqlZJtn9uIRATFpnO5XElYRa/X\ns8ypiKog6BS1WyayC7rfZrNBpVKxVtGihUKsSQaDQcLPwIPbk8mkIhYt8fAPhUKM1rDculMDw2Aw\nyGSumndAWf5gMFh2PSi5E41GEYlEJLSA+/v7rPcZDyOrpLDkQPj1HJ5GoxE2mw12u50hB/g5z2Qy\nsvR7Bw0n8GPX6/VwOBxwu90SFq9CocByGalUCuFwmK0JtZGm2K3FYmFQOz6EZrPZDiW7X5OFetgX\nL0TEXUm90nnSjFgshkgkAoPBgN7eXmSz2QOTpIjK0Gg0ore3F16vVxEJtVywPBQKYWtrC0tLSxIC\nlErxQYJNBYNBBt3ieztR3Ima2fl8PsWYx1rijru7u3j69KkE+0eWttPphNfrhdPplGR0gb/Bqkwm\nE9rb2zEyMsJq6GmDUF+xra0tZDIZ1t+elKrVamV8pqKypnnd2dnB9va24t5YZL0Eg0EGcZNTVvl8\nHj6fD4uLi6wbLiEwqimFbDaLlZUVBINBSVUQXy0UDAaxvr4Oj8eDYDDIDk2VSsX6y/PtkJttWfHY\nYbfbjd7eXkQiEbhcLobZJAQC4aLLtWs+iIIlebdarRgaGkIymZRwJWcyGXYA09oRmTfFWOkQ6+zs\nZJzJPEVnb28v7HZ7TZymL5RCFd2J7e1tfPHFF5ifn0coFGI/12g0jPS2p6cHFy5cgMFgaJiFSp1F\ne3p6FGNbeYUajUYxPz+PZDKJJ0+eyCZpysWoNBoNXC4Xenp68P7778NqtUoA8nTIfPfdd5icnCyL\nJDjot+dyOdy9e5cpdX4DaLVajI2N4cKFCzhz5oyki+3+/j5MJhM6Ojrw05/+FOPj4yWubTqdZpjG\nVColKb0F/sYxe+rUKbz22musaIC3WMLhML799lt89dVXihUqKQ4qBFldXZX93VQqhfv378Pn87G2\n4tUaxPFji0QiWFhYKGlJTAfB/Pw84vE47t+/D71eLzlsUqkUfD4fdnZ2DmWf8V6ixWJhxRSXL1+W\nYEWpW+vTp0/xv//7vyVY83rHoNVq0d3djY8//hivvfaaxIsrFAqIxWLY3NzEvXv38Je//IUl5sjN\n1+v1aG9vx89//nOmfHlZpmIMIgdvtlLVHCcFKvczv9+PW7du4ebNm9jZ2ZEIaldXFy5cuICJiQl8\n+OGHrP1toyZNLimmtD46mUxibW0Na2truHHjhmIBI5LlCxcu4OTJk0xx8YolHA5jbm4OW1tbuH37\ndsPXg/rbz8zMlFgVRqMRwWCQWTTiRTSObrdb9vmBQAD/9m//hgcP/p+9N3uO6zjPhx8Cs2/AzGAG\n+74SJLiCkkhTlkQxicSylaScpCoXucx/lKrcpCpVqdykEsebJDu2NlqiKREEuAPEMlgH2+z7DvB3\n4e/tr09Pn5lzBkOKceVUqUwDmDN9+nS//S7P+zwPsLm5yaBu9N3nzp1DqVTCxMQEhoeHFTk1AoE/\nfPgQP//5z6Utqie5isUiVlZWsLKy0vT1fXR0xNbD63LRvNtsNoyMjGB0dLRq7VcqFezu7sJms+Gr\nr77C7u6uJqFHrUU66rzz+/3S9Nf6+jr+8z//E0tLS5ibm1MQVFssFvT19eGDDz7A9evXMTk5eaIU\nxJ9syC+bdDIofPgoTpCYWG+2gX/Zl0x4TSwaUKhTT7/oZXgzYsJfb15WVrASSbXrVeLp98S09H9X\ncw9TGaqklu79yxgDv9ZFA8gjI3jbIFO7/T4aQgyvy4tUC51l0r+yPKSI8zwJQcWrOs3UCgxqoThP\nRvIyK/xqYxPnXw3hobZR1QopokHVogEvQrqafSA2g2RH732/7/ZikUKQN1L11ptWXlitRp32sbge\neIy2nuaPV2VcW172Rmx0Ql9X+jotz90Ik89J5/dlLph62FAt3K31SMq1erevYh6aCY7/vsbyOnm7\nzXruWof76zJfhmZNnigrLGMAl23CWhuiVg+0bEJl3uzLXMAyedxG2iP5+wFQEBdrwUK+Kq9FbZPU\nUoyV/UzkFZUx/KvxdFL0QfSBzeiQe5WeYqMy3q/Cg+UjBhHfXWtfyWTDG4FyiQZTVEbgERM8HzPP\nA/t9G9emGFSCyrhcrioD4HK5albfeR0iccFQlU8mNsdPbi6XYwqXzVr0lJ8xmUys0i2Oj3gOnE5n\nVU6T8pylUknaR0y94WazWSqP7XA4FCJy4oKn7yaMqniRDpCsMYFykCaTqQr2VO8iXgdiwYrFYlUw\nGJo3XkiPfwai+HO5XFW/I1axXC6HRCKhkEOmd01QG94o0+dLpRJrZ9RbsCJMJImy6eWFODo6QqFQ\nqKKo5J+bsLt601I8/VyzDcXx8TGbM5o3npMik8kwykC1dlmSsk4kElIio1oXYY9l+5cgkna7nSEv\n6DKbzXA4HAr2re/7MjTDmPb39+NHP/oRDg4Oqjo8vF4vLly4gK6uLoYR5WV5M5kMAoEAHj16VMVn\neHx8jM3NTWxubjIKOz4Xl8vlsLW1hbt37yKVSjHilZOc0LRxjUYjg1xcuHBB+rL7+vrw3nvvYWxs\njOmxk0FJp9PY2dlBIBBAIBBQ3J+M6eTkJGZmZthC4XNHAwMDOH36NDweTxU3pslkgt/vxxtvvAGD\nwcDUM/kW4JWVFTx8+BDJZBL5fF6xCV0uF3p7ezExMYHBwUHmMdYLvUnAzmKxIBaL4csvv8TXX3/N\n3mulUoHdbofH48HMzAxGRkaq5s1sNmNychK3bt1CLBZDLpdjG4dIhk0mE+7fv4+nT58qAOZktBwO\nB/72b/9W0dFEekRra2tYXV3F7u6ubtpDi8WC06dPY3x8HF6vl4HvteBQK5UKotEo4wWm5gEeuTE8\nPIzR0VH09/fDarXWvTc/9w6HA2fOnEFbW1tToIH8Xspms9jc3MTGxgZ2d3cZDSZhPhOJBNbW1pBI\nJKQecyKRwHfffYdUKgWXy6XJsaHPGo1GdHd3MzpI8cAgSJfBYMD4+LiiKcNgMKC9vR2nT5+uOpy/\nLy+1IU0p/t9kUD/88MMqjNrx8THjQ3W73WyiRVLep0+f4mc/+xmi0WgVeXUmk8H+/r7i3vS/xCGZ\nzWaxsrKiaMs8iUElYP/g4CDK5TLjvhSv3t5evPPOO4zNhgfgHx4eYn5+ngG+xaIMGdRbt26hr6+P\neYo8wN3n8zH8nOjZ+nw+zM7OYmhoiHnGfBHvs88+QzAYRLFYVJBfk0EdHx/HjRs3cOXKFSafUStH\nylddA4EAHjx4gJWVFezv7zMvslQqwePxYGhoCC6XCwMDA1UieyaTCePj42hra2PeHG0Oo9GI7e1t\nLC8vY2FhATs7O4oiRGtrK9rb23H9+nW8//77DJtLihEtLS24ffs2KpUKkskkMpmMglO03mU2mzE9\nPY0bN25geHgYNptNQdxSaz/Qe04kEggGg1XGkuTWr1+/jkuXLsHj8TC8ar3wmPC/PT09jB6vWfR8\ntI9WV1fxzTff4PHjx6yTi+a9WCwimUwyikox/ZBMJjE3N4e1tTXNAHpyvEwmE86dO4fe3l5FEw3d\nw+FwYHp6Gj09PUilUgqHjSIKt9sNl8v1WuSbT+yhUvg1MjJS1bHDdzXJZGTpZUWjUWxsbGB/f1+B\nO6STn6RzxatSqSCVSqFQKCASiVSF7CcJgWgzzczMqPIS2O129Pf3K0JPHq9JFHz8IcKHxR0dHZic\nnMTAwEBVe6fBUGlnowAAIABJREFUYJCmA/hUQ1dXF7xebxUq4sWLF3j27BlsNpv080Sl1tPTg7Gx\nsbocCHx+qlgsIhwOI5/Psy4w+o6joyN4vV5UKhXWViobO7X0imxara2tzDBFo1EEAgFFe2ZLSwu6\nu7vx/vvvY3p6WsEJQJt/ZWUF7e3tDXXGGAwG+P1+jI6OYmRkBA6HQxOwn9ai0WhUOA5imsbtdqO/\nvx/Dw8Pw+/2K9Fg9g0q0ibXkmBtNbZXLZUQiEWxvb2NzcxORSKSK7Yqkv9XSSwcHB4jFYppDb36d\n2+12pNNp6XoxmUzwer1wuVyKQ4p3HiiV8tqG/FqKQWIOpN4DyYoNfJ8wtZHW2tBqRaFKpcJCx2YU\nCciQp1Kpmj3j4kHBF3CSySTsdjubF7G40traCovFgra2NkV7p8xjlhGPiBLL4jPZbDYF25WY56S8\nlMPhkBoANZ2tXC4Hk8nE5CdIqYD3pFKpFGvZlGkkUe5Y/J6WlhaWJ6Q1QSEe36ZIZM/0fHSVy2XY\nbDbmXekt6tD3O51OxlWrhbyFjJLT6azirxW9KbvdDqfTiba2toYLao0gLeop91KvfjqdRjqd1rX/\nj4+PGa+E3ovSY+VyuaqozUcOtfKyzVAIbmTeZL8zaP2ykyiPqmm0yxa0eMJplQM+CW2Z6NVSeKvm\nWavdQ6z211P/5L1vGYF2vVY5GcJAC1uSSJsmsnbJnqsWvpf3UMlj4JEK/L1FAytyXopMZTzbEPHP\nUisnpXj4/O9JMLr0zmhz02Etvj8ZyqRcLrPiqRqsh1f/5N+dGj+uGntSI3u0lhox5a/5VAId8DJq\nP7XDSG+zB1+Y5Z9VNg8nwe/WKuRpmTc99qVFq8FpNMErmxhR010Md/VMVrNCH/EZG2XxEbliZTrr\nvGqo2veI8DEtJ2gzDpZ6i0pN5leNc1SGE6z1/9V4QUX+UJHKrRnrpRb8px4ch2cC4yFdIscnDy8U\nHQ01Cel67/Yknq3sgG10HvUQf4sNA7wMvWwetO4BPc98UtvWUA5V9FIaOZ1EHBkVpMgzI89DxhT1\nsuAQPC9lLWJdLYTBsrwtTx1HXpX497x3R56QqC0lLirey1PjKpUxldc7gcW5lvFf8l53rXvTuMrl\nskKDqB4MiTxDkVdU7WCu1WLY6Aah75bp3NfbtOQxk4EQPUCRG1bkX1XrVBKfu17UoTZGtYiH/yxv\n2NT2r9oa4h0lPQZZhGnJIi41x6NeJxevJCHjeOU/r2bbeMXjhg0qD1MhTGA8Hme64PzGd7lc6Orq\nYvkvfjJKpRISiQSSySSDFtEDkh5MpVLB8PAw3G73K0kc00vK5XKIxWJIp9MsV6p3Mah5llR97O/v\nx8TEhKKAwucRNzc3GeED733Z7XZ0dHTAbrfDYrEovofyl7FYDLFYrCrMBIBgMIhsNqsZmiNuoFAo\nxPhQ+XddLpexvb2NaDTKcmaiwSXZ4efPn9cVZRQJmtfX1xEMBlWLFPU885NUvyuVCg4PD7GysoJ8\nPg+bzaa5KEXMaC6XC6dPn67i9TSbzejt7WWUh7JUQyaTQSgUYtpN/OFJelLt7e0M0SDKKadSKUZn\nx0d9xMrU09PDlEPFWkBHRweGhoaQy+Xg8/kUh1qhUEA6nUYoFJLmSc1mMzo6OhQ0eXq8Zr/fj1Ao\nhGfPnlXtA6PRyIpSxE3M71OyIeFwGIVCoSqKcTgc8Pv9sNvtLKXBzxvxFdM+4pFClKvv7OxkOdx6\n68BQyx2m3BDpha+uriKXy8FoNLLFbjAYMDg4CIfDoais0ucLhQK2t7eZXjmR19LflEolFAoFnDt3\nTtHL/bJCe55zNBwO4/nz59je3mbA5mZ1WVmtVnR3d2NqagqZTIbxgPLdUFarFY8ePVIA+Cks7Orq\nwvT0NHp7e2E2mxWbmgpmq6urWF5eZvpM/GGxsrKi4JDVEgLx6YjNzU08ffqUiaPx3vTa2hr29vYY\nNyZv+Ahis7Kywho6tIjiEapha2sLq6urSCaTr7wFmRAG9+/fx+7uLsxmsy6sKMHGrl27pvAy6f1M\nTk4y7XrR+BcKBRweHuLRo0cM7cLnmU0mE2ZnZ2EymeB0OquwuclkEpubm3j+/DkSiQQz2jS3pDxq\ntVqrCpVmsxn9/f04d+4c7HY7MpkMa24A/giLIniiuJ5orY+OjmJ4eLhKKr5ekZkUW0WUD0UsDocD\nU1NTGBoaYntIdPaCwSAePXqEZDKpOCyOjo7Q2dmJixcvoqenR+HU8NjhQCCAlZUVlMvlKts2NDTE\nCp38WlZbD3UNarFYxM7ODu7fv487d+4gGo1WeahXrlzB6Ogo2tvbq06/VCqFJ0+e4LvvvmNckbzG\nOwF3b968yTzUl4kn48OI1dVVGI1GxqSuJlWi16CSaurQ0BDD0YlSJkdHR7h79y5u375dRWF36tQp\nnD59mlWdSS2SvI1isYhQKIT5+Xl88cUXCj5UXuI6FoupQl1qhV/lchmPHj3Cf//3fzP8Lx1E9E7D\n4bCiGkxzViqVEIlEcPfuXSwvL2vqCOKhZNRto1fbvhlXsVjE8+fPEQ6HGeRMT7eV3+/Hn/3Zn+Hc\nuXOKMJHu4fP54PF4qirWpBRAPLFPnz6tCvnb2tpgt9vh8/kYkTIVCkulEvb39/Ho0SPcvn0bOzs7\nVTnugYEB9Pb2orOzsypXabPZMDY2Bq/Xi4sXLyp4WokP9cGDB4xAW1zr7e3tuHr1Kt58880q0vF6\nB/ipU6ewsbGBTz/9FBsbG1WRUmdnJwqFAvOi+fQZ8eOurKwwGXtRauXMmTMMp0rqERTR5fN5bG1t\nYW5uDl9//TXS6XSVbfvBD36AkZERqW3THfIT63U8Hsfm5iY7PcVckMvlQiaTkRZgCoUCdnd3sbS0\nhMePHyOXyyn4DLu6ujA1NYWzZ8+ir6/vlRWgKLe5srICp9NZlV+qlUtV81jETqiOjg54vV5MTExU\nfSafz+PBgwfMQ+bDdnpx09PTyGazipC6tbWVSQ5vbm5iYWGhqoOF9xr1YnIp/xkMBjE/P89Cb1mR\nTJbfLJfLKJfLWFtbO7FgXDNyonqucrmMvb09tsb1jLmlpQVTU1P4m7/5G1y8eFFhNEUEhXhoEyt+\nJBLB4uIivvvuu6qQv6OjA2+//TZyuZwCnUGeFnmRT548werqahViJZlMIh6PV9FevnjxgnXe+Xy+\nKmN3dHSEg4MD1okomxer1Yrh4WGcP3+eeeC1RAxFo1ksFrG7u4u5ubmqfPvAwABGRkYwOTnJogV6\nbkp17O/v4/Hjx4rn5p/jnXfeQaFQqEKqkGzN+vo6Hjx4gHg8XuV0+Xw+xZzXWxctWrwu3lXmPRV6\nGbU0WwiCQTAMUWiOClJk0BqBvMgqqmr/iWBysR+8VkFKNCI8OYqsaij7bvrOYrHIckSifDIPepad\nivzmFCuz9ZQrtV7UX12rCNKsd/I6MYzpHSOf46RwkeeekBVkaxUHReFC2c/07lFKp8ggiTJ0ivh9\nBOoXGxH4NchzVsjWvqwARA4bSZrwni1v+HgkkFpUWAv6p1Y0l80b/z2Er9dzuBoaXXRqFVe1ApBa\nEUEmA32S3KXe0LxRueOTjI9fVPVYfNQgVbVUR09qmLRIOWtNrTQTelOPfUvNIDZCp1jrczLGel7R\nVA2GJ/seGSRNbS5Ew1CLaU0cg0xlWE2NQra+6h3UWp+7VnpR7dnVUB38c+ld1zKkjgzCp5eMxqB3\nkfMnLsFL6kktiyeh2t/L9NC1YO+0PrCMzVur0WjEOMgWCL1Aseov/o1eI9TsfKOMYk/v1Ux5ElmU\noPZ7sdlBzwHTCKZVhKpRtFWviFELj6tGCckbhVowKJ7fgWfcr2fgxe+iMFmERIl/x6MCZPtYtsb5\ne/OS7bKDU+3gEPHJ/DrVg4vl144MnthUg8o/AB/aEOSiWf3FtYDNspctht1aNzlV+cVJlG1cetGE\nkWzGM/K0fq8rkbbYKSZudj1zrveSgfuprZWvPqt9li+68DAetc2q13NXGxsVikqlEkwmk6bv4Z0S\nMsh8y7CoQkE0kUS1x69jEcXCp+VIMoZy3FoiQvpOGhu9Fx5TS2Pmmxa07BX6DMlC03rjDS6lEPi1\nRs9Oc03P87rsI0O9xUNcp16vF729vUyEjU4TIukQsZKv4qpUKgx/l06n64Z3/OK0Wq3Y399HPB6v\nyg/xyfJYLIatra0qDaNGO6iIEo1076nn/XW56L17vV7GGiUyUeVyOaRSKeRyOVWN+0Yvs9kMm82G\ntrY2WK1WhaEwmUzo6emB2+1W9fgId9jb28s4SMlTJN7deDyuWw6ZevFtNhva29tZ4YUfm9/vZ5Vj\ngifVKs5QfvPFixeIRqPIZDJob2/H8PCwgpyEKAsrlQpTRaXipMlkQrlcZoVJv9+PSqXCOCR4xrdU\nKoXNzU1WMJN5gHwITmM4ODhAPp+Hz+djKB3eoPr9fhSLRezv7zMjr8ZeJhadqOjtdrsxNDTEpNaJ\nz8Hn86GlpYWxeLW2tjIimnK5jJ2dHYaX1pPjf6UGlfcOLRYLhoaG8MMf/hA9PT1MS5xfEAMDA/D5\nfFXdIC/j4pPlxOP48OFDPHnyRCF/W4vghQ6KcDiM5eVlHB4eVjHAl0olhMNhfPvttyiVSnWxdXo2\nJhnr58+fKyqvr4NhJRD45cuXYTabkc/n2eFJ731tbQ0LCwsIBAI4PDxs6vd3dHRgfHwcly9fxuDg\nIPN8aIO7XC7MzMwoCFD4UHNkZAQvXrzA2NgYUqkU86iAP8K9dnZ28PXXX2NxcVHz+6JiRWdnJ8bH\nx/HGG2+gr6+PYTLJcJZKJezu7mJlZUVXQwAVIK1WK65fv46bN29WsSodHx8jHo/j17/+tYJSkP7X\nYrHAbrfjr/7qrxQRJO8JLi4uYn5+XvM65jlLrVYrPvjgA+ZF8p8lcP2vfvUrXbhdMrgWiwUXL17E\n1atXq3KYlUoF6XQa9+/fxzfffKPwlI+OjhgCiQ6U73sPGWp5KeQx9Pb2wufz4cKFC6pM5Ha7XcGY\n9CqwpCTV/Ic//AG/+c1vGCC5Vt5DBMgXi0VWaeQvOjkfPnyI5eXlpj4PjY0Yel5W6NxouG00GjEz\nM4Px8XEFRId06u/evYt0Oo1wOIzDw8MTy4/wn3e73ZiamsJf/MVf4OLFiyzMJeNJDRF8mon/fH9/\nP/x+P2ZnZ5mXROsyHA7j0aNHWF9f12VQyeB1dHTgzJkzuHXrFmZmZhjDmcFgQLFYxNraGv7t3/4N\nn3/+uYJwvF6UderUKXR1deHKlSu4ceMGLl26pEgBEOzpX/7lX3D79m1sb2+jXC7DbDajWCzCYrFg\nZmYG7777Lm7evImhoSEUCgW2j2ls//RP/4R79+4x71zL2Ai6dPXqVXz00UcYHR1VHBbU3fbv//7v\nuH37Nvb29lAqlaRt5LJ9aDKZcOnSJfzjP/4jg5uRV05R5K9+9St89913mJ+fR6FQUMCyKH2mF2/9\nykN+0WDSKaVWTGoGi3gjhROCdBA4Xw9ioF7SmXBuzQ5rxVzk6xLq8/+2Wq2KhUvGgTawmMs8KUqD\n99RMJhOsVivsdntVH3UtfSNaq3wExecp8/k8nE6nQjlCa68+GWbqNuKpGanZgjh0U6kUw2XXI+6g\ndsdsNstCeJfLVTX+crmMo6MjZLNZ1rGUy+VY9ECpI5IF4VNwNDbqYqNmjXpOAr1zGhvRTYpoAKvV\ninK5zMZGra/1iodEI5nP52GxWKpSKbQWyAsuFArIZDIKqs7XTdTToHUxaTnRGtm8eqq6YhWOXno9\nApeTsPQ0WkFvhA/gZYoL1sKTymgVeb5VmWgeX5jhYSd6FzZftaZ55teZDNJSz0jJIE18qCjT6dIy\nbyLEhlegoPtS624tfLOM35YvKKmRiovFUj4FJt6f3g/NKxVxiNxG60HOQ8HUYFsiXaTW+9M74T1x\nGdkQjyx6FU7ISfahoZkGQg2CJMN96cE5iuxKWsDRsk2g10Ot9/mTeL+iweA3Vq00hexd8Iu61jOo\njYev1tYq5qlRCopqmXo4bMWxiwcoD/cRsctqa1RstOA3Jn8A89FMLRYltcOdZ0vjoUm11ot4QIiK\nBWrvmDdovMfM81/IqO54SJdWzKbsQOKNoMjZy8+lnohFPEx5NVPSddOyx5tlQGktimvupQD79YKj\nxU0hThYvraCHJo2n4iJ4CP8z2YusB9J+GTnekxbcavGpyv6/VuMuA73XkoGWPRNBV3gvqZFFLkYe\n4qblja3ehS3b3NRxI6Nxqzc+MUISjSMRNPOeYa3cofidtBfU6AplksmioyH+rhm0hiL/ba0mEy3r\nSO2wp1QNf2jy0ZB4EDXK1yqLeEXMLp+f1Wqb6halmmVM+DCDh4LQaak2aBFcK9vU4iZR2yC1Fng9\nEbdG9cW1AMTVTkCek1MW3vDj5dvytISvfGjKq53W494U2yBpEYpk0jLDo7aJxIoub0BlOl0i879s\nrtXmi8ZLG1cm+1Jv3kS8Je/5Ej67lgco64jivaJ6+E3CXPJgeN7TFRUiGt3PajwKfPMCvw9Fj06v\nseMNKn9Y8d8n1kaa5QjJ0hk8R7FeOfLmCNnXMMpOpxNTU1MoFAro6elhC4L62N1uN2ZmZmCz2aQv\nlsgLIpEI44mkh4/H41hdXcXW1pa0ymc0GtHV1YWJiQmmnUQGxGAwIJFIYGdnB6FQCMlkUuENknhY\nf38/xsfHNS0UvvKZy+UQCoWwt7eHvb09xean7x8YGMDw8DAcDoeCvg8AxsfHMTY2BrfbXUW2TMJl\n586dY1yuehavw+FAe3s71tfXkcvlFAcSjW18fBxDQ0MKTSwqGnV1deHSpUswm82Ymppi76OlpQX5\nfB7pdBrr6+vY39+vyj+bTCb09vZicHAQTqdTAYAnVVO73Y7FxUUcHh4qaOhaWlpgs9kwOjpaJWxI\nRuXg4AD7+/uMV5Q3hKVSCalUCgMDA/joo4/0eR4GA+P7fPjwIba3t6v62Xd3dxkVpGjwDQYDenp6\n0N3dDb/fD4vFwhwJ4hSemppCR0eH1AiazWacO3eO8eAS8oFwpkNDQ0xOuZkUmC9evEA2m8X29jZu\n376NQCBQdcgGg0FsbGwgk8lIxTTr1ScODw/x+9//HqFQqKqHPxwOY3FxEaFQSLe3WM9Bslgs6O3t\nxYULF1iRj3LNZGdmZ2cZ09SJCKZPOmh6cKfTienpaUa8S4uLuh0cDgcGBwdhtVqlEx6NRnHv3j08\nf/4ckUhE0a2Ry+VweHiInZ0dKe+nyWTCwMAAbt68ic7OThiNRmZQiXvzzp07rEJJoGJ+A505cwYf\nfPCBAtivNrF8F1Y0GsXS0hLm5uawt7dX5TGYTCaMjo7ixo0bjFKN98x8Ph9GR0cVIHYeytbR0YEL\nFy6gra1NE48r793lcjlEo1Gsra0pmI3I0zKZTPjggw/YuHivi4iOL1++jJ6eHsTjcZZ2oUNqf3+f\n4XhlBnV4eBjvvPMOurq6GGCdjH0qlUI0GsWzZ88Uoo1kcDs6OnDz5k309PRIvZa9vT3cv38fz549\nQyQSUcCrTCYTW2+zs7OaDkg+iiEiYmLh4j0nYnza2Nio6tyhQ7a/vx+zs7PM8FHl/tSpU7DZbOjq\n6mIGVbzMZjPOnz8Pt9vNGMD4fdTR0YHe3l6Fym6zPLhMJoPNzU18/vnnaGtrqyJvSaVSCAQCjAJT\nz0UG9auvvsLi4qICHUB7fH19HQcHBwy83wyjSnPa29uL4+NjeDwe1jDA8//29fUpnJpXblBlJ2tf\nXx88Hg9j++bDFcKwylRTX7x4gUQigadPn2JhYYFJRdNCps4XgnWIiXSj0Yju7m689dZb6OvrU3wv\nKWju7OwgGAwyyjbeoyBt+TfeeAMWi0UXae7+/j4AYGtrS6qAaTQa0d/fj7feegu9vb1VBR2LxQKX\ny6UgI+bzdS6XC2NjY+jq6qoLzxFTKMFgEI8fP8bh4SEWFhYUPLA0NxMTE/jBD34Ah8NRFZqTTHNv\nby87hOhz8XgcwWAQT58+xePHj6tCdqPRiL6+PszOzqKnp4dtUPLUAoEAwxevrKwopGEIr0lUbmIj\nyYsXL3B4eIilpSU8ePBA8U7pfQ8MDGB2dhbXrl3THPqS8sT6+joymQw2NjawtrZW9WwEcKd0lLie\nuru7cebMGVy4cAFer1cRShoMBvbOZWvMaDRicHAQPp+Pwfj49UxdXFqZ5fV4kUR+XSwWWUTBr/Vy\nuYxkMqkbU02poUQigWfPnmF9fV3xPvmuwlwup8v71ZK+MxgM8Hq9sFqt6OnpUciR09/abDZFBNkw\nY38zijK8YSJsnQyKUitEIR34vb09hEKhqsJNrapya2sr7HY7enp60N/fX0UeG4vFmNESkQeEkWtv\nb0d/f78qBlc2Z/Tv7e1tBYekeH+n04menh4MDAxUhfUydAHPp2CxWJjMitZ3QnNGGyOdTiMYDDIP\nl4cWUQpEBqeyWq3S9kUKyY+OjmC326sWIS8F3d3djf7+foXHQy2GfDqGPygp10htxrJnJO97f38f\nu7u7irG53W643W44nU4MDg7WVeHl541aVmnd8CG/WtFKzBmTrE13dzc6Ozt1sbbR+Nvb21X3kdrP\nZAgKPRcZtVqppUbhTLQew+Fwzciv2VhTPoVktVoZibuabdJ6QOmSkT6pcVUzPvXo/yjZz8NS6hlT\nPlFPUs0Wi4WFY7zMcS0+VB5ZUE9HXfRg68lIHx0dMe5MSilopZsTtXW0vgexD5u8U9HbqdXpImPi\n4Q8AIryQESvTc9N74N+r+E7Eyr/InauW6+TzrhRC0mFBRCHk/aitHX7d86E9z4qkpZlFlCohYhJK\nE8go47QUOtX2kVpB6SQ6aaLB1lu81ZpaUYv8tLbI6imUi1C9WnOq53ppRalmIAZogYn4Ob0cprU4\nDxuFkcgmvRYZhNohJWIjtcoWi0ZV66EmA0jLCIC1qBKoLULRS1NTRRXhW7WMm6isWWsDqsHLZIeA\n7EBXUycQyZFlsCo9+0FckyelkVSj5FOT5tbrGGmN0Jp5/2Z4puKzv0zdOoOeB23Epa/nNmsloFUD\nfmvxyAgiw+caRWJbLQB8cSOL8yFjClfzEHgDIZJ86NlcWrykevAlMm70/QTf0QIlUzO+fFeSGPLL\n+CzV1oI4x1o2Nv9eRdgNwXzUQPj8WpVBxtTSMVoOMx7uJOPmrecViU5FrUNTZlTqrYV6xOX19oea\nx6kFRqfV85Xdu5YMtLhWxQ6zk9imhg0q9dGSAqYeQufW1lbYbDaYzWapnEAzmeZl35/P55noGl/B\nMxqNjIJOpP6q58nSvwkdwBsg2jTJZBKpVEoK51Jja3+ZJ6iYjLdarXA6nWhvb1eE/IQJpD76egtN\nxPFSWO1wOODxeGCz2RSQMBKbEzGbsudvZA4sFgucTifa2toYbIruSZCsYrGISCRSZXwop2axWKqE\n7AiZYbPZ4HK5mBgdn/4gCe1CoSD1kvP5PJLJJJLJJEwmk4KZidAVagXaWnNBTQHFYhH5fL4qlVAu\nlxEOh6WKpfTcZrNZwdHQjL3I5+wLhYJq0cpoNFapJuvJ7xaLRWSzWSnCgKgNo9Eowx/ze5We22Kx\nqNYsTmxQ+cmsVCqIx+MIhUI4ODhAsVjUtNhpEVmtVvT29sLv9yuUA182dyot8EgkgsePHyMSicBk\nMilgU4SVzGQyig4JLZ7vqVOnmHRvMplUULkZjUaEw2Gsr68jFos1xAL/MtMvVqsVfr8fo6OjSKVS\nbKFRzzfJCsvIpetdtDmGhoZw/vx5hjumHCJhe4mdrJkHBRVuhoeHkUwm4fP5FLygNpsNPp+PqXiK\nyhEmkwn9/f3o7u5muGXeI3U4HOju7sbExASryvMA9Ewmg/X1dQUdJJ8vj0QiCAQCsNvtaG9vV6wZ\ns9kMj8eD4eFheDweXaqhVKgLhUJsPfNpsmKxiO3tbcTjcamnSFyunZ2dDMHRjHVKeepYLIZQKITd\n3d0qoiEqUo6NjcHj8eiKzo6Pjxnee2trS8pxm06nsba2BpPJxLhV6b0Tntvv96O7u1tBmtPUkJ8P\nmwqFAra2tjA/P4+5uTnEYjFdBrWrqwvXrl3DpUuXWOVXDIdflkEtFotYXV3Ff/3Xf7ENzGtuJ5NJ\nBINBhEIhViTRs5C2t7fxm9/8BoFAQKEOSgD3cDiM/f39pnd3NLq46Wpvb8f09DTa29vx5ptvVklc\nGwwGjIyMKLxLrUaNCMdv3ryJM2fOVB0mRqORHbDELNSMPDt5Q8PDw7BarYxejw5wEkZMJpN49uwZ\nfvvb31Z5Sy6XCzdv3sTVq1dZYY5HVvj9fly6dAkdHR1IJpMK2BYpxf7iF79AIpGoyo2Xy2Wsrq4i\nk8ngwYMHDNhP9yac9o9+9CNWcdayvwjStbe3hwcPHuDu3bsM98wXAVOpFKP9E7uRSMr98uXLGBsb\nUzBKnfSwy+fzWF5exvz8POLxOOMW5rGmfX19+PGPf4ypqSldud5yuYxIJIKFhQUkk0mpQQ2Hw/jy\nyy/x6NEj1jxEc9fW1obJyUnMzs7C7XYzLPhJbFNNGWniUjw4OMCTJ0/w+eefK6AoWq7R0VF4PB4m\nB9usRLPWCQ8GgwgGgy+lgHZwcIDvvvsOCwsL34uOvB4jzT+b0+mE0+nE8PBw076TB0uTt6XlahZp\nNxkI6kYS70eb79mzZ/jkk0/w8ccfV93H5/Ohr68P09PT6OzsVG4UgwEejwcejwfj4+PS0HNpaQkL\nCwuYn5+XIjrU1qLRaGRyxVrwseIepZB+aWkJX331FVZWVnTVNiwWC4aHh/Hmm2/i8uXL8Pv9Jz7o\n6PPpdBputxvxeBxzc3NIJpMKsvbW1lb4fD5cu3YN165d0yWnlM/nEQwGUSqVcPv2benfxONxJg8t\nXnQw+nw+zM7O6rZNsnFqirlEcgI+sV7rRdWCDDXDM/m+L56cpZ5i5et2vWylVy1MQy/7+UTVUx7y\n1Gj+vhb+bzTcAAAgAElEQVR3rp6+bxl/A08OovdAEZEwYitzvYsnMBJ76PVefI5Si44XT3lYLw3E\nF3xFAUKt80TfyXNbaC0MnrgoJZO5rfeyZNg6WXW9nt57s+m5tGyQehV/2XNphUq9rkazkXvUglTp\nuW8trftmYJ/FzSF2+cieSQ/uUWslW82D49fSSUJN2T49idprs+aeN7BaDGWtOZZ9j9Y5r1X81WKb\nmgrsV5ssNQ9VL9D2ZRiCk95PbZO/Cu/qVV4vi9bwVdIlNsub/b9LbpwbDfebQZx+0sNPZrtqNTuc\ndB1ogk3xp0C9k1hGuyeGyWonhjhZ34c8iMjj+jrpPTXbsOkBib+scdXSWW/GvfnNzUtMN7qBXiZ4\n/nUxoiddA3o9PAq91bhkm8lLUAvX3kijhWaDKp4AvLaUnov+ntosZRi7Wnkdyq3UarurdTW60BvN\nZ70ul5gvlG2eWgzudJioff4kIWqtnBrfQdXoc8t6v3ne3UZQF6LMjvjZZlDL/al4t3rngcfxygwo\n7d9G8rmiHIxom3jFWhkeXa/9qCsjbbVaMTIygnfffZdpe9d7MB5+Q0Jbd+/exb179xQM+1pC/62t\nLayurjJCDD0vi6qXV65cYUBsrfcwGo3wer04f/58U/CSr9q7Xl5exsOHDxGLxRh8iBatx+PB0NAQ\nxsfHMTAwoHjvZIjn5+fx+PFj5HI5Bvin5H9/fz8mJyfR398Pr9db1VFUK21SKBSwsrKCp0+fIhaL\nIZ/PK4qee3t7CAQC2Nvb0xwh0Ho7OjpCIBDA2toatra2GMaWxp7NZnFwcICNjQ3N64/vww+Hw9jZ\n2cGzZ89weHjIpKx5Xs+lpSXGz/CnnBKq9y60zmulUsHOzg5++tOfYn5+XrEWisUiXC4XpqenMTQ0\nxLCiemxAZ2cnLl68yKgNeZpKWht7e3v413/9V+Yw8pzJo6OjuHLlCjwejybDWtdDJc5Au92O0dFR\nBVC73qQajUZEIhF89913ePLkCQKBACMC0eohZLNZHB4eIpvN6iZ4MJlMGBoawq1bt9Df3w+z2aw5\nQd7S0gKLxcImstHT91UbU7q2trbwu9/9DltbW0gkEsyglstlDA4O4s0334TD4UBfX59CIoS6bp48\neYKf/exnSCQSODo6Ykbp1KlTuHTpEiNF5g2q2mbix1YqlbC6uor/+Z//wdbWFpLJJPMUTp06hWw2\ni2QyiXg8rlqRl3mltFGCwSC+/fZb3Lt3D/v7+4rOn1KphHw+j8PDQ90G4ujoiPG0fvrpp1hZWWHK\nopQGKxQKODg4UBBM/99Ve24rlQoODg7wxRdfMJo8eteFQgFdXV1Madfn8zGDWi+FQPPf0dGBq1ev\n4sKFC+js7GTr2Gg0IpvNMsfj/v37jIWN1rnJZMIPf/hDjI6Ooq2tTVObd10JFKIdI2yhntZTPqQk\nnsx8Pl9FVVcv7Ce2qEZc/fb2doyNjWFwcFCXIafxUzvc/6bwn8iQ19fXsb29jUQioXju1tZWDA4O\nIpPJSBfn0dERQqEQlpeXkUwmFXlxs9mMnp4eJJNJ1vWix3gcHR0hHo9jY2ODjY3fRMTIJJI0azlI\nXrx4gVQqhf39fYb5FHu5aT01EuoTNeDe3h42NzerpHfo3n8q3umrWqu5XA67u7uKzjSaT+owo9bS\neggQMX9utVrR39+PkZER+P1+hUGOx+PY29tDuVzG3t4eksmkgrG/tbUVw8PDrJW4HvKgpofKGxXS\neyGy43r5Vt6rICZ+6rclGRM9G1HNS9GCdaRWSNJjV5uYWsUbMe+mpZjTTE7ZRsKxcrmMXC6HTCaD\ndDpd5fUXCgVFTpGnNKMus3Q6jVQqpXjmSqWCQqGAYrEoZYzSMp+lUomNLZPJ1FTsVEsdiLAcntgl\nn8+ztaZmeGVrqR4RD/WN0/1ljoEeJIgWaW+1+eSVaBvhO32dHISjoyPkcrkqjoujoyPk83kFHaTe\nvdXa2gqr1cpsAN8NVSwWGb9HPp9nLbt8N2U+n1etRTRkUPmXJ8P1yXJnfBeETJRMb+isxkakBb7F\ne7g85yg/llo0eDK2I1F9lR8nj3A4iadyUolrItug3/MSK6I+vQzFQd55a2urQmJF5FXlPy9KPatt\nWhqbKAut9syyn4la7fy9ZOqZMiNVy9Plv1ccJ6/GKa4RvWkpng5Q9nxqBpXyy7J3WOv7ZPPyOhhY\nfr3w3LPivDeyj0hZmQqKfAMBvy7IeaTilMlkUuyhExtUkYlHLdyvV4yQwTEaBR3rDfvVpKa1eqi1\naMkoJKnFkXkS7/Qki1xUwazFUSoqGZjNZpawl0GQ+IS+eOBpGbNMMllNLpv/GaE+KL9F4+NVYusZ\nR7V3wxNJ846A6BTwBVXZAaB3XfNetixnrDanPOUj/060NrGI81Kvm+lV1gBEms2TjIuHZIlzJu4x\nUUaa7x5rikHlH4g2qOyEJyZ1PZ0mWsMTsb1TPN3JoIkPLv6bp9gTuVJrecAEt1ELq4E/IgJ4zSn+\n5ehpjRONDm8U1fhGtagdWCyWKno9ItUoFArMe+UPCnGuZHrm9HkZc78o1SwzXiaTiRV2ah2y/L15\nr5CYz/iedmLEJ1o2PWkli8XCcmjFYlExL4VCgb1vunczvDqSCaJ0FKUU9BTMCoVCVfpFRk3IF//4\ne5AE0PfpnZISA78PSdH1pGMjdYRCocDmmdI3VCQnSSGq7ovO1Ik7pXgrnc1mkUgkEIvFUC6XFXyJ\nLS0taGtrQ3d3N6xWa1MLOCSS5ff74XQ6FVX61tZWlMtlpNNpxONxJJPJKsNHBZDl5WWk02m2QcjY\n2Ww2dHR0wOVysbHzksSFQgGxWAyHh4eK8IqueDwOj8eD0dFRZLNZRf9zsVhEKpVCPB5nRSE9J3Uu\nl2PPlcvlFGEQccx6vV54PJ4qw3Xq1Cm43W6MjY3BarWyHCq9F5IxjsfjeP78ueIgpMPp8PCwyouk\nOU2n09jd3cX6+rrC6BObFNED8nSN/OHb0dGBsbEx2O12pNPputVT3qC2t7ejVCphcXFResCmUinY\n7XYmU621L/vFixdwOp04deoUo5nj2bDK5TIODg5wdHSErq4uTWgXre+b1H/b2toQCoWwuLio6cCl\n+czn89jY2MDh4WEVPR7tUYvFgp6eHrhcLkW4f3R0xHSuXC5XQ5SNJ93jdrudUSbyY6tUKkx/S49Q\nnlgv2NragsvlQiQSYbbr1KlTyGQySCQSsFgsGBkZYfuML0qRIvOJDCqfOyImm0AggJWVFeRyuSoa\nvMHBQYYE0FPB13K5XC6cOXOG4cho4xoMBmQyGezu7mJtbY2pIvL5MqI1u3PnDjo6OhjPI4WOfr8f\n09PTGBwcZF4bj49Lp9MIBAKYn59nUAp+IZRKJQwMDKCrq0vBAN/S0oJ0Os2UO8VKuRavPZlMYnl5\nGdvb2wiHw+y+R0dHjNvxzJkzcLlcUoPU3d2NN998k+nTiwbZYrFgd3cXkUhEwdhPnufa2ho7wWW8\nnktLSwxDWCqVWPRis9ngdrtx+fJlOJ3OKqPDq72Gw2Fks1kWJWj1UHO5HL788kvFWqP5KRQK8Hg8\nsNvtCvVKrd4eADx79ox5c3SQ0vsulUqYmJjAyMhIUygoeeSFyWTC5uYmdnd3NWNkTSYTyuUytre3\nsb6+zgpxYtTgcDhw7tw5xnNLz1Yul+FwODAxMcFgSXrSNyc1pq2trXC73bhw4QJ6e3tZaE7rkFA6\nXq9XgQLQ2tqcTCbx6NEjpFIptLW1Kd4pRSJ2ux1XrlxRKFhQdDc9Pa04hBpWPaWBFQoF7O7uYmFh\nAd988w0ikUjVQn7jjTcwNTUFt9utqxNKSyjg9/tx/fp1nD17lhHQ0vfSxiZqtEKhUGVQt7e38bvf\n/U7ByE1GYnx8HC9evIDdbofb7WbhXmtrK0qlEmKxGJ48eYKf//znTC6Zv2ZmZvD222+jt7eXcYfS\n94dCITx9+hSFQgGBQKBu5Vs0quFwGHNzc3jy5Ak2NzcVWEvCjxLwWERfnDp1CgMDAzCZTCxU5Sun\ndEA+efKESTXzBv/4+BgHBwcKhnXeQyWs5draGlM5pXG7XC50dXWx5gGxs85sNjNcn4xdvp5BTSQS\n+N3vfodPP/206jMGgwEzMzM4e/YshoeHmZ66VoOaTqfxzTff4N69e4y7kz8Iuru7MTY2htnZWQwM\nDDQt5Cdy6s3NTdy+fZtJVGsxxGQYKIqkaIQ3LCSX/O677+LSpUuKgszx8TFrYmlvb1fIlr8Kg0ry\n2u+//z7OnTun+E7eeWhra2uoezEajeLevXtYWlpiz0Zr3eFwYHBwENPT0zh//jyTTOfnlpRytXZL\n1eVDpbB5c3MTjx8/ZuS1vEFtb2/XDbzXejmdToyPj+PixYvw+/0Kg7q3t4dKpYLFxUVFqMKHM5FI\nBJFIRJofJW+DyKFFMbZsNotgMIiFhQXk8/mq3JPf74ff78fMzAxrAKDPk4F/9OiRoogg5lNlLD+E\np9zc3MSzZ8/w/PlzRcHF5XIhlUrh8uXLVbr1dBF3pyxUXF1dxcHBAfb39zE3NyfNEdeiWkulUkil\nUtI5dbvd6O/vRzQalWpuGQwGNm+NGJ9gMIiPP/4YCwsLVZVwMnptbW04ffo0BgcHdW3AUCiEu3fv\nYnNzk3l79HmLxYKZmRkMDQ1hbGwMFy9ebNp6r1QqCIfDSCaT2NnZwb1793SNWwsSxOFwMDJlLe3j\nJ1EwrVdEElE/9L7IS9QSSWidn2w2yxwa/rlevHgBn88Hu90Oh8OB8+fPw+v16pqLhopSdMLR6UAF\nB/JKSI9Fax5ML9fg0dERCoUC8xYoX0f4MT7crLWgxMkh+BCPAJB5yHwlm/fMqdjEfz8vjcyPrVaF\ntVYoZDab2djIq6hUKixkF8l4RSYdsXLOHzb8oufF43jDqQU8LR5gBoMBNputZrtuI5AyKixQIcpq\ntTIPmiILvpgnVm3VPFURQket0vT3vA4ZFQL5gmWjDO9iNb9SqTC8pVgQ0XqvWoVe2keFQkHa+n1S\nhql631/LKPNj471I2R5upFtRhIvRd/Jrn68fiDZDz/s16B2QLD+jpRVVzymnVvGWwVXUfqeWH5MZ\nWxlERQvrkYjPFRe3DHkg/p0MwkWblA8zZHhIWZK+lhzyqyg0aGWL0hqG8++Fx5zWaqCQkaPUGgeP\nopBxZNaKJk4yTzwwv55X1yjlpUweXDRMzTCmsrVXr1mG30P8Pq7lzZ6Ep1VG+FTr7xpJfRi0GjSR\n0JU2PRV4tLzQkxIH8ydMPXB2owtf7XCo9cLVvGFZVVb00GRNDzxzOn+K858ViUNkzRa8J6KWcqB7\n6yVHrjXf9UhNGmEO4gtPvHdIkQEVdtQ2pJgD45+B/xwPweMZkAghIhqlRkHnfLFLzaNs1kXPQnhM\nMeJq1NGpV2yqZ0x5A8njaGVroxm4bi34bt5ZeSky0qLLS5hTOl1FMTO1xDMtaEofaD1xxa4e0QDx\nv+O/p1a4ygPLxc1DYSt/UNAzi6EBDxaWGUZ+bISzo41EmDeS/+W7mGRytjTHFPLTc1KoWC+EFg0S\nPz80tpOApykFQtVqtSS+6JFo9SIBsI4XWnd8CoQMkIyuTav3ReuT5oOXHa4FEG/Es+PhObxh5psm\nZKDzepSK4vonJACxKJVKJRgMBoUTxH9/o+kLGhs/PsrV8o4UPR95gpTW4tM5onwSv4/UnpvHlItd\nm1qpFfl38VL4UOlhCArT2dnJNN3p5LZYLEzBUuaaGwwGtLW1wefzoaurC5VKheH7ahkBegF+vx9W\nq1WKtRTHRtreokcoC6mLxSLa29sZkcjBwQFaWlpQLpdZdTwajQIAenp62Male5fLZXi9XlitVmkb\nqsFgYNr03d3drPuIjCapsIZCIbaJ+bxuKpWCyWRCe3s7enp62GIplUpwOp1wu92oVCrY399HMpms\nKXZHc03fE4vFUCqVYLfb0dPTo1jkjRIuEwTF7/ejq6sLdrtdtZU3k8kwcpV64xZzqIeHh0wpkwdm\nk7ElyFQjlIuEqe7q6kImk0E2m2XsQ8Af8bsej6epSBZ+vRAuure3V1HR5ovDmUymykBQs4bdbofT\n6YTJZFJEVGazGV6vF+l0GsFgkOEqeUy30+mE3W6HxWLRPXflchmJRAK5XI69UzKW5XKZ9cj7fD5Y\nLBaFTDWtcVIgprmltWgwGOByuWCz2arwoDxXR2dnJ2tS4ddToVBAPB5HPp9/JaQ1p15IdhAvskWU\nZJubmwgEAorOGnrg/v5+XL58mcEL+JMvlUohEAhga2sLBwcHbANoxdl1dnZiZmaGAX/5exO13/r6\nOjY2NljTgRbPl/CM8Xgc6XSadafQQiMwdHt7O3w+X9Wpf3x8jMHBQZw9e5YB5fnGgEwmg/39fayt\nrSEQCCg6suhEj8fjiEajikVIv7fZbPB4PHA4HLBarYrCSKVSQT6fZ00DIkZWzfDRnJrNZjidTrS3\ntzPwux7MZi0vhQ64s2fPYmhoqGpz5nI5zM/P4w9/+AMODg6QyWTq4lDFDdTR0QGPx6PwJMhDGh4e\nxujoKHp6euBwOFQ9VFnaolAo4Pnz5wgEAohGoyiXywrMtd/vR19fH8NFyngN9MwXn0PNZrPY39/H\n48ePcXh4WKXhls1m8dvf/pZx3PKYa4vFgr6+Ppw5cwZXrlyB3+9nFIL0N4VCAYeHh8hkMoq1Vi6X\n4XK5cOnSJczMzGB4eJjtM1n4LQufDw4OcPv2bTx9+pThmnkHwW63o62tjUk1i+mvbDbL8NJ8KqRY\nLMLtduPNN9/EmTNnMDQ0pGi2OD4+RjqdxtbWFp4+fapAnpDDtbGxgc8++wzr6+tIpVIK+CGprd66\ndQt//dd/DbfbzYqcTfVQ+ZuZTCZ0d3fD4/Fgenpa2qdPp6NsIAQaHhoaYrkuPQUJOrllNHpWqxU9\nPT3wer04d+6cJsgHH3IvLS3h008/xYMHD7C8vMy80HK5DJvNhuHhYXz44Yf4y7/8S0W1ly6TycQq\n2uKmstvtGBgYgN/vx+XLlxXhSaVSQSaTwa9+9St88skn2NnZYYcBpRPOnTuHjz76iGF8KUVhMpmQ\nSCSwurqKX/7yl/j0008VzEf1iiDlchnDw8O4du0a3nrrLVy7do2lN04CVOc3GHVL8br1dJVKJayv\nr+PLL7/E2toaYrFY3ZQDvxZ6enrw93//97h16xbzpvhoh9pCtdIu8r83m82YmJjA4OBgFTaXD52b\n1RHIvzOimfN6vVUwttbWViQSCebUJJNJll4h49XR0YEzZ87gz//8zzEyMsIoCskpCgQC+Od//mfM\nzc0xZidqViA4os/nq3JctFzpdBoPHz7E559/jmAwyKK8YrEIs9mM2dlZ3LhxAx9++CHrdKO5KxaL\nePDgAb755hssLCyw39G4+/r6YLPZmMQ3j7kmz3p8fBx9fX1VeWeDwYD5+XksLy+zw1sP/WhDkYaW\nkI4Wkt1ur5m/USNxIHe9kRxdrQIGGUaTycS8Ea3VPvostZhmMhnG1Ur5QOo6aWtrk/aFi3AOcWxi\neMOHrmREqD2VwPcUGZRKJUY95nQ6FQWU4+Nj2Gw2BkZPJpO6DikC1FO4RN5hM1uG1e5FVGmJRILh\nWbWgKSgn53A40NraCq/Xy9IotSA2eg2c1WpV5QAQoTfNREZQflZcL3zIT/BEWQGSeBHIG+RzyuSd\n5vN5ppLAe3k2m43R5NVilVO7yEGgd1osFtk+cjgcDPJos9nY2HiDarPZWLTIN1MQFjyfz0v5cWne\n1N4Z4W/5nP7LRrpoMqj1FiePAGhWVfekG1etOijm7GTigyL7Do8/1JtblH2ODyt4TGs90UIxYc7z\nEmgZj1jR5helXsC01sqyrKorzq+MIrFW4YsvVqrNr6yqqwWW1Oha1coyVm9+1djNeEOqRp/Jrw3+\n3zzWmp93NS5VGS1ivbHzzExq71WG0uFbTfl7yFJsYqpEq9P1KrkJDHoXTD0oRC2vsFkYNz1jE6ui\ntYogfBVfTbNbbUHXG5eorMgTqfAUbLVSFSJwXw+ZcD2vkQ6Okx5wssOVh9mJlVl+89ej2OM3jtjZ\nJhrsRiE39eZBCy65UedE/Ly4Zuo9j4zTlp8TWaOKiMGt5STViiTEyEBtDsX3w689EQ+rBguUrREZ\nV8b3wfHaNPW5ZgC5X9Znxf5c8VSXvUytB4BWbRvZwiJqQB5jKoP68F4kjZdUFF7Xq548uBpFYCMR\nyeuwkfR8dy08ZK2fNeptkYEtl8tVzPdit1yttEktY6pHgloLST2/D3g4pN6xvRYGVcui5RcGseLL\n+tT5zS/LYzRjImqNjec9FDtDiKFKy8autwDqbTBZXzu1l4pFAIKmUb6TtG7oc9lsVtGm2Exj0Ajg\nXuYdqcnyptNpVoAjRigxrCde03rPJ5t/OqTUeGS11AuoyCjmlmulDui5SR1CFp3QvWXcvnTAUruy\nOO5UKiWl5tOzXokbV+zlp7x0qVRCJpOBxWJR3JdSK4QZPWkDgB5VVEppFQoFxrkh1kLEduHXzqDq\nuUjQbXFxEalUSpEMJ2qwwcFBdHd3M9jEy5BdkBnVUqmE/f19xocq9u9ubW0hEAggHo/r0lVvZNxi\nq5/RaMTw8DB++MMfIhwOV+XwvF4vstksY5vitcmz2Sz29vawtbUlNVqvOgoQq/iZTAYrKyvY29ur\nOkiKxSIymQzOnj2LsbExZvjo4I1Gozg4OEAwGEQ8Hq/LJyCGp6FQCLu7u0wpl5AGWhofTCYTRkZG\n0N/fX0U9WE9xgkhjVldXsbu7q0C0UH58YGAAfX196OjoYAVRHtYUDoexurqqYHSje6TTaayvryOT\nyUiVCWpdJFZ55coV2O12BYqAisYOhwPb29tIpVKMhpPmjHCe4+PjcLlcr6QGwvMCBwIB2O12xONx\nNm9Uh3A4HOju7sbo6KhqYfpVGllDo5uHJ3XY3d3Fl19+iZ2dHcXpWiqV4PP5cP36dQbQ5UPXZl/8\n2MhLIvq+g4MDtpDoVCP1TZ4TVG/OrRGjRQiD8fFxhlnlcabA/68Su76+zqr45NWWSiXGAKbmtbzq\nizyGYrGIaDSKubk53L9/n8GxyOgYjUb09vZidnYWdrudwdHIAyJaQfLM1TSXRM+QDNPe3h7u37+P\np0+fIhwOK7Sr6jkGdrsdN27cgMPhYJ4cn39UE4nkgff379/H/fv3mZIBNYu0trbi6tWrDJdJ4Hu6\nZy6Xw87ODm7fvo3l5eWqIlS5XMbKygpSqZSi7baed0ohs9vtxttvv42JiQm2D2hNEdacnItSqaSQ\nlPH7/Th79iw6OzsZ4uRlGiv+uTKZDJaWlhg/MEHFCKXi9/tx4cIF+P3+qkjvf10OlafIm5ubw/r6\nelXCub+/H/39/RgaGtJ9sp70Ipb1e/fuYXd3V1GQImgSgfpf5dhokRP4XPSOj4+Psbi4iJWVFQQC\nAQUfKv2ePEG98tpavMyTeqipVApra2uYn59HoVBQ/K3L5UJHRwcmJiZYdxuvVWW321EoFLC8vFzF\ngFXvIg/1+fPnePToEfb39zWLQhL14Pj4OM6ePVsz3aCmeZVOp7G4uIg//OEPVfAfq9UKn8+H4eFh\nDA4OKg4hgu6Fw2EsLi5iYWGhKo94fHyMRCKhu+OHvsPpdGJqagpDQ0NVaZZwOIx4PI6DgwOsrKww\naW+KHHw+H1paWvDOO++8cgNVLBaxv7+PRCKB9fV1BZmMyWRCZ2cn7HY7rl+/rntt1/p5o8bYoPWL\n1Lw30tXe39/H9va2wmiRJEYymVSQFWu5r9aiT70NRqz+/Nj0pA60Tqzel9bS0gKn01l14pO3tL+/\nj3K5jGg0iu3tbRY2NioIpzVfVQsFofZZ8TAoFAqIRCLY2dlRyAO/ePECHo8H5XIZHo8Hvb29rDuF\n5iSRSMDtdrOwU+/CzmaziEaj2NvbQzAYrKuUIK7jeDyuyLmrKaDKPl8ulxGJRLC9vc34Gejv7XY7\nYrEYcrmc9PCuVCqs829ra+vEKRhxDZM3JzMcxFVB3X3hcLgKE00dfbWY215GSqlSqSCZTCKVSlXl\nsU0mEyqVCpNmEudU795VI3GqVYxryEOtRztHPfVms5mBeinUoSJLLcZrLXLJjXqCRqMRNpsNRqNR\nMTbZBIreTDPkLbRSson4OhF7SHg9NTq2ZhpWfrPVe2cyQyO2TVJBjQwJXygkb5sKQjwvqAgT03IZ\njcYqRVRRRlpLKqvWgV9LIddsNrMedmqzFvlUtWxQGVRKxl+q56CXwZXo3fAEJJTPpuiHus+0stbL\nyIKaUSzl70ltrSSuJ0ovnZTTVdZE0NSQX6Zdz3d48IBhGZ6uHkepXpiF3rSEGkhYbdERS02jlXSt\nL7ZWxZg3mPWklk9SDOCr2Y3CftQOAppL2Qbhv18tNOeJoyl3poVUR/Y+tYR5otHTaxTU2IrUGMnU\nfl8PS6uGWRV78EU+3VoGVgTPyzw3tfkW5dRFys+THv5aI0BZbaZelMvPFY8Ff2n0fWpGlU44SppT\nLlA0Qmq0Yy+b9JjGIjLna/FSeDq/k3qBtcIkNSJjnvOT5zE9Ccmu2nfX6sDRconeAR8FqMHFqPrO\ny/byRl0WLfAKq7XSPHxeWW+qRNS3F0lb6q1Z0fioGfh686yFe7dWJ5g4brUDi+/W4w0izzFbqVSk\nrZ/8M/Fy66INaETfXmu0J64JmY3ScvjVcvCaSjBN2LpCocCKN/wgyuUystks3G43uru7FQu4Uqkw\nRiNeJE98Efl8Htlstoo1iZiRqCqqF8hORY7u7m6FZnu9UJb6mzs7O9HW1taQ0SdDns/nFWQU/IK3\n2WyMXEU0cBaLBW63Gx6PB16vV3F6ElYzl8up5qZrLUx6Z8lkEtFoVOHt0DtyOByw2+2Kd80XCvL5\nPMNc8kY0FoshkUjAaDTC5/Mp4EfHx8dMQTIej8NutzP8MqVnqIpNVHY8O1Brayt6enqY3LPsslqt\n8JLPqGkAACAASURBVHg8cLvdyOfzilQJzVsmk2HkIeI7SyaTODw8hMPhYGuSx5GazWaWQnqVFxWW\niC6S5pTmym63A/gjXvXw8FCRMqFDy+VyKdIhfDrJ6XQyHTL6e1oTnZ2d8Hg8qs9sNBrh8XjQ1dXF\nCpNEqUjvw+l06m7fprFZLBZYrVY2dvJ4TSYTo1NMJBJM5ps/uOPxOAqFgoL3mE8b5HI5pFIpxuAl\nIiAsFgucTqdmgcC6RSniOjw4OMDe3p4iD0mbMxQKYXR0FF6vlxlcwtZ1dnair6+PbSTe4lMBY39/\nHxsbG1VCeMAfxeaGh4fh9XrruuPiqW0wGODz+XDhwgV0dnYqmGxqGdRKpcIo0UjaVm9YQvChvb09\n7O7uVkmtEO3h0NAQU1sUN8/w8DDS6TRjVaKXSpX0nZ0dBXpBa4iez+cRCoWwuroKh8OhIG6mdzs2\nNsbo0mRGZ29vD5FIBOl0WhEqU2HH6XTi3LlzCogcMSOZTCZsbGwgFovBYrEwjXuz2YxwOIxisYie\nnh5GakEQHoPBgM7OTnR3d0s5aFtaWuDxeDAyMoJ0Oo3Ozk7WVEKOQTKZxPr6Og4PD6vmqVwuY3d3\nF0+fPkUymYTNZmNRColREutRW1vbS8FTq27U/48DtqenR8HBS7A0v9+PFy9eIBAIIBwOKzxKMphT\nU1Po6OioikjMZjO6urowMTGBo6MjpNNpmM1m5rWS2is1m4h7jnTt4/E44w6mmoXRaMTk5CS6u7sV\nPLJa58xsNqO7u5sZdYJd0jtpa2uD1WpFIBBAKBRStGi3trZiZWUF0WiU5ez5/VAulxGLxZgAqdVq\nVZBct7S0oLu7G+Pj44oDoVaUUlNGmii0Njc3MTc3h3v37iEajVZ5W4ODg3jvvffgdrsVOYlKpQKr\n1Yre3l6F5jdNaLlcRjwex4MHD/DJJ58wQmd+g0xOTuLHP/4xY9OpVzSS0bH93d/9HauuaskTiqBh\nrXkVPiwh3Ny3336Lu3fvVmlCmc1m3Lhxgy0IUgSg+3R2duIHP/gBpqamkEwmFWF0JpNBMBjEF198\ngUgkogncz5/OiUQCz549Qzwex927dxX5MzJgP/nJT+D3+9m4+EW4vb2NO3fu4NmzZwgGg4o8KHV+\nnTt3Du+9956CeJwq6SsrK7h9+zYymYyCC7a1tZURcl+9ehWdnZ0MR0rr0Wq1YmBgQDFfvBc9MjIC\nu92Oc+fOMQ+VUiapVApbW1v4xS9+ITWohUIBDx8+xMHBAfNKaIOaTCYMDw/j7NmzePfdd+FyuU7M\nIavnslqtuHr1Kq5evcqYtninJBqNIhgM4te//jXi8bgi5G5tbUV/fz/+4R/+AW1tbVU5YofDgenp\naXR0dODq1asKKkmSWfd6vcx7FZ0Xt9uN69evY3JyksG6KFVATSp+vx82m60qzK6VjiKF34sXL+LS\npUuYmJhgrHXk+GSzWWxvb7PnFtMeRHtIjT18Ljmfz2NzcxO5XE6BceUjrjfffBNutxtWq1UTdt5Q\nbwMSFGRlZQV37tzB/v4++z0B5N9//32cPn0aU1NTVUTKvNcjWvfj42PkcjlsbW3hzp072N3drXL3\nM5kMrly5gpGREc2JapoQ4nLt7OxsOH/DV6nVKsCy3BmBpZ88eYIvv/yyqoJvs9nQ29uL9957T5pY\nb29vR1tbW1XumQzi8vIyVlZWdIeeZNTy+Tz29/ercm2UQ7x48SKDyYjFnWg0iufPn+Pbb7/FysqK\nwmB6vV4MDw/j5s2beOedd1goSlcsFmPda1tbW0gmk4rfnz17Fm63G5OTk7h8+bLUqxElMfh59fv9\n6OjoqMq5EV7a7Xbjzp070rkplUrY2trCzs5OlaE0m82IRCKwWCyM3/ZVhPl8umFsbAxXr15lXirt\npVQqhcePH2NrawsPHjzA6uqq4n2Tl/jhhx8qQmL+2SgaE8NiPm0ga5kF/ggJm5iYwPj4eE0DqRUG\nR397dHQEq9WKwcFBXLx4EZcvX2aE6NSQEAwGEQqF8PDhQ8Vziyk8GVKpXC4jHA4jEong+fPnVXuQ\nuJhv3bpVRU7UcA6Vr9pTjoGn2+JPG+JzlMFM1Prt+dwWhX78RPBdIY0UtGqxOGld1Ce56Nn4Q0Ts\nh1YrVIjsSiIM6SQKkCJMi19sfJFIbWz8e+O9QN7TlRG48FRy/Od5GkPesIteqJYDUGTkUtvQaqgC\nmYAi7718nxevy8ZL5vDihbSPeNapeu9Tq2JCrT1WrwB0kr1EUC5el41vK6bn1lu0pXctFn0b1dcy\naD0tRGyh2JKnF3PZDO3vRtvMmtmeJoOWyBireEoy0WsX71PrO+ohFRo9LOotpFq4vHrEMWKKRra5\n1JAGehsm6iEs9OoKyeSW1d6BHlVfGYBcS/OBGi+oDKcqixDrVc1fx6sWUuJltok3YlBbGnkwPR0k\njS44rQbxf8slWwRajYUaPdpJWbvUxtSoBvyr8Pj1flejULBaRvP79lAbncvXheKumWtG6wH8qi5N\nIX8t0C/9TjwFawGiRQb6eoS+alyNamGbnkXULPpACktqAaD5lkM++a1l44uHlhZ8YyOHEz82Pmcm\nzrmeEE4vOJ73DGTy4XqerZlFIxmJstgRpgVELuYkZftHbV7E7+RJuut9nlc40BpVvC4Gu5Yz8Tpd\nmkJ+woI5nU4FfRffB1wsFpFOp2tqaItXLpdDLpdjbXoy7424Vkl6mM8HUR6FxqDGj0lYR7EgRrLK\nfF6vFnu5uFHL5TJrk+TDL9LYqVQqTCaXP4SoZY4S6zRvfPjGj00s6PFaOlRtbtbF52hzuVzV3NA7\nqwew17vw+QOacLLpdFqzZDOvO0W5Ni15QT0HDrXJEnaRTwUQnlpsIOH/q1QqKBQKSKVSDIJEnyVs\nrNqcUoGYvptgUVSUku0j/j/iFM1kMoqcvpZnp33G86Hyn+ebZ2TyKrSW1fbon9JlqHeSWq1WDA0N\n4e2330ZHR4dCVI28VaPRiC+//BK3b9/W1ANO31Eul5FKpfD06VPkcjlpGHpwcIDf/va3WF5ehsvl\nYt9L+vQDAwOYmJjAyMgII8alvykWiwgEAvjuu+8YgQItiFKphK6uLiZP6/P5GFerlvEDwPb2Nh48\neIC9vT2mPU7PRQZ2cnIS4+PjDM8okjv8+te/roKiVCoV9Pb2YmZmBv39/QrsIABYLBZ0d3fj7bff\nRltbWxWj00kNCG3K//iP/6gy5JVKBZubm3j69Cni8bgiL9mI8RJbKMPhMB49eoTj42PMz89rEhCk\ncR0dHWFqagpTU1Po7++Hy+VqmkEl5rIHDx6gUqngzp07inET09Xy8jIjRuGjuVKphOfPn+PUqVNY\nXFxk1Wr6DpJDJhSNOJ/5fB5/+MMfkEwm0dbWplirxWIRe3t7WF1dRSKRqIoiK5UKwuEwPv74Yzx7\n9qwKGaI2t+SEeDweDA0NYXZ2Fh0dHVX7OB6PY2FhgVFNUuGV9tvg4CDGx8cxNTXFSMX/VA1rXRlp\ni8WC/v5+tLW1YXJykkkt84bt8ePH+OlPf8okZOsZJN6oEEidFEb5ixbp119/jfn5eYZJJOydz+fD\n7Ows66AhzW4ymsViEevr6/jlL3+JnZ0dFItFhi3M5/OYnp7G8fExHA6HQjNcKypgd3cXX331FZ48\necJIgYkUxuv14syZM7h27RquXr3KPFlCSOTzefz+97/HZ599xjpb6HelUgnnz59n8txer1cxf2az\nGX6/H2+88QYmJiaa5qHyjPmffPIJPv744ypibuCPjE6JRIK9s2Z6gfF4HEtLS9jf32fKrrUMKi+H\nfHR0hJs3b8JoNKK9vV3Bj3nSMR4dHSEcDiOXyyEYDMJqtVbhGgkPKoOblctlBrp3OBxsrdFzkfcp\nYrHpKhaLWFhYwNraGsOg8t+dy+WQTqcZK5PIZBWJRPDFF1+w7rdaBpU/2F+8eIH+/n689dZbGBsb\nU6xFupLJJObm5vD1119jf3+fAfsLhQLMZjOuXLmCSqWCwcFB9k7/N+d0TxTyE5jaaDSyE583iJVK\nBRsbGwiFQtja2tK9uXmtG7WFFIlEqkJf+p5QKKSQRhDvTSc/UeDxbYh+v78mtWC9K5vN4uDgALu7\nu6yFk/c28/k8zGYzOjs7FRuA8LdGoxEHBwfY2dlRkCSfOnUKsVgMyWRS2iJJAHpq6WvmxUPVgsEg\nkslklTGiEO9lwIgI6E8deVoPAjoIY7GYgie2WXwRdPhT6CyDCdG8qBnvXC6HUqmERCIhzZET05ba\ne0kmk8hms9J5oYNQjR+XMJfxeFxXGoachMPDQ9WxUbckYUJFGelwOIxkMvlawM5eixwq4d7ENkTa\nAAaDgeVnZC+0Xi6tVmX56OgI+Xy+6l7U6UCa3TIVTD7nRWPjlU0LhUKVcJnMa1ITNeN5CLLZrKIf\nnvqHiU+AN5Y8zjGfz1cdCK2traxXXqYkwLN8UZrjpMUocWOSASA1gVps9fXECPXIOfN6VHqKXpR3\npncqFlG1rDUtXqqIK66V0pLl8+t1tdXaKydJ7dB6rzduGflRJpNhTocaQUmhUEA2m2W5YB6GR2tZ\nBNjreR9amK9kz6ZX1uik5EOa+VBFCi4KiykZTQUUsfgj5mTV7q0VVCwyG4lFMKqY8nyPJGdB/eCU\n5+Q/X0tiWdyQ/Fhk4HMZ7IlyfDRHZCyp6EPGV0RA8ItbBjhvFC4lzjt9HxVOgD920BDJBc/fIMM8\nqrGJ8fOntUiktWrN/62ImuCfUzaHJ0mLqI1NC5OZlvvrNQx67q221sX3x6sl8DwSdLDwBzsVA+lv\nqLDJvxN+bdNaVztw6R5quXm+WUEctxg5aKUNVGM404tFNWj1YtTyLlS9q/fFzVhsskngDaIIaSFj\nx/Oa8qE1n3hXy/OKRksk4xAnnb+3SNrLkzaYTCbVqifdk8hB1KSt9WISRSMovlNa+FRZFz1/LXys\nIp2aGu+plrWi1fjR39Jc8WuCz/eTbtVJ9cxqja0ZjQjN3CNa96EaDE8mtS6SHMk60UQCen4d88aZ\nd8R4KSARFSPy7dLPeBTKSSMQ8fmpe1PP/XThUHnjI8ojq4XM/IklW8h033p8ibWKC5R7EmUneG9K\nhP8Q1ErNa+LhJmp5Kcr38YtAhFuRx8ejIuo9J995Vi6XFTk73jumQ0OPpyrK84q93WKnF3knWsMh\nqiCL46bPU0heSxqm1nqpFfLT5qR8J88cJG7YRq5GxiZLGcjWgOgEyN7bSfh5+XvL0jc0LtmhycOu\n+LQD3YdPTcnSY/T5YrEo3aPMGAnG0Wg0sgOQPk/CiTwc0mAwwGKxSNNf/AEvmzcy9rJCtLgnTmRQ\neQ8unU4jkUggGo0qerfpwdbW1hh3pHiZTCZ4vV7Gi0qLmwwZ0dwdHh5qZk3iDVosFkMwGMTy8jKc\nTqdiDIQgGBkZQXt7u8JYVSoVjIyMwO/3SyufVImPxWLY29tTbFxa/Jubm0gmk1WGlRZZLBbD9vY2\nlpaWFFhVyv/u7OwoRNf4BZjJZLC9va3QXKIFbzAYYLfb0dHRAa/XW9UvX697pFgsMg5IEmSTtTBO\nTU0x9U4tRvvFixew2Wzwer3IZDJYXFxkyAv6fDqdZjAz2XqxWCxMyI+q9FoWNOXr2trakEqlsL6+\nziBENOck9CYSsmg12jabDS6XCz6fDzabrSplorZWaW1FIhHEYjGk02nFWicuWKfTia6uLgapElVV\n9/b2EIvF2HrTM3aioyTlYT5HStpl8Xi86r3w6IXV1dWqQ4nk2CORiCLPSv/L0z2urKwgFApV9c3v\n7++jq6sLMzMzVfPn8XjQ0tKCUCiEpaUltp4ojUbChQMDAwqDSgcp6WTRnIsG3Ol0wu12o6Ojo4qv\nobW1lbGXncig8ouY2KZWV1exvLyMbDaryIeUSiWsrq4ilUpVLTDaYMPDwxgdHUVPTw87bWjwqVSK\nycTqNaiFQgGHh4d49uwZgxPxsC3yfi9fvlz1EkulEnp6ejAyMgK3210F7K9UKkin01hbW8N3331X\n5X22trZieXmZ8XeKJ3Iul8Pe3h6ePHnC5pEn3y4UClhaWlJISPNkyvF4HIuLiygUCgwFQCetxWKB\nz+fDzMwMo2OrF/rz48tmswgGg1haWsLm5qZqfvT69eu6yavJg4vH4/jmm2+qDEuhUMDz58+RSqWk\nVWOn04nBwUFMT0+jq6tLwX+gJZRtbW1FNBpFKpVSdCEBf6Q93NvbQygU0h1Gt7a2oq2tDYODg0xS\nmVdUqDUuWutLS0tYXl6uKrpRo0dXVxdmZ2fR19dXpUxaKBTw7bffMq9Mz3tpbW2Fy+XChQsXMDg4\nyLw8+l0mk8Hy8jJWV1cZKTp/wObzeezt7eHevXvY2NioUg/mBRlFg0qQreXlZdjtdlitVrbPeZKd\n0dFRDA8PV+U/KZrc3NxkVJEii1ilUqkyxjSvu7u7mJubU5BH0z1MJhP8fj/Gx8dx+vRpxgHLN4lM\nTU0xLmctjSqGepuPKLIWFhbw9ddfIxKJKJK3BE1KJBIKo0W/dzqdOHPmDN566y1MTk7CYrEoAMmx\nWAxWqxWLi4tIp9O6vIZ8Po9gMIhsNouVlRWWyKaHNhgMuHTpEn7yk5/A6/UqvBWS9pWxiROuMRqN\n4smTJ/jlL3/Jwkf+b5LJJCKRCPL5fJUxIlpCOjD4Fl0y9OStyHJX0WgUDx8+RCAQYNg9Wsh2ux39\n/f0wm80YHx+Xoi9koQ9dqVQKq6uruHPnDubn56saDgDgo48+wq1btxT3rmc46Lmj0Sg+++wzLCws\nVFWmj4+PEYvFmKclphI8Hg8mJyfxzjvv4PTp0yyE1/L9lUoFDx48wKNHjxAIBBCLxRSbn7Ce4XBY\nl3dHhqejowNnzpzBjRs3MDk5qfBmanmoZBCdTify+Tyi0ShyuZwir2632zE4OIh33nkH58+fr/p8\nIpFgRO/ZbFaT88EbVI/Hg3fffReXL19WsImR9+dwOJDP5xGPxxWoGlIO3tzcRD6fZ/uXf+5isYhQ\nKMSQNPw+qFQqODg4QKFQwPb2tkIJgMYwPj6On/zkJxgfH69KB4TDYczNzbHDn5wXMngulwtnzpzB\nzZs30d3dXfXunj59ilAo9P/Ye9PmOK7zbPgCZl8BzAoMVmJfSIjgTooyLVmOpbJlJ7KdVFL5lK/5\nIfkHKX9MKknFVa646rFplWVrI0VRpMR9A4iF2JcBBrMDs2AwfD/4uc9z+szpnu6ZASXndVepRIKY\nnu6z3Odervu6kEwmWYcf7UGbzYbu7m6cOXNGwXErHqK8w1VXyE9udSqVwurqKp49e4aNjY2q8Bc+\nB0cn79DQECYnJ5lxoEW2tbWFmZkZ3S2G/HVwcIBUKsVCODHH53K5MDQ0hGPHjqGvr0+KHZQpYpLx\nopP50aNHFad2tatYLKJYLCKRSDA9cSMFCIJiyfI5Xq8XuVwOsVhMGjarsSDxB1EsFsPCwgIePXpU\ngdlsbm7Gj3/8Y4yOjqK1tVU3lIS8FUqFPH78WNqwoabe+fLlSzgcDoRCIQwODmJyctLQuiDy60wm\ng7m5OaysrNTNd8B7kS6XC+FwGCMjI5icnDR0n2w2ixcvXqC1tZXlmfkUEsl5DA8PY2pqqmKMYrEY\nwuGwQkpIr24SpSv6+/tZwwgfhW5sbGBpaYl1YIl7iVICRC5vpGBGKcNMJsN4ZsVcvdfrRTgcxuTk\nZEWb9eLiIu7fv4+trS08efIE2WyW/bvNZkNnZyeGhoYwODiI4eFh6T5sbW1l8il8NEYNID09PYyH\nVxZxNFRTii9M8BU/LSEycUApxOET6wRjyufzmj3MehPuIkUbseI3NzejUCgw6I/oVWjhz9RIWcSw\nRA8ERg9URfZeosfPJ+H19EbL5oa4RnkJYTo8ebwxFZBEr0Lt8KVcXz6fV2hNiWMrvrcYwtFa4ZsM\nZAgH/iAUlSvFyrNYPKzloiYUPpyVrT/xPXn+V7XCmEiEzIee9HkRwmf02amoxLPx8xGTVtFOC52h\nh0VOpupKBwlB8wqFAsuR8hBHfh/Sn6kOQ5I6/P4QIVRq48aLC/JFWjUSHF22qBZsXC2sP1owm0ZA\nQtQ4UsXNVI39SvafFrSi1veuBcysNSd651APezq/gfUWpGRFLT30d7LNKPterXmrds9GtMbKsNi1\nrM168KSNUA1Vm896n61We8A7C3qNuWy/qu1l2XqUSWRXOzQa5qHKjIiRhSV6tWLxRwTW19LtIGJL\nxY0po4PTMgqyv8vksfUeMFrYPyPjLpsDPZ8VvXc9Rk5mhKt5qLITXW3ctA4q2b20nkH0fPhxEWWk\n9a5ZPWMjwyGL9+GLYtXGUXxvWaRS68XjN/l7GqFHrMdBkI0/v45Fr1BschENotohUW2sZF2HfD5Z\nj0det0Gt5+LDCcrHUGcVX7km910GX1KravJUdrJuKbof0eyJqQoZvygZf8K2qmFQZYvUiIGlza5l\npMXDhkIUXg6i2rjzi5DwdjTuIjxGZjTU7s3/RxuTB2hTUVBPWoInZeFB5ITGoPnki438wcwbdF46\nRcyZ8eG02mHEjznPsEXoBX6N6j1w9KwNvXm7Wj0oSlcUi0WWwyUInp4DWovvlU9RqLWEytYyH/JT\napD3KinXq4W9FeWZZCG/iDUlmyAaYV5GReS51Ys7PhKDKhZ3stks0uk0kskk61Mn+WAiTWhpaWE5\nPDGpTBAb0fhQN5HT6WSqhLw0BOmQJ5NJbG9vKxiC1AwqEY9ks1lGtKE2mVarFW63u6L7Ru9JT5yf\nMqNqsVjgdDpht9tZYYbAzaQ773Q6pdIWwP/DmvI5IgJKp1IpZDIZRuShpy9alBbf29tDPp9nm4A6\nrBKJBDKZDMxmM9ra2uB2u6tGBVSBz+VycDqdbI3E43F26PCdMR6PB263W2pg7HY7WlpaWHWWODzp\ngCkUCuzZZUbD4XDA6XSyIgatQRJO9Hg8hoURaymCNSrk5rlYE4kEq+iTAbXb7UilUop+fdEbpQ4z\nr9ergFyJhSfirxCjDdqjNLe8DLTdbofb7cbe3h52dnZgs9nYXLlcLvZsIhcAfzjmcjkkk0kmn83X\nfvb29mC329Ha2soQAmazGYVCge1dgm9SMwpvUAl7rJfy8EgNKvAn+M+NGzewvLyM3/3ud8z7I2/Q\nbrcjEAjgn//5nxWTRS/04sUL/PGPf8T8/Dzj3+QhWf39/Thz5gympqaYkeaxpIlEAr/61a8UAHW1\n0I6vch8cHCCZTGJxcVEVojI0NIQrV65gcHCQkUirSVWLhZv9/X3cunULn332GXZ2dhSfa2pqQk9P\nD86ePYvx8XH09PQoCiJ2ux0+nw+Dg4PS7pCXL1/i8ePH+OSTT7CxsYFUKqXw3JLJJNbX1xk7mB5J\nFh4GMz8/j7t37+Lp06dYX19XdLPQQTAxMYE33nhD0YlWDfxuMpmQyWQQj8fxm9/8Bv/93/+t+D2z\n2YxAIIC33noLly9frohozGYzxsbG4HQ6ce7cOcZRS4d0KpXC0tISPvnkEzx+/LjiWVwuF15//XWc\nPXsWnZ2dDDNJcxMMBhGJRNDe3l6Xt/iqr1KphI2NDfzyl7/EtWvXFFA0k8mEfD6PxcVFrKyssCo6\nf8i0tbVhbGwM77zzDjo6OhTwyObmZmxtbeGjjz7C48ePGZ6c9qjdbkd/fz9OnjyJS5cuwe12MwY1\nSolkMhncuHEDH3zwgcJLJoO4sLCAtbU15gDQmiWM/JdffolUKlUBeyqXy/B4PBgaGsLp06cVtIck\nc017/F/+5V8U+Hg6CE6ePIl3330XHR0dFc7eKw35acKy2SxmZmawsLCgeKCDgwPGtfrDH/4Q3/ve\n9xAOhytaIe/cuYOZmRmsr68z2jMySiTFfPbsWbz77rvwer0oFovsFEylUvj444/xP//zP1heXkY+\nn9ckaZGFElrUgh0dHbh06RLOnj2L9vZ25gloFbPoQEmlUsjlcrh79y52d3fZiU2/4/f7MTU1hTfe\neAMnTpxgoTSf5qAKp+xaWVnBp59+itnZWcbVyhebqE/ZSL88bc5oNIp79+7h2rVrmJmZgcPhYDC4\nQCCAoaEhnDlzBn/1V38Fu92uwIKqFSUtFgvsdjsePHiA69ev4/79+3j06JGiuGA2m9HT04Pu7m6c\nP3++ou22qakJnZ2dCAaDOHnypILc4+XLl9je3sbDhw8xPT3NDCofgtpsNoyOjuKtt97C6OgoPB6P\ngo6P0C5UVf5zuQ4PD5FMJnHz5k2pUSDjRNGMSBDicrnQ19eH73//+xgZGVEcwmazGbOzs1hcXMTi\n4iIymYyCsMZsNiMcDuO1117Dj370I/j9foUXmM/ncefOHXz88ce4c+cOixx48hNaq7yEEO8Zz83N\nYXl5uaKnv1QqMfnpc+fOoaOjg9kOu93OxmRmZgZXr15FNpuF3W5nY2C321EoFHDx4kWEQqGqEjev\nJIfKT5ZYHKEBJZCty+VSeIr0c55MQQwViZzFYrHA4XDAZrOxzxLkhyj2RHB+PegEWkyUbiAvTauK\nynvO9G5qBp7CLCJRoVBIpqQqOxAODg5YGCf2T9P41+PxFAoFBofjpXiLxSLbMHa7nc2plofKd1jx\nkshiDps8FrHDSuxgI69dbN2kcJ7HgYr3sdlsLNVit9srWmcbVSR61Vc1+r5q8D9aj06nsyLiorSK\nbG3ye5SH+/FzarPZUCwW2R5VO3S1csOifeHrCFarlc0nQQDpcKS5pNQBr7ZB9JxG+BPMr2IyZVyL\nsvyVTIhLD02djEWJr9qJ1cRG5LX49IDIwqOVg+Qrv9UKWmK7Wy1jUg1CpCX3LJMsVlO9lcFP1IQb\n1WBg1Ta6HnSJTJqbP8Bl60xtLYqdd/VyZdZbYKoHcF5rlb4alFBWuFGTUBfXtuiJqhHHGEXSyNaZ\nmoS5TJyQ9mctKs2vxKDKsI88KJofVF7ky2i+VmTL4blZRc5So/eWhVHipGkReahNtprHSd/BynGh\negAAIABJREFUTyrvoVbDkvKLnP99NcOqRhitxn/Kbx4KqSnXzM+pHgVYXptMhD3xa0NvRV1tPvh3\nEQ0+T+/Ij7usEaRWz1RmVMSefb3rUq3RpFbnQOug0iPVrPVuMuYpfo2LkZfWvfXCzvjv5FEdNL+y\nsSMkgJjXb2inVCM9VBm9HbnrIm2cmMdRw/nJsHUinyhPjGD0xKnm0clYyPXeV5QSEbt+xNBSL+ky\nT5fGhytaHUri5whpIPOiZV09/KFG36t18Quan3uChKmleKptPC1PUsRQi5hGWk98ikkUCayF0o0f\nW+oCEw98gulp0WES7Ens+KrXoDYincB3Q4rQNLFRg08PiHzKWnNXzZOWpZboO+g7ZVyuYhTDt9xq\nSdp8IwaVWkAJb8Y/MOVkyuUykslkRcW6XC4rJHNlLj5VzImGTmSjKpVKcDgcaGlpMSwOVm0gCUJT\nLbxRWwAWiwUul0tBLUgnJVHXEdkIT7lGlWur1apKmEz5KtKcEg2AnjZBIvDgr1wux37u8XiYCibd\n0+v1wm63q+JEibJRNPb079lsVmpYjB5YfPGSX4sEuyKxOf65qM8+n88jmUxW5GoJV0tr2YhRJU+e\n1qLINuXxeFguUu3zBNNrbW1VYDZr8ZTFFBTxx9bCt0rOC4ld0rMBf0JOUKEnkUhUFMWIeU0Nx0r3\n5gnZ9XjS9Du0j/b29iq+P5lM4uDgAFarFW1tbRX1CEIhGYlqj9ygOp1O9PT0IBKJIBgMsio3j100\nm824desWS3jzkz4/P4/NzU0FoxO9HJGXPHnyhHGEikw2sVgMp06dwtjYWMNOZ/JsTp48iVAoxKrc\n1XJj/ERZLBb09fXhypUr2NnZqTjBW1tbsbe3h0ePHuHFixeKCj0tgL6+PkbHJi6szs5OXL58Gdvb\n20yiWy+rPz3L559/rjAcVDnd3d1FS0sLpqamMDw8rPD2PB4PgsEgOjs7peTXBwcHWFtbw8LCAtLp\nNBN0I094eXkZ09PTDINaiyEVQ2PyTGw2G0MAyBQL6HB68uQJ5ufnmQNAa8rv96O9vR09PT2MSENr\nXPl1YDab0dnZiampKbjdbqTTaQVpuNfrxfDwMNra2qT3tFqtGB0dRTabRSKRYE0Q9UaNJpMJhUIB\nKysrWFtbY6qtavla0eg0NTXB4/HgxIkTTEiQ124jRiiSwbbb7YpxKZfLDIkipj+ILKe7uxudnZ0I\nhUIKPg4969nn8zH7wcPs6GAnWe7Lly+zyIxPqUxNTSno+74xg0oD4nK5MDw8jJMnT2JoaEihUURE\nGuvr67hx40ZFFbKpqQm7u7tYX19nRoHf8ETfRxRk1HHBewTt7e24ePEiI5FuVFHh8PAQkUgEHR0d\nrKlA72anyujQ0BAjwRXzSPF4HKurq4wQmVdrJfq+ly9foqOjQ2FQ6fM9PT148803FUbLSOFibm4O\nf/zjHxUYXPKO/X4/Y/nxeDwKDkwiiO7u7q6ISIA/geQXFxfx2WefIRqNsiYAMqjxeBxbW1vY3d01\nxCWgZ8wdDgfC4TDOnz+P7u7uCm+wWCxiaWkJ9+7dY0TLfKfUsWPHGAetXoNK4242m9HX1wez2Yxj\nx44pJM2JNzgUClV4zryxn5ycRFtbG3s2vZRyWsU+anz56quvWMMGNTJUq/zzkdrU1BTa29sZ0TzN\nJ/Ghbm1t4bPPPmP35p9jZ2cH29vbUiIcYoyjw9tisbD0nZ4ocHd3l7GqERadDkmr1YpAIID29naM\nj4+zHD6f/olEImhtba1omX+lBpXPhTgcDvT29uLEiROYmJiAw+FgxoPY+mOxGJ48eYJYLFZxr0Kh\ngEwmo+BB5DdAIpFgnK2iwbTZbLh8+TJOnDjByIprCR/VLofDUdE5o2fjk7GPRCLwer2KlAaFqU+f\nPsXz58+xsLCgIPUlL3BnZwfHjh1TbY0NBAKMcFsvRIo3frOzs7h7966Cfo+A2pOTkxgdHcXIyAh6\nenoqPB6LxQK32y3d8OSh3r17FxsbGwy3SP8R7Gpvb68h8yRS5LW1tWFiYgL9/f0V+dBEIoGlpSXM\nzs5ifX1d4bFYLBZkMhk4HA4pmbGesDgYDMLj8aCvr68iX0fwIeoAEy+LxYLe3l4Eg0FVViijOV0a\n82g0it3dXSwvL2Ntbc3w4UXUgJFIRPFszc3N2Nvbw9OnT7G6uoonT54gHo9XRBHkKcrWqd1uR29v\nLyYmJhj9pwzXrDYejx8/xpdffolnz54pOJspxXP8+HFGayimBekQdrvduouRR2pQyXCQbAR1n9Dv\n5HI55kpHo1Gsr6/rqijyXuL+/j729/fZRPEnjMvlQqFQgN/vR1dXFwuxGg19MZp/pdOPWihlpC7r\n6+s4ODhgEi/8QvB6vXA6ncyzFVUSyNjTWBs1PmSkt7a2mIwIHVYOhwP9/f2wWCzw+/2si6ta1Zd/\nt2w2i2g0yrq4ZHjaasxHtbBJURVXRshNUQN5yRsbG9jb22PvbbPZ4PP5mOSNkfnm16PL5appPRHZ\nMb/p6zWo/Dy1trYquFaNXBaLhaUqxHtnMhmsrKywhpCtrS1phV3GEkcHGdmPSCSi2C/VDGpzczPW\n1taQz+exvb3NvGBeNePYsWOw2WyIRCLw+Xx1s7qZ6zGYehcTrx5IvdlEjsJ3QIh5Lb0bRiTUEPlQ\nCdxOXTuNNKhaZL/VJkPEVYrtp3zehufUJKOglaSvRTKZWm4pNKIiCX2nqHjA94mLBCZqcBPKqzkc\nDoVKqRqjkJrR0vNnLbSJ+HOeK4CvOhMPAJ/zV8O6aq1XPZjGanm6aoiSWppW+N76WgUAxfXG35tf\n53xhkJ8HLbSCiCDg76Vmg3ivn4patFfoUJVB/PhuRDXmq4YYVHGBGwW8GuFDrVcCVsRtipi9RsNG\n9ODj9Hok4oZSA6HLgNQyL7WWnDG/6LTgaiLlol7NHbX1JFsrMs+dDh0e2qSHq5c/DKpx4soaErSw\nv3z4bBRO1aiIyOjvVKNwrMfJUuO31cI2a32/zEbooUJU4+hVczRk67jh9H0yai/xhKg2GSKwXsT1\naXXQ6E2wy9rOKH8o6tu/ykuEDGkZPDrReRSEjMBF/K9a94eRZ+W167VIn0U6PaOeDJ/b1VrgagaV\nx6oaMTLVusvUOsGqrc9qhlRGjqz2rmoerhFZ7WrGVQTUN6Jhgd/bsn0tppSMRE6ix8hHh9VsA99O\nKnq4ouqD7J5GDsqqO8FkMsHpdKK1tRU+n4+F6/zmyOfzFdK4tYYiRi4KwahHm4e4UIXQ4XBgZ2dH\ngR18FUaUesrVcpmkWcULm/FeKdHgUb6On1ACz6dSKWxvbyukqOslISZOSKJVlHmJJOYWi8Xg8/kU\nxpGA8W63uwJORv/u8XjQ0dGBYrHIMKvVvGla8FSUWVtbY+iAepnsadxJRllLplnru4rFYgUNHv8Z\nnvfBaIX+5cuXyGQyyOVyimo4Tzlps9ngcDh00Qu+Ki+6ubkZTqcTLS0tLEfJp6qoKMXTSRr5jlKp\nhHw+r5C/5qPSbDYLt9uNYDDICr70f6/XC4fDgVKpxEQjRdwyFZ71Og3maqeO2WxGa2srurq6MDo6\nivb2dgX5xOHhIXZ2djA7O6upSXMUF4lstbe3IxwOs7wsDShBeObn57G9va2ARRy1QXU4HPD7/ejo\n6JBS7B0eHmJ7exvLy8vY399nxosOiYWFBUSjUUW1m2d8ymazWFtbw5MnTxjPa72pBzKoBGXj0Qd8\n/jGdTmNlZQV+v59V5ekwpUp1X18fOjo6KgyHyWRCMBjE2NgYw2NSXrIafSAZ43w+jwcPHlQFehsx\nqCSnvLGxweSQjUQf5XKZKd1ubW0puqDIO+rs7ER7ezt8Pp/iINAzZ6VSCevr69ja2mLPR9Amwi1T\n4YbW+TdJ3sKnp7xeLzo7OzEyMoJMJsOwqOQtxuNxRs9pZC7JmaN9RIgUHva0vb0Nn8+HoaEhhvQh\n/l2LxQKfz4d8Po/Z2VmYTCaGwaXPh8NhDA4OwuPx1O6h8i67w+HAsWPHGHj34OBA0bVTKpVw584d\n/Md//Ac7PV/FRBEf6vDwMC5cuIBz586xCihNSrFYxNzcHH7zm98wZdRXYfCbm5sRCAQwPj6ON954\nA+FwWOFlEbPN3bt38dvf/hZbW1sVWuepVAobGxtIJpMVmzufz2NjYwMff/wxnj59WreXJo7r4eEh\nVlZWFDrr/HwvLy8jl8vh/v37CrJiAPB6vWhvb8f7778Pv99fcZg4HA5MTk4iGAwyzGO1pD8flmUy\nGdy+fRu/+MUv6koTqXnn6+vriEajDKant15QKpWwvb2NDz74ADdv3qzwtux2O15//XVcvHgRx48f\nZ2z0WqE2b3D39/fx+eef44svvkAsFlMgDQi2dPr0aVy5coU1uPDh8as2phQ6W61W9Pb2wuVyYXR0\nlNkPMqilUgnT09P4r//6L80oV0wZUWEpHo/j/v37uHr1KtbW1ir2IdF7Xr58mXnv5KHu7e1hY2MD\ni4uLuH79Ovb29hT70GQy4cKFC/iHf/gHBdG71iForuayEzzG5/NhYGCgIgFfLBaRy+UYM/tRn4r8\n/W02GwKBAIaHh3H+/HkEAgHF5s9kMojFYpiensby8vKRe9D8qUwwrbGxsQovjwzTxsYG7ty5g6Wl\npQpSGLHnXNy86XQa2WwWCwsLDWNBEnWZZBIph4eHSCQSrNlAzP0FAgH09fXh8uXLFQcBRTwdHR0I\nh8Oquldq4XWpVMLq6iquXbuG27dva3LV1vLuMr00I4XXbDaL58+f48svv2SdfXRR2Dk0NKRI4+gt\nCh0cHGBxcRF37tzBxsYGa4IhxyKbzSIYDCoaYLTWxVE7Fnx+nRQmyH7wz0AUm21tbYZUL/ioYH19\nHXfu3MHc3FzF586ePYsf/OAHmJycRCgUUhjFWCyGW7du4eHDh7h9+7YCeslH5zw8sW5gP288Rb5P\nnmHoVZ+AYjKZCBDo9BKT+EQ+8SpOZV5XSc9GJNIM/t30fq5RBsVomMxL7vLzwb+3GthaD4We+Hl+\noesh//4mL1ErjfaJVl7WCL8EEQrReueLLq/SaBqJ2GT2Qzy069HLoty/SLojatZRdxqvD8ZzqlIE\nWat3bza6kbTCsWohm9rvN2ri1e6rxsup57v1UsWpVQS1GHRk8CNe+vrbfKmhNHhhvHpIaPRAYhoB\nVWuU9yZywPJ/r1bg0utFimPLGyoRQqdX1uZVeKrVbEM9a12L/tKIjeDHWMSDGzo8GrUQjUjk1rPY\n9Q6u1iAelddWK43fqw7Hvo3j0Oi1UM/zN/L9G3E/rXvXO95a5Omvav8c1TzX8sz1vqfZyEvLeCH1\nUtXxv88THxvNu8pgPGpta2L4JS4YvaH1UYaGPG9kozbhqzY8Il5Vi3ndyCbSAuB/k0ZTy9PiO45k\nHUBGmiFkOFyeiIZ+JhpXPfuK/x2ZURY5Y+uNmNTmst7GmGqgfZmqBv+9ja77mI0udqNG6PDwENls\nFrFYDBsbG3A6nezf8/k8SwSHw2HDLxYOh1XllGmwnE4ngsEgwwbyC65YLGJ/f5/Bfvjnpm4kp9PJ\nIBPixiAcaS25PJKoDQaDColcniSENHa+iTy11nMT3pH0gXjj6fP54Pf7pRhUWvzEvyDm/qgJg/C7\nagKEtV48cYvD4ZAeznt7e9jf3zdcwKRmA4LxiWQ+hIne399HNBpl+Tq9RoMUfwkLziuHulwupvi5\ns7PD+AL0dkxFo1EUi0W4XC60t7czHS2CqoXDYbS0tOjCYuo5BBt1oJFz5na7EQ6HWUGOv9ra2lAo\nFBg9IN8Qsru7i0QiwXDcjfDEG06OIp52qVQKDx8+xN7eHh4+fAir1ao48Sjx++Mf/9hQL/HLly/h\ndrvR3d3N5JTFE89ut2NoaAg//elPGfyIEtRWqxWbm5t4/PgxFhcXFcQJJOLl8/kwMTGBixcvVrR3\nmkwmzM7Osqrr/v6+Zr5UNPR2ux3Hjx/Hz372M/ZsPHn02toaHjx4gJWVFWxvb3/jXitftY1EIhgd\nHcXAwABCoZDiQHE6nQwRIgOY5/N5zMzM4OHDh4jFYtjf32dGuVAooLOzE4ODgxgbG2MqlY3wTAmk\nTfR9Q0NDioOgubkZuVwO9+7dw7NnzxCPx5moo95OQL/fjytXriAcDiuiImpAKJfLWFhYwOzsLCuS\n6DEwtG5tNhvefvttVnQtlUqsX50KKx9++KFC9aBa3z9/qI2NjeH48eOKYjNxtR47dkxBgPJtWYut\nra2YmJjA+++/j93dXWnOeWVlhUmm817q3t4eVlZWMDs7yw7Aerk+jpxgOpvN4unTp1hZWWGeJK9G\nGAqFcOHCBbz77rtM216vQSVSaa/Xy9RO+VDCarUyDC2PKySDNj09zYDqiUSCac1QN0dbWxtee+01\n/OxnP4PFYqngWr1+/To2NzcZhaDeggcZ9JGREYRCIdaZQx6B2WxmhxBBv15VEaFayoY4Zs+ePYsL\nFy5geHiYKSPQvxMzkxof6vz8PD788EMsLS0hlUqxQ3Z/fx8nTpzApUuXEAgEmHRvPQaVD+0cDgfa\n29vxxhtv4Lvf/W5Fh1o6ncbh4SG2traQTqcVRMtanhfNm8/nw6VLl3D8+PEKqeVSqYQvvvgCt27d\nwtOnT9l76zHYxIH7k5/8BBcuXEAwGGS8oBaLBYVCAQsLC7h79y6++OILbG5u6pa6LhaLaGtrw/nz\n53H27FmMjIwoKCXJ83a73WhpafnGlV5FhVsi5g4EAgoUDxnO+fl5XL16FTMzM4xjlwxtqVRie4w8\n/npTG0duUEulEjKZDPL5fIVuNoG+Dw4OGNGrnu4R/ndEOVgxxHO5XAwqwX/WZDIhGo0yyQ7RuyWj\n5/V60dHRUSEn3NTUBJ/PB4fDITUcejwmkr0Q++TL5TJ8Ph9aWlrYQWEk73vUC9rpdMLv9yMUCiEU\nClVImVBorUbfl06nsbGxgc3NTaRSKYXHtbOzg93dXcZ41ciLJEj8fj8ikUiFKubu7i47nI3S2NEB\n7vP54PV6FfcmXlCLxYJcLod4PI7t7W1DIb/P54PFYkEwGGTdd7Qmstkstre30dTUhFQqpaDI0xtR\nlstluFwuBAIBBAKBCqFEYuH6NhUBydjz+0jkyohGo2x8dnZ2mPQM31gg1li+FQZVRtBBF9H3iac6\ndQwRs7/H46lZQlatqEMGV0xgk8fCE6fI8jPUSil2/FAXGS+roPe5RYEy/tl4DXmte9dbpNGzkMUD\nhg9hKc/pcrkM0clROLm/v4+9vT1ks1mFsmkul6sq8qclp62Hh5b6s0XJjXw+z/rsZexk1QpIxN+g\nlcM9ODhALpdTEHfruejQJ8JjoqKkeaF8c6FQUIypnnluaWlh+UWn06lKcq2FFzbKPEcGTSb1rLdg\nxRe4Zfl2yvfTeiOehmpFQCMUnA01qGrsQ2r63fzPKF9JYFvaUPRz0ZurFRIl/httVOp31jqdtJiG\nRG+bf0e91Ggy2Wt6Vxk6oZphMTpveo2qKEHNSy3zY6q304VntKJ8H3Xd0d/VDhIZHaOoUVQNe8mP\nt5jLFze9iOusFvrLYE5qiBj+IOH3kXhfGl9eNZV4QsUDmY/c+HuLKSMR7yw+N2Ex9dJe6jWqRtZc\nvWua57QV14sa8kKcj4bT9+l5Eao6it1BMsMiPiAPsZF1J1TzRKq9tLhQeOovI+SxMplaXgZapCjT\naxBFT0IGL2t02FSLjLYoR80bIzWvVisnSL3uYiGADjmtZyR5XzVO1WqpFq0/E+yJhyfx7y12PGl1\nfIkGVfb7WoevaCR4iWtRM15sXtEDxasmJmnEoNTye5QmIS04ft5FulCtg7IaikDPYSDOhUiM/0pD\nfjotqaVL78Km8JbavvSKgskWoxHdJH6SZOqXeoyquPn5kJgWuprRUVvA/KYm418tbVDraV7NS5VF\nBfwBZGSDyg5gKiDwni+fS9WKGqjNUHYAa1Vq+bkX2bn4fBpFCnxBjJ6zmrHX4jlVm4dqISYRfvPt\n1fxeE+GA/JiIuvNqZN5aRk/PetJi3a9mB0gVQrQfvBeth29WL3sXv/b5CEx28BvRZKvboNKC9vv9\nOHXqFAKBgG4aOarSe71eWK1WTE9PY2Njo+KliTuTfk/0VDKZDHZ3d5nscDXjyFcunz9/jvX1dVbd\n1ZsTpj8TrMpkMjE2KzKkoVCIVR/VjMLOzg6i0aiCSIOe//nz59jY2EA2m5V6KqSSGQgEqlLBiWFQ\nLpdDMplEPB5HKpWSbuhIJIL29nZWXKL3MpvNjAqN1weTjZlsc1ksFkQiEaaSmc1mmZEolUoYGhpC\nf38/k+4V7+9wODA4OIiLFy9WhOxNTU2IxWLY3d1laq/8sxQKBSQSCczNzSEYDFYUA7PZLABgcHAQ\nra2tzGjTew8ODqK/v1+aY1RLBejp0ydPzePxVOgm0bO73W7k83lMT09jfX1dQdFXKBSYHtvg4GCF\n7DEhKFZXV1XF8GR5aZlxl81pLpfD1taWIbQLf7/V1VV0d3fj3LlzivEqlUoIh8Po6elRKI/KxrwW\nukKyPz6fj0nci9Hy2NgYPB6PbqfLXIsRFXOJ4XAYr7/+OoaGhnRLvPIGxGQy4c6dO4p70/87Oztx\n7tw5WCwWRnlGHiFxIU5PT2Nubq4CSaBlUAmHuri4yNQQjXYqBYNBnD59GqFQSFEIKJVKaGlpQX9/\nf0XDAp24BwcHWF5ext27dxUUfVRRXVlZwcrKCtLpdIUnYbVa0draipGREUYFp2fh0kkcj8exuLiI\nmZkZpNPpit8xm80YGBjA6dOnmUQ20dsBQF9fH7q6utjGN7KQLRYLenp6cPHiRcRiMaaXTlEO4VDb\n2toqvHBq1BgbG2NUkTyRRVNTE2ZmZjAzM8PSAiKRcSwWw4MHD5DP5yvQCXQdP35c0c9NeX16No/H\nU1dBUOal2e12tLe34/Tp0+ju7pZKDuXzedy7d0+RJuIjvaamJqbIKpL17OzsMDXZRpAE8eO2t7eH\n6elpzM/PI5PJ6HJsRO92YGAA/f39ivVULBbR0tKC4eFh+P1+VdmbWornVMgLBoMYHh7GxMQEbDab\nYk1YLBaMjo4yg6oHZ16zSB9v5bu6uvD2228roC56DGqxWEQ6ncadO3fw+9//XgrMPX78OMLhMIOj\n8CfI/v4+lpaW8NVXX+HmzZtMQVPvIiZPLZPJsFDOCFlKR0cHXn/9ddZZwxtMwu55vV5p3qxQKGBm\nZgZXr17F5uZmxbORkqtMTtlmsyEYDOLUqVP4wQ9+AK/Xq9ugkkdw7949pNNpBnjmN6jFYsHk5CTe\nf/99JqHLbyKXy4XW1lY4nU5dxTH+81arFQMDA4zYl8f+Et6SMI9iyoOgZlNTU0yKWZTfbmtrQ7FY\nZF4q//75fB7RaBQ3btzAo0ePKsa1paUFb731Fs6dO4dAIMA8cF5Jlp6t1qKFLAJqbm6Gy+VCb28v\n3nzzTbz22msVc5dKpfCb3/wGd+/eRTqdVnTPOZ1O9PT0YHx8HBcuXEBnZ2dFOmNpaQnz8/OMOLyR\nVyqVwu3bt3Hz5k0kEgnm2eu9hoeH8Xd/93cYGRmpCLlJ+puXJa913EVjbLfb0dPTg7Nnz+LNN99k\n+4h39siDVUuj6DKo1YyKGCK63e6q8riyz+VyOWxsbODu3bt48eJFhYx0c3MzY3XnT1WeuT6TyWBj\nYwOzs7MKzW89hlEshhhNrPPvbSQRTsYjkUhgYWEBy8vLFQeRFqSEQv6Ojg6MjIygra1Nd8hPTQub\nm5twuVzSMI+kRoaGhtDa2lrBpq+VDqk2bsR92draKi0IaLEHEQyGFBpkfKkvXrxAS0tLBbCdUgrU\nWipTCAgGg7hy5Qo6OjpYaK8XQlMLnpLPu1Pbal9fH8bHxyu+d2dnB+VyGWtra9jc3FR0cXk8Htjt\ndpw4cQK9vb0YGRmpOGiampoUnpYeoTu9lftCoYCtrS0sLCxgZ2dHkWqpdlHKMBAIYGRkREFer1aU\nrpdASQz5I5EIhoeHK2SkRcVhXXNqtJBRS0VZVCLl+7f5opTItSpTLZVtUBlPqxHjXivjkxosTK+x\n4TkZeT0cPQcanyIQZZ21yC74/JRWsp34Y9VgN/UubLXCmKwyrvY5mmse4iPCoWResmyMeWSGCBkS\nhRa11nc9qr0iFZ9IdsLrovF8v/zv8LA7em9+LuvZv1oHA0k1V5s/8b5UcKOCYL0oAqPvRqgOsSBc\n62HZkCq/lldYrepZreoo+7yeSmojaNP0LECt99EyriJvppFnlo2RHrygCOuSNUTI3ltPga4eT6Fa\naKa13mR5rVrwkDL5cVnkUk+YL8PBklFRG3e1AoweQ85DkGTQIy00hBG0Qi1GmM//8s9Y65qpNxes\nZwwaZlDrAeNWWyBqkrO1DKDoqRndwEYnT1bVNgKAFr1wo2OuJket96CTGSbRSPN5vkZdjeS8lam9\nGsEmi3OnBr4X5c9rfbda8LJqjQNiIVXca/yz6yE8r1Ummz+IjK5fMQoVn++opd9lLed6JOcNaUrJ\nXlqUKxAnX62fniZeDMMIzMvjz+gevFKkUfZ3cWHQs+mdGL5jiXB/egZVRsorA8CLIRjffspvpGq8\novz9ZfK74nuLrPr8ouGlIIjcBPh/AHrZZuU5bWs59LQaA2jOtWAyslSLEYNdDUsqgxHxIaLaIUXM\nUmopHh6YT1VlnpNCyzvkeSvoXoRAoNBZBjXj+RWsVquiDZzCbN6r5DuyeN5ivsouW2u0jujZtC6e\n9U3WGWeEb7mRB3s9+O6qRSkybMTIQlrt4uJ1u90IhUIKxie6Dg4OkEwmkc1mmaogDXixWEQ0GsXh\n4SEikQicTqdCEbFcLjNcnl5dbHGi6dmqSRXzF3FDdnd3w+fz1STlQf3DyWQS6XRaUfAhxcWDgwN0\ndHQwblb+lN7f30cqlUI2m61I8pdKJeRyOcRiMSwtLcHlclXMi9frRSAQYFwF/HwR6Usix3UDAAAg\nAElEQVQ4HEZvby/bqKRTRAZ1ZWUFiUSioo2Rqvwul0tBGqMn/VIul5FKpZBIJFjPPp9PdzqdcLlc\naGlpUXCqflPs/XzfOem/J5NJ5PP5Ci+SRCNluEVCKLS3t6OrqwtOpxNOp5MZrvb2dgW2t2Kjms0I\nBALo7e1l68tms6FYLMJmsyESicDv90sJTOjZOjs7MTAwgGw2q5BTJq7TVCrFcNl04NN6cbvdTMVW\n3EPEGkdriSSa9ewVei6n0/mNM1k14jJXe+H9/X0sLCzg3r17+Prrr5HJZBjd2suXL2Gz2XD8+HH8\n+Mc/Rmdnp4KIpLm5GYlEAl999RUePHiAubk5BoWgjUQclf/0T/+k2Jz0/0AggLGxMUYdpqc6SYuI\nOEd/+MMfIhwOK55ba/OT50hVV70sO/yzp1IpzM7O4vbt27h9+zYzbLRISf3zr//6rxnWk05ts9mM\n+fl53LhxA7Ozs1hbW1MsYgJyf/jhh5ibm2PFAD4XdeHCBbzzzjsIhUIKgmxiyTp58iTa2tpw5coV\nRccReY8rKyv493//d0VHE3lDo6OjOH/+PMbGxhhrk16jl8vl8ODBA1y/fh0bGxtsPRGsqb+/HydO\nnMDZs2dx7Nixuun7GpVjI5Xa6elp3LhxA8vLy4wI5fDwEBaLBV1dXfjBD36AqakpRmZChpX2idfr\nxYULFxT4W+BP0CcytrLL6XTiO9/5Dvr6+pBOp5ljcnh4CJPJhEAggM7OTvj9/op0DVEuvv/++7h0\n6ZLC+zSZTCgUCohGo7h37x4++eQTJvVMnmw4HMbExATeeecdRCKRimfz+/14++23MTY2xhRC9TbY\nmEwmhEIh9PX16aYc/LMzqGRUmpubUSgUsLm5iQcPHuCDDz7A9vY27HY7C3scDgcymQy+853voL29\nXVGFBMCkda9fv47bt2+jVCrBZrMxZp/e3l689957ePvttxEOh9l9+dydGHrrGXQKqXp6evD9738f\n/f39cDgcqmBurVSG3k3NezREXnvr1i38+te/hs1mY2kOwrf9/Oc/x4ULF9hion8zm834+uuvsbm5\nie3tbWxsbCiq7YSzTKVSePz4cUVOkTbb2bNn0dLSwrCk9J/X62XYRb6zrbm5mbEh/eIXv8DHH3+M\n3d1dtmnp+S5fvoxQKITOzk6FQdVzFYtFvHjxAp988gnm5uYQj8cZ9Voul8OpU6dQLpfR39+P3t7e\nhuZu6zGoh4eHiMfjmJmZwUcffYRHjx4xb/Lw8BA2mw1jY2MYHR3FxMQEq8jzHmZPTw8ikUjFGueL\nlNSkIa41q9WK48ePY2xsTJp6o5BfljYgqNqlS5dYiE8Hu81mQzQaxdWrV/Hll1/i66+/RiKRYCxN\nNBf5fB4XL16UGlSPx4OTJ0/ixIkTNdHgmUymikjqf52HKuYUaRHQIPOeIi/hIav0ESyKQhW6n8Vi\nYfejQZUVk+rJoxDVnN1uZ4vVKHWdnhBf9u58npCkTPguL2Jh56VEeE9Si3WJh/io5a1lc0JjSQeF\neLjw31coFBRhOXHY0nfrUesUq+W0HoiUmm+o4PN3smevli9vdKgvQoD496YDQOzEEmW0xa5CGnOt\nYq0sH09rWcRpimtVbb2oQZtkjFoEqSOnqlgsSve4qGHPR6dGU3NqDFBG7idGt7UWCPVwD9dclNLy\nYGWchjJlRhEjybMz8dIfIp5UfIFaNw5f5OAxsHpZaPROIl9x1oMF5auKfFcQPWO171bzBmgcZbAo\n/t4ypis+XOPhNrL31YLqVMOZahG06KVklBk9tSKDXpIave8kexcRnqSGNtGDsZVtaiNEPtWQAyI6\nQvYuajC6Wolx6i0U6j0EZegIPXMuIhW07ITamtNlUMU2OSpgEIaO38B6QM4E5BUfVsYCVIsyqmh0\nyCsWFRz15GG1vltG7yYuXNGo81VZNbo3oyez1rurGVM1gyoeDLLNqHeBi00BPIyHf39KE4l9+XrH\nvJpBrbbhRYMrGlA1BAE9NwnuiUxctYL91Z6zHrJxtUNLy6OVrQN+nozip2t5dj1E0zKnrZbDp5pq\nakNCfgofeYPEe5jEB8rDH0RcGYUqanAUHuohy6PUAx6nkJ8KS42WjeVDJjHPy3+XKP1LKQAjwoRG\n81J2u71i3KstTC2DpEWWLJ7aWlyvIi0an7YQO7T0bDKRPlF2yOnxUmj9ETRJNPziJuU3MXFniuTZ\njTSoR5EfFvGeIh6Uh7GJe7SRBrWaUa0Wymvha7X2PA81o/mux0aY9eQQaZF4vV6m7ik+1MHBQYWs\nQ1NTEzKZjLSFkZ/UQqGAdDrNyDbEHCgVdIxMIF9MKBQKhiUnaCFZLBZWsRUvwmmKmMpyuYxsNsuK\nFa2trRWhnM1m0yVxUo93Su8tRhFkNHgMbKM2MUUAfM6YvwiSQ+Qx4ny5XC6pHhU/fvl8Xoq9LRaL\njHHM4/GgpaXF0Gb3er0sr59OpxX50Hw+j1wux56RuAjEwtHh4SGTyG7kRagVnk7RyLypdRzq6TKk\nKC+TySCZTL7SSjztFd4pkxG5U01C/Gw2m63I0/PPT/YhnU4ragr0edr/eo2sWe0leJq7jo4OTE5O\n4vDwEMlkskIuwu/34+7du0xFlDfE29vbePbsGZNp5nOoRG4yNzeHjz76SGF46N7BYBBjY2MIhUIK\njJ6efvdisYjl5WX84Q9/QDAYrBgwLY/cYrGgpaUFvb29GB8flw729vY25ubmsLOzww4awpnm83lk\nMhl0dnbivffeq5hQm82GkydPKjCLjTrxX758ieXlZXz66acIBoOMBIUijZaWFkQiEfT29jJ6QdG7\nrDX3VSgUkMlkMD09jdXVVUWfNG3MbDaLqakpjI+PKzgMDg8P0dPTg9HRUcbzKm7svb09zMzMYH5+\nnh1kPPlzLBZDMBjEpUuX2CbTS3xDnuX9+/fx9OlTxUFExCoHBweYmprCwMBAhUqD0+nE9vY2fv/7\n3xsiPNazHgl21dPTw4Qn6+FVqBal8OuVECvXrl3D/Px8w/gcql0HBwdwuVzo7+9HZ2cnAoEAK97y\neO719XVMT08jk8lUqDAsLCxgbW2NYeD5SDGfz2N9fR0PHjxgCso8AoOY9Ajupkfdw1wtgU0GtVwu\no62tDYVCQXFSlMtlRKNRRivGF5lMJhP29vawtLSEWCxWQZF3eHiITCaD+fl5dgKLBnVoaAherxce\njwcOh8NQCFUsFrG6uopPPvlEsQi1+nfpnWw2Gzo6OnDx4kWMjIxIC2bRaBS3b9/G/Pw8o4qj0NPp\ndCIQCKCrq4sR5/Ib0GKxoLe31xB5rREDt7a2hmvXrjEVTz5dE4lEcPz4cTgcDoRCoYZtjqamJhSL\nRcTjcdy7dw937txRULkRfV9XVxdOnjypaAygZ/P5fAiHw/D7/RUtk4eHh8hms3j8+DE+/fRTVo0W\nKRU7OzsxMTEBp9Opm6yDDoPFxUXcv3+fUTryKYXW1lYEg0FMTk4yyXPeoKbTaczOzuLevXuGDLke\nr5+E+Xw+H0vlNMpgVyvUkEG9fv06o9A8SmPK86EGAgHk83nGAczvYbIfL168wGeffcbUXvmU4+7u\nLtbX17G/v19RQC8Wi9jY2EBTUxOSyaSiNkS1ojNnzjDuXz1jrumhAn+iFfP5fHA6nejq6qpYwC9f\nvsTNmzfxq1/9CktLS4qwllrbcrkc474UT15iEk8kEtLCRz6fx+nTp1mHiJGQ/+DgANvb29jf369g\npar2WYfDga6uLrS3tzOPVbxisRgePnyIJ0+eMJJoeu9wOIwTJ07gtddew8WLFyvyO0SW7HK5Kjpu\nGpGTIq9ZhNq8fPmSNSuQl1Xvd/KfLRaLSCaTrKmBoEV0tbS0IBQKYXR0FO3t7YysmZ7NarUyKJno\nMb98+RL7+/uYnZ3F9evXK4yWyWTClStXcOLECUxMTKCjo8PQJuaJt9fX1xXPbrVaGZP/wMAA4+7k\n331paQlffvklbt261dCQn2Skp6amMDExgba2tleaYyUeWZLCflVS5uVyGV1dXYhEIgwzLSIR9vf3\nsb6+jvv372NxcbGigFgsFlm3oZgSODg4QDweZ/fg0TlkkO12O9566y3dB6RmDpUsNS1wItYVjaLD\n4UA6nUY0GtXUApL9jNx2WY6TThiZMda7IPL5PJNl0LOp6DmdTifsdjt7LhkkgyQ1tre3EY/HFaeX\nxWJBsViEw+Go2Nh61VvrwVjSISYaJDWO2UZuAmo3jkaj2N/fr/ACi8UivF4vQqEQ2traVEXv1NZL\nOp3G1tZWhYdIuvdWqxV+vx/t7e1Ve/z5OaMQP5VKMQNCh7DNZkMoFMLLly/R0tLCojYelhWPx1nX\nUaFQaJiHSs5BNptleel68bcy6Jra/cjxoRzyq7zsdruiFZZvOqJx2dvbw87ODra2tnTbHlqr+Xwe\nhUKBSRiJtaFEIlFVR8xwlV+saPIpAQIz22w22Gw21ncuAoarhdpqXlo1YH81kTOjIny0gOgg4T1T\n8fn5ghlfKeRllUVMp5pUcKMB6rKqLc0hL/imp5JuJK8rIjn49+Wr+vwGoQUre2bZ/a1WK+x2Ozto\nCV/MjzNvgGkDaq0hekYq1lFai8I88Z3o4KBcGx0UVMClw6oRZMgi3I3fk7Lx1rNPjIbt9cIX9aYY\n+Kq8CKNTI2YRC+hqWGE961Xc/5RXr7vKL252Nclbyn2pMSPpPU1l+EsjYF4tELKYpqgllJUZZtkz\ni9V+ta4b/v3ELiXe8NbDvcnnhGWcoVpzIspgV+NMVVs3sv/LJJD5fxM7eGQbQMvgigeWnmIC/73i\nJuUNKr+5RXpDkeO21nWndYDzraXicxopRIl0hDKVW72eXiMMqtYzU+OLbD75MZfhSPU2iciKctXk\nqw3lUGV/5z1OnsyD/7keyjW9F0/hVm3Q+cVW78Tz9GPkifBVVb5izhOa8EzvYjsdT4MmYlNl3kMt\nKQ41j0IM+Y3Q2/G4PFKqNWLoeaMizouM1pHv1KrmbYngfvEQFcH6WiE/6cKLjoGMTId/ZpHTU/Zs\njTQ65NHztHsyz16mMiB67/zBWY2l/qg9VBGPLY6lSGfJRx9i62sjCmJiO25DPFQ9X9rU1MQkjVOp\nlG7VU71Xa2sr7Ha7dLBMJhMcDge8Xi+TmRXhJLXmAR0OB1pbW5k0MZ+Mp/fO5XJwuVysIs0bCtJN\nUqNjIwjQ3t6eAv1Axpio+3gsp5H3IkE5PrTnK+ktLS1SfC29G+UJnU4nC4GIL9Xr9cLhcNS0gKlS\nv729zejr+Pe3Wq1wOBxwOp2aaq5qOXleIpvIcPR4ik1NTUgkEmzMZYanWCwyLGYsFlOE9QcHByxn\nfBSeXLlcZnlpi8WiUOgkGJ7D4YDD4agooJIRTqVSTEiTLzqTUKVarYJSWx6PRzfzmhFjSjhQSheK\nJNqZTAbxeBy7u7tMENNkMjFEycHBAcvJNwIxwyNxfD6fFBfdMIMq3ri5uRltbW04ceIEvF5vQ3JH\n/Mk/NDQEn8/HODr5k9JqtcLn8zHFR4JX1JusJ8NB4nfE6CRibBOJBCtU5HI5NpkE9+jv71fwqfJh\nbKlUws7ODpaWlhQYOSKJmZ+fV2xQo55OW1sb+vv7GTSJJ7bu7u5Gb28vo0QUD0mTyYTOzk5MTU0x\nDlxqF3758iX6+/sRDAYZjM1IqFgqlRCNRvHs2TNkMhm2Zuj9CZoUiUTYgWYk7ROPx7G0tITW1lZm\n9LS4EXhPPJPJYHNzE3t7e9KKciaTwdbWFubm5hh6hfZAsVjEysoKdnZ2DBUx9F6lUgmrq6t48uQJ\n4vE4LBYLS8mYzWa0trYiFAohEolUOBV0eM/PzzP2MFpPdrsdyWQSq6urSCaTDJ0gQvz8fj8GBgbg\n8XjqgmvJmgbi8Tjm5uYqSHGoqEwCgORYUa6aaDJzuRz6+vrg9/sbwljFH1KDg4MMiaOHr6BuH5ng\nN3//93/PDEMjL4/Hg66uLsbpyU+k2+1mypznzp1TVP/qHVCC/zx79gz/+q//WtH109TUhOHhYZw5\ncwbhcFhBjk1A7La2NgSDwYq8KQH/7969i//zf/6PomLNe6hbW1tIpVI1tS6OjY3hpz/9KTo6OhjW\nlZdqpmcT842UjL9w4QJ6enrYe/MHCm1e6hYysrHy+TweP36MWCwGp9PJgNr0jgMDA3jttdfw3e9+\nFx6PRxd1Ih8CLiwsIJVK4auvvlJgXPV4qAcHB4wykRwDunepVMLW1hby+TxWVlbg8XgqpMOz2SzW\n1tZYhb+RVy6Xw82bNzE7O8uIt+nZXC4XBgYGcObMGVy5cgUul0uRhz88PEQ0GsWvf/1rPHz4UDGn\nRNm4vb2NWCxWUckn/O3ExAR+/vOfo7e3t2HRJ83Z06dP8Z//+Z9MHpv3oNPpNO7evYvFxUX88Y9/\nZJESGXq3242BgQH8zd/8DQKBQENTEqTIGgqFVNUKdBlUIxVdIrcNBAJHklvREgsjWr5gMNgQkDP/\n3gQYfvToEW7cuKHAJPJtku+99x5OnTqFYDAoTTfIKuW0QdfX1/HVV19haWlJQQpT72YkHOypU6fQ\n19cHn8+nqhory1sDQF9fH/r6+mqao2qe1ubmJjY3N6VFrGQyCZfLhampKV35VHFcY7EYYrFYwwsm\n5XIZ6XQa6XQaKysreNXXwcEBXrx4gRcvXlTkGb1eLzKZDILBoBTaRN71kydPcOPGDQWMUK3wx/+Z\noH9nzpzBxMREXfURkdmM6hO/+93vFFEQfwCvrq5idXW14pkJK97V1YXJyckK+exv4jI3ctEdVeXP\niPBdvXkqvgKqR46YT5TL6PmqFd2oyMPnrhphVGmx8nAiMbSvZ04btWB5+WdR7+ovl/bakWmvaY1z\nPYXbWvL41dYV7R8jKRJZylEsjB/F1fAc6qvqjnhV3yueZGo8nkbhXkZOSBn0pVGdUrKxE2n6jmpe\narm3XgYsvZumHrhZo571qC+Z0qsWY5OoKlorBV8tRNDVqPeMvreaSi2PtlB7tqM8rM34y6U6yH9u\nXpKR521kHkzPRjJyMDXCg/7ffmmx/r+qdVbLdzayzfko1/X/OoPaKPYcvae7llKA1qYX+RSN5BR5\n7GOjwioZCF2PB2NkXNXkN/gxaUSHkOhV8XyV32RE9edozHkpIrWGi1qMqBFWLS0KwUamkGp5tiM3\nqLQxiS8wl8uxKn4jw9JvwlDzmEdi8SF8nRGDSFLOxGbDM+EQsTXJBcvCL5IV5juS6N8LhQIjdRB7\n7omn1e12M0iHqF3kdDqRSqWwsbGBbDZrqP2WhPxkTFiEG6Tebp5NCgCSySQrLPX09CCXy6nKktN7\ni/Lb2WwWW1tbWFlZUeAeDw8Psbm5iWw2q0qGTRhWh8MhpVzUSv0QRpZo+sTPUsur2+1mCrpH5RmJ\n303y24TDNHpZLBbGfsa/Gz8n+/v7Vcm9ZfuDuFLz+TyDXfH5XcLHikRAr+IiOklR70vP1dzcDIfD\ngZaWFt1YVHO1cIKqbDMzM3jy5An29vbqxnp+0waVQNodHR04efIkBgYGGDTCSGi6urqKP/zhD3j8\n+DGcTieDdBwcHDBWoomJCYyOjlZ0TRG/5d/+7d8ypip6PrPZjNXVVdy7dw/Ly8vY3t5m31kul5kO\n+smTJzE5OclUQ3ljXS6X8eWXXzKjVc1r5DvdrFYrLl26hDNnzijei7Csa2trePbsGcPKEs6VOsXM\nZjN6e3vR19enMJgkTvj48WPcvXsX8XhcYXABYHd3F48fP8bh4SHu379f0bueTqfx+PFjRcGNJ/Ih\n/trBwUG0tLQoKP60DGpzczNyuRzu3LmDJ0+eYHd3F4VCgR1WJpMJwWAQ/f39mJqaQkdHh4Lk+igN\nqslkQi6Xw+eff45nz56xBhq930nP/s477zDVVB7Yn81m8fTpU0xPTzPnwMj7pFIp3L59G7Ozs0gk\nEgwbWywWYTab0d/fj9HRURw/fhxut7vullwjY7izs4Nbt25heXkZyWRS2s0pXvR8VqsVIyMjeOON\nNxAIBHRBp6oa1EKhgK2tLTx48AAfffQRdnd3Gb7vz9GoknHI5/MYGxuD3W5HW1sbAwUb8VA3Nzfx\n5Zdfwul0ssEmg9re3o5z586htbVVAefgvZ3BwUH4fD4FsJ36lh89eoRUKoVUKoWdnR3F99psNvj9\nfrz22mt499132SLlPcybN2/i97//Pba2tpDJZHS9E20EwtAeP36cdVPxqIZoNIr79+/j9u3bDHBN\nxtbr9aKjowPvvvsuTp8+regwa25uZiTACwsLyGazFTAfApcTTlUkcSYJbT505fu6Ozs7cfr0aZw/\nfx4dHR3M8OoxqAQSX19fRyqVQrFYVOhe+f1+jIyM4M0338To6CjrOmpkyKpmUAmXvLq6ytQg1L5X\nDHt5GenJyUkFNtdqtSIWi8FsNiORSCAWi2F/f18hKVPt+TKZDB4+fIjPP/8cW1tbKJVKsFgsKBQK\nsFqtOHPmDMxmMwPJN4qFS49nH4/HcefOHdy7d4+x4VUjmueB/UQH6fP5KiKamkP+bDaLeDyOaDSK\nzc3NP3v9bFpQfr8fyWQSuVxOl/aQLOSPRqOKvB4/4NFoFNlsVhoumUwmtLS0wOFwVISO5XIZm5ub\naG1tZd6feCjY7Xb4/X50d3crpD7o83fv3sXOzg7W19fZyazHQyUoF08ILhrd/f19xGIxbG1tYX19\nXcG3QK16RCTNt95SeyeRJMvCPzpccrmcdOGTUZUt7KamJrjdboRCIbS3t6Orq0s3wTS1GNOYi/hX\nIkBvbW1FOBxGV1dX3XwLRqKq3d1dtLS0wGq1Gg6byXCGw2EEAoEKZieTyQSfz8dI2I0aO6IsXF1d\nZdSFZJBdLhei0SiSyaRivI7SqPJXPp/HxsYG62I7ODioOn68bPfQ0JAh5QezHuNDdGv5fJ6dXjKB\nr2+r8VSTluWF8mq51PrEqc+/WCwqSCxkOu0yWZdyucza7MROJgrpyZMkkmoREmUymTRz37I5o9Ob\nwjWZHDKtB7o3tdzS79jtdhbq8c9G30VeixrRBqVjxNysWh5PfA+z2azgA9CT46T7EZcqf0CKxTbq\no+cPwmqcq0aKWWrCh7lcTlODTMZsRj/nDwRZ7tjhcMBqtdZkTPlDLpfLYX9/n6l60HqifdCIhhWj\n6RV+rVKOWKsGxEOuiJbRCKzLrOclRNVDtWrdq0446zWmogfIJ8zFqnEtVXAR38cD1HnPVaaFLk4+\nfx8Z05HMOMvuzTcN0N9FPgKR+YqMPF+k4+8vo6qjv9Pzi8B8/mQXJZb1rrlqByT/XiKVJN+sYURH\nSTyg6CDhe/zJ6Is6RmrfI2MWE9edOCc8V6uRNJvsd/m9y6eY6O9Gqer4d+abBqhoSgWqRjRriGgA\nvZEHPRvfwqz1GT4fTyKWDeNDrXZyysLBb6OHqpX7aJTmjwxgzH+nyPMpGhWRWk+mPy9GDLI8oho5\ntx5FAPpO2gjEVCXr9xchWWoLv5Yxlh2Eal6eyNUrO4i08pzi/UqlkqrEtXhwyTapmrw2/2/V5Lpr\ngfvwcyKjbtTax0aNtWz98x1PIh0ffxA1IjfK/0yEgmkZY6MRQy2Rd0NwqOQe19p5cRQ5J5Hv8agK\nXKKON8+ITxs0n88bOuVoU1MIS1Rt9HcRwqHHeIky1qJ3LuuiokITf28Kx/UsTFnUoieXyY+rXiA3\nSaDI+HhlXJ5acCoi3uDpAykVQJtYlLFWw/7KeFJlniB9nt9HssOymmEjRjHZsxHdIo8E0ToIjNYk\nKFfLrzFaq7UabD5aEfeZ1WrVDeE0Qq5eS6qmYQaV2Gi6u7u/EZxZNcO0u7uLtbU1VpFt5EWcoR6P\nh20+WlgtLS1obW1FIpHAvXv3dOMh6c8bGxtwOBzo6+tT5FkPDw/hdrvR29uLjo4O3Zyk/Oam4kow\nGFSod4ob6/79++y7yYMulUqYn5/H1tYW04uqhQ1L7QB0Op3s2Ygqrlpox0O2+vv7meS4rAVR67JY\nLOju7sbk5CR8Ph8rjFEqpKOjAxaLBUtLSxXaTs3NzXC5XIhEIgrECM/Utbu7i93dXYZk4KVbbDYb\nk/f2er26vCbeA0ylUgzOlslkFFhTwiX39PQw3uBGXk6nEwMDA+z9iK+UpJFGR0cRiUQUB5TeOSFE\nC3H40kFQLpdhsVgQDofR39+vyjv8qq+6DCqdyKFQCOfPn0cwGPzWIACo6DQ7O4tkMolisdjwqmwg\nEMBrr72Gzs5OuFwuRS6KTtadnR189tlnFV6JWujF5yQ9Hg/GxsYwOjrKflYqleB0OhEOh9HT08M8\nYb1dKkT31tnZifHxcfT39yuY3HmiiS+++EIhy0LGe2lpiWmdy9IqteTG6PMejwfd3d04fvw4IpGI\nakpFvAd1nI2Pj6Ozs5NtMCOel9VqRX9/P3K5HKPw43OM5CU9f/4cs7OzipwoYT3Pnz8Pr9db4flT\nU8LMzAyWl5eZgijdw+PxoKenB06nE16vt+pBwhvzg4MDJBIJzM/Pw+VyYX5+XpG2MJvNCAQCjHS8\nlpysVorC7XZjYmICVquVYap53tJjx46hr6+PIVZENQutA5ecisHBQXR3dzNljMPDQ5jNZvh8PgwP\nD7P992fdekoGtaenB++99x6OHTv2rar25/N5fPbZZ3j69CkjSm7k1dXVhbfeegtjY2Ps9KTNE4vF\nMDc3h9u3b+P27duG8ssmkwnDw8O4fPkyRkZG0NXVxYwZbV7yaLRY7dUWKmFjr1y5gnPnzknD8l/+\n8pe4evUqo3ojL4yknNPpdIVBrXctAYDf78f4+Di+973vYXx8XLcHTsaBOrycTqeuUJk35jabDWNj\nY+jq6mLVXR6dsLy8jOnpaXzxxRdYXFxUHCTNzc3o6+tj4H8xHCXP/tq1a3j8+DHi8biiENXa2oqT\nJ0+ir68PPT09hsJYXi59eXmZdXHxGFsySl1dXQ1n3fd6vTh16hRGRkaYZ8ynFPm8M8AAACAASURB\nVFwuF+tINJq2c7vdOHHiBC5evIjx8XGGGqHDxmq1wuVyMTnyP0sPlT/1SZa4p6cHQ0NDujSgXlUO\ndW9vDzMzM2xxN+reoqfX39/PZFBosp1OJwOIz8zMqAodyu5tMpnQ2toKi8WC9vZ2hYcq/q7oCekJ\ns61WK1paWtDZ2cnmjN8EFD6vrKwwj0P0amrJQWl5mHyI19bWhu7ubgwODho6MKp5pHp0yXw+H3w+\nX8Xvkhz58+fPmafJV8wp55tOpys0piglkU6nsbGxgRcvXmB7e1vRhUWy13olz0VGfmoF5rlgeTxl\nU1MTstlszYVjNRFNymWGw2HVMVY72ESkipg3PTw8hMViQVtbG7q6ujA0NAS3263JJaFnvX1rPVQ+\nV5nP51EsFtkp9E11UvEwmkKhUIEja+QgE8aNKpi8JAU9A7+5qnWfiBArvqJMf+fDJaPy2Py9eP4A\nghlZLBYcHh6ydlAqxIjFC73wGiNUezLRODJERkJ3mRChUVYmUYCPvx8/p9SqTGNHkuKqm+3/YmT5\n7it6VyqCNaIGIUKLLBZLzRpgRgtTWoWlWoo+hHGlQigvYClCAr9pR65hBrUaldhRnxS18DM26vvU\nGhzUYB56eETV2gn1arDXYmTVsLgyZiIthUwZjlMr/0ebpFbYk56il9Fx4dEFMuwjb3hlGNZq86e2\nbqvhoWWk53rUShu9H/TId1dbb0bQBeLvi/hnLcSLDBp4lFLZDYNNiTjLbzqX2gjZW3Eiqy0OLZ10\nI3g/tcJeo9ns+eeWEfaK8s7VNpVRr1Xt8JGNrx5yl0alH8T3VztgRMNWzXNXM8i1eFdaoa6aHHO9\nDkQtWE+jTpARg6pXHFJ2OB6V42VuxKZUM6Q0mXSqNhL4z4fRMvB5vd6cqHXOd1vQO/EYVJnBbYQX\nKeMbrXcx8JufqsS8sinRBVqtVoYjrJb/pJQHL+VdKpUUgnWUF6N8JVXNqYhSLBYrOryqjaVoIMVO\nKRkPAhHQGPWk6Nl4MUP6TqvVylIkR+UgUMqAnp8P4SkUbnThlcfOHh4eVojo1dK0waeOiJ5SzTbQ\nOqL34hsIqjVR8Dlq2qviPqb3apRtanhSRSy+FAoFhr3LZDINSwFQ3srr9aKtrQ1tbW1VWWSMercO\nhwPt7e04fvw4SqUSW8CU5yMpZiO63d/EJYY8+Xweu7u7WFxcRCgUYo0EZrOZGTYAGB4eZoWMapVy\nGhOv14twOIxMJoOnT58qKBGJIi+fz7Nq8/7+PqxWKw4PD7G/v4+hoSFEIhFDmGb+/VKpFOLxOGOL\n4sN34pANh8NobW3V7SXRenC5XAiFQhgcHGR8CwTZslqtGBgYYIKIjV4PJpMJkUgEo6OjcLlcKBaL\nrC2SFFcTiQQSiYTuwpbe9VIoFJjUMxm3eg0qPXexWMTCwgIymYzivvT/YrGI7e1tLCwsMFQLNS5o\nGVQas42NDbS0tGBwcBB+v58VEE0mEw4ODpBKpZBIJJBMJhklYj02xHxUG5gePJlM4quvvsL9+/fx\n/PlzdprX0zlBk+zz+TA2NoZz587h5MmTjMauVi+BH0ybzYZQKIQ33ngD4XBYgYWk9+vo6EB/fz/b\n/N/G1ltZuBmPx/Hw4UPE43F8/vnnFThUk8mEoaEh/OM//iNjXlIr7PEby2QyIZ/PI5PJYG5uDteu\nXVMYYyrkdHV14Xvf+x48Hg/jciXvyu/3IxwOIxKJ6GLn57t0yuUy5ubm8PXXX+PRo0eIxWJsrZXL\nZbS2tuLYsWN49913MTU1pftgpc1JlIzBYBDJZLICyub1ejEyMgKHw9EQOXP+cjqduHz5Mvr6+pDN\nZlEqlZh3XygUMD8/j3v37uH27duIRqMNkRrhpZyfPHmCf/u3f2PNFo3IV9O87OzsYGVlRdFCShFG\nKpXCnTt3sL6+jmvXriminGrhfrlchs/nw9DQEM6ePatoUrHZbMhms4yb9+uvv8be3l7d+/jIDCpd\ne3t7mJ+fx82bN/HVV1+hWCwq9NKNXrRQ8/k8IpEI9vf3EYlEMD4+3hA2G74C29raCrfbjaGhIanR\nJQIFUTv+2+it8ic/8ZCur68rDBZ5/Q6HA0NDQ3jjjTfg9/sriLdlnAW0ube3tzE3N4fPP/8cH374\nIaNyo/u3tLTgJz/5CU6cOIGBgQH4/X5FyMeHs0YPRqI9fPDgAT777DOsrKwo1hqRcp86dcpwrpI4\nRb1eLyPOFseC1gNvaBtVPLRarRgdHcXQ0JACaWCz2bC3t4dgMMiigmg0ygxDI8QY9/b2sLKygq2t\nrSNZ25RKkBXb9vf38eLFCywtLRleD6VSCadPn8brr7+OCxcuIBKJMINss9mQSCRgs9mws7ODhw8f\n6uKB/UYMqlYORCZ7UYsXSYtKDzlCPQuZNrZMRVGtsnmU6IJG8EjyeW3xnUS6N5vNpiCJrubNkTEk\nyBNP0kxpAV7SmPKlMkKXejcn5ej4tlmCudWTx1RLLR0l4xr/3bJcIXE81JIm0XtYFQqFIzGoWtEq\n2Q+RV8LIfYk1itYbD23kWbK+lTnUagOmRWFmxNA1giXHqNdazfMTJTn0PJsWsYlM0lpPtV32cy34\nkvh3sQ1WDF/VvlOk9eMxg7JDQVY0bGSoKlsnjWq3bOShbSQ6E9/JiAijOAZa46HFntaIdzF6j2pG\nt1pNRywy82OqVois5d1eiUGVQYtq9VKNaJE34jLynDKPTw/UROx60soJyRaJ1iKqRh0n0gVSLpRH\nAogIDbV+bLVDTo1IWqR6Exd+Ld44z0pEHogaB2wtKZNq60Hr/rL5Nhpe8s/B1wtk+N9qh5MahpU3\nPFqYVzWDX2uhyqix1TsnMqdExmcgQ+t8I/R9R3Ea6wn7X/VhYMR7FvOr1SZaTCOIm1+kCdSTP8rn\n8xWywVqYTwqZC4UCgD8V5gj/KYOl1RwW/V9KQhqbegi+q+XjeGNda8gveuy1eGoUuvJKCLyAIlEC\nVjOwavcXOUdFWByhOKhTS9a6LGuuMILvrVURuV6DWuv9RdJwvksP+BPCQKRC/NYY1D+HSxb+lkol\nBe5Nz2f53J2a8eQlNURvghY+Tere3p4CcygjeVZbhCSToldpUoYTFA8xHtenZwOpdY2RNAX/O3Rf\ner9avVSSKeELiPVwOvDeDd+2K3ZyiYeomCagZyN5FkI+VIPeqalk8BepLRB1ocx7FCXLgT9poxGG\nmKTP+XEXMaiyZxPJyI9KM0pNSUHt2fQYairE5vP5ishIbxPBXwxqlYu0xl+8eIEnT54owoRqRoPE\n6Obn57G8vCxdDBaLBYODgxgZGYHX61VwYxIEJ51O49atW3j48CHbpIeHh0ypdXBwEMeOHasgECFe\n0B/96EfY2dlhvKV6DSo9529/+1sFgoE8u/b2dvT396O9vb0Cz1ntKhQKmJ6extWrVxEMBtnmpYMr\nFAqhs7MTfX19hpVoSUb69ddfRzAYRCKRUMyZy+VCV1cXuru7awqx4/E4Njc3MTc3h93dXQUHLgnd\njY+Po7u7u2JOaL6vXLmCrq4upNNplo5oamqC1+vF4OAgIxnRGzkR4xJJohPzFB22NJ8OhwPPnz9H\nNBqVHprpdBpDQ0Po7OxkHj7NPZG6EGubON9er5exdHk8HgW06agMqslkYoQza2trmJmZQTqdNhRx\nOhwO9PT04OzZs0yqm+euMJlMmJycRFtbm+5i318MqsqElUolJJNJTE9P44MPPmC4Pz0GlSZne3sb\nGxsbFRAb2gTHjh3Dm2++ifb2dsbzSP8ei8WwuLiIubk5JJNJRdeZy+VCT08PTCYTurq6pMS93d3d\nuHLlCjKZjAK6pNegPnnyBB9//DED+ZNBbW5uxvj4OGMZM2pQi8UiFhcXUS6XFThUai4YGBjA5OQk\na9jQk5fjx7WzsxNNTU3o6upSEEQTxKitrQ0dHR2Gw9jDw0MkEgnMzs7i+vXrWFxcZJ1SVDXu7u6G\n2+1Ge3u7gqmep7k0m804duwYCoWCIr9rt9sRDAbh9/sNp6LMZjOCwSDGxsbgcrmQzWZZ5ZreIZVK\n4f79+4hGo4p1Vi6X4XQ60dXVhWPHjiEQCLA5obHb3t7G48ePsbq6ilQqVRGxeDweTE5OYmpqisHs\n+O84KoNKh8e9e/ewtrbGDKoemRlKaUUiETQ1NcHv9zP5a96xIaeBdyy01vtfDKrEmJDHlMlksLy8\njK+//pqFA3oXO68Uq+ahdnd348KFC+jq6qpgXHr48CGePn2K+fl5LCwsKApSbrcbsVgMAwMDFXIk\ndAUCATidzprb6p4+fcrAzvzmI/nnvr4+xn9rxKCWSiVsbW0hlUopIFO08ff29uBwODAxMaEbJcE/\ng8/ng9vtRl9fn8JL4iWyayEjJqO0srKCJ0+e4NmzZ4rwtrm5GQMDAzhz5gxLEYk58GAwiJaWFgwM\nDFTkGyn9Q6kAvR45pQy8Xi/sdjvC4XDF4V8ul7G0tISrV6/i66+/rtDJam9vRzAYREdHB8bHxxl9\nIa3j7e1tHB4e4tNPP5XWMlwuF0ZGRnDu3DkEAgHWTHHUtQ2Sr97b28Pnn39eYTS1jCodRH6/H263\nG93d3RWUi3zKTG+e/y8GVcO4lkol7O3tIRaLIZfL1UT+oAVJISmSQCCgqKiS93Z4eIhMJoNYLKbw\nlIrFIvx+f0Welr+/3W5nnmu1QhS/Qfl+8FQqhWQyqQi57XY70uk08vm8QgFUPJC0DFM+n1dgGnnU\nRzKZxN7eHgs7+UNGz/hbrVYG5ld7b6OHAH/I5nI5JJNJxGIxBRrCZDIhEAiwOZHpQTkcjqoky0Zx\nrDzwn8iWZfwGOzs7KBaLiMfjLOqgNWez2VAqlWC32+Hz+RAIBBTSLaVSCW63W6qXRfdxuVxoa2tT\neLhGDy0jOX5qYy4Wi3C5XAqBQq1ClNiIYbPZYLVaNQmqj0T19P+Pl+j9GG0nrOYZUiX+4OAAFouF\nAZf5Kj+fRqAFTgtBC5Aswqz0FDkopUBetd1uZ+Ebn+Otxv6kZ4xEZq6mpiams0QEIHplp2XvXS3k\nU9skWjyzfNMCjQF9lx4+VDFHXYtBMfLuNMaEICB0Bclf87pXfFWfOEjpXYvFooL3V0ZpSCQnfOHO\naKOD0aIppZD4SnytFI9qe5VnYvuLQa3RiFYzkI3klaSwl

5cl1pJ75iub1Qy2Fpt/tfekyinfUSWT\nxea/h690V9tIImm1muE0UmWV4W/VDGotxkvG20o/IxYkmSfNG5+jwE2LYaqYK+SNnKxfXm1d8gUa\nLV5Y8YAUJa0bZVD1cAyr4Wa18NeN7HD7i0FtQAhf6/14r5D/GW1OPrfGk5fw9HZa91fTQueB2+IJ\nzHuftLH4Z6Xv5gtJIsWbHvC7zMPlpaPp3q+SF4EfE63vJU+VHz89BqSRxlQ8NPhcrdiiLGKbeWFH\n/lAXja7YoszD+fh1xrNe8WvCiLeoFm3JugfFw5jmQ4Se0XrVW9BshOP1F4Nag1FtxH3K5TIymQyi\n0SgDufNexv7+PsxmMzweD9OronyY1+tFIBCA2+1WndhcLsfkhEXGJ4vFwvCGREHHbzCSwe7o6IDD\n4VCwOfFhYzqdxs7OjkLGIxaLMcE4mQdNtIhut1uB2aRDxOPxwGQyYX9/H7u7u+x7XwVpOSEXnE5n\nxeYkZIbb7UZLSwv8fr+iym+xWBAKhSoKGI0K52vx6HipHKvVikAggI6ODlYPoMObVFopP0yGlO4f\nj8dRKBQYNSP/veVyGV6vF4VCAYlEghk2vTlUKvx4vV7GbKb1nuJBYTab4XQ64fP5EAqFFBjgUqmE\ntrY22O12aYPNUczJXwzqN2SYS6USNjY2cPfuXaytrTE9JwqZ4/E4HA4HY2SiDX5wcACXy4Xe3l6m\nEy+7fywWw/Pnz5HNZlkRgi6Px4NQKITu7m4F7pH3WHp7e3H+/HkmOkcFq3K5jEAggGw2i+fPn2Nr\na4t5JCQjvLq6iu3tbalBNZvNDMdKSpi8R+rz+WC327G2toZsNqtIbRy1QbXZbOjv70d3dzc8Ho+i\nEYCwwV1dXThx4gQ8Hg+jgyODSuMpFm++ydQVeaUk9dzU1MRy5NQ9RsD2ra0tJoxH+WwS90smkxgc\nHER7e7siv00wvmw2i6dPnzIqS4qwqr0/FfPGxsYQDAYN9dE3NzfD6XQiEong5MmT6Pj/2ru2n7aO\nr7vAF8A22AZsY0y4hEuAJgY1TdIqjZqfWqlVlb+h/2DfqqoPldK+NBclaUhIQghgCMFggy9gfMEX\njL+HT3s0ZzzHPscXoO3ZUhQlmOOZOTN79uxZey2/X8H0dXp6iqmpKQwODjJ0SrvNcKgXYHTTvby8\njIODA1bZQrsvYRqDwSCCwSB8Ph9jfKJjjN1uh8fjYVGSmFNaXV3Fzz//jGg0inQ6rch/BgIBLCws\n4JtvvlFMYv7oeuvWLVy5ckVxfCPaxI8fP2JlZQUvXrxgCASa4MViEblcDpFIRArp6u7uRjAYxIMH\nDzA0NKTQoCf6vY8fP+Kvv/5COBxWkAm321wuF3788Ud0dXUpUBK08IeGhhgYPJvNKnLetLgDgYBq\npHVRZjab4fV68eDBA9y7d0/B2lSpVHB4eIjV1VW8efMGkUhEMV9MJhN6e3sxMTGBH374AUNDQ4q+\nVSoVRKNRRs+ZyWQUVUtaHOr169fx008/Mdyx1rSJxWJBf38/FhcX4fP5qqCNhJYJBALs5NPuk47h\nUC/IyuUyIpEIIpGINA92+/Zt3L59G9euXcP169erOFfr6TLF43EsLy/j48ePODw8VNz8Tk1NweFw\nYGFhocpZ8SD00dFRhZOmVMTp6SmeP3+O9+/fK+SUtaRELBYL/H4/gsEgJiYm4Ha7FUf6paUlRCIR\nbG5u4sWLFyy6Pg/uBo/Hg+vXrzMCZ3Hh9/b2ore3FyMjIy1PF7WDUERMZczNzVVtvB0dHQiHw9jZ\n2UE0GsXff//NJK4JDjYyMoKBgQHMzc1hfn6+KvpeWVnBw4cP8e7dO0QiEc2KARQ8AGBy5Xr6SpsY\nbWTnncKTvbOWOdSLlm/9J5vstlwW1daSSBYdLH95JWNw4i+A6l24iTk1cZcXCTbqzQWekIJ/tgxy\ndB4qtmqoAN7pqN0YtxpneV7rUGSrEglT+P/n/02/y/9MvMyr9c7E23Wex7UZEUZZRNyoTEsz763z\nIh3IP9XxteuZtY4jjSiKqon8yfrSDJWimkhhrXbKJJhrHe8u0gm1inO33UFHo4KNapSYIhpEja9X\njUqynpot75Qvc7B26dim2kUC3WooUzPRTCteltouy4PNtVSDNNMWNcB/rQXTCNl3s7yT572g9GwY\n/zSrRTrdCmJu2TjykX+rhDUvQ+BmPq+XxVdiNKPZIi7iVujmXJYoQ+ybGo5UbcKQY6p3K84f1bTo\nnKthAcUj4L8h9cLLkotj8286QcmO52KKhzZykWC8Vfy1fEHEeSgC/GMdqkj6YLfb0d/fD7/fz6jk\nWmFerxdOp5OpTLYqeuQB0L29vfD7/VWJdoKfUN25SFpMJZQ9PT0KXk4tZjKZMDAwAJvNJgUmE4A6\nl8vh5OSk6tlnZ2c4PDxEsVisKhogOAnhPCORSFXusqOjg+ExZeW2VquVYWGHh4cVv0cLJJvNIp/P\n/6Ny60TOkkgk4HA4mOx5qyJcquWn0tpWoRdIW61QKCCXy+mizqtUKojFYiiVSrDZbPB6vQoNMZPJ\nBLfbDbPZjGQyib29vaoj+sHBAbLZrFTbjfC7hHsW9cM6OzvhcrlUuWpJXpwvbT0v50qcGA6HQ7Pu\nlLmdjQH+H4pCLDR3795lNb6tmEQOhwPDw8OYmZlhpBPNKkzSy7ZarfB4PPjqq69gtVoVmt2UU/rw\n4QMeP36McDiMbDarcFqkjhkMBrG4uIhiscieUS/53tHRwZh/vF5v1efz+Tz29/fx8uVLvHr1SkrP\n9/79e0QiEZycnFRFkMlkEsvLy8jn83j9+rUiqqXKrHv37uHOnTtsEdDzLRYLxsfH8e2332J6ehrJ\nZFIhFJdOpxGNRvHkyROsrq5WYWAvs+VyOTx79gypVAr9/f1NsybReyuVSujs7MTi4iJu3LiBsbEx\nhRxzo3OW0BHFYhG7u7tYW1vDy5cvGVdrvQCDcM3El7qwsIDbt28DAGOsIihcsVjEb7/9JuUFpvlE\n2vbi5js6Oor5+XncvHkTNpuNOUZ6fiAQYNSGYkoglUrhzZs3WF1dxebmJsPJtvO0SN9NSrP379+H\nx+PR5FTbFqHSH7vdzohzWxmd8nhMqrJohcaUKCM9OzsLj8dTdbNLMJpQKMTYqPgFQlCOmzdv4vvv\nv2fqrFoJIGw2G9xut3RXL5VKSCaTePv2LX7//XdkMpmqiOfo6IhFqeLEy2Qy2N7extHREVZWVhSp\nE5PJhK6uLni9XiwsLDBAtMi9SSB4wv5R+V8ikcDm5iY+ffqE9fV1xZhe9mi1WCxiY2ODYYN5BrBm\n5tTp6Sk7BQwODsLn88HhcDDn1KjGFf1+qVRCIpHA+/fv8eeff2JnZwdWq1UTmU+pVILL5cKdO3cw\nOzuLmZkZ9Pb2sk0AAGKxGN6+fYtff/1VIT1O861QKCCRSLDomB8vqiCbn5/Hd999B7fbrYg0yUd4\nPB6GJODnYi6XQygUwtOnT7G0tIRCoSAtZmn1SYWqy7LZLBYXFxlPbb1N0NwOZ8qbxWKBy+VCX19f\nS0lnRfiPXs3uehEqDejAwACcTqf0YmJ1dVVxHOAjVKvVCqfTCY/Hw0iPtS5OmkxizT5Px5bP55FI\nJBAOhxkBtbiIZXIX5DjK5TKTVpFtFvF4XCrbS0fXrq4u9Pf3K/pEi+Ps7AxOp/NSgdu1WLlcRiqV\nQiaTaWnbaYOMx+NIp9NVwPpmc/lnZ2fI5XJIJpM4ODjAzs6OLkJxSln19vYyblSeLtJisWBrawuJ\nRALb29vSFBNJxYvrhKj9BgYG4Pf74fP5mMPkYVpqEjC0WUQiEezt7SGbzZ7bkd9kMmF6ehqFQqGq\nzW2LUMVLJ7FunKKa874sEtmA9E5cHi4iaz85XBkNnfgZngNTbwSthoOkvFk+n1do4dQaE/7/yeGS\nZhTfZrPZrHpRQA6XHL6YDyMKu1Y6pEYjXL3QMF7QrtHLEdl40QZJjqsRDS6ZE+U5FogdrFAoKCqG\n1DCz/M9JHJB4Grq7u1keloIDikRzuVzdNAKtCQqgyGF2dXXV5EoVfQlPlEMUgjwvcSOIEq1BFWFk\n9WpVmdvh1GQLUUa624rvkjkoEbDe7GYhXjjx31kLZcDfjqoB8xudCCIQWzzeydpd7zuofbzaqZYN\nlG8DOXq9yqL1+knHMD0s/jJSDa2/X2/Ma42NmpSzFiYrLfNR/C5RtJH+XYtijydHEZ9Hzpnn4OU3\nAjVaSBFbytNd8uuAr/OXjafYN9rA+WfrcaZ6eBV4qR+r1VpXPLEtDpVutPkvl9GLtcuhygaw0QGR\nTRDKT6pNHL1g/FZU18hkf/VEY2oRsNY8NE/7x+Nkadz1pGBkG4F44tEracz3TW90q3a001sAIDIj\ntTJaF6XGzWZz3ZOBWPml9t55Sj9elbUekkYmYc0HFiL3qBr8SpxTPIytkRJdPcgAPmCgew89sMCW\nOFSS5cjlcjUJfs/LeCIPGZRD68Lm4SiySU3yu2rAZ9kRi78xbzSdQZOMIB18NCgymWvB6epJFdD7\nppQBD9Hp7OxELpdjlIGNvjuz2cwo/nhOVHonxWJR9ShGi593CKKzJsSF3qM7pUOIdlCUNKZnU8qg\nlbk+OprTAue/O5PJsLkuMu/z8CdR5YF+RhIipVIJ2WxWgZgpl8t15zltonypM/9sovPLZrPIZDK6\nostcLqeYx3qLSCjY45UW6qUsRFlwPacKc7MvmdQg3717x26btdyGtTOPSt+ZzWYRCoWk0CEtm8TJ\nyQlisRh2dnYUR05aXKFQCEdHR1XQoEZrvbWaxWKBw+HAyMgIPvvsM2SzWUXbOjo6sL+/j93dXZyc\nnNTMCeod27OzMxwfHyMej+Pw8JB9N0URR0dH2N3dRTwe13zs58fIbrfD5/NhcnJSIQlD331ycoK9\nvT1Eo9GqzYIwjYODg4wHk78IJWnw3d1dJJNJ3Y7ebrfD5XJhaGgIDodDcXQlh6G371qN6B7j8Tjj\nmiUHn8vlsL6+jt3dXSkxCXHQjo+PKxQ8ySkRSiYWi+HDhw/sYpHm1MHBAUKhkCpKp7u7G8PDw+jv\n72foCEoRWK1WeL1elEolrK2tSVWA1aJ8i8WCg4MD7O7uIpVKKdIOWp0yoW1cLhfbKOpdDvN3P1NT\nU7DZbO11qHyny+Uy9vf38ejRI6yvr7OLiot0qDQR8vk81tfXkclkFPkcLcfo09NTHB8fY21tDU+e\nPKkiB+ns7MT6+jpisRjy+Xxbq4XEvJHFYoHb7cbs7Cy7WBId6vLyMuMT1ROl1xuXs7MzJBIJrKys\nYHNzE7FYjF1QmUwmpNNpxGIx7O3tKfJzWi+dCL/7xRdfwO/3M6dBm3cqlcLTp08Ri8WkUaTP58Pc\n3BwmJibgcrkUTi+bzSIajTKxOj3W2dkJp9OJiYkJBINB+P1+RSRaLpcRj8fx6NEjpFKplswHfg0V\ni0Wsra1hZWUFqVSKwZqIu3Rvbw+hUIip1IqVTX19fVhcXMTExARLg4mXtuFwGOFwmK1ruoxNJpPY\n2tpCJpORttNut2Nubg7T09Po6+tjOmT8vCkUCnj27Jkit6+2DqntXV1dbA3yqBM9c9npdCIYDGJ0\ndBR9fX110Tb8zy0WC2ZmZhhiRUvKoSURaiQSwR9//KFgf78MRqqh6XRa8wSnl0VYz3fv3uGXX35R\nqHTSwKfTaRweHjKly/PqO8G5Pv/88ypJYl7umaIKWTVVo4ubIqXnz5/j5cuX2N7eVuTESBAumUzW\nPVbLHKrT6cT09DS8Xq+CCJl+vr+/j6OjI7x+/VoB06Gc2+joKL788kss/FM9KAAAB3RJREFULi5i\naGhIsUiPj4+xubmJcDiMDx8+6Gqb2WzG4OAg5ufn8b///Q+zs7NVOcmtrS1EIhGEQiEp/rcZy+fz\nWFpawsOHDxGPxxXKpZVKhSk0yKq7zGYz+vv7cf/+fdy6dUuBWiEy8mfPnmFpaQlbW1tIpVJV6aNs\nNovj42Npn5xOJ27duoW7d+9WFURQ9Pzq1Ss8fvxYQSVZL4dN84mUcLXOJ948Hg++/vprBINBVvFV\nL9jjAzOHw8Gi+nOplKpUKkin06q712UwvRObcnX5fB6xWAxra2tSaJJWeeZWRqqUF7LZbOjp6WFO\nQ8znLS8vo6enR5E7amQsZNEDRXpbW1tYX1+X5qYauYWl4yPJGcsulkiuWLyxpr8dDgf8fj8mJycx\nMjKiQGOQhLLdbleMlZYxJ/ztwMAAxsfHce3aNcWYU6TX19enKrfcbHAQi8WwubmJaDTKNvh6+W9e\nsnxkZAQzMzMKeXHiQ11eXsbh4SE7dcjmi1o/rFYrS9N4vV7mUDs7O5FOp5FIJFAsFhEKhbC/v9/Q\nmDQ6hj09PRgeHsbk5CQ8Ho+irLYVaJu2XEq1UjWwHc60noqo2uCJC0OEi2ghemk3mYqYpOedW6MY\n3FpJf7o0ImgVP05iakDv9/K5Uhn8iHC3tXLCBPmhZ/AVP6VSCScnJw3nN+nZ1DaqfDOZTCgWi3Uv\nb5otY+3q6mI5Sn68arFB8bfW+XwehUJBkUKhaFWEJvFVS/UugeiikADwlGaiiiYePijKV2vdxJvZ\niPL5vELiWq9GWcsvpWRwkPN0HK12Qo3AlmROWG3BnFepZT1mqEacmtaJLoMkNYP9FQsiZItIjUpO\nBiFTi0L0tlHsm9qYqrVN/HyzTlX2LC19qufkm6Xs0/p5Pgg5L58hziU9Jep6oVrmRhySbBFcZoda\nq2JGK6RILRqVPZuP1to5LmoY3FoLQgsrej1HLD5bjd1Ibdy1TFAZiF+toEL2OdmYqI2Z1jmvRsQs\n+55GHXi9aKseDWatvKCsvWoBgyyKr4fNFUmp1T7fSMTZKN8BH8nzz2mmwKJph0qQGEpwt5vtpd3O\nlTB9Yt/U8pWEZauX1qDfIaYeXia5HdFozRdrNqO7u5u1QVZNJdvJSWK6VkEEzzNArDxaqldIcqMW\nFldLQQGpdNLtuslkUtzmi7IvovQLj0rQInPMH+0Jlyg6EPo5lW5S2oFXAKXvbmQhEyaSiiYIyF8P\naF+pVFjJpyhSJ8ox0/Novtdb4+Qc+X7Joj/+fdMYthurTpsCXxQg9vlcHSoPbHU6nQgEApibm8PQ\n0BC6urraHn21y+g4mc/nMT09DZ/Px6Rv+YVHAmBDQ0O4ceMGTk9P6zpHvvTS5/NhbGwMLper4R22\nGXO73ewC4vDwkE36eg6VHDFJVIsTkSA4o6OjuHbtGnPAJpOpbuRxdnYGu92OkZERxvXaSB7xypUr\nWFhYYHA1s9nMCF/Gx8fZTbPMIZGC58LCgiY6Nt6hTk1NIRAIwGazST9ns9kwNjaGYDDIAOx0U01K\nti6Xi42rnkVtMpnYGuzt7UWxWKzrmHj40dWrV6sIa/g17vF4cPXqVWQyGaRSKaamW8+hlstljI2N\nYXBwkKm9ipsM7z+Gh4c1PbtVDnVqagput1uVb7XlAVtF0is+gVwsFhVsL4VCoWVR10XmUcvlMpxO\nJ65cuQKv14u+vj5F5EEkyeFwGBsbG1IeyFpHs56eHsY05ff7G87J6Mnx8ba7u4tQKIRMJsNuhLUc\n92kRTE9PY2xsjNEiijjUvb09HBwc4Pj4WDP5LkXAgUAAExMTsNvtCoiNrP5evEnP5XLY3NzE9va2\nAjZFR2G/349AIIDBwUH09PQovr9QKOD4+BgbGxuIRqOa5zGtB7fbDY/HgytXrjD5a74mPp1Os2fT\n5RS1raOjAyMjIwwAX4swRya8WCgUsLGxgUgkwnDVWrSYiJilr6+PUVHywP6Ojg6cnJwgGo0iGo2y\nG3ktY0PPdzgcmJychM/nY5dm9Oxyucz8x6dPn1AsFs+NLKlSqcDlcmF6epoVHbQ7QpU6VDHHSGWG\nrai4uUxOlY6PsvIyvvRUL0myqOgo8je2w6GKRu1uVCLGarVK0xw0H4gAhWcX0xpl8uWbtXKasnbT\njbLsnfB157K6drqB5pUM9Iwxn/6RORyx9FT8fWqXrG31+l2pVFAoFHTXlvOnJ7H0lB8X/p02cnEr\nlp6q+Y/zxGtTv/m2tWsd6nKo7UiwX5Z8qh72oEZynrKd8DwcKk9G0Uj765G+NDMutQTvtFx01tok\nar3TZtEIWqKbem0TL0n09rveZ2q1XS2i1SIlflHrqJ1r/EIcqmHtecntdqj/hrH5L83D/2q//y3r\nkMz8X124Wga22T5fhjLcdvXhosamWVLhdrZby7ObnRMX3f6LevZldJ5GhGpEqEakZvT73Pt1Wftz\nbkd+wwwzzDDD9FunMQSGGWaYYYZDNcwwwwwzHKphhhlmmOFQDTPMMMMMMxyqYYYZZpjhUA0zzDDD\nDIdqmGGGGWY4VMMMM8wwwxqw/wMzOs1Xer8ihAAAAABJRU5ErkJggg==")) image_1: pin names not known
  // Hyperlink #(.background("#4bdd32"), .href("#Floating Buses")) hyperlink_1: pin names not known
  // Hyperlink #(.href("https://wikipedia.org")) hyperlink_2: pin names not known

  // Notes on the sheet:
  //   NOT Gate
  //   A NOT gate by default emits the complement of whatever input it receives. So it outputs a 1 when the input
  //   is 0, and it outputs a 0 when the input is 1.
  //   If the input is not connected, or has an error (E) or floating (X) value, then the output will be an error. This default
  //   behavior can be summarized with the truth table above.
  //   Multi-bit NOT Gate
  //   A multi-bit NOT gate performs the same transformation as a bitwise operation, with each output bit
  //   determined by the corresponding input bit.
  //   High-impedance Output Modes
  //   Instead of the default behavior described above, a NOT gate can be configured in special high-impedance output modes:
  //   * If the output behavior is set to "0/floating", it behaves in "open-collector" (a.k.a. "open-drain") inverter mode, 
  //   where output is either 0 (when the input is 1) or floating (when the input is 0). 
  //   * If the output behavior is set to "floating/1", the output is either floating (when the input is 1) or 0 (when the input is 1).
  //   When combined with pull-up or pull-down resistors, these modes can be used to create a circuit similar to a "wired-AND"
  //   or "wired-OR". See example circuits below.
  //   NOT Gate Attributes
  //   Facing - Used to rotate the gate. You can also rotate the gate using arrow keys (up/down/left/right).
  //   Data Bits - The width, in bits, of the gate's input and output.
  //   Gate Size - Used to select a wide or narrow symbol.
  //   Output Value - Configures the output behavior. Mode "0/1" is the traditional behavior, with the NOT gate outputing
  //   either 0 or 1, depending on the input. Mode "0/floating" is open-collector (aka open-drain) behavior, so the NOT gate
  //   either outputs 0 or leaves the output floating. Mode "floating/1" makes the NOT gate leave the output floating or output a 1.
  //   Label - A label to appear above the gate.
  //   Label Font - Font for the label.
  //   Example Circuits
  //   input
  //   0
  //   1
  //   other
  //   output
  //   floating
  //   0
  //   error
  //   "
  //   Output behavior as 0/floating
  //   input
  //   0
  //   1
  //   other
  //   output
  //   1
  //   0
  //   error
  //   input
  //   0
  //   1
  //   other
  //   Output behavior as floating/1
  //   output
  //   1
  //   floating
  //   error
  //   Transient Pulse Generator
  //   Link test
  //   Maybe go to [wikipedia](https://en.wikipedia.org/wiki/List_of_7400-series_integrated_circuits) to see stuff?
  //   Or try [this page](http://sneaindia.com/Admin_index.php?id=21&f=Technical) fro sneaindia.com
  //   Or go to the [floating bus example](#Floating Buses) circuit
  //   Alt link to the [floating bus example](logisim:///live/help.circ#Floating Buses) circuit
  //   Or a doc [page](/libs/wiring/pin.html) link for pin
endmodule

module Common_Gates___Basics (
  input  A,
  input  X,
  input  in_3,
  input  B,
  input  Y,
  input  in_6,
  input  P,
  input  in_8,
  input  in_9,
  input  Q,
  input  in_11,
  input  in_12,
  input  A_2,
  input  [7:0] P_2,
  input  B_2,
  input  [7:0] Q_2,
  input  C,
  input  [7:0] R,
  input  D,
  input  E,
  input  [4:0] in_21,
  input  [4:0] in_22,
  input  in_23,
  input  in_24,
  input  in_25,
  input  in_26,
  output C_2,
  output V,
  output out_29,
  output R_2,
  output out_31,
  output out_32,
  output out,
  output [7:0] out_2,
  output out_35,
  output out_36,
  output out_37,
  output out_38
);

  wire callout_5_p1, medium_out, not_1_out, not_2_out, wide_out;

  and and_1 (C_2, A, B);
  // Callout #(.background("#b7e1eb71"), .dx(-15), .dy(-20), .foreground("#185fba"), .halign("center"), .style("margin: 4px;"), .text("2-input\nAND gate"), .valign("top")) callout_1: pin names not known
  nand nand_1 (R_2, P, Q);
  // Callout #(.background("#b7e1eb71"), .dx(-15), .dy(-20), .foreground("#236494"), .halign("center"), .style("margin: 4px;"), .text("2-input\nNAND gate"), .valign("top")) callout_2: pin names not known
  or or_1 (out, A_2, B_2, C, D, E);
  // Callout #(.background("#b7e1eb71"), .dx(-15), .dy(-20), .foreground("#236494"), .halign("center"), .style("margin: 4px;"), .text("5-input\nOR gate"), .valign("top")) callout_3: pin names not known
  or or_2 (out_36, in_23, in_26);
  // Callout #(.background("#b7e1eb71"), .dx(20), .dy(-20), .foreground("#236494"), .halign("center"), .style("margin: 4px;"), .text("Unconnected\ninputs are ignored"), .valign("top")) callout_4: pin names not known
  not not_1 (not_1_out, in_22[0]);
  not not_2 (not_2_out, in_22[2]);
  // Probe on callout_5_p1
  // Callout #(.background("#b7e1eb71"), .dx(20), .dy(-20), .foreground("#236494"), .halign("center"), .style("margin: 4px;"), .text("Floating input causes\nerror, unless a result\ncan be determined\nfrom remaining inputs"), .valign("top")) callout_5: pin names not known; wires that end beside it: callout_5_p1
  // XOR_Gate xor_1 has open pins: out=out_38
  or or_3 (V, X, Y);
  // Callout #(.background("#b7e1eb71"), .dx(-15), .dy(-20), .foreground("#236494"), .halign("center"), .style("margin: 4px;"), .text("2-input\nOR gate"), .valign("top")) callout_6: pin names not known
  nor nor_1 (out_31, in_8, in_11);
  // Callout #(.background("#b7e1eb71"), .dx(-15), .dy(-20), .foreground("#236494"), .halign("center"), .style("margin: 4px;"), .text("2-input\nNOR gate"), .valign("top")) callout_7: pin names not known
  // Callout #(.background("#b7e1eb71"), .dx(-20), .dy(-19), .foreground("#236494"), .format("wrapped"), .halign("center"), .style("p-margin: 0px;"), .text("Each output bit is the result of ANDing the corresponding input bits."), .textwidth(228), .valign("base")) callout_8: pin names not known
  and wide (wide_out, not_1_out, in_22[1], not_2_out, in_22[3], in_22[4]);
  LED led_1 (.in(wide_out));
  // Callout #(.background("#b7e1eb71"), .dx(-15), .dy(-20), .foreground("#236494"), .halign("center"), .style("margin: 4px;"), .text("Both circuits work the same: the LED\nturns on only when  the input is 11010."), .valign("top")) callout_9: pin names not known
  or or_4 (out_37, in_24, callout_5_p1);
  // Callout #(.background("#b7e1eb71"), .dx(-13), .dy(-16), .foreground("#236494"), .halign("center"), .style("margin: 4px;"), .text("If no inputs, then error output"), .valign("top")) callout_10: pin names not known
  // Callout #(.background("#b7e1eb71"), .dx(20), .dy(-20), .foreground("#236494"), .halign("center"), .style("margin: 4px;"), .text("Same for \nerror inputs"), .valign("top")) callout_11: pin names not known
  xor xor_2 (out_29, in_3, in_6);
  // Callout #(.background("#b7e1eb71"), .dx(-15), .dy(-20), .foreground("#236494"), .halign("center"), .style("margin: 4px;"), .text("2-input\nXOR gate"), .valign("top")) callout_12: pin names not known
  xnor xnor_1 (out_32, in_9, in_12);
  // Callout #(.background("#b7e1eb71"), .dx(-15), .dy(-20), .foreground("#236494"), .halign("center"), .style("margin: 4px;"), .text("2-input\nXNOR gate"), .valign("top")) callout_13: pin names not known
  // Callout #(.background("#b7e1eb71"), .dx(-15), .dy(24), .foreground("#236494"), .format("wrapped"), .style("p-margin: 0px;"), .text("8-bit 3-input AND gate"), .textwidth(88), .valign("base")) callout_14: pin names not known
  assign out_2 = P_2 & Q_2 & R;  // AND_Gate and_2, 8 bits wide
  and \medium  (medium_out, in_21[4], in_21[3], ~in_21[2], in_21[1], ~in_21[0]);  // AND_Gate
  LED led_2 (.in(medium_out));
  and and_3 (out_35, out_37, in_25);

  // Notes on the sheet:
  //   # Common Gates - Basics
  //   The common logic gates are: AND, OR, NAND, NOR, XOR, XNOR.
  //   Each one takes several inputs, combines these using the rules of Boolean logic, and outputs the result.
  //   See also: [Advanced Features](#Common Gates - Advanced) and [Online Documentation & Reference](/libs/gates/common.html)
  //   ### Gate Behavior with 2 Inputs
  //    A | B || AND | NAND | OR | NOR | XOR | XNOR
  //   ---|---||-----|------|----|-----|-----|------
  //    0 | 0 ||  0  |  1   |  0 |  1  |  0  |   1
  //    0 | 1 ||  0  |  1   |  1 |  0  |  1  |   0
  //    1 | 0 ||  0  |  1   |  1 |  0  |  1  |   0
  //    1 | 1 ||  1  |  0   |  1 |  0  |  0  |   1
  //   ## Multiple Inputs and Multi-Bit Gates
  //   Use the ***number of inputs*** attribute to allow more than two inputs. All inputs are combined using the usual rules of Boolean logic to produce a single output result. Use the *data bits* attribute to allow a gate to operate on multiple bits simultaneously.
  //   **Keyboard shortcut** 👉To change the *number of inputs* for a gate, select it and type a number. Or select several gates to change them all.
  //   **Keyboard shortcut** 👉To change the *data bits*, select some gates, hold the option key (⌥) or Alt key, and type a number.
  //   ## Visuals
  //   The ***gate size*** attribute allows a choice of *narrow*, *medium*, or *wide*. Gates can be rotated to face any direction using the ***facing*** attribute. A gate can be given a ***label***, which will follow the gate if it is moved or copied.
  //   **Keyboard shortcut** 👉Select some gates, then use arrow keys (↑→↓←) to rotate them so they face a different direction.
  //   ## Negated Inputs
  //   Any of the inputs can be configured to be active-low. This behaves exactly as if there were a NOT gate attached to that input, but used judiciously, negated inputs can make circuits more compact and easier to undertand.
  //   ## XOR & XNOR Multiple-Input Behavior
  //   Multi-input XOR and XNOR gates can be confusing. Normally, XOR outputs a 1 when an *odd number of inputs* are 1, and XNOR does the opposite. This "parity" behavior is most typical. For XOR and XNOR gates with more than two inputs, the ***multiple-input behavior*** attribute allows for a different, less common behavior, where XOR outputs a 1 when *exactly one input* is a 1, and XNOR does the opposite. 
  //   **Suggestion** 👉 Don't use multi-input XOR and XNOR gates. For parity calculations, use the ***Even Parity*** or ***Odd Parity*** gates instead. For *exactly-one* calculations, which are less common, consider building a circuit from a ***Bit Adder*** and a ***Comparator*** (found under ***Arithmetic***).
  //   ## Errors, Unconnected, and Floating Inputs
  //   * As a convenience, any input left unconnected is ignored: if there is no wire or other connection to the input, the simulator acts as if the input did not exist at all. So a 5-input gate with only two inputs connected behaves just like a 2-input gate. This doesn't match physical circuits or more realistic simulators, where such inputs would be considered *floating*, but it makes editing a circuit a little more forgiving. 
  //   * If all inputs are unconnected, the output is an error. 
  //   * If only one input is connected, the behavior depends on the gate type.
  //   * If some inputs are errors, a gate's output is calculated from the remaining inputs, but only the output would be unchanged even if the errors were replaced by any combination of 0 and 1 values. For example, for an AND gate, if any input is 0, then the output is 0, even if some inputs are errors. Similarly, for an OR gate, if any input is 1, then the output is 1, regardless of other inputs.
  //   To enable a more strict simulation behavior, treating unconnected inputs as floating values, go to ***Project > Options > Simulation***.
  //   Note: See below for behavior when some inputs are floating (z), errors (e), or unconnected.
endmodule

module Common_Gates___Advanced (
  input  [1:0] in_1,
  input  in_2,
  input  in_3,
  input  in_4,
  input  in_5,
  input  in_6,
  input  in_7,
  input  in_8,
  input  in_9,
  output out_10,
  output out_11,
  output out_12
);

  wire or_1_out;

  and and_1 (out_10, in_1[0], in_1[1]);
  or or_1 (or_1_out, in_2, in_4);
  and and_2 (or_1_out, in_3, in_5);
  xor xor_1 (or_1_out, in_6, in_8);
  and and_3 (or_1_out, in_7, in_9);
  Pull_Resistor pull_resistor_1 (.node(or_1_out));
  // Image #(.image("PNG:\niVBORw0KGgoAAAANSUhEUgAAAdUAAADOCAYAAABo35gbAAAfOElEQVR4Xu2dwaolx5GGT6O1NjbM\nwmhphFEPCNvyakBCIPAYZuEH0NIPICG88KKlplcSWozxGBk/gMEIP4RsELRhYGaMvTPGe7+D7yhO\nK6TsuJlVUZl/ZmTW+T8IuvvcvJEVf0dFVmZV5bncEUIIIQTCxX5ACCGEkDo4qBJCCCEgOKgSQggh\nIDioEkKW5tNPP737+Se/sR/f48mTJ1+Z/A55BvXDsjmoXi6XIfa917579/7jR1/Z06ef20OZAjmu\nreNWe/e9d+yv3gT2/7WXWd1nzRcvzKs2VLe9Qm/zKGcPH75+HTRkkNnzdxaoH5YpBtWSSXGZrZDI\nMdnj3LOPPv7wJoqijXu0zZgvXphX9UgRFz3efvtn9kfPIQVftZO2Vs8tk9/1zOZWhPphcQ2qvZEr\n9fSKPFdg5LM//+VP9leHo7OKt95843o8djYhJsXOHr+N5QwzLAvzpR7mVRuqwd7saK+dfK4zrXQQ\nsXa2mdieLspeu1vVL2WzAqoAUcgVuC2YUjSi0WPxFm2Jo1T8xaRYnqEQMl/aYF7VowV8b7alszJp\nfwS9l2g1Vl+rDxDUD0e2Av7P/93d/fIXd3cv/cv/3r3w4Fv2xyFI8Uj/IyKKZarL5cHDazGTz44i\nha4064iIqxXmSxvMq3qkGL/yyj+/MolVivcWqkltIdfZmF0C1fuJK0H98GQHVTnBX3jp7u7Vbz/7\ncxbkCj69Kn/5Oy/bJl1Jdfm3f32WgP/1n/9tmx1ClzLtbGOlWQbzpQ3mVT1SmO2gsDeL8t5D9CJL\nmanGYtJH7aAzEuqHJzuo/vBHz07w2YqkIsVSxR957yzVRUz7RyHFzhZB+ffsRZD50gbzqh4pyHZQ\nENvD2+4IMgjY2Zf8e+bBgfrhyaoiS09SHPWqeVZk5qHijyiUqovY737rT8Aa7PLljIOBwnxpg3nV\nRvrQi94b3FtG9LarQY7Fzr569IOC+mHZPHN7ntwoIgulXv33fKXBFsGZ740xXzAwr+rRYuxdwtxr\n14r2ozb74ED92tmsgBrI7KSFciRS9KRP5FJdiTRGsRkHhIj/gxqi8sUL86oN7/+tt10rdllz9qdd\nvbp427WynH72g5RRoiHQ4jD6YZSRGtl7Y6Nj3WOkFq1E5YuXkVrOnldH8S5NetuhsIPDqH6P4tXF\n2w7FKvptnrUjT2wEEUVhxFKdJX3wRmyW2QXzBQfzqh7v0qS3HZp0SXPGWZdXF287NLPrt1kBVyuS\naVEY9WTjyKU6S7p0N8M9MeYLDuZVG95c9LZDY2dd0w0MTl287dDMrN+mGlGCtaAPYIwsRpE6pQ+c\nRM+4InWoJSJfvETqOVNeebBF1bs06W3XC+1fDPXeZw3UD0f2jJ1xh5wjqMjo2YfqIu8Vyp9i6SsQ\nNbvgIIhetmO+tMG8qkcGg/Q9S/u+5V6x16XEvXY9kRj0eEcvpVI/PNlBddYdcrz0mn2kuqT24uWn\n1/6il8rSZbuRBZD50gbzqh67I5CadwY1w6AgpMuZIwcG6ocnO6jOvkOOBy0CyNmH3flmtuInRBRA\n5ksbzKt6SjOtdLa1h7fdCEbfJ6R+eLJKrLJDzha6sbj8iSLd+UaX6cRkn1bpK2qmY0mX7UYUQOZL\nG8yrNkpfI+Yt9t52o0jvE+biQkP9sGwqMZtYR5AZx8jjH9mXh7QAjnrQZDYNjjA6X7zMdkwReVWL\nFte9wuptN5IZZlxeXbztRhKp3+bZOtsJfZSRxz+yLy+jC+CMGhxhxuOf8ZhG51Uter9PZmJbeNuN\nJnrG5dXF2240Ufptnq0zntBH0CW9ES/Q68v6EffktkgLYO97c8wXPMyrerwP0XjbRZDOuEbj1cXb\nLoIj+qGOf7Mn78HMij7VOeKkH9nXUUbdCztjvsgAm95vHT3g5o5pFjx5Famft9h720WhM67RT7V6\ndfG2i2JLP5nBag6n1hLLZgXUDlZF75ONeNBj5uIneApgK2fKF9Eo3Q/XWi8NLavmld1P2NoI/bzF\n3tsukojXRby6eNtFktPPfr1culxs2x5hswKq85UZFcPsxU/QYxTrUdRGad0TjeGtN9/46u8ywxK9\nUv1GxblqXqUD6gj9cvfMvMXe2y6SdEYlA0Qu3hZy/ry6eNtFktNP/22PW+MRy+myRzazV98hR/nH\n3/569+MHl7vff/Mb17+3ktv5Ru0//v2D63/CzMVPkAdLXv9CE9Hlj9//AVSX1fNFSIu+WA7Vj3n1\nNel7rL/69SfD9JOiZ9+vtO9a7s04tMDutYtGj1NjQ2zL59FPbOshpNX0E8vNXFNSXY7qnM16OZlX\n3iFH+fsHj+7+8IVwaq2kulib6UX9PX6SaILWZeV8EfSkEyu9s8q8ymOXe0foV9oRyA4Ke3jbRWPj\nbcX6s6a67M3YVtHPLvGWLhasLkfIqnCGHXIEuRJGnbxCaeeb1YofelA9S74I6QlXWiJnXuWxg+oI\n/bwzrT287SKZdaYqrKSf2N67tfCZ6hl2yBFkaUlP3NZlJqG0881Ky3T6YEkPXVbPF0FPuq3/S5mB\n9dDvDHklpvejS8eM1q+0I5D3Xp+3XSQSXzoQ7A1yR7gV/TQ/VT/5e2nATO+rHmXzN2qdzsSoGFZ4\noKT0pCaKUVr3RGPYikVnZCM2Plgxr/S7YKP18xZ7b7so0gFh5DF6dfG2iyLVTy9G7CBbal8TUz7r\nv2TrxFiFUTHMXvzSwtfrGEdp3RONQU0GAN14wb4m0uPCxLJqXs2gn7fYe9tFoXqVHqrphVcXb7so\nVD87K03vr8rP5PjtZzVsVkB1vip6xVx6YALJzMUvLXw9ZwdnypdUs5z1HhCUVfNqBv28xd7bLgIt\n8rUFvgWvLt52Eew95avHbq3U3sNmBdQOVkV3chlRkGbc4k4Ztdx2xnzRQU1NN4YYxep5Famft9h7\n241GB9SWAt+CVxdvu9Ec0U+OXc0uBx9lswLqibAqevwj9k2dUautmUQPZtTgCCPzxcuMmo7Oq1q8\nxd7bbiQ6w4qYoSpeXbztRrI3Q+3J5tk64wl9hJHHP7IvDxGFbzYNjjLj8c92TBF55SE3u/Bq5203\ngvQp35EDAvXDkVXiDDvk9LifWtr5Rr9MepbEGl34mC9tMK/qkSJq362071ju4W3Xm/Sp01EDwln1\ni5zhZ5WQE3r1HXL0fg9yKS/VJfeCfkRBtkQUPuZLG8yreuzON3ZQ2BuctBDvtetNOsMaOSCcUb/o\nY8kOqqvvkKPfNiKGpLTzzSy73qQPhYwsfMyXNphX9ZRmWnq8e/f5dBOAvXY90XuSEQMC9cOTrSKr\n75Cjsw50McrtfPO7336h0YOH1/4iZjmKFDtNLHTcezBf2mBetZHbEcj78Iy3XS90dhV5DNQPy2YF\n1INdCb2qlkI5ikid7PuAo15XyBGpQy0R+eIlUs+Z8qoGr3bedmjS+39idlCLxquLtx2amfXbVCNK\nsBb0mEdd3esDLhFFebZlOeYLDuZVPWnB3cLbDk26XDny/qkXry7edmhm129TjQjBWtClqpGFIOrl\n/BmX5ZgvOJhX9Xjv841eurSzq1H9HoX6tbFZAVcqkmkxGMnoPu0ONTMty43WooWofPEy+thmzquj\naAx7S4Ledq2If92MQEz+3rvPFry6eNu1spx+9oMUDWJ20vs/I4uBPjU6YonO3uOacXbFfMHAvKrH\nuyTpbddK+iCN2MyDgeDVxduuldX0EzYVGSFaK5EFcsQSnf1mD/n7bPf/FOYLBubVcbTYepckvUuc\ntaT3/Xr2g4L64chWwFV2yEmX8EYUyHTnm+srD1/23QNb9EbFWAPzpQ3mVT0yGOTer9yb0XjbHUF8\n2ZnV7EuV1A9P9sxdYYeciAJpd76RvtFLdPbeltjsD4wwX9pgXtVjdwTSQryFzoL22nkRf3YwkM9W\nGAyoH57soDrzDjm2OIwskKkuutGB7M/aiswedMkvtVWKHvOlDeZVPbmZ1t5SoerQUrRl+dMOBJ6+\nZ4P64ckOqjPukGOXrSIeqFBdroPHg29dj0M+q0Hul+UK3or3tpgvbTCv2pACrU+H7m1Tp7OsvXY5\ncjMqsRWXKFOoH5bNCqhBRyJFYrYHKvR4jlzxyzFLe3s/S00KYXRcrTBf2mBe1aPx7hVnTzv5mQwA\npdmUmHx+hlmV4tFF8LS7Rf1SNiugCjCS0pW22JFi0wspUFu6yPHLcW4VOjH5Wc+nOyPY0qUXs+eL\nF+ZVPd57fGmBl4Ivv6dWKv6pSbutwWRVqB+W/Bn8JVaUCJvtSnuroG2Z/J4UxJliQWNjjrDZ8sUL\n86oe1WKvYFvttkxnWns+zwD1wzLdoCpFcdYikc4mSqbHP2sMPbFajLCZ88UL86oNnSntoe3sLOtW\ni79C/bBsDqqEEEII8cNBlRBCCAHBQZUQQggBwUGVEEIIAcFBlRBCCAHBQZUQQggBwUGVEEIIAcFB\nlRBCCAHBQZUQQggBwUGVEEIIAcFBlRBCCAHBQZUQQggBwUGVEEIIAcFBlRBCCAHBQZUQQggBwUGV\nEEIIAcFBlRBCCAHBQZUQQggBwUGVEEIIAcFBlRBCCAFRHFTffe+du/cfPzqFSSwoqEse6tIG9avn\nyZMnN2korN9bsV4UB9XL5XIqQ2H9rm4orN/VbTS2/9VtJLbvWzEU1u+tWC+KnrXjjz7+8N6V6Com\nx44WkLrkoS5tUL96tE87EzmroTWmfliKnnt3PAp0HGh/UaDjQPuLIiqOqH7RRMQR0Wck6HjR/man\nd7xFz9eOHzy0Hy8HWkDqkoe6tEH96onoMxJ0vGh/s9M73qznX/7i7u7Vbz+zH/7I/nQtkAJSlzzU\npQ3qV8+nn35698or/7za22//zP74lCA1pn54sp7lxNaT/IWX7E8xyBOCI54SRAo4QpccT59+fjUk\nq+myYr54GaFfjtnzyoMMBDooiI1CBqOff/Ib+/EQkBpTPzxZz72vnF/+zsvPWU+QAvbQZa+oyUDy\nvde+e30QBMnsuqSsmi9eeuh3hrzyIIV59ExrxMMuWyD7pn54ip5fvPz0aj1IA+oZnIAWEK2LDBJy\nfKXitkrxQ+uSsnK+eEHrd5a88hDRpxDRp4COF+3PS0SfQu94i557dpzOOv78lz91WYZS0HGg/SlS\n3MSvaGK10FcWkKDjQPtLWTlfvPTqd/W88hDRpxDRp4COF+3PS0SfQu94i557dixXyfJOmy7l9bxf\nho4D7S9FNJHZg/W/QvFD+0tZOV+89Ox35bzyENGnENGngI4X7c9LRJ9C73iLnnt1LFfLWhBl1iF9\n/OrXnyxTJNH+RA+dTcifdjYhrFD80P6U1fPFC7rfs+SVh4g+hYg+BXS8aH9eIvoUesdb9NyrY511\nKP/421+v/cifPUDH0cPf3gCxQvFD+1NWzxcv6H7PklceIvoUIvoU0PGi/XmJ6FPoHW/Rc6+O5YpZ\n/Op2bLKkJzMP+UxmImjQcaD9aWGTApj+XZG/y9Kd2F6RPAI6DrQ/ZfV88YLu9yx55SGiTyGiTwEd\nL9qfl4g+hd7xFj1fO+64w4ucyGK6LJUu8yFBC4jWJS16peKX+7yV2XWxrJovXtD6nSWvPIzuU9+x\nlD7l9RD590jQ8aL97XE2/SxZzz3em4sCKSB1yUNd2qB+9UTsCCR96ubsMjisPChQPzxZz1E7vPQA\nKSB1yUNd2qB+9UTtCBQJUmPqhyfrmVfOeahLHurSBvWrJ2JHoGiQGlM/PEXP6B1eokALSF3yUJc2\nqF89EX1Ggo4X7W92esdb9Ny741Gg40D7iwIdB9pfFFFxRPWLJiKOiD4jQceL9jc7veMteu7d8SjQ\ncaD9RYGOA+0viqg4ovpFExFHRJ+RoONF+5ud3vEWPffueBToOND+okDHgfYXRSkO5GsnOUr9rkYp\njp76lfo8K+h40f5mpxSvPI2M4L7nLyl1vBroOND+okDHgfYXRRqHbotoTd7tREP96jmLdl7Q8aL9\nzU4ar7zOY/NTrGWALSp5FqHRcaD9RYGOA+0vCo1Dd21Se+vNN577N/p7XalfPWfRzgs6XrS/2dF4\ndQMKtYcPX7/37xqKSl4dA3d4iQKdMNQlz9l0UbOzKvm3/gy5/zD1qwedy7ODjhftb3ZsjtpZaeuX\nqGd/6yzvzf39g0d3f/hCGLHff/Mb9seHoS55zqKLkJ5ssi9uDupXZrR+ETsCRYKOF+1vBdIcLc1G\nW97fzQ6qZ9nhRU5YPXnFWqEuec6ii5CecHaWpVC/MqP1u7UdgdDxov2tQJqjMnjmaNElm9FnuXJG\nXhEL1CXPWXQR0hOu9C041K/MaP1aZhQrgo4X7W8F0hwt7Tvcokt2UBXOssPLjx9croaCuuQ5iy7p\nCVdavpSvofvJFz9/nfrdI0I/7e9WQMeL9jc7aY6WBsyW+6rF36h1OBvoOND+okDHgfYXRXrCidnZ\nVvqaSGl5swbqV89ZtPOCjhftb3ZsjtrZavqajX2IyUNRybMIjY4D7S8KdBxof1FoHOkrIDLjktmV\n/KmfIV8JEahfPWfRzgs6XrS/2dF401doZMYqA6j9rIaikmcRGh0H2l8U6DjQ/qJI40hf/0gNOSAo\n1K+es2jnBR0v2t/spPGmy7yplZ4K9lBU8ixCo+NA+4sCHQfaXxS5OGSLPRkgxJ4+/fy5n6HI9bsi\nuTh665fr88yg40X7m51cvPql6WJ2OfgoRSVzHa8IOg60vyjQcaD9RREVR1S/aCLiiOgzEnS8aH+z\n0zveoudrxyfa4QUFdclDXdqgfvVE9BkJOl60v9npHW/W8xnfm0NAXfJQlzaoXz23vCMQAuqHJ+v5\njDu8IKAueahLG9Svnpadb1YFqTH1w5P1zCvnPNQlD3Vpg/rV07LzzaogNaZ+eIqez7bDCwrqkoe6\ntEH96onoMxJ0vGh/s9M73qLn3h2PAh0H2l8U6DjQ/qKIiiOqXzQRcUT0GQk6XrS/2ekdb9Fz745H\ngY4D7S8KdBxof1FExRHVL5qIOCL6jAQdL9rf7PSOt+i5d8ejQMeB9hcFOg60vyii4ojqF01EHBF9\nRoKOF+1vdnrHW/Tcu+NRoONA+4sCHQfaXxRRcUT1iyYijog+I0HHi/Y3O73jLXru3fEo0HGg/UWB\njgPtL4qoOKL6RRMRR0SfkaDjRfubnd7xFj1fO+YOL/egLnmoSxvUr56IPiNBx4v2Nzu948165ntz\neahLHurSBvWrhzsCtUH98GQ9c4eXPNQlD3Vpg/rVwx2B2qB+eLKeeeWch7rkoS5tUL96uCNQG9QP\nT9Ezd3jJQ13yUJc2qF89EX1Ggo4X7W92esdb9Ny741Gg40D7iwIdB9pfFFFxRPWLJiKOiD4jQceL\n9jc7veMtetaOP/r4w7v3Hz9a0uTY0QJSlzzUpQ3qV4/2+eTJk5swtMbUD0vRs3Z8FkNh/a5uKKzf\n1W00tv/VbSS271sxFNbvrVgvip7ffe+de1eiq5rEgoK65KEubVC/euxM5FYMhfV7K9aL4qBKCCGE\nkGNwUCWEEEJAcFAlhBBCQHBQJYQQQkBwUCWEEEJAcFAlhBBCQHBQJYQQQkBwUCWEEEJAcFAlhBBC\nQHBQJYQQQkBwUCWEEEJAcFAlhBBCQHBQJYQQQkBwUCWEEEJAcFAlhBBCQHBQJYQQQkBwUCWEEEJA\ncFAlhBBCQBQH1Xffe+fu/ceP7p4+/dz+6KahLnmoSxvUj5BzUBxUL5dL1r732ndv+uS3elCXZ1g9\nqMsxrG7Uz49qRcgMFDNRE/WtN9+4d6Kn9tHHH97UCU9d8lCXNqhfPVaj1Mg+1ApLUcmS0HJCy4lt\nk/fl77xsm54S6pKHurRB/eqx2uwZeR6rD7Vqo6jaVdQHD+3Hz5E74WWp6sx4dPnzX/5EXTLcYr54\n8eh3i3nlQbXIkWqVGvkaq82ekW2yCv3yF3d3r377mf3wR/aneeTKORVeCsDZsLpIQduyX/36k3sJ\necYiaHXxcAv54sXqZ/PI2q3klZcjxd7qRrb1s3pttSXPyKojJ7ae5C+8ZH9aRmYi8mCFCn+2Qpnq\nImYTzWtn1oX5chzmVRuPHz++2hFS3W6dIzrYnCP3yapir5yPIlfNKvqZ7v1YXewMYs/Spbsz63KU\ns+aLF6ufzZs9O2teedABtXVgveUBolU78jxFRV68/PRqtchV8xlPdOqSh7q0Qf3qqRkUUm55gOBF\nCZ6iEgihzniiU5c81KUN6lcPQjv10epnRWoG1JRb1i5HUQWUSOmJfoZ7PtQlD3Vpg/rVg9JO/SB8\nrQQi5lvVLkdRAaRAZzrRqUse6tIG9asHqR3S1yqgYlY/CF8rU4weLU76CsXKoGOgLnnOoosXdKy3\npB86TrS/2UHGi/S1KsXoe4ijr0/IE4urQl3yUJc2qF89aO3UH9LnzKBjRftbjWLkV2F2dng5iryX\nuLrgPXRJl+tWpYcuZ8gXLz30O0NeeegRYw+fs4KOVf0hfa5ENmr73hySla+erS72fcFaW/09Q6sL\nkpXzxYvVz+ZHra2eV156FfBefmejR5w9fK5CNuraHXI8rDz7QO18s2erwXxpg3nVRq/4bkE7oVeM\nvfzOTjZie+WMRmcf8sXMK2F1sTODVtOv/VpdFzSr5osXq5/Ni1ZbNa+89CzePX3PQq8Y1W8P3zNT\njLZ1h5ct5OQWoaVYrgZ1yUNd2qB+9fQs3D19z0LPGHv6npVitL3F6O2/F72Pu7f/XvQ+7t7+o+kd\nX2//kdTEdqR9jf+V6BlfT9+zUoy2txi6pCf3zFaCuuShLm1Qv3pqtDvSvsb/SvSOr7f/2ShG2lsI\nudcj/uXPlaAueahLG9SvnhrtjrSv8b8SvePr7X82ipH2FkLv88hj/ytBXfL01kUHhdV08UL96ilp\np5/XmvVzVnrH19v/bBQjHSHEiD7QjDjmEX2g6XnMsomBPsEqJkuZZ3uSlfrVU6PdkfY1/leiFJ9+\nXmvWz61QjPQqBHiHF8sosf/xt7/aj6qhLnl66mJPVrXo+4PUrw2UfjXnS037o7+zCr1j6+1/NrKR\n2vfmeqFi//2DR13sj9//wd0fvvAv9vtvfsN2fxiri30fEGHpLjg2HpT11gWJLofnTGZcNrYR1ls/\nmxMtpg8o5ews+mk8R6hpf/R3VmFEbCP6mIVslD13yElRofUE622tjNr5Rs0efy9rpWe+pN+2kjMb\nS4S1MjqvUrOxRFgrGssRatqLfTaRobhcjut3lBF9zEI2Snvl3AsV2l7Jogx9RWx1sbMChHGm+jyi\nieph7SwzLaufzYkWu+WZqo33qOV8fTaZIbhc7seLRvuwx7+CHaX4Gz13eFEul/7/mXoio6AueXrq\nonpYi7wnSP3aQOpXc77UtD/6O7347FJX7EuUYrP5ctRyvj5b1I5QbH253BcGzYg+0Iw45hF9oOl5\nzDLjUv9q8tmZoH711GhX0/7o76zCiNhG9IHms8vxAVUo/kZvEfTbR1bbj5S65OmtizwpuqIuXqhf\nPTXa1bQ/+jurMCK2EX3MQjHK3iLo1fNqV8zUJQ91aYP61VOj3ZH2Nf5XYkR8I/qYhWKUvUXQByhW\newmduuShLm1Qv3pK2unntWb9nJXe8fX2PxvFSHsL0dt/L3ofd2//veh93L39R9M7vt7+I6mJ7Uj7\nGv8rUYpPP6816+dWKEZ6FaLTDi+r3jcUqEse6tIG9aunpmgfaV/jfyV6x9fb/2xkI7XvzaHRdzFX\nW4qyuth3AltN92ddXRc0q+aLF6ufzYtWWzWvvNQU7SPta/yvRO/4evufjWykPXfIEVYVedTON6vB\nfGmDedVGz/h6+p6F3jH29j8b2UjtlTMSuXIWgVdcirK62BlBi+ls4gy6IBFtVtXFi9XP5kaLrZxX\nXnoW7Z6+Z6FnjD19z0ox2h47vMhXUKnI8vcVoS55qEsb1K+eXoW7l9/Z6BlnT9+zUoy2hxj6WL9c\nQa8KdclDXdqgfvX00E59ov3OSK84e/mdnWLEaEHSq+aVQcdAXfKcRRcv6FhvSb8ecfbwOSs9YlWf\naL8rUIwYKciZlqGoSx7q0gb1qwepnYD2Nzs94u3hcxWKUSNFUV/y3ZirQ13yUJc2qF89PbRD+VsB\ndLxof6tRjBwljH7J9FlOcOqSh7q0Qf3qQWknIH2tAjJm9YXytyLFyK/CNOzwIstO+qDEmU5w6pKH\nurRB/epBFXGUn9VAxo30tSrZ6O17c0dJ7+mc6QS3uth3AvdMdwY6uy5HOWu+eLH62bzZs7PmlZfW\nQq6/3+pnVVBxo/ysTlaBlh1y5CQ/6wmO2vnmzLowX47DvGrj8ePHV6sh1e9WaY3f5uGtk1XAXjl7\nSGcbYlIsz4bVxc4YrMkMQne0uSVdPNxCvnix+tk8snYreeVBB9SjAysHgq85ql0KNbxPUQnvDi/y\nDRh6L0dM/n7mx/i9uqT3uKjL19xavnjx6ndreeXh6KDAgeBreFGCp6jGlljybRfpfRy1Wzi5qUse\n6tIG9atnS7sUqx95RsuASu5TVEVFk5NZl5xsUorJlfJZv1IqB3XJQ13aoH71qDa5z3JGnserC3X0\nUVTGCpjaLZ/YVgvq8gyrBXU5htWM+vmxepWM5MnpY7Wjjn6KCslJnD4cwZP6GdQlD3Vpg/rVY4s+\nC/8xrHYlIz6oFCGE3DB28OQA2gbVI4QQQkBwUCWEEEJAcFAlhBBCQHBQJYQQQkD8P7DZZVW9I2vY\nAAAAAElFTkSuQmCC"), .xscale(0.8), .yscale(0.8)) image_1: pin names not known
  // Callout #(.background("#b7e1eb71"), .dx(10), .dy(-10), .foreground("#236494"), .halign("right"), .style("margin: 4px;"), .text("ANSI/IEEE\n91a-1991"), .valign("bottom-overall")) callout_1: pin names not known
  // Callout #(.background("#b7e1eb71"), .dx(10), .dy(-10), .foreground("#236494"), .halign("right"), .style("margin: 4px;"), .text("IEC 60617-12"), .valign("bottom-overall")) callout_2: pin names not known
  // Callout #(.background("#b7e1eb71"), .dx(10), .dy(-10), .foreground("#236494"), .halign("right"), .style("margin: 4px;"), .text("DIN 40700"), .valign("bottom-overall")) callout_3: pin names not known
  // Callout #(.background("#b7e1eb71"), .dx(-20), .dy(-20), .foreground("#236494"), .format("wrapped"), .halign("right"), .style("p-margin: 0px;"), .text("push-pull output is always driving"), .textwidth(111), .valign("top")) callout_4: pin names not known
  // Callout #(.background("#b7e1eb71"), .dx(-15), .dy(-20), .foreground("#236494"), .format("wrapped"), .style("p-margin: 0px;"), .text("single bus wire with multiple device outputs"), .textwidth(267), .valign("base")) callout_5: pin names not known
  // Callout #(.background("#b7e1eb71"), .dx(-15), .dy(13), .foreground("#236494"), .format("wrapped"), .style("p-margin: 0px;"), .text("any of the four devices can drive the bus wire to 1, or even more than one of them at the same time"), .textwidth(216), .valign("base")) callout_6: pin names not known
  // Callout #(.background("#b7e1eb71"), .dx(-21), .dy(-16), .foreground("#236494"), .format("wrapped"), .style("p-margin: 0px;"), .text("pull-down resistor ensures the bus is pulled down to 0 if no output is driving to 1"), .textwidth(267), .valign("base")) callout_7: pin names not known
  and and_4 (out_11, in_1[0], in_1[1]);
  // Probe on or_1_out
  // Callout #(.background("#b7e1eb71"), .dx(-20), .dy(-20), .foreground("#236494"), .format("wrapped"), .halign("right"), .style("p-margin: 0px;"), .text("pull-down-only output is floating when not driving output low"), .textwidth(146), .valign("top")) callout_8: pin names not known
  and and_5 (out_12, in_1[0], in_1[1]);
  // Callout #(.background("#b7e1eb71"), .dx(-20), .dy(-20), .foreground("#236494"), .format("wrapped"), .halign("right"), .style("p-margin: 0px;"), .text("pull-up-only output is floating when not driving output high"), .textwidth(134), .valign("top")) callout_9: pin names not known

  // Notes on the sheet:
  //   # Common Gates - Advanced Features
  //   ## Output Driver Option
  //   Normally, gates use **push-pull** outputs: they actively output either 1 or 0 at all times, as long as the inputs are well defined. The ***Output Driver*** attribute allows for two other behaviors. 
  //   * With a **pull-up-only** output driver (equivalent to open-emitter/open-source) a gate can actively output 1, but instead of outputting 0 it will produce a floating (z) output. 
  //   * With **pull-down-only** output driver (equivalent to open-collector/open-drain), a gate can actively output 0, but instead of outputting 1 it will produce a floating (z) output. 
  //   This allows creation of *wired-OR* and *wired-AND* busses. ***Pull Resistor*** (found in the ***Analog*** library) can be useful for these too.
  //   ## Gate Appearance and International Standards
  //   Different standards bodies have adopted different symbols for  common gates. In **Logisim > Settings > International** you can choose from **ANSI/IEEE Standard 91a-1991** (curved, distinctive shapes commonly used in computer science textbooks and educational materials), **IEC 60617-12** (rectangular, uniform shapes often used in professional settings and engineering), and **DIN 40700** (an older, less common standard).
  //   or_1 drives only 1 and floats otherwise
  //   and_2 drives only 1 and floats otherwise
  //   xor_1 drives only 1 and floats otherwise
  //   and_3 drives only 1 and floats otherwise
  //   AND
  //   OR
  //   and_4 drives only 0 and floats otherwise
  //   NAND
  //   NOR
  //   XOR
  //   and_5 drives only 1 and floats otherwise
  //   XNOR
endmodule

module Common_Gates___Reference (
);


  // Notes on the sheet:
  //   # Common Gates - Reference
  //   ## Properties
  //   Common multiple-input logic gates, AND, OR, NAND, NOR, XOR, XNOR, support these properties:
  //   | Property      | Values                       | Notes
  //   |:--------      |:---------                    |:----------
  //   | Facing        | East, North, West, South     | Orientation of the output port.
  //   | Data Bits     | 1-32                         | Width of each input and output port. If set 
  //   +               |                              | to *N*, the gate outputs *N* values, with 
  //   +               |                              | each output value computed from the 
  //   +               |                              | corresponding bit of the input ports.
  //   | Gate Size     | Narrow, Medium, Wide         | Size of the gate symbol.
  //   | Number of     | 2-32                         | Up to 32 inputs are allowed.
  //   +    Inputs     |                              | Unconnected inputs are ignored.
  //   | Output Driver | 0/1 (push-pull),<br>         | Determines the set of possible output values,
  //   +               | 0/floating (pull-down-only), | in other words, if the output port is capable
  //   +               | <br>floating/1 (pull-up-only)| of actively driving high values, low values,
  //   +               |                              | or both.
  //   | Label         | any text                     | Text to be shown on top of the gate.
  //   | Label Font    | any font                     | Font to be used for the label.
  //   | Negate *i*    | Yes, No                      | Whether to invert the value of input port 
  //   +               |                              | *i*. Negated inputs are drawn with a "bubble"
  //   +               |                              | symbol at the port.
  //   | Multiple-Input| When an odd number are on,   | For XOR and XNOR gates with more than two 
  //   + Behavior      | <br>When one input is on     | inputs, chooses between parity-style 
  //   +               |                              | behavior and one-hot behavior.
  //   ## Keyboard Shortcuts
  //   + 👉Arrow keys (↑→↓←) change the *Facing* property for the selected gate or gates.
  //   + 👉Typing a number (2-32) changes the *Number of Inputs* property for the 
  //     selected gate or gates.
  //   + 👉Typing a number (1-32) while holding the option key (⌥) or Alt key changes the *Data Bits*
  //      property for the selected gate or gates.
  //   ## Behavior
  //   * **AND** Gate
  //     - Unconnected inputs are ignored.
  //     - If there are no connected inputs, outputs error (e).
  //     - Outputs 1 when *all* connected inputs are 1 (and there are some connected inputs).
  //     - Outputs 0 when *any* input is 0.
  //     - In all other cases, outputs error (e). This includes cases where some inputs are floating
  //       (z) or errors (e), unless some input is 0, in which case the above rule applies and the
  //       output is 0.
  //   * **NAND** Gate
  //     - Outputs 1, 0, or e, whenever AND would have outputted 0, 1, or e, respectively.
  //   * **OR** Gate
  //     - Unconnected inputs are ignored.
  //     - If there are no connected inputs, outputs error (e).
  //     - Outputs 1 when *any* input is 1.
  //     - Outputs 0 when *all* connected inputs are 0 (and there are some connected inputs).
  //     - In all other cases, outputs error (e). This includes cases where some inputs are floating
  //       (z) or errors (e), unless some input is 1, in which case the above rule applies and the
  //       output is 1.
  //   * **NOR** Gate
  //     - Outputs 1, 0, or e, whenever OR would have outputted 0, 1, or e, respectively.
  //   * **XOR** Gate with Multiple-Input Behavior set to "When an odd number are on"
  //     - Unconnected inputs are ignored.
  //     - If there are no connected inputs, outputs error (e).
  //     - Outputs 1 when an odd number of inputs are 1, and all other connected inputs
  //       are 0.
  //     - Outputs 0 when an even number of inputs are 1, and all other connected inputs
  //       are 0 (and there are some connected inputs).
  //     - In all other cases, outputs error (e). This includes all cases where some inputs are 
  //       floating (z) or errors (e).
  //   * **XOR** Gate with Multiple-Input Behavior set to "When one input is on"
  //     - Unconnected inputs are ignored.
  //     - If there are no connected inputs, outputs error (e).
  //     - Outputs 1 when exactly one input is 1, and all other connected inputs
  //       are 0.
  //     - Outputs 0 when either zero or more than two connected inputs are 1, and all
  //       other connected inputs are 0 (and there are some connected inputs).
  //     - In all other cases, outputs error (e). This includes all cases where some inputs are 
  //       floating (z) or errors (e).
  //   * **XNOR** Gate
  //     - Outputs 1, 0, or e, whenever XOR would have outputted 0, 1, or e, respectively.
endmodule

module Floating_Buses (
  input  A,
  input  X,
  input  in_3,
  input  B,
  input  Y,
  input  in_6,
  input  P,
  input  in_8,
  input  in_9,
  input  Q,
  input  in_11,
  input  in_12,
  input  A_2,
  input  [7:0] P_2,
  input  B_2,
  input  [7:0] Q_2,
  input  C,
  input  [7:0] R,
  input  D,
  input  E,
  input  [4:0] in_21,
  input  [4:0] in_22,
  input  in_23,
  input  in_24,
  input  in_25,
  input  in_26,
  input  [1:0] in_27,
  input  in_28,
  input  in_29,
  input  in_30,
  input  in_31,
  input  in_32,
  input  in_33,
  input  in_34,
  input  in_35,
  output C_2,
  output V,
  output out_38,
  output R_2,
  output out_40,
  output out_41,
  output out,
  output [7:0] out_2,
  output out_44,
  output out_45,
  output out_46,
  output out_47,
  output out_48,
  output out_49,
  output out_50
);

  wire callout_9_p1, medium_out, not_1_out, not_2_out, or_3_out, wide_out;

  // Callout #(.background("#b7e1eb71"), .dx(20), .dy(-20), .foreground("#236494"), .halign("center"), .style("margin: 4px;"), .text("Unconnected\ninputs are ignored"), .valign("top")) callout_1: pin names not known
  and and_1 (C_2, A, B);
  // Callout #(.background("#b7e1eb71"), .dx(-15), .dy(-20), .foreground("#185fba"), .halign("center"), .style("margin: 4px;"), .text("2-input\nAND gate"), .valign("top")) callout_2: pin names not known
  nand nand_1 (R_2, P, Q);
  // Callout #(.background("#b7e1eb71"), .dx(-15), .dy(-20), .foreground("#236494"), .halign("center"), .style("margin: 4px;"), .text("2-input\nNAND gate"), .valign("top")) callout_3: pin names not known
  or or_1 (out, A_2, B_2, C, D, E);
  // Callout #(.background("#b7e1eb71"), .dx(-15), .dy(-20), .foreground("#236494"), .halign("center"), .style("margin: 4px;"), .text("5-input\nOR gate"), .valign("top")) callout_4: pin names not known
  or or_2 (out_45, in_23, in_26);
  // XOR_Gate xor_1 has open pins: out=out_47
  // Callout #(.background("#b7e1eb71"), .dx(-13), .dy(-16), .foreground("#236494"), .halign("center"), .style("margin: 4px;"), .text("If no inputs, then error output"), .valign("top")) callout_5: pin names not known
  and and_2 (out_48, in_27[0], in_27[1]);
  or or_3 (or_3_out, in_28, in_30);
  and and_3 (or_3_out, in_29, in_31);
  xor xor_2 (or_3_out, in_32, in_34);
  and and_4 (or_3_out, in_33, in_35);
  Pull_Resistor pull_resistor_1 (.node(or_3_out));
  // Callout #(.background("#b7e1eb71"), .dx(25), .dy(16), .foreground("#236494"), .halign("right"), .style("margin: 4px;"), .text("ANSI/IEEE\n91a-1991"), .valign("bottom-overall")) callout_6: pin names not known
  // Callout #(.background("#b7e1eb71"), .dx(25), .dy(16), .foreground("#236494"), .halign("right"), .style("margin: 4px;"), .text("IEC 60617-12"), .valign("bottom-overall")) callout_7: pin names not known
  // Callout #(.background("#b7e1eb71"), .dx(25), .dy(16), .foreground("#236494"), .halign("right"), .style("margin: 4px;"), .text("DIN 40700"), .valign("bottom-overall")) callout_8: pin names not known
  not not_1 (not_1_out, in_22[0]);
  not not_2 (not_2_out, in_22[2]);
  // Callout #(.background("#b7e1eb71"), .dx(20), .dy(-20), .foreground("#236494"), .halign("center"), .style("margin: 4px;"), .text("Floating input causes\nerror, unless a result\ncan be determined\nfrom remaining inputs"), .valign("top")) callout_9: pin names not known; wires that end beside it: callout_9_p1
  // Callout #(.background("#b7e1eb71"), .dx(-20), .dy(-20), .foreground("#236494"), .format("wrapped"), .halign("right"), .style("p-margin: 0px;"), .text("push-pull output is always driving"), .textwidth(111), .valign("top")) callout_10: pin names not known
  // Callout #(.background("#b7e1eb71"), .dx(-15), .dy(-20), .foreground("#236494"), .format("wrapped"), .halign("center"), .style("p-margin: 0px;"), .text("single bus wire with multiple device outputs"), .textwidth(267), .valign("base")) callout_11: pin names not known
  // Callout #(.background("#b7e1eb71"), .dx(-15), .dy(13), .foreground("#236494"), .format("wrapped"), .halign("center"), .style("p-margin: 0px;"), .text("any of the four devices can drive the bus wire to 1, or even more than one of them at the same time"), .textwidth(216), .valign("base")) callout_12: pin names not known
  // Callout #(.background("#b7e1eb71"), .dx(-21), .dy(-16), .foreground("#236494"), .format("wrapped"), .halign("center"), .style("p-margin: 0px;"), .text("pull-down resistor ensures the bus is pulled down to 0 if no output is driving to 1"), .textwidth(267), .valign("base")) callout_13: pin names not known
  // Image #(.image("PNG:\niVBORw0KGgoAAAANSUhEUgAAASYAAADOCAYAAACTpK+BAAATo0lEQVR4Xu2dwapcxxGG70Vrb2zI\nImhphEEBY9leBSwMBseQhR/CD+AQtFSUZUIWAcdI6A2yyEvYYJAhkMTYO2G89ztkopqrivrUqT7T\nZ7q6q6vn/6CRfK/Vfeq7/9Q5c6bvzNUBAAAG40p+AQAAvEFjAgAMBxoTAGA40JgAAMOx2Ziurq66\njHvvvXP4wx8f/n88e/aNPJQhoOPaOm4ev/v95/KfXgTy59pqSO+j5qUU5GrNEI0pN+gHNNoPg45J\nHuep8ee//OkigiXr7j1GzEspyNWSosbUGjpjpGcG7YdEX/v+h+/kP+0On90++vD+8XjkWY0GBUYe\nv6xlhjO9BHk5H+RqyWaKegUtB50JZOhIvDd8LKXBpzpyDyAaFLgpwoS8VIFcvUJN0b/+czh8+cXh\ncPsX/z7cuv6l/LYL9APwDlzq5er67jEQ9LW9UFhyZz+PumpBXupArtaojYkk3bp9OLz95s2fo0Bn\nkvTscOetO/J/aUrq5de/+u/xGP7213/K/20X/LREnvUine2QlzqQqzVqY/r4kxtJowWNocCx6J73\nElIvNHh9KygwMkj036MHCXmpA7laozYmuoykgHH3HhU6A7LoHmFjLzT+8fcbN638yKciIz6gGOSl\nDuRqzWb1LQVZ4Rk2Pgu1fLlWBmnkewXIiw3I1QSNiUjD1hMKDq1pedmdI61x1AeVx8/gHLzyUgpy\nNUljIlhw7xucPR3JewW9az1FTxe1eOWllJ4uR8zVZuU95VjgIbbHZbckvZlLY5izHPJixqXnajNF\n0YKWiu31ikPPy25Jehk+wj0C5MWOS8/VZoqiBY3gm3o9f6CentKbmN5nfk8P5+KRl1I8fXrnSq16\nxJ28e2Ch1mdB9kL7TuhPGunLu+fs1rXA+xIceakDuVqjNqZRd/KW0uosmHpJx2tXD47reV32Mukl\neM8QIS91IFdr1MY0+k7eElqcBeUO3dECRHiECHmpA7laozamKDt5t+BfZqQ/rUh36PIlNw36vSbP\nM64kvQTvESLkpQ7kas1mivggIkJnvp7H33OtEtIQ9bp5OZqDPfTOSymjHVOvXG1WPJqUvfQ8/p5r\nldIrRMyIDvYw4vGPeEw9crVZ8YhS9sCX5z02qfGGOI97FFukIWp9rwJ5sedSc7WZouhB41dbWoiT\n9FxrL73uDcyYF2pS6f2n3k1LO6ZRKMnVuf42UxQ9aHzfoMfNw5EDRJSEqJaZ8kKO0t8fk6OVQ0nU\nXMnfv5PjlL/NFPEkkelVw+gBIvgYS4JxDr1ct4RroA8F4L/TmZ58pf561Rk1V2lTOsef+t3oO3mZ\nn398fvj0+urw1RuvH/9ei7ZDl8dvf/No+AARdLPygxdOyMu3775v6iV6Xoj0gZN78LA/5OoV6T6n\nJ08fV/tT/yUJibyTl/np0cPD1y/k8Kgl9SLHSJvhTvFZ4sTaS+S8EGlTyu1pQq505FO3Gn/qV2fY\nyUtQRz4lYA+5HbrRAmTdmGbJC5E+sHJPd5ErHdmYavypX51hJy9Bl4lcfO6ScQ+5HbqRLrn5ZmUL\nL9HzQqQPrNzPkq4EWvibIVc0+P5c7phL/G2miBeKTK8aItykzL2CYkUv1y1JG1OuFr4yaLW5MCVi\nrvi9pGr86f/yJVuTR6FXDaMHKA1Pq2Ps5bolXAMPehDx5kb5EniL5i6Jmqtaf5spih407ty5m3CW\njBygNDxbZ6laZspL6kwbWw8qS6LmqtbfZop4kqjwjtMeP9QRf52BKbl0tmDGvHBj4MGbL3sRPVfn\n+ttMUfSg8fH3+D2jEV1tndFaMKKDPfTMSykjOu2Rq82KR5Syh57H33OtEnqERzKag72MePyjHVOv\nXKkVz7CTt8X9pdwOXX5Dr1EC1Cs8DPJSB3K1Rq2YpETfycvPfy0vy1Mv2iY4j1BLeoaHQV7qQK7W\nqI0p+k7eVu9GmNuhO8ru3PRGY4/wMMhLHcjVGvUnEX0nL5/9rH+g2g7d48fsXN91O9syFBgOj3Xd\np0Be6kCu1mymyPMsci7c3SlsvfD0JPeLlLwU2wpPD+fikZdSPH1652qzak8x58LH3Oss4/lRzh6X\n2FsgL3Zceq42UxQtaHzZ2VOm1wY4r0vsLZAXOy49V5spihS0VGhPeq8pd9L2vsTeoreLGrzyUkrv\nYxstV5uV95ZzLunz4Z5C0/eIbo18zj/iWR55sQG5mqAxeYasx+W2/I1s+vto90MY5MUG5CrTmKLs\n5E0vx3uELN2he3w5t+EDUQanV43ngLzUgVytUauPsJPXI2Ryhy6tbX25LZ/r0/C8CVkC8lIHcrVG\nbUwj7+SVgnuGLPXCmwnp95lqobMYX75HCU4K8lIHcrVGbUwj7uSVl6AeN+nYy/EB+OIpCx0Hfe0c\n0k8oTcdoz/VLQF7qQK7WbKaIi/KERI92k46PZ8+Zh46Z/n/5/J4Hhcm7rlqQlzqQq1dspsgjaLmO\nv/cH1gr6IW95oeOn49wKCw36XstXXTzY8tKK0fNSCnK1RLfwElm0xxit42+FYmvQv6NQjVSLNbJm\njzFaXkpBrpYM15goWKOKTs9qucHHP2oNLZEueoyR81IKcrVmszEBAIAHaEwAgOFAYwIADAcaEwBg\nONCYAADDgcYEABgONCYAwHCgMQEAhgONCQAwHGhMAIDhQGMCAAwHGhMAYDjQmAAAw4HGBAAYDjQm\nAMBwoDEBAIYDjQkAMBxoTACA4UBjAgAMBxoTAGA4so0p/biY6MPy42zgRQde6oC/JdnGJD+lIfqw\nQs4bfVgh540+eiPXjz5qyc7AC6QfGxNtpB+EaAW86MBLHfC3JDuD1QLeWNdhPZ8X1nVYz+eFVx1e\n61pjVUd2huMC13fll8NhJYqBFx14qQP+lqgzfPnF4fD2mzfj40/kd2NhJYqAFx14qQP+1qgzkBwW\ndeu2/K4NdOfe4u79KaxEET28aNBHQlt/LHQ0LxHzUkoPfxoj50qdoXUHv/PWncVoiZUoooWXU8Gg\nB+O999453ly0ZHQvKVHzUkoLf9FzlZ3htasHx9GC9MAtitjCShRj7YUeaHR8uYCMHiDG2ktK5LyU\nYu0veq6yM1gtoJGe/b7/4bsml5SMdR3W8zEUEJqXnEgX/HKsJdZ1WM+XEjkvpbRaN2qusjNYLaBB\n3Zr2PPBlecv7B9Z1WM+XQk7oLCbnHzlAjPV8KZHzUkrLdSPmKjuD1QIS6tocKjr70RpPnj4OEzTr\n+cgHn9XoT3lWI0YOEGM9HxM9L6VYrxs9V9kZrBaQ8NmP+fnH58d16M8WWNfRYr5TD7KRA8RYz8dE\nz0sp1utGz1V2BqsFJNS5aV7eek+X53QGpK/RGdEa6zqs5+NwUIjSvzP0d7oMp3EqaHuwrsN6PiZ6\nXkqxXjd6rrIzHBdouBOVZNDgS8z0kt0SK1GMtZc0OLkAaV+vZXQvkqh5KcXaX/RcqTO02FfhhZUo\nAl504KUO+FujzuC1E7UFVqIIeNGBlzrgb406Azq4DrzowEsd8LcmO4P1TlQvrEQx8KIDL3XA35Ls\nDFYLeGNdh/V8XljXYT2fF151eK1rjVUd2RmsFvDGug7r+bywrsN6Pi+86vBa1xqrOrIzWC3gjXUd\n1vN5YV2H9Xxe5OqwfEldI7duNHJ17PW3nuEluQWiYV2H9XxeWNdhPZ8XaR38KzBy0N4fa+BvSdbE\njKIssJ7PC+s6rOfzguvg3eU8Pvrw/uK/rd8XCv6WZE0cJzDcieqF9Q8cXnRm88JDnt3pv/l7lr+v\nB39L1GTOsq/ip0cPD1+/EEDjqzdel9/eDbzozOKFSB9U9HtkGvCXx8qf2phm2YlKRbMAGrXAi84s\nXoitsz0Df3ms/KlfnaWDl3TmPcCLzixeiPSBlXv3AvjLY+VPbUzELDtRP72+Og4r4EVnFi8lT0Xo\nLVg+e/H9D+BvhZW/7Hd48uhY12E9nxfWdVjP50X6wKIhz/rpS+C5pyrnAH9LsiZmE2WF9XxeWNdh\nPZ8XXEf68jad+dP3zaZx6uXuvcDfkqyJ2URZYT2fF9Z1WM/nRVpH+tJ2Ok49qM4B/pZkTcwoygLr\n+bywrsN6Pi+0OtJ3e9Te1N8Cbd2IaHWc4y9rQlsgItZ1WM/nhXUd1vN54VWH17rWWNWRneG4wEQ7\nUa2AFx14qQP+lqgzzLivwgJ40YGXOuBvjTrDjDtRLYAXHXipA/7WqDOgg+vAiw681AF/a7IzzLYT\n1Qp40YGXOuBvSXYGqwW8sa7Dej4vrOuwns8Lrzq81rXGqo7sDFYLeGNdh/V8XljXYT2fF151eK1r\njVUd2RmsFvDGug7r+bywrsN6Pi+86vBa1xqrOrIzWC3gjXUd1vN5YV2H9XxeeNXhta41VnVkZ7Ba\nwBvrOqzn88K6Duv5vPCqw2tda6zqyM5wXAA7UVfAiw681AF/S9QZsK9CB1504KUO+FujzoCdqDrw\nogMvdcDfGnUGdHAdeNGBlzrgb012BuxE1YEXHXipA/6WZGewWsAb6zqs5/PCug7r+bzwqsNrXWus\n6sjOwAvQe/Xyu89FG3TsVqIYeNGBlzrgb0l2Bl5glmGFnDf6sELOG330Rq4ffdSSnSF9n97og2qx\nAl504KUO+FuSbUwAAOAFGhMAYDjQmAAAw4HGBAAYDjQmAMBwoDEBAIYDjQkAMBxoTACA4UBjAgAM\nBxoTAGA40JgAAMOBxgQAGA40JgDAcKAxAQCGA40JADAcaEwAgOFAYwIADAcaEwBgOLKNid/q89mz\nb+S3Lhp40YGXOuBvSbYxyTcX53HvvXcuWqD0AS83SB/wsg/p7dL9nWxMH314fyUrHfSRLZckDV50\n4KUO+FtysjFJSEr6+VE87rx1R/6vUwIvOvBSB/wtWZt4yVHA9V355QWaNLrsnJkSL9//8B28KFxi\nXkop8XdJuVIb05dfHA5vv3kzPv5EfleHOngqjCTOhvQiP09LjidPHy+czBok6aWES8hLKdKfzJEc\nl5ArtTGRHBZ167b8bh46I9LNulnDlnqhIcNROmb2grzsB7laozYm2cH3Qt2bZc30XFh6kWeyUyO9\nDJ/Zy15mzUsp0p/MzakxY67UxkS8dvXgOM6Fuvdssgh40YGXOuBvSbYxcZE1zCaLgBcdeKkD/pZk\nTViIIlJZMzwHhhcdeKkD/pZkTViJImaRRcCLDrzUAX9LsiYsRRHpy8ORsa4BXnRm8VKKda3R/WWP\nukVR/NIwvZIQFXjRgZc64G9J1sRR1ImdqHuhfSstfgA9aeElvfSOSgsvM+SllBb+IudKPWK5r8KS\nyF1cepH7Sc4d0fehSC+WRM5LKdKfzMe5I3Ku1MZ07k7eEiKfBa126J4a0UBe6kCu1qhHKzu4NXwW\npDfHioT0Is9QtYPf8iK6F2ui5qUU6U/monZEzJXamIjanahbkCASRYGLBrzowEsd8Lck25haX/61\nnr8VrY+79fytaH3cref3pnV9ree3JnukrQvhy/No78YHLzrwUgf8LcmaaC2KnvvS/PRnJOBFB17q\ngL8lWROtRfHzXnpJMxLwotPaCz+wonkpBf6WZE20FkX0WMOaHsfcYw1rWh4zbRRM36SfnpZEeoWp\nBPhbkjVxLMJ4J6qk5Q8j5ecfn8svnQ286LT0wj7k8L5fAn91bPlT0y/3VbSCBf306GGT8e277x++\nfjE/ja/eeF0uvxvpRe4XsRjpbl1Zj9Vo7cUSfmqrDTrzy9p6jNb+ZCZqBt/01sbI/tTG1HInbwoL\n4oNsPWrptUOXhzz+VqOWlnlJf0teG7IWj1FL71ylQ9biMTTUr8oO3gqWIzuq1SjpzHuQXuTZyWLg\nimkJOZEPJh4jn/H3IP3JTNSMqa6YiJY7URkW1BKWYQW86LT0Ih9QPDzvkcBfHaf8ZdPf48HRYw1r\nehxzjzWsaXnMdOaXDyr62kzA35KsiZaiCP6t8Ui/v0PAi05rL/QKTkQvpcDfkqyJ1qK4i4/euSXw\nogMvdcDfkqyJ1qL4ptzoG70k8KIDL3XA35KsidaiWs/fitbH3Xr+VrQ+7tbze9O6vtbzW5M90mMh\njXaiRr2PQsCLDrzUAX9L1MYk91VYw3t1olxWMtKL3DNSOyK+0yAhvVgTNS+lSH8yF7UjYq7UxtRy\nJy8R7bKS6bVDNxrISx3I1Rr1aGUHt4Q6OEmKdFnJSC/yzFQz+Kw2gxdLyE1UL6VIfzIbNSNqrtTG\nRLTYiTrDRxfDiw681AF/S7KNqcXlH79kSZ08KvCiAy91wN+SrAlrUZE/FTTFugZ40ZnFSynWtUb3\nlz1qy6IiX1JK4EUHXuqAvyVZE5aieK5oH1OsAS868FIH/C3JmrASxW/0FVlSCrzowEsd8Lcka+Io\nqmInKl1C8s236JJS4EUHXuqAvyVqY5L7KvaSPsedQRIjvcg9I6dG+u6UM3vZy6x5KUX6k7k5NWbM\nldqYanbykqjZJDFWO3Rn9oK87Ae5WqM2JtnBS0jPejQocLMhvcgzlxx0Jks/z+tSvJRwCXkpRfqT\nOZLjEnKlNiaidCcq/eYyP7elQX+P+hJlCaVe0uf88PKKS8tLKaX+LiVX2cbEhWvQbymnz2t5zChI\nAi868FIH/C3RTRxeiSIhfPkoxdCgjh3p7RRqgRcdeKkD/pacbEzauBQ5GtIFvNwgXcDLPqSzS/eX\nbUwkIr3hdmlicsCLDrzUAX9Lso0JAAC8QGMCAAwHGhMAYDjQmAAAw4HGBAAYjv8BQJY77djkFokA\nAAAASUVORK5CYII=")) image_1: pin names not known
  or or_4 (V, X, Y);
  // Callout #(.background("#b7e1eb71"), .dx(-15), .dy(-20), .foreground("#236494"), .halign("center"), .style("margin: 4px;"), .text("2-input\nOR gate"), .valign("top")) callout_14: pin names not known
  nor nor_1 (out_40, in_8, in_11);
  // Callout #(.background("#b7e1eb71"), .dx(-15), .dy(-20), .foreground("#236494"), .halign("center"), .style("margin: 4px;"), .text("2-input\nNOR gate"), .valign("top")) callout_15: pin names not known
  // Callout #(.background("#b7e1eb71"), .dx(-20), .dy(-19), .foreground("#236494"), .format("wrapped"), .halign("center"), .style("p-margin: 0px;"), .text("Each output bit is the result of ANDing the corresponding input bits."), .textwidth(228), .valign("base")) callout_16: pin names not known
  and wide (wide_out, not_1_out, in_22[1], not_2_out, in_22[3], in_22[4]);
  LED led_1 (.in(wide_out));
  // Callout #(.background("#b7e1eb71"), .dx(-15), .dy(-20), .foreground("#236494"), .halign("center"), .style("margin: 4px;"), .text("Both circuits work the same: the LED\nturns on only when  the input is 11010."), .valign("top")) callout_17: pin names not known
  or or_5 (out_46, in_24, callout_9_p1);
  and and_5 (out_49, in_27[0], in_27[1]);
  // Probe on or_3_out
  // Callout #(.background("#b7e1eb71"), .dx(-18), .dy(14), .foreground("#236494"), .format("wrapped"), .halign("center"), .style("p-margin: 0px;"), .text("8-bit 3-input AND gate"), .textwidth(107), .valign("base")) callout_18: pin names not known
  assign out_2 = P_2 & Q_2 & R;  // AND_Gate and_6, 8 bits wide
  // Callout #(.background("#b7e1eb71"), .dx(20), .dy(-20), .foreground("#236494"), .halign("center"), .style("margin: 4px;"), .text("Same for \nerror inputs"), .valign("top")) callout_19: pin names not known
  // Callout #(.background("#b7e1eb71"), .dx(-20), .dy(-20), .foreground("#236494"), .format("wrapped"), .halign("right"), .style("p-margin: 0px;"), .text("pull-down-only output is floating when not driving output low"), .textwidth(146), .valign("top")) callout_20: pin names not known
  xor xor_3 (out_38, in_3, in_6);
  // Callout #(.background("#b7e1eb71"), .dx(-15), .dy(-20), .foreground("#236494"), .halign("center"), .style("margin: 4px;"), .text("2-input\nXOR gate"), .valign("top")) callout_21: pin names not known
  xnor xnor_1 (out_41, in_9, in_12);
  // Callout #(.background("#b7e1eb71"), .dx(-15), .dy(-20), .foreground("#236494"), .halign("center"), .style("margin: 4px;"), .text("2-input\nXNOR gate"), .valign("top")) callout_22: pin names not known
  and \medium  (medium_out, in_21[4], in_21[3], ~in_21[2], in_21[1], ~in_21[0]);  // AND_Gate
  LED led_2 (.in(medium_out));
  and and_7 (out_44, out_46, in_25);
  and and_8 (out_50, in_27[0], in_27[1]);
  // Callout #(.background("#b7e1eb71"), .dx(-20), .dy(-20), .foreground("#236494"), .format("wrapped"), .halign("right"), .style("p-margin: 0px;"), .text("pull-up-only output is floating when not driving output high"), .textwidth(134), .valign("top")) callout_23: pin names not known

  // Notes on the sheet:
  //   # Overview of Common Gates
  //   Common mutliple-input logic gates are AND, OR, NAND, NOR, XOR, XNOR.
  //   Each one takes several inputs, combines these using the rules of Boolean logic, and outputs the result.
  //   ## Multiple Inputs and Multi-Bit Gates
  //   Use the ***number of inputs*** attribute to allow more than two inputs. All inputs are combined using the usual rules of Boolean logic to produce a single output result. Use the *data bits* attribute to allow a gate to operate on multiple bits simultaneously.
  //   **Keyboard shortcut** 👉To change the *number of inputs* for a gate, select it and type a number. Or select several gates to change them all.
  //   **Keyboard shortcut** 👉To change the *data bits*, select some gates, hold the option key (⌥) or Alt key, and type a number.
  //   ## Visuals
  //   The ***gate size*** attribute allows a choice of *narrow*, *medium*, or *wide*. Gates can be rotated to face any direction using the ***facing*** attribute. A gate can be given a ***label***, which will follow the gate if it is moved or copied.
  //   **Keyboard shortcut** 👉Select some gates, then use arrow keys (↑→↓←) to rotate them so they face a different direction.
  //   ## Negated Inputs
  //   Any of the inputs can be configured to be active-low. This behaves exactly as if there were a NOT gate attached to that input, but used judiciously, negated inputs can make circuits more compact and easier to undertand.
  //   ## XOR & XNOR Multiple-Input Behavior
  //   Multi-input XOR and XNOR gates can be confusing. Normally, XOR outputs a 1 when an *odd number of inputs* are 1, and XNOR does the opposite. This "parity" behavior is most typical. For XOR and XNOR gates with more than two inputs, the ***multiple-input behavior*** attribute allows for a different, less common behavior, where XOR outputs a 1 when *exactly one input* is a 1, and XNOR does the opposite. 
  //   **Suggestion** 👉 Don't use multi-input XOR and XNOR gates. For parity calculations, use the ***Even Parity*** or ***Odd Parity*** gates instead. For *exactly-one* calculations, which are less common, consider building a circuit from a ***Bit Adder*** and a ***Comparator*** (found under ***Arithmetic***).
  //   ## Errors, Unconnected, and Floating Inputs
  //   As a convenience, any input left unconnected is ignored: if there is no wire or other connection to the input, the simulator acts as if the input did not exist at all. So a 5-input gate with only two inputs connected behaves just like a 2-input gate. This doesn't match physical circuits or more realistic simulators, where such inputs would be considered *floating*, but it makes editing a circuit a little more forgiving. If all inputs are unconnected, the output is an error. If only one input is connected, the behavior depends on the gate type. To enable a more strict simulation behavior, treating unconnected inputs as floating values, go to ***Project > Options > Simulation***.
  //   ## Output Driver Option
  //   Normally, gates use **push-pull** outputs: they actively output either 1 or 0 at all times, as long as the inputs are well defined. The ***Output Driver*** attribute allows for two other behaviors. 
  //   * With a **pull-up-only** output driver (equivalent to open-emitter/open-source) a gate can actively output 1, but instead of outputting 0 it will produce a floating (z) output. 
  //   * With **pull-down-only** output driver (equivalent to open-collector/open-drain), a gate can actively output 0, but instead of outputting 1 it will produce a floating (z) output. 
  //   This allows creation of *wired-OR* and *wired-AND* busses. ***Pull Resistor*** (found in the ***Analog*** library) can be useful for these too.
  //   ## Gate Shapes and International Standards
  //   Different standards bodies have adopted different shapes for  common gates. In **Logisim > Settings > International** you can choose from **ANSI/IEEE Standard 91a-1991** (curved, distinctive shapes commonly used in computer science textbooks and educational materials), **IEC 60617-12** (rectangular, uniform shapes often used in professional settings and engineering), and **DIN 40700** (an older, less common standard).
  //   or_3 drives only 1 and floats otherwise
  //   and_3 drives only 1 and floats otherwise
  //   xor_2 drives only 1 and floats otherwise
  //   and_4 drives only 1 and floats otherwise
  //   AND
  //   and_5 drives only 0 and floats otherwise
  //   OR
  //   NAND
  //   and_8 drives only 1 and floats otherwise
  //   NOR
endmodule
