// Logisim project interaction.circ as structural Verilog: 1 circuit, main circuit main
module main (
  input  Load,
  input  in_2,
  input  B,
  output out_4,
  output out_5
);

  wire A_2_out, A_out, clock_1_out, counter_1_carry, R_out;
  wire [3:0] meter_1_p1;
  wire [7:0] counter_1_q, dipswitch_1_sw8;

  Button A (.out(A_out));
  and and_1 (out_4, A_out, in_2);
  // Meter #(.shape("dial"), .width(4)) meter_1: pin names not known; wires that end beside it: meter_1_p1
  Slider #(.width(4)) slider_1 (.out(meter_1_p1));
  // Probe on meter_1_p1
  DipSwitch dipswitch_1 (
    .sw1(dipswitch_1_sw8[7]), .sw2(dipswitch_1_sw8[6]), .sw3(dipswitch_1_sw8[5]), .sw4(dipswitch_1_sw8[4]),
    .sw5(dipswitch_1_sw8[3]), .sw6(dipswitch_1_sw8[2]), .sw7(dipswitch_1_sw8[1]), .sw8(dipswitch_1_sw8[0]));
  // Callout #(.background("#ace8b5b5"), .dx(15), .dy(10), .halign("right"), .text("Type 'A' to poke\nthis button.")) callout_1: pin names not known
  // Callout #(.background("#ace8b5b5"), .dx(15), .dy(-10), .halign("right"), .text("Type 'B' to toggle\nthis input pin.")) callout_2: pin names not known
  Counter counter_1 (
    .load(Load), .D(dipswitch_1_sw8), .Q(counter_1_q), .carry(counter_1_carry), .clk(clock_1_out), .clr(R_out));  // open: count
  Clock clock_1 (.out(clock_1_out));
  Button R (.out(R_out));
  Button A_2 (.out(A_2_out));
  and and_2 (out_5, A_2_out, B);
  LED Overflow (.in(counter_1_carry));
  _7_Segment_Display u_7_segment_display_1 ();  // open: g, f, a, b, e, d, c, dp
  // Hex_to_7_Segment_decoder hex_to_7_segment_decoder_1: pin names not known
  _7_Segment_Display u_7_segment_display_2 ();  // open: g, f, a, b, e, d, c, dp
  // Hex_to_7_Segment_decoder hex_to_7_segment_decoder_2: pin names not known
endmodule
