// Logisim project invaders.circ as structural Verilog: 4 circuits, main circuit main
module main (
  input  [7:0] difficulty,
  output Ouch
);

  wire buffer_2_out, buffer_9_out, clock_1_out, clock_2_out, column_state_1_boom, column_state_1_score,
       column_state_2_boom, column_state_2_score, column_state_3_boom, column_state_3_score,
       column_state_4_boom, column_state_4_score, column_state_5_boom, column_state_5_score,
       column_state_6_boom, column_state_6_score, column_state_7_boom, column_state_7_score,
       column_state_8_boom, column_state_8_score, decoder_1_out0, decoder_1_out1, decoder_1_out2,
       decoder_1_out3, F_out;
  wire [2:0] Position_out;
  wire [3:0] binairy_to_bcd_converter_1_p2, binairy_to_bcd_converter_1_p3, decoder_1_out4;
  wire [5:0] Score_q;
  wire [15:0] column_state_1_column, column_state_2_column, column_state_3_column, column_state_4_column,
       column_state_5_column, column_state_6_column, column_state_7_column, column_state_8_column;

  Clock clock_1 (.out(clock_1_out));
  Decoder #(.enable("false"), .select(3)) decoder_1 (
    .out0(decoder_1_out0), .out1(decoder_1_out1), .out2(decoder_1_out2), .out3(decoder_1_out3),
    .out4(decoder_1_out4[0]), .out5(decoder_1_out4[1]), .out6(decoder_1_out4[2]), .out7(decoder_1_out4[3]),
    .sel(Position_out));
  Slider #(.width(3)) Position (.out(Position_out));
  Button #(.behavior("oneshot-no"), .\clocking ("synchronous")) F (.out(F_out));
  column_state column_state_1 (
    .ship(decoder_1_out0), .fire(F_out), .difficulty(difficulty), .clk(clock_1_out),
    .boom(column_state_1_boom), .score(column_state_1_score), .column(column_state_1_column));
  column_state column_state_2 (
    .ship(decoder_1_out1), .fire(F_out), .difficulty(difficulty), .clk(clock_1_out),
    .boom(column_state_2_boom), .score(column_state_2_score), .column(column_state_2_column));
  column_state column_state_3 (
    .ship(decoder_1_out2), .fire(F_out), .difficulty(difficulty), .clk(clock_1_out),
    .boom(column_state_3_boom), .score(column_state_3_score), .column(column_state_3_column));
  column_state column_state_4 (
    .ship(decoder_1_out3), .fire(F_out), .difficulty(difficulty), .clk(clock_1_out),
    .boom(column_state_4_boom), .score(column_state_4_score), .column(column_state_4_column));
  DotMatrix #(.matrixcols(8), .matrixrows(16)) dotmatrix_1 (
    .col0(column_state_1_column), .col1(column_state_2_column), .col2(column_state_3_column),
    .col3(column_state_4_column), .col4(column_state_5_column), .col5(column_state_6_column),
    .col6(column_state_7_column), .col7(column_state_8_column));
  buf buffer_1 (Ouch, column_state_1_boom);
  buf buffer_2 (buffer_2_out, column_state_1_score);
  buf buffer_3 (Ouch, column_state_2_boom);
  buf buffer_4 (buffer_2_out, column_state_2_score);
  buf buffer_5 (Ouch, column_state_3_boom);
  buf buffer_6 (buffer_2_out, column_state_3_score);
  buf buffer_7 (Ouch, column_state_4_boom);
  buf buffer_8 (buffer_2_out, column_state_4_score);
  Pull_Resistor pull_resistor_1 (.node(Ouch));
  Clock clock_2 (.out(clock_2_out));
  Hex_Digit_Display hex_digit_display_1 (.value(binairy_to_bcd_converter_1_p2));  // open: dp
  Counter #(.max('h3f), .width(6)) Score (
    .count(buffer_2_out), .Q(Score_q), .clk(clock_2_out));  // open: load, D, carry, clr
  // Binairy_to_BCD_converter #(.binvalue(6)) binairy_to_bcd_converter_1: pin names not known; wires that end beside it: Score_q, binairy_to_bcd_converter_1_p2, binairy_to_bcd_converter_1_p3
  column_state column_state_5 (
    .ship(decoder_1_out4[0]), .fire(F_out), .difficulty(difficulty), .clk(clock_1_out),
    .boom(column_state_5_boom), .score(column_state_5_score), .column(column_state_5_column));
  column_state column_state_6 (
    .ship(decoder_1_out4[1]), .fire(F_out), .difficulty(difficulty), .clk(clock_1_out),
    .boom(column_state_6_boom), .score(column_state_6_score), .column(column_state_6_column));
  column_state column_state_7 (
    .ship(decoder_1_out4[2]), .fire(F_out), .difficulty(difficulty), .clk(clock_1_out),
    .boom(column_state_7_boom), .score(column_state_7_score), .column(column_state_7_column));
  column_state column_state_8 (
    .ship(decoder_1_out4[3]), .fire(F_out), .difficulty(difficulty), .clk(clock_1_out),
    .boom(column_state_8_boom), .score(column_state_8_score), .column(column_state_8_column));
  Hex_Digit_Display hex_digit_display_2 (.value(binairy_to_bcd_converter_1_p3));  // open: dp
  buf buffer_9 (buffer_9_out, column_state_5_boom);
  buf buffer_10 (buffer_9_out, column_state_6_boom);
  buf buffer_11 (buffer_9_out, column_state_7_boom);
  buf buffer_12 (buffer_9_out, column_state_8_boom);
  buf buffer_13 (buffer_2_out, column_state_5_score);
  buf buffer_14 (buffer_2_out, column_state_6_score);
  buf buffer_15 (buffer_2_out, column_state_7_score);
  buf buffer_16 (buffer_2_out, column_state_8_score);
  Pull_Resistor pull_resistor_2 (.node(buffer_2_out));

  // Notes on the sheet:
  //   buffer_1 drives only 1 and floats otherwise
  //   buffer_2 drives only 1 and floats otherwise
  //   buffer_3 drives only 1 and floats otherwise
  //   buffer_4 drives only 1 and floats otherwise
  //   buffer_5 drives only 1 and floats otherwise
  //   buffer_6 drives only 1 and floats otherwise
  //   buffer_7 drives only 1 and floats otherwise
  //   buffer_8 drives only 1 and floats otherwise
  //   buffer_9 drives only 1 and floats otherwise
  //   buffer_10 drives only 1 and floats otherwise
  //   buffer_11 drives only 1 and floats otherwise
  //   buffer_12 drives only 1 and floats otherwise
  //   buffer_13 drives only 1 and floats otherwise
  //   buffer_14 drives only 1 and floats otherwise
  //   buffer_15 drives only 1 and floats otherwise
  //   buffer_16 drives only 1 and floats otherwise
endmodule

module column_state (
  input  ship,
  input  fire,
  input  [7:0] difficulty,
  input  clk,
  output boom,
  output score,
  output [15:0] column
);

  wire and_1_out, comparator_1_lt, or_1_out, pew, step;
  wire [3:0] adder_1_out, bit_extender_1_out, invader_step_q;
  wire [7:0] bit_extender_2_out, callout_1_p1;
  wire [15:0] bit_extender_3_out, bit_reverse_1_out_2, detect_hit_1_newplayer, detect_hit_1_remaining, inv,
       mis;

  assign bit_extender_1_out = {{2{1'b0}}, difficulty[7:6]};  // Bit_Extender bit_extender_1
  and and_1 (and_1_out, ship, fire);
  Adder #(.width(4)) adder_1 (.a(bit_extender_1_out), .b(invader_step_q), .out(adder_1_out), .cin(1'b1), .cout(step));
  Register #(.width(4)) invader_step (.D(adder_1_out), .Q(invader_step_q), .clk(clk));  // open: en, clr
  or or_1 (or_1_out, step, score);
  // Shift_Register #(.length(16)) invader_pos: pin names not known; wires that end beside it: 1'b0, clk, or_1_out, pew, detect_hit_1_remaining[15], detect_hit_1_remaining[14], detect_hit_1_remaining[13], detect_hit_1_remaining[12], detect_hit_1_remaining[11], detect_hit_1_remaining[10], detect_hit_1_remaining[9], detect_hit_1_remaining[8], detect_hit_1_remaining[7], detect_hit_1_remaining[6], detect_hit_1_remaining[5], detect_hit_1_remaining[4], detect_hit_1_remaining[3], detect_hit_1_remaining[2], detect_hit_1_remaining[1], boom
  // Shift_Register #(.length(16)) missile_pos: pin names not known; wires that end beside it: clk, 1'b1, and_1_out, detect_hit_1_newplayer[15], detect_hit_1_newplayer[14], detect_hit_1_newplayer[13], detect_hit_1_newplayer[12], detect_hit_1_newplayer[11], detect_hit_1_newplayer[10], detect_hit_1_newplayer[9], detect_hit_1_newplayer[8], detect_hit_1_newplayer[7], detect_hit_1_newplayer[6], detect_hit_1_newplayer[5], detect_hit_1_newplayer[4], detect_hit_1_newplayer[3], detect_hit_1_newplayer[2], detect_hit_1_newplayer[1]
  Bit_Extender #(.out_width(8), .\type ("zero")) bit_extender_2 (.in(difficulty), .out(bit_extender_2_out));
  // Random random_1: pin names not known; wires that end beside it: invader_step_q, clk
  Comparator #(.mode("unsigned")) comparator_1 (
    .a(bit_extender_2_out), .b(callout_1_p1), .lt(comparator_1_lt));  // open: gt, eq
  // Callout #(.text("When difficulty is higher, RNG is\nmuch more likely to be below that level.")) callout_1: pin names not known; wires that end beside it: callout_1_p1
  not not_1 (pew, comparator_1_lt);
  bit_reverse bit_reverse_1 (.in_1(mis), .out_2(bit_reverse_1_out_2));
  detect_hit detect_hit_1 (
    .invader(inv), .player(mis), .remaining(detect_hit_1_remaining), .Hit(score),
    .newplayer(detect_hit_1_newplayer));
  assign bit_extender_3_out = {{15{1'b0}}, ship};  // Bit_Extender bit_extender_3
  assign column = inv | bit_reverse_1_out_2 | bit_extender_3_out;  // OR_Gate or_2, 16 bits wide

  // Other names for the same wires on the sheet: shp = ship

  // Notes on the sheet:
  //   This keeps track of info for one column:
  //    + where the falling "invader" is (if any)
  //    + where the rising "missile" is (if any)
  //   It outputs:
  //    + If a point was scored
  //    + if ship was destroyed
  //    + current column state
  //   It takes as input:
  //    + clock
  //    + if ship is here
  //    + if ship is firing
  //    + difficulty level
endmodule

module detect_hit (
  input  [15:0] invader,
  input  [15:0] player,
  output [15:0] remaining,
  output Hit,
  output [15:0] newplayer
);

  wire bitfinder_1_found;
  wire [3:0] bitfinder_1_index, bitfinder_2_index, subtractor_1_out;
  wire [15:0] and_2_out, and_3_out, bit_extender_1_out, bit_extender_2_out, bit_reverse_1_out_2, blast,
       shifter_1_out, shifter_2_out, shifter_3_out;

  BitFinder #(.width(16)) bitfinder_1 (.in(player), .index(bitfinder_1_index), .found(bitfinder_1_found));
  Subtractor #(.width(4)) subtractor_1 (.a(4'b1111), .b(bitfinder_1_index), .out(subtractor_1_out));  // open: bin, bout
  assign bit_extender_1_out = {{15{bitfinder_1_found}}, bitfinder_1_found};  // Bit_Extender bit_extender_1
  Shifter #(.width(16)) shifter_1 (.in(16'h7), .\dist (subtractor_1_out), .out(shifter_1_out));
  Shifter #(.shift("ar"), .width(16)) shifter_2 (.in(shifter_1_out), .\dist (4'b0001), .out(shifter_2_out));
  // Callout #(.text("This circuit calculates\nthe \"blast radius\" of\nthe highest missile")) callout_1: pin names not known
  assign blast = shifter_2_out & bit_extender_1_out;  // AND_Gate and_1, 16 bits wide
  assign and_2_out = player & ~bit_reverse_1_out_2;  // AND_Gate and_2, 16 bits wide
  bit_reverse bit_reverse_1 (.in_1(blast), .out_2(bit_reverse_1_out_2));
  // Callout #(.dx(23), .dy(36), .halign("right"), .text("Find lowest invader\ntouching the blast")) callout_2: pin names not known
  assign and_3_out = invader & blast;  // AND_Gate and_3, 16 bits wide
  // Probe on blast
  assign remaining = invader & ~shifter_3_out;  // AND_Gate and_4, 16 bits wide
  // Probe on shifter_3_out
  BitFinder #(.width(16)) bitfinder_2 (.in(and_3_out), .index(bitfinder_2_index), .found(Hit));
  assign bit_extender_2_out = {{15{1'b0}}, Hit};  // Bit_Extender bit_extender_2
  Multiplexer #(.enable("false"), .width(16)) multiplexer_1 (.in0(player), .in1(and_2_out), .out(newplayer), .sel(Hit));
  Shifter #(.width(16)) shifter_3 (.in(bit_extender_2_out), .\dist (bitfinder_2_index), .out(shifter_3_out));

  // Notes on the sheet:
  //   This checks a column to see if there was a hit.
  //   Inputs:
  //    - bit pattern of invaders
  //    - bit pattern of missiles
  //   Outputs:
  //    - if there was a hit
  //    - the remaining invaders
endmodule

module bit_reverse (
  input  [15:0] in_1,
  output [15:0] out_2
);


  assign out_2 = {in_1[0], in_1[1], in_1[2], in_1[3], in_1[4], in_1[5], in_1[6], in_1[7], in_1[8], in_1[9], in_1[10], in_1[11], in_1[12], in_1[13], in_1[14], in_1[15]};

  // Notes on the sheet:
  //   bit-reverse: take a 16-bit value and reverses the order of
  //   the bits.
endmodule
