// Logisim project io-examples.circ as structural Verilog: 1 circuit, main circuit ledbar-example
module ledbar_example (
);

  wire clock_1_out, ledbar_2_p3, ledbar_2_p5, ledbar_2_p7, ledbar_2_p9, ledbar_2_p11, shift_register_1_p1,
       shift_register_1_p2, shift_register_1_p5, shift_register_1_p7, shift_register_1_p8;
  wire [7:0] ledbar_1_p1;

  // Callout #(.background("#83ff8536"), .dx(26), .dy(23), .format("wrapped"), .text("8-segment LED bar, with round LEDs, showing the contents of an 8-bit counter"), .textwidth(262), .valign("bottom-overall")) callout_1: pin names not known
  // LEDBar #(.dotshape("circle"), .inputtype("bus")) ledbar_1: pin names not known; wires that end beside it: ledbar_1_p1
  Counter counter_1 (.Q(ledbar_1_p1), .clk(clock_1_out));  // open: load, D, count, carry, clr
  Clock clock_1 (.out(clock_1_out));
  // Callout #(.background("#6938ff36"), .dx(26), .dy(23), .format("wrapped"), .text("1-bit random number generator, feeding into an 8-stage shift register"), .textwidth(230), .valign("bottom-overall")) callout_2: pin names not known
  Random #(.width(1)) random_1 ();  // open: clk, next, out, clr
  // Shift_Register shift_register_1: pin names not known; wires that end beside it: shift_register_1_p1, shift_register_1_p2, shift_register_1_p2, shift_register_1_p1, shift_register_1_p5, shift_register_1_p5, shift_register_1_p7, shift_register_1_p8
  Clock clock_2 (.out(shift_register_1_p1));
  // LEDBar ledbar_2: pin names not known; wires that end beside it: shift_register_1_p7, shift_register_1_p8, ledbar_2_p3, ledbar_2_p3, ledbar_2_p5, ledbar_2_p5, ledbar_2_p7, ledbar_2_p7, ledbar_2_p9, ledbar_2_p9, ledbar_2_p11, ledbar_2_p11
  // Callout #(.background("#6938ff36"), .dx(-19), .dy(-17), .format("wrapped"), .halign("right"), .text("Contents of shift register are displayed with an 8-segment LED Bar"), .textwidth(231), .valign("top")) callout_3: pin names not known
endmodule
