// Logisim project pins.circ as structural Verilog: 2 circuits, main circuit main
module main (
  input  A,
  input  [3:0] P,
  input  [11:0] in_3,
  input  B,
  input  in_5,
  input  in_6,
  output [3:0] Q,
  output F,
  output [7:0] out_9,
  output [1:0] out_10,
  output out_11,
  output out_12,
  output out_13,
  output out_14
);

  wire inner_1_q, not_1_out, or_1_out;

  // Callout #(.background("#ace8b5b5"), .dx(15), .dy(-14), .halign("right"), .text("1-bit input\npins")) callout_1: pin names not known
  or or_1 (or_1_out, in_5, in_6);
  not not_1 (not_1_out, in_6);
  and and_1 (F, A, B);
  // Callout #(.background("#e3a5e8b5"), .dx(-6), .dy(-11), .halign("center"), .text("1-bit output\npin"), .valign("top")) callout_2: pin names not known
  inner inner_1 (.A(in_5), .B(or_1_out), .C(not_1_out), .P(out_13), .Q(inner_1_q));
  // Callout #(.background("#f7ff0a2c"), .dx(-35), .dy(-34), .format("wrapped"), .text("diagram of inner circuit"), .textwidth(290), .valign("top")) callout_3: pin names not known
  // Image #(.image("PNG:\niVBORw0KGgoAAAANSUhEUgAAASQAAACOCAYAAACYCXXQAAAldUlEQVR4Xu2df5xNdf7HjUEREWry\nuyUNIUQISbVSQkm7JCmbH+NnWSwx2WRDIWpKaMc2RVtCfmyIxqCE2uy3oiWr1NYqbbEUpnb3/fX8\n2HO7zj333nPv3B9nZt5/PB9j7nk59965577O+/P+vD/vTwmRN0VRFMULlLA/oCiKkizUkBRF8Qxq\nSIqieAY1JEVRPIMakqIonsFnSD/+uDngoBOR6GKN/TmcUJ0zqnNGdc4kS2cMCfG8eaPD/qdIdAMH\ndpXBg7tJRkb3oHC8S5fWYXXw4IP9XT2v29enukBU54zqnIm1DuISIaHBZEqUKCHnnVdOLrywUlSk\npVWUUqVKmp/bt88PeB4n3Lw+1QVHdc6ozplY6+KSQ+LJiWowo+eemyjvvPNMVGBCt956lTEnfrc/\nj6IoRYu4GlIoI/nPf7YY3Q8/bjI/+d2ucXOeosq//x2YQ4sHPA9/+//+942A16AoiSbhhvTv/2yW\nDz7OkVkvD5OeUztIt8w20mVya5m5ZKh5nONuzlOUwSSysu6VIUNujgv8TXv0aG/yd6NG/UJmzx4u\nK1ZMlU2bsuSDD3Lk+PFc8xrsr0tR4k3UhvT996/Ltm3z5ODBlQHHghnJifxcWfCnsdJgRC2Zt3q0\nHPhqqRz8doWs2jZN0kfWlIuHXWiOowt1nqIO7xvjKGgOLhjk5MqXP0vOOquU72dKSoqcfXYpqVPn\nfLn66stk4sQ7ZePGx+Wbb9Y4Rq+KEg+iNqQ33nhKqlc/z9xd7Resk5EQ+WA25ww6S4ZkdZdjJzbI\n7OUjZMwzveTI9+vk2bUTJHVAijmODr3TeYoDliEVNAcXii1bnpS8vCfMTyKjV199VGbMGCK33dZB\nmjS5yBgVtGnTUB5/fKT87W8vatSkxJ2oDIkvzOjRvaR27arSunUD+ec/Xw04bjcShmNEQKUHlpR1\nO2bJrgM58rNhaZK5sJ/JI733SY7UGlpVSgwoYXTorfOk1awk23fMl/9K0c9z8B5PnMyVwRndEm7E\n3Fh++GGTfPHFK8asxo7tbcyJmc6GDWvJI49kyGefLdN8kxI3ojKkjz9eYu6cq1ZNl6ZN68prr806\n47jdkLjQZ7w01JhNxYxy8tbupyVv5xPSaky67PviRdmxb4F8eXilNBtR12gAfX5+ntwzqouk9E6R\n6zNbyJq3Z8o7Hz1TpOE93vxQW6l6Z3lJuzKxhmSHzxEDWrhwvLRqlW6MiRvQ0qVT5MSJ08NqRYkl\nEdchcQddvHiSMRwuygkT+sqvfnWjedz/XNQhWYbE7zf8tqUxmupDKsvO/dmy8e05smTzZNm6a65M\nXzJYjp98Xdrc19BnSOiPnzp/x9FNfY8xnEsbUqlIw3u03m9a34ryzp9DG5Lbz60gOm4o5ArnzBkh\n9epdaIZy999/h4mk7Fo7TudzQnXOFDddxJXajz6aYe6S69bNNCZE/qFBg5qye/fzZ+iYwbEMiSFZ\nuzGNzJesSkZ52bZnnomMPvt6mYkGspbfK4eOrJbmI+v5vozo7YZU3AhnSJF8brHQkUP6y18Wyi23\ntJPSpVPlhhuukL/+dXHQIVy486lOdXYijpA2b86SGjUqm5mYm25qLddc00wuuOBcWbBgrC+5zbmC\nRUipg1Il9505Jmk9f/UYOWtQKVmzdYZ8+Nkik1OyvozoyaVYQ7aWo+rLgKybZMjTNxdpeI9Xj79M\nKvd1N2Rz+7nFUnfo0GqZMuUeKVeujFx5ZUN5993skKZkf8wJ1TlT3HQR5ZA46bhxfcysy9//vtyE\n7J9//opkZ48zBnXkyDqfLlgOCe7P7iMn83Ml8w/9pOeUDvL518tlWd4USRlY0qcxOaQf8s5Iav/4\n79OFfEUZ3mOyktqRwHD9ySfvMzOBLVvWl/ffzwlqSorilogM6cCBpSaZ7T88g/37XzKzMQzf+N1u\nSDxmzbJhNjWGVpGVb02Vo8fXy3fHN8i7e7Ol9dh0nxnZZ9m8/MWMB7xvpv29/r4ZshMZV6hwlnTo\n0MRcB3aNokRCRIbEjAumw53c/3F+Zyj3f//3B3OXdDIS/zokkx8ZXEE6jGsinTIvlzpDfxqqaR1S\n4TEkyM/Pk8ceG26KK/v1u14OH14boFEUt0RkSG4JZiRWpbYVKdnRSu3TFCZDgqNH18uwYbeYRDcz\ncW7zBYpiJ6GGBNZaNtaukbhuN7qR+alr2X6isBkSMJwnwc3Sk8LymhXvEVdDsvoY8bsdEtYkb0mO\n8pPf7ZqTJzeeMVtnf56iSmE0JIbqFMqee+7Z0qfPdXLs2PoAjaKEI66GRGUv/Yz4dzRgRunpNQrV\nFzMWFEZDAroEDBrU1SS5qVPTWTclUiKuQ3Kj84+Q+FIFg+OsMA+nu/jiarJjx4KA53HCzevzus76\n+7kxJDfnS6SODhB8nj17dpDvvtsQVGdHdc4kWkeJjik/+fF0GYr9uJ1w54tUF3GltlsdPbAZrvGF\nCgbHqWsKp8OMZs0a5up53b4+r+v8K93tx6M5X6J0zLr173+jVK58jlmgG0zn9nyqi78OE/r22zWm\ng8ezz04wi6q7dm0j06YNMl0gPvxw0RlLw8Kdz45bHcQlQlJdcNzo0BTWCAnWr39MypYtLQ880M/k\nAe3HnQh1PtUFPm4nWh1lGosWPSDt2zc2+b/U1JLmZ9Wq5U0pR8mSKVK3bpqZRX3vvWcDoib7+YLh\nVheXHJJSMPjwCmMOyYKlJVRvt2hR3/zbflzxBhSy3nHHz6VMmVSzaBrTISIiUmLUQoT79NOj5brr\nmpvUSv361SUnZ4KJgu3nihVqSB6ksBsSd1H6ZVWsWFbefHNuwHEl+WBGrEPFjIYP7yG7dj1nrjur\nINnqdQ9EUS+++KA0alTbRE9z5/7adcQTKWpIHqSwGxJwpyX8Z52jvaOoklwwGCsyounev/71Wthe\n9xgUi6iJfFlMv2bNjLjMoqoheZCiYEg7d2abrhAsJ4nX3VSJHG4O5IysyAgzctvr/vjJXLN0rGbN\nKnLVVY3lyy9XBZybCSii4q1b55qcE7337a8hFGpIHqQoGBK5o2bN6ppFt/HMOSiRwWwaCWxyRuww\nE2mv+5P5G2XSpLtMjeHLLz90RpTETFzHjk3l5pvbyl13dTaV+7fffm2AcYVCDcmDFAVD4uK85rpm\nclmzi+Qf/1gRcFxJLPRqp7XNps1ZJg9EApvrLJpe91yT1apVMhtC+JcD8G8ipw0bZptzszEEeSeS\n4/bXEww1JA9S2A2Ji3/n3mxJH1BDLrijgixeOymgd7iSWEyv9intpOGg2pLaIsXk+IiOoul1f/TY\nehNl0U/fP/qxDInts/id/mhXXHGJ73c3aB1SGJKhQ1OY65C4E99y6uL3bylj7x2uJBb/Xu3l+5wt\nb7z5lPkMo+11T3RUq1ZV09LY+twtQ8LsWGxNI8e2bS+VTz9dGvJ68SduldqqCyQSXWGt1DbHbYak\neIuqfcrLtu3zCtTrnhwRLYzZ7MG6DixDIiqi3zpRPp1EeTzU9eKPRkhhSIYOTWGOkBiybXnvSanZ\nv6qUub2U/PJ3HQN6hyuJhV7tHcc3lfq/qiZntyxl8jp8htH0umcRNYbDGlM2ebA+d8uQVq6cZir0\n/a+RUNeLP5pD8iB8eIU5hwS0k7mxyxVyyaU1ZN++07veKsmDqJWIaPXq6aY+jApsrrNoet0fODUE\na9y4jskj+U/r23NI0aCG5EGKgiFxF2Xalw0m6ShpP64kBxbKsjaN5SAUSEba6/79/TnyyisPm3Vu\nLKDH7KxzqyEVUYqCITHle8klNcxWWW7DdSX+YBpM+bM2jeUgRE1ue93PP6X7x8EVcu21zaR69fMC\nrk0KIxkK0nvf/rxuUUPyIEXBkFigSb0LSU//u6iSfKigZqEsNUIsB6ECO1yve8zom8NrfEWREyfe\n6diSpKCoIXmQwm5I3CnZHolcxdq1MwOOK8mFGwSr9rlhsDaN5SBUYAfrdc8wjcjot7+92wzVOndu\nafZjtJ83FqgheZDCbkj5+Xlmu+2LLrrArCK3H1eSD58Rq/ZZKMvaNCIfrjWKHpnWNxzPNQlsckYM\n04iMMKOPPvpjwPlihRqSBynshsT+fBTNYUpuG7QpiYfrjFX7JKIxG5aDMHNG0ePdd99gpvaZTSMq\nImfEMC1ekZGF1iGFIRk6NIW1DonhGlPKDNdM0tRlniHY+eyozplodSyOZfkHC2UxIpaDcDOh4yd5\nJgyK2TSuQ6fP0n6+YLjVaaW2w3Ev6AprpTYLaclLcGel/iiYzu35VJcYHcaE4WBOLAcZP76P7Nmz\n2NQZBZuUCHW+aHSgEVIYkqFDUxgjJKIjmsQT/s+YMeR0QZ6DzgnVOVPcdJpD8iB8eIUxh0RbVHog\nXXpp7bgmPpWiixqSBymMhsSsDUnP0qVTZf78MUHDfEUJhRqSBylshsRQbenSKVKpUlmT+/rnP18N\n0CiKG9SQPEhhMiSSoUzzk8Rmqcif//z7AI2iuEUNyYMUJkNiJo2+2VT9Pv98pg7VlAKhhuQx6CV0\n4mSuDM7o5mlDIjLCjG68sZVZqPnYY8O1mb9SYNSQgvDV4VWy6S9ZpscwzcbsPYrjhel9/FBbqXpn\neUm70puGRM6IYRqREWY0Zco9EW93oyhOxLUOKdbYn8OJWOkwo/IZZU3nvLKD6Ql9bkCf4njg3/s4\nrW9FeefPoQ0p3PuItS7/VBREApucEcM0IqNQZhTufKoLTXHTxa1Se+DArjJ4cDdT4BcMjjMrE04H\nlK+7eV63ry+cjsgIM7K3Ykgk4QzJzfuIlY6oiDqjCRP6mtk0EtjkjDAou9bN+VSnOifiEiGhwWRK\nlCgh551XzuRCoiEtraKp+uXn9u3zA57HCTevz42OYRqREcaQ/uuaMnhut4A+xfGA3sdXj79MKvd1\nN2QL9z4KqsOIWA5CBTZFj9QZcRNhNs1NAtt+vmCozpnipotLDoknJ6rBjJ57bqL5UkUDJnTrrVcl\nJblLPodhGoaEGZ38YWNAn+J4QO/jZCe1MSEiH/JELJRlbRo3BiqwKXrUOiMlXsTVkEJ9objo0dFC\nk5/8bte4OU+8OG1IlYwhEblgFnZNvOB9M+1vRYb8Hm/ofUPbWTo9PvPMb8x2yKz6ZtU++SLWprEc\nJJF/B6X4kXBDYpsVOtPNenmY9JzaQbpltpEuk1ubznQ8znE354k3XjAkohIiRP4dS/ib9ujR3vS7\n4SdT9zTkJy9EohoTorkapvTSS5Plk09eTuj7V4ovERsSkcyOHQvkzTfnyltvPS17975gvkD+mmBG\nciL/dO/eBiNqybzVo+XAV0vl4LcrZNW2aZI+sqbp3ctxdKHOkwje3rvAN2TLeLq7GUrZNfGC9z18\neI+AnFqsIPIqX/4sM2Vfo0ZladCgptkdhIb89MCm7SydHmmuRr2R/fUpSryI2JDomdKxY1Pp1u1K\n+cUvrpbmzev5Wk1YGicjIfKxdjcYktVdjp3YILOXj5Axz/SSI9+vk2fXTpDUASnmODr0TudJBJ9+\nuVQm/L6vbz+qnz9wuXx8cEmALl5gAvSisefUYsmWLU+aXsr0vvn44yVy7Nh68/fWSEhJJlEZEi0v\nN2yYbf69ZMlkY0pffbXap3EyEmv/p9KnvuTrdsySXQdyzI6YmQv7mTzSe5/kSK2hVY0BoENvnSet\nZiXZvmO+qWK2v55Y88kpM7p2YvOAKXge45hdryhK7IjakHJz55i76YoVU00u4rvvNvg0dkNimGft\nkFkxo5y8tftpU+fTaky62Ut8x74F8uXhldJsRF2fAaBnpueeUV0kpXeKXJ/ZwlQx2yubYwnDNCIj\nuxlZTH1h4Bk5LkVRYkvEdUgnTuSaPrsPPzxQZs0aZhKi1KT45xo4F3VIliHxu7WHePUhlWXn/mzZ\n+PYcWbJ5smzdNVemLxksx0++Lm3ua+j78ps9xE89V8fRTX2PMZyzVzbHlnPP2DbYztXjm556L5sC\n/iaR/P1U54zqnCluuogrtWfPHi4/+1mayRtRqct6JqaJ/RuAo/PvCc2QrN2YRuZLXSWjvGzbM89E\nRp99vcys28pafq8cOrJamo+s5/vyo7cbUrIJZkiR/P1UF4jqnCluOog6QmL/bqKi99/PMQVz27bN\n82k4V7AIKXVQquS+M8cMfeavHmOWZ6zZOkM+/GyRySlZX370FAhaQ7aWo+qbKmZ7ZXMsYTaNBLbd\niCxCDdnc/v1U54zqnCluugLlkMgNsY93kyYXGYOyNDx5sBwS3J/dR07m50rmH/pJzykd5POvl8uy\nvClnDJdMDumHvDOS2ky92yubYwnnZzZNk9qKkhyiNiTqVdj5ksK6665rLp9++tOX1W5IPGbNsvHl\nrjG0iqx8a6ocPb5evju+Qd7dmy2tx6b7vvz2WbbiNu1f3CDSzs/PC3jcruF6sLBuItzstFaq6BCx\nIXEB5OU9Ia+/PtvAv1l86a9xMhL/OiS+5GmDK0iHcU2kU+blUmfoT0M1L9QhQTILI4sTfMbLlv1O\n7rjj5/LNN2sCjltQKzVyZE9ftflvfnO72Ws+K+teU3rCtUhdFdcJleWkFji305IkxbtEbEhuCGYk\nVqW2FSnZ8VKlNmUAzLzxusgvcTe2a5SCw9+VTQnZrhljChbtcC2MG9fHdJBISUkxC7dZ5lKmTKr5\nHag8pwqdyvO2bS+VXr2ukZkzh8r69Y+ZAtCjR08XfwZ7DiX5JNSQwFrLxto1EtftRjcyP3UtW/GF\nrgK1a1eVTp1ayOHDawOO23X16l0oq1ZNNwuBrWh9+fKHzcwvkymdO7c0HQrQYnSszWOJTJs2DWXo\n0Ftk5cppvqUxGkF5i7gaUqjV6iSsmUUjtOYnv9s1XDD+s3X254knakiJgep7yjuGDb9FypYrbcwi\nWATDNfHrX//S7Dtv1/FvXweJHzbJkSPrzAwwhkVZSp8+18nll18slSufIyVLppjFw5SmLFw43hid\nrtvzBnE1JGu1Ov+OBswoPb1GUgxp2575pmYKQ7r1kQ6yfe/8gMpupeCYHuJT2kqdgedLiRYl5IYb\nW8quU5FyMHOgCJdop3v3tiFb5/pjGRV9nFgQnp09zqzFpJ4Oc6LNym23dTBRFvlQvfkkj4jrkNzo\n/CMkzCQYHLfG/fZj/lx8cTXTYcD+PE64eX1udHk7s3wtbFl/l6ie2sUN/x7iJXqXkJLnpsiwmbcE\nNQX6Nt15ZyepUqW8bN06N+C4RajP12pAt3v385KTM8GYW7VqlUw3TNZlknfimP85Qp3PH9U541YX\ncaW2Wx09sBmuEdkEg+MkKsPpMCOWqbh5XrevL5zOCz21ix13nKJ8CenSu/UZlf/+nxsdLP/0p0fk\nnHPKyKhRv3D8DN18vpaO0hXWYRJ5TZs2yLTpJbInT0Vpy3vvPWvSCm7Pp7pA3OogLhFSUdC9vWeB\ndJ3SWm6YfIXcOq29ZMztHlDZrRScfrM7SfuxjaX9mMbS7cErpVZ6VTNMp3ul/TOxPjcS39TCMZsW\nSmd/zAl/HVHZ55+/IosWPWDOzwweuaYHHuhnIqZgUVuw84VCdc7EJYdUFPjPf7eY2iP+kObn/wrx\nlNjC35W1jsDEBhELs2Ivv/xQ0DwSQy4ipXC6aOF85JvolokxMZRjeRSvjTY7sX4+5SfUkBRPsXNn\ntkla9+zZIWT1tltdQcB4Dh1abWbirKHctdc2M3VN8XrO4o4akuIpmH5nBqxOnfPlgw9yAo5HqosF\nRGRUilMZziRL1arlJTOzn1nHqdFSbFFDUjwFX372gGM6PlTltltdLGH4vnlzlmlISLRkdb1wmx9R\nwqOGpHgOZlUvuOBcufvuG0J+2d3qYgnGRx7p0UczTLRUvfp58vjjI00hpl2rRI4akuI5WHPGWrSm\nTesGLNyORhcPMED6yrMchdm4QYO6yoEDSxMSqRVl1JAUz8HsGzVGlSqVNdtt2Y9HqosXmM/+/S/J\nPfd0MTNx7MZDsl3Xx0WP1iGFQXXOxFPHF53NI8gP/fGPvz0j6ohGF4pY6KiLeuSRDKlYsaxpVsi+\ndpilXef2fMnUYaamHOPH02UZ9uN2wp0vUl3cKrVVF4jqnHHSWfmhAQNu8j1eEJ0TsdRRBvDccxPN\nrB8sXjwpqN7N+RKpw4S+/XaN6Z7ARMHYsb2la9c2pnL91VcflQ8/XBS0ct7pfHbc6kAjpDCozpl4\n6778cpXJDbGJhH/NT7S6YMRSR0Sxbt1Mady4jikNWLBgrOMX2e35EqEjuqMynRlDaxt1fvL6ad1C\n9Fm3bpoMG3aLWUZjj5rs5wuGW53mkBRPwheZ1shUSPu3R7bjVpcoiDbY8KJFi/pmCPfUU6M8W0RJ\n/otOnSTlWbuH6RARESmxvpTWLVTE8/dlEXz9+tXNYuR4vh81JMWTcEelVe3551cwXw778Uh1iYRc\nFh0qW7duYKINTClYpJQsMKNrrmlmzGj48B6mYR1/S6t1NEt5+AlEUS+++KA0alTbvB+W0LiNeCJF\nDUnxJEQa9Mtm9sp/Rxs7bnWJBlNiiIMpESnRJC5eX+JIwWCsyIhk/L/+9Zqvk+usl4dJz6kdpFtm\nG+kyubWvkysG9e672aYTJzm7NWtmxKXEQQ1J8SRc7KtXTzc9tJm1sh+PVJcMrEiJ4Rs5GRLd9hxM\nosHAyRlZkRFmZPW6bzCilsxbPVoOfLVUDn67QlZtmybpI2v6et0fP5lrNlKoWbOKWXRM/s5+fgpE\n6VPFej+0DKMjMS41JMWzsPcfSVaii1C1PW51yYAvI0NJEt3MvmGayXyNzKaRwCZnxBpA/92AhmR1\nl2MnNsjs5SNkzDO95Mj36+TZtRMkdUCKbzegk/kbZdKku8zSGXunBXZ7oXne7bdfa4Z11Igx2YA5\nuX3PakiKZ2HdWLlyZWTKlHtCRhZudcmCL+Nrr80yvZUwJprBMQSin7hdGy94Llq9bDr1tyIPRAKb\nIaS1XyJdUdftmCW7DuSYHaQzF/Yzr/G9T3Kk1tCqpoGetV8iTRPpsEnbXys3xmJnIi6a2hEl8Z45\nxhZVV1xxiTEr+2tyQg1J8SxUX5N/YZukUEbjVpdMeF0M2Sq2KisX968mN09pZ/qJ23uMx4vTvcvb\nScNBtSW1RYqZTSM6snaUrphRTt7a/bTplNpqTLrs++JF2bFvgXx5eKU0G1HX19UT/dFj602URbmF\nNWxjowRmOskz+b9vunFef32LgMLVYGgdUhhU50widEyf0zubDSKt4wXROZFIHVFEu/sa+b7cDIPs\nPcbjhX/v8vJ9zpY33nzKvFa2IOOx6kMqy8792bLx7TmyZPNk2bprrkxfMliOn3xd2tzX0Pd/0bNL\nDNERmyOQI+O9kS8iV0ZjO/vfg8+FjT3d3Cy0UtvhuOq8oaMKm+l89lLjWEF1dhKt4/HOk04bQDKp\n2qe8bNs+zwzJ2o05bZDssLNtzzwTGX329TK5+aG2krX8Xjl0ZLU0H1nP93/RY0h33dXZDJMZovG+\nmOFkaGbveoAJsXXVTTe1Dvp38UcjpDCozplE6NiyiB1qR4/u5bu7FkTnRCJ15FGu6HaJlLm9tHT4\nTRMZkHVTQI/xeMFzdRzfVOr/qpqc3bKUKXrktVoRUuqgVMl9Z44Zxs1fPcZscLFm6wz58LNFJqdk\nGZKJkI7nmp5Q7Ab0178uNu+NvBJDNnuzvPz8PNNIb86cEa4S25pDUjwLFcMVKpxlmuyHCvfd6pIJ\nPZT69u10uvbn0QwTZSSyT7vVu5wSCWYkqcDGkKwcEtyf3UdO5udK5h/6Sc8pHeTzr5fLsrwpkjKw\npE+D/sCnS01ynjyStTfesWPr5Ze/7CizZw/3JboxoC1bnjSbMbz9trttzNSQFM/CXZz1VOyTFuru\n6laXLBjGEL1RvMlUOLU/dk2iYKEsa9NYDkKBpDXLhtnUGFpFVr41VY4eXy/fHd8g7+7NltZj031m\nhO79/TnyyisPm783W51hdta5KQRlmp9FuWxvThKf3YKffPK+kJGjP2pIimehAVpKSkpAvYsdt7pk\nwCzT5Mn9TWREdfTBgysDNImE6IUpf9amsRyEqMmqQ8J00gZXkA7jmkinzMulztCfhmocn39K94+D\nK8xGB3TKZJjmf27+9hRCYljUKtGBgUjq+eczfduV21+PHTUkxZNwcVNRzGpz7rb245HqkgHDGZZm\nEE106dLaE4t/gUiGhbKsTWOangpsTMmKlOzwOGb0zeE1vqLIiRPvDLo+j8+EyInjDNVIatPZkxtH\nuBuGGpLiSbigGRKwQy15CPvxSHWJBjOi7zaRCMMjFrPaNcmCvxmr9imQZG0aU/ZUYDN8Y+0aiet2\noxuZn/zOMI3IiF1XMNfOnVuaDTXt5w0GwzX0boZtakiKJ+HiZc+1cNscudUlEnp9P/zwQGNGDG8+\n+uiPAZpkw+wXyztYKMvaNCIfhmAUPZJwNxzPNQlshmC8DyIjzCie70cNSfEkRBg00OcObq9tiUaX\nKCgMZDhDzogK5X37nLf69gKYOav2WSiL2bAchJkzih7ZyYWpfXJAREXkjHhfkURG0RDXOqRYY38O\nJ1TnTGHT7dmz2CwApZWq/7FodcGIpe7vf18uGRndzWxajx7tzeaSdk0k50uEjpwOyz+YEMCIWA5C\nBXbZsqVNngmDYkhM9OSUM7KfLxhudXGr1B44sKsMHtzNfEDB4DjJvnA64I/i5nndvj7VBeIlHVP5\nDHmmTh3om1ouiM6JWOn4UjOdTjUyZsS1HyqSCHe+ZOh4DxgO5sRyENYFYvZEoP5T+27PF40O4hIh\nocFk6FFDBS0b6kVDWlpFE0ry0203QDevT3XB8YKOWiJqV/jsmZkpqC4UBdXxOCv5qbdhKQU3Tvt6\nLieCnc9OcdPFJYfEkxPVYEbsxEC4Fw2Y0K23XmXMid/tz6MUTbhT87mTqH7//ZyA45Hq4gUFjhgi\n+RUSw/RjIhFs1ynuiashhTIS7m7orN69ThW2bs6jFD1Y89WwYS3T8znUF9ytLtZwre7d+4L073+j\nSV63apVuaqCCDW0U9yTckML17uW4m/MoRRc6DPJFp44n1JfcrS6WkFOhwpnkL7NP5Iv+9rcXwxb8\nKe6IypC4QzCdSUKR8TM/TcXn/+5SwYzEbe9edKHOoxRdMBY2KmSxLJ0g7ccj1cUKno+dOTAgijCZ\ngfr978eZmiO7VomeiA0Jk6DKk9oPLoiFC8ebjDyzZcw0WBq7kUTau9fajsV+HqVow1qv5s3rmbqi\nr7/+U8DxSHUFhcjniy9ekSeeuNeYEDN6rElz2jRRKTgRGxK9Z+h7QkMmK/fDB8MiQmvxnJORRNO7\n1zpPWs1Ksn3H/IT2IFYSg9XrGfjys/MrX3oWpIb6wrvVRQuvhdmyF16YZG6+zOTREZHfNSqKHxEZ\nEh887RPozOdUJGVhNyRMK5revZS33zOqi6T0TpHrM1sktAexkhisXs+w8o3pcuddnaRy5XPMVjr2\n68qCa2/QoK5hddHAtXro0GqTJ7r66stMjopGZNOnD5YDB5Y6Tr4osSOiOiQ0lJPTTiBUEg8ddUiW\nIZn/F2Xv3o6jm57RAsHeK1gp3Pj3ei7dP1VSKqVIm/YNg0YhXEu7dz9vqrNZtBpKZ3/MCUvHT2bO\n5s8fYzZ3pMCRXUJo0UruyE3rDP/zhUN1zkRUqc2diQZML700OawhkVOyDKkgvXv9DUkp2qT0PvXz\nnBLSb/z1ZgjndF1R90MjNroe0nbE6Tp0ez1jMlR4MzHDFj6XXFLDnJdSAla2U9vEOdyeT3XOuNVB\nxBESswz0Nwml51iwCCmS3r0nTub6hmwtR9VPaA9iJTH0m91J2o9tLA2H1JYSLUvI+bUqyOylI84o\n//CHBDPN5Js0uShkfyGn6xPz4nES4swM0/LWWrdFKw5utsycMY1vz0s5nc8J1TnjVhdRDokPdNWq\n6ZKeXsM0XrLG0zx+4lQ0Eyyp7Z9DAre9e/N/yDsjqZ3IHsRKYuAz5XPOeW6CpJYqaTZ75Hf7tWdd\nZ+zvxXAq3KaQ/k3CMDFyTbRUZWdVaohY5oERNWtWV8aM6WV6AtHSVXNEySUiQwIKwzIz+5kpV8bb\nVKhykfTufa0Z26OxGxKPRdq713+WTaf9izbMZhGdkBeyriEnLB25HVqicn1gOMAyDiIbbpREP6xe\nHzeuj8l5Ek2xjImuklxLdC+klQZbcBMtub17K/EnYkMCIiF2C83OHmfG2tQisVlfsAiJx/zrkDCd\nUL17tQ6p+EAkg3kwm4VJBDMHfx2za716XWPaZdBziH4+1CORA2IhNhp6bLObLdE8s2X33XebrFgx\n1WxjzQ4ZoaIrJXlEZUgWVg2SPcwNZiRWpXao3r1aqV28yM/PM4WGREcUG9qPWxAdderUwlwLULt2\nVbN7BjVx1AfRt4eJFK4X9gBbu3amuWnSOpYbJdepUwJc8RYFMqRghDISay2bU+9eXctWPPnmmzVm\n+UeoqAUN0Q3XAWBerAwgsU3uh2Eb1wvYb5BK4SGuhmT1MbIuFH9IXDKLRjKcn/xu13Bn85+tsz+P\noihFi7gaEuX29Kvh39GAGZEDUENSlOJBRHVIbnX+EZI15neC46xHCqejdH/HDndb8bp5faoLjuqc\nUZ0zsdZFVKkdiY5WngzXrDG/ExxnajacDjOaNWuYq+d1+/pUF4jqnFGdM7HWQVwiJNUFR3XOqM6Z\n4qaLSw5JURQlGtSQFEXxDGpIiqJ4BjUkRVE8gxqSoiieQQ1JURTPoIakKIpn0DqkMKjOGdU5ozpn\n3OriVqmtukBU54zqnCluOtAIKQyqc0Z1zqjOGbc6zSEpiuIZ1JAURfEMakiKoniG/weGsDMUzTrZ\nIgAAAABJRU5ErkJggg==")) image_1: pin names not known
  // Callout #(.background("#ace8b5b5"), .dx(-6), .dy(-11), .halign("center"), .text("4-bit input\npin"), .valign("top")) callout_4: pin names not known
  not not_2 (out_14, inner_1_q);
  assign Q = ~P;  // NOT_Gate not_3, 4 bits wide
  // Callout #(.background("#e3a5e8b5"), .dx(10), .dy(-10), .halign("center"), .text("4-bit output\npin"), .valign("top")) callout_5: pin names not known
  // Callout #(.background("#ace8b5b5"), .dx(30), .dy(-15), .halign("center"), .text("12-bit input pin\n(hexadecimal display)"), .valign("top")) callout_6: pin names not known
  // Callout #(.background("#e3a5e8b5"), .dx(2), .dy(-23), .halign("center"), .text("8 bit output\npin (hex)"), .valign("top")) callout_7: pin names not known
  // Callout #(.background("#e3a5e8b5"), .dx(-54), .dy(-26), .halign("center"), .text("2-bit and 1-bit output\npins (binary display)"), .valign("top")) callout_8: pin names not known

  assign out_9 = in_3[11:4];
  assign out_10 = in_3[3:2];
  assign out_11 = in_3[1];
  assign out_12 = in_3[0];

  // Notes on the sheet:
  //   outer circuit, with inner subcircuit
endmodule

module inner (
  input  A,
  input  B,
  input  C,
  output P,
  output Q
);

  and and_1 (P, A, B);
  xor xor_1 (Q, B, C);

  // Notes on the sheet:
  //   inner circuit: takes three 1-bit inputs, A, B, and C, and produces two 1-bit outputs, P and Q,
  //   where P = A * B, and Q = B ^ C.
endmodule
