// Logisim project tick-test.circ as structural Verilog: 1 circuit, main circuit main
module main (
  input  in_1
);

  wire clock_1_out;
  wire [31:0] counter_1_q;

  Clock clock_1 (.out(clock_1_out));
  Counter #(.max('hffffffff), .width(32)) counter_1 (
    .count(in_1), .Q(counter_1_q), .clk(clock_1_out));  // open: load, D, carry, clr
  // Probe on counter_1_q

  // Notes on the sheet:
  //   kwalsh notes:
  //   Mac laptop reaches 1.7 MHz
  //   old Linux desktop reches 650 kHz
  //   Windows laptop reaches 250 kHz
endmodule
