// Logisim project vga-joystick.circ as structural Verilog: 1 circuit, main circuit main
module main (
  input  EnableDrawing
);

  wire clock_1_out, clock_2_out, clock_3_out, clock_4_out, Reset_out;
  wire [1:0] joystick_1_x, joystick_1_y;
  wire [5:0] adder_1_out, adder_2_out, bit_extender_1_out, bit_extender_2_out, X_q, Y_q;
  wire [6:0] rgb_video_1_p8;

  // Probe on joystick_1_x
  Joystick #(.bits(2), .mode("twosComplement")) joystick_1 (.x(joystick_1_x), .y(joystick_1_y));
  // Probe on joystick_1_y
  assign bit_extender_1_out = {{4{joystick_1_x[1]}}, joystick_1_x};  // Bit_Extender bit_extender_1
  assign bit_extender_2_out = {{4{joystick_1_y[1]}}, joystick_1_y};  // Bit_Extender bit_extender_2
  Adder #(.width(6)) adder_1 (.a(bit_extender_1_out), .b(X_q), .out(adder_1_out));  // open: cin, cout
  Clock clock_1 (.out(clock_1_out));
  Adder #(.width(6)) adder_2 (.a(bit_extender_2_out), .b(Y_q), .out(adder_2_out));  // open: cin, cout
  Clock clock_2 (.out(clock_2_out));
  Button Reset (.out(Reset_out));
  Clock clock_3 (.out(clock_3_out));
  Register #(.width(6)) X (.D(adder_1_out), .Q(X_q), .clk(clock_1_out));  // open: en, clr
  Register #(.width(6)) Y (.D(adder_2_out), .Q(Y_q), .clk(clock_2_out));  // open: en, clr
  // RGB_Video #(.cursor("No Cursor"), .fixed("2b#Atari 2600 (7 bit)"), .height(64), .scale(4), .width(64)) rgb_video_1: pin names not known; wires that end beside it: clock_2_out, clock_1_out, Reset_out, clock_3_out, EnableDrawing, X_q, Y_q, rgb_video_1_p8
  Counter #(.max('h7f), .width(7)) Color (.Q(rgb_video_1_p8), .clk(clock_4_out));  // open: load, D, count, carry, clr
  Clock clock_4 (.out(clock_4_out));

  // Notes on the sheet:
  //   Enable the clock at a moderate slow
  //   speed (like 8Hz), turn on the EnableDrawing
  //   input, then use the joystick at bottom left
  //   to draw.
endmodule
