// Logisim project wiring.circ as structural Verilog: 6 circuits, main circuit splitter-examples
module splitter_examples (
  input  [2:0] in_1,
  input  in_2,
  output out_3,
  output out_4,
  output out_5,
  output out_6,
  output [3:0] alternatingBits,
  output [3:0] bottomHalf
);

  wire clock_1_out, clock_2_out;
  wire [1:0] joystick_1_x, joystick_1_y;
  wire [3:0] slider_1_out;
  wire [7:0] dipswitch_1_sw8;
  wire [7:5] callout_9_p2;
  wire [11:0] counter_1_q;

  // Callout #(.background("#81e6df80"), .dx(48), .dy(23), .foreground("#2e5c56"), .format("wrapped"), .text("join eight signals into one 8-bit bus"), .textwidth(117), .valign("bottom-overall")) callout_1: pin names not known
  DipSwitch dipswitch_1 (
    .sw1(dipswitch_1_sw8[7]), .sw2(dipswitch_1_sw8[6]), .sw3(dipswitch_1_sw8[5]), .sw4(dipswitch_1_sw8[4]),
    .sw5(dipswitch_1_sw8[3]), .sw6(dipswitch_1_sw8[2]), .sw7(dipswitch_1_sw8[1]), .sw8(dipswitch_1_sw8[0]));
  // Probe on slider_1_out
  Slider #(.width(4)) slider_1 (.out(slider_1_out));
  Joystick #(.bits(2)) joystick_1 (.x(joystick_1_x), .y(joystick_1_y));
  // Callout #(.background("#81e6df80"), .dx(12), .dy(-12), .foreground("#2e5c56"), .format("wrapped"), .halign("right"), .text("combined end"), .textwidth(68), .valign("top")) callout_2: pin names not known
  // Probe on joystick_1_x
  // Probe on joystick_1_y
  // Callout #(.background("#81e6df00"), .dx(-18), .dy(39), .foreground("#2e5c56"), .format("wrapped"), .text(""), .textwidth(37), .valign("top")) callout_3: pin names not known
  // Callout #(.background("#81e6df80"), .dx(-22), .dy(-14), .foreground("#2e5c56"), .format("wrapped"), .text("taps"), .textwidth(37), .valign("top")) callout_4: pin names not known
  // Callout #(.background("#81e6df00"), .dx(-20), .dy(8), .foreground("#2e5c56"), .format("wrapped"), .text(""), .textwidth(37), .valign("top")) callout_5: pin names not known
  // Callout #(.background("#81e6df80"), .dx(-29), .dy(21), .foreground("#2e5c56"), .format("wrapped"), .halign("right"), .text("split 8-bit bus into two 4-bit buses"), .textwidth(123), .valign("bottom-overall")) callout_6: pin names not known
  // Callout #(.background("#81e6df80"), .dx(19), .dy(18), .foreground("#2e5c56"), .format("wrapped"), .text("split 4-bit bus into four signals"), .textwidth(123), .valign("bottom-overall")) callout_7: pin names not known
  Adder #(.width(4)) adder_1 (
    .a(dipswitch_1_sw8[3:0]), .b(dipswitch_1_sw8[7:4]), .out({out_6, out_5, out_4, out_3}));  // open: cin, cout
  // Callout #(.background("#81e6df80"), .dx(-25), .dy(-29), .foreground("#2e5c56"), .format("wrapped"), .text("merge a motley set of buses and signals into one 12-bit bus"), .textwidth(123), .valign("bottom-overall")) callout_8: pin names not known
  DotMatrix #(.inputtype("row"), .matrixcols(12), .matrixrows(1)) dotmatrix_1 (.row0({in_2, in_1, joystick_1_y, joystick_1_x, slider_1_out}));
  Random random_1 ();  // open: clk, next, out, clr
  Counter #(.max('hfff), .width(12)) counter_1 (
    .Q(counter_1_q), .clk(clock_1_out));  // open: load, D, count, carry, clr
  Clock clock_1 (.out(clock_1_out));
  Hex_Digit_Display hex_digit_display_1 (.value(counter_1_q[11:8]));  // open: dp
  LED isOdd (.in(alternatingBits[0]));
  Clock clock_2 (.out(clock_2_out));
  // Callout #(.background("#81e6df80"), .dx(26), .dy(-26), .foreground("#2e5c56"), .format("wrapped"), .text("use splitters to pull out one bit of a bus, or a subset of the bits of a bus"), .textwidth(219), .valign("top")) callout_9: pin names not known; wires that end beside it: clock_2_out, {callout_9_p2[7], alternatingBits[3], callout_9_p2[5], alternatingBits[2], bottomHalf[3], alternatingBits[1], bottomHalf[1], alternatingBits[0]}
  Hex_Digit_Display hex_digit_display_2 (.value(counter_1_q[7:4]));  // open: dp
  // Callout #(.background("#81e6df80"), .dx(-26), .dy(-15), .foreground("#2e5c56"), .format("wrapped"), .halign("center"), .text("split 12-bit bus into three 4-bit buses"), .textwidth(262), .valign("top")) callout_10: pin names not known; wires that end beside it: {callout_9_p2[7], alternatingBits[3], callout_9_p2[5], alternatingBits[2], bottomHalf[3], alternatingBits[1], bottomHalf[1], alternatingBits[0]}
  LED isNegative (.in(callout_9_p2[7]));
  Hex_Digit_Display hex_digit_display_3 (.value(counter_1_q[3:0]));  // open: dp

  assign {bottomHalf[2], bottomHalf[0]} = alternatingBits[1:0];
endmodule

module tunnel_examples (
  input  in_1
);

  wire and_1_out, bar, clock_1_out;
  wire [7:0] stored_value, switches;

  DipSwitch dipswitch_1 (
    .sw1(switches[7]), .sw2(switches[6]), .sw3(switches[5]), .sw4(switches[4]), .sw5(switches[3]),
    .sw6(switches[2]), .sw7(switches[1]), .sw8(switches[0]));
  Button button_1 (.out(bar));
  Hex_Digit_Display hex_digit_display_1 (.value(stored_value[7:4]));  // open: dp
  // Callout #(.background("#fcff3367"), .dx(-46), .dy(-21), .text("All tunnels\nnamed \"foo\"\nare invisibly\nconnected.")) callout_1: pin names not known
  // Callout #(.background("#89feff67"), .dx(-49), .dy(-42), .text("A tunnel can appear\nas many times as\nneeded. All three\n\"bar\" tunnels are\ninvisibly connected.")) callout_2: pin names not known
  Hex_Digit_Display hex_digit_display_2 (.value(stored_value[3:0]));  // open: dp
  // Callout #(.background("#bdbf2667"), .dx(72), .dy(-26), .halign("right"), .text("")) callout_3: pin names not known
  // Callout #(.background("#ff9dec67"), .dx(-46), .dy(-11), .text("Tunnels can\ncarry multi-bit\nsignals")) callout_4: pin names not known
  // Callout #(.background("#bfffae67"), .dx(-38), .format("wrapped"), .text("Like wires and splitters, tunnels have no \"direction\"... values are carried from any tunnel to every other identically-named tunnel."), .textwidth(184)) callout_5: pin names not known
  // Callout #(.background("#6bc7c767"), .dx(54), .dy(-36), .halign("right"), .text("")) callout_6: pin names not known
  // Callout #(.background("#6bc7c767"), .dx(50), .dy(56), .halign("right"), .text("")) callout_7: pin names not known
  and and_1 (and_1_out, in_1, bar);
  LED led_1 (.in(and_1_out));
  Register register_1 (.D(switches), .en(bar), .Q(stored_value), .clk(clock_1_out));  // open: clr
  Clock clock_1 (.out(clock_1_out));
  // Callout #(.background("#97c98967"), .dx(-17), .dy(-57), .format("wrapped"), .halign("right"), .text("Values go into this tunnel, and appear near the hex displays at left."), .textwidth(99), .valign("top")) callout_8: pin names not known

  // Other names for the same wires on the sheet: foo = in_1
endmodule

module clock_examples (
);

  wire clock_1_out, clock_2_out, clock_3_out, clock_4_out, clock_6_out, clock_7_out, clock_8_out, scope_1_p2;

  Clock #(.highDuration(20), .lowDuration(20)) clock_1 (.out(clock_1_out));
  // Scope #(.samples(128), .scopeheight(40), .scopewidth(160), .width(1)) scope_1: pin names not known; wires that end beside it: clock_1_out, scope_1_p2
  Clock #(.highDuration(60), .lowDuration(40)) clock_2 (.out(clock_2_out));
  // Scope #(.samples(128), .scopeheight(40), .scopewidth(160), .width(1)) scope_2: pin names not known; wires that end beside it: clock_2_out, scope_1_p2
  Clock #(.highDuration(20), .lowDuration(80)) clock_3 (.out(clock_3_out));
  // Scope #(.samples(128), .scopeheight(40), .scopewidth(160), .width(1)) scope_3: pin names not known; wires that end beside it: clock_3_out, scope_1_p2
  Clock #(.highDuration(20), .lowDuration(80), .phaseOffset(15)) clock_4 (.out(clock_4_out));
  // Scope #(.samples(128), .scopeheight(40), .scopewidth(160), .width(1)) scope_4: pin names not known; wires that end beside it: clock_4_out, scope_1_p2
  Clock clock_5 (.out(scope_1_p2));
  // Callout #(.background("#a8ff9573"), .dx(31), .dy(7), .format("wrapped"), .halign("right"), .text("Default clock: 1 tick high, 1 tick low."), .textwidth(136)) callout_1: pin names not known
  Clock #(.lowDuration(4)) clock_6 (.out(clock_6_out));
  // Callout #(.background("#ffb55073"), .dx(26), .dy(2), .format("wrapped"), .halign("right"), .text("Unbalanced clocks with 1 high for every 4 lows. The right one is phase-shifted by 1."), .textwidth(136)) callout_2: pin names not known
  LED led_1 (.in(clock_7_out));
  Clock clock_7 (.out(clock_7_out));
  Clock #(.lowDuration(4), .phaseOffset(1)) clock_8 (.out(clock_8_out));
  LED led_2 (.in(clock_6_out));
  LED led_3 (.in(clock_8_out));
  // Callout #(.background("#a8ff9573"), .dx(-15), .dy(-1), .format("wrapped"), .text("Balanced: 20 ticks high, 20 ticks low"), .textwidth(118)) callout_3: pin names not known
  // Callout #(.background("#a8ff9573"), .dx(-15), .dy(-1), .format("wrapped"), .text("60 high, 40 low"), .textwidth(118)) callout_4: pin names not known
  // Callout #(.background("#a8ff9573"), .dx(-15), .dy(-1), .format("wrapped"), .text("20 high, 80 low, no phase offset"), .textwidth(118)) callout_5: pin names not known
  // Callout #(.background("#a8ff9573"), .dx(-15), .dy(-1), .format("wrapped"), .text("20 high, 80 low, +15 phase offset"), .textwidth(118)) callout_6: pin names not known

  // Notes on the sheet:
  //   Poke any clock to make all clocks tick once. Or enable auto-ticks in the Simulate menu, and adjust the auto-tick frequency to your liking.
  //   All clocks in a simulation are internally tied to a common tick source.
  //   Let's visualize different clock parameters! For this demo, it's best to enable auto-ticks and set the auto-frequecy to around 32Hz. The scopes capture and display one value per clock cycle (2 ticks), so the clocks at the left are set to use 40 or more ticks per cycle.
  //   Notice how the +15 phase offset makes the high pulse arrive a little earlier (15 ticks earlier than the other display, above).
endmodule

module constant_examples (
  input  [15:0] V,
  input  [1:0] select,
  output [15:0] out_3
);

  wire and_1_out, clock_1_out, comparator_1_gt, comparator_2_gt;
  wire [7:0] callout_2_p1;

  Random random_1 ();  // open: clk, next, out, clr
  Clock clock_1 (.out(clock_1_out));
  // Callout #(.background("#ff00e626"), .dx(18), .dy(14), .format("wrapped"), .halign("right"), .text("Hex constants, 16 bits each."), .textwidth(105)) callout_1: pin names not known
  // Callout #(.background("#ff00e626"), .dx(-24), .dy(-23), .format("wrapped"), .text("Two 20-bit binary constants, each used to control parts of 7-segment displays."), .textwidth(267)) callout_2: pin names not known; wires that end beside it: callout_2_p1
  // Callout #(.background("#ff00e626"), .dx(-24), .dy(-23), .format("wrapped"), .text("Two 8-bit constants in signed decimal format, used for a comparison."), .textwidth(267)) callout_3: pin names not known; wires that end beside it: clock_1_out
  _7_Segment_Display u_7_segment_display_1 (
    .g(1'b1), .f(1'b1), .a(1'b0), .b(1'b1), .e(1'b1), .d(1'b0), .c(1'b1), .dp(1'b0));
  Comparator comparator_1 (.a(8'h19), .b(callout_2_p1), .gt(comparator_1_gt));  // open: eq, lt
  Comparator comparator_2 (.a(callout_2_p1), .b(8'he7), .gt(comparator_2_gt));  // open: eq, lt
  Multiplexer #(.select(2), .width(16)) multiplexer_1 (
    .in0({16{1'b1}}), .in1(16'h8e96), .in2(16'ha5a5), .in3(V), .out(out_3), .sel(select));  // open: en
  _7_Segment_Display u_7_segment_display_2 (
    .g(1'b1), .f(1'b1), .a(1'b1), .b(1'b0), .e(1'b1), .d(1'b1), .c(1'b0), .dp(1'b0));
  _7_Segment_Display u_7_segment_display_3 (
    .g(1'b1), .f(1'b1), .a(1'b1), .b(1'b0), .e(1'b1), .d(1'b1), .c(1'b0), .dp(1'b0));
  and and_1 (and_1_out, comparator_1_gt, comparator_2_gt);
  DotMatrix #(.inputtype("row"), .matrixcols(4), .matrixrows(4)) dotmatrix_1 (
    .row0(out_3[3:0]), .row1(out_3[7:4]), .row2(out_3[11:8]), .row3(out_3[15:12]));
  // Callout #(.background("#4324ff26"), .format("wrapped"), .text("A multiplexor, selecting one of three constants, or an input value V.\nEach constant is enough bits to fill the 4x4 matrix."), .textwidth(162)) callout_4: pin names not known
  _7_Segment_Display u_7_segment_display_4 (
    .g(1'b0), .f(1'b1), .a(1'b0), .b(1'b0), .e(1'b1), .d(1'b1), .c(1'b0), .dp(1'b0));
  _7_Segment_Display u_7_segment_display_5 (
    .g(1'b1), .f(1'b0), .a(1'b0), .b(1'b0), .e(1'b1), .d(1'b1), .c(1'b1), .dp(1'b0));
  LED Is_random_between__25_and__25 (.in(and_1_out));

  // Notes on the sheet:
  //   Use a constant when a circuit calls for a fixed, known value. It's a common mistake to use an Input Pin when a constant would be better:
  //   * Input Pin - takes on any value, depending on user interaction, and resets to zero when simulation is reset or project file is opened.
  //   * Constant - fixed value, does not change during a simulation, saved with project file.
endmodule

module fizz_buzz (
);

  wire clock_1_out, comparator_1_eq, comparator_2_eq;
  wire [3:0] binary_to_bcd_converter_1_p2, binary_to_bcd_converter_1_p3, slideshow_2_p1;
  wire [7:0] counter_1_q, divider_1_rem, divider_2_rem;

  Counter counter_1 (.Q(counter_1_q), .clk(clock_1_out));  // open: load, D, count, carry, clr
  Clock clock_1 (.out(clock_1_out));
  // Callout #(.background("#ff00e626"), .dx(18), .dy(-34), .format("wrapped"), .halign("right"), .text("8-bit unsigned decimal constants, used here to compute (value mod 3), and (value mod 5)"), .textwidth(143)) callout_1: pin names not known
  Divider #(.mode("unsigned")) divider_1 (.a(counter_1_q), .b(8'h3), .rem(divider_1_rem));  // open: out, upper
  Divider #(.mode("unsigned")) divider_2 (.a(counter_1_q), .b(8'h5), .rem(divider_2_rem));  // open: out, upper
  // Callout #(.background("#ff00e626"), .dx(-34), .dy(-42), .format("wrapped"), .text("8-bit zero constants, used for comparisons"), .textwidth(143)) callout_2: pin names not known
  Hex_Digit_Display hex_digit_display_1 (.value(binary_to_bcd_converter_1_p2));  // open: dp
  // Binary_to_BCD_converter #(.width(8)) binary_to_bcd_converter_1: pin names not known; wires that end beside it: counter_1_q, binary_to_bcd_converter_1_p2, binary_to_bcd_converter_1_p3
  Comparator comparator_1 (.a({8{1'b0}}), .b(divider_1_rem), .eq(comparator_1_eq));  // open: gt, lt
  // Slideshow #(.addrWidth(1), .count(2), .height(56), .image0("JPG:\n/9j/4AAQSkZJRgABAQEBLAEsAAD//gATQ3JlYXRlZCB3aXRoIEdJTVD/4gIoSUNDX1BST0ZJTEUA\nAQEAAAIYYXBwbAQAAABtbnRyUkdCIFhZWiAH5gABAAEAAAAAAABhY3NwQVBQTAAAAABBUFBMAAAA\nAAAAAAAAAAAAAAAAAAAA9tYAAQAAAADTLWFwcGwAAAAAAAAAAAAAAAAAAAAAAAAAAAAAAAAAAAAA\nAAAAAAAAAAAAAAAAAAAAAAAAAApkZXNjAAAA/AAAADBjcHJ0AAABLAAAAFB3dHB0AAABfAAAABRy\nWFlaAAABkAAAABRnWFlaAAABpAAAABRiWFlaAAABuAAAABRyVFJDAAABzAAAACBjaGFkAAAB7AAA\nACxiVFJDAAABzAAAACBnVFJDAAABzAAAACBtbHVjAAAAAAAAAAEAAAAMZW5VUwAAABQAAAAcAEQA\naQBzAHAAbABhAHkAIABQADNtbHVjAAAAAAAAAAEAAAAMZW5VUwAAADQAAAAcAEMAbwBwAHkAcgBp\nAGcAaAB0ACAAQQBwAHAAbABlACAASQBuAGMALgAsACAAMgAwADIAMlhZWiAAAAAAAAD21QABAAAA\nANMsWFlaIAAAAAAAAIPfAAA9v////7tYWVogAAAAAAAASr8AALE3AAAKuVhZWiAAAAAAAAAoOAAA\nEQsAAMi5cGFyYQAAAAAAAwAAAAJmZgAA8qcAAA1ZAAAT0AAACltzZjMyAAAAAAABDEIAAAXe///z\nJgAAB5MAAP2Q///7ov///aMAAAPcAADAbv/bAEMAAwICAwICAwMDAwQDAwQFCAUFBAQFCgcHBggM\nCgwMCwoLCw0OEhANDhEOCwsQFhARExQVFRUMDxcYFhQYEhQVFP/bAEMBAwQEBQQFCQUFCRQNCw0U\nFBQUFBQUFBQUFBQUFBQUFBQUFBQUFBQUFBQUFBQUFBQUFBQUFBQUFBQUFBQUFBQUFP/CABEIADgA\nkAMBEQACEQEDEQH/xAAaAAEAAwEBAQAAAAAAAAAAAAAFAgMEAAEI/8QAFgEBAQEAAAAAAAAAAAAA\nAAAAAQAC/9oADAMBAAIQAxAAAAH5eBzBBfSB2tZJ1IDNPUnkisKF0vYz4swD2uYMa6yjVsayP0ns\n7g6gtqBIZMjVTKsjbA6qFUyFadQVKvkKbyer2lQI02hlVbIVpvCC3BvI5oTpjQWVo11SrUWds0zh\nEsDUrMKFVyE6dQVKvkKXyur2FSI02hlVXIXpvDqxrrKNWxrI/SezuDqC2oEhkyNVMqyNsAPa5ggv\noA701knUgM09SeSKwoXS9g8aYB7f/8QAIhAAAgECBwEBAQAAAAAAAAAAAwQBAgUAERITFBU1NDMh\n/9oACAEBAAEFAl15PV1gMdaLObaHKsVY6xW2iaKraLHWgw0psYVU38daDFNtFgttoiigVZK4tocu\ntFn1gMMLyCq2fLcARGG/MSBAgteo2GGcWf8ARdfktNTFVvVmKbewvxmrx+igYWwr6joIKFTzLeCJ\nxc/ltnyoEgw6gbix2N51r1HDyvcAjphgtUJqR40+MKqHVTDplhM8sXBX1AMbLtINtZ8kBHc/ltuf\nHHwdf8yp4OpnV2R+NuC0aS8PM+ngA08AXDzLo0g424tq7Krg6v5kTg67lnx7Z8qA4COo+2sdfZda\n9RwEsXAJKZYLTDqseNPjCphNQxKYYTBK9wV9QC+87SfcWfHBh3P5bZ8twPE4b8xI8FC16jZoWxZ/\n0XY4zTURTb1Yiq3sMclq8fooaGcK+o6eBBU8y3niMXP5V2JBV2YMdkLObkHKstZKxXKiKKrkLHZA\nw03v4Vb2MdkDFNyFgtyomigtY64uQcuyFn2YMMMSer//xAAXEQEBAQEAAAAAAAAAAAAAAAABIEBg\n/9oACAEDAQE/AdDJwbJp/8QAHhEAAgICAwEBAAAAAAAAAAAAAAERMRAhAkFCUXH/2gAIAQIBAT8B\nJZJOJJJYmNksknEkkvDEKxioWjkNwhWOxOUcR7HQh2MQ7H9xGhUKsWz0eisPSHRGsL6Kxm8bOjfR\n+mzs7Nn4b7OjeNiHY/mJ0KhaWKPR6LeHQ6J1hfBWMQrGKhbOQ1KFY7EoRxHodCHYxYhkEYgghiQ0\nQyCMQQQ8f//EAC4QAAEDAQYDBwUBAAAAAAAAAAABAgMREiEyM0FRIjGBBBMUI0KR8FJhcbHBQ//a\nAAgBAQAGPwLZurtjP/RmrTRS6e8sK3i2PMlsP2OGVXL9jPKsW3HuVetiP6jPOKVWr9zy5bb9iwje\nLYvnvM1aaqZ/6N26O3JxszMDyHoJK/E9URvuQ9CRiZicSEv4FT0otVJbPKv9IrXKv9ET0qtUIvwR\ns/0XiUm6iysxMVUd7k3UdM/AwgJ/mg7sz+S4Ts8a7pUia3AxyIhD0Eem146RmGRtSjcyW8X5qJ81\nKOzIrxsj8MbaivXa4m6krXYHuVFJ403uG9mZyTEQfNCX6a3iWK2tKVEtWu79NOYlitvTnzIa0tXC\n+IzOonh69RO8tVprUf3WTp7jO9ydfcXu7VaaVF8RXoJ4fM6k1KWrxbdbevPmLZtd36q8xbdbWtak\nX01uJ/mg7tL+SYSCRd7yJzcD3IqEPQRibXjo2YY20KtzIrhfmonzUq7MluGxvwyNoKxdribqSudg\nY5VU7RIm60G9pZyXEQfNCcbCzAwh6CRPxMVFb7kPQkf/AKLwoS/gVfSq0Uls8q/0itcq/wBEX0ot\nEIvwRvXMThUm6ixMxPVVd7k3UdC/A8gN26t3Mj9GUtNELoLy2ruLc8yK2/c4Ylav2MgoxLEf0lHp\nbj2Mg4olcv3PLisP3LaO4ty+C8ylpqhkfo2bo3Y//8QAIhAAAgEDBAMBAQAAAAAAAAAAAAERITFR\nQWGhsXGB8JHB/9oACAEBAAE/IYOqPiQ+DClyjWxDzUnfAsSlLkEB5imgglUVoOmrPq0TsWjoydi0\ntWfVoYTqK0FTRjA8RTUlKfARvkWHDhmliFip8GIO6viQ7XQ9qVVjRnz7FBBEPEDj9mUaRr8RIQ6O\nA9rcN2kbELagNiFtyHpbRu0iShVciWohf4HH7IqIIhYkfPsPaFFJydLo7Qd/RlsCXunATF6Kg8nH\n7MtOJYZQ/agLUyo2eEcw8wpLKyR5Q/RSKi043hhHH7IXZUD8i3ekl7JD/aMtk6Qwf6YisG6nJkfl\nm5o1itpN7qp9FzZRZa7P5VRGljE0PXEbSbLEYz0dVfI9nUXwN1icZiaFriN4P7VRGtzZRda6N7rr\n9lheGbmjSa2g3U5MmD/TEUk7QX7RhMi1ekH7Ji7qgXk4/ZlpxrLCF6KBQNKKzZZRzDzClIqJFhC9\nqg2nE8so4/ZC9VQeRK3TgJCv6MJg6Q7XQ9oUVjJ8+xUQZDxA4/ZkNRCvwGljq4D2t4naRMQvqAmI\nX3IelsE7SNDFRyKNI3+Jx+yKCDIWJHz7D2pVSdGdLok6q+JD4IKXLNbELNCd8CxKU+AQFmKajCVR\nXgqao+qROzaGrJ2bT0Z9UhBOorwdNEMCxFNCUpchG+RYcOEaWIeKHwQk7o+JD//aAAwDAQACAAMA\nAAAQriQHb4Ccda2bHb4b2Tc+YH2wDjjhFVltsqoMccYG24D3ja2bHb4b2TrjQHb4CUd//8QAHBEA\nAgMBAQEBAAAAAAAAAAAAAAERITFBEFFx/9oACAEDAQE/EGyWSS/JJJYnI3BLJJ8kkliY9F8FoxYK\nvDcIWj0TleG5Hgh6Ni0ej+kwyKFgrQ8NZ06YxYOkPCKJsX0WjL8s4Xw/S+HbO0X0/C+nC/LEPR/C\nLJoWCpDwxnTprFg7Q8JoiGL4LR6JC0YsEp8NShaPRKF4dDwQ9H9Fo0QyCPIIIYlA1JDII8hkEMSP\n/8QAHhEAAwEAAgMBAQAAAAAAAAAAAAERMSFREEFhcZH/2gAIAQIBAT8Qbh8i+i+hNNUb+kX0fIpp\nDD5F9Cf2htJUvovo+QnTaH9M1HriNRuDMLwGBp4DDG5MxHjjMR/SNsyFjgsbYoZmolgbcjF/AYQf\nL9E3IhOAxHSMtaYtdGxtD7n4fYti4B0LqLF0epo+4qHwDyfJ+i6m2ZD1wStoVMjUbkGnKxcv0YQf\n8BJyoa0YjhESNIeOjY2hfbNRY6jUTgjC8BgaeAwxOSMRa6zEX2jbGqfYvsvsSSUG/pl9n2IaUw+x\nfYn9saTUL7L7PsJQ/8QAJRABAAEDAgUFAQAAAAAAAAAAAREAITFhcUFRgaHwEJGxwdHx/9oACAEB\nAAE/ELkGihPMPnatD5a0442QA94CsxbvyoqmwYK5eFi70q+dwIXliOc0UKRvh0s53xVukJNSRYOR\nNDkg89aVGWEUjcFLf2lBlwBByhbfykyYeetRwhQasmw8yKKFIX06SMb4q+d0YXhmeUU1TIEBMPGz\nc60Y4WwE/A4E3rQ+WtXINUCOYPO1eFrorgJWMP38jXia6i4zeLi28TsegY20KcUsjZhPamIIAjkZ\naMR2oMOuKSNXnCAlvaknEcK0LL+9GI6klh0xTGFAAyslHthrxCyNiQ9/QMVBkccxtM7NeJpqKpZR\nsxz0+YrwtNdn8lXwQRlZQ2bnWjShBHEUhvFKSARgsBfo29A0lCCPFmSiQIgMTN3rI7zR4Yw5X8GN\n1a8LRXhaqv0EOR/Qh1CiSlJhM2ekPapqAHksQegZWRxQCoH6d6unajwFE7TUQYAMrIPW70rs/grG\nYH8YmJrQ19kRWpXmmU+wNM3iu4Cl2xmM2ruG91HHtv1L9XmdK2B3N76s4i05rvRpyxwjOK4Guzbo\nWTeJ568Irga7NuldF4nlpwmu9GnPPCMZrcHc3tqzmbTiuPbfuX4vMa13De6juApdsZnFq1K80wj3\nBpi81qa+6JrOZH8YmIrs/kqIMhGVhTrY61dOxDgCY2mhZHFAKFPs39A01AjyWZaJKEuEzc6Qd6t0\nEOR/Qk1GvC0V4Wqjwzhyv4M7oUSBULiZsdZTeKkoUV4sQ+gYSQSMFkh9u1GlCgeIIXeKtggDKwLs\n2eldn8FeFrqKoYDsxx0+ZrxNdNQZHHIbTGz6Bjyy14hdOxK+1M4URXKy04jqSWXTNBOJ5VoS296C\nNWnCBt/anEdqDLrmmYIIJkZKNvCnFLp2YH39A0XGbxYX3iNivE001wkDGH7+QrwtNXINBGOQfO1a\nHy0ozwskJ+IwJt3pomQZIYeFy50q+dxJXhiOUUUKRtp1s42xUcIEurIuHMmgyIeelKjLCSDnIW/l\nKDLgaRuINv7S5CPPSr9IQ6km48iKKFIWw6yM7Yq+d1ZXlmec0UTYEgcvG7d60542yA9pIsxftyrQ\n+WlXINQGeQPO1f/Z"), .image1("JPG:\n/9j/4AAQSkZJRgABAQEBLAEsAAD//gATQ3JlYXRlZCB3aXRoIEdJTVD/4gIoSUNDX1BST0ZJTEUA\nAQEAAAIYYXBwbAQAAABtbnRyUkdCIFhZWiAH5gABAAEAAAAAAABhY3NwQVBQTAAAAABBUFBMAAAA\nAAAAAAAAAAAAAAAAAAAA9tYAAQAAAADTLWFwcGwAAAAAAAAAAAAAAAAAAAAAAAAAAAAAAAAAAAAA\nAAAAAAAAAAAAAAAAAAAAAAAAAApkZXNjAAAA/AAAADBjcHJ0AAABLAAAAFB3dHB0AAABfAAAABRy\nWFlaAAABkAAAABRnWFlaAAABpAAAABRiWFlaAAABuAAAABRyVFJDAAABzAAAACBjaGFkAAAB7AAA\nACxiVFJDAAABzAAAACBnVFJDAAABzAAAACBtbHVjAAAAAAAAAAEAAAAMZW5VUwAAABQAAAAcAEQA\naQBzAHAAbABhAHkAIABQADNtbHVjAAAAAAAAAAEAAAAMZW5VUwAAADQAAAAcAEMAbwBwAHkAcgBp\nAGcAaAB0ACAAQQBwAHAAbABlACAASQBuAGMALgAsACAAMgAwADIAMlhZWiAAAAAAAAD21QABAAAA\nANMsWFlaIAAAAAAAAIPfAAA9v////7tYWVogAAAAAAAASr8AALE3AAAKuVhZWiAAAAAAAAAoOAAA\nEQsAAMi5cGFyYQAAAAAAAwAAAAJmZgAA8qcAAA1ZAAAT0AAACltzZjMyAAAAAAABDEIAAAXe///z\nJgAAB5MAAP2Q///7ov///aMAAAPcAADAbv/bAEMAAwICAwICAwMDAwQDAwQFCAUFBAQFCgcHBggM\nCgwMCwoLCw0OEhANDhEOCwsQFhARExQVFRUMDxcYFhQYEhQVFP/bAEMBAwQEBQQFCQUFCRQNCw0U\nFBQUFBQUFBQUFBQUFBQUFBQUFBQUFBQUFBQUFBQUFBQUFBQUFBQUFBQUFBQUFBQUFP/CABEIADgA\nkAMBEQACEQEDEQH/xAAcAAADAAMBAQEAAAAAAAAAAAAEBQcAAwYCAQj/xAAaAQACAwEBAAAAAAAA\nAAAAAAABBAACBgMF/9oADAMBAAIQAxAAAAH8+I8rNnFFTNjeQgGses+bUbr0JoJP77WSVjwFVTFh\nL2jGkbv+TRC6lqtWF6l26ZZKF658sTzJtgLEpuZSj+kcYWOSIrljUVfPqyzQNaofUne+CpwnvNWf\nJIxDXPtKhVYlAaibplUY1pHAetsk+yVfwVOC9PuobuKS95V7vPKS/SuWDKok1nAaBrlnOniEmCke\nGtO/ZYHuckL5goRd1I0PuB5xqruQ+lrXkUIhrn2tQpsSgNRN0yqMa0jgPW2SV7MIzfTOqLHaB2fj\nL6Wr8T6HbeBaMkjC9c+WJ5k2wFiU3MpR7SOMbHoUeawBJ6PZhUCGUfPqzXQNiGGAB8wZ0Pgn6Ahv\na0ZtNuvQmgk/vtZJWPAVVMWEvaMaRu/5NELqWq1YXqXf/8QAJhAAAgEDAwMFAQEAAAAAAAAAAwUE\nAQIGAAc1EhMUERUXNDYWM//aAAgBAQABBQJChM7k/HCXQcIRmnSdu0445A3DKiwZaxWn27V22/HK\nWusoQgSTcXQgdzfjlLTS7B0k8T3Blq9aMNxCxtvE5I5sIRhnfHCXTdfRbO24/MMAUpqXxkIFBBlc\npLDSTraT7hI/ktpVaXL4taWr5EfxpTa2t5WScOPIIvKTQUKGJxmAIxkuafW24/MQCUMO4HcjHkd6\nbK5SYesdhtqO2jBldSHWnDV4YV1JsXFF8czSY6I/yCLygJHZmxYXXbnTASdez+rt33P5+z+F623h\nebb4PVJ6vcj+N3MK8zvy/F7x+nwAdPgRI8eRWsiogA8buRur3K7weogiwSyjRJEhl6+Ptx+YgDoE\ndx+3GPH7M2VykwFZDDbUltWDK2kytOGrw8eKPD8MMS2kiGCsdhF5TCsfo2dvW9riZPHQw2f1duPz\nDA9K6l8ZCPQoZXKSzUja2k+4SR4zaVSlq/FRBPJy3IK5C8cf6RDUk6i8o5dCVYjE4xeelNM/qr28\nlbb7mDXuQvWrIPpeW8l6LOVq9afcRXdb8jJdZQ+A7m4u+Akm13GS10uzhJAE9zlaxWjNcMsbcROO\nObN0Zp3yOl03YUZTv//EACcRAAIBAgUEAwADAAAAAAAAAAECAAMRBBASIDEUMkFSEyFCIiRh/9oA\nCAEDAQE/AXcIJ1D+sNaoBfTBXe/bk9ZlawEFd/InUVPWU3Li5EqOUFwJ1FT1jVqi/mJWZmsRka73\n7YK1Qi+mdQ/rFOoXmI713YrgQcbabmo5PjZXf8DzBMR3ruxXAi8bK7EDSPMRNC2zJt9yius/I2WI\n7xP7ETVb+XOyvpsNcH+Zk25lr7LhhALfQyxHeu7FcCLxnf5av1wNld9K2HJlNdCgZ4jvXdiuBBxl\nVuFNpST41gzVNVQsfGwqG+zteizNcGDDv5M6ep7SmhQWJlRC4sDOnqe0ajUb9RKLK1ycjQe/dBRq\nAW1Tp39oo0ixn//EAC0RAAAFAgQDCQADAAAAAAAAAAABAgMEBTEREiFBEzKxEBQVNEJRU3HwJWKB\n/9oACAECAQE/AZUpMZP9ti9x4xK+LqFVKYltLnCuEVeUaiI2eoI8RLqUhh00Ia0CavI9TeA8Yl/F\n1EGSuS3mcTlMTpLkZvM2nMY8Yl/F1D1SmMmRG0IlSkPukhbWgM8AurykqMiZ6hNSmKbU5wrDxiV8\nXUMOG62S1FgYrHmmv24IFcGCsC0Ff5Gw2eDSfoFcHcEeJAjwLExEkKlynHC5SLAgdgQO4qslRYRm\nuZQSKx5pr9uD9+zDQFYFYV3kb/0M6oT9D1D1Cwqrq0tky3dYixiisk2QOww0C15Emv2FLZVIcVNd\n3sCuKvh3lv32H8x+wEbjcIuPzDUbDXYVXgZE9499gjlLLYbjcLWSMM53BoSpRKw1Ia7jYahKkPJ0\n1IITkSSU2BCseaa/bg/bsx0BWBaEK7yNhnRCfoeobg1qqE4iRyN9h2B2FUl8Bnho5lCEwcZhLarg\nvYFcVjzTX7cECuDBWBaiv8jYbLFpP0CuJ6lJYWaLinxO6MZTudwkHoDsGYyn5y33LJsDuDBBxht0\nyUstSGBjAYdkumyH3TWh3QJpEj1OYjweX8vUQYzkZvK4rMYnRlyW8raspjweX8vUPU2Y8ZGboiU2\nQw6S1u6AyxC6RKNRmT3UJpsxLam+LceDyvl6hhs2myQo8TH/xAA6EAABAwEDCAcGBgMBAAAAAAAB\nAAIDEQQSIQUTIjEyQVGBFDM1QmGRohUjobLB8CRDUnOx4QYlcdH/2gAIAQEABj8CoKx2Zh99PTBg\nXbPrYprP7Xd7sDSN2h44qRzctAODai85tFcI0lHPasqiGZ2uMEC74YoZjKUtofUVbHddRtcTh4Lt\nn1sVyy2oWyGlbw7p4FXLVahY4abR7x4Bds+tie72u5ha9zaOutwrgcfBST2XKommbqjJBveGCuAa\nSjc7LQLi2puubRQWc5Xd7wHS0aDhiu2fWxSwslE8TXUbK3U5ZZ5/ImzM2HqHkhK/aeQG+ah5KRg6\nwaQWUf22/wAlWgd0SuJ81Ld1V+qivaq/VAd0moULWipOAAWTrI6nT5n56Ub9Sm5oys2mEh3mpuan\nyvbNGyWQEgu1F39KFZZ5/InWZ+o7Ks8Z4iqia3YY4AKHkg8cMVb5GbMkTT8VOG9ZLI4/FH73ofe9\nUd1kWKfb7W4CGwR5yh48fgprW/BpwY39Ldym5qVrth7iCn2ZppffdB4VVm/x6wmjI2gzkb/vWoPv\ncspUpmM5739V27jTkhcre3Uzqd0POdC/LrWv/qFyt/dr1qGtL2CPSOs5qf2Tc6o3s9q8PindIvZz\nfWqfmup3eaZnep3+ak6Ox7yxhc67XBqljle5scgF8N1EbqodH6zmpqUvYo3639+vWqFr4rtHG9tD\ngpJJ3OfM41c51a1UX6a4LLPP5E60v1DZUEh44qJzdh7gQoeSDBwxVvjZsxxNHxU5b1kUjh8Ufveh\n971I+0N/2GUhcDd4B/rFNjfsyNoiw8MFNzUtqtA/BWR195OoncFb7ZEKRl1GeIAom2lmo7Sg+9yy\nzz+RNhZsMUPJCJ+0wgt81DyUj/zDohZR/bb/ACVaD3TK4HzUt3VX6qwNtABhzlXXtWGKMrT+GjNy\nIeHFRf8AFG89YNEqbmrNk2yaM9rrJORwr9VNzToX7D1ApWQyubFMKSMBwcF1H8LqjTcFhBir5dpc\nVHBaslCaZuuQAG944oZjJstnfUVdHdbVtcRh4Lsb0MV+y2UWOGmyO8eJV+1WUWyGlLp7p4hdjehi\ne32Q55c9zquuuwrgMfBSQWXJQhmdqkIAu+OCvg6Sja7IoDg2hutbRQ2j2Q73YOiLtDwwXY3oYpZm\nRCCJzqsibqav/8QAIxAAAgIBAwUBAQEAAAAAAAAAAREAITFRYaFBcYGRsfDB0f/aAAgBAQABPyGt\nZGtrj+3NTcwGcbAIBbQFRVY1hJwiEsuoF+oXGFkEM9o4AXn6ycfIFEqFehj6HWAYEGjBy5ElE6gK\nil2ZCgdQNQjEk0IWhRAhAqNSGLQF4+snA4wMixjvA7xEBZdAb9w6WwQJFpCFB3nSbmBLTA1M5cjt\nkVroZ+faUIAg6JOP9GU0WPTBQzRiFL5B2eFhMYUFhMZcHC4hdnDUBkFkuFRcd4hdgwPc4/0JYgCB\no0/PtAOjopRnw5IhM/7E5cjf0stIE7rgAwfRUHecf6MxOAU1EP5/RoVSwHQNOZPMkJJcAOomjMrW\na8G8qPZBJfQwnH+hB4VAe8Qbamx/s6/RFFkA7k28T4o9aj+Kdpvr1Dn+yVV9mU71m90V8GZsowxk\nz+VUXTE56Cuh9fTWbkT5U8HWzqnk6mdEpGA9TJO0HLkLKR6G8/tVF1zNlGWMibnc/JiNI0rCgEg7\nwoQPMqZbpofspU5y5D9pQawYvSHyBg8qgHecf6MxOEW0EDwMD7oFS4DUNOZPKkN0t3DUPBNuVB7W\nJxOA21E4/wBCCsAjrJfAz23jboM6EB8pwX9KDSfFHLkdogtaz8+0sQJB0Scf6MTSSPRDZzZiFL4h\n2eBhM4UUnIugRt6hZHgefrPqEiCi0pos+mcf6ESoCZ2DPPguwn59odsip9DPi+SirzkX4CA2ydak\nNaj3sMRpR4I9AXn6ycXIHMqF+ph6PSAYQOCl2IKgdAFRy5MFE6AagIgmQYUhRAgIvAQRQAvH1k4H\nGFmWc94CcIBLLoTfuHONAgAtMQoq86zcwJaYSpn/2gAMAwEAAgADAAAAELiKgAAVQc8tmyW/Y9ud\nPmAtsw4O+nVR7QqrXNHGAtiA0Y8tmzWgG1k240gAAVQc/wD/xAAhEQACAgICAgMBAAAAAAAAAAAA\nARExIUFx8BBRYaGxgf/aAAgBAwEBPxD5xpHVIg7htE/0IdJKPSTokxVMzVM6JGCTCpBQxNkv0MOo\n6pHpZQzq5F6FYxULHivC8CsdicoThSxB6KEOhDsYot8HVyP2TDIwKhZR9kyTg2bKYg24CFqOiMED\n4Dm7qFZD5YwdUYJZNGdH9RootDeTeBEJWNWTjKM7NGRYDKICoEdXI/RGScCoWEfZME4NmxupBVDy\nh14aHsbF6FZ1ciQrGKhKfFWV4FYzKxjXbvweB0MrdB2P2Kx8kZRDII8OkFHsJ0SZqmYqmdEjBNhU\nkoY2zX6GHcdUj0sln//EACURAQACAgAGAgMBAQAAAAAAAAEAESExQVFhcYGxodGRwfAQ4f/aAAgB\nAgEBPxC/uV3F/fRmfzIbpq3PxjZedyxoKaLfMoXLSw0ot9cYqPWoU5bM1gzzfuUf8xs/K79S8zY+\nfjq1mCY9YJrkHi7MmOTiUlltBK65xUoXKCgLst8QuGqc/ONtY1P5kX+YtHhPTh8GbY7aJtiwZ8h9\nE8Qepomz/AJEoJ9/UB/LVzTHTTNMNzlLrdX+/UwZ6cGmkulYUTNsF0jann6E8EPUYIcu8G/JXjGP\nN/i5s/NvN4zTGwZcBdF/E2NpPt40eZum84Oy7xfHceeeGeev6r51idcN4YRxVycXXxXnlPAiu0NL\n3HatzCgsBfFdEdQbKeV7qOEOs6YpWJZ05MpnQ0E3Z6cO2kq1IWRNsWSFueb6Iu6HqP8Ai72S75p9\nuDpmA1ZFdppjEnDK2HF/RHGwLe63XiOm03T04PFm2GmybYMCfIfRPEHqaJwPVFdaIQBxu7l41NGD\nImmZkXrur9b7s0w8SbsPy5ReE60vzl+cACpSWWhUrpjFQq1CnDbmsOeT9Sz/ALjY+fjoXmbPy+/R\nrMAyfOCa4A4mjLjm5lpYbBW+mcVKFSxoK7bfELpqnPznZeNT+bFfmKV4z//EACYQAQABAwMDBQEB\nAQAAAAAAAAERACExQVFhcYHwEJGhscHR4fH/2gAIAQEAAT8QDg6opvufAYAp5j+0uvWhlhDX5MS2\nYBKa/BJJkTpdtRbxATPDImGnu9LtjYb2qQhkiS7rMpsQgULw5QJQLUQSOU96EzM1FyNckOEkLSpj\nR6LgaZZcCA3gqoJXCe9FqIDBRAKFIWlTSKb/APKtLhtahbEMwXG3iAmOWBMFKEdfkFkwJ0u3qOj/\nAEywjp8iUbk+Y/tO+5YB1OTDFmJFEa8jvorgJWMP79jXic6i4zeLi3WJ6HoGNtCmqWR0YT2pjiAI\n5KDKYkaCx3xSRq84QEt7Uk4jhWhZf3oxHkksO2KVjaSKAAaq0b8HLgGy3S7st/QMVBkcbjpM9GvE\n40Xz5rVrfkgfwUBWFEr5HfV8EEZWUOjc70aUII1FIdYpSQCMFgL+HT0DSUII6syUDREBibr3kes0\nfmPOV+oY6q14XCvC5VfoIcj/AEIeQp5qGFzStIKRqtlPQx5ZwdWLu6voGVkcUAqB/HrVkJR5ISLv\nH0oQqSQyyNx1BXw/oqbRDJiZeAnteK4xPZkRXO7qD7XgJ2V8gKXdDMZtXyG91GvbfyX9XmeK/p15\n321G7ZXzVPMpxaJnFtq0Ndm3Qsm8TvzpFaGuzbpXReJ240mpi79lrtgWzQ7MSZ+NVE5tOLVr239l\n/F5jmvkN7qDuB1l3QzOLUzbIJJ55D6RF5pCCELN1OtZzI/4xMRXkd9RBkIysKd7Herp2IaAmOk0L\nI4oBQp+nX0DTUCOyzLRPAhwm6doPmrfhzkfsCTka8LhV/myrEIg8OTUGcBsokCoXEzY7ynWKkoUV\n1Yh9A1hxm5klbIS4gNI+CjJW9oWtJirYIAysC9Gz2r4f0V5HfUVQwHZjjt9zXic6agyONh0mOj6B\njyy11C6ehK+1M8URXLQ5jyKVztmgnE8q0Jbe9X5jpEDdElagImrBcQ3Z2Q0pmCCCZGSjbwpql09G\nB9/QMys84IUWZgho5qV4nGmuEgYw/v2FeFxoJzIMDh2dJMijIpXB8uKM8LJCfUYE2+aaJkGSGHS5\nc7VfO4krwxG0U335dpctrQhYgiCwy5WyISChQOFCEIGCAgP8aExo9FwNMEGAVbQpmZqLka4ZMLCX\nke4IjdPai9OBgAlKDRFpF1mnu9Ltjdb2iFhlmSyW8SEzyQZhoE5rsAMGROt29Lr1oZcQ0+DENiPM\nfykr8kU6HLlixMAAFf/Z"), .width(144)) slideshow_1: pin names not known; wires that end beside it: comparator_1_eq
  Comparator comparator_2 (.a({8{1'b0}}), .b(divider_2_rem), .eq(comparator_2_eq));  // open: gt, lt
  Hex_Digit_Display hex_digit_display_2 (.value(binary_to_bcd_converter_1_p3));  // open: dp
  Hex_Digit_Display hex_digit_display_3 (.value(slideshow_2_p1));  // open: dp
  // Slideshow #(.addrWidth(1), .count(2), .height(56), .image0("JPG:\n/9j/4AAQSkZJRgABAQEBLAEsAAD//gATQ3JlYXRlZCB3aXRoIEdJTVD/4gIoSUNDX1BST0ZJTEUA\nAQEAAAIYYXBwbAQAAABtbnRyUkdCIFhZWiAH5gABAAEAAAAAAABhY3NwQVBQTAAAAABBUFBMAAAA\nAAAAAAAAAAAAAAAAAAAA9tYAAQAAAADTLWFwcGwAAAAAAAAAAAAAAAAAAAAAAAAAAAAAAAAAAAAA\nAAAAAAAAAAAAAAAAAAAAAAAAAApkZXNjAAAA/AAAADBjcHJ0AAABLAAAAFB3dHB0AAABfAAAABRy\nWFlaAAABkAAAABRnWFlaAAABpAAAABRiWFlaAAABuAAAABRyVFJDAAABzAAAACBjaGFkAAAB7AAA\nACxiVFJDAAABzAAAACBnVFJDAAABzAAAACBtbHVjAAAAAAAAAAEAAAAMZW5VUwAAABQAAAAcAEQA\naQBzAHAAbABhAHkAIABQADNtbHVjAAAAAAAAAAEAAAAMZW5VUwAAADQAAAAcAEMAbwBwAHkAcgBp\nAGcAaAB0ACAAQQBwAHAAbABlACAASQBuAGMALgAsACAAMgAwADIAMlhZWiAAAAAAAAD21QABAAAA\nANMsWFlaIAAAAAAAAIPfAAA9v////7tYWVogAAAAAAAASr8AALE3AAAKuVhZWiAAAAAAAAAoOAAA\nEQsAAMi5cGFyYQAAAAAAAwAAAAJmZgAA8qcAAA1ZAAAT0AAACltzZjMyAAAAAAABDEIAAAXe///z\nJgAAB5MAAP2Q///7ov///aMAAAPcAADAbv/bAEMAAwICAwICAwMDAwQDAwQFCAUFBAQFCgcHBggM\nCgwMCwoLCw0OEhANDhEOCwsQFhARExQVFRUMDxcYFhQYEhQVFP/bAEMBAwQEBQQFCQUFCRQNCw0U\nFBQUFBQUFBQUFBQUFBQUFBQUFBQUFBQUFBQUFBQUFBQUFBQUFBQUFBQUFBQUFBQUFP/CABEIADgA\nkAMBEQACEQEDEQH/xAAaAAEAAwEBAQAAAAAAAAAAAAAFAgMEAAEI/8QAFgEBAQEAAAAAAAAAAAAA\nAAAAAQAC/9oADAMBAAIQAxAAAAH5eBzBBfSB2tZJ1IDNPUnkisKF0vYz4swD2uYMa6yjVsayP0ns\n7g6gtqBIZMjVTKsjbA6qFUyFadQVKvkKbyer2lQI02hlVbIVpvCC3BvI5oTpjQWVo11SrUWds0zh\nEsDUrMKFVyE6dQVKvkKXyur2FSI02hlVXIXpvDqxrrKNWxrI/SezuDqC2oEhkyNVMqyNsAPa5ggv\noA701knUgM09SeSKwoXS9g8aYB7f/8QAIhAAAgECBwEBAQAAAAAAAAAAAwQBAgUAERITFBU1NDMh\n/9oACAEBAAEFAl15PV1gMdaLObaHKsVY6xW2iaKraLHWgw0psYVU38daDFNtFgttoiigVZK4tocu\ntFn1gMMLyCq2fLcARGG/MSBAgteo2GGcWf8ARdfktNTFVvVmKbewvxmrx+igYWwr6joIKFTzLeCJ\nxc/ltnyoEgw6gbix2N51r1HDyvcAjphgtUJqR40+MKqHVTDplhM8sXBX1AMbLtINtZ8kBHc/ltuf\nHHwdf8yp4OpnV2R+NuC0aS8PM+ngA08AXDzLo0g424tq7Krg6v5kTg67lnx7Z8qA4COo+2sdfZda\n9RwEsXAJKZYLTDqseNPjCphNQxKYYTBK9wV9QC+87SfcWfHBh3P5bZ8twPE4b8xI8FC16jZoWxZ/\n0XY4zTURTb1Yiq3sMclq8fooaGcK+o6eBBU8y3niMXP5V2JBV2YMdkLObkHKstZKxXKiKKrkLHZA\nw03v4Vb2MdkDFNyFgtyomigtY64uQcuyFn2YMMMSer//xAAXEQEBAQEAAAAAAAAAAAAAAAABIEBg\n/9oACAEDAQE/AdDJwbJp/8QAHhEAAgICAwEBAAAAAAAAAAAAAAERMRAhAkFCUXH/2gAIAQIBAT8B\nJZJOJJJYmNksknEkkvDEKxioWjkNwhWOxOUcR7HQh2MQ7H9xGhUKsWz0eisPSHRGsL6Kxm8bOjfR\n+mzs7Nn4b7OjeNiHY/mJ0KhaWKPR6LeHQ6J1hfBWMQrGKhbOQ1KFY7EoRxHodCHYxYhkEYgghiQ0\nQyCMQQQ8f//EAC4QAAEDAQYDBwUBAAAAAAAAAAABAgMREiEyM0FRIjGBBBMUI0KR8FJhcbHBQ//a\nAAgBAQAGPwLZurtjP/RmrTRS6e8sK3i2PMlsP2OGVXL9jPKsW3HuVetiP6jPOKVWr9zy5bb9iwje\nLYvnvM1aaqZ/6N26O3JxszMDyHoJK/E9URvuQ9CRiZicSEv4FT0otVJbPKv9IrXKv9ET0qtUIvwR\ns/0XiUm6iysxMVUd7k3UdM/AwgJ/mg7sz+S4Ts8a7pUia3AxyIhD0Eem146RmGRtSjcyW8X5qJ81\nKOzIrxsj8MbaivXa4m6krXYHuVFJ403uG9mZyTEQfNCX6a3iWK2tKVEtWu79NOYlitvTnzIa0tXC\n+IzOonh69RO8tVprUf3WTp7jO9ydfcXu7VaaVF8RXoJ4fM6k1KWrxbdbevPmLZtd36q8xbdbWtak\nX01uJ/mg7tL+SYSCRd7yJzcD3IqEPQRibXjo2YY20KtzIrhfmonzUq7MluGxvwyNoKxdribqSudg\nY5VU7RIm60G9pZyXEQfNCcbCzAwh6CRPxMVFb7kPQkf/AKLwoS/gVfSq0Uls8q/0itcq/wBEX0ot\nEIvwRvXMThUm6ixMxPVVd7k3UdC/A8gN26t3Mj9GUtNELoLy2ruLc8yK2/c4Ylav2MgoxLEf0lHp\nbj2Mg4olcv3PLisP3LaO4ty+C8ylpqhkfo2bo3Y//8QAIhAAAgEDBAMBAQAAAAAAAAAAAAERITFR\nQWGhsXGB8JHB/9oACAEBAAE/IYOqPiQ+DClyjWxDzUnfAsSlLkEB5imgglUVoOmrPq0TsWjoydi0\ntWfVoYTqK0FTRjA8RTUlKfARvkWHDhmliFip8GIO6viQ7XQ9qVVjRnz7FBBEPEDj9mUaRr8RIQ6O\nA9rcN2kbELagNiFtyHpbRu0iShVciWohf4HH7IqIIhYkfPsPaFFJydLo7Qd/RlsCXunATF6Kg8nH\n7MtOJYZQ/agLUyo2eEcw8wpLKyR5Q/RSKi043hhHH7IXZUD8i3ekl7JD/aMtk6Qwf6YisG6nJkfl\nm5o1itpN7qp9FzZRZa7P5VRGljE0PXEbSbLEYz0dVfI9nUXwN1icZiaFriN4P7VRGtzZRda6N7rr\n9lheGbmjSa2g3U5MmD/TEUk7QX7RhMi1ekH7Ji7qgXk4/ZlpxrLCF6KBQNKKzZZRzDzClIqJFhC9\nqg2nE8so4/ZC9VQeRK3TgJCv6MJg6Q7XQ9oUVjJ8+xUQZDxA4/ZkNRCvwGljq4D2t4naRMQvqAmI\nX3IelsE7SNDFRyKNI3+Jx+yKCDIWJHz7D2pVSdGdLok6q+JD4IKXLNbELNCd8CxKU+AQFmKajCVR\nXgqao+qROzaGrJ2bT0Z9UhBOorwdNEMCxFNCUpchG+RYcOEaWIeKHwQk7o+JD//aAAwDAQACAAMA\nAAAQriQHb4Ccda2bHb4b2Tc+YH2wDjjhFVltsqoMccYG24D3ja2bHb4b2TrjQHb4CUd//8QAHBEA\nAgMBAQEBAAAAAAAAAAAAAAERITFBEFFx/9oACAEDAQE/EGyWSS/JJJYnI3BLJJ8kkliY9F8FoxYK\nvDcIWj0TleG5Hgh6Ni0ej+kwyKFgrQ8NZ06YxYOkPCKJsX0WjL8s4Xw/S+HbO0X0/C+nC/LEPR/C\nLJoWCpDwxnTprFg7Q8JoiGL4LR6JC0YsEp8NShaPRKF4dDwQ9H9Fo0QyCPIIIYlA1JDII8hkEMSP\n/8QAHhEAAwEAAgMBAQAAAAAAAAAAAAERMSFREEFhcZH/2gAIAQIBAT8Qbh8i+i+hNNUb+kX0fIpp\nDD5F9Cf2htJUvovo+QnTaH9M1HriNRuDMLwGBp4DDG5MxHjjMR/SNsyFjgsbYoZmolgbcjF/AYQf\nL9E3IhOAxHSMtaYtdGxtD7n4fYti4B0LqLF0epo+4qHwDyfJ+i6m2ZD1wStoVMjUbkGnKxcv0YQf\n8BJyoa0YjhESNIeOjY2hfbNRY6jUTgjC8BgaeAwxOSMRa6zEX2jbGqfYvsvsSSUG/pl9n2IaUw+x\nfYn9saTUL7L7PsJQ/8QAJRABAAEDAgUFAQAAAAAAAAAAAREAITFhcUFRgaHwEJGxwdHx/9oACAEB\nAAE/ELkGihPMPnatD5a0442QA94CsxbvyoqmwYK5eFi70q+dwIXliOc0UKRvh0s53xVukJNSRYOR\nNDkg89aVGWEUjcFLf2lBlwBByhbfykyYeetRwhQasmw8yKKFIX06SMb4q+d0YXhmeUU1TIEBMPGz\nc60Y4WwE/A4E3rQ+WtXINUCOYPO1eFrorgJWMP38jXia6i4zeLi28TsegY20KcUsjZhPamIIAjkZ\naMR2oMOuKSNXnCAlvaknEcK0LL+9GI6klh0xTGFAAyslHthrxCyNiQ9/QMVBkccxtM7NeJpqKpZR\nsxz0+YrwtNdn8lXwQRlZQ2bnWjShBHEUhvFKSARgsBfo29A0lCCPFmSiQIgMTN3rI7zR4Yw5X8GN\n1a8LRXhaqv0EOR/Qh1CiSlJhM2ekPapqAHksQegZWRxQCoH6d6unajwFE7TUQYAMrIPW70rs/grG\nYH8YmJrQ19kRWpXmmU+wNM3iu4Cl2xmM2ruG91HHtv1L9XmdK2B3N76s4i05rvRpyxwjOK4Guzbo\nWTeJ568Irga7NuldF4nlpwmu9GnPPCMZrcHc3tqzmbTiuPbfuX4vMa13De6juApdsZnFq1K80wj3\nBpi81qa+6JrOZH8YmIrs/kqIMhGVhTrY61dOxDgCY2mhZHFAKFPs39A01AjyWZaJKEuEzc6Qd6t0\nEOR/Qk1GvC0V4Wqjwzhyv4M7oUSBULiZsdZTeKkoUV4sQ+gYSQSMFkh9u1GlCgeIIXeKtggDKwLs\n2eldn8FeFrqKoYDsxx0+ZrxNdNQZHHIbTGz6Bjyy14hdOxK+1M4URXKy04jqSWXTNBOJ5VoS296C\nNWnCBt/anEdqDLrmmYIIJkZKNvCnFLp2YH39A0XGbxYX3iNivE001wkDGH7+QrwtNXINBGOQfO1a\nHy0ozwskJ+IwJt3pomQZIYeFy50q+dxJXhiOUUUKRtp1s42xUcIEurIuHMmgyIeelKjLCSDnIW/l\nKDLgaRuINv7S5CPPSr9IQ6km48iKKFIWw6yM7Yq+d1ZXlmec0UTYEgcvG7d60542yA9pIsxftyrQ\n+WlXINQGeQPO1f/Z"), .image1("JPG:\n/9j/4AAQSkZJRgABAQEBLAEsAAD//gATQ3JlYXRlZCB3aXRoIEdJTVD/4gIoSUNDX1BST0ZJTEUA\nAQEAAAIYYXBwbAQAAABtbnRyUkdCIFhZWiAH5gABAAEAAAAAAABhY3NwQVBQTAAAAABBUFBMAAAA\nAAAAAAAAAAAAAAAAAAAA9tYAAQAAAADTLWFwcGwAAAAAAAAAAAAAAAAAAAAAAAAAAAAAAAAAAAAA\nAAAAAAAAAAAAAAAAAAAAAAAAAApkZXNjAAAA/AAAADBjcHJ0AAABLAAAAFB3dHB0AAABfAAAABRy\nWFlaAAABkAAAABRnWFlaAAABpAAAABRiWFlaAAABuAAAABRyVFJDAAABzAAAACBjaGFkAAAB7AAA\nACxiVFJDAAABzAAAACBnVFJDAAABzAAAACBtbHVjAAAAAAAAAAEAAAAMZW5VUwAAABQAAAAcAEQA\naQBzAHAAbABhAHkAIABQADNtbHVjAAAAAAAAAAEAAAAMZW5VUwAAADQAAAAcAEMAbwBwAHkAcgBp\nAGcAaAB0ACAAQQBwAHAAbABlACAASQBuAGMALgAsACAAMgAwADIAMlhZWiAAAAAAAAD21QABAAAA\nANMsWFlaIAAAAAAAAIPfAAA9v////7tYWVogAAAAAAAASr8AALE3AAAKuVhZWiAAAAAAAAAoOAAA\nEQsAAMi5cGFyYQAAAAAAAwAAAAJmZgAA8qcAAA1ZAAAT0AAACltzZjMyAAAAAAABDEIAAAXe///z\nJgAAB5MAAP2Q///7ov///aMAAAPcAADAbv/bAEMAAwICAwICAwMDAwQDAwQFCAUFBAQFCgcHBggM\nCgwMCwoLCw0OEhANDhEOCwsQFhARExQVFRUMDxcYFhQYEhQVFP/bAEMBAwQEBQQFCQUFCRQNCw0U\nFBQUFBQUFBQUFBQUFBQUFBQUFBQUFBQUFBQUFBQUFBQUFBQUFBQUFBQUFBQUFBQUFP/CABEIADgA\nkAMBEQACEQEDEQH/xAAcAAADAAMBAQEAAAAAAAAAAAAEBQcCAwYIAAH/xAAaAQACAwEBAAAAAAAA\nAAAAAAABBAACBgUD/9oADAMBAAIQAxAAAAHzcvS6ZZIe8ykh2mdaSD+tsgNfmGq1KxwFVTFhL2jG\nkbv+TRC9S1WrC9S6Z6EMm55JCXaJutZpNB0fWV99teZ6ByKEb1byK5Y1FXz6ss0DWqHKTveCpwne\na/JNBN8yPPjmjcr2aT5Dp+3JdtlUZZMojGtW/wDslX4KnBdP3UN3FJe+Ve7zykv0rmBO4C+47nrb\nET0PL9T35Pre4plRzacs0jhfmChF3qRoc4HnjVXch+lswNBN8yPPjmjcr2aT5Dp+3JdtlUTZMohG\ntW/XswjN9M6osdoHZ8ZfS1fieh7bwPpAybnkkJdom61mk0HR9ZX3215noHIoTzutLAEnR9mFQIZR\n8+rNdA2IYYAH5i6ZZIe8ykh2mdsWeU+Mar1m3YYA97VjgKqmLCXtGNI3f8miF6lqtWF6l3//xAAn\nEAABAwIFBAMBAQAAAAAAAAAFAQMEAgYABxMUFxI0NTcRFTMWNv/aAAgBAQABBQIQPQlO44C4py7F\naz2XIhGpYmXBnugqoVdQ1rH1rGJIWQzEtcCwbm8chUwOscJPaO2MNHjW2anHY2XgdyO9ZANmdxwF\nwXHoNnDO1IMImLn9a2ywjRC5fZmYzKSTgf8ASPH3MqtUqytiqlI+RH20otStbpIOzbwCL5SawjrM\nTxlgA23KinbDO1gOI82eY1LAGyNa5bl9mZjvrHu1lulJDtSQ4jHqRfDNVJNi2oPjvFJhpw/cEXyj\nEjRmxYXXTfRBoOPJ9qN+du3seuHp/wA7G/jNyf3HIl7f6Bro6Xdn80a/HDHTsIkePIVZCtMMbbUj\ndX2VWx6nGnYLsp6JIkEvnbjO1gNoy2ff07AGx9G5bl9mZjsLIu1lylZDtKTYrHqRfDx4rdn2Y85S\nkiGwschF8pZVvoWNnS9JiZPbR5sn2oztSD6Li5/Wtsvo6QuX2ZmM8kY4H/SPI20qtEpyttVpl+Td\ntwLcJwx+kR5JOIvlDJpoVaMTxg99EwT7UQQQbO5HC4pzEFI69mMIVqWWlzp4zMSHREI3wEntcjBU\nxc92qaW1zzASauYwVcDr4CQGjt8jSI1t6pt2NmIHbjvXuDencjhcFyCEp3//xAApEQABAwEGBQUB\nAAAAAAAAAAABAAIDERASExQzUgQgITEyIjRBQlFE/9oACAEDAQE/AXG6KhZh+1Y7/wAWYftQcCKh\nBwd1Ft4VuqR5YKgLMSbU6aRv1TJnOdQiwzvr4oTSEVurMP2ppvCtseuVJ4lR6Dlw3gjZ/RyRvMjy\nfjknf9B8oWx6xT/AqPQcuG07T7i2dxAuj5TGXG0tJp1ULb5xHcjtQ4fdHHp6uyZTBcoKXPTaaY4/\nbCad1SvJUOCAp0HJHrFP8Co9By4bTtPuLK4svTsOSd91tB3KjbcaByx65UniVHoOXDeCNn9ClqGm\niiZhtQtay9IXH45HC8KLLv3LLv8A1Zd+5BoAoE6B1fSU2GRv2WXk3KOK51PdSMLxQFZeTcnQyO+y\nZC5rqk2GB9fJCGQCl5Zd+5NF0UK//8QAMhEAAQMBBAcIAgIDAAAAAAAAAQACAwQFESExEhMVNUGB\nsRQiMlFTccHwECMkNEKR4f/aAAgBAgEBPwGeQxRl7ReVtiq9Lqja9RdhHim2xU396LDmo6iOSPWt\nOCjmbM3TjN4V6vK18es1V/eVdUyU0elG3SK2xV+l1U1pVkJAMSpLSqJ5Qx8WCJuT7XqmuIEPVNtK\nsdG6TVZLbFV6XVQSGWMPcLiigqLeknNVh/RJ7FUe65efwrFwpeZTkTcE7fA+8Ec0DeEDcLyqSodV\n1Ukg8IFwRyQRzVq1LhdTReJyajmj5qj3nLzVUP40nsVR7rl5/CsX+pzP4zKdvgfeC/yWStWV7YxD\nHm9UtMKWERhHJXYJ79Bpf5Ky4XVEjq2XjkhmisVLf2t/YvHx/wCJ+1NE63w8cslS6GzZdHLH4Vl6\nHZhqvpXusVJqtqMu8XH/AEuKe8Mu0zmixrnB12IWPFcFimuZM3DEJjdBoa3JBHNHyVHvOXmqo/xp\nPYqj3XLz+FYv9Tmfxknb4H3guKL3WhXAM8Ef4OSOStSr1EOrZ4nKigNNA2N2aHkhmigqLeknNVg/\nRJ7FUe65efwrFxpeZTkReEd8D7wVe5zYHlmas+k7JBonM5pqOCOShpnT1z55Mm5I5ooKeMyxljTc\nVseq9XqjZFRdhJim2PU396XDmo6eOOPVNGCmsiUv/RJc3yUNm1kJJEq2PV+r1VFQdm70h0nearqZ\n9THoxu0Stj1fq9VNZtZMQTKqSzaiCUPfLgiL0+yKouJE3VNs2sbG6PW5rY9V6vVQRmKMMcbyv//E\nAD0QAAEDAQMFDQUIAwAAAAAAAAIAAQMRBBIhBRMxMkEUFSIzNUJRYXGBorLwI1JykqEkQ1NjkcHD\n4QYls//aAAgBAQAGPwKKE5WgiIqHKWgVyz4wRMWUpQh5kr3WEn20dHm8s+0pwauL4rccsBDaK0YK\naexPFbHeCdtIOuDK5P1Lj09sCMjsdbud2VVy1WprHDTWfnP0MuWfGCMt9yBxMhoV0cK4Pj1KSey5\nVaaYdEbuz3urBXGbhKMiy0zk41e6Q0UFnfK5e0Z+FwaN0YrlnxgpYQlaeISoMo6CU6GYNQ1knsi8\nqsMhax2iNh+Zlkf4Y/MSlBuMaICZS9iduaz1dWm7ovfyqK9or+6Zua71ZQiLVd8GZlk6yFTd8x56\nVtuhTd6eUNYHdi/VTd6nyvbODZLIzuzlocv6UKn9bEVmPQ+qskRv+XX5XWTRHUC0AzfMsj/DH5iT\nG34I1+qKQNWQaqg8ZLipe3+VN62qhcZFijt9rJmhsEeco/T0/RTWs8BfAB90dim71KJahk7Ojswv\nS+d1n6Kqzf49YXoEYs87tt9aVB62KX3a4prlb2ylVY9/OTfuLlb3Vepjo/tRbivbsvNmbt+t/Zpw\nWR85m89cj1a3dJKbfG7nqNduVpc2Jtz1702cvVptqrbdubhvNm/e12r9UGd4nb+qk3OBm4A5Fdrg\nKljlMhjkZr7DodtlU25+M71NSl7FPfrf26dKo4nFdoT3tZuhSSTkRzE9SIq1qovdrgp/WxFaT0Nq\nrJEj/l+V1k0h1DtAO3zLI/wx+YkwN+CNfqijDVjGiqPGRYKXt/lTetqkO0D/ALDKTXGHazP/AFih\njPVkGicH6MFN3qW1WhvsVkK+bvod9jK32yJqRuVA62ZqIbSGh9ZQetinQwhqAsk9kXlVhjLWC0Ru\nPzMsj/DH5iUh/ePEIspexO/Nd6OrTd0Xn/6qwDaGZ4c5Ur2jDFPKL/Zo3uRN1dKi7FGb8Y3BdTd6\ns2TbJwZ7XWSd26K/upu9FCeoagUUxxNPEJVKItBLkbwAivZNlKHmRPdcRfbRkebyN7SnBqwtit2S\nzkVorVjro7ELZRyduq186agve/VAO9BA4mJVG6OFcWw6lyN4AWZskT2Ow4O8Lc5+l1ftVla2Q0pd\nfmv0suRvACMd6CNyMiqV0sK4Nj1KSCy5KaGYtEjszXevBX2fhKMSyKzEw0e6I0UNo3oL2bPwWu0f\nowXI3gBSzBE0ERFUIh0Cv//EACUQAAICAQMEAgMBAAAAAAAAAAERACExQVFhcYGhsZHwEMHR4f/a\nAAgBAQABPyEFpgKmcmBySAjYkJRVY52hicxAx0ULPaPGoWRfHJzTqLwR/YABYsIa1M+0iDIYTEU2\n/wCxS7MhQO4GoRiSaELQogQgVG5DFoC7fWTgcYGRYx1gd4iAstAb+YdLYIEi0hCg7ztOTAlpgame\n16h2yK1oZ9hulJYAO34BCaPeMBANFIcrkF4cPSXJdELCYy4OFxC8OGoDILJcKi46xC6BgfM8f2Es\nQBA2afX4gHRopRns8kQmf7ie1Bv6WW0Gf1XsgPQUnR+BGJwLbhwfahJUSwkdhPMek8yQklwA7ibM\nytZrsbuo9kEl6GE8f2EHhUB6xBtqcH9mv0RRZAPJNu09KNj+SlanKncuagoOjH5Il5KfsZk85Zqf\nueD5ov01r5zrNpkdaXDnCwtud/xf83lzxO51M7JSMB6mSeIOXIWUjocz91UWuZwoyxkTk7n3MRpG\nlYUAkHeFCB5lTLlNj+SlTntQP2lBvAj9XPeA8ikHR+BGJwvbBwPQIUhSC4kNxPOek8qQ3S3cNQ7E\n3JUHtYnE4DbcTx/YQVgEayX4GenMbdBmhAe6cF/Sg2npR7XqHaILW8+w3S0sgHb8QgNl7UhMhspD\nlcwPDg6TGXRKTkWgRt8QsjsPPtn4hIgotKaLPwzx/YRKgJnYM89i6CfX4h2yKnoZ6XqAtMLUzkwO\naUGbExKDrzvBEpjBhosWO0WNQoiuOCl3GN45nR0xKQogQgFm5hAMADQgYGNjAA9AV8bRy5MFE7Aa\ngIgmQYUhRAgIuwQRQAu31k4HGFmWc9YCcIBLLQm/mHONAgAtMQoq87zkwJaYSpn/2gAMAwEAAgAD\nAAAAEHmbR4AVQc2gQx8/Y9uXCwB3sw4O4dmpfQqrXHCQBniA0Y2gQx0gG1k3maCEAVQc/wD/xAAk\nEQACAgECBgMBAAAAAAAAAAAAARExIUHwEFGBkbHBYXGh4f/aAAgBAwEBPxB7USzakcWFkUucOpP7\nAollEks17JmqZsSMEmFSChibJeQw6RtSPSyhjsXI80bts8z0Ydb4G4Q6b0HYnKE4UsQeihDoQ7GK\nLeA7HzG/cXss8z0ZdTHRbKN6GpTEG3AQtR0RggfAc3WoVjMku5fzf0ZHUqiorPowdpPszoVn27Gu\nBEJWNWTjKM6mhkWAyiAqBDsfIT9x+yzzPRh1MdFMo3oajdSCqHlDrg0PY2LkKx2JHmidpnmehJ63\nwNSh03oMysY1274HgdDK3Qdj5ise1HDNqRwYWRS5w6kfsDVNchg2hsSXGeYxVM2JGCbCpJQxtmvI\nYdY2pHpZLP/EACURAAICAQMEAgMBAAAAAAAAAAERACExQVHwYXGBsZGhEMHR4f/aAAgBAgEBPxBf\nmDAGs4xAIkB1CyQNGMh8zCR7qgrua+YjM79llwMYNRH2nSgUMaNarn9mR8+OpVwEr1gTWwDqcixW\nxqJLFkgELrdKIOIKAE5DfUFwUm/mslVicYh/mDIOkzEPQzh9RGC5Iz7/AKQaDwqYD8B6M5PwAiEQ\nE/v1AH5Kcww0UZhg28UNZT/fqUMxQUUho3NiKJyRn3/SBacKhJSMHwT1pEG3eBvsXiq8v4cyfjJ3\nOswwsBjgDQn4mRsiP68YHmZpmId88t2S62rOX4pzRtTalLxeNr2mtrZJ4jX6Zbzu/wAhcDbNSU7M\nl9Q5LMpQGAD1JwIdQFiOzyoaQcZ0wpJgjHTYxM0GAJmZihspBYubEcDkjPv+kGm4VCCmYLd5634z\nvWN7kf00OlwApiE2mGGETTCyBqf0IcagZ7kteIaLTNMxB1M4fURBuSM+/wCkCgcKmA/AerOh6QXV\nCCADW7tvGJgYFhMMuROu5frPczDB1EzMf5ggRpOMwSIANRtnZnJXMQEe6sq7GvmIzG3d5cMDsVgv\nj3neCa2CNTkUb2Nwkv3gYfrIbB3xCZPx9+hVwAsfeBNaAGowLNbm40sGQCS+l0ogoxoCTkt9QXRS\nb+byHWJxmF+YIk6z/8QAJhABAAEDAwMFAQEBAAAAAAAAAREAITFBYXFRgfAQkaGxwdHx4f/aAAgB\nAQABPxBK/JFOru4JsTKgLXmP7UGsJxrJG+tcpQbQ2iUWL3mCLnS9QR0pavBhojcyJSWawBbl1sS8\nlulW6Qk1JFg6E0OSDz3q/mebtSaTaFpQmbUpjR6LYaZZcCA3gqoJXCe9FqIDBRAKFIWlTSKb/wDK\ntLhtahbEMwXG3iAmOWBMFKEdfkFkwJ0u61HR/plhHT5Eo6k+Y/tO+5YB1NzDFmJFEa8LfRXASsYf\n37H0Sxd5DF1bmF4PSjbQMapbHDCe1MQQBHIy0YjxQYd8U0ajvCAbe1JOI4VoWX96MR3JLDtilY2k\nigAGqtG/By4BsuqXqy6+gYqDI46jiZ4a8TbRfPmtWt+SB/BQFYUSvw/sq+CCMrKHDc71EVKw1FJ3\nilBAMwWFfw49KM0SCOrIUSBEBiZu95HmaPDGHK/wY5V9F3hbqv0EOR/oQ7hTzUMLmlaQUjVdFPQx\n5ZwcsXeqvoGVkcUAqB/HmrISjyQkXrH0oQqSQyyOo5BXw/orGYH+MTE1sa+yIr7KGeWMTQi+B3Nn\nhU2r/qHizhM9or+hDNkXnVldpFcA7q992cRac180adMaRnFebxh3Iy4U0Ndm3Sui8T020mpi79lr\n0wLZodmJM/Gqic2nFq17b+y/i8xvXyG91B6gdZdwZnFqZtkEk78h8RF5pCCELN1OtZzI/wAYmIr4\nf2VEGQjKwp3sd6uFaU0BPtNCiOLAVU/Tn0ozQCPRZGiShLhM3O0HzVughyP9CTcfQdf5sqxCIPDk\n1BmwdFEgVC4mbHeU5ipKFFdWIfQNYcZuZJWyEtoDSPgoyVvpC1pMVbBAGVgXhs9q+H9FeFvqKoYD\nsxx2+59ErdmQhYQcSnD6UT1l7qEOeCV9qZwoiuVlpxHcksu2aKMTJrQrb3q/MdIgbhJWoCJqwXEO\nrOyGlMwQQTIyUbeFNUunhgff0DMrPOCFFmYIaOaleJtprhIGMP79hXhbad9ywDo7mSbMQiKV5j+V\nNdS8a6TtpphKTaPalFydphm40vUEdKWj0YaI3cq0owIJrpFlRBCwCALDamAwUyChQNpR0miqggMJ\n7UzJtmApRa1jBZYhTMzUW41wyYWEvI9wRG6e1F6cDABKUGiLSLrNPd6XbG63tELDLMlkt4kJnkgz\nDQJzXYAYMidbutLr1oZcQ0+DEOhHmP5SV+SKdDdyxYmAACv/2Q=="), .width(144)) slideshow_2: pin names not known; wires that end beside it: slideshow_2_p1, comparator_2_eq
  // Callout #(.background("#85f76826"), .dx(-36), .dy(-19), .format("wrapped"), .halign("center"), .text("Each of these is just a slideshow with two images; the comparison output determines which image is displayed."), .textwidth(143), .valign("top")) callout_3: pin names not known

  // Notes on the sheet:
  //   FizzBuzz - Displays various messages depending on the value of a counter.
  //   Poke the counter register to enter a new value, poke the clock twice to advance to the next value, or enable auto-ticks (with a slow auto-tick frequency, approx 1Hz is plenty fast).
endmodule

module timedpulse_example (
);

  wire _1_0_hz_p1, _1_0_hz_p2, Lights_p1, Lights_p2, Lights_p3, Lights_p4, Lights_p5, Lights_p6, Lights_p7,
       Lights_p8;
  wire [2:0] Counter_q;

  // Callout #(.background("#ff59fc8c"), .dx(109), .dy(32), .format("wrapped"), .halign("center"), .style("margin: 4px;"), .text("Timed Pulse component generates one single-cycle pulse each second"), .textwidth(158), .valign("base")) callout_1: pin names not known
  // Callout #(.background("#fffe578c"), .dx(108), .dy(11), .format("wrapped"), .halign("center"), .style("margin: 4px;"), .text("Clock in simulation, or on FPGA, can be running at a higher frequency."), .textwidth(158), .valign("base")) callout_2: pin names not known
  // TimedPulse #(.interval(1.0)) _1_0_hz: pin names not known; wires that end beside it: _1_0_hz_p1, _1_0_hz_p2
  Clock clock_1 (.out(_1_0_hz_p1));
  Counter #(.max('h7), .width(3)) Counter (
    .count(_1_0_hz_p2), .Q(Counter_q), .clk(_1_0_hz_p1));  // open: load, D, carry, clr
  LED Blink (.in(_1_0_hz_p2));
  // LEDBar Lights: pin names not known; wires that end beside it: Lights_p1, Lights_p2, Lights_p3, Lights_p4, Lights_p5, Lights_p6, Lights_p7, Lights_p8
  Decoder #(.enable("false"), .select(3)) decoder_1 (
    .out0(Lights_p1), .out1(Lights_p2), .out2(Lights_p3), .out3(Lights_p4), .out4(Lights_p5),
    .out5(Lights_p6), .out6(Lights_p7), .out7(Lights_p8), .sel(Counter_q));
  // Callout #(.background("#b6f7ff8c"), .dx(-93), .dy(-20), .format("wrapped"), .halign("center"), .style("margin: 4px;"), .text("Counts up only once per second, even though clock rate is faster."), .textwidth(158), .valign("base")) callout_3: pin names not known
endmodule
